// Logisim project ESP32C3_Logisim.circ as structural Verilog: 48 circuits, main circuit PlacaDevKit
module PlacaDevKit (
  input  DBG
);

  wire BOOT_out, BOTON_1_out, BOTON_2_out, controlled_buffer_1_out, controlled_buffer_2_out,
       controlled_buffer_3_out, hay_tecla, leer_tecla, RESET_out, tty_escribe, U1_dbg_busca, U1_dbg_ejecuta,
       U1_dbg_escribe, U1_dbg_lee, U1_gpio0, U1_gpio1, U1_gpio4, U1_gpio5, U1_gpio6, U1_gpio7, U1_gpio8,
       U1_gpio9, U1_gpio10, U1_gpio11, U1_gpio12, U1_gpio13, U1_gpio14, U1_gpio15, U1_gpio16, U1_gpio17,
       U1_gpio18, U1_gpio19, U1_gpio20, U1_gpio21, U1_halt, U2_qa, U2_qb, U2_qc, U2_qd, U2_qe, U2_qf, U2_qg,
       U2_qh, XTAL;
  wire [3:0] U1_dbg_op;
  wire [4:0] U1_dbg_rd;
  wire [6:0] tecla, tty_dato;
  wire [31:0] dbg_pc, U1_dbg_a, U1_dbg_b, U1_dbg_ciclos, U1_dbg_dato_esc, U1_dbg_dato_lec, U1_dbg_dir,
       U1_dbg_instret, U1_dbg_ir, U1_dbg_wb, U1_dbg_y;

  assign controlled_buffer_1_out = BOTON_1_out ? 1'b1 : 1'bz;  // Controlled_Buffer controlled_buffer_1
  Button BOTON_1 (.out(BOTON_1_out));
  assign controlled_buffer_2_out = RESET_out ? 1'b0 : 1'bz;  // Controlled_Buffer controlled_buffer_2
  Button RESET (.out(RESET_out));
  assign controlled_buffer_3_out = BOTON_2_out ? 1'b1 : 1'bz;  // Controlled_Buffer controlled_buffer_3
  Button BOTON_2 (.out(BOTON_2_out));
  ESP32C3 U1 (
    .XTAL_P(XTAL), .CHIP_EN(controlled_buffer_2_out), .DBG(DBG), .GPIO0_IN(U1_gpio0), .GPIO1_IN(U1_gpio1),
    .GPIO2_IN(controlled_buffer_1_out), .GPIO3_IN(controlled_buffer_3_out), .GPIO4_IN(U1_gpio4),
    .GPIO5_IN(U1_gpio5), .GPIO6_IN(U1_gpio6), .GPIO7_IN(U1_gpio7), .GPIO8_IN(U1_gpio8), .GPIO9_IN(U1_gpio9),
    .GPIO10_IN(U1_gpio10), .GPIO11_IN(U1_gpio11), .GPIO12_IN(U1_gpio12), .GPIO13_IN(U1_gpio13),
    .GPIO14_IN(U1_gpio14), .GPIO15_IN(U1_gpio15), .GPIO16_IN(U1_gpio16), .GPIO17_IN(U1_gpio17),
    .GPIO18_IN(U1_gpio18), .GPIO19_IN(U1_gpio19), .GPIO20_IN(U1_gpio20), .GPIO21_IN(U1_gpio21),
    .GPIO0(U1_gpio0), .GPIO1(U1_gpio1), .GPIO2(controlled_buffer_1_out), .GPIO3(controlled_buffer_3_out),
    .GPIO4(U1_gpio4), .GPIO5(U1_gpio5), .GPIO6(U1_gpio6), .GPIO7(U1_gpio7), .GPIO8(U1_gpio8),
    .GPIO9(U1_gpio9), .GPIO10(U1_gpio10), .GPIO11(U1_gpio11), .GPIO12(U1_gpio12), .GPIO13(U1_gpio13),
    .GPIO14(U1_gpio14), .GPIO15(U1_gpio15), .GPIO16(U1_gpio16), .GPIO17(U1_gpio17), .GPIO18(U1_gpio18),
    .GPIO19(U1_gpio19), .GPIO20(U1_gpio20), .GPIO21(U1_gpio21), .HALT(U1_halt), .PC(dbg_pc),
    .DBG_BUSCA(U1_dbg_busca), .DBG_EJECUTA(U1_dbg_ejecuta), .DBG_IR(U1_dbg_ir), .DBG_A(U1_dbg_a),
    .DBG_OP(U1_dbg_op), .DBG_B(U1_dbg_b), .DBG_Y(U1_dbg_y), .DBG_RD(U1_dbg_rd), .DBG_WB(U1_dbg_wb),
    .DBG_DIR(U1_dbg_dir), .DBG_ESCRIBE(U1_dbg_escribe), .DBG_DATO_ESC(U1_dbg_dato_esc), .DBG_LEE(U1_dbg_lee),
    .DBG_DATO_LEC(U1_dbg_dato_lec), .DBG_INSTRET(U1_dbg_instret), .DBG_CICLOS(U1_dbg_ciclos));
  LED led_1 (.in(U1_gpio0));
  LED led_2 (.in(U1_gpio1));
  LED led_3 (.in(controlled_buffer_1_out));
  LED led_4 (.in(controlled_buffer_3_out));
  MemoriaI2C U3 (.CLK(XTAL), .SCL(U1_gpio5), .SDA(U1_gpio4), .SDA_SALE(U1_gpio4));
  LED led_5 (.in(U1_gpio4));
  Pull_Resistor #(.pull(1)) pull_resistor_1 (.node(U1_gpio4));
  Clock u_XTAL (.out(XTAL));
  LED led_6 (.in(U1_gpio5));
  Pull_Resistor #(.pull(1)) pull_resistor_2 (.node(U1_gpio5));
  PuenteUSB_Serie PUENTE_USB (
    .CLK(XTAL), .RST(1'b0), .TECLADO_HAY(hay_tecla), .TECLADO_DATO(tecla), .RX_DESDE_CHIP(U1_gpio21),
    .TX_AL_CHIP(U1_gpio20), .TECLADO_LEER(leer_tecla), .TTY_DATO(tty_dato), .TTY_ESCRIBE(tty_escribe));
  LED led_7 (.in(U1_gpio6));
  Registro74HC595 U2 (
    .SER(U1_gpio7), .SRCLK(U1_gpio6), .RCLK(U1_gpio10), .QA(U2_qa), .QB(U2_qb), .QC(U2_qc), .QD(U2_qd),
    .QE(U2_qe), .QF(U2_qf), .QG(U2_qg), .QH(U2_qh));
  LED led_8 (.in(U2_qa));
  LED led_9 (.in(U2_qb));
  LED led_10 (.in(U1_gpio20));
  LED led_11 (.in(U1_gpio21));
  LED led_12 (.in(U1_gpio7));
  LED led_13 (.in(U1_gpio8));
  LED led_14 (.in(U2_qc));
  LED led_15 (.in(U2_qd));
  LED led_16 (.in(U2_qe));
  LED led_17 (.in(U1_gpio19));
  LED led_18 (.in(U1_gpio9));
  LED led_19 (.in(U1_gpio10));
  Pull_Resistor #(.pull(1)) pull_resistor_3 (.node(U1_gpio9));
  assign U1_gpio9 = BOOT_out ? 1'b0 : 1'bz;  // Controlled_Buffer controlled_buffer_4
  Button BOOT (.out(BOOT_out));
  LED led_20 (.in(U2_qf));
  LED led_21 (.in(U2_qg));
  LED led_22 (.in(U1_gpio18));
  LED led_23 (.in(U2_qh));
  LED led_24 (.in(U1_gpio17));
  LED led_25 (.in(U1_gpio16));
  LED led_26 (.in(U1_gpio15));
  LED led_27 (.in(U1_gpio14));
  LED led_28 (.in(U1_gpio13));
  LED led_29 (.in(U1_gpio12));
  LED led_30 (.in(U1_gpio11));
  TTY #(.rows(12), .cols(64)) tty_1 (.data(tty_dato), .clk(XTAL), .we(tty_escribe), .clr(1'b0));
  Keyboard #(.buflen(32)) keyboard_1 (.clk(XTAL), .re(leer_tecla), .clr(1'b0), .avail(hay_tecla), .data(tecla));
  Hex_Digit_Display #(.decimalPoint("false")) hex_digit_display_1 (.value(dbg_pc[27:24]));
  Hex_Digit_Display #(.decimalPoint("false")) hex_digit_display_2 (.value(dbg_pc[31:28]));
  // Probe on dbg_pc
  LED CPU_DETENIDA (.in(U1_halt));
  LED BUSCANDO (.in(U1_dbg_busca));
  LED EJECUTANDO (.in(U1_dbg_ejecuta));
  // Probe on U1_dbg_ir
  // Probe on U1_dbg_a
  // Probe on U1_dbg_op
  // Probe on U1_dbg_b
  // Probe on U1_dbg_y
  // Probe on U1_dbg_rd
  // Probe on U1_dbg_wb
  // Probe on U1_dbg_dir
  LED BUS_ESCRIBE (.in(U1_dbg_escribe));
  // Probe on U1_dbg_dato_esc
  LED BUS_LEE (.in(U1_dbg_lee));
  // Probe on U1_dbg_dato_lec
  // Probe on U1_dbg_instret
  // Probe on U1_dbg_ciclos
  Hex_Digit_Display #(.decimalPoint("false")) hex_digit_display_3 (.value(dbg_pc[19:16]));
  Hex_Digit_Display #(.decimalPoint("false")) hex_digit_display_4 (.value(dbg_pc[23:20]));
  Hex_Digit_Display #(.decimalPoint("false")) hex_digit_display_5 (.value(dbg_pc[11:8]));
  Hex_Digit_Display #(.decimalPoint("false")) hex_digit_display_6 (.value(dbg_pc[15:12]));
  Hex_Digit_Display #(.decimalPoint("false")) hex_digit_display_7 (.value(dbg_pc[3:0]));
  Hex_Digit_Display #(.decimalPoint("false")) hex_digit_display_8 (.value(dbg_pc[7:4]));

  // Notes on the sheet:
  //   DBG: initial=0x1
  //   Como usarla:
  //   1. Ctrl+K (Simular > Activar reloj) pone a andar el reloj.
  //   2. El programa de la FLASH arranca solo: mira la terminal.
  //   3. Haz clic en el teclado y escribe para mandar texto al chip.
  //   4. RESET reinicia; BOOT presionado al reiniciar = modo descarga.
  //   5. Otro programa: abre el circuito ESP32C3, clic derecho en la
  //      ROM 'FLASH' > Load Image (Cargar imagen) y elige un .hex.
  //   6. Paso a paso: Ctrl+K detiene el reloj; Ctrl+T = medio ciclo.
  //      Con Ctrl+E apagado, cada Ctrl+I avanza un paso de compuertas.
  //   7. Para mirar adentro SIN detener nada: pestaña Simular, arbol
  //      de la simulacion activa: PlacaDevKit > U1 > CPU > ...
  //   8. Pestaña State (abajo a la izquierda): registros x1..x31 en vivo.
  //   Cada LED verde muestra el nivel de un GPIO (rojo = GPIO8).
  //   pone GPIO2 en 1
  //   pin EN: reinicia el chip
  //   pone GPIO3 en 1
  //   DBG=1: 'ebreak' detiene la CPU
  //   Memoria I2C (direccion 0x50): GPIO4 = SDA, GPIO5 = SCL
  //   Cristal (reloj del sistema)
  //   Placa de desarrollo ESP32-C3  (modelo en Logisim Evolution)
  //   0
  //   1
  //   Registro 74HC595 en el SPI2:
  //   GPIO6 = SCK, GPIO7 = MOSI, GPIO10 = CS0
  //   (CS0 sube al final: copia el byte a los LEDs)
  //   UART0: GPIO21 = TX del chip, GPIO20 = RX del chip
  //   2
  //   3
  //   4
  //   5
  //   6
  //   7
  //   Contador de programa (PC)
  //   Panel de depuracion: lo que hace la CPU en cada ciclo
  //   Para verlo paso a paso: Ctrl+K detiene el reloj y cada Ctrl+T avanza medio ciclo
  //   contador de programa: direccion de la instruccion actual
  //   la CPU se detuvo (instruccion ebreak con DBG=1)
  //   fase BUSCAR: la CPU trae la instruccion desde la memoria
  //   fase EJECUTAR: decodifica, calcula y guarda el resultado
  //   registro de instruccion (IR): la instruccion de 32 bits
  //   ALU, ultima instruccion: operando A
  //   operacion: 0 suma, 8 resta, 1 <<, 5 >>, D >> con signo, 2 y 3 comparar, 4 xor, 6 or, 7 and
  //   ALU, ultima instruccion: operando B
  //   ALU, ultima instruccion: resultado (A op B)
  //   numero del registro escrito (x0..x31)
  //   valor que se guardo en ese registro
  //   bus: direccion que pide la CPU
  //   bus: la CPU escribe (store)
  //   bus: dato que la CPU escribe
  //   bus: la CPU lee (instruccion o load)
  //   bus: dato que llega a la CPU
  //   instrucciones ejecutadas desde el reset
  //   ciclos de reloj desde el reset
  //   Terminal serie (lo que el ESP32-C3 imprime)
  //   <- teclado: haz clic aqui y escribe
endmodule

module LaboratorioTransistores (
  input  NOT_A,
  input  NAND_A,
  input  NOR_A,
  input  NAND_B,
  input  NOR_B,
  input  FA_A,
  input  FA_B,
  input  FA_Cin,
  input  [3:0] A4,
  input  [3:0] B4
);

  wire RELOJ_out, RESET_CONTADOR_out, U_FA_cout, U_FA_s, U_NAND_y, U_NOR_y, U_NOT_y, U_SUMA4_cout;
  wire [3:0] U_CONTADOR_q, U_SUMA4_s;

  InversorCMOS U_NOT (.A(NOT_A), .Y(U_NOT_y));
  SumadorCompletoCMOS U_FA (.A(FA_A), .B(FA_B), .Cin(FA_Cin), .Cout(U_FA_cout), .S(U_FA_s));
  LED led_1 (.in(U_FA_cout));
  Hex_Digit_Display #(.decimalPoint("false")) hex_digit_display_1 (.value(A4));
  Clock RELOJ (.out(RELOJ_out));
  LED led_2 (.in(RELOJ_out));
  LED led_3 (.in(U_NOT_y));
  LED led_4 (.in(U_FA_s));
  Hex_Digit_Display #(.decimalPoint("false")) hex_digit_display_2 (.value(B4));
  Button RESET_CONTADOR (.out(RESET_CONTADOR_out));
  Sumador4CMOS U_SUMA4 (.A(A4), .B(B4), .Cin(1'b0), .Cout(U_SUMA4_cout), .S(U_SUMA4_s));
  LED led_5 (.in(U_SUMA4_cout));
  Contador4 U_CONTADOR (.CLK(RELOJ_out), .R(RESET_CONTADOR_out), .Q(U_CONTADOR_q));
  NandCMOS U_NAND (.A(NAND_A), .B(NAND_B), .Y(U_NAND_y));
  Hex_Digit_Display #(.decimalPoint("false")) hex_digit_display_3 (.value(U_SUMA4_s));
  Hex_Digit_Display #(.decimalPoint("false")) hex_digit_display_4 (.value(U_CONTADOR_q));
  LED led_6 (.in(U_NAND_y));
  NorCMOS U_NOR (.A(NOR_A), .B(NOR_B), .Y(U_NOR_y));
  LED led_7 (.in(U_NOR_y));

  // Notes on the sheet:
  //   Laboratorio: de transistores a compuertas, a un sumador y a la memoria
  //   Haz clic en las entradas con la herramienta de la mano para cambiarlas. Para ver los transistores por dentro: pestaña Simular, arbol de la simulacion > doble clic en cada bloque (U_NOT, U_FA, U_SUMA4...).
  //   1. Compuertas hechas con transistores
  //   2. Sumador completo de 28 transistores
  //   3. Sumador de 4 bits (112 transistores): A + B
  //   4. El reloj y la memoria: contador de 4 bits
  //   Ctrl+K pone a andar el reloj (Ctrl+T avanza medio ciclo). En cada flanco de subida los flip-flops guardan Q + 1, que el sumador CMOS ya calculo.
  //   NOT (2 transistores)
  //   Cout (acarreo)
  //   A
  //   reloj
  //   S (suma)
  //   B
  //   acarreo final (S >= 16)
  //   NAND (4 transistores)
  //   Prueba: A = 1, B = 1, Cin = 0 -> S = 0 y Cout = 1 (1 + 1 = 10 en binario)
  //   <- cuenta 0, 1, 2 ... F y vuelve a 0
  //   S = A + B
  //   Haz clic en cada bit de los pines A4 y B4.
  //   Ejemplo: A = 0111 (7), B = 0101 (5) -> S = 1100 (C = 12)
  //   NOR (4 transistores)
endmodule

module ESP32C3 (
  input  XTAL_P,
  input  CHIP_EN,
  input  DBG,
  input  GPIO0_IN,
  input  GPIO1_IN,
  input  GPIO2_IN,
  input  GPIO3_IN,
  input  GPIO4_IN,
  input  GPIO5_IN,
  input  GPIO6_IN,
  input  GPIO7_IN,
  input  GPIO8_IN,
  input  GPIO9_IN,
  input  GPIO10_IN,
  input  GPIO11_IN,
  input  GPIO12_IN,
  input  GPIO13_IN,
  input  GPIO14_IN,
  input  GPIO15_IN,
  input  GPIO16_IN,
  input  GPIO17_IN,
  input  GPIO18_IN,
  input  GPIO19_IN,
  input  GPIO20_IN,
  input  GPIO21_IN,
  output GPIO0,
  output GPIO1,
  output GPIO2,
  output GPIO3,
  output GPIO4,
  output GPIO5,
  output GPIO6,
  output GPIO7,
  output GPIO8,
  output GPIO9,
  output GPIO10,
  output GPIO11,
  output GPIO12,
  output GPIO13,
  output GPIO14,
  output GPIO15,
  output GPIO16,
  output GPIO17,
  output GPIO18,
  output GPIO19,
  output GPIO20,
  output GPIO21,
  output HALT,
  output [31:0] PC,
  output DBG_BUSCA,
  output DBG_EJECUTA,
  output [31:0] DBG_IR,
  output [31:0] DBG_A,
  output [3:0] DBG_OP,
  output [31:0] DBG_B,
  output [31:0] DBG_Y,
  output [4:0] DBG_RD,
  output [31:0] DBG_WB,
  output [31:0] DBG_DIR,
  output DBG_ESCRIBE,
  output [31:0] DBG_DATO_ESC,
  output DBG_LEE,
  output [31:0] DBG_DATO_LEC,
  output [31:0] DBG_INSTRET,
  output [31:0] DBG_CICLOS
);

  wire bus_error, bus_intencion_esc, escribe_RTC_FAST, escribe_SRAM, from_cpu0, from_cpu1, from_cpu2,
       from_cpu3, i2c_scl_entra, i2c_scl_sale, i2c_sda_entra, i2c_sda_sale, irq, irq_GPIO, irq_GPIO_NMI,
       irq_I2C, irq_LEDC, irq_RTC, irq_SPI2, irq_systimer0, irq_systimer1, irq_systimer2, irq_t0_TIMG0,
       irq_t0_TIMG1, irq_UART0, irq_UART1, irq_wdt_TIMG0, irq_wdt_TIMG1, ledc_pwm0, ledc_pwm1, ledc_pwm2,
       ledc_pwm3, ledc_pwm4, ledc_pwm5, perif_escribe, perif_lee, reloj_I2C, reloj_I2C_permitido, reloj_LEDC,
       reloj_LEDC_permitido, reloj_on_I2C, reloj_on_LEDC, reloj_on_SPI2, reloj_on_SYSTIMER, reloj_on_TIMG0,
       reloj_on_TIMG1, reloj_on_UART0, reloj_on_UART1, reloj_SPI2, reloj_SPI2_permitido, reloj_SYSTIMER,
       reloj_SYSTIMER_permitido, reloj_TIMG0, reloj_TIMG0_permitido, reloj_TIMG1, reloj_TIMG1_permitido,
       reloj_UART0, reloj_UART0_permitido, reloj_UART1, reloj_UART1_permitido, reset_cpu, reset_I2C,
       reset_LEDC, reset_sistema, reset_SPI2, reset_SYSTIMER, reset_TIMG0, reset_TIMG1, reset_UART0,
       reset_UART1, retira, sel_EFUSE, sel_FLASH, sel_GPIO, sel_I2C, sel_INTERRUPT, sel_IO_MUX, sel_LEDC,
       sel_PERIF, sel_ROM, sel_RTC_CNTL, sel_RTCMEM, sel_SPI2, sel_SRAM, sel_SYSCON, sel_SYSTEM,
       sel_SYSTIMER, sel_TIMG0, sel_TIMG1, sel_UART0, sel_UART1, spi_miso, u0_rxd, u0_txd, u1_rxd, u1_txd,
       wdt_rcpu_TIMG0, wdt_rcpu_TIMG1, wdt_rsis_TIMG0, wdt_rsis_TIMG1;
  wire [3:0] bus_bytes;
  wire [4:0] irq_id;
  wire [5:3] fspi_salidas;
  wire [9:0] perif_dir;
  wire [31:0] irq_lineas, perif_dato, rd_EFUSE, rd_FLASH, rd_GPIO, rd_I2C, rd_INTERRUPT, rd_LEDC, rd_ROM,
       rd_RTC_CNTL, rd_RTCMEM, rd_SPI2, rd_SRAM, rd_SYSCON, rd_SYSTEM, rd_SYSTIMER, rd_TIMG0, rd_TIMG1,
       rd_UART0, rd_UART1;

  CPU_RV32IMC CPU (
    .CLK(XTAL_P), .RST(reset_cpu), .RDATA(DBG_DATO_LEC), .BUS_ERR(bus_error), .IRQ(irq), .IRQ_ID(irq_id),
    .IRQ_LINES(irq_lineas), .DBG(DBG), .ADDR(DBG_DIR), .WDATA(DBG_DATO_ESC), .WSTRB(bus_bytes),
    .WE(DBG_ESCRIBE), .RE(DBG_LEE), .WR(bus_intencion_esc), .FETCH(DBG_BUSCA), .HALTED(HALT), .PC_DBG(PC),
    .RETIRA(retira), .DBG_EJECUTA(DBG_EJECUTA), .DBG_IR(DBG_IR), .DBG_A(DBG_A), .DBG_B(DBG_B), .DBG_Y(DBG_Y),
    .DBG_OP(DBG_OP), .DBG_RD(DBG_RD), .DBG_WB(DBG_WB), .DBG_INSTRET(DBG_INSTRET), .DBG_CICLOS(DBG_CICLOS));
  MuxLectura LECTURA (
    .RD_ROM(rd_ROM), .RD_FLASH(rd_FLASH), .RD_SRAM(rd_SRAM), .RD_RTCMEM(rd_RTCMEM), .SEL_ROM(sel_ROM),
    .SEL_FLASH(sel_FLASH), .SEL_SRAM(sel_SRAM), .SEL_RTCMEM(sel_RTCMEM), .RD_UART0(rd_UART0),
    .RD_UART1(rd_UART1), .RD_GPIO(rd_GPIO), .RD_RTC_CNTL(rd_RTC_CNTL), .RD_EFUSE(rd_EFUSE),
    .RD_TIMG0(rd_TIMG0), .RD_TIMG1(rd_TIMG1), .RD_SYSTIMER(rd_SYSTIMER), .RD_SYSCON(rd_SYSCON),
    .RD_SYSTEM(rd_SYSTEM), .RD_INTERRUPT(rd_INTERRUPT), .RD_LEDC(rd_LEDC), .RD_SPI2(rd_SPI2),
    .RD_I2C(rd_I2C), .RDATA(DBG_DATO_LEC));
  InterfazPerifericos APB (
    .DIR(DBG_DIR), .WDATA(DBG_DATO_ESC), .WE(DBG_ESCRIBE), .RE(DBG_LEE), .ERR(bus_error),
    .SEL_PERIF(sel_PERIF), .A(perif_dir), .WD(perif_dato), .WE_P(perif_escribe), .RE_P(perif_lee));
  BusSistema BUS (
    .ADDR(DBG_DIR), .FETCH(DBG_BUSCA), .WR(bus_intencion_esc), .ERR(bus_error), .SEL_ROM(sel_ROM),
    .SEL_FLASH(sel_FLASH), .SEL_SRAM(sel_SRAM), .SEL_RTCMEM(sel_RTCMEM), .SEL_PERIF(sel_PERIF),
    .SEL_UART0(sel_UART0), .SEL_UART1(sel_UART1), .SEL_GPIO(sel_GPIO), .SEL_IO_MUX(sel_IO_MUX),
    .SEL_RTC_CNTL(sel_RTC_CNTL), .SEL_EFUSE(sel_EFUSE), .SEL_TIMG0(sel_TIMG0), .SEL_TIMG1(sel_TIMG1),
    .SEL_SYSTIMER(sel_SYSTIMER), .SEL_SYSCON(sel_SYSCON), .SEL_SYSTEM(sel_SYSTEM),
    .SEL_INTERRUPT(sel_INTERRUPT), .SEL_LEDC(sel_LEDC), .SEL_SPI2(sel_SPI2), .SEL_I2C(sel_I2C));
  ROM #(.addrWidth(12), .dataWidth(32)) ROM_ARRANQUE (.addr(DBG_DIR[13:2]), .data(rd_ROM));
  ROM #(.addrWidth(18), .dataWidth(32)) FLASH (.addr(DBG_DIR[19:2]), .data(rd_FLASH));
  and and_1 (escribe_SRAM, DBG_ESCRIBE, sel_SRAM);
  RAM #(.addrWidth(17), .dataWidth(32), .enables("byte"), .trigger("rising"), .asyncread("true"), .byteenables("byteEnables"), .databus("bibus")) SRAM (
    .addr(DBG_DIR[18:2]), .we(escribe_SRAM), .oe(1'b1), .clk(XTAL_P), .din(DBG_DATO_ESC), .dout(rd_SRAM),
    .be3(bus_bytes[3]), .be2(bus_bytes[2]), .be1(bus_bytes[1]), .be0(bus_bytes[0]));
  and and_2 (escribe_RTC_FAST, DBG_ESCRIBE, sel_RTCMEM);
  RAM #(.addrWidth(11), .dataWidth(32), .enables("byte"), .trigger("rising"), .asyncread("true"), .byteenables("byteEnables"), .databus("bibus")) RTC_FAST (
    .addr(DBG_DIR[12:2]), .we(escribe_RTC_FAST), .oe(1'b1), .clk(XTAL_P), .din(DBG_DATO_ESC),
    .dout(rd_RTCMEM), .be3(bus_bytes[3]), .be2(bus_bytes[2]), .be1(bus_bytes[1]), .be0(bus_bytes[0]));
  UART UART0 (
    .CLK(reloj_UART0), .RST(reset_UART0), .SEL(sel_UART0), .A(perif_dir), .WD(perif_dato),
    .WE(perif_escribe), .RE(perif_lee), .RXD(u0_rxd), .TXD(u0_txd), .IRQ(irq_UART0), .RD(rd_UART0));
  UART UART1 (
    .CLK(reloj_UART1), .RST(reset_UART1), .SEL(sel_UART1), .A(perif_dir), .WD(perif_dato),
    .WE(perif_escribe), .RE(perif_lee), .RXD(u1_rxd), .TXD(u1_txd), .IRQ(irq_UART1), .RD(rd_UART1));
  LEDC LEDC_2 (
    .CLK(reloj_LEDC), .RST(reset_LEDC), .SEL(sel_LEDC), .A(perif_dir), .WD(perif_dato), .WE(perif_escribe),
    .RE(perif_lee), .PWM0(ledc_pwm0), .PWM1(ledc_pwm1), .PWM2(ledc_pwm2), .PWM3(ledc_pwm3), .PWM4(ledc_pwm4),
    .PWM5(ledc_pwm5), .IRQ(irq_LEDC), .RD(rd_LEDC));
  SPI2 SPI2_2 (
    .CLK(reloj_SPI2), .RST(reset_SPI2), .SEL(sel_SPI2), .A(perif_dir), .WD(perif_dato), .WE(perif_escribe),
    .RE(perif_lee), .MISO(spi_miso), .SCK(fspi_salidas[3]), .MOSI(fspi_salidas[4]), .CS0(fspi_salidas[5]),
    .IRQ(irq_SPI2), .RD(rd_SPI2));
  I2C I2C_2 (
    .CLK(reloj_I2C), .RST(reset_I2C), .SEL(sel_I2C), .A(perif_dir), .WD(perif_dato), .WE(perif_escribe),
    .RE(perif_lee), .SCL_ENTRA(i2c_scl_entra), .SDA_ENTRA(i2c_sda_entra), .SCL_SALE(i2c_scl_sale),
    .SDA_SALE(i2c_sda_sale), .IRQ(irq_I2C), .RD(rd_I2C));
  GPIO_IOMUX GPIO (
    .CLK(XTAL_P), .RST(reset_sistema), .SEL(sel_GPIO), .A(perif_dir), .WD(perif_dato), .WE(perif_escribe),
    .RE(perif_lee),
    .PAD_IN({GPIO21_IN, GPIO20_IN, GPIO19_IN, GPIO18_IN, GPIO17_IN, GPIO16_IN, GPIO15_IN, GPIO14_IN, GPIO13_IN, GPIO12_IN, GPIO11_IN, GPIO10_IN, GPIO9_IN, GPIO8_IN, GPIO7_IN, GPIO6_IN, GPIO5_IN, GPIO4_IN, GPIO3_IN, GPIO2_IN, GPIO1_IN, GPIO0_IN}),
    .SIG_U0TXD(u0_txd), .SIG_U1TXD(u1_txd), .SIG_LEDC0(ledc_pwm0), .SIG_LEDC1(ledc_pwm1),
    .SIG_LEDC2(ledc_pwm2), .SIG_LEDC3(ledc_pwm3), .SIG_LEDC4(ledc_pwm4), .SIG_LEDC5(ledc_pwm5),
    .SIG_I2C_SCL(i2c_scl_sale), .SIG_I2C_SDA(i2c_sda_sale), .SIG_FSPICLK(fspi_salidas[3]),
    .SIG_FSPID(fspi_salidas[4]), .SIG_FSPICS0(fspi_salidas[5]), .FSPI_OUT({fspi_salidas, 3'b110}),
    .FSPI_OE(6'b111000), .SEL_IOMUX(sel_IO_MUX),
    .PAD_OUT({GPIO21, GPIO20, GPIO19, GPIO18, GPIO17, GPIO16, GPIO15, GPIO14, GPIO13, GPIO12, GPIO11, GPIO10, GPIO9, GPIO8, GPIO7, GPIO6, GPIO5, GPIO4, GPIO3, GPIO2, GPIO1, GPIO0}),
    .IRQ(irq_GPIO), .IRQ_NMI(irq_GPIO_NMI), .U0RXD(u0_rxd), .U1RXD(u1_rxd), .I2C_SCL(i2c_scl_entra),
    .I2C_SDA(i2c_sda_entra), .FSPIQ(spi_miso), .RD(rd_GPIO));
  TIMG TIMG0 (
    .CLK(reloj_TIMG0), .RST(reset_TIMG0), .SEL(sel_TIMG0), .A(perif_dir), .WD(perif_dato),
    .WE(perif_escribe), .RE(perif_lee), .IRQ_T0(irq_t0_TIMG0), .IRQ_WDT(irq_wdt_TIMG0),
    .WDT_RESET_CPU(wdt_rcpu_TIMG0), .WDT_RESET_SIS(wdt_rsis_TIMG0), .RD(rd_TIMG0));
  TIMG TIMG1 (
    .CLK(reloj_TIMG1), .RST(reset_TIMG1), .SEL(sel_TIMG1), .A(perif_dir), .WD(perif_dato),
    .WE(perif_escribe), .RE(perif_lee), .IRQ_T0(irq_t0_TIMG1), .IRQ_WDT(irq_wdt_TIMG1),
    .WDT_RESET_CPU(wdt_rcpu_TIMG1), .WDT_RESET_SIS(wdt_rsis_TIMG1), .RD(rd_TIMG1));
  SYSTIMER SYSTIMER_2 (
    .CLK(reloj_SYSTIMER), .RST(reset_SYSTIMER), .SEL(sel_SYSTIMER), .A(perif_dir), .WD(perif_dato),
    .WE(perif_escribe), .RE(perif_lee), .IRQ_T0(irq_systimer0), .IRQ_T1(irq_systimer1),
    .IRQ_T2(irq_systimer2), .RD(rd_SYSTIMER));
  RTC_CNTL RTC_CNTL_2 (
    .CHIP_EN(CHIP_EN), .CLK(XTAL_P), .SEL(sel_RTC_CNTL), .A(perif_dir), .WD(perif_dato), .WE(perif_escribe),
    .RE(perif_lee), .TG0_RESET_SIS(wdt_rsis_TIMG0), .TG1_RESET_SIS(wdt_rsis_TIMG1),
    .TG0_RESET_CPU(wdt_rcpu_TIMG0), .TG1_RESET_CPU(wdt_rcpu_TIMG1), .IRQ(irq_RTC), .RST_SIS(reset_sistema),
    .RST_CPU(reset_cpu), .RD(rd_RTC_CNTL));
  SYSTEM SYSTEM_2 (
    .CLK(XTAL_P), .RST(reset_sistema), .SEL(sel_SYSTEM), .A(perif_dir), .WD(perif_dato), .WE(perif_escribe),
    .RE(perif_lee), .FROM_CPU0(from_cpu0), .FROM_CPU1(from_cpu1), .FROM_CPU2(from_cpu2),
    .FROM_CPU3(from_cpu3), .CLKEN_UART0(reloj_on_UART0), .RST_UART0(reset_UART0),
    .CLKEN_UART1(reloj_on_UART1), .RST_UART1(reset_UART1), .CLKEN_SPI2(reloj_on_SPI2), .RST_SPI2(reset_SPI2),
    .CLKEN_I2C(reloj_on_I2C), .RST_I2C(reset_I2C), .CLKEN_LEDC(reloj_on_LEDC), .RST_LEDC(reset_LEDC),
    .CLKEN_TIMG0(reloj_on_TIMG0), .RST_TIMG0(reset_TIMG0), .CLKEN_TIMG1(reloj_on_TIMG1),
    .RST_TIMG1(reset_TIMG1), .CLKEN_SYSTIMER(reloj_on_SYSTIMER), .RST_SYSTIMER(reset_SYSTIMER), .RD(rd_SYSTEM));
  Register #(.width(1), .trigger("low")) RELOJ_UART0_LATCH (
    .D(reloj_on_UART0), .en(1'b1), .Q(reloj_UART0_permitido), .clk(XTAL_P), .clr(1'b0));
  Register #(.width(1), .trigger("low")) RELOJ_UART1_LATCH (
    .D(reloj_on_UART1), .en(1'b1), .Q(reloj_UART1_permitido), .clk(XTAL_P), .clr(1'b0));
  Register #(.width(1), .trigger("low")) RELOJ_SPI2_LATCH (
    .D(reloj_on_SPI2), .en(1'b1), .Q(reloj_SPI2_permitido), .clk(XTAL_P), .clr(1'b0));
  Register #(.width(1), .trigger("low")) RELOJ_I2C_LATCH (
    .D(reloj_on_I2C), .en(1'b1), .Q(reloj_I2C_permitido), .clk(XTAL_P), .clr(1'b0));
  Register #(.width(1), .trigger("low")) RELOJ_LEDC_LATCH (
    .D(reloj_on_LEDC), .en(1'b1), .Q(reloj_LEDC_permitido), .clk(XTAL_P), .clr(1'b0));
  Register #(.width(1), .trigger("low")) RELOJ_TIMG0_LATCH (
    .D(reloj_on_TIMG0), .en(1'b1), .Q(reloj_TIMG0_permitido), .clk(XTAL_P), .clr(1'b0));
  Register #(.width(1), .trigger("low")) RELOJ_TIMG1_LATCH (
    .D(reloj_on_TIMG1), .en(1'b1), .Q(reloj_TIMG1_permitido), .clk(XTAL_P), .clr(1'b0));
  SYSCON SYSCON_2 (
    .CLK(XTAL_P), .RST(reset_sistema), .SEL(sel_SYSCON), .A(perif_dir), .WD(perif_dato), .WE(perif_escribe),
    .RE(perif_lee), .RD(rd_SYSCON));
  EFUSE EFUSE_2 (
    .CLK(XTAL_P), .RST(reset_sistema), .SEL(sel_EFUSE), .A(perif_dir), .WD(perif_dato), .WE(perif_escribe),
    .RE(perif_lee), .RD(rd_EFUSE));
  and and_3 (reloj_UART0, XTAL_P, reloj_UART0_permitido);
  and and_4 (reloj_UART1, XTAL_P, reloj_UART1_permitido);
  and and_5 (reloj_SPI2, XTAL_P, reloj_SPI2_permitido);
  and and_6 (reloj_I2C, XTAL_P, reloj_I2C_permitido);
  and and_7 (reloj_LEDC, XTAL_P, reloj_LEDC_permitido);
  and and_8 (reloj_TIMG0, XTAL_P, reloj_TIMG0_permitido);
  and and_9 (reloj_TIMG1, XTAL_P, reloj_TIMG1_permitido);
  Register #(.width(1), .trigger("low")) RELOJ_SYSTIMER_LATCH (
    .D(reloj_on_SYSTIMER), .en(1'b1), .Q(reloj_SYSTIMER_permitido), .clk(XTAL_P), .clr(1'b0));
  and and_10 (reloj_SYSTIMER, XTAL_P, reloj_SYSTIMER_permitido);
  MatrizInterrupciones INTERRUPT (
    .CLK(XTAL_P), .RST(reset_sistema), .SEL(sel_INTERRUPT), .A(perif_dir), .WD(perif_dato),
    .WE(perif_escribe), .RE(perif_lee), .INT_GPIO(irq_GPIO), .INT_GPIO_NMI(irq_GPIO_NMI),
    .INT_SPI2(irq_SPI2), .INT_UART0(irq_UART0), .INT_UART1(irq_UART1), .INT_LEDC(irq_LEDC),
    .INT_USB_SERIAL_JTAG(1'b0), .INT_RTC_CORE(irq_RTC), .INT_I2C_EXT0(irq_I2C), .INT_TG0_T0(irq_t0_TIMG0),
    .INT_TG0_WDT(irq_wdt_TIMG0), .INT_TG1_T0(irq_t0_TIMG1), .INT_TG1_WDT(irq_wdt_TIMG1),
    .INT_SYSTIMER_T0(irq_systimer0), .INT_SYSTIMER_T1(irq_systimer1), .INT_SYSTIMER_T2(irq_systimer2),
    .INT_SHA(1'b0), .INT_FROM_CPU0(from_cpu0), .INT_FROM_CPU1(from_cpu1), .INT_FROM_CPU2(from_cpu2),
    .INT_FROM_CPU3(from_cpu3), .IRQ(irq), .IRQ_ID(irq_id), .IRQ_LINEAS(irq_lineas), .RD(rd_INTERRUPT));

  // Other names for the same wires on the sheet: byte0 = bus_bytes[0]; byte1 = bus_bytes[1]; byte2 = bus_bytes[2];
  //   byte3 = bus_bytes[3]; DBG_A_2[31:0] = DBG_A; dbg_a_t[31:0] = DBG_A; DBG_B_2[31:0] = DBG_B;
  //   dbg_b_t[31:0] = DBG_B; bus_fetch = DBG_BUSCA; DBG_CICLOS_2[31:0] = DBG_CICLOS; dbg_ciclos_t[31:0] = DBG_CICLOS;
  //   bus_dato_esc[31:0] = DBG_DATO_ESC; bus_dato_lec[31:0] = DBG_DATO_LEC; bus_dir[31:0] = DBG_DIR;
  //   dir_flash[17:0] = DBG_DIR[19:2]; dir_rom[11:0] = DBG_DIR[13:2]; dir_rtc_fast[10:0] = DBG_DIR[12:2];
  //   dir_sram[16:0] = DBG_DIR[18:2]; DBG_EJECUTA_2 = DBG_EJECUTA; dbg_ejecuta_t = DBG_EJECUTA;
  //   bus_escribe = DBG_ESCRIBE; DBG_INSTRET_2[31:0] = DBG_INSTRET; dbg_instret_t[31:0] = DBG_INSTRET;
  //   DBG_IR_2[31:0] = DBG_IR; dbg_ir_t[31:0] = DBG_IR; bus_lee = DBG_LEE; DBG_OP_2[3:0] = DBG_OP;
  //   dbg_op_t[3:0] = DBG_OP; DBG_RD_2[4:0] = DBG_RD; dbg_rd_t[4:0] = DBG_RD; DBG_WB_2[31:0] = DBG_WB;
  //   dbg_wb_t[31:0] = DBG_WB; DBG_Y_2[31:0] = DBG_Y; dbg_y_t[31:0] = DBG_Y; spi_sck = fspi_salidas[3];
  //   spi_mosi = fspi_salidas[4]; spi_cs0 = fspi_salidas[5]; pad0 = GPIO0;
  //   pads_salida[21:0] = {GPIO21, GPIO20, GPIO19, GPIO18, GPIO17, GPIO16, GPIO15, GPIO14, GPIO13, GPIO12, GPIO11, GPIO10, GPIO9, GPIO8, GPIO7, GPIO6, GPIO5, GPIO4, GPIO3, GPIO2, GPIO1, GPIO0};
  //   pad1 = GPIO1; pad2 = GPIO2; pad3 = GPIO3; pad4 = GPIO4; pad5 = GPIO5; pad6 = GPIO6; pad7 = GPIO7; pad8 = GPIO8;
  //   pad9 = GPIO9; pad10 = GPIO10; pad11 = GPIO11; pad12 = GPIO12; pad13 = GPIO13; pad14 = GPIO14; pad15 = GPIO15;
  //   pad16 = GPIO16; pad17 = GPIO17; pad18 = GPIO18; pad19 = GPIO19; pad20 = GPIO20; pad21 = GPIO21;
  //   cpu_detenida = HALT;
  //   pads_entrada[21:0] = {GPIO21_IN, GPIO20_IN, GPIO19_IN, GPIO18_IN, GPIO17_IN, GPIO16_IN, GPIO15_IN, GPIO14_IN, GPIO13_IN, GPIO12_IN, GPIO11_IN, GPIO10_IN, GPIO9_IN, GPIO8_IN, GPIO7_IN, GPIO6_IN, GPIO5_IN, GPIO4_IN, GPIO3_IN, GPIO2_IN, GPIO1_IN, GPIO0_IN};
  //   PC_2[31:0] = PC; pc_t[31:0] = PC

  // Notes on the sheet:
  //   CPU
  //   Bus del sistema
  //   contents of ROM_ARRANQUE (hex, n*v repeats v):
  //   3fcde137 71010113 297 f828293 12e293 30529073 a0012c3d 138502 55*130000 10000 800006f 7c0006f
  //   780006f 740006f 700006f 6c0006f 680006f 640006f 600006f 5c0006f 580006f 540006f 500006f 4c0006f
  //   480006f 440006f 400006f 3c0006f 380006f 340006f 300006f 2c0006f 280006f 240006f 200006f 1c0006f
  //   180006f 140006f 100006f c0006f 80006f 40006f 34202573 341025f3 34302673 a00122c9 18*0 60000737
  //   6b745a9 7716000 7700613 47834835 e3910005 9a638082 431c00b7 f79383c1 6ce33ff7 a023fef6 48830106
  //   5050005 83c1431c 3ff7f793 fef66ce3 116a023 1101b7f9 400006b7 87aace06 10623 86934721 503986 533177d
  //   f61300e6 963600f7 64603 238391 c39100c5 3769f37d 610540f2 71398082 600087b7 5f80dc22 40000537
  //   600047b7 3b050513 da26de06 5f84d84a 3f47413 d452d64e d05ad256 cc62ce5e 85223f91 5373f59 5134000
  //   37993e45 47c1147d f4f913 287eb63 400007b7 8793040a 97a25707 372d4388 40000537 3e850513 854a3705
  //   378588a1 537ec91 5134000 37393f45 10500073 537bff5 5134000 bfd13ac5 40000537 42050513 420004b7
  //   aedb0437 9b735f5 4914200 e900a13 41d40413 40000ab7 40000b37 40000bb7 7cf00c13 9a903 8513409c
  //   7713438b 1630ff9 18630347 96630089 5370087 5214200 851339c5 355d480a 35e5854a 494b0513 c6023d71
  //   45e347b2 47b2fcfc c63e0785 1141bfd5 892ac04a 40000537 49850513 c422c606 8432c226 3d8d84ae 3d55854a
  //   40000537 4c050513 85263595 537355d 5134000 3d994cc5 3d618522 40000537 49450513 7335a1 bff51050
  //   33323130 37363534 62613938 66656463 0 3f 5053450a 4d4f522d 7073653a 33633233 676f6c2d 6d697369
  //   6f6d2820 6f6c6564 75646520 69746163 a296f76 3a747372 7830 2820 6f622c29 303a746f 78 4f442820
  //   4f4c4e57 55284441 30545241 770a2929 69746961 6620676e 6420726f 6c6e776f a64616f 0 50532820 41465f49
  //   465f5453 4853414c 4f4f425f a2954 6d726f66 206f7461 69206564 6567616d 5345206e 44492d50 6f6e2046
  //   706f7320 6174726f 70206f64 6520726f 6f6d206c 6f6c6564 7375203a 69642061 74636572 6f6f6220 a74
  //   61766e69 2064696c 64616568 203a7265 7830 a 7275470a 654d2075 61746964 6e6f6974 72724520 2820726f
  //   294d4f52 636d203a 65737561 78303d 70656d20 78303d63 0 76746d20 303d6c61 78 45574f50 4e4f52 5f435452
  //   535f5753 525f5359 5453 57304754 535f5444 525f5359 5453 57314754 535f5444 525f5359 5453 57435452
  //   535f5444 525f5359 5453 57304754 435f5444 525f5550 5453 5f435452 435f5753 525f5550 5453 57435452
  //   435f5444 525f5550 5453 57435452 525f5444 525f4354 5453 57314754 435f5444 525f5550 5453 400004d8
  //   400003ac 400004e0 400003ac 400003ac 400003ac 400004f0 40000500 40000510 400003ac 40000520 40000530
  //   40000540 400003ac 400003ac 40000550 40000560
  //   contents of FLASH (hex, n*v repeats v):
  //   aedb041d aedb041d fdc80197 7f818193 fdcd0117 ff010113 fdc80517 fe850513 fa002597 65858593 fdc80617
  //   fd860613 c57963 5a283 552023 5910511 517bfc5 513fdc8 8593fbe5 76639001 202300b5 5110005 297bfdd
  //   82930000 e2930a62 90730012 23353052 fa002417 60c40413 fa002497 60448493 947763 42283 4119282
  //   24b5bfd5 739002 bff51050 27*0 ce0006f 7c0006f 780006f 740006f 700006f 6c0006f 680006f 640006f
  //   600006f 5c0006f 580006f 540006f 500006f 4c0006f 480006f 440006f 400006f 3c0006f 380006f 340006f
  //   300006f 2c0006f 280006f 240006f 200006f 1c0006f 180006f 140006f 100006f c0006f 80006f 40006f
  //   c0067139 c41ac216 c82ac61e cc32ca2e d03ace36 d442d23e d872d646 dc7ada76 2573de7e 242d3420 42924082
  //   43b24322 45d24542 46f24662 57925702 58b25822 5ed25e42 5ff25f62 736121 71193020 c60ec206 ca16c812
  //   ce1ecc1a d226d022 d62ed42a da36d832 de3edc3a c2c6c0c2 c6cec4ca cad6c8d2 cedeccda d2e6d0e2 d6eed4ea
  //   daf6d8f2 defedcfa 8010293 850ac416 342025f3 34102673 343026f3 a0012ac9 52*0 11010000 ce060028
  //   22edcc22 3c002537 5050513 181000ef 2a65227d 253785aa 5133c00 ef0785 480316f0 478300d1 470300c1
  //   468300b1 460300a1 45830091 25370081 5133c00 ef0905 25f314b0 26733010 2537f110 5133c00 ef0b45
  //   67791370 24070713 5ce56b7 3c002537 9c00813 31500793 f4068693 31500613 51385ba ef0d45 253710f0
  //   5133c00 ef0f45 44351030 28194501 fe054ee3 851363 75134529 ef0ff5 b7ed1090 600107b7 7f1872a 7b7e501
  //   7f16000 557d439c 3ff7f793 7b7cb89 e3196001 600007b7 75134388 80820ff5 7b7897d 50a3fc8 8078793
  //   439897aa 7b7cb01 87933fc8 97aa0007 87024388 71398082 da26dc22 de06d64e d452d84a d05ad256 8713ce5e
  //   47a9fff5 842e89aa ef6384b2 27b708e7 70a3c00 41078793 438c97ba 3c002537 12450513 efc636 46b205b0
  //   3c002537 85a68622 16c50513 3c0024b7 3c002937 3c002a37 3c002ab7 39000ef 43c48493 9134405 a1311c9
  //   4b8d118a 120a8a93 3c002b37 864a40cc 25c783 8652c391 241793 439497ce 347793 9363874a 87560177
  //   1a4b0513 7f8000ef 7930405 4910200 fcf418e3 3c002537 12050513 7e0000ef a0019002 3c0025b7 11458593
  //   87b7b7b5 5f886000 3f57513 157d8082 ea6347c1 27b700a7 50a3c00 3cc78793 438897aa 25378082 5133c00
  //   80821145 600097b7 60009737 84478793 84870713 4318439c f502a3 875693 e500a3 187d713 e50123 107d713
  //   e501a3 87d713 d50023 e50223 47b78082 879350d8 f737aa17 d37c6001 6001f6b7 406a423 6072223 60020737
  //   6b7d37c a4236002 22230406 87370607 7136000 c31c0a87 600087b7 9078793 7a023 72023 600087b7 8f1d3737
  //   b078793 12a70713 8737c398 7136000 43140ac7 80000637 c3148ed1 7a023 11418082 3771c606 27b740b2
  //   8793600c 47051947 141c398 71398082 da26dc22 d64ed84a d256d452 de06d05a 89aace5e 8b328a2e 84ba8936
  //   44018abe 793ef89 4330200 7a340d7 4b8100f1 48bc663 45363 86524401 855a85ca 944a9982 20a8063 2000793
  //   412484b3 f107a3 4a634901 87260299 4d363 943a4701 852250f2 54d25462 59b25942 5a925a22 4bf25b02
  //   80826121 45858652 f10513 b859982 8652b765 5134585 998200f1 b7c10905 c70387aa e7010007 40a78533
  //   7858082 87aabfcd 7634501 873300b5 470300a7 e3110007 5058082 17b7b7fd 71350004 ca3e07d5 3c0027b7
  //   4bc78793 c94acb26 dce2c74e cf0689aa c552cd22 c15ac356 dae6dede d6eed8ea 8532c22e 490184b6 2500c13
  //   4783cc3e e38d0005 446a40fa 49ba44da 4a9a4a2a 5bf64b0a 5cd65c66 5db65d46 494a854a 8082610d 150413
  //   7879d63 c602c802 4a01c402 2b00713 2d00693 2000613 2300593 44783 ae78163 6f76a63 ac78163 8b78d63
  //   2a00713 6e79863 4ac83 4910405 44603 2e00693 1b6357fd 468308d6 7930014 826302a0 40508f6 46254781
  //   468345a9 86930004 6b63fd06 87b306d6 40502b7 b7f597b6 47830405 c3990004 ff879ce3 a334612 85d240a4
  //   99529982 513147d b7810014 2d78c63 3000513 2a78a63 46a54c81 47834629 87930004 e7e3fd07 8733f8f6
  //   40502cc e78cb3 4785b7ed 405c63e 4785bf91 bfe5c83e bfd54a05 c43e4785 409cb7fd 4910409 45494601
  //   6c00813 9363a029 6050105 45830405 86930004 f693f985 67630ff6 475202d5 d756b3 f2e58a85 7300693
  //   2b6ec63 f9d58693 ff6f693 65634541 476202d5 96ba068a 86824294 7300693 b6ec63 6200693 fcb6eee3 f858563
  //   4bc6463 e8058ce3 d6634685 86932ac6 9ae10074 6aa83 46ab03 868493 7800693 36d58c63 7000693 34d58463
  //   5800693 28d58663 6f00693 83634621 462900d5 aca94d01 fbb58693 ff6f693 6be34509 8693fad5 9ae10074
  //   6aa83 46ab03 868493 c7634d99 8dbe0007 d36347a5 4da501b7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
  //   Memorias
  //   Perifericos
  //   Temporizadores y reset
  //   Sistema e interrupciones
endmodule

module SumadorCompletoCMOS (
  input  A,
  input  B,
  input  Cin,
  output Cout,
  output S
);

  wire Cn, Sn, transistor_1_out, transistor_4_out, transistor_5_out, transistor_8_out, transistor_11_out,
       transistor_12_out, transistor_15_out, transistor_16_out, transistor_17_out, transistor_21_out;

  Transistor #(.\type ("p"), .width(1)) transistor_1 (.in(1'b1), .out(transistor_1_out), .gate(A));
  Transistor #(.\type ("p"), .width(1)) transistor_2 (.in(transistor_1_out), .out(Cn), .gate(B));
  Transistor #(.\type ("n"), .width(1)) transistor_3 (.in(transistor_4_out), .out(Cn), .gate(B));
  Transistor #(.\type ("n"), .width(1)) transistor_4 (.in(1'b0), .out(transistor_4_out), .gate(A));
  Transistor #(.\type ("p"), .width(1)) transistor_5 (.in(1'b1), .out(transistor_5_out), .gate(A));
  Transistor #(.\type ("p"), .width(1)) transistor_6 (.in(transistor_5_out), .out(Cn), .gate(Cin));
  Transistor #(.\type ("n"), .width(1)) transistor_7 (.in(transistor_8_out), .out(Cn), .gate(Cin));
  Transistor #(.\type ("n"), .width(1)) transistor_8 (.in(1'b0), .out(transistor_8_out), .gate(A));
  Transistor #(.\type ("p"), .width(1)) transistor_9 (.in(1'b1), .out(transistor_5_out), .gate(B));
  Transistor #(.\type ("n"), .width(1)) transistor_10 (.in(1'b0), .out(transistor_8_out), .gate(B));
  Transistor #(.\type ("p"), .width(1)) transistor_11 (.in(1'b1), .out(transistor_11_out), .gate(A));
  Transistor #(.\type ("p"), .width(1)) transistor_12 (.in(transistor_11_out), .out(transistor_12_out), .gate(B));
  Transistor #(.\type ("p"), .width(1)) transistor_13 (.in(transistor_12_out), .out(Sn), .gate(Cin));
  Transistor #(.\type ("n"), .width(1)) transistor_14 (.in(transistor_15_out), .out(Sn), .gate(Cin));
  Transistor #(.\type ("n"), .width(1)) transistor_15 (.in(transistor_16_out), .out(transistor_15_out), .gate(B));
  Transistor #(.\type ("n"), .width(1)) transistor_16 (.in(1'b0), .out(transistor_16_out), .gate(A));
  Transistor #(.\type ("p"), .width(1)) transistor_17 (.in(1'b1), .out(transistor_17_out), .gate(A));
  Transistor #(.\type ("p"), .width(1)) transistor_18 (.in(1'b1), .out(transistor_17_out), .gate(B));
  Transistor #(.\type ("p"), .width(1)) transistor_19 (.in(transistor_17_out), .out(Sn), .gate(Cn));
  Transistor #(.\type ("n"), .width(1)) transistor_20 (.in(transistor_21_out), .out(Sn), .gate(Cn));
  Transistor #(.\type ("n"), .width(1)) transistor_21 (.in(1'b0), .out(transistor_21_out), .gate(A));
  Transistor #(.\type ("n"), .width(1)) transistor_22 (.in(1'b0), .out(transistor_21_out), .gate(B));
  Transistor #(.\type ("p"), .width(1)) transistor_23 (.in(1'b1), .out(transistor_17_out), .gate(Cin));
  Transistor #(.\type ("n"), .width(1)) transistor_24 (.in(1'b0), .out(transistor_21_out), .gate(Cin));
  Transistor #(.\type ("p"), .width(1)) transistor_25 (.in(1'b1), .out(Cout), .gate(Cn));
  Transistor #(.\type ("n"), .width(1)) transistor_26 (.in(1'b0), .out(Cout), .gate(Cn));
  Transistor #(.\type ("p"), .width(1)) transistor_27 (.in(1'b1), .out(S), .gate(Sn));
  Transistor #(.\type ("n"), .width(1)) transistor_28 (.in(1'b0), .out(S), .gate(Sn));

  // Notes on the sheet:
  //   Sumador completo CMOS de 28 transistores ("mirror adder")
  //   S = A xor B xor Cin ;  Cout = A.B + Cin.(A+B).  Los nombres A, B, Cin, Cn y Sn son etiquetas: cada compuerta de transistor esta conectada a la senal con ese nombre.
  //   P (con circulito): conduce si su compuerta = 0; deja pasar el 1 de VDD
  //   N: conduce si su compuerta = 1; deja pasar el 0 de GND
  //   Red de acarreo: 10 transistores
  //   arriba P (sube Cn a 1), abajo N (baja Cn a 0)
  //   Red de suma: 14 transistores
  //   usa Cn: la suma reutiliza el acarreo negado
  //   2 inversores: 4 transistores
  //   Cout = NOT Cn ;  S = NOT Sn
endmodule

module FIFO128x8 (
  input  CLK,
  input  RST,
  input  PUSH,
  input  [7:0] DIN,
  input  POP,
  output [7:0] DOUT,
  output [7:0] COUNT,
  output FULL,
  output EMPTY
);

  wire mete, not1, not2, not3, or9, saca;
  wire [6:0] dir_ram, puntero_esc, puntero_lec, sum4, sum5;
  wire [7:0] mux8, sum6, sum7;

  not not_1 (not3, PUSH);
  Register #(.width(7)) WPTR (.D(sum4), .en(mete), .Q(puntero_esc), .clk(CLK), .clr(RST));
  Register #(.width(7)) RPTR (.D(sum5), .en(saca), .Q(puntero_lec), .clk(CLK), .clr(RST));
  Register #(.width(8)) CUENTA (.D(mux8), .en(or9), .Q(COUNT), .clk(CLK), .clr(RST));
  RAM #(.addrWidth(7), .dataWidth(8), .enables("byte"), .trigger("rising"), .asyncread("true"), .databus("bibus")) MEM_FIFO (
    .addr(dir_ram), .we(mete), .oe(1'b1), .clk(CLK), .din(DIN), .dout(DOUT));
  Comparator #(.width(8), .mode("unsigned")) comparator_1 (.a(COUNT), .b(8'h80), .eq(FULL));  // open: gt, lt
  Comparator #(.width(8), .mode("unsigned")) comparator_2 (.a(COUNT), .b({8{1'b0}}), .eq(EMPTY));  // open: gt, lt
  Adder #(.width(8)) adder_1 (.a(COUNT), .b(8'h1), .out(sum6));  // open: cin, cout
  Adder #(.width(8)) adder_2 (.a(COUNT), .b({8{1'b1}}), .out(sum7));  // open: cin, cout
  Adder #(.width(7)) adder_3 (.a(puntero_esc), .b(7'b0000001), .out(sum4));  // open: cin, cout
  Adder #(.width(7)) adder_4 (.a(puntero_lec), .b(7'b0000001), .out(sum5));  // open: cin, cout
  Multiplexer #(.select(1), .width(7), .enable("false")) multiplexer_1 (
    .in0(puntero_lec), .in1(puntero_esc), .out(dir_ram), .sel(PUSH));
  not not_2 (not1, FULL);
  not not_3 (not2, EMPTY);
  and and_1 (mete, PUSH, not1);
  and and_2 (saca, POP, not2, not3);
  Multiplexer #(.select(1), .width(8), .enable("false")) multiplexer_2 (.in0(sum7), .in1(sum6), .out(mux8), .sel(mete));
  or or_1 (or9, mete, saca);

  // Other names for the same wires on the sheet: cuenta[7:0] = COUNT; dato_salida[7:0] = DOUT; vacio = EMPTY;
  //   lleno = FULL
endmodule

module TransmisorSerie (
  input  CLK,
  input  RST,
  input  [11:0] DIV,
  input  START,
  input  [7:0] DATA,
  output TXD,
  output BUSY,
  output FIN
);

  wire carga, eq4, lt2, mux15, not1, not3, or5, or7, or11, or14, or16, tick_bit;
  wire [0:0] desplaza;
  wire [3:0] mux13, num_bit, sum12;
  wire [8:0] cat8;
  wire [9:0] mux10;
  wire [11:0] cuenta_baud, cuenta_mas1, mux6;

  Register #(.width(12)) BAUD (.D(mux6), .en(or7), .Q(cuenta_baud), .clk(CLK), .clr(RST));
  Register #(.width(10)) SHIFT (.D(mux10), .en(or11), .Q({cat8, desplaza[0]}), .clk(CLK), .clr(RST));
  Register #(.width(4)) BIT (.D(mux13), .en(or14), .Q(num_bit), .clk(CLK), .clr(RST));
  Register #(.width(1)) OCUPADO (.D(mux15), .en(or16), .Q(BUSY), .clk(CLK), .clr(RST));
  not not_1 (not1, BUSY);
  Adder #(.width(12)) adder_1 (.a(cuenta_baud), .b(12'h1), .out(cuenta_mas1));  // open: cin, cout
  Comparator #(.width(4), .mode("unsigned")) comparator_1 (.a(num_bit), .b(4'b1001), .eq(eq4));  // open: gt, lt
  Adder #(.width(4)) adder_2 (.a(num_bit), .b(4'b0001), .out(sum12));  // open: cin, cout
  and and_1 (carga, START, not1);
  Comparator #(.width(12), .mode("unsigned")) comparator_2 (.a(cuenta_mas1), .b(DIV), .lt(lt2));  // open: gt, eq
  Multiplexer #(.select(1), .width(1), .enable("false")) multiplexer_1 (
    .in0(1'b1), .in1(desplaza[0]), .out(TXD), .sel(BUSY));
  not not_2 (not3, lt2);
  Multiplexer #(.select(1), .width(1), .enable("false")) multiplexer_2 (
    .in0(1'b0), .in1(1'b1), .out(mux15), .sel(carga));
  or or_1 (or7, carga, BUSY);
  Multiplexer #(.select(1), .width(10), .enable("false")) multiplexer_3 (
    .in0({1'b1, cat8}), .in1({1'b1, DATA, 1'b0}), .out(mux10), .sel(carga));
  Multiplexer #(.select(1), .width(4), .enable("false")) multiplexer_4 (
    .in0(sum12), .in1(4'b0000), .out(mux13), .sel(carga));
  and and_2 (tick_bit, BUSY, not3);
  and and_3 (FIN, tick_bit, eq4);
  or or_2 (or5, carga, tick_bit);
  or or_3 (or11, carga, tick_bit);
  or or_4 (or14, carga, tick_bit);
  Multiplexer #(.select(1), .width(12), .enable("false")) multiplexer_5 (
    .in0(cuenta_mas1), .in1({12{1'b0}}), .out(mux6), .sel(or5));
  or or_5 (or16, carga, FIN);

  // Other names for the same wires on the sheet: ocupado = BUSY; desplaza[9:1] = cat8; desplaza_9_1[8:0] = cat8;
  //   cat9[8:1] = DATA; desplaza_0 = desplaza[0]; ultimo_bit = FIN; linea_tx = TXD
endmodule

module ReceptorSerie (
  input  CLK,
  input  RST,
  input  [11:0] DIV,
  input  RXD,
  output [7:0] DATA,
  output VALID,
  output FERR
);

  wire bit_dato, eq10, eq11, falso_inicio, inicio, lt8, medio_bit, muestrea, mux17, mux23, not5, not6, not9,
       not12, not13, not25, ocupado, or14, or16, or18, or21, or24, qx2, qx4, rx_sinc1, xor1, xor3;
  wire [3:0] indice, mux20, sum19;
  wire [7:7] cat22;
  wire [11:0] cuenta_baud, cuenta_mas1, mux15, periodo;

  xor xor_1 (xor1, RXD, 1'b1);
  Register #(.width(1)) SINC1 (.D(xor1), .en(1'b1), .Q(qx2), .clk(CLK), .clr(RST));
  Register #(.width(1)) SINC2 (.D(xor3), .en(1'b1), .Q(qx4), .clk(CLK), .clr(RST));
  Register #(.width(12)) BAUD (.D(mux15), .en(or16), .Q(cuenta_baud), .clk(CLK), .clr(RST));
  Register #(.width(1)) MEDIO (.D(mux17), .en(or18), .Q(medio_bit), .clk(CLK), .clr(RST));
  Register #(.width(4)) IDX (.D(mux20), .en(or21), .Q(indice), .clk(CLK), .clr(RST));
  Register #(.width(8)) DATO (.D({cat22[7], DATA[7:1]}), .en(bit_dato), .Q(DATA), .clk(CLK), .clr(RST));
  Register #(.width(1)) u_OCUPADO (.D(mux23), .en(or24), .Q(ocupado), .clk(CLK), .clr(RST));
  xor xor_2 (rx_sinc1, qx2, 1'b1);
  xor xor_3 (cat22[7], qx4, 1'b1);
  not not_1 (not5, ocupado);
  Comparator #(.width(4), .mode("unsigned")) comparator_1 (.a(indice), .b(4'b0000), .eq(eq10));  // open: gt, lt
  Comparator #(.width(4), .mode("unsigned")) comparator_2 (.a(indice), .b(4'b1001), .eq(eq11));  // open: gt, lt
  Adder #(.width(4)) adder_1 (.a(indice), .b(4'b0001), .out(sum19));  // open: cin, cout
  Adder #(.width(12)) adder_2 (.a(cuenta_baud), .b(12'h1), .out(cuenta_mas1));  // open: cin, cout
  xor xor_4 (xor3, rx_sinc1, 1'b1);
  not not_2 (not6, cat22[7]);
  Multiplexer #(.select(1), .width(12), .enable("false")) multiplexer_1 (
    .in0(DIV), .in1({1'b0, DIV[11:1]}), .out(periodo), .sel(medio_bit));
  not not_3 (not12, eq10);
  not not_4 (not13, eq11);
  not not_5 (not25, cat22[7]);
  and and_1 (inicio, not5, not6);
  Comparator #(.width(12), .mode("unsigned")) comparator_3 (.a(cuenta_mas1), .b(periodo), .lt(lt8));  // open: gt, eq
  not not_6 (not9, lt8);
  or or_1 (or16, inicio, ocupado);
  Multiplexer #(.select(1), .width(1), .enable("false")) multiplexer_2 (
    .in0(1'b0), .in1(1'b1), .out(mux17), .sel(inicio));
  Multiplexer #(.select(1), .width(4), .enable("false")) multiplexer_3 (
    .in0(sum19), .in1(4'b0000), .out(mux20), .sel(inicio));
  Multiplexer #(.select(1), .width(1), .enable("false")) multiplexer_4 (
    .in0(1'b0), .in1(1'b1), .out(mux23), .sel(inicio));
  and and_2 (muestrea, ocupado, not9);
  and and_3 (falso_inicio, muestrea, eq10, cat22[7]);
  and and_4 (VALID, muestrea, eq11);
  and and_5 (bit_dato, muestrea, not12, not13);
  or or_2 (or14, inicio, muestrea);
  or or_3 (or18, inicio, muestrea);
  or or_4 (or21, inicio, muestrea);
  Multiplexer #(.select(1), .width(12), .enable("false")) multiplexer_5 (
    .in0(cuenta_mas1), .in1({12{1'b0}}), .out(mux15), .sel(or14));
  or or_5 (or24, inicio, falso_inicio, VALID);
  and and_6 (FERR, VALID, not25);

  // Other names for the same wires on the sheet: cat7[10:0] = DIV[11:1]; DIV_11_1[10:0] = DIV[11:1];
  //   cat22[6:0] = DATA[7:1]; dato[7:0] = DATA; dato_7_1[6:0] = DATA[7:1]; rx = cat22[7]; and26 = FERR;
  //   fin_byte = VALID
endmodule

module SumadorCompleto (
  input  A,
  input  B,
  input  Cin,
  output S,
  output Cout
);

  wire and_1_out, and_2_out, xor_1_out;

  xor xor_1 (xor_1_out, A, B);
  and and_1 (and_1_out, A, B);
  xor xor_2 (S, xor_1_out, Cin);
  and and_2 (and_2_out, xor_1_out, Cin);
  or or_1 (Cout, and_1_out, and_2_out);

  // Notes on the sheet:
  //   P
  //   G
  //   Sumador completo: S = A xor B xor Cin ;  Cout = A.B + Cin.(A xor B)
  //   T
endmodule

module Sumador32 (
  input  [31:0] A,
  input  [31:0] B,
  input  Cin,
  output Cout,
  output [31:0] S
);

  wire FA0_cout, FA1_cout, FA2_cout, FA3_cout, FA4_cout, FA5_cout, FA6_cout, FA7_cout, FA8_cout, FA9_cout,
       FA10_cout, FA11_cout, FA12_cout, FA13_cout, FA14_cout, FA15_cout, FA16_cout, FA17_cout, FA18_cout,
       FA19_cout, FA20_cout, FA21_cout, FA22_cout, FA23_cout, FA24_cout, FA25_cout, FA26_cout, FA27_cout,
       FA28_cout, FA29_cout, FA30_cout;

  SumadorCompleto FA31 (.A(A[31]), .B(B[31]), .Cin(FA30_cout), .S(S[31]), .Cout(Cout));
  SumadorCompleto FA30 (.A(A[30]), .B(B[30]), .Cin(FA29_cout), .S(S[30]), .Cout(FA30_cout));
  SumadorCompleto FA29 (.A(A[29]), .B(B[29]), .Cin(FA28_cout), .S(S[29]), .Cout(FA29_cout));
  SumadorCompleto FA28 (.A(A[28]), .B(B[28]), .Cin(FA27_cout), .S(S[28]), .Cout(FA28_cout));
  SumadorCompleto FA27 (.A(A[27]), .B(B[27]), .Cin(FA26_cout), .S(S[27]), .Cout(FA27_cout));
  SumadorCompleto FA26 (.A(A[26]), .B(B[26]), .Cin(FA25_cout), .S(S[26]), .Cout(FA26_cout));
  SumadorCompleto FA25 (.A(A[25]), .B(B[25]), .Cin(FA24_cout), .S(S[25]), .Cout(FA25_cout));
  SumadorCompleto FA24 (.A(A[24]), .B(B[24]), .Cin(FA23_cout), .S(S[24]), .Cout(FA24_cout));
  SumadorCompleto FA23 (.A(A[23]), .B(B[23]), .Cin(FA22_cout), .S(S[23]), .Cout(FA23_cout));
  SumadorCompleto FA22 (.A(A[22]), .B(B[22]), .Cin(FA21_cout), .S(S[22]), .Cout(FA22_cout));
  SumadorCompleto FA21 (.A(A[21]), .B(B[21]), .Cin(FA20_cout), .S(S[21]), .Cout(FA21_cout));
  SumadorCompleto FA20 (.A(A[20]), .B(B[20]), .Cin(FA19_cout), .S(S[20]), .Cout(FA20_cout));
  SumadorCompleto FA19 (.A(A[19]), .B(B[19]), .Cin(FA18_cout), .S(S[19]), .Cout(FA19_cout));
  SumadorCompleto FA18 (.A(A[18]), .B(B[18]), .Cin(FA17_cout), .S(S[18]), .Cout(FA18_cout));
  SumadorCompleto FA17 (.A(A[17]), .B(B[17]), .Cin(FA16_cout), .S(S[17]), .Cout(FA17_cout));
  SumadorCompleto FA16 (.A(A[16]), .B(B[16]), .Cin(FA15_cout), .S(S[16]), .Cout(FA16_cout));
  SumadorCompleto FA15 (.A(A[15]), .B(B[15]), .Cin(FA14_cout), .S(S[15]), .Cout(FA15_cout));
  SumadorCompleto FA14 (.A(A[14]), .B(B[14]), .Cin(FA13_cout), .S(S[14]), .Cout(FA14_cout));
  SumadorCompleto FA13 (.A(A[13]), .B(B[13]), .Cin(FA12_cout), .S(S[13]), .Cout(FA13_cout));
  SumadorCompleto FA12 (.A(A[12]), .B(B[12]), .Cin(FA11_cout), .S(S[12]), .Cout(FA12_cout));
  SumadorCompleto FA11 (.A(A[11]), .B(B[11]), .Cin(FA10_cout), .S(S[11]), .Cout(FA11_cout));
  SumadorCompleto FA10 (.A(A[10]), .B(B[10]), .Cin(FA9_cout), .S(S[10]), .Cout(FA10_cout));
  SumadorCompleto FA9 (.A(A[9]), .B(B[9]), .Cin(FA8_cout), .S(S[9]), .Cout(FA9_cout));
  SumadorCompleto FA8 (.A(A[8]), .B(B[8]), .Cin(FA7_cout), .S(S[8]), .Cout(FA8_cout));
  SumadorCompleto FA7 (.A(A[7]), .B(B[7]), .Cin(FA6_cout), .S(S[7]), .Cout(FA7_cout));
  SumadorCompleto FA6 (.A(A[6]), .B(B[6]), .Cin(FA5_cout), .S(S[6]), .Cout(FA6_cout));
  SumadorCompleto FA5 (.A(A[5]), .B(B[5]), .Cin(FA4_cout), .S(S[5]), .Cout(FA5_cout));
  SumadorCompleto FA4 (.A(A[4]), .B(B[4]), .Cin(FA3_cout), .S(S[4]), .Cout(FA4_cout));
  SumadorCompleto FA3 (.A(A[3]), .B(B[3]), .Cin(FA2_cout), .S(S[3]), .Cout(FA3_cout));
  SumadorCompleto FA2 (.A(A[2]), .B(B[2]), .Cin(FA1_cout), .S(S[2]), .Cout(FA2_cout));
  SumadorCompleto FA1 (.A(A[1]), .B(B[1]), .Cin(FA0_cout), .S(S[1]), .Cout(FA1_cout));
  SumadorCompleto FA0 (.A(A[0]), .B(B[0]), .Cin(Cin), .S(S[0]), .Cout(FA0_cout));

  // Notes on the sheet:
  //   Sumador de 32 bits con acarreo en cascada (ripple-carry): 32 sumadores completos; el acarreo avanza de derecha (bit 0) a izquierda (bit 31)
endmodule

module ALU (
  input  [31:0] A,
  input  [31:0] B,
  input  [3:0] OP,
  output [31:0] Y
);

  wire acarreo, f3_0, f3_1, f3_2, f3_3, f3_4, f3_5, f3_6, f3_7, menor_con_signo, menor_sin_signo, resta,
       signos_distintos;
  wire [31:0] \and , B_o_notB, \or , rep1, sll, slt32, sltu32, sr, sra, srl, suma, \xor ;

  assign \xor  = A ^ B;  // XOR_Gate xor_1, 32 bits wide
  assign \or  = A | B;  // OR_Gate or_1, 32 bits wide
  assign \and  = A & B;  // AND_Gate and_1, 32 bits wide
  Decoder #(.select(3), .enable("false")) decoder_1 (
    .out0(f3_0), .out1(f3_1), .out2(f3_2), .out3(f3_3), .out4(f3_4), .out5(f3_5), .out6(f3_6), .out7(f3_7),
    .sel(OP[2:0]));
  xor xor_2 (signos_distintos, A[31], B[31]);
  Shifter #(.width(32), .shift("ll")) shifter_1 (.in(A), .\dist (B[4:0]), .out(sll));
  Shifter #(.width(32), .shift("lr")) shifter_2 (.in(A), .\dist (B[4:0]), .out(srl));
  Shifter #(.width(32), .shift("ar")) shifter_3 (.in(A), .\dist (B[4:0]), .out(sra));
  or or_2 (resta, OP[3], f3_2, f3_3);
  Multiplexer #(.select(1), .width(32), .enable("false")) multiplexer_1 (.in0(srl), .in1(sra), .out(sr), .sel(OP[3]));
  assign rep1 = {{31{resta}}, resta};  // Bit_Extender bit_extender_1
  assign B_o_notB = B ^ rep1;  // XOR_Gate xor_3, 32 bits wide
  Sumador32 SUMADOR (.A(A), .B(B_o_notB), .Cin(resta), .Cout(acarreo), .S(suma));
  not not_1 (menor_sin_signo, acarreo);
  Multiplexer #(.select(1), .width(1), .enable("false")) multiplexer_2 (
    .in0(suma[31]), .in1(A[31]), .out(menor_con_signo), .sel(signos_distintos));
  assign sltu32 = {{31{1'b0}}, menor_sin_signo};  // Bit_Extender bit_extender_2
  assign slt32 = {{31{1'b0}}, menor_con_signo};  // Bit_Extender bit_extender_3
  Multiplexer #(.select(3), .width(32), .enable("false")) multiplexer_3 (
    .in0(suma), .in1(sll), .in2(slt32), .in3(sltu32), .in4(\xor ), .in5(sr), .in6(\or ), .in7(\and ),
    .out(Y), .sel(OP[2:0]));

  // Other names for the same wires on the sheet: A_31 = A[31]; B_4_0[4:0] = B[4:0]; B_31 = B[31];
  //   OP_2_0[2:0] = OP[2:0]; OP_3 = OP[3]; suma_31 = suma[31]; resultado[31:0] = Y
endmodule

module BancoRegistros (
  input  CLK,
  input  RST,
  input  WE,
  input  [4:0] RD,
  input  [31:0] WD,
  input  [4:0] RS1,
  input  [4:0] RS2,
  output [31:0] R1,
  output [31:0] R2
);

  wire sel_rd_0, sel_rd_1, sel_rd_2, sel_rd_3, sel_rd_4, sel_rd_5, sel_rd_6, sel_rd_7, sel_rd_8, sel_rd_9,
       sel_rd_10, sel_rd_11, sel_rd_12, sel_rd_13, sel_rd_14, sel_rd_15, sel_rd_16, sel_rd_17, sel_rd_18,
       sel_rd_19, sel_rd_20, sel_rd_21, sel_rd_22, sel_rd_23, sel_rd_24, sel_rd_25, sel_rd_26, sel_rd_27,
       sel_rd_28, sel_rd_29, sel_rd_30, sel_rd_31, we_x1, we_x2, we_x3, we_x4, we_x5, we_x6, we_x7, we_x8,
       we_x9, we_x10, we_x11, we_x12, we_x13, we_x14, we_x15, we_x16, we_x17, we_x18, we_x19, we_x20, we_x21,
       we_x22, we_x23, we_x24, we_x25, we_x26, we_x27, we_x28, we_x29, we_x30, we_x31;
  wire [31:0] dato_a_escribir, rep1, x1, x2, x3, x4, x5, x6, x7, x8, x9, x10, x11, x12, x13, x14, x15, x16,
       x17, x18, x19, x20, x21, x22, x23, x24, x25, x26, x27, x28, x29, x30, x31;

  Decoder #(.select(5), .enable("false")) decoder_1 (
    .out0(sel_rd_0), .out1(sel_rd_1), .out2(sel_rd_2), .out3(sel_rd_3), .out4(sel_rd_4), .out5(sel_rd_5),
    .out6(sel_rd_6), .out7(sel_rd_7), .out8(sel_rd_8), .out9(sel_rd_9), .out10(sel_rd_10), .out11(sel_rd_11),
    .out12(sel_rd_12), .out13(sel_rd_13), .out14(sel_rd_14), .out15(sel_rd_15), .out16(sel_rd_16),
    .out17(sel_rd_17), .out18(sel_rd_18), .out19(sel_rd_19), .out20(sel_rd_20), .out21(sel_rd_21),
    .out22(sel_rd_22), .out23(sel_rd_23), .out24(sel_rd_24), .out25(sel_rd_25), .out26(sel_rd_26),
    .out27(sel_rd_27), .out28(sel_rd_28), .out29(sel_rd_29), .out30(sel_rd_30), .out31(sel_rd_31), .sel(RD));
  assign rep1 = {{31{WE}}, WE};  // Bit_Extender bit_extender_1
  Register #(.width(32)) x01_ra (.D(dato_a_escribir), .en(we_x1), .Q(x1), .clk(CLK), .clr(RST));
  Register #(.width(32)) x02_sp (.D(dato_a_escribir), .en(we_x2), .Q(x2), .clk(CLK), .clr(RST));
  Register #(.width(32)) x03_gp (.D(dato_a_escribir), .en(we_x3), .Q(x3), .clk(CLK), .clr(RST));
  Register #(.width(32)) x04_tp (.D(dato_a_escribir), .en(we_x4), .Q(x4), .clk(CLK), .clr(RST));
  Register #(.width(32)) x05_t0 (.D(dato_a_escribir), .en(we_x5), .Q(x5), .clk(CLK), .clr(RST));
  Register #(.width(32)) x06_t1 (.D(dato_a_escribir), .en(we_x6), .Q(x6), .clk(CLK), .clr(RST));
  Register #(.width(32)) x07_t2 (.D(dato_a_escribir), .en(we_x7), .Q(x7), .clk(CLK), .clr(RST));
  Register #(.width(32)) x08_s0_fp (.D(dato_a_escribir), .en(we_x8), .Q(x8), .clk(CLK), .clr(RST));
  Register #(.width(32)) x09_s1 (.D(dato_a_escribir), .en(we_x9), .Q(x9), .clk(CLK), .clr(RST));
  Register #(.width(32)) x10_a0 (.D(dato_a_escribir), .en(we_x10), .Q(x10), .clk(CLK), .clr(RST));
  Register #(.width(32)) x11_a1 (.D(dato_a_escribir), .en(we_x11), .Q(x11), .clk(CLK), .clr(RST));
  Register #(.width(32)) x12_a2 (.D(dato_a_escribir), .en(we_x12), .Q(x12), .clk(CLK), .clr(RST));
  Register #(.width(32)) x13_a3 (.D(dato_a_escribir), .en(we_x13), .Q(x13), .clk(CLK), .clr(RST));
  Register #(.width(32)) x14_a4 (.D(dato_a_escribir), .en(we_x14), .Q(x14), .clk(CLK), .clr(RST));
  Register #(.width(32)) x15_a5 (.D(dato_a_escribir), .en(we_x15), .Q(x15), .clk(CLK), .clr(RST));
  Register #(.width(32)) x16_a6 (.D(dato_a_escribir), .en(we_x16), .Q(x16), .clk(CLK), .clr(RST));
  Register #(.width(32)) x17_a7 (.D(dato_a_escribir), .en(we_x17), .Q(x17), .clk(CLK), .clr(RST));
  Register #(.width(32)) x18_s2 (.D(dato_a_escribir), .en(we_x18), .Q(x18), .clk(CLK), .clr(RST));
  Register #(.width(32)) x19_s3 (.D(dato_a_escribir), .en(we_x19), .Q(x19), .clk(CLK), .clr(RST));
  Register #(.width(32)) x20_s4 (.D(dato_a_escribir), .en(we_x20), .Q(x20), .clk(CLK), .clr(RST));
  Register #(.width(32)) x21_s5 (.D(dato_a_escribir), .en(we_x21), .Q(x21), .clk(CLK), .clr(RST));
  Register #(.width(32)) x22_s6 (.D(dato_a_escribir), .en(we_x22), .Q(x22), .clk(CLK), .clr(RST));
  Register #(.width(32)) x23_s7 (.D(dato_a_escribir), .en(we_x23), .Q(x23), .clk(CLK), .clr(RST));
  Register #(.width(32)) x24_s8 (.D(dato_a_escribir), .en(we_x24), .Q(x24), .clk(CLK), .clr(RST));
  Register #(.width(32)) x25_s9 (.D(dato_a_escribir), .en(we_x25), .Q(x25), .clk(CLK), .clr(RST));
  Register #(.width(32)) x26_s10 (.D(dato_a_escribir), .en(we_x26), .Q(x26), .clk(CLK), .clr(RST));
  Register #(.width(32)) x27_s11 (.D(dato_a_escribir), .en(we_x27), .Q(x27), .clk(CLK), .clr(RST));
  Register #(.width(32)) x28_t3 (.D(dato_a_escribir), .en(we_x28), .Q(x28), .clk(CLK), .clr(RST));
  Register #(.width(32)) x29_t4 (.D(dato_a_escribir), .en(we_x29), .Q(x29), .clk(CLK), .clr(RST));
  Register #(.width(32)) x30_t5 (.D(dato_a_escribir), .en(we_x30), .Q(x30), .clk(CLK), .clr(RST));
  Register #(.width(32)) x31_t6 (.D(dato_a_escribir), .en(we_x31), .Q(x31), .clk(CLK), .clr(RST));
  assign dato_a_escribir = WD & rep1;  // AND_Gate and_1, 32 bits wide
  Multiplexer #(.select(5), .width(32), .enable("false")) multiplexer_1 (
    .in0({32{1'b0}}), .in1(x1), .in2(x2), .in3(x3), .in4(x4), .in5(x5), .in6(x6), .in7(x7), .in8(x8),
    .in9(x9), .in10(x10), .in11(x11), .in12(x12), .in13(x13), .in14(x14), .in15(x15), .in16(x16), .in17(x17),
    .in18(x18), .in19(x19), .in20(x20), .in21(x21), .in22(x22), .in23(x23), .in24(x24), .in25(x25),
    .in26(x26), .in27(x27), .in28(x28), .in29(x29), .in30(x30), .in31(x31), .out(R1), .sel(RS1));
  Multiplexer #(.select(5), .width(32), .enable("false")) multiplexer_2 (
    .in0({32{1'b0}}), .in1(x1), .in2(x2), .in3(x3), .in4(x4), .in5(x5), .in6(x6), .in7(x7), .in8(x8),
    .in9(x9), .in10(x10), .in11(x11), .in12(x12), .in13(x13), .in14(x14), .in15(x15), .in16(x16), .in17(x17),
    .in18(x18), .in19(x19), .in20(x20), .in21(x21), .in22(x22), .in23(x23), .in24(x24), .in25(x25),
    .in26(x26), .in27(x27), .in28(x28), .in29(x29), .in30(x30), .in31(x31), .out(R2), .sel(RS2));
  and and_2 (we_x1, WE, sel_rd_1);
  and and_3 (we_x2, WE, sel_rd_2);
  and and_4 (we_x3, WE, sel_rd_3);
  and and_5 (we_x4, WE, sel_rd_4);
  and and_6 (we_x5, WE, sel_rd_5);
  and and_7 (we_x6, WE, sel_rd_6);
  and and_8 (we_x7, WE, sel_rd_7);
  and and_9 (we_x8, WE, sel_rd_8);
  and and_10 (we_x9, WE, sel_rd_9);
  and and_11 (we_x10, WE, sel_rd_10);
  and and_12 (we_x11, WE, sel_rd_11);
  and and_13 (we_x12, WE, sel_rd_12);
  and and_14 (we_x13, WE, sel_rd_13);
  and and_15 (we_x14, WE, sel_rd_14);
  and and_16 (we_x15, WE, sel_rd_15);
  and and_17 (we_x16, WE, sel_rd_16);
  and and_18 (we_x17, WE, sel_rd_17);
  and and_19 (we_x18, WE, sel_rd_18);
  and and_20 (we_x19, WE, sel_rd_19);
  and and_21 (we_x20, WE, sel_rd_20);
  and and_22 (we_x21, WE, sel_rd_21);
  and and_23 (we_x22, WE, sel_rd_22);
  and and_24 (we_x23, WE, sel_rd_23);
  and and_25 (we_x24, WE, sel_rd_24);
  and and_26 (we_x25, WE, sel_rd_25);
  and and_27 (we_x26, WE, sel_rd_26);
  and and_28 (we_x27, WE, sel_rd_27);
  and and_29 (we_x28, WE, sel_rd_28);
  and and_30 (we_x29, WE, sel_rd_29);
  and and_31 (we_x30, WE, sel_rd_30);
  and and_32 (we_x31, WE, sel_rd_31);

  // Other names for the same wires on the sheet: dato_rs1[31:0] = R1; dato_rs2[31:0] = R2
endmodule

module GeneradorInmediatos (
  input  [31:0] INSTR,
  output [31:0] I,
  output [31:0] S,
  output [31:0] B,
  output [31:0] U,
  output [31:0] J
);

  assign I[31:12] = {{19{INSTR[31]}}, INSTR[31]};  // Bit_Extender bit_extender_1
  assign S[31:12] = {{19{INSTR[31]}}, INSTR[31]};  // Bit_Extender bit_extender_2
  assign B[31:12] = {{19{INSTR[31]}}, INSTR[31]};  // Bit_Extender bit_extender_3
  assign J[31:20] = {{11{INSTR[31]}}, INSTR[31]};  // Bit_Extender bit_extender_4

  assign B[11:0] = {INSTR[7], INSTR[30:25], INSTR[11:8], 1'b0};
  assign I[11:0] = INSTR[31:20];
  assign J[19:0] = {INSTR[19:12], INSTR[20], INSTR[30:21], 1'b0};
  assign S[11:0] = {INSTR[31:25], INSTR[11:7]};
  assign U = {INSTR[31:12], {12{1'b0}}};

  // Other names for the same wires on the sheet: immB[31:1] = {B[31:12], INSTR[7], INSTR[30:25], INSTR[11:8]};
  //   immS[31:0] = {S[31:12], INSTR[31:25], INSTR[11:7]}; INSTR_11_7[4:0] = INSTR[11:7];
  //   INSTR_11_8[3:0] = INSTR[11:8]; INSTR_7 = INSTR[7]; rep3[19:0] = B[31:12]; immI[31:0] = {I[31:12], INSTR[31:20]};
  //   rep1[19:0] = I[31:12]; immJ[31:1] = {J[31:20], INSTR[19:12], INSTR[20], INSTR[30:21]};
  //   immU[31:12] = INSTR[31:12]; INSTR_30_21[9:0] = INSTR[30:21]; INSTR_31_12[19:0] = INSTR[31:12];
  //   INSTR_31_20[11:0] = INSTR[31:20]; INSTR_30_25[5:0] = INSTR[30:25]; INSTR_31_25[6:0] = INSTR[31:25];
  //   INSTR_20 = INSTR[20]; INSTR_19_12[7:0] = INSTR[19:12]; rep4[11:0] = J[31:20]; INSTR_31 = INSTR[31];
  //   rep2[19:0] = S[31:12]
endmodule

module ExpansorRVC (
  input  [15:0] C,
  output [31:0] I32,
  output ILEGAL
);

  wire and22, and23, and38, eq20, ilegal_4spn, ilegal_jr_x0, ilegal_q1_100, imm6_cero, not21, not36, not37,
       or39, rd_cero, rd_es_sp, rs2_cero;
  wire [0:0] joff21;
  wire [12:0] boff13;
  wire [31:0] add_jalr_ebreak, grupo_q1_100, grupo_q2_100, lui_o_addi16sp, mux35, mv_o_jr, sub_xor_or_and;
  wire [31:12] cat7, cat11;
  wire [31:20] cat6, cat10;

  not not_1 (not36, C[12]);
  Comparator #(.width(5), .mode("unsigned")) comparator_1 (.a(C[11:7]), .b(5'b00010), .eq(rd_es_sp));  // open: gt, lt
  Comparator #(.width(2), .mode("unsigned")) comparator_2 (.a(C[11:10]), .b(2'b11), .eq(eq20));  // open: gt, lt
  Comparator #(.width(5), .mode("unsigned")) comparator_3 (.a(C[6:2]), .b({5{1'b0}}), .eq(rs2_cero));  // open: gt, lt
  Comparator #(.width(5), .mode("unsigned")) comparator_4 (.a(C[11:7]), .b({5{1'b0}}), .eq(rd_cero));  // open: gt, lt
  assign cat6 = {{6{C[12]}}, {C[12], C[6:2]}};  // Bit_Extender bit_extender_1
  assign {cat7[31], cat7[19:12], cat7[20], cat7[30:21], joff21[0]} = {{9{C[12]}}, {C[12], C[8], C[10:9], C[6], C[7], C[2], C[11], C[5:3], 1'b0}};  // Bit_Extender bit_extender_2
  assign cat10 = {{2{C[12]}}, {C[12], C[4:3], C[5], C[2], C[6], 4'b0000}};  // Bit_Extender bit_extender_3
  assign cat11 = {{14{C[12]}}, {C[12], C[6:2]}};  // Bit_Extender bit_extender_4
  Comparator #(.width(6), .mode("unsigned")) comparator_5 (
    .a({C[12], C[6:2]}), .b({6{1'b0}}), .eq(imm6_cero));  // open: gt, lt
  not not_2 (not21, C[11]);
  and and_1 (and23, C[12], eq20);
  assign boff13 = {{4{C[12]}}, {C[12], C[6:5], C[2], C[11:10], C[4:3], 1'b0}};  // Bit_Extender bit_extender_5
  Multiplexer #(.select(1), .width(32), .enable("false")) multiplexer_1 (
    .in0({{7{1'b0}}, C[6:2], {8{1'b0}}, C[11:7], 7'b0110011}), .in1({{12{1'b0}}, C[11:7], 15'h67}),
    .out(mv_o_jr), .sel(rs2_cero));
  Multiplexer #(.select(1), .width(32), .enable("false")) multiplexer_2 (
    .in0({{12{1'b0}}, C[11:7], 15'he7}), .in1(32'h100073), .out(mux35), .sel(rd_cero));
  and and_2 (ilegal_jr_x0, not36, rs2_cero, rd_cero);
  not not_3 (not37, C[11]);
  Comparator #(.width(8), .mode("unsigned")) comparator_6 (
    .a({C[10:7], C[12:11], C[5], C[6]}), .b({8{1'b0}}), .eq(ilegal_4spn));  // open: gt, lt
  Multiplexer #(.select(2), .width(32), .enable("false")) multiplexer_3 (
    .in0({9'h81, C[4:2], 2'b01, C[9:7], 5'b00001, C[9:7], 7'b0110011}),
    .in1({9'h1, C[4:2], 2'b01, C[9:7], 5'b10001, C[9:7], 7'b0110011}),
    .in2({9'h1, C[4:2], 2'b01, C[9:7], 5'b11001, C[9:7], 7'b0110011}),
    .in3({9'h1, C[4:2], 2'b01, C[9:7], 5'b11101, C[9:7], 7'b0110011}), .out(sub_xor_or_and), .sel(C[6:5]));
  and and_3 (and22, C[12], not21);
  Multiplexer #(.select(1), .width(32), .enable("false")) multiplexer_4 (
    .in0({{7{1'b0}}, C[6:2], C[11:7], 3'b000, C[11:7], 7'b0110011}), .in1(mux35), .out(add_jalr_ebreak),
    .sel(rs2_cero));
  and and_4 (and38, C[12], not37);
  Multiplexer #(.select(1), .width(32), .enable("false")) multiplexer_5 (
    .in0({cat11, C[11:7], 7'b0110111}), .in1({cat10, 20'h10113}), .out(lui_o_addi16sp), .sel(rd_es_sp));
  Multiplexer #(.select(2), .width(32), .enable("false")) multiplexer_6 (
    .in0({{7{1'b0}}, C[6:2], 2'b01, C[9:7], 5'b10101, C[9:7], 7'b0010011}),
    .in1({7'b0100000, C[6:2], 2'b01, C[9:7], 5'b10101, C[9:7], 7'b0010011}),
    .in2({cat6, 2'b01, C[9:7], 5'b11101, C[9:7], 7'b0010011}), .in3(sub_xor_or_and), .out(grupo_q1_100),
    .sel(C[11:10]));
  or or_1 (ilegal_q1_100, and22, and23);
  Multiplexer #(.select(1), .width(32), .enable("false")) multiplexer_7 (
    .in0(mv_o_jr), .in1(add_jalr_ebreak), .out(grupo_q2_100), .sel(C[12]));
  or or_2 (or39, ilegal_q1_100, and38);
  Multiplexer #(.select(5), .width(1), .enable("false")) multiplexer_8 (
    .in0(ilegal_4spn), .in1(1'b1), .in2(1'b0), .in3(1'b1), .in4(1'b1), .in5(1'b1), .in6(1'b0), .in7(1'b1),
    .in8(1'b0), .in9(1'b0), .in10(1'b0), .in11(imm6_cero), .in12(or39), .in13(1'b0), .in14(1'b0),
    .in15(1'b0), .in16(C[12]), .in17(1'b1), .in18(rd_cero), .in19(1'b1), .in20(ilegal_jr_x0), .in21(1'b1),
    .in22(1'b0), .in23(1'b1), .in24(1'b1), .in25(1'b1), .in26(1'b1), .in27(1'b1), .in28(1'b1), .in29(1'b1),
    .in30(1'b1), .in31(1'b1), .out(ILEGAL), .sel({C[1:0], C[15:13]}));
  Multiplexer #(.select(5), .width(32), .enable("false")) multiplexer_9 (
    .in0({2'b00, C[10:7], C[12:11], C[5], C[6], 12'h41, C[4:2], 7'b0010011}), .in1({32{1'b0}}),
    .in2({{5{1'b0}}, C[5], C[12:10], C[6], 4'b0001, C[9:7], 5'b01001, C[4:2], 7'b0000011}), .in3({32{1'b0}}),
    .in4({32{1'b0}}), .in5({32{1'b0}}),
    .in6({{5{1'b0}}, C[5], C[12], 2'b01, C[4:2], 2'b01, C[9:7], 3'b010, C[11:10], C[6], 9'h23}),
    .in7({32{1'b0}}), .in8({cat6, C[11:7], 3'b000, C[11:7], 7'b0010011}), .in9({cat7, 12'hef}),
    .in10({cat6, {8{1'b0}}, C[11:7], 7'b0010011}), .in11(lui_o_addi16sp), .in12(grupo_q1_100),
    .in13({cat7, 12'h6f}),
    .in14({boff13[12], boff13[10:5], 7'b0000001, C[9:7], 3'b000, boff13[4:1], boff13[11], 7'b1100011}),
    .in15({boff13[12], boff13[10:5], 7'b0000001, C[9:7], 3'b001, boff13[4:1], boff13[11], 7'b1100011}),
    .in16({{7{1'b0}}, C[6:2], C[11:7], 3'b001, C[11:7], 7'b0010011}), .in17({32{1'b0}}),
    .in18({4'b0000, C[3:2], C[12], C[6:4], 10'h12, C[11:7], 7'b0000011}), .in19({32{1'b0}}),
    .in20(grupo_q2_100), .in21({32{1'b0}}), .in22({4'b0000, C[8:7], C[12], C[6:2], 8'h12, C[11:9], 9'h23}),
    .in23({32{1'b0}}), .in24({32{1'b0}}), .in25({32{1'b0}}), .in26({32{1'b0}}), .in27({32{1'b0}}),
    .in28({32{1'b0}}), .in29({32{1'b0}}), .in30({32{1'b0}}), .in31({32{1'b0}}), .out(I32),
    .sel({C[1:0], C[15:13]}));

  // Other names for the same wires on the sheet: cat8[31:12] = cat7; jenc[19:0] = cat7;
  //   joff21[20:1] = {cat7[31], cat7[19:12], cat7[20], cat7[30:21]}; joff21_19_12[7:0] = cat7[19:12];
  //   joff21_11 = cat7[20]; joff21_10_1[9:0] = cat7[30:21]; joff21_20 = cat7[31]; nzimm_16sp_sext[11:0] = cat10;
  //   lui_imm20[19:0] = cat11; cat9 (some bits) = {cat6, C[11:7]}; cat15 (some bits) = {cat6, C[9:7], C[9:7]};
  //   imm6_sext[11:0] = cat6; boff13_11 = boff13[11]; cat24[4:0] = {boff13[4:1], boff13[11]};
  //   cat26 (some bits) = {boff13[12], boff13[10:5], C[9:7], boff13[4:1], boff13[11]};
  //   cat27 (some bits) = {boff13[12], boff13[10:5], C[9:7], boff13[4:1], boff13[11]}; boff13_4_1[3:0] = boff13[4:1];
  //   C_7 = C[7]; C_8_7[1:0] = C[8:7]; C_9_7[2:0] = C[9:7]; C_10_7[3:0] = C[10:7]; C_11_7[4:0] = C[11:7];
  //   cat2[2:0] = C[9:7]; cat3 (some bits) = {C[10:7], C[12:11], C[5], C[6], C[4:2]};
  //   cat4 (some bits) = {C[5], C[12:10], C[6], C[9:7], C[4:2]};
  //   cat5 (some bits) = {C[5], C[12], C[4:2], C[9:7], C[11:10], C[6]}; cat6 (some bits) = {C[11:7], C[11:7]};
  //   cat11[11:7] = C[11:7]; cat12 (some bits) = {C[6:2], C[9:7], C[9:7]};
  //   cat14 (some bits) = {C[6:2], C[9:7], C[9:7]}; cat16 (some bits) = {C[4:2], C[9:7], C[9:7]};
  //   cat17 (some bits) = {C[4:2], C[9:7], C[9:7]}; cat18 (some bits) = {C[4:2], C[9:7], C[9:7]};
  //   cat19 (some bits) = {C[4:2], C[9:7], C[9:7]}; cat28 (some bits) = {C[6:2], C[11:7], C[11:7]};
  //   cat29 (some bits) = {C[3:2], C[12], C[6:4], C[11:7]}; cat30 (some bits) = {C[8:7], C[12], C[6:2], C[11:9]};
  //   cat31[19:15] = C[11:7]; cat32 (some bits) = {C[6:2], C[11:7]}; cat33[19:15] = C[11:7];
  //   cat34 (some bits) = {C[6:2], C[11:7], C[11:7]};
  //   joff12[11:1] = {C[12], C[8], C[10:9], C[6], C[7], C[2], C[11], C[5:3]};
  //   nzuimm_4spn[9:2] = {C[10:7], C[12:11], C[5], C[6]}; nzuimm_4spn_9_2[7:0] = {C[10:7], C[12:11], C[5], C[6]};
  //   uimm_swsp[7:2] = {C[8:7], C[12:9]}; uimm_swsp_11_5[2:0] = {C[8:7], C[12]}; C_8 = C[8]; C_10_9[1:0] = C[10:9];
  //   C_12_9[3:0] = C[12:9]; uimm_swsp_4_0[4:2] = C[11:9]; boff13_10_5[5:0] = boff13[10:5];
  //   cat25[6:0] = {boff13[12], boff13[10:5]}; boff13_12 = boff13[12];
  //   boff9[8:1] = {C[12], C[6:5], C[2], C[11:10], C[4:3]}; C_11_10[1:0] = C[11:10]; C_12_10[2:0] = C[12:10];
  //   uimm_lw[6:2] = {C[5], C[12:10], C[6]}; uimm_lw_4_0[4:2] = {C[11:10], C[6]}; C_11 = C[11]; C_11_10_1 = C[11];
  //   C_12_11[1:0] = C[12:11]; C_2 = C[2]; C_3_2[1:0] = C[3:2]; C_4_2[2:0] = C[4:2]; C_6_2[4:0] = C[6:2];
  //   cat1[2:0] = C[4:2]; cat13[4:0] = C[6:2]; imm6[5:0] = {C[12], C[6:2]};
  //   nzimm_16sp[9:4] = {C[12], C[4:3], C[5], C[2], C[6]}; shamt12[4:0] = C[6:2];
  //   uimm_lwsp[7:2] = {C[3:2], C[12], C[6:4]}; C_4_3[1:0] = C[4:3]; C_5_3[2:0] = C[5:3]; C_6_4[2:0] = C[6:4];
  //   C_5 = C[5]; C_6_5[1:0] = C[6:5]; uimm_lw_11_5[1:0] = {C[5], C[12]}; C_6 = C[6]; C_12 = C[12];
  //   instr32[31:0] = I32; ILEGAL_2 = ILEGAL; ilegal_t = ILEGAL; C_15_13[2:0] = C[15:13];
  //   op_f3[4:0] = {C[1:0], C[15:13]}; C_1_0[1:0] = C[1:0]
endmodule

module Decodificador (
  input  [31:0] INSTR,
  input  ES_C,
  input  ILEGAL_C,
  output LUI,
  output AUIPC,
  output JAL,
  output JALR,
  output BRANCH,
  output LOAD,
  output STORE,
  output CSR,
  output ECALL,
  output EBREAK,
  output MRET,
  output WFI,
  output ILEGAL,
  output [3:0] ALUOP,
  output [1:0] ALU_A,
  output ALU_B_IMM,
  output [1:0] SEL_IMM,
  output ESCRIBE_RD,
  output [2:0] SEL_WB
);

  wire alt, and12, and14, and17, and21, and23, and24, bits_1_0_son_11, eq1, eq2, eq3, eq4, es_FENCE, es_OP,
       es_OPIMM, es_SYSTEM, f3_0, f3_1, f3_2, f3_3, f3_4, f3_5, f3_6, f3_7, f7_0, f7_01, f7_20,
       ilegal_branch, ilegal_fence, ilegal_jalr, ilegal_load, ilegal_op, ilegal_opimm, ilegal_store,
       ilegal_system, nor8, nor13, nor18, nor19, nor20, not5, not6, not10, not11, not22, opcode_0, opcode_1,
       opcode_2, opcode_3, opcode_4, opcode_5, opcode_6, opcode_7, opcode_8, opcode_9, opcode_10, opcode_11,
       opcode_12, opcode_13, opcode_14, opcode_15, opcode_16, opcode_17, opcode_18, opcode_19, opcode_20,
       opcode_21, opcode_22, opcode_23, opcode_24, opcode_25, opcode_26, opcode_27, opcode_28, opcode_29,
       opcode_30, opcode_31, opcode_valido, or7, or9, or15, or16, or27, usa_funct3;

  Comparator #(.width(32), .mode("unsigned")) comparator_1 (.a(INSTR), .b(32'h73), .eq(eq1));  // open: gt, lt
  Comparator #(.width(32), .mode("unsigned")) comparator_2 (.a(INSTR), .b(32'h100073), .eq(eq2));  // open: gt, lt
  Comparator #(.width(32), .mode("unsigned")) comparator_3 (.a(INSTR), .b(32'h30200073), .eq(eq3));  // open: gt, lt
  Comparator #(.width(32), .mode("unsigned")) comparator_4 (.a(INSTR), .b(32'h10500073), .eq(eq4));  // open: gt, lt
  and and_1 (and21, ES_C, ILEGAL_C);
  Decoder #(.select(5), .enable("false")) decoder_1 (
    .out0(opcode_0), .out1(opcode_1), .out2(opcode_2), .out3(opcode_3), .out4(opcode_4), .out5(opcode_5),
    .out6(opcode_6), .out7(opcode_7), .out8(opcode_8), .out9(opcode_9), .out10(opcode_10), .out11(opcode_11),
    .out12(opcode_12), .out13(opcode_13), .out14(opcode_14), .out15(opcode_15), .out16(opcode_16),
    .out17(opcode_17), .out18(opcode_18), .out19(opcode_19), .out20(opcode_20), .out21(opcode_21),
    .out22(opcode_22), .out23(opcode_23), .out24(opcode_24), .out25(opcode_25), .out26(opcode_26),
    .out27(opcode_27), .out28(opcode_28), .out29(opcode_29), .out30(opcode_30), .out31(opcode_31),
    .sel(INSTR[6:2]));
  Decoder #(.select(3), .enable("false")) decoder_2 (
    .out0(f3_0), .out1(f3_1), .out2(f3_2), .out3(f3_3), .out4(f3_4), .out5(f3_5), .out6(f3_6), .out7(f3_7),
    .sel(INSTR[14:12]));
  Comparator #(.width(2), .mode("unsigned")) comparator_5 (
    .a(INSTR[1:0]), .b(2'b11), .eq(bits_1_0_son_11));  // open: gt, lt
  Comparator #(.width(7), .mode("unsigned")) comparator_6 (.a(INSTR[31:25]), .b({7{1'b0}}), .eq(f7_0));  // open: gt, lt
  Comparator #(.width(7), .mode("unsigned")) comparator_7 (
    .a(INSTR[31:25]), .b(7'b0100000), .eq(f7_20));  // open: gt, lt
  Comparator #(.width(7), .mode("unsigned")) comparator_8 (
    .a(INSTR[31:25]), .b(7'b0000001), .eq(f7_01));  // open: gt, lt
  not not_1 (not5, f3_0);
  not not_2 (not6, f3_4);
  or or_1 (or7, f3_3, f3_6, f3_7);
  or or_2 (or9, f3_2, f3_3);
  not not_3 (not10, f3_0);
  not not_4 (not11, f7_0);
  or or_3 (or16, f3_0, f3_5);
  and and_2 (LOAD, bits_1_0_son_11, opcode_0);
  and and_3 (es_FENCE, bits_1_0_son_11, opcode_3);
  and and_4 (es_OPIMM, bits_1_0_son_11, opcode_4);
  and and_5 (ALU_A[0], bits_1_0_son_11, opcode_5);
  and and_6 (SEL_IMM[0], bits_1_0_son_11, opcode_8);
  and and_7 (es_OP, bits_1_0_son_11, opcode_12);
  and and_8 (ALU_A[1], bits_1_0_son_11, opcode_13);
  and and_9 (BRANCH, bits_1_0_son_11, opcode_24);
  and and_10 (JALR, bits_1_0_son_11, opcode_25);
  and and_11 (JAL, bits_1_0_son_11, opcode_27);
  and and_12 (es_SYSTEM, bits_1_0_son_11, opcode_28);
  nor nor_1 (nor8, f3_0, f3_1, f3_2);
  nor nor_2 (nor13, f7_0, f7_20);
  nor nor_3 (nor19, f3_0, f3_1);
  and and_13 (SEL_WB[2], es_OP, f7_01);
  and and_14 (ilegal_load, LOAD, or7);
  and and_15 (ilegal_store, SEL_IMM[0], nor8);
  and and_16 (ilegal_jalr, JALR, not10);
  and and_17 (and12, f3_1, not11);
  and and_18 (and14, f3_5, nor13);
  and and_19 (and17, f7_20, or16);
  and and_20 (ilegal_fence, es_FENCE, nor19);
  or or_4 (usa_funct3, es_OP, es_OPIMM);
  and and_21 (and23, es_OP, INSTR[30]);
  and and_22 (and24, es_OPIMM, f3_5, INSTR[30]);
  or or_5 (ALU_B_IMM, es_OPIMM, LOAD, SEL_IMM[0], ALU_A[1], ALU_A[0], JALR);
  or or_6 (SEL_IMM[1], ALU_A[1], ALU_A[0]);
  or or_7 (or27, JAL, JALR);
  and and_23 (ECALL, es_SYSTEM, eq1);
  and and_24 (EBREAK, es_SYSTEM, eq2);
  and and_25 (MRET, es_SYSTEM, eq3);
  and and_26 (WFI, es_SYSTEM, eq4);
  and and_27 (CSR, es_SYSTEM, not5, not6);
  or or_8 (opcode_valido, LOAD, es_FENCE, es_OPIMM, ALU_A[0], SEL_IMM[0], es_OP, ALU_A[1], BRANCH, JALR, JAL, es_SYSTEM);
  and and_28 (ilegal_branch, BRANCH, or9);
  or or_9 (or15, and12, and14);
  nor nor_4 (nor18, f7_0, f7_01, and17);
  nor nor_5 (nor20, ECALL, EBREAK, MRET, WFI, CSR);
  not not_5 (not22, opcode_valido);
  or or_10 (alt, and23, and24);
  or or_11 (ESCRIBE_RD, ALU_A[1], ALU_A[0], JAL, JALR, LOAD, es_OPIMM, es_OP, CSR);
  or or_12 (SEL_WB[0], or27, CSR);
  or or_13 (SEL_WB[1], LOAD, CSR);
  and and_29 (ilegal_op, es_OP, nor18);
  and and_30 (ilegal_opimm, es_OPIMM, or15);
  and and_31 (ilegal_system, es_SYSTEM, nor20);
  Multiplexer #(.select(1), .width(4), .enable("false")) multiplexer_1 (
    .in0(4'b0000), .in1({alt, INSTR[14:12]}), .out(ALUOP), .sel(usa_funct3));
  or or_14 (ILEGAL, and21, not22, ilegal_load, ilegal_store, ilegal_branch, ilegal_jalr, ilegal_opimm, ilegal_op, ilegal_fence, ilegal_system);

  assign AUIPC = ALU_A[0];
  assign LUI = ALU_A[1];
  assign STORE = SEL_IMM[0];

  // Other names for the same wires on the sheet: es_AUIPC = ALU_A[0]; sel_alu_a[1:0] = ALU_A; es_LUI = ALU_A[1];
  //   alu_b_inmediato = ALU_B_IMM; ALUOP_2[3:0] = ALUOP; aluop_t[3:0] = ALUOP; es_BRANCH = BRANCH;
  //   cat25[3:0] = {alt, INSTR[14:12]}; INSTR_14_12[2:0] = INSTR[14:12]; es_CSR = CSR; es_EBREAK = EBREAK;
  //   es_ECALL = ECALL; ESCRIBE_RD_2 = ESCRIBE_RD; escribe_rd_t = ESCRIBE_RD; ILEGAL_2 = ILEGAL; ilegal_t = ILEGAL;
  //   INSTR_1_0[1:0] = INSTR[1:0]; INSTR_6_2[4:0] = INSTR[6:2]; INSTR_31_25[6:0] = INSTR[31:25]; INSTR_30 = INSTR[30];
  //   es_JAL = JAL; es_JALR = JALR; es_LOAD = LOAD; es_MRET = MRET; es_STORE = SEL_IMM[0]; SEL_IMM_2[1:0] = SEL_IMM;
  //   sel_imm_t[1:0] = SEL_IMM; or26 = SEL_IMM[1]; or28 = SEL_WB[0]; SEL_WB_2[2:0] = SEL_WB; sel_wb_t[2:0] = SEL_WB;
  //   or29 = SEL_WB[1]; es_MULDIV = SEL_WB[2]; es_WFI = WFI
endmodule

module UnidadMulDiv (
  input  [31:0] A,
  input  [31:0] B,
  input  [2:0] F3,
  output [31:0] Y
);

  wire div_por_cero, xor3;
  wire [31:0] abs_a, abs_b, coc_abs, coc_s, coc_u, corr_a, corr_b, div, divu, menos_a, menos_b, menos_coc,
       menos_rest, mulh, mulhsu, prod_hi_u, prod_lo, rem, remu, rep1, rep2, rest_abs, rest_s, rest_u;

  Multiplier #(.width(32)) multiplier_1 (.a(A), .b(B), .out(prod_lo), .cin({32{1'b0}}), .cout(prod_hi_u));
  Comparator #(.width(32), .mode("unsigned")) comparator_1 (.a(B), .b({32{1'b0}}), .eq(div_por_cero));  // open: gt, lt
  Divider #(.width(32)) divider_1 (.a(A), .b(B), .out(coc_u), .upper({32{1'b0}}), .rem(rest_u));
  Negator #(.width(32)) negator_1 (.in(A), .out(menos_a));
  Negator #(.width(32)) negator_2 (.in(B), .out(menos_b));
  assign rep1 = {{31{A[31]}}, A[31]};  // Bit_Extender bit_extender_1
  assign rep2 = {{31{B[31]}}, B[31]};  // Bit_Extender bit_extender_2
  Multiplexer #(.select(1), .width(32), .enable("false")) multiplexer_1 (
    .in0(A), .in1(menos_a), .out(abs_a), .sel(A[31]));
  Multiplexer #(.select(1), .width(32), .enable("false")) multiplexer_2 (
    .in0(B), .in1(menos_b), .out(abs_b), .sel(B[31]));
  xor xor_1 (xor3, A[31], B[31]);
  Multiplexer #(.select(1), .width(32), .enable("false")) multiplexer_3 (
    .in0(rest_u), .in1(A), .out(remu), .sel(div_por_cero));
  Multiplexer #(.select(1), .width(32), .enable("false")) multiplexer_4 (
    .in0(coc_u), .in1({32{1'b1}}), .out(divu), .sel(div_por_cero));
  assign corr_a = B & rep1;  // AND_Gate and_1, 32 bits wide
  assign corr_b = A & rep2;  // AND_Gate and_2, 32 bits wide
  Divider #(.width(32)) divider_2 (.a(abs_a), .b(abs_b), .out(coc_abs), .upper({32{1'b0}}), .rem(rest_abs));
  Subtractor #(.width(32)) subtractor_1 (.a(prod_hi_u), .b(corr_a), .out(mulhsu));  // open: bin, bout
  Negator #(.width(32)) negator_3 (.in(coc_abs), .out(menos_coc));
  Negator #(.width(32)) negator_4 (.in(rest_abs), .out(menos_rest));
  Subtractor #(.width(32)) subtractor_2 (.a(mulhsu), .b(corr_b), .out(mulh));  // open: bin, bout
  Multiplexer #(.select(1), .width(32), .enable("false")) multiplexer_5 (
    .in0(coc_abs), .in1(menos_coc), .out(coc_s), .sel(xor3));
  Multiplexer #(.select(1), .width(32), .enable("false")) multiplexer_6 (
    .in0(rest_abs), .in1(menos_rest), .out(rest_s), .sel(A[31]));
  Multiplexer #(.select(1), .width(32), .enable("false")) multiplexer_7 (
    .in0(coc_s), .in1({32{1'b1}}), .out(div), .sel(div_por_cero));
  Multiplexer #(.select(1), .width(32), .enable("false")) multiplexer_8 (
    .in0(rest_s), .in1(A), .out(rem), .sel(div_por_cero));
  Multiplexer #(.select(3), .width(32), .enable("false")) multiplexer_9 (
    .in0(prod_lo), .in1(mulh), .in2(mulhsu), .in3(prod_hi_u), .in4(div), .in5(divu), .in6(rem), .in7(remu),
    .out(Y), .sel(F3));

  // Other names for the same wires on the sheet: A_31 = A[31]; B_31 = B[31]; resultado_md[31:0] = Y
endmodule

module UnidadCargaAlmacen (
  input  [2:0] F3,
  input  [1:0] ADDR_LO,
  input  [31:0] RS2,
  input  [31:0] RDATA,
  output [31:0] WDATA,
  output [3:0] WSTRB,
  output DESALINEADO,
  output [31:0] LDATA
);

  wire byte_sel_0, byte_sel_1, byte_sel_2, byte_sel_3, not1, not2, or3;
  wire [31:0] lb, lbu, lh, lhu, rdata_desplazado;

  Decoder #(.select(2), .enable("false")) decoder_1 (
    .out0(byte_sel_0), .out1(byte_sel_1), .out2(byte_sel_2), .out3(byte_sel_3), .sel(ADDR_LO));
  not not_1 (not1, ADDR_LO[1]);
  not not_2 (not2, ADDR_LO[1]);
  or or_1 (or3, ADDR_LO[0], ADDR_LO[1]);
  Shifter #(.width(32), .shift("lr")) shifter_1 (.in(RDATA), .\dist ({ADDR_LO, 3'b000}), .out(rdata_desplazado));
  Multiplexer #(.select(2), .width(32), .enable("false")) multiplexer_1 (
    .in0({RS2[7:0], RS2[7:0], RS2[7:0], RS2[7:0]}), .in1({RS2[15:0], RS2[15:0]}), .in2(RS2), .in3(RS2),
    .out(WDATA), .sel(F3[1:0]));
  Multiplexer #(.select(2), .width(1), .enable("false")) multiplexer_2 (
    .in0(1'b0), .in1(ADDR_LO[0]), .in2(or3), .in3(1'b1), .out(DESALINEADO), .sel(F3[1:0]));
  Multiplexer #(.select(2), .width(4), .enable("false")) multiplexer_3 (
    .in0({byte_sel_3, byte_sel_2, byte_sel_1, byte_sel_0}), .in1({{2{ADDR_LO[1]}}, not2, not1}),
    .in2(4'b1111), .in3(4'b1111), .out(WSTRB), .sel(F3[1:0]));
  assign lb = {{24{rdata_desplazado[7]}}, rdata_desplazado[7:0]};  // Bit_Extender bit_extender_1
  assign lbu = {{24{1'b0}}, rdata_desplazado[7:0]};  // Bit_Extender bit_extender_2
  assign lh = {{16{rdata_desplazado[15]}}, rdata_desplazado[15:0]};  // Bit_Extender bit_extender_3
  assign lhu = {{16{1'b0}}, rdata_desplazado[15:0]};  // Bit_Extender bit_extender_4
  Multiplexer #(.select(3), .width(32), .enable("false")) multiplexer_4 (
    .in0(lb), .in1(lh), .in2(RDATA), .in3(RDATA), .in4(lbu), .in5(lhu), .in6(RDATA), .in7(RDATA),
    .out(LDATA), .sel(F3));

  // Other names for the same wires on the sheet: DESALINEADO_2 = DESALINEADO; desalineado_t = DESALINEADO;
  //   ADDR_LO_0 = ADDR_LO[0]; desplaz[4:3] = ADDR_LO; F3_1_0[1:0] = F3[1:0]; F3_2 = F3[2];
  //   byte_x4[31:0] = {RS2[7:0], RS2[7:0], RS2[7:0], RS2[7:0]}; half_x2[31:0] = {RS2[15:0], RS2[15:0]};
  //   RS2_7_0[7:0] = RS2[7:0]; RS2_15_0[15:0] = RS2[15:0]; dato_cargado[31:0] = LDATA;
  //   rdata_desplazado_7_0[7:0] = rdata_desplazado[7:0]; rdata_desplazado_15_0[15:0] = rdata_desplazado[15:0];
  //   strb_byte[3:0] = {byte_sel_3, byte_sel_2, byte_sel_1, byte_sel_0};
  //   strb_half[3:0] = {{2{ADDR_LO[1]}}, not2, not1}; ADDR_LO_1 = ADDR_LO[1]; WDATA_2[31:0] = WDATA;
  //   wdata_t[31:0] = WDATA; WSTRB_2[3:0] = WSTRB; wstrb_t[3:0] = WSTRB
endmodule

module RegistrosCSR (
  input  CLK,
  input  RST,
  input  [11:0] ADDR,
  input  [31:0] SRC,
  input  [1:0] OP,
  input  WE,
  input  TRAP,
  input  [31:0] CAUSE,
  input  [31:0] EPC,
  input  [31:0] TVAL,
  input  MRET,
  input  RETIRE,
  input  [31:0] IRQS,
  output [31:0] RDATA,
  output [31:0] MTVEC_BASE,
  output [31:0] PC_RETORNO,
  output MIE_GLOBAL,
  output [31:0] INSTRET,
  output [31:0] CICLOS
);

  wire and15, and16, and17, cuenta_ciclos, cuenta_instr, cuenta_mpccr, en_mstatus, mcycle_max, mcycleh_max,
       MIE_sig, minstret_max, minstreth_max, mpccr_max, MPIE_sig, mux4, mux5, nor14, or7, or9, or11, or18,
       sel_cycle, sel_cycleh, sel_instret, sel_instreth, sel_marchid, sel_mcause, sel_mcycle, sel_mcycleh,
       sel_mepc, sel_mhartid, sel_mie, sel_mimpid, sel_minstret, sel_minstreth, sel_mip, sel_misa, sel_mpccr,
       sel_mpcer, sel_mpcmr, sel_mscratch, sel_mstatus, sel_mtval, sel_mtvec, sel_mvendorid, we_cycle,
       we_cycleh, we_instret, we_instreth, we_marchid, we_mcause, we_mcycle, we_mcycleh, we_mepc, we_mhartid,
       we_mie, we_mimpid, we_minstret, we_minstreth, we_mip, we_misa, we_mpccr, we_mpcer, we_mpcmr,
       we_mscratch, we_mstatus, we_mtval, we_mtvec, we_mvendorid;
  wire [0:0] valor_nuevo;
  wire [7:7] mstatus;
  wire [31:0] and3, mcause, mcycleh, mepc_sig, mie, minstreth, mpccr, mpcer, mpcmr, mscratch, mtval, mux8,
       mux10, not1, or2, qx13, rd_cycle, rd_cycleh, rd_instret, rd_instreth, rd_marchid, rd_mcause,
       rd_mcycle, rd_mcycleh, rd_mepc, rd_mie, rd_mimpid, rd_minstret, rd_minstreth, rd_mip, rd_misa,
       rd_mpccr, rd_mpcer, rd_mpcmr, rd_mscratch, rd_mstatus, rd_mtval, rd_mtvec, rd_mvendorid, rep19, rep20,
       rep21, rep22, rep23, rep24, rep25, rep26, rep27, rep28, rep29, rep30, rep31, rep32, rep33, rep34,
       rep35, rep36, rep37, xor12;
  wire [31:1] cat6;

  Comparator #(.width(12), .mode("unsigned")) comparator_1 (.a(ADDR), .b(12'h300), .eq(sel_mstatus));  // open: gt, lt
  Comparator #(.width(12), .mode("unsigned")) comparator_2 (.a(ADDR), .b(12'h301), .eq(sel_misa));  // open: gt, lt
  Comparator #(.width(12), .mode("unsigned")) comparator_3 (.a(ADDR), .b(12'h304), .eq(sel_mie));  // open: gt, lt
  Comparator #(.width(12), .mode("unsigned")) comparator_4 (.a(ADDR), .b(12'h305), .eq(sel_mtvec));  // open: gt, lt
  Comparator #(.width(12), .mode("unsigned")) comparator_5 (.a(ADDR), .b(12'h340), .eq(sel_mscratch));  // open: gt, lt
  Comparator #(.width(12), .mode("unsigned")) comparator_6 (.a(ADDR), .b(12'h341), .eq(sel_mepc));  // open: gt, lt
  Comparator #(.width(12), .mode("unsigned")) comparator_7 (.a(ADDR), .b(12'h342), .eq(sel_mcause));  // open: gt, lt
  Comparator #(.width(12), .mode("unsigned")) comparator_8 (.a(ADDR), .b(12'h343), .eq(sel_mtval));  // open: gt, lt
  Comparator #(.width(12), .mode("unsigned")) comparator_9 (.a(ADDR), .b(12'h344), .eq(sel_mip));  // open: gt, lt
  Comparator #(.width(12), .mode("unsigned")) comparator_10 (
    .a(ADDR), .b(12'hf11), .eq(sel_mvendorid));  // open: gt, lt
  Comparator #(.width(12), .mode("unsigned")) comparator_11 (.a(ADDR), .b(12'hf12), .eq(sel_marchid));  // open: gt, lt
  Comparator #(.width(12), .mode("unsigned")) comparator_12 (.a(ADDR), .b(12'hf13), .eq(sel_mimpid));  // open: gt, lt
  Comparator #(.width(12), .mode("unsigned")) comparator_13 (.a(ADDR), .b(12'hf14), .eq(sel_mhartid));  // open: gt, lt
  Comparator #(.width(12), .mode("unsigned")) comparator_14 (.a(ADDR), .b(12'h7e0), .eq(sel_mpcer));  // open: gt, lt
  Comparator #(.width(12), .mode("unsigned")) comparator_15 (.a(ADDR), .b(12'h7e1), .eq(sel_mpcmr));  // open: gt, lt
  Comparator #(.width(12), .mode("unsigned")) comparator_16 (.a(ADDR), .b(12'h7e2), .eq(sel_mpccr));  // open: gt, lt
  Comparator #(.width(12), .mode("unsigned")) comparator_17 (.a(ADDR), .b(12'hb00), .eq(sel_mcycle));  // open: gt, lt
  Comparator #(.width(12), .mode("unsigned")) comparator_18 (.a(ADDR), .b(12'hb80), .eq(sel_mcycleh));  // open: gt, lt
  Comparator #(.width(12), .mode("unsigned")) comparator_19 (.a(ADDR), .b(12'hb02), .eq(sel_minstret));  // open: gt, lt
  Comparator #(.width(12), .mode("unsigned")) comparator_20 (
    .a(ADDR), .b(12'hb82), .eq(sel_minstreth));  // open: gt, lt
  Comparator #(.width(12), .mode("unsigned")) comparator_21 (.a(ADDR), .b(12'hc00), .eq(sel_cycle));  // open: gt, lt
  Comparator #(.width(12), .mode("unsigned")) comparator_22 (.a(ADDR), .b(12'hc80), .eq(sel_cycleh));  // open: gt, lt
  Comparator #(.width(12), .mode("unsigned")) comparator_23 (.a(ADDR), .b(12'hc02), .eq(sel_instret));  // open: gt, lt
  Comparator #(.width(12), .mode("unsigned")) comparator_24 (.a(ADDR), .b(12'hc82), .eq(sel_instreth));  // open: gt, lt
  assign not1 = ~SRC;  // NOT_Gate not_1, 32 bits wide
  Register #(.width(32)) u_mcause (.D(mux8), .en(or9), .Q(mcause), .clk(CLK), .clr(RST));
  Register #(.width(32)) u_mtval (.D(mux10), .en(or11), .Q(mtval), .clk(CLK), .clr(RST));
  Register #(.width(1)) mstatus_MIE (.D(MIE_sig), .en(en_mstatus), .Q(MIE_GLOBAL), .clk(CLK), .clr(RST));
  Register #(.width(1)) mstatus_MPIE (.D(MPIE_sig), .en(en_mstatus), .Q(mstatus[7]), .clk(CLK), .clr(RST));
  Register #(.width(32)) u_mie (.D({cat6, valor_nuevo[0]}), .en(we_mie), .Q(mie), .clk(CLK), .clr(RST));
  Register #(.width(32)) u_mscratch (.D({cat6, valor_nuevo[0]}), .en(we_mscratch), .Q(mscratch), .clk(CLK), .clr(RST));
  Register #(.width(24)) mtvec_31_8 (.D(cat6[31:8]), .en(we_mtvec), .Q(MTVEC_BASE[31:8]), .clk(CLK), .clr(RST));
  Register #(.width(32)) mepc (.D(mepc_sig), .en(or7), .Q(PC_RETORNO), .clk(CLK), .clr(RST));
  Register #(.width(32)) u_mpcer (.D({cat6, valor_nuevo[0]}), .en(we_mpcer), .Q(mpcer), .clk(CLK), .clr(RST));
  Register #(.width(32)) u_mpcmr (.D(xor12), .en(we_mpcmr), .Q(qx13), .clk(CLK), .clr(RST));
  Counter #(.width(32), .max('hffffffff), .ongoal("wrap")) u_mcycleh (
    .load(we_mcycleh), .D({cat6, valor_nuevo[0]}), .count(and15), .Q(mcycleh), .carry(mcycleh_max),
    .up(1'b1), .clk(CLK), .clr(RST));
  Counter #(.width(32), .max('hffffffff), .ongoal("wrap")) minstret (
    .load(we_minstret), .D({cat6, valor_nuevo[0]}), .count(cuenta_instr), .Q(INSTRET), .carry(minstret_max),
    .up(1'b1), .clk(CLK), .clr(RST));
  Counter #(.width(32), .max('hffffffff), .ongoal("wrap")) u_minstreth (
    .load(we_minstreth), .D({cat6, valor_nuevo[0]}), .count(and16), .Q(minstreth), .carry(minstreth_max),
    .up(1'b1), .clk(CLK), .clr(RST));
  Counter #(.width(32), .max('hffffffff), .ongoal("wrap")) u_mpccr (
    .load(we_mpccr), .D({cat6, valor_nuevo[0]}), .count(cuenta_mpccr), .Q(mpccr), .carry(mpccr_max),
    .up(1'b1), .clk(CLK), .clr(RST));
  Counter #(.width(32), .max('hffffffff), .ongoal("wrap")) mcycle (
    .load(we_mcycle), .D({cat6, valor_nuevo[0]}), .count(cuenta_ciclos), .Q(CICLOS), .carry(mcycle_max),
    .up(1'b1), .clk(CLK), .clr(RST));
  and and_1 (we_mstatus, WE, sel_mstatus);
  and and_2 (we_misa, WE, sel_misa);
  and and_3 (we_mie, WE, sel_mie);
  and and_4 (we_mtvec, WE, sel_mtvec);
  and and_5 (we_mscratch, WE, sel_mscratch);
  and and_6 (we_mepc, WE, sel_mepc);
  and and_7 (we_mcause, WE, sel_mcause);
  and and_8 (we_mtval, WE, sel_mtval);
  and and_9 (we_mip, WE, sel_mip);
  and and_10 (we_mvendorid, WE, sel_mvendorid);
  and and_11 (we_marchid, WE, sel_marchid);
  and and_12 (we_mimpid, WE, sel_mimpid);
  and and_13 (we_mhartid, WE, sel_mhartid);
  and and_14 (we_mpcer, WE, sel_mpcer);
  and and_15 (we_mpcmr, WE, sel_mpcmr);
  and and_16 (we_mpccr, WE, sel_mpccr);
  and and_17 (we_mcycle, WE, sel_mcycle);
  and and_18 (we_mcycleh, WE, sel_mcycleh);
  and and_19 (we_minstret, WE, sel_minstret);
  and and_20 (we_minstreth, WE, sel_minstreth);
  and and_21 (we_cycle, WE, sel_cycle);
  and and_22 (we_cycleh, WE, sel_cycleh);
  and and_23 (we_instret, WE, sel_instret);
  and and_24 (we_instreth, WE, sel_instreth);
  assign mpcmr = qx13 ^ 32'h1;  // XOR_Gate xor_1, 32 bits wide
  assign rep19 = {{31{sel_mstatus}}, sel_mstatus};  // Bit_Extender bit_extender_1
  Multiplexer #(.select(1), .width(32), .enable("false")) multiplexer_1 (
    .in0({32{1'b0}}), .in1(32'h40001104), .out(rd_misa), .sel(sel_misa));
  assign rep20 = {{31{sel_mie}}, sel_mie};  // Bit_Extender bit_extender_2
  assign rep21 = {{31{sel_mtvec}}, sel_mtvec};  // Bit_Extender bit_extender_3
  assign rep22 = {{31{sel_mscratch}}, sel_mscratch};  // Bit_Extender bit_extender_4
  assign rep23 = {{31{sel_mepc}}, sel_mepc};  // Bit_Extender bit_extender_5
  assign rep24 = {{31{sel_mcause}}, sel_mcause};  // Bit_Extender bit_extender_6
  assign rep25 = {{31{sel_mtval}}, sel_mtval};  // Bit_Extender bit_extender_7
  assign rep26 = {{31{sel_mip}}, sel_mip};  // Bit_Extender bit_extender_8
  Multiplexer #(.select(1), .width(32), .enable("false")) multiplexer_2 (
    .in0({32{1'b0}}), .in1(32'h612), .out(rd_mvendorid), .sel(sel_mvendorid));
  Multiplexer #(.select(1), .width(32), .enable("false")) multiplexer_3 (
    .in0({32{1'b0}}), .in1(32'h1), .out(rd_mimpid), .sel(sel_mimpid));
  Multiplexer #(.select(1), .width(32), .enable("false")) multiplexer_4 (
    .in0({32{1'b0}}), .in1(32'h80000001), .out(rd_marchid), .sel(sel_marchid));
  assign rep27 = {{31{sel_mpcer}}, sel_mpcer};  // Bit_Extender bit_extender_9
  assign rep28 = {{31{sel_mpcmr}}, sel_mpcmr};  // Bit_Extender bit_extender_10
  assign rep29 = {{31{sel_mpccr}}, sel_mpccr};  // Bit_Extender bit_extender_11
  assign rep30 = {{31{sel_mcycle}}, sel_mcycle};  // Bit_Extender bit_extender_12
  assign rep31 = {{31{sel_mcycleh}}, sel_mcycleh};  // Bit_Extender bit_extender_13
  assign rep32 = {{31{sel_minstret}}, sel_minstret};  // Bit_Extender bit_extender_14
  assign rep33 = {{31{sel_minstreth}}, sel_minstreth};  // Bit_Extender bit_extender_15
  assign rep34 = {{31{sel_cycle}}, sel_cycle};  // Bit_Extender bit_extender_16
  assign rep35 = {{31{sel_cycleh}}, sel_cycleh};  // Bit_Extender bit_extender_17
  assign rep36 = {{31{sel_instret}}, sel_instret};  // Bit_Extender bit_extender_18
  assign rep37 = {{31{sel_instreth}}, sel_instreth};  // Bit_Extender bit_extender_19
  or or_1 (en_mstatus, TRAP, MRET, we_mstatus);
  or or_2 (or7, TRAP, we_mepc);
  or or_3 (or9, TRAP, we_mcause);
  or or_4 (or11, TRAP, we_mtval);
  nor nor_1 (cuenta_ciclos, we_mcycle, we_mcycleh);
  nor nor_2 (nor14, we_minstret, we_minstreth);
  and and_25 (and17, mpcer[1], RETIRE);
  assign rd_mstatus = {24'h18, mstatus[7], 3'b000, MIE_GLOBAL, 3'b000} & rep19;  // AND_Gate and_26, 32 bits wide
  assign rd_mie = mie & rep20;  // AND_Gate and_27, 32 bits wide
  assign rd_mtvec = {MTVEC_BASE[31:8], 8'h1} & rep21;  // AND_Gate and_28, 32 bits wide
  assign rd_mscratch = mscratch & rep22;  // AND_Gate and_29, 32 bits wide
  assign rd_mepc = PC_RETORNO & rep23;  // AND_Gate and_30, 32 bits wide
  assign rd_mcause = mcause & rep24;  // AND_Gate and_31, 32 bits wide
  assign rd_mtval = mtval & rep25;  // AND_Gate and_32, 32 bits wide
  assign rd_mip = IRQS & rep26;  // AND_Gate and_33, 32 bits wide
  assign rd_mpcer = mpcer & rep27;  // AND_Gate and_34, 32 bits wide
  assign rd_mpcmr = mpcmr & rep28;  // AND_Gate and_35, 32 bits wide
  assign rd_mpccr = mpccr & rep29;  // AND_Gate and_36, 32 bits wide
  assign rd_mcycle = CICLOS & rep30;  // AND_Gate and_37, 32 bits wide
  assign rd_mcycleh = mcycleh & rep31;  // AND_Gate and_38, 32 bits wide
  assign rd_minstret = INSTRET & rep32;  // AND_Gate and_39, 32 bits wide
  assign rd_minstreth = minstreth & rep33;  // AND_Gate and_40, 32 bits wide
  assign rd_cycle = CICLOS & rep34;  // AND_Gate and_41, 32 bits wide
  assign rd_cycleh = mcycleh & rep35;  // AND_Gate and_42, 32 bits wide
  assign rd_instret = INSTRET & rep36;  // AND_Gate and_43, 32 bits wide
  assign rd_instreth = minstreth & rep37;  // AND_Gate and_44, 32 bits wide
  and and_45 (cuenta_instr, RETIRE, nor14);
  and and_46 (and15, cuenta_ciclos, mcycle_max);
  or or_5 (or18, mpcer[0], and17);
  assign RDATA = rd_mstatus | rd_misa | rd_mie | rd_mtvec | rd_mscratch | rd_mepc | rd_mcause | rd_mtval | rd_mip | rd_mvendorid | rd_marchid | rd_mimpid | rd_mpcer | rd_mpcmr | rd_mpccr | rd_mcycle | rd_mcycleh | rd_minstret | rd_minstreth | rd_cycle | rd_cycleh | rd_instret | rd_instreth;  // OR_Gate or_6, 32 bits wide
  assign or2 = RDATA | SRC;  // OR_Gate or_7, 32 bits wide
  assign and3 = RDATA & not1;  // AND_Gate and_47, 32 bits wide
  and and_48 (and16, cuenta_instr, minstret_max);
  and and_49 (cuenta_mpccr, mpcmr[0], or18);
  Multiplexer #(.select(2), .width(32), .enable("false")) multiplexer_5 (
    .in0(SRC), .in1(SRC), .in2(or2), .in3(and3), .out({cat6, valor_nuevo[0]}), .sel(OP));
  Multiplexer #(.select(1), .width(32), .enable("false")) multiplexer_6 (
    .in0({cat6, valor_nuevo[0]}), .in1(CAUSE), .out(mux8), .sel(TRAP));
  Multiplexer #(.select(1), .width(32), .enable("false")) multiplexer_7 (
    .in0({cat6, valor_nuevo[0]}), .in1(TVAL), .out(mux10), .sel(TRAP));
  assign xor12 = {cat6, valor_nuevo[0]} ^ 32'h1;  // XOR_Gate xor_2, 32 bits wide
  Multiplexer #(.select(1), .width(1), .enable("false")) multiplexer_8 (
    .in0(cat6[3]), .in1(mstatus[7]), .out(mux4), .sel(MRET));
  Multiplexer #(.select(1), .width(1), .enable("false")) multiplexer_9 (
    .in0(cat6[7]), .in1(1'b1), .out(mux5), .sel(MRET));
  Multiplexer #(.select(1), .width(1), .enable("false")) multiplexer_10 (
    .in0(mux4), .in1(1'b0), .out(MIE_sig), .sel(TRAP));
  Multiplexer #(.select(1), .width(1), .enable("false")) multiplexer_11 (
    .in0(mux5), .in1(MIE_GLOBAL), .out(MPIE_sig), .sel(TRAP));
  Multiplexer #(.select(1), .width(32), .enable("false")) multiplexer_12 (
    .in0({cat6, 1'b0}), .in1(EPC), .out(mepc_sig), .sel(TRAP));

  assign MTVEC_BASE[7:0] = {8{1'b0}};

  // Other names for the same wires on the sheet: valor_nuevo[31:1] = cat6; valor_nuevo_31_1[30:0] = cat6;
  //   valor_nuevo_3 = cat6[3]; valor_nuevo_7 = cat6[7]; valor_nuevo_31_8[23:0] = cat6[31:8]; mcycle[31:0] = CICLOS;
  //   minstret[31:0] = INSTRET; mstatus[3] = MIE_GLOBAL; mstatus_MIE = MIE_GLOBAL; mpcer_0 = mpcer[0];
  //   mpcer_1 = mpcer[1]; mpcmr_0 = mpcmr[0]; mstatus_MPIE = mstatus[7]; mtvec[31:8] = MTVEC_BASE[31:8];
  //   mtvec_base32[31:8] = MTVEC_BASE[31:8]; MTVEC_BASE_2[31:8] = MTVEC_BASE[31:8];
  //   mtvec_base_t[23:0] = MTVEC_BASE[31:8]; mepc[31:0] = PC_RETORNO; valor_actual[31:0] = RDATA
endmodule
module CPU_RV32IMC (
  input  CLK,
  input  RST,
  input  [31:0] RDATA,
  input  BUS_ERR,
  input  IRQ,
  input  [4:0] IRQ_ID,
  input  [31:0] IRQ_LINES,
  input  DBG,
  output [31:0] ADDR,
  output [31:0] WDATA,
  output [3:0] WSTRB,
  output WE,
  output RE,
  output WR,
  output FETCH,
  output HALTED,
  output [31:0] PC_DBG,
  output RETIRA,
  output DBG_EJECUTA,
  output [31:0] DBG_IR,
  output [31:0] DBG_A,
  output [31:0] DBG_B,
  output [31:0] DBG_Y,
  output [3:0] DBG_OP,
  output [4:0] DBG_RD,
  output [31:0] DBG_WB,
  output [31:0] DBG_INSTRET,
  output [31:0] DBG_CICLOS
);

  wire and15, and16, and45, and46, and53, and55, carga_ir_alto, condicion, csr_escribe, csr_ilegal,
       csr_solo_lectura, csr_we, d_ALU_B_IMM, d_AUIPC, d_BRANCH, d_CSR, d_EBREAK, d_ECALL, d_ESCRIBE_RD,
       d_ILEGAL, d_JAL, d_JALR, d_LOAD, d_LUI, d_MRET, d_STORE, d_WFI, detener, ebreak, eq2, eq11, eq12,
       es_comprimida, es_FETCH, es_memoria, est_1, exc_carga_desal, exc_carga_falla, exc_ebreak, exc_ecall,
       exc_guarda_desal, exc_guarda_falla, exc_ilegal, excepcion_exec, exec_legal, falla_fetch, fetch_ok,
       gt1, ilegal_c, llega_comprimida, ls_desalineado, lt3, menor_u, MIE, mret_ejecuta, necesita_fetch2,
       nor23, not4, not5, not6, not13, not14, not18, not19, not20, not21, not22, not41, not44, not52, not54,
       not56, not57, or17, or32, pc_actualiza, rf_we, rvc_ilegal, salto_tomado, trap, usa_destino, wfi_espera;
  wire [1:0] d_ALU_A, d_SEL_IMM, estado, estado_sig, mux47, mux48, mux49, mux50, mux51;
  wire [2:0] d_SEL_WB;
  wire [3:0] d_ALUOP, mux62;
  wire [4:0] and35, codigo_causa, mux24, mux25, mux26, mux27, mux28, mux29, mux30, mux31, rep34;
  wire [11:0] csr_direccion, rep10;
  wire [15:0] ir_alto_sig, ir_bajo_sig, mitad_inferior, mux43, parcela_fetch, rep42;
  wire [31:0] alu_a, alu_b, alu_y, csr_operando, csr_valor, dato_wb, desplazamiento, desplazamiento_mem,
       dir_datos, dir_exec, imm_alu, immB, immI, immJ, immS, immU, instr_expandida, largo_instr, ls_dato,
       mepc, mtval_nuevo, mtvec_base, muldiv_y, mux8, mux33, mux36, mux37, mux38, mux59, mux60, mux61,
       pc_destino, pc_nuevo, pc_siguiente, qx40, rep9, rs1_val, rs2_val, xor39, zx7;
  wire [31:2] dir_fetch2;
  wire [31:31] mcause_nuevo;

  not not_1 (not19, DBG);
  not not_2 (not22, IRQ);
  Register #(.width(32)) PC (.D(xor39), .en(pc_actualiza), .Q(qx40), .clk(CLK), .clr(RST));
  Register #(.width(16)) IR_15_0 (.D(ir_bajo_sig), .en(fetch_ok), .Q(DBG_IR[15:0]), .clk(CLK), .clr(RST));
  not not_3 (not44, BUS_ERR);
  Register #(.width(16)) IR_31_16 (.D(ir_alto_sig), .en(carga_ir_alto), .Q(DBG_IR[31:16]), .clk(CLK), .clr(RST));
  Register #(.width(1)) ES_C (.D(llega_comprimida), .en(fetch_ok), .Q(es_comprimida), .clk(CLK), .clr(RST));
  Register #(.width(1)) u_ILEGAL_C (.D(and46), .en(fetch_ok), .Q(ilegal_c), .clk(CLK), .clr(RST));
  Register #(.width(2)) u_ESTADO (.D(estado_sig), .en(1'b1), .Q(estado), .clk(CLK), .clr(RST));
  not not_4 (not57, BUS_ERR);
  Register #(.width(32)) ULTIMA_A (.D(mux59), .en(RETIRA), .Q(DBG_A), .clk(CLK), .clr(RST));
  Register #(.width(32)) ULTIMA_B (.D(mux60), .en(RETIRA), .Q(DBG_B), .clk(CLK), .clr(RST));
  Register #(.width(32)) ULTIMO_RESULTADO (.D(mux61), .en(RETIRA), .Q(DBG_Y), .clk(CLK), .clr(RST));
  Register #(.width(4)) ULTIMA_OP (.D(mux62), .en(RETIRA), .Q(DBG_OP), .clk(CLK), .clr(RST));
  Register #(.width(5)) ULTIMO_RD (.D(DBG_IR[11:7]), .en(rf_we), .Q(DBG_RD), .clk(CLK), .clr(RST));
  Register #(.width(32)) ULTIMO_VALOR (.D(dato_wb), .en(rf_we), .Q(DBG_WB), .clk(CLK), .clr(RST));
  Decoder #(.select(2), .enable("false")) decoder_1 (
    .out0(es_FETCH), .out1(est_1), .out2(DBG_EJECUTA), .out3(HALTED), .sel(estado));
  Multiplexer #(.select(1), .width(32), .enable("false")) multiplexer_1 (
    .in0(32'h4), .in1(32'h2), .out(largo_instr), .sel(es_comprimida));
  assign PC_DBG = qx40 ^ 32'h40000000;  // XOR_Gate xor_1, 32 bits wide
  GeneradorInmediatos IMM (.INSTR(DBG_IR), .I(immI), .S(immS), .B(immB), .U(immU), .J(immJ));
  Decodificador DEC (
    .INSTR(DBG_IR), .ES_C(es_comprimida), .ILEGAL_C(ilegal_c), .LUI(d_LUI), .AUIPC(d_AUIPC), .JAL(d_JAL),
    .JALR(d_JALR), .BRANCH(d_BRANCH), .LOAD(d_LOAD), .STORE(d_STORE), .CSR(d_CSR), .ECALL(d_ECALL),
    .EBREAK(d_EBREAK), .MRET(d_MRET), .WFI(d_WFI), .ILEGAL(d_ILEGAL), .ALUOP(d_ALUOP), .ALU_A(d_ALU_A),
    .ALU_B_IMM(d_ALU_B_IMM), .SEL_IMM(d_SEL_IMM), .ESCRIBE_RD(d_ESCRIBE_RD), .SEL_WB(d_SEL_WB));
  Adder #(.width(32)) adder_1 (.a(PC_DBG), .b(largo_instr), .out(pc_siguiente));  // open: cin, cout
  and and_1 (mcause_nuevo[31], es_FETCH, IRQ, MIE);
  and and_2 (and16, est_1, BUS_ERR);
  assign rep42 = {{15{es_FETCH}}, es_FETCH};  // Bit_Extender bit_extender_1
  and and_3 (and45, est_1, not44);
  or or_1 (FETCH, es_FETCH, est_1);
  Multiplexer #(.select(2), .width(32), .enable("false")) multiplexer_2 (
    .in0(rs1_val), .in1(PC_DBG), .in2({32{1'b0}}), .in3({32{1'b0}}), .out(alu_a), .sel(d_ALU_A));
  Multiplexer #(.select(2), .width(32), .enable("false")) multiplexer_3 (
    .in0(immI), .in1(immS), .in2(immU), .in3(immU), .out(imm_alu), .sel(d_SEL_IMM));
  UnidadMulDiv MULDIV (.A(rs1_val), .B(rs2_val), .F3(DBG_IR[14:12]), .Y(muldiv_y));
  or or_2 (es_memoria, d_LOAD, d_STORE);
  Multiplexer #(.select(1), .width(32), .enable("false")) multiplexer_4 (
    .in0(immI), .in1(immS), .out(desplazamiento_mem), .sel(d_STORE));
  Multiplexer #(.select(1), .width(32), .enable("false")) multiplexer_5 (
    .in0(immB), .in1(immJ), .out(desplazamiento), .sel(d_JAL));
  Adder #(.width(30)) adder_2 (.a(PC_DBG[31:2]), .b(30'h1), .out(dir_fetch2));  // open: cin, cout
  assign zx7 = {{27{1'b0}}, DBG_IR[19:15]};  // Bit_Extender bit_extender_2
  assign rep9 = {{31{d_CSR}}, d_CSR};  // Bit_Extender bit_extender_3
  assign rep10 = {{11{d_CSR}}, d_CSR};  // Bit_Extender bit_extender_4
  Comparator #(.width(5), .mode("unsigned")) comparator_1 (
    .a(DBG_IR[19:15]), .b({5{1'b0}}), .eq(eq12));  // open: gt, lt
  and and_4 (necesita_fetch2, PC_DBG[1], RDATA[16], RDATA[17]);
  not not_5 (not14, mcause_nuevo[31]);
  assign rep34 = {{4{mcause_nuevo[31]}}, mcause_nuevo[31]};  // Bit_Extender bit_extender_5
  Multiplexer #(.select(1), .width(16), .enable("false")) multiplexer_6 (
    .in0(RDATA[15:0]), .in1(RDATA[31:16]), .out(mitad_inferior), .sel(PC_DBG[1]));
  not not_6 (not52, mcause_nuevo[31]);
  not not_7 (not13, eq12);
  Multiplexer #(.select(1), .width(2), .enable("false")) multiplexer_7 (
    .in0(2'b10), .in1(2'b01), .out(mux47), .sel(necesita_fetch2));
  and and_5 (and53, es_FETCH, not52);
  Multiplexer #(.select(1), .width(32), .enable("false")) multiplexer_8 (
    .in0(rs2_val), .in1(imm_alu), .out(alu_b), .sel(d_ALU_B_IMM));
  Adder #(.width(32)) adder_3 (.a(PC_DBG), .b(desplazamiento), .out(pc_destino));  // open: cin, cout
  Multiplexer #(.select(1), .width(32), .enable("false")) multiplexer_9 (
    .in0(rs1_val), .in1(zx7), .out(mux8), .sel(DBG_IR[14]));
  assign csr_direccion = DBG_IR[31:20] & rep10;  // AND_Gate and_6, 12 bits wide
  Comparator #(.width(2), .mode("unsigned")) comparator_2 (.a(DBG_IR[13:12]), .b(2'b01), .eq(eq11));  // open: gt, lt
  and and_7 (csr_solo_lectura, DBG_IR[31], DBG_IR[30]);
  and and_8 (and15, es_FETCH, not14, BUS_ERR);
  assign and35 = IRQ_ID & rep34;  // AND_Gate and_9, 5 bits wide
  assign parcela_fetch = mitad_inferior & rep42;  // AND_Gate and_10, 16 bits wide
  Multiplexer #(.select(1), .width(4), .enable("false")) multiplexer_10 (
    .in0(d_ALUOP), .in1(4'b0000), .out(mux62), .sel(es_memoria));
  Adder #(.width(32)) adder_4 (.a(rs1_val), .b(desplazamiento_mem), .out(dir_datos));  // open: cin, cout
  ALU U_ALU (.A(alu_a), .B(alu_b), .OP(d_ALUOP), .Y(alu_y));
  assign csr_operando = mux8 & rep9;  // AND_Gate and_11, 32 bits wide
  or or_3 (csr_escribe, eq11, not13);
  or or_4 (falla_fetch, and15, and16);
  ExpansorRVC RVC (.C(parcela_fetch), .I32(instr_expandida), .ILEGAL(rvc_ilegal));
  Multiplexer #(.select(1), .width(32), .enable("false")) multiplexer_11 (
    .in0({PC_DBG[31:2], 2'b00}), .in1(dir_datos), .out(dir_exec), .sel(es_memoria));
  nand nand_1 (llega_comprimida, mitad_inferior[0], mitad_inferior[1]);
  Multiplexer #(.select(1), .width(32), .enable("false")) multiplexer_12 (
    .in0(alu_b), .in1(desplazamiento_mem), .out(mux60), .sel(es_memoria));
  UnidadCargaAlmacen LSU (
    .F3(DBG_IR[14:12]), .ADDR_LO(dir_datos[1:0]), .RS2(rs2_val), .RDATA(RDATA), .WDATA(WDATA), .WSTRB(WSTRB),
    .DESALINEADO(ls_desalineado), .LDATA(ls_dato));
  and and_12 (csr_ilegal, d_CSR, csr_escribe, csr_solo_lectura);
  and and_13 (and46, llega_comprimida, rvc_ilegal);
  Multiplexer #(.select(2), .width(32), .enable("false")) multiplexer_13 (
    .in0({PC_DBG[31:2], 2'b00}), .in1({dir_fetch2, 2'b00}), .in2(dir_exec), .in3({PC_DBG[31:2], 2'b00}),
    .out(ADDR), .sel(estado));
  Multiplexer #(.select(1), .width(32), .enable("false")) multiplexer_14 (
    .in0(alu_y), .in1(dir_datos), .out(mux61), .sel(es_memoria));
  or or_5 (or17, d_ILEGAL, csr_ilegal);
  not not_8 (not20, ls_desalineado);
  not not_9 (not21, ls_desalineado);
  Multiplexer #(.select(1), .width(16), .enable("false")) multiplexer_15 (
    .in0(mitad_inferior), .in1(instr_expandida[15:0]), .out(ir_bajo_sig), .sel(llega_comprimida));
  Multiplexer #(.select(1), .width(16), .enable("false")) multiplexer_16 (
    .in0(RDATA[31:16]), .in1(instr_expandida[31:16]), .out(mux43), .sel(llega_comprimida));
  not not_10 (not54, ls_desalineado);
  not not_11 (not56, ls_desalineado);
  and and_14 (exc_ilegal, DBG_EJECUTA, or17);
  Multiplexer #(.select(1), .width(16), .enable("false")) multiplexer_17 (
    .in0(mux43), .in1(RDATA[15:0]), .out(ir_alto_sig), .sel(est_1));
  not not_12 (not18, exc_ilegal);
  and and_15 (exec_legal, DBG_EJECUTA, not18);
  and and_16 (exc_ecall, exec_legal, d_ECALL);
  and and_17 (ebreak, exec_legal, d_EBREAK);
  and and_18 (exc_carga_falla, exec_legal, d_LOAD, not20, BUS_ERR);
  and and_19 (exc_guarda_falla, exec_legal, d_STORE, not21, BUS_ERR);
  and and_20 (wfi_espera, exec_legal, d_WFI, not22);
  and and_21 (and55, exec_legal, d_LOAD, not54);
  and and_22 (WR, exec_legal, d_STORE);
  and and_23 (exc_carga_desal, exec_legal, d_LOAD, ls_desalineado);
  and and_24 (exc_guarda_desal, exec_legal, d_STORE, ls_desalineado);
  Multiplexer #(.select(1), .width(5), .enable("false")) multiplexer_18 (
    .in0({5{1'b0}}), .in1(5'b00111), .out(mux24), .sel(exc_guarda_falla));
  Multiplexer #(.select(1), .width(2), .enable("false")) multiplexer_19 (
    .in0(2'b00), .in1(2'b10), .out(mux50), .sel(wfi_espera));
  or or_6 (RE, and53, est_1, and55);
  and and_25 (detener, ebreak, DBG);
  and and_26 (exc_ebreak, ebreak, not19);
  or or_7 (or32, exc_carga_desal, exc_guarda_desal, exc_carga_falla, exc_guarda_falla);
  and and_27 (WE, WR, not56, not57);
  Multiplexer #(.select(1), .width(5), .enable("false")) multiplexer_20 (
    .in0(mux24), .in1(5'b00110), .out(mux25), .sel(exc_guarda_desal));
  Multiplexer #(.select(1), .width(32), .enable("false")) multiplexer_21 (
    .in0({32{1'b0}}), .in1(dir_datos), .out(mux33), .sel(or32));
  Multiplexer #(.select(1), .width(2), .enable("false")) multiplexer_22 (
    .in0(mux50), .in1(2'b11), .out(mux51), .sel(detener));
  or or_8 (excepcion_exec, exc_ilegal, exc_ecall, exc_ebreak, exc_carga_desal, exc_guarda_desal, exc_carga_falla, exc_guarda_falla);
  Multiplexer #(.select(1), .width(5), .enable("false")) multiplexer_23 (
    .in0(mux25), .in1(5'b00101), .out(mux26), .sel(exc_carga_falla));
  Multiplexer #(.select(1), .width(32), .enable("false")) multiplexer_24 (
    .in0(mux33), .in1(PC_DBG), .out(mtval_nuevo), .sel(falla_fetch));
  or or_9 (trap, mcause_nuevo[31], falla_fetch, excepcion_exec);
  nor nor_1 (nor23, excepcion_exec, detener, wfi_espera);
  and and_28 (RETIRA, DBG_EJECUTA, nor23);
  Multiplexer #(.select(1), .width(5), .enable("false")) multiplexer_25 (
    .in0(mux26), .in1(5'b00100), .out(mux27), .sel(exc_carga_desal));
  not not_13 (not41, trap);
  Multiplexer #(.select(1), .width(2), .enable("false")) multiplexer_26 (
    .in0(mux47), .in1(2'b00), .out(mux48), .sel(trap));
  Multiplexer #(.select(1), .width(2), .enable("false")) multiplexer_27 (
    .in0(2'b10), .in1(2'b00), .out(mux49), .sel(trap));
  Multiplexer #(.select(1), .width(5), .enable("false")) multiplexer_28 (
    .in0(mux27), .in1(5'b01011), .out(mux28), .sel(exc_ecall));
  and and_29 (fetch_ok, es_FETCH, not41);
  Multiplexer #(.select(2), .width(2), .enable("false")) multiplexer_29 (
    .in0(mux48), .in1(mux49), .in2(mux51), .in3(2'b11), .out(estado_sig), .sel(estado));
  and and_30 (mret_ejecuta, RETIRA, d_MRET);
  and and_31 (csr_we, RETIRA, d_CSR, csr_escribe);
  or or_10 (pc_actualiza, trap, RETIRA);
  and and_32 (rf_we, RETIRA, d_ESCRIBE_RD);
  Multiplexer #(.select(1), .width(5), .enable("false")) multiplexer_30 (
    .in0(mux28), .in1(5'b00011), .out(mux29), .sel(exc_ebreak));
  or or_11 (carga_ir_alto, fetch_ok, and45);
  Multiplexer #(.select(1), .width(5), .enable("false")) multiplexer_31 (
    .in0(mux29), .in1(5'b00010), .out(mux30), .sel(exc_ilegal));
  Multiplexer #(.select(1), .width(5), .enable("false")) multiplexer_32 (
    .in0(mux30), .in1(5'b00001), .out(mux31), .sel(falla_fetch));
  Multiplexer #(.select(1), .width(5), .enable("false")) multiplexer_33 (
    .in0(mux31), .in1(IRQ_ID), .out(codigo_causa), .sel(mcause_nuevo[31]));
  RegistrosCSR CSR (
    .CLK(CLK), .RST(RST), .ADDR(csr_direccion), .SRC(csr_operando), .OP(DBG_IR[13:12]), .WE(csr_we),
    .TRAP(trap), .CAUSE({mcause_nuevo[31], {26{1'b0}}, codigo_causa}), .EPC(PC_DBG), .TVAL(mtval_nuevo),
    .MRET(mret_ejecuta), .RETIRE(RETIRA), .IRQS(IRQ_LINES), .RDATA(csr_valor), .MTVEC_BASE(mtvec_base),
    .PC_RETORNO(mepc), .MIE_GLOBAL(MIE), .INSTRET(DBG_INSTRET), .CICLOS(DBG_CICLOS));
  Multiplexer #(.select(3), .width(32), .enable("false")) multiplexer_34 (
    .in0(alu_y), .in1(pc_siguiente), .in2(ls_dato), .in3(csr_valor), .in4(muldiv_y), .in5({32{1'b0}}),
    .in6({32{1'b0}}), .in7({32{1'b0}}), .out(dato_wb), .sel(d_SEL_WB));
  BancoRegistros REGS (
    .CLK(CLK), .RST(RST), .WE(rf_we), .RD(DBG_IR[11:7]), .WD(dato_wb), .RS1(DBG_IR[19:15]),
    .RS2(DBG_IR[24:20]), .R1(rs1_val), .R2(rs2_val));
  Comparator #(.width(32), .mode("twosComplement")) comparator_3 (
    .a(rs1_val), .b(rs2_val), .gt(gt1), .eq(eq2), .lt(lt3));
  Comparator #(.width(32), .mode("unsigned")) comparator_4 (.a(rs1_val), .b(rs2_val), .lt(menor_u));  // open: gt, eq
  Multiplexer #(.select(1), .width(32), .enable("false")) multiplexer_35 (
    .in0(alu_a), .in1(rs1_val), .out(mux59), .sel(es_memoria));
  not not_14 (not4, eq2);
  not not_15 (not5, lt3);
  not not_16 (not6, menor_u);
  Multiplexer #(.select(3), .width(1), .enable("false")) multiplexer_36 (
    .in0(eq2), .in1(not4), .in2(1'b0), .in3(1'b0), .in4(lt3), .in5(not5), .in6(menor_u), .in7(not6),
    .out(condicion), .sel(DBG_IR[14:12]));
  and and_33 (salto_tomado, d_BRANCH, condicion);
  or or_12 (usa_destino, d_JAL, salto_tomado);
  Multiplexer #(.select(1), .width(32), .enable("false")) multiplexer_37 (
    .in0(pc_siguiente), .in1(pc_destino), .out(mux36), .sel(usa_destino));
  Multiplexer #(.select(1), .width(32), .enable("false")) multiplexer_38 (
    .in0(mux36), .in1({alu_y[31:1], 1'b0}), .out(mux37), .sel(d_JALR));
  Multiplexer #(.select(1), .width(32), .enable("false")) multiplexer_39 (
    .in0(mux37), .in1(mepc), .out(mux38), .sel(d_MRET));
  Multiplexer #(.select(1), .width(32), .enable("false")) multiplexer_40 (
    .in0(mux38), .in1({mtvec_base[31:8], 1'b0, and35, 2'b00}), .out(pc_nuevo), .sel(trap));
  assign xor39 = pc_nuevo ^ 32'h40000000;  // XOR_Gate xor_2, 32 bits wide

  // Other names for the same wires on the sheet: bus_dir[31:0] = ADDR; mon_A[31:0] = DBG_A; mon_B[31:0] = DBG_B;
  //   ciclos_reloj[31:0] = DBG_CICLOS; es_EXEC = DBG_EJECUTA; est_2 = DBG_EJECUTA;
  //   instr_ejecutadas[31:0] = DBG_INSTRET; INSTR[31:0] = DBG_IR; IR_bajo[15:0] = DBG_IR[15:0];
  //   rd[4:0] = DBG_IR[11:7]; funct3[2:0] = DBG_IR[14:12]; funct3_1_0[1:0] = DBG_IR[13:12]; funct3_2 = DBG_IR[14];
  //   rs1[4:0] = DBG_IR[19:15]; IR_alto[15:0] = DBG_IR[31:16]; INSTR_31_20[11:0] = DBG_IR[31:20];
  //   rs2[4:0] = DBG_IR[24:20]; INSTR_31_20_10 = DBG_IR[30]; INSTR_31_20_11 = DBG_IR[31]; mon_OP[3:0] = DBG_OP;
  //   mon_RD[4:0] = DBG_RD; mon_WB[31:0] = DBG_WB; mon_Y[31:0] = DBG_Y; alu_y_31_1[30:0] = alu_y[31:1];
  //   destino_jalr[31:1] = alu_y[31:1]; dir_datos_1_0[1:0] = dir_datos[1:0]; dir_fetch[31:2] = PC_DBG[31:2];
  //   PC[31:0] = PC_DBG; PC_31_2[29:0] = PC_DBG[31:2]; pc_palabra_sig[29:0] = dir_fetch2; est_0 = es_FETCH;
  //   or58 = FETCH; est_3 = HALTED; instr_expandida_15_0[15:0] = instr_expandida[15:0];
  //   instr_expandida_31_16[15:0] = instr_expandida[31:16]; mcause_nuevo[4:0] = codigo_causa;
  //   toma_interrupcion = mcause_nuevo[31]; mitad_inferior_0 = mitad_inferior[0];
  //   mitad_inferior_1 = mitad_inferior[1]; PC_1 = PC_DBG[1]; RDATA_15_0[15:0] = RDATA[15:0]; RDATA_16 = RDATA[16];
  //   RDATA_31_16[15:0] = RDATA[31:16]; RDATA_17 = RDATA[17]; bus_lee = RE; instr_completa = RETIRA;
  //   vector_trap (some bits) = {mtvec_base[31:8], and35}; mtvec_base_31_8[23:0] = mtvec_base[31:8];
  //   ls_wdata[31:0] = WDATA; bus_escribe = WE; bus_intencion_escribir = WR; ls_wstrb[3:0] = WSTRB
endmodule

module UART (
  input  CLK,
  input  RST,
  input  SEL,
  input  [9:0] A,
  input  [31:0] WD,
  input  WE,
  input  RE,
  input  RXD,
  output TXD,
  output IRQ,
  output [31:0] RD
);

  wire and45, and49, eq25, eq29, eq43, esc_000, esc_00C, esc_010, esc_014, esc_020, esc_024, esc_060,
       escribe, ev_rx_ovf, ev_rx_tout, ev_rxfifo_full, ev_tx_done, ev_txfifo_empty, lee, lee_000, lin_0,
       lin_1, lin_2, lin_3, lin_4, lin_5, lin_6, lin_7, lin_8, lin_9, lin_10, lin_11, lin_12, lin_13, lin_14,
       lin_15, lin_16, lin_17, lin_18, lin_19, lin_20, lin_21, lin_22, lin_23, lin_24, lin_25, lin_26,
       lin_27, lin_28, lin_29, lin_30, lin_31, lt32, mete_rx, mux18, not13, not14, not15, not17, not24,
       not28, not30, not33, or16, or19, or20, pag_0, pag_1, pag_2, pag_3, pag_4, pag_5, pag_6, pag_7, pag_8,
       pag_9, pag_10, pag_11, pag_12, pag_13, pag_14, pag_15, pag_16, pag_17, pag_18, pag_19, pag_20, pag_21,
       pag_22, pag_23, pag_24, pag_25, pag_26, pag_27, pag_28, pag_29, pag_30, pag_31, r000, r00C, r01C,
       r02C, r004, r06C, r008, r010, r014, r020, r024, r028, r030, r060, r064, r068, r070, r074,
       registros_uart_acceso, registros_uart_existe, rx_linea, rx_llena, rx_pendiente, rx_vacia, rx_valido,
       rxd_entrada, tout_alcanzado, tout_reinicia, tx_empieza, tx_fin, tx_linea, tx_ocupado, tx_vacia;
  wire [3:3] INT_eventos;
  wire [7:0] rx_byte, rx_cuenta, rx_dato, rx_retenido, tx_dato;
  wire [8:0] zx31, zx34;
  wire [9:0] dir_registro, rep44;
  wire [15:0] mux27, sum26, tout_ciclos, tout_limite, zx22, zx23;
  wire [23:16] status;
  wire [31:0] and1, and4, and7, and10, and37, and39, and42, and48, and52, and54, and56, and58, and60, and67,
       and69, and71, and73, and75, CLKDIV, CONF0, CONF1, dato_escrito, INT_clr, INT_ENA, INT_raw, INT_st,
       MEM_CONF, mux61, mux62, mux63, mux64, mux65, not36, not47, or38, qx3, qx6, qx9, qx12, qx41,
       registros_uart_a_guardar, registros_uart_bits_fijos, registros_uart_bits_rw, registros_uart_guardado,
       registros_uart_reset_rw, registros_uart_valor, registros_uart_valor_reset, rep35, rep46, rep51, rep53,
       rep55, rep57, rep59, rep66, rep68, rep70, rep72, rep74, xor2, xor5, xor8, xor11, xor40, xor50, zx21;

  Register #(.width(32)) u_CLKDIV (.D(xor2), .en(esc_014), .Q(qx3), .clk(CLK), .clr(RST));
  Register #(.width(32)) u_CONF0 (.D(xor5), .en(esc_020), .Q(qx6), .clk(CLK), .clr(RST));
  Register #(.width(32)) u_CONF1 (.D(xor8), .en(esc_024), .Q(qx9), .clk(CLK), .clr(RST));
  Register #(.width(32)) u_MEM_CONF (.D(xor11), .en(esc_060), .Q(qx12), .clk(CLK), .clr(RST));
  Register #(.width(8)) RX_HOLD (.D(rx_byte), .en(rx_valido), .Q(rx_retenido), .clk(CLK), .clr(RST));
  Register #(.width(1)) PEND (.D(mux18), .en(or19), .Q(rx_pendiente), .clk(CLK), .clr(RST));
  Register #(.width(16)) TOUT (.D(mux27), .en(not28), .Q(tout_ciclos), .clk(CLK), .clr(RST));
  Register #(.width(32)) u_INT_RAW (.D(xor40), .en(1'b1), .Q(qx41), .clk(CLK), .clr(RST));
  Register #(.width(32)) u_INT_ENA (.D(and42), .en(esc_00C), .Q(INT_ENA), .clk(CLK), .clr(RST));
  assign rep44 = {{9{SEL}}, SEL};  // Bit_Extender bit_extender_1
  and and_1 (and45, SEL, WE);
  and and_2 (escribe, WE, SEL);
  and and_3 (lee, RE, SEL);
  ROM #(.addrWidth(10), .dataWidth(1)) u_REGISTROS_UART_EXISTE (.addr(dir_registro), .data(registros_uart_existe));
  ROM #(.addrWidth(10), .dataWidth(32)) u_REGISTROS_UART_VALOR_RESET (
    .addr(dir_registro), .data(registros_uart_valor_reset));
  ROM #(.addrWidth(10), .dataWidth(32)) u_REGISTROS_UART_BITS_RW (.addr(dir_registro), .data(registros_uart_bits_rw));
  RAM #(.addrWidth(10), .dataWidth(32), .enables("byte"), .trigger("rising"), .asyncread("true"), .databus("bibus"), .clearpin("true")) REGISTROS_UART (
    .addr(dir_registro), .we(and49), .oe(1'b1), .clk(CLK), .din(registros_uart_a_guardar),
    .dout(registros_uart_guardado), .clr(RST));
  assign CLKDIV = qx3 ^ 32'h4;  // XOR_Gate xor_1, 32 bits wide
  assign CONF1 = qx9 ^ 32'hc060;  // XOR_Gate xor_2, 32 bits wide
  assign MEM_CONF = qx12 ^ 32'ha0012;  // XOR_Gate xor_3, 32 bits wide
  assign INT_raw = qx41 ^ 32'h2;  // XOR_Gate xor_4, 32 bits wide
  assign dir_registro = A & rep44;  // AND_Gate and_4, 10 bits wide
  assign rep46 = {{31{and45}}, and45};  // Bit_Extender bit_extender_2
  assign CONF0 = qx6 ^ 32'h1000001c;  // XOR_Gate xor_5, 32 bits wide
  Adder #(.width(16)) adder_1 (.a(tout_ciclos), .b(16'h1), .out(sum26));  // open: cin, cout
  and and_5 (registros_uart_acceso, SEL, registros_uart_existe);
  assign not47 = ~registros_uart_bits_rw;  // NOT_Gate not_1, 32 bits wide
  assign registros_uart_reset_rw = registros_uart_valor_reset & registros_uart_bits_rw;  // AND_Gate and_6, 32 bits wide
  assign INT_st = INT_raw & INT_ENA;  // AND_Gate and_7, 32 bits wide
  assign dato_escrito = WD & rep46;  // AND_Gate and_8, 32 bits wide
  assign registros_uart_bits_fijos = registros_uart_valor_reset & not47;  // AND_Gate and_9, 32 bits wide
  and and_10 (and49, escribe, registros_uart_acceso);
  assign xor50 = registros_uart_guardado ^ registros_uart_reset_rw;  // XOR_Gate xor_6, 32 bits wide
  assign rep51 = {{31{registros_uart_acceso}}, registros_uart_acceso};  // Bit_Extender bit_extender_3
  Decoder #(.select(5), .enable("false")) decoder_1 (
    .out0(pag_0), .out1(pag_1), .out2(pag_2), .out3(pag_3), .out4(pag_4), .out5(pag_5), .out6(pag_6),
    .out7(pag_7), .out8(pag_8), .out9(pag_9), .out10(pag_10), .out11(pag_11), .out12(pag_12), .out13(pag_13),
    .out14(pag_14), .out15(pag_15), .out16(pag_16), .out17(pag_17), .out18(pag_18), .out19(pag_19),
    .out20(pag_20), .out21(pag_21), .out22(pag_22), .out23(pag_23), .out24(pag_24), .out25(pag_25),
    .out26(pag_26), .out27(pag_27), .out28(pag_28), .out29(pag_29), .out30(pag_30), .out31(pag_31),
    .sel(dir_registro[9:5]));
  Decoder #(.select(5), .enable("false")) decoder_2 (
    .out0(lin_0), .out1(lin_1), .out2(lin_2), .out3(lin_3), .out4(lin_4), .out5(lin_5), .out6(lin_6),
    .out7(lin_7), .out8(lin_8), .out9(lin_9), .out10(lin_10), .out11(lin_11), .out12(lin_12), .out13(lin_13),
    .out14(lin_14), .out15(lin_15), .out16(lin_16), .out17(lin_17), .out18(lin_18), .out19(lin_19),
    .out20(lin_20), .out21(lin_21), .out22(lin_22), .out23(lin_23), .out24(lin_24), .out25(lin_25),
    .out26(lin_26), .out27(lin_27), .out28(lin_28), .out29(lin_29), .out30(lin_30), .out31(lin_31),
    .sel(dir_registro[4:0]));
  assign and1 = dato_escrito & 32'hf00fff;  // AND_Gate and_11, 32 bits wide
  assign and4 = dato_escrito & 32'h1fffffff;  // AND_Gate and_12, 32 bits wide
  assign and7 = dato_escrito & 32'h3fffff;  // AND_Gate and_13, 32 bits wide
  assign and10 = dato_escrito & 32'hffffffe;  // AND_Gate and_14, 32 bits wide
  or or_1 (or16, RST, CONF0[18]);
  xor xor_7 (rxd_entrada, RXD, CONF0[19]);
  or or_2 (or20, RST, CONF0[17]);
  assign zx22 = {{4{1'b0}}, CLKDIV[11:0]};  // Bit_Extender bit_extender_4
  assign zx23 = {{6{1'b0}}, MEM_CONF[25:16]};  // Bit_Extender bit_extender_5
  Comparator #(.width(9), .mode("unsigned")) comparator_1 (.a(CONF1[8:0]), .b({9{1'b0}}), .eq(eq29));  // open: gt, lt
  assign and42 = dato_escrito & 32'h411b;  // AND_Gate and_15, 32 bits wide
  Comparator #(.width(32), .mode("unsigned")) comparator_2 (.a(INT_st), .b({32{1'b0}}), .eq(eq43));  // open: gt, lt
  assign and48 = dato_escrito & registros_uart_bits_rw;  // AND_Gate and_16, 32 bits wide
  assign registros_uart_valor = xor50 | registros_uart_bits_fijos;  // OR_Gate or_3, 32 bits wide
  and and_17 (r014, SEL, pag_0, lin_5);
  assign xor2 = and1 ^ 32'h4;  // XOR_Gate xor_8, 32 bits wide
  and and_18 (r020, SEL, pag_0, lin_8);
  assign xor5 = and4 ^ 32'h1000001c;  // XOR_Gate xor_9, 32 bits wide
  and and_19 (r024, SEL, pag_0, lin_9);
  assign xor8 = and7 ^ 32'hc060;  // XOR_Gate xor_10, 32 bits wide
  and and_20 (r060, SEL, pag_0, lin_24);
  assign xor11 = and10 ^ 32'ha0012;  // XOR_Gate xor_11, 32 bits wide
  and and_21 (r000, SEL, pag_0, lin_0);
  Multiplier #(.width(16)) multiplier_1 (.a(zx22), .b(zx23), .out(tout_limite), .cin({16{1'b0}}));  // open: cout
  not not_2 (not30, eq29);
  and and_22 (r010, SEL, pag_0, lin_4);
  and and_23 (r00C, SEL, pag_0, lin_3);
  not not_3 (IRQ, eq43);
  and and_24 (r028, SEL, pag_0, lin_10);
  and and_25 (r02C, SEL, pag_0, lin_11);
  and and_26 (r030, SEL, pag_0, lin_12);
  and and_27 (r064, SEL, pag_0, lin_25);
  and and_28 (r068, SEL, pag_0, lin_26);
  and and_29 (r06C, SEL, pag_0, lin_27);
  and and_30 (r070, SEL, pag_0, lin_28);
  and and_31 (r074, SEL, pag_0, lin_29);
  and and_32 (r01C, SEL, pag_0, lin_7);
  and and_33 (r004, SEL, pag_0, lin_1);
  and and_34 (r008, SEL, pag_0, lin_2);
  assign registros_uart_a_guardar = and48 ^ registros_uart_reset_rw;  // XOR_Gate xor_12, 32 bits wide
  assign and52 = registros_uart_valor & rep51;  // AND_Gate and_35, 32 bits wide
  and and_36 (esc_014, escribe, r014);
  and and_37 (esc_020, escribe, r020);
  and and_38 (esc_024, escribe, r024);
  and and_39 (esc_060, escribe, r060);
  and and_40 (esc_000, escribe, r000);
  and and_41 (lee_000, lee, r000);
  Comparator #(.width(16), .mode("unsigned")) comparator_3 (
    .a(tout_ciclos), .b(tout_limite), .eq(eq25));  // open: gt, lt
  and and_42 (esc_010, escribe, r010);
  and and_43 (esc_00C, escribe, r00C);
  assign rep53 = {{31{r014}}, r014};  // Bit_Extender bit_extender_6
  assign rep55 = {{31{r020}}, r020};  // Bit_Extender bit_extender_7
  assign rep57 = {{31{r024}}, r024};  // Bit_Extender bit_extender_8
  assign rep59 = {{31{r060}}, r060};  // Bit_Extender bit_extender_9
  Multiplexer #(.select(1), .width(32), .enable("false")) multiplexer_1 (
    .in0({32{1'b0}}), .in1(32'hfff), .out(mux61), .sel(r028));
  Multiplexer #(.select(1), .width(32), .enable("false")) multiplexer_2 (
    .in0({32{1'b0}}), .in1(32'hfff), .out(mux62), .sel(r02C));
  Multiplexer #(.select(1), .width(32), .enable("false")) multiplexer_3 (
    .in0({32{1'b0}}), .in1(32'h80100), .out(mux63), .sel(r068));
  Multiplexer #(.select(1), .width(32), .enable("false")) multiplexer_4 (
    .in0({32{1'b0}}), .in1(32'hfff), .out(mux64), .sel(r070));
  Multiplexer #(.select(1), .width(32), .enable("false")) multiplexer_5 (
    .in0({32{1'b0}}), .in1(32'hfff), .out(mux65), .sel(r074));
  assign rep66 = {{31{r000}}, r000};  // Bit_Extender bit_extender_10
  assign rep68 = {{31{r01C}}, r01C};  // Bit_Extender bit_extender_11
  assign rep70 = {{31{r00C}}, r00C};  // Bit_Extender bit_extender_12
  assign rep72 = {{31{r004}}, r004};  // Bit_Extender bit_extender_13
  assign rep74 = {{31{r008}}, r008};  // Bit_Extender bit_extender_14
  assign rep35 = {{31{esc_010}}, esc_010};  // Bit_Extender bit_extender_15
  assign and54 = CLKDIV & rep53;  // AND_Gate and_44, 32 bits wide
  assign and56 = CONF0 & rep55;  // AND_Gate and_45, 32 bits wide
  assign and58 = CONF1 & rep57;  // AND_Gate and_46, 32 bits wide
  assign and60 = MEM_CONF & rep59;  // AND_Gate and_47, 32 bits wide
  assign and71 = INT_ENA & rep70;  // AND_Gate and_48, 32 bits wide
  assign and73 = INT_raw & rep72;  // AND_Gate and_49, 32 bits wide
  assign and75 = INT_st & rep74;  // AND_Gate and_50, 32 bits wide
  not not_4 (not15, esc_000);
  FIFO128x8 FIFO_TX (
    .CLK(CLK), .RST(or16), .PUSH(esc_000), .DIN(dato_escrito[7:0]), .POP(tx_empieza), .DOUT(tx_dato),
    .COUNT(status), .EMPTY(tx_vacia));  // open: FULL
  not not_5 (not17, lee_000);
  assign INT_clr = dato_escrito & rep35;  // AND_Gate and_51, 32 bits wide
  not not_6 (not14, tx_vacia);
  and and_52 (mete_rx, rx_pendiente, not17);
  assign zx34 = {{1{1'b0}}, status};  // Bit_Extender bit_extender_16
  assign not36 = ~INT_clr;  // NOT_Gate not_7, 32 bits wide
  and and_53 (tx_empieza, not13, not14, not15);
  FIFO128x8 FIFO_RX (
    .CLK(CLK), .RST(or20), .PUSH(mete_rx), .DIN(rx_retenido), .POP(lee_000), .DOUT(rx_dato),
    .COUNT(rx_cuenta), .FULL(rx_llena), .EMPTY(rx_vacia));
  assign and37 = INT_raw & not36;  // AND_Gate and_54, 32 bits wide
  Comparator #(.width(9), .mode("unsigned")) comparator_4 (
    .a(CONF1[17:9]), .b(zx34), .gt(ev_txfifo_empty));  // open: eq, lt
  TransmisorSerie TX (
    .CLK(CLK), .RST(RST), .DIV(CLKDIV[11:0]), .START(tx_empieza), .DATA(tx_dato), .TXD(tx_linea),
    .BUSY(tx_ocupado), .FIN(tx_fin));
  assign zx21 = {{24{1'b0}}, rx_dato};  // Bit_Extender bit_extender_17
  and and_55 (ev_rx_ovf, mete_rx, rx_llena);
  assign zx31 = {{1{1'b0}}, rx_cuenta};  // Bit_Extender bit_extender_18
  not not_8 (not13, tx_ocupado);
  xor xor_13 (TXD, tx_linea, CONF0[22]);
  Multiplexer #(.select(1), .width(1), .enable("false")) multiplexer_6 (
    .in0(rxd_entrada), .in1(tx_linea), .out(rx_linea), .sel(CONF0[14]));
  Comparator #(.width(9), .mode("unsigned")) comparator_5 (.a(zx31), .b(CONF1[8:0]), .lt(lt32));  // open: gt, eq
  and and_56 (ev_tx_done, tx_fin, tx_vacia);
  assign and67 = zx21 & rep66;  // AND_Gate and_57, 32 bits wide
  ReceptorSerie RX (
    .CLK(CLK), .RST(RST), .DIV(CLKDIV[11:0]), .RXD(rx_linea), .DATA(rx_byte), .VALID(rx_valido),
    .FERR(INT_eventos[3]));
  not not_9 (not33, lt32);
  Multiplexer #(.select(1), .width(1), .enable("false")) multiplexer_7 (
    .in0(1'b0), .in1(1'b1), .out(mux18), .sel(rx_valido));
  or or_4 (or19, rx_valido, mete_rx);
  and and_58 (ev_rxfifo_full, not30, not33);
  assign and69 = {TXD, 7'b1100000, status, rx_linea, 7'b1000000, rx_cuenta} & rep68;  // AND_Gate and_59, 32 bits wide
  or or_5 (tout_reinicia, rx_valido, rx_vacia, lee_000);
  not not_10 (not24, tout_reinicia);
  Multiplexer #(.select(1), .width(16), .enable("false")) multiplexer_8 (
    .in0(sum26), .in1({16{1'b0}}), .out(mux27), .sel(tout_reinicia));
  assign RD = and54 | and56 | and58 | and60 | mux61 | mux62 | mux63 | mux64 | mux65 | and67 | and69 | and71 | and73 | and75 | and52;  // OR_Gate or_6, 32 bits wide
  and and_60 (tout_alcanzado, not24, eq25);
  not not_11 (not28, tout_alcanzado);
  and and_61 (ev_rx_tout, CONF1[21], tout_alcanzado);
  assign or38 = and37 | {{17{1'b0}}, ev_tx_done, {5{1'b0}}, ev_rx_tout, 3'b000, ev_rx_ovf, INT_eventos[3], 1'b0, ev_txfifo_empty, ev_rxfifo_full};  // OR_Gate or_7, 32 bits wide
  assign and39 = or38 & 32'h411b;  // AND_Gate and_62, 32 bits wide
  assign xor40 = and39 ^ 32'h2;  // XOR_Gate xor_14, 32 bits wide

  // Other names for the same wires on the sheet: CLKDIV_11_0[11:0] = CLKDIV[11:0]; CONF0_14 = CONF0[14];
  //   CONF0_17 = CONF0[17]; CONF0_18 = CONF0[18]; CONF0_19 = CONF0[19]; CONF0_22 = CONF0[22];
  //   CONF1_8_0[8:0] = CONF1[8:0]; CONF1_17_9[8:0] = CONF1[17:9]; CONF1_21 = CONF1[21];
  //   dato_escrito_7_0[7:0] = dato_escrito[7:0]; dir_registro_4_0[4:0] = dir_registro[4:0];
  //   dir_registro_9_5[4:0] = dir_registro[9:5];
  //   INT_eventos (some bits) = {ev_tx_done, ev_rx_tout, ev_rx_ovf, ev_txfifo_empty, ev_rxfifo_full};
  //   rx_error_trama = INT_eventos[3]; INT_irq = IRQ; lee_fifo_rx = lee_000; MEM_CONF_25_16[9:0] = MEM_CONF[25:16];
  //   mete_tx = esc_000; or76[31:0] = RD; status (some bits) = {TXD, rx_linea, rx_cuenta}; tx_cuenta[7:0] = status;
  //   txd_salida = TXD

  // Notes on the sheet:
  //   contents of REGISTROS_UART_EXISTE (hex, n*v repeats v):
  //   6*0 1 6*0 11*1 6*0 1 1 1
  //   contents of REGISTROS_UART_VALOR_RESET (hex, n*v repeats v):
  //   6*0 8 7*0 f0 26e0 2200 a 40100 0 901 901 b 32b 6*0 3701000 2008270 40000500
  //   contents of REGISTROS_UART_BITS_RW (hex, n*v repeats v):
  //   6*0 1ff 6*0 3f 3ff 1ffff 1ffff ff fffff 3ff 4*ffff 6*0 fffffff ffffffff ffffffff
endmodule

module PadGPIO (
  input  PAD_IN,
  input  OPEN_DRAIN,
  input  [10:0] OUT_CFG,
  input  [4:0] IOMUX_CFG,
  input  GPIO_OUT,
  input  GPIO_EN,
  input  [15:0] SIGS,
  input  F0_ES_GPIO,
  input  F0_OUT,
  input  F0_OE,
  input  F2_OUT,
  input  F2_OE,
  output ENTRADA,
  output PAD_OUT
);

  wire and5, con_pulldown, con_pullup, habilita_salida, mux1, mux2, mux3, mux4, nivel_pin, not6, oe_final,
       oe_matriz, sel_es_gpio, senal_periferico, valor_matriz, valor_matriz_inv, valor_salida;
  wire [4:0] tabla_senal;

  Pull_Resistor #(.pull(1)) pull_resistor_1 (.node(con_pullup));
  Pull_Resistor #(.pull(0)) pull_resistor_2 (.node(con_pulldown));
  assign con_pullup = 1'b1 ? PAD_IN : 1'bz;  // Controlled_Buffer controlled_buffer_1
  assign con_pulldown = 1'b1 ? PAD_IN : 1'bz;  // Controlled_Buffer controlled_buffer_2
  ROM #(.addrWidth(8), .dataWidth(5)) TABLA_SENALES (.addr(OUT_CFG[7:0]), .data(tabla_senal));
  Multiplexer #(.select(1), .width(1), .enable("false")) multiplexer_1 (
    .in0(con_pulldown), .in1(con_pullup), .out(nivel_pin), .sel(IOMUX_CFG[0]));
  Comparator #(.width(8), .mode("unsigned")) comparator_1 (
    .a(OUT_CFG[7:0]), .b(8'h80), .eq(sel_es_gpio));  // open: gt, lt
  and and_1 (ENTRADA, nivel_pin, IOMUX_CFG[1]);
  Multiplexer #(.select(4), .width(1), .enable("false")) multiplexer_2 (
    .in0(SIGS[0]), .in1(SIGS[1]), .in2(SIGS[2]), .in3(SIGS[3]), .in4(SIGS[4]), .in5(SIGS[5]), .in6(SIGS[6]),
    .in7(SIGS[7]), .in8(SIGS[8]), .in9(SIGS[9]), .in10(SIGS[10]), .in11(SIGS[11]), .in12(SIGS[12]),
    .in13(SIGS[13]), .in14(SIGS[14]), .in15(SIGS[15]), .out(senal_periferico), .sel(tabla_senal[3:0]));
  Multiplexer #(.select(1), .width(1), .enable("false")) multiplexer_3 (
    .in0(tabla_senal[4]), .in1(GPIO_EN), .out(mux1), .sel(sel_es_gpio));
  Multiplexer #(.select(1), .width(1), .enable("false")) multiplexer_4 (
    .in0(senal_periferico), .in1(GPIO_OUT), .out(valor_matriz), .sel(sel_es_gpio));
  Multiplexer #(.select(1), .width(1), .enable("false")) multiplexer_5 (
    .in0(mux1), .in1(GPIO_EN), .out(mux2), .sel(OUT_CFG[9]));
  xor xor_1 (valor_matriz_inv, valor_matriz, OUT_CFG[8]);
  xor xor_2 (oe_matriz, mux2, OUT_CFG[10]);
  Multiplexer #(.select(1), .width(1), .enable("false")) multiplexer_6 (
    .in0(F0_OE), .in1(oe_matriz), .out(mux4), .sel(F0_ES_GPIO));
  Multiplexer #(.select(1), .width(1), .enable("false")) multiplexer_7 (
    .in0(F0_OUT), .in1(valor_matriz_inv), .out(mux3), .sel(F0_ES_GPIO));
  Multiplexer #(.select(3), .width(1), .enable("false")) multiplexer_8 (
    .in0(mux3), .in1(valor_matriz_inv), .in2(F2_OUT), .in3(1'b0), .in4(1'b0), .in5(1'b0), .in6(1'b0),
    .in7(1'b0), .out(valor_salida), .sel(IOMUX_CFG[4:2]));
  Multiplexer #(.select(3), .width(1), .enable("false")) multiplexer_9 (
    .in0(mux4), .in1(oe_matriz), .in2(F2_OE), .in3(1'b0), .in4(1'b0), .in5(1'b0), .in6(1'b0), .in7(1'b0),
    .out(habilita_salida), .sel(IOMUX_CFG[4:2]));
  and and_2 (and5, OPEN_DRAIN, valor_salida);
  not not_1 (not6, and5);
  and and_3 (oe_final, habilita_salida, not6);
  assign PAD_OUT = oe_final ? valor_salida : 1'bz;  // Controlled_Buffer controlled_buffer_3

  // Other names for the same wires on the sheet: ENTRADA_2 = ENTRADA; entrada_t = ENTRADA; IOMUX_CFG_0 = IOMUX_CFG[0];
  //   IOMUX_CFG_1 = IOMUX_CFG[1]; IOMUX_CFG_4_2[2:0] = IOMUX_CFG[4:2]; OUT_CFG_7_0[7:0] = OUT_CFG[7:0];
  //   OUT_CFG_8 = OUT_CFG[8]; OUT_CFG_9 = OUT_CFG[9]; OUT_CFG_10 = OUT_CFG[10]; pad_salida = PAD_OUT;
  //   SIGS_0 = SIGS[0]; SIGS_1 = SIGS[1]; SIGS_2 = SIGS[2]; SIGS_3 = SIGS[3]; SIGS_4 = SIGS[4]; SIGS_5 = SIGS[5];
  //   SIGS_6 = SIGS[6]; SIGS_7 = SIGS[7]; SIGS_8 = SIGS[8]; SIGS_9 = SIGS[9]; SIGS_10 = SIGS[10]; SIGS_11 = SIGS[11];
  //   SIGS_12 = SIGS[12]; SIGS_13 = SIGS[13]; SIGS_14 = SIGS[14]; SIGS_15 = SIGS[15];
  //   tabla_senal_3_0[3:0] = tabla_senal[3:0]; tabla_senal_4 = tabla_senal[4]

  // Notes on the sheet:
  //   contents of TABLA_SENALES (hex, n*v repeats v):
  //   0 0 0 0 0 0 10 0 0 11 0 0 0 0 0 0 0 0 0 0 0 0 0 0 0 0 0 0 0 0 0 0 0 0 0 0 0 0 0 0 0 0 0 0 0 12 13 14
  //   15 16 17 0 0 18 19 0 0 0 0 0 0 0 0 1a 0 1b 0 0 1c 0 0 0 0 0 0 0 0 0 0 0 0 0 0 0 0 0 0 0 0 0 0 0 0 0
  //   0 0 0 0 0 0 0 0 0 0 0 0 0 0 0 0 0 0 0 0 0 0 0 0 0 0 0 0 0 0 0 0 0 0 0 0 0 0 0 0 0 0 0 0 0 0 0 0 0 0
  //   0 0 0 0 0 0 0 0 0 0 0 0 0 0 0 0 0 0 0 0 0 0 0 0 0 0 0 0 0 0 0 0 0 0 0 0 0 0 0 0 0 0 0 0 0 0 0 0 0 0
  //   0 0 0 0 0 0 0 0 0 0 0 0 0 0 0 0 0 0 0 0 0 0 0 0 0 0 0 0 0 0 0 0 0 0 0 0 0 0 0 0 0 0 0 0 0 0 0 0 0 0
  //   0 0 0 0 0 0 0 0 0 0 0 0
endmodule
module GPIO_IOMUX (
  input  CLK,
  input  RST,
  input  SEL,
  input  [9:0] A,
  input  [31:0] WD,
  input  WE,
  input  RE,
  input  [21:0] PAD_IN,
  input  SIG_U0TXD,
  input  SIG_U1TXD,
  input  SIG_LEDC0,
  input  SIG_LEDC1,
  input  SIG_LEDC2,
  input  SIG_LEDC3,
  input  SIG_LEDC4,
  input  SIG_LEDC5,
  input  SIG_I2C_SCL,
  input  SIG_I2C_SDA,
  input  SIG_FSPICLK,
  input  SIG_FSPID,
  input  SIG_FSPICS0,
  input  [5:0] FSPI_OUT,
  input  [5:0] FSPI_OE,
  input  SEL_IOMUX,
  output [21:0] PAD_OUT,
  output IRQ,
  output IRQ_NMI,
  output U0RXD,
  output U1RXD,
  output I2C_SCL,
  output I2C_SDA,
  output FSPIQ,
  output [31:0] RD
);

  wire and261, and265, and287, CFG_ENTRADA0_escribe, CFG_ENTRADA1_escribe, CFG_IOMUX0_escribe,
       CFG_IOMUX1_escribe, CFG_IOMUX2_escribe, CFG_IOMUX3_escribe, CFG_PIN0_escribe, CFG_PIN1_escribe,
       CFG_PIN2_escribe, CFG_PIN3_escribe, CFG_PIN4_escribe, CFG_SALIDA0_escribe, CFG_SALIDA1_escribe,
       CFG_SALIDA2_escribe, CFG_SALIDA3_escribe, CFG_SALIDA4_escribe, CFG_SALIDA5_escribe,
       CFG_SALIDA6_escribe, CFG_SALIDA7_escribe, CFG_SALIDA8_escribe, CFG_SALIDA9_escribe,
       CFG_SALIDA10_escribe, directa0, directa1, directa3, directa4, directa5, directa6, directa7, directa10,
       directa11, directa12, directa13, directa14, directa15, directa16, directa17, directa18, directa19,
       directa20, directa21, directo_FSPIQ, directo_U0RXD, eq249, eq251, eq254, eq259, esc_00C, esc_004,
       esc_04C, esc_5A0, esc_5A4, esc_5A8, esc_008, esc_16C, esc_020, esc_22C, esc_024, esc_028, esc_044,
       esc_048, esc_55C, esc_56C, esc_57C, esc_58C, esc_59C, esc_178, esc_228, esc_554, esc_558, esc_560,
       esc_564, esc_568, esc_570, esc_574, esc_578, esc_580, esc_584, esc_588, esc_590, esc_594, esc_598,
       escribe, in0, in1, in2, in3, in4, in5, in6, in7, in8, in9, in10, in11, in12, in13, in14, in15, in16,
       in17, in18, in19, in20, in21, iomux_esc_00C, iomux_esc_01C, iomux_esc_02C, iomux_esc_03C,
       iomux_esc_004, iomux_esc_04C, iomux_esc_008, iomux_esc_010, iomux_esc_014, iomux_esc_018,
       iomux_esc_020, iomux_esc_024, iomux_esc_028, iomux_esc_030, iomux_esc_034, iomux_esc_038,
       iomux_esc_040, iomux_esc_044, iomux_esc_048, iomux_esc_050, iomux_esc_054, iomux_esc_058, iomux_r00C,
       iomux_r0FC, iomux_r01C, iomux_r02C, iomux_r03C, iomux_r004, iomux_r04C, iomux_r008, iomux_r010,
       iomux_r014, iomux_r018, iomux_r020, iomux_r024, iomux_r028, iomux_r030, iomux_r034, iomux_r038,
       iomux_r040, iomux_r044, iomux_r048, iomux_r050, iomux_r054, iomux_r058, lee, lin_0, lin_1, lin_2,
       lin_3, lin_4, lin_5, lin_6, lin_7, lin_8, lin_9, lin_10, lin_11, lin_12, lin_13, lin_14, lin_15,
       lin_16, lin_17, lin_18, lin_19, lin_20, lin_21, lin_22, lin_23, lin_24, lin_25, lin_26, lin_27,
       lin_28, lin_29, lin_30, lin_31, matriz_FSPIQ, matriz_I2C_SCL, matriz_I2C_SDA, matriz_U0RXD,
       matriz_U1RXD, not239, or8, or16, pag_0, pag_1, pag_2, pag_3, pag_4, pag_5, pag_6, pag_7, pag_8, pag_9,
       pag_10, pag_11, pag_12, pag_13, pag_14, pag_15, pag_16, pag_17, pag_18, pag_19, pag_20, pag_21,
       pag_22, pag_23, pag_24, pag_25, pag_26, pag_27, pag_28, pag_29, pag_30, pag_31, r0A0, r0A4, r0A8,
       r0AC, r0B0, r0B4, r0B8, r0BC, r00C, r0C0, r0C4, r0C8, r03C, r004, r04C, r5A0, r5A4, r5A8, r05C, r07C,
       r008, r08C, r09C, r14C, r16C, r020, r22C, r024, r028, r038, r044, r048, r55C, r56C, r57C, r58C, r59C,
       r060, r074, r078, r080, r084, r088, r090, r094, r098, r178, r228, r254, r554, r558, r560, r564, r568,
       r570, r574, r578, r580, r584, r588, r590, r594, r598, registros_gpio_acceso, registros_gpio_existe,
       registros_iomux_acceso, registros_iomux_existe, seleccionado, strap_capturado, xor253, xor255, xor256,
       xor257, xor258;
  wire [3:1] cat238;
  wire [6:0] and162, and163, CFG_ENTRADA1, CFG_ENTRADA1_mascara, CFG_ENTRADA1_sig, not161;
  wire [9:0] dir_registro, rep260;
  wire [10:0] and74, and75, CFG_PIN4, CFG_PIN4_mascara, CFG_PIN4_sig, not73;
  wire [17:0] and224, and225, CFG_IOMUX3, CFG_IOMUX3_mascara, CFG_IOMUX3_sig, not223, qx227, xor226;
  wire [21:0] and79, and80, and86, and87, and93, and94, and100, and101, and107, and108, and114, and115,
       and121, and122, and128, and129, and135, and136, and142, and143, and149, and150, and233, and234,
       and236, and237, anterior, CFG_SALIDA0, CFG_SALIDA0_mascara, CFG_SALIDA0_sig, CFG_SALIDA1,
       CFG_SALIDA1_mascara, CFG_SALIDA1_sig, CFG_SALIDA2, CFG_SALIDA2_mascara, CFG_SALIDA2_sig, CFG_SALIDA3,
       CFG_SALIDA3_mascara, CFG_SALIDA3_sig, CFG_SALIDA4, CFG_SALIDA4_mascara, CFG_SALIDA4_sig, CFG_SALIDA5,
       CFG_SALIDA5_mascara, CFG_SALIDA5_sig, CFG_SALIDA6, CFG_SALIDA6_mascara, CFG_SALIDA6_sig, CFG_SALIDA7,
       CFG_SALIDA7_mascara, CFG_SALIDA7_sig, CFG_SALIDA8, CFG_SALIDA8_mascara, CFG_SALIDA8_sig, CFG_SALIDA9,
       CFG_SALIDA9_mascara, CFG_SALIDA9_sig, CFG_SALIDA10, CFG_SALIDA10_mascara, CFG_SALIDA10_sig,
       eventos_pads, flancos_bajada, flancos_subida, int_bajada, int_nivel_alto, int_nivel_bajo, int_subida,
       not78, not85, not92, not99, not106, not113, not120, not127, not134, not141, not148, not228, not229,
       not230, not231, not232, not235, qx82, qx89, qx96, qx103, qx110, qx117, qx124, qx131, qx138, qx145,
       qx152, sinc1, xor81, xor88, xor95, xor102, xor109, xor116, xor123, xor130, xor137, xor144, xor151;
  wire [21:21] CFG_SALIDA0_nuevo;
  wire [25:25] CFG_PIN0_nuevo;
  wire [27:0] and158, and159, CFG_ENTRADA0, CFG_ENTRADA0_mascara, CFG_ENTRADA0_sig, not157;
  wire [27:21] CFG_ENTRADA0_nuevo;
  wire [29:0] and41, and42, and54, and55, and67, and68, and195, and196, and212, and213, CFG_IOMUX1,
       CFG_IOMUX1_mascara, CFG_IOMUX1_sig, CFG_IOMUX2, CFG_IOMUX2_mascara, CFG_IOMUX2_sig, CFG_PIN1,
       CFG_PIN1_mascara, CFG_PIN1_sig, CFG_PIN2, CFG_PIN2_mascara, CFG_PIN2_sig, CFG_PIN3, CFG_PIN3_mascara,
       CFG_PIN3_sig, not40, not53, not66, not194, not211, qx198, qx215, xor197, xor214;
  wire [30:0] and28, and29, CFG_PIN0, CFG_PIN0_mascara, CFG_PIN0_sig, not27;
  wire [31:0] and1, and3, and7, and9, and11, and15, and178, and179, and240, and242, and246, and264, and268,
       and270, and272, and274, and276, and278, and280, and282, and284, and286, and290, CFG_IOMUX0,
       CFG_IOMUX0_mascara, CFG_IOMUX0_sig, eventos, GPIO_ENABLE, GPIO_ENABLE_sig, GPIO_IN, GPIO_OUT,
       GPIO_OUT_sig, mux2, mux5, mux10, mux13, mux241, mux244, mux247, mux291, not6, not14, not177, not245,
       not263, not285, or4, or12, or243, or248, PCPU_INT, PCPU_NMI_INT, qx181, registros_gpio_a_guardar,
       registros_gpio_bits_fijos, registros_gpio_bits_rw, registros_gpio_guardado, registros_gpio_reset_rw,
       registros_gpio_valor, registros_gpio_valor_reset, registros_iomux_a_guardar,
       registros_iomux_bits_fijos, registros_iomux_bits_rw, registros_iomux_guardado,
       registros_iomux_reset_rw, registros_iomux_valor, registros_iomux_valor_reset, rep262, rep267, rep269,
       rep271, rep273, rep275, rep277, rep279, rep281, rep283, rep289, STATUS, STRAP, xor180, xor266, xor288;
  wire [31:11] dato_escrito;
  wire [31:27] CFG_IOMUX0_nuevo;

  Register #(.width(32)) u_GPIO_OUT (.D(GPIO_OUT_sig), .en(or8), .Q(GPIO_OUT), .clk(CLK), .clr(RST));
  Register #(.width(32)) u_GPIO_ENABLE (.D(GPIO_ENABLE_sig), .en(or16), .Q(GPIO_ENABLE), .clk(CLK), .clr(RST));
  Register #(.width(31)) u_CFG_PIN0 (.D(CFG_PIN0_sig), .en(CFG_PIN0_escribe), .Q(CFG_PIN0), .clk(CLK), .clr(RST));
  Register #(.width(30)) u_CFG_PIN1 (.D(CFG_PIN1_sig), .en(CFG_PIN1_escribe), .Q(CFG_PIN1), .clk(CLK), .clr(RST));
  Register #(.width(30)) u_CFG_PIN2 (.D(CFG_PIN2_sig), .en(CFG_PIN2_escribe), .Q(CFG_PIN2), .clk(CLK), .clr(RST));
  Register #(.width(30)) u_CFG_PIN3 (.D(CFG_PIN3_sig), .en(CFG_PIN3_escribe), .Q(CFG_PIN3), .clk(CLK), .clr(RST));
  Register #(.width(11)) u_CFG_PIN4 (.D(CFG_PIN4_sig), .en(CFG_PIN4_escribe), .Q(CFG_PIN4), .clk(CLK), .clr(RST));
  Register #(.width(22)) u_CFG_SALIDA0 (.D(xor81), .en(CFG_SALIDA0_escribe), .Q(qx82), .clk(CLK), .clr(RST));
  Register #(.width(22)) u_CFG_SALIDA1 (.D(xor88), .en(CFG_SALIDA1_escribe), .Q(qx89), .clk(CLK), .clr(RST));
  Register #(.width(22)) u_CFG_SALIDA2 (.D(xor95), .en(CFG_SALIDA2_escribe), .Q(qx96), .clk(CLK), .clr(RST));
  Register #(.width(22)) u_CFG_SALIDA3 (.D(xor102), .en(CFG_SALIDA3_escribe), .Q(qx103), .clk(CLK), .clr(RST));
  Register #(.width(22)) u_CFG_SALIDA4 (.D(xor109), .en(CFG_SALIDA4_escribe), .Q(qx110), .clk(CLK), .clr(RST));
  Register #(.width(22)) u_CFG_SALIDA5 (.D(xor116), .en(CFG_SALIDA5_escribe), .Q(qx117), .clk(CLK), .clr(RST));
  Register #(.width(22)) u_CFG_SALIDA6 (.D(xor123), .en(CFG_SALIDA6_escribe), .Q(qx124), .clk(CLK), .clr(RST));
  Register #(.width(22)) u_CFG_SALIDA7 (.D(xor130), .en(CFG_SALIDA7_escribe), .Q(qx131), .clk(CLK), .clr(RST));
  Register #(.width(22)) u_CFG_SALIDA8 (.D(xor137), .en(CFG_SALIDA8_escribe), .Q(qx138), .clk(CLK), .clr(RST));
  Register #(.width(22)) u_CFG_SALIDA9 (.D(xor144), .en(CFG_SALIDA9_escribe), .Q(qx145), .clk(CLK), .clr(RST));
  Register #(.width(22)) u_CFG_SALIDA10 (.D(xor151), .en(CFG_SALIDA10_escribe), .Q(qx152), .clk(CLK), .clr(RST));
  Register #(.width(28)) u_CFG_ENTRADA0 (
    .D(CFG_ENTRADA0_sig), .en(CFG_ENTRADA0_escribe), .Q(CFG_ENTRADA0), .clk(CLK), .clr(RST));
  Register #(.width(22)) u_SINC1 (
    .D({directa21, directa20, directa19, directa18, directa17, directa16, directa15, directa14, directa13, directa12, directa11, directa10, cat238[3:2], directa7, directa6, directa5, directa4, directa3, cat238[1], directa1, directa0}),
    .en(1'b1), .Q(sinc1), .clk(CLK), .clr(RST));
  Register #(.width(22)) SINC2 (
    .D(sinc1), .en(1'b1),
    .Q({in21, in20, in19, in18, in17, in16, in15, in14, in13, in12, in11, in10, in9, in8, in7, in6, in5, in4, in3, in2, in1, in0}),
    .clk(CLK), .clr(RST));
  Register #(.width(22)) u_ANTERIOR (
    .D({in21, in20, in19, in18, in17, in16, in15, in14, in13, in12, in11, in10, in9, in8, in7, in6, in5, in4, in3, in2, in1, in0}),
    .en(1'b1), .Q(anterior), .clk(CLK), .clr(RST));
  Register #(.width(1)) STRAP_OK (.D(1'b1), .en(1'b1), .Q(strap_capturado), .clk(CLK), .clr(RST));
  Register #(.width(32)) u_STRAP (.D({{28{1'b0}}, cat238, 1'b0}), .en(not239), .Q(STRAP), .clk(CLK), .clr(RST));
  Register #(.width(32)) u_STATUS (.D(or248), .en(1'b1), .Q(STATUS), .clk(CLK), .clr(RST));
  Register #(.width(7)) u_CFG_ENTRADA1 (
    .D(CFG_ENTRADA1_sig), .en(CFG_ENTRADA1_escribe), .Q(CFG_ENTRADA1), .clk(CLK), .clr(RST));
  Register #(.width(32)) u_CFG_IOMUX0 (.D(xor180), .en(CFG_IOMUX0_escribe), .Q(qx181), .clk(CLK), .clr(RST));
  Register #(.width(30)) u_CFG_IOMUX1 (.D(xor197), .en(CFG_IOMUX1_escribe), .Q(qx198), .clk(CLK), .clr(RST));
  Register #(.width(30)) u_CFG_IOMUX2 (.D(xor214), .en(CFG_IOMUX2_escribe), .Q(qx215), .clk(CLK), .clr(RST));
  Register #(.width(18)) u_CFG_IOMUX3 (.D(xor226), .en(CFG_IOMUX3_escribe), .Q(qx227), .clk(CLK), .clr(RST));
  or or_1 (seleccionado, SEL, SEL_IOMUX);
  ROM #(.addrWidth(10), .dataWidth(1)) u_REGISTROS_GPIO_EXISTE (.addr(dir_registro), .data(registros_gpio_existe));
  ROM #(.addrWidth(10), .dataWidth(32)) u_REGISTROS_GPIO_VALOR_RESET (
    .addr(dir_registro), .data(registros_gpio_valor_reset));
  ROM #(.addrWidth(10), .dataWidth(32)) u_REGISTROS_GPIO_BITS_RW (.addr(dir_registro), .data(registros_gpio_bits_rw));
  ROM #(.addrWidth(10), .dataWidth(1)) u_REGISTROS_IOMUX_EXISTE (.addr(dir_registro), .data(registros_iomux_existe));
  ROM #(.addrWidth(10), .dataWidth(32)) u_REGISTROS_IOMUX_VALOR_RESET (
    .addr(dir_registro), .data(registros_iomux_valor_reset));
  ROM #(.addrWidth(10), .dataWidth(32)) u_REGISTROS_IOMUX_BITS_RW (.addr(dir_registro), .data(registros_iomux_bits_rw));
  RAM #(.addrWidth(10), .dataWidth(32), .enables("byte"), .trigger("rising"), .asyncread("true"), .databus("bibus"), .clearpin("true")) REGISTROS_GPIO (
    .addr(dir_registro), .we(and265), .oe(1'b1), .clk(CLK), .din(registros_gpio_a_guardar),
    .dout(registros_gpio_guardado), .clr(RST));
  RAM #(.addrWidth(10), .dataWidth(32), .enables("byte"), .trigger("rising"), .asyncread("true"), .databus("bibus"), .clearpin("true")) REGISTROS_IOMUX (
    .addr(dir_registro), .we(and287), .oe(1'b1), .clk(CLK), .din(registros_iomux_a_guardar),
    .dout(registros_iomux_guardado), .clr(RST));
  assign CFG_SALIDA0 = qx82 ^ 22'h40080;  // XOR_Gate xor_1, 22 bits wide
  assign CFG_SALIDA1 = qx89 ^ 22'h40080;  // XOR_Gate xor_2, 22 bits wide
  assign CFG_SALIDA2 = qx96 ^ 22'h40080;  // XOR_Gate xor_3, 22 bits wide
  assign CFG_SALIDA3 = qx103 ^ 22'h40080;  // XOR_Gate xor_4, 22 bits wide
  assign CFG_SALIDA4 = qx110 ^ 22'h40080;  // XOR_Gate xor_5, 22 bits wide
  assign CFG_SALIDA5 = qx117 ^ 22'h40080;  // XOR_Gate xor_6, 22 bits wide
  assign CFG_SALIDA6 = qx124 ^ 22'h40080;  // XOR_Gate xor_7, 22 bits wide
  assign CFG_SALIDA7 = qx131 ^ 22'h40080;  // XOR_Gate xor_8, 22 bits wide
  assign CFG_SALIDA8 = qx138 ^ 22'h40080;  // XOR_Gate xor_9, 22 bits wide
  assign CFG_SALIDA9 = qx145 ^ 22'h40080;  // XOR_Gate xor_10, 22 bits wide
  assign CFG_SALIDA10 = qx152 ^ 22'h40080;  // XOR_Gate xor_11, 22 bits wide
  assign CFG_IOMUX3 = qx227 ^ 18'h4310;  // XOR_Gate xor_12, 18 bits wide
  assign CFG_IOMUX0 = qx181 ^ 32'h84210800;  // XOR_Gate xor_13, 32 bits wide
  assign CFG_IOMUX1 = qx198 ^ 30'h31086210;  // XOR_Gate xor_14, 30 bits wide
  assign CFG_IOMUX2 = qx215 ^ 30'h218c6318;  // XOR_Gate xor_15, 30 bits wide
  assign not228 = ~anterior;  // NOT_Gate not_1, 22 bits wide
  assign not229 = ~{in21, in20, in19, in18, in17, in16, in15, in14, in13, in12, in11, in10, in9, in8, in7, in6, in5, in4, in3, in2, in1, in0};  // NOT_Gate not_2, 22 bits wide
  assign not235 = ~{in21, in20, in19, in18, in17, in16, in15, in14, in13, in12, in11, in10, in9, in8, in7, in6, in5, in4, in3, in2, in1, in0};  // NOT_Gate not_3, 22 bits wide
  assign GPIO_IN = {{10{1'b0}}, {in21, in20, in19, in18, in17, in16, in15, in14, in13, in12, in11, in10, in9, in8, in7, in6, in5, in4, in3, in2, in1, in0}};  // Bit_Extender bit_extender_1
  not not_4 (not239, strap_capturado);
  assign rep260 = {{9{seleccionado}}, seleccionado};  // Bit_Extender bit_extender_2
  and and_1 (and261, seleccionado, WE);
  and and_2 (escribe, WE, seleccionado);
  and and_3 (lee, RE, seleccionado);
  assign not263 = ~registros_gpio_bits_rw;  // NOT_Gate not_5, 32 bits wide
  and and_4 (registros_gpio_acceso, SEL, registros_gpio_existe);
  assign registros_gpio_reset_rw = registros_gpio_valor_reset & registros_gpio_bits_rw;  // AND_Gate and_5, 32 bits wide
  and and_6 (registros_iomux_acceso, SEL_IOMUX, registros_iomux_existe);
  assign registros_iomux_reset_rw = registros_iomux_valor_reset & registros_iomux_bits_rw;  // AND_Gate and_7, 32 bits wide
  assign not285 = ~registros_iomux_bits_rw;  // NOT_Gate not_6, 32 bits wide
  assign flancos_subida = {in21, in20, in19, in18, in17, in16, in15, in14, in13, in12, in11, in10, in9, in8, in7, in6, in5, in4, in3, in2, in1, in0} & not228;  // AND_Gate and_8, 22 bits wide
  assign flancos_bajada = not229 & anterior;  // AND_Gate and_9, 22 bits wide
  Multiplexer #(.select(5), .width(1), .enable("false")) multiplexer_1 (
    .in0(in0), .in1(in1), .in2(in2), .in3(in3), .in4(in4), .in5(in5), .in6(in6), .in7(in7), .in8(in8),
    .in9(in9), .in10(in10), .in11(in11), .in12(in12), .in13(in13), .in14(in14), .in15(in15), .in16(in16),
    .in17(in17), .in18(in18), .in19(in19), .in20(in20), .in21(in21), .in22(1'b0), .in23(1'b0), .in24(1'b0),
    .in25(1'b0), .in26(1'b0), .in27(1'b0), .in28(1'b0), .in29(1'b0), .in30(1'b1), .in31(1'b0),
    .out(matriz_FSPIQ), .sel(CFG_ENTRADA1[4:0]));
  assign dir_registro = A & rep260;  // AND_Gate and_10, 10 bits wide
  assign rep262 = {{31{and261}}, and261};  // Bit_Extender bit_extender_3
  assign registros_gpio_bits_fijos = registros_gpio_valor_reset & not263;  // AND_Gate and_11, 32 bits wide
  and and_12 (and265, escribe, registros_gpio_acceso);
  assign xor266 = registros_gpio_guardado ^ registros_gpio_reset_rw;  // XOR_Gate xor_16, 32 bits wide
  assign rep267 = {{31{registros_gpio_acceso}}, registros_gpio_acceso};  // Bit_Extender bit_extender_4
  assign registros_iomux_bits_fijos = registros_iomux_valor_reset & not285;  // AND_Gate and_13, 32 bits wide
  and and_14 (and287, escribe, registros_iomux_acceso);
  assign xor288 = registros_iomux_guardado ^ registros_iomux_reset_rw;  // XOR_Gate xor_17, 32 bits wide
  assign rep289 = {{31{registros_iomux_acceso}}, registros_iomux_acceso};  // Bit_Extender bit_extender_5
  Multiplexer #(.select(5), .width(1), .enable("false")) multiplexer_2 (
    .in0(in0), .in1(in1), .in2(in2), .in3(in3), .in4(in4), .in5(in5), .in6(in6), .in7(in7), .in8(in8),
    .in9(in9), .in10(in10), .in11(in11), .in12(in12), .in13(in13), .in14(in14), .in15(in15), .in16(in16),
    .in17(in17), .in18(in18), .in19(in19), .in20(in20), .in21(in21), .in22(1'b0), .in23(1'b0), .in24(1'b0),
    .in25(1'b0), .in26(1'b0), .in27(1'b0), .in28(1'b0), .in29(1'b0), .in30(1'b1), .in31(1'b0),
    .out(matriz_U0RXD), .sel(CFG_ENTRADA0[4:0]));
  Comparator #(.width(3), .mode("unsigned")) comparator_1 (
    .a(CFG_IOMUX3[12:10]), .b(3'b000), .eq(eq254));  // open: gt, lt
  Multiplexer #(.select(5), .width(1), .enable("false")) multiplexer_3 (
    .in0(in0), .in1(in1), .in2(in2), .in3(in3), .in4(in4), .in5(in5), .in6(in6), .in7(in7), .in8(in8),
    .in9(in9), .in10(in10), .in11(in11), .in12(in12), .in13(in13), .in14(in14), .in15(in15), .in16(in16),
    .in17(in17), .in18(in18), .in19(in19), .in20(in20), .in21(in21), .in22(1'b0), .in23(1'b0), .in24(1'b0),
    .in25(1'b0), .in26(1'b0), .in27(1'b0), .in28(1'b0), .in29(1'b0), .in30(1'b1), .in31(1'b0),
    .out(matriz_U1RXD), .sel(CFG_ENTRADA0[11:7]));
  Multiplexer #(.select(5), .width(1), .enable("false")) multiplexer_4 (
    .in0(in0), .in1(in1), .in2(in2), .in3(in3), .in4(in4), .in5(in5), .in6(in6), .in7(in7), .in8(in8),
    .in9(in9), .in10(in10), .in11(in11), .in12(in12), .in13(in13), .in14(in14), .in15(in15), .in16(in16),
    .in17(in17), .in18(in18), .in19(in19), .in20(in20), .in21(in21), .in22(1'b0), .in23(1'b0), .in24(1'b0),
    .in25(1'b0), .in26(1'b0), .in27(1'b0), .in28(1'b0), .in29(1'b0), .in30(1'b1), .in31(1'b0),
    .out(matriz_I2C_SCL), .sel(CFG_ENTRADA0[18:14]));
  Multiplexer #(.select(5), .width(1), .enable("false")) multiplexer_5 (
    .in0(in0), .in1(in1), .in2(in2), .in3(in3), .in4(in4), .in5(in5), .in6(in6), .in7(in7), .in8(in8),
    .in9(in9), .in10(in10), .in11(in11), .in12(in12), .in13(in13), .in14(in14), .in15(in15), .in16(in16),
    .in17(in17), .in18(in18), .in19(in19), .in20(in20), .in21(in21), .in22(1'b0), .in23(1'b0), .in24(1'b0),
    .in25(1'b0), .in26(1'b0), .in27(1'b0), .in28(1'b0), .in29(1'b0), .in30(1'b1), .in31(1'b0),
    .out(matriz_I2C_SDA), .sel(CFG_ENTRADA0[25:21]));
  assign {dato_escrito[31:15], CFG_IOMUX0_nuevo[29:27], dato_escrito[11], CFG_SALIDA0_nuevo[21], CFG_IOMUX0_nuevo[31:30], CFG_PIN0_nuevo[25], CFG_ENTRADA0_nuevo} = WD & rep262;  // AND_Gate and_15, 32 bits wide
  xor xor_18 (xor258, matriz_FSPIQ, CFG_ENTRADA1[5]);
  Comparator #(.width(3), .mode("unsigned")) comparator_2 (
    .a(CFG_IOMUX0[14:12]), .b(3'b010), .eq(eq259));  // open: gt, lt
  assign registros_gpio_valor = xor266 | registros_gpio_bits_fijos;  // OR_Gate or_2, 32 bits wide
  assign registros_iomux_valor = xor288 | registros_iomux_bits_fijos;  // OR_Gate or_3, 32 bits wide
  Decoder #(.select(5), .enable("false")) decoder_1 (
    .out0(pag_0), .out1(pag_1), .out2(pag_2), .out3(pag_3), .out4(pag_4), .out5(pag_5), .out6(pag_6),
    .out7(pag_7), .out8(pag_8), .out9(pag_9), .out10(pag_10), .out11(pag_11), .out12(pag_12), .out13(pag_13),
    .out14(pag_14), .out15(pag_15), .out16(pag_16), .out17(pag_17), .out18(pag_18), .out19(pag_19),
    .out20(pag_20), .out21(pag_21), .out22(pag_22), .out23(pag_23), .out24(pag_24), .out25(pag_25),
    .out26(pag_26), .out27(pag_27), .out28(pag_28), .out29(pag_29), .out30(pag_30), .out31(pag_31),
    .sel(dir_registro[9:5]));
  Decoder #(.select(5), .enable("false")) decoder_2 (
    .out0(lin_0), .out1(lin_1), .out2(lin_2), .out3(lin_3), .out4(lin_4), .out5(lin_5), .out6(lin_6),
    .out7(lin_7), .out8(lin_8), .out9(lin_9), .out10(lin_10), .out11(lin_11), .out12(lin_12), .out13(lin_13),
    .out14(lin_14), .out15(lin_15), .out16(lin_16), .out17(lin_17), .out18(lin_18), .out19(lin_19),
    .out20(lin_20), .out21(lin_21), .out22(lin_22), .out23(lin_23), .out24(lin_24), .out25(lin_25),
    .out26(lin_26), .out27(lin_27), .out28(lin_28), .out29(lin_29), .out30(lin_30), .out31(lin_31),
    .sel(dir_registro[4:0]));
  assign and1 = {dato_escrito[31:15], CFG_IOMUX0_nuevo[29:27], dato_escrito[11], CFG_SALIDA0_nuevo[21], CFG_IOMUX0_nuevo[31:30], CFG_PIN0_nuevo[25], CFG_ENTRADA0_nuevo} & 32'h3fffff;  // AND_Gate and_16, 32 bits wide
  assign and3 = {dato_escrito[31:15], CFG_IOMUX0_nuevo[29:27], dato_escrito[11], CFG_SALIDA0_nuevo[21], CFG_IOMUX0_nuevo[31:30], CFG_PIN0_nuevo[25], CFG_ENTRADA0_nuevo} & 32'h3fffff;  // AND_Gate and_17, 32 bits wide
  assign not6 = ~{dato_escrito[31:15], CFG_IOMUX0_nuevo[29:27], dato_escrito[11], CFG_SALIDA0_nuevo[21], CFG_IOMUX0_nuevo[31:30], CFG_PIN0_nuevo[25], CFG_ENTRADA0_nuevo};  // NOT_Gate not_7, 32 bits wide
  assign and9 = {dato_escrito[31:15], CFG_IOMUX0_nuevo[29:27], dato_escrito[11], CFG_SALIDA0_nuevo[21], CFG_IOMUX0_nuevo[31:30], CFG_PIN0_nuevo[25], CFG_ENTRADA0_nuevo} & 32'h3fffff;  // AND_Gate and_18, 32 bits wide
  assign and11 = {dato_escrito[31:15], CFG_IOMUX0_nuevo[29:27], dato_escrito[11], CFG_SALIDA0_nuevo[21], CFG_IOMUX0_nuevo[31:30], CFG_PIN0_nuevo[25], CFG_ENTRADA0_nuevo} & 32'h3fffff;  // AND_Gate and_19, 32 bits wide
  assign not14 = ~{dato_escrito[31:15], CFG_IOMUX0_nuevo[29:27], dato_escrito[11], CFG_SALIDA0_nuevo[21], CFG_IOMUX0_nuevo[31:30], CFG_PIN0_nuevo[25], CFG_ENTRADA0_nuevo};  // NOT_Gate not_8, 32 bits wide
  PadGPIO PAD0 (
    .PAD_IN(PAD_IN[0]), .OPEN_DRAIN(CFG_PIN0[0]), .OUT_CFG(CFG_SALIDA0[10:0]), .IOMUX_CFG(CFG_IOMUX0[4:0]),
    .GPIO_OUT(GPIO_OUT[0]), .GPIO_EN(GPIO_ENABLE[0]),
    .SIGS({3'b000, SIG_FSPICS0, SIG_FSPID, SIG_FSPICLK, SIG_I2C_SDA, SIG_I2C_SCL, SIG_LEDC5, SIG_LEDC4, SIG_LEDC3, SIG_LEDC2, SIG_LEDC1, SIG_LEDC0, SIG_U1TXD, SIG_U0TXD}),
    .F0_ES_GPIO(1'b1), .F0_OUT(1'b0), .F0_OE(1'b0), .F2_OUT(1'b0), .F2_OE(1'b0), .ENTRADA(directa0),
    .PAD_OUT(PAD_OUT[0]));
  PadGPIO PAD1 (
    .PAD_IN(PAD_IN[1]), .OPEN_DRAIN(CFG_PIN0[6]), .OUT_CFG(CFG_SALIDA0[21:11]), .IOMUX_CFG(CFG_IOMUX0[9:5]),
    .GPIO_OUT(GPIO_OUT[1]), .GPIO_EN(GPIO_ENABLE[1]),
    .SIGS({3'b000, SIG_FSPICS0, SIG_FSPID, SIG_FSPICLK, SIG_I2C_SDA, SIG_I2C_SCL, SIG_LEDC5, SIG_LEDC4, SIG_LEDC3, SIG_LEDC2, SIG_LEDC1, SIG_LEDC0, SIG_U1TXD, SIG_U0TXD}),
    .F0_ES_GPIO(1'b1), .F0_OUT(1'b0), .F0_OE(1'b0), .F2_OUT(1'b0), .F2_OE(1'b0), .ENTRADA(directa1),
    .PAD_OUT(PAD_OUT[1]));
  PadGPIO PAD2 (
    .PAD_IN(PAD_IN[2]), .OPEN_DRAIN(CFG_PIN0[12]), .OUT_CFG(CFG_SALIDA1[10:0]),
    .IOMUX_CFG(CFG_IOMUX0[14:10]), .GPIO_OUT(GPIO_OUT[2]), .GPIO_EN(GPIO_ENABLE[2]),
    .SIGS({3'b000, SIG_FSPICS0, SIG_FSPID, SIG_FSPICLK, SIG_I2C_SDA, SIG_I2C_SCL, SIG_LEDC5, SIG_LEDC4, SIG_LEDC3, SIG_LEDC2, SIG_LEDC1, SIG_LEDC0, SIG_U1TXD, SIG_U0TXD}),
    .F0_ES_GPIO(1'b1), .F0_OUT(1'b0), .F0_OE(1'b0), .F2_OUT(FSPI_OUT[0]), .F2_OE(FSPI_OE[0]),
    .ENTRADA(cat238[1]), .PAD_OUT(PAD_OUT[2]));
  PadGPIO PAD3 (
    .PAD_IN(PAD_IN[3]), .OPEN_DRAIN(CFG_PIN0[18]), .OUT_CFG(CFG_SALIDA1[21:11]),
    .IOMUX_CFG(CFG_IOMUX0[19:15]), .GPIO_OUT(GPIO_OUT[3]), .GPIO_EN(GPIO_ENABLE[3]),
    .SIGS({3'b000, SIG_FSPICS0, SIG_FSPID, SIG_FSPICLK, SIG_I2C_SDA, SIG_I2C_SCL, SIG_LEDC5, SIG_LEDC4, SIG_LEDC3, SIG_LEDC2, SIG_LEDC1, SIG_LEDC0, SIG_U1TXD, SIG_U0TXD}),
    .F0_ES_GPIO(1'b1), .F0_OUT(1'b0), .F0_OE(1'b0), .F2_OUT(1'b0), .F2_OE(1'b0), .ENTRADA(directa3),
    .PAD_OUT(PAD_OUT[3]));
  PadGPIO PAD4 (
    .PAD_IN(PAD_IN[4]), .OPEN_DRAIN(CFG_PIN0[24]), .OUT_CFG(CFG_SALIDA2[10:0]),
    .IOMUX_CFG(CFG_IOMUX0[24:20]), .GPIO_OUT(GPIO_OUT[4]), .GPIO_EN(GPIO_ENABLE[4]),
    .SIGS({3'b000, SIG_FSPICS0, SIG_FSPID, SIG_FSPICLK, SIG_I2C_SDA, SIG_I2C_SCL, SIG_LEDC5, SIG_LEDC4, SIG_LEDC3, SIG_LEDC2, SIG_LEDC1, SIG_LEDC0, SIG_U1TXD, SIG_U0TXD}),
    .F0_ES_GPIO(1'b0), .F0_OUT(1'b0), .F0_OE(1'b0), .F2_OUT(FSPI_OUT[1]), .F2_OE(FSPI_OE[1]),
    .ENTRADA(directa4), .PAD_OUT(PAD_OUT[4]));
  PadGPIO PAD5 (
    .PAD_IN(PAD_IN[5]), .OPEN_DRAIN(CFG_PIN0[30]), .OUT_CFG(CFG_SALIDA2[21:11]),
    .IOMUX_CFG(CFG_IOMUX0[29:25]), .GPIO_OUT(GPIO_OUT[5]), .GPIO_EN(GPIO_ENABLE[5]),
    .SIGS({3'b000, SIG_FSPICS0, SIG_FSPID, SIG_FSPICLK, SIG_I2C_SDA, SIG_I2C_SCL, SIG_LEDC5, SIG_LEDC4, SIG_LEDC3, SIG_LEDC2, SIG_LEDC1, SIG_LEDC0, SIG_U1TXD, SIG_U0TXD}),
    .F0_ES_GPIO(1'b0), .F0_OUT(1'b0), .F0_OE(1'b0), .F2_OUT(FSPI_OUT[2]), .F2_OE(FSPI_OE[2]),
    .ENTRADA(directa5), .PAD_OUT(PAD_OUT[5]));
  PadGPIO PAD6 (
    .PAD_IN(PAD_IN[6]), .OPEN_DRAIN(CFG_PIN1[5]), .OUT_CFG(CFG_SALIDA3[10:0]),
    .IOMUX_CFG({CFG_IOMUX1[2:0], CFG_IOMUX0[31:30]}), .GPIO_OUT(GPIO_OUT[6]), .GPIO_EN(GPIO_ENABLE[6]),
    .SIGS({3'b000, SIG_FSPICS0, SIG_FSPID, SIG_FSPICLK, SIG_I2C_SDA, SIG_I2C_SCL, SIG_LEDC5, SIG_LEDC4, SIG_LEDC3, SIG_LEDC2, SIG_LEDC1, SIG_LEDC0, SIG_U1TXD, SIG_U0TXD}),
    .F0_ES_GPIO(1'b0), .F0_OUT(1'b0), .F0_OE(1'b0), .F2_OUT(FSPI_OUT[3]), .F2_OE(FSPI_OE[3]),
    .ENTRADA(directa6), .PAD_OUT(PAD_OUT[6]));
  PadGPIO PAD7 (
    .PAD_IN(PAD_IN[7]), .OPEN_DRAIN(CFG_PIN1[11]), .OUT_CFG(CFG_SALIDA3[21:11]), .IOMUX_CFG(CFG_IOMUX1[7:3]),
    .GPIO_OUT(GPIO_OUT[7]), .GPIO_EN(GPIO_ENABLE[7]),
    .SIGS({3'b000, SIG_FSPICS0, SIG_FSPID, SIG_FSPICLK, SIG_I2C_SDA, SIG_I2C_SCL, SIG_LEDC5, SIG_LEDC4, SIG_LEDC3, SIG_LEDC2, SIG_LEDC1, SIG_LEDC0, SIG_U1TXD, SIG_U0TXD}),
    .F0_ES_GPIO(1'b0), .F0_OUT(1'b0), .F0_OE(1'b0), .F2_OUT(FSPI_OUT[4]), .F2_OE(FSPI_OE[4]),
    .ENTRADA(directa7), .PAD_OUT(PAD_OUT[7]));
  PadGPIO PAD8 (
    .PAD_IN(PAD_IN[8]), .OPEN_DRAIN(CFG_PIN1[17]), .OUT_CFG(CFG_SALIDA4[10:0]), .IOMUX_CFG(CFG_IOMUX1[12:8]),
    .GPIO_OUT(GPIO_OUT[8]), .GPIO_EN(GPIO_ENABLE[8]),
    .SIGS({3'b000, SIG_FSPICS0, SIG_FSPID, SIG_FSPICLK, SIG_I2C_SDA, SIG_I2C_SCL, SIG_LEDC5, SIG_LEDC4, SIG_LEDC3, SIG_LEDC2, SIG_LEDC1, SIG_LEDC0, SIG_U1TXD, SIG_U0TXD}),
    .F0_ES_GPIO(1'b1), .F0_OUT(1'b0), .F0_OE(1'b0), .F2_OUT(1'b0), .F2_OE(1'b0), .ENTRADA(cat238[2]),
    .PAD_OUT(PAD_OUT[8]));
  PadGPIO PAD9 (
    .PAD_IN(PAD_IN[9]), .OPEN_DRAIN(CFG_PIN1[23]), .OUT_CFG(CFG_SALIDA4[21:11]),
    .IOMUX_CFG(CFG_IOMUX1[17:13]), .GPIO_OUT(GPIO_OUT[9]), .GPIO_EN(GPIO_ENABLE[9]),
    .SIGS({3'b000, SIG_FSPICS0, SIG_FSPID, SIG_FSPICLK, SIG_I2C_SDA, SIG_I2C_SCL, SIG_LEDC5, SIG_LEDC4, SIG_LEDC3, SIG_LEDC2, SIG_LEDC1, SIG_LEDC0, SIG_U1TXD, SIG_U0TXD}),
    .F0_ES_GPIO(1'b1), .F0_OUT(1'b0), .F0_OE(1'b0), .F2_OUT(1'b0), .F2_OE(1'b0), .ENTRADA(cat238[3]),
    .PAD_OUT(PAD_OUT[9]));
  PadGPIO PAD10 (
    .PAD_IN(PAD_IN[10]), .OPEN_DRAIN(CFG_PIN1[29]), .OUT_CFG(CFG_SALIDA5[10:0]),
    .IOMUX_CFG(CFG_IOMUX1[22:18]), .GPIO_OUT(GPIO_OUT[10]), .GPIO_EN(GPIO_ENABLE[10]),
    .SIGS({3'b000, SIG_FSPICS0, SIG_FSPID, SIG_FSPICLK, SIG_I2C_SDA, SIG_I2C_SCL, SIG_LEDC5, SIG_LEDC4, SIG_LEDC3, SIG_LEDC2, SIG_LEDC1, SIG_LEDC0, SIG_U1TXD, SIG_U0TXD}),
    .F0_ES_GPIO(1'b1), .F0_OUT(1'b0), .F0_OE(1'b0), .F2_OUT(FSPI_OUT[5]), .F2_OE(FSPI_OE[5]),
    .ENTRADA(directa10), .PAD_OUT(PAD_OUT[10]));
  PadGPIO PAD11 (
    .PAD_IN(PAD_IN[11]), .OPEN_DRAIN(CFG_PIN2[5]), .OUT_CFG(CFG_SALIDA5[21:11]),
    .IOMUX_CFG(CFG_IOMUX1[27:23]), .GPIO_OUT(GPIO_OUT[11]), .GPIO_EN(GPIO_ENABLE[11]),
    .SIGS({3'b000, SIG_FSPICS0, SIG_FSPID, SIG_FSPICLK, SIG_I2C_SDA, SIG_I2C_SCL, SIG_LEDC5, SIG_LEDC4, SIG_LEDC3, SIG_LEDC2, SIG_LEDC1, SIG_LEDC0, SIG_U1TXD, SIG_U0TXD}),
    .F0_ES_GPIO(1'b1), .F0_OUT(1'b0), .F0_OE(1'b0), .F2_OUT(1'b0), .F2_OE(1'b0), .ENTRADA(directa11),
    .PAD_OUT(PAD_OUT[11]));
  PadGPIO PAD12 (
    .PAD_IN(PAD_IN[12]), .OPEN_DRAIN(CFG_PIN2[11]), .OUT_CFG(CFG_SALIDA6[10:0]),
    .IOMUX_CFG({CFG_IOMUX2[2:0], CFG_IOMUX1[29:28]}), .GPIO_OUT(GPIO_OUT[12]), .GPIO_EN(GPIO_ENABLE[12]),
    .SIGS({3'b000, SIG_FSPICS0, SIG_FSPID, SIG_FSPICLK, SIG_I2C_SDA, SIG_I2C_SCL, SIG_LEDC5, SIG_LEDC4, SIG_LEDC3, SIG_LEDC2, SIG_LEDC1, SIG_LEDC0, SIG_U1TXD, SIG_U0TXD}),
    .F0_ES_GPIO(1'b0), .F0_OUT(1'b0), .F0_OE(1'b0), .F2_OUT(1'b0), .F2_OE(1'b0), .ENTRADA(directa12),
    .PAD_OUT(PAD_OUT[12]));
  PadGPIO PAD13 (
    .PAD_IN(PAD_IN[13]), .OPEN_DRAIN(CFG_PIN2[17]), .OUT_CFG(CFG_SALIDA6[21:11]),
    .IOMUX_CFG(CFG_IOMUX2[7:3]), .GPIO_OUT(GPIO_OUT[13]), .GPIO_EN(GPIO_ENABLE[13]),
    .SIGS({3'b000, SIG_FSPICS0, SIG_FSPID, SIG_FSPICLK, SIG_I2C_SDA, SIG_I2C_SCL, SIG_LEDC5, SIG_LEDC4, SIG_LEDC3, SIG_LEDC2, SIG_LEDC1, SIG_LEDC0, SIG_U1TXD, SIG_U0TXD}),
    .F0_ES_GPIO(1'b0), .F0_OUT(1'b0), .F0_OE(1'b0), .F2_OUT(1'b0), .F2_OE(1'b0), .ENTRADA(directa13),
    .PAD_OUT(PAD_OUT[13]));
  PadGPIO PAD14 (
    .PAD_IN(PAD_IN[14]), .OPEN_DRAIN(CFG_PIN2[23]), .OUT_CFG(CFG_SALIDA7[10:0]),
    .IOMUX_CFG(CFG_IOMUX2[12:8]), .GPIO_OUT(GPIO_OUT[14]), .GPIO_EN(GPIO_ENABLE[14]),
    .SIGS({3'b000, SIG_FSPICS0, SIG_FSPID, SIG_FSPICLK, SIG_I2C_SDA, SIG_I2C_SCL, SIG_LEDC5, SIG_LEDC4, SIG_LEDC3, SIG_LEDC2, SIG_LEDC1, SIG_LEDC0, SIG_U1TXD, SIG_U0TXD}),
    .F0_ES_GPIO(1'b0), .F0_OUT(1'b0), .F0_OE(1'b0), .F2_OUT(1'b0), .F2_OE(1'b0), .ENTRADA(directa14),
    .PAD_OUT(PAD_OUT[14]));
  PadGPIO PAD15 (
    .PAD_IN(PAD_IN[15]), .OPEN_DRAIN(CFG_PIN2[29]), .OUT_CFG(CFG_SALIDA7[21:11]),
    .IOMUX_CFG(CFG_IOMUX2[17:13]), .GPIO_OUT(GPIO_OUT[15]), .GPIO_EN(GPIO_ENABLE[15]),
    .SIGS({3'b000, SIG_FSPICS0, SIG_FSPID, SIG_FSPICLK, SIG_I2C_SDA, SIG_I2C_SCL, SIG_LEDC5, SIG_LEDC4, SIG_LEDC3, SIG_LEDC2, SIG_LEDC1, SIG_LEDC0, SIG_U1TXD, SIG_U0TXD}),
    .F0_ES_GPIO(1'b0), .F0_OUT(1'b0), .F0_OE(1'b0), .F2_OUT(1'b0), .F2_OE(1'b0), .ENTRADA(directa15),
    .PAD_OUT(PAD_OUT[15]));
  PadGPIO PAD16 (
    .PAD_IN(PAD_IN[16]), .OPEN_DRAIN(CFG_PIN3[5]), .OUT_CFG(CFG_SALIDA8[10:0]),
    .IOMUX_CFG(CFG_IOMUX2[22:18]), .GPIO_OUT(GPIO_OUT[16]), .GPIO_EN(GPIO_ENABLE[16]),
    .SIGS({3'b000, SIG_FSPICS0, SIG_FSPID, SIG_FSPICLK, SIG_I2C_SDA, SIG_I2C_SCL, SIG_LEDC5, SIG_LEDC4, SIG_LEDC3, SIG_LEDC2, SIG_LEDC1, SIG_LEDC0, SIG_U1TXD, SIG_U0TXD}),
    .F0_ES_GPIO(1'b0), .F0_OUT(1'b0), .F0_OE(1'b0), .F2_OUT(1'b0), .F2_OE(1'b0), .ENTRADA(directa16),
    .PAD_OUT(PAD_OUT[16]));
  PadGPIO PAD17 (
    .PAD_IN(PAD_IN[17]), .OPEN_DRAIN(CFG_PIN3[11]), .OUT_CFG(CFG_SALIDA8[21:11]),
    .IOMUX_CFG(CFG_IOMUX2[27:23]), .GPIO_OUT(GPIO_OUT[17]), .GPIO_EN(GPIO_ENABLE[17]),
    .SIGS({3'b000, SIG_FSPICS0, SIG_FSPID, SIG_FSPICLK, SIG_I2C_SDA, SIG_I2C_SCL, SIG_LEDC5, SIG_LEDC4, SIG_LEDC3, SIG_LEDC2, SIG_LEDC1, SIG_LEDC0, SIG_U1TXD, SIG_U0TXD}),
    .F0_ES_GPIO(1'b0), .F0_OUT(1'b0), .F0_OE(1'b0), .F2_OUT(1'b0), .F2_OE(1'b0), .ENTRADA(directa17),
    .PAD_OUT(PAD_OUT[17]));
  PadGPIO PAD18 (
    .PAD_IN(PAD_IN[18]), .OPEN_DRAIN(CFG_PIN3[17]), .OUT_CFG(CFG_SALIDA9[10:0]),
    .IOMUX_CFG({CFG_IOMUX3[2:0], CFG_IOMUX2[29:28]}), .GPIO_OUT(GPIO_OUT[18]), .GPIO_EN(GPIO_ENABLE[18]),
    .SIGS({3'b000, SIG_FSPICS0, SIG_FSPID, SIG_FSPICLK, SIG_I2C_SDA, SIG_I2C_SCL, SIG_LEDC5, SIG_LEDC4, SIG_LEDC3, SIG_LEDC2, SIG_LEDC1, SIG_LEDC0, SIG_U1TXD, SIG_U0TXD}),
    .F0_ES_GPIO(1'b1), .F0_OUT(1'b0), .F0_OE(1'b0), .F2_OUT(1'b0), .F2_OE(1'b0), .ENTRADA(directa18),
    .PAD_OUT(PAD_OUT[18]));
  PadGPIO PAD19 (
    .PAD_IN(PAD_IN[19]), .OPEN_DRAIN(CFG_PIN3[23]), .OUT_CFG(CFG_SALIDA9[21:11]),
    .IOMUX_CFG(CFG_IOMUX3[7:3]), .GPIO_OUT(GPIO_OUT[19]), .GPIO_EN(GPIO_ENABLE[19]),
    .SIGS({3'b000, SIG_FSPICS0, SIG_FSPID, SIG_FSPICLK, SIG_I2C_SDA, SIG_I2C_SCL, SIG_LEDC5, SIG_LEDC4, SIG_LEDC3, SIG_LEDC2, SIG_LEDC1, SIG_LEDC0, SIG_U1TXD, SIG_U0TXD}),
    .F0_ES_GPIO(1'b1), .F0_OUT(1'b0), .F0_OE(1'b0), .F2_OUT(1'b0), .F2_OE(1'b0), .ENTRADA(directa19),
    .PAD_OUT(PAD_OUT[19]));
  PadGPIO PAD20 (
    .PAD_IN(PAD_IN[20]), .OPEN_DRAIN(CFG_PIN3[29]), .OUT_CFG(CFG_SALIDA10[10:0]),
    .IOMUX_CFG(CFG_IOMUX3[12:8]), .GPIO_OUT(GPIO_OUT[20]), .GPIO_EN(GPIO_ENABLE[20]),
    .SIGS({3'b000, SIG_FSPICS0, SIG_FSPID, SIG_FSPICLK, SIG_I2C_SDA, SIG_I2C_SCL, SIG_LEDC5, SIG_LEDC4, SIG_LEDC3, SIG_LEDC2, SIG_LEDC1, SIG_LEDC0, SIG_U1TXD, SIG_U0TXD}),
    .F0_ES_GPIO(1'b0), .F0_OUT(1'b0), .F0_OE(1'b0), .F2_OUT(1'b0), .F2_OE(1'b0), .ENTRADA(directa20),
    .PAD_OUT(PAD_OUT[20]));
  assign PCPU_INT = STATUS & {{10{1'b0}}, CFG_PIN4[9], CFG_PIN4[3], CFG_PIN3[27], CFG_PIN3[21], CFG_PIN3[15], CFG_PIN3[9], CFG_PIN3[3], CFG_PIN2[27], CFG_PIN2[21], CFG_PIN2[15], CFG_PIN2[9], CFG_PIN2[3], CFG_PIN1[27], CFG_PIN1[21], CFG_PIN1[15], CFG_PIN1[9], CFG_PIN1[3], CFG_PIN0[28], CFG_PIN0[22], CFG_PIN0[16], CFG_PIN0[10], CFG_PIN0[4]};  // AND_Gate and_20, 32 bits wide
  assign PCPU_NMI_INT = STATUS & {{10{1'b0}}, CFG_PIN4[10], CFG_PIN4[4], CFG_PIN3[28], CFG_PIN3[22], CFG_PIN3[16], CFG_PIN3[10], CFG_PIN3[4], CFG_PIN2[28], CFG_PIN2[22], CFG_PIN2[16], CFG_PIN2[10], CFG_PIN2[4], CFG_PIN1[28], CFG_PIN1[22], CFG_PIN1[16], CFG_PIN1[10], CFG_PIN1[4], CFG_PIN0[29], CFG_PIN0[23], CFG_PIN0[17], CFG_PIN0[11], CFG_PIN0[5]};  // AND_Gate and_21, 32 bits wide
  Multiplexer #(.select(1), .width(1), .enable("false")) multiplexer_6 (
    .in0(1'b1), .in1(in20), .out(directo_U0RXD), .sel(eq254));
  Multiplexer #(.select(1), .width(1), .enable("false")) multiplexer_7 (
    .in0(1'b0), .in1(in2), .out(directo_FSPIQ), .sel(eq259));
  PadGPIO PAD21 (
    .PAD_IN(PAD_IN[21]), .OPEN_DRAIN(CFG_PIN4[5]), .OUT_CFG(CFG_SALIDA10[21:11]),
    .IOMUX_CFG(CFG_IOMUX3[17:13]), .GPIO_OUT(GPIO_OUT[21]), .GPIO_EN(GPIO_ENABLE[21]),
    .SIGS({3'b000, SIG_FSPICS0, SIG_FSPID, SIG_FSPICLK, SIG_I2C_SDA, SIG_I2C_SCL, SIG_LEDC5, SIG_LEDC4, SIG_LEDC3, SIG_LEDC2, SIG_LEDC1, SIG_LEDC0, SIG_U1TXD, SIG_U0TXD}),
    .F0_ES_GPIO(1'b0), .F0_OUT(SIG_U0TXD), .F0_OE(1'b1), .F2_OUT(1'b0), .F2_OE(1'b0), .ENTRADA(directa21),
    .PAD_OUT(PAD_OUT[21]));
  assign not230 = ~{CFG_PIN4[6], CFG_PIN4[0], CFG_PIN3[24], CFG_PIN3[18], CFG_PIN3[12], CFG_PIN3[6], CFG_PIN3[0], CFG_PIN2[24], CFG_PIN2[18], CFG_PIN2[12], CFG_PIN2[6], CFG_PIN2[0], CFG_PIN1[24], CFG_PIN1[18], CFG_PIN1[12], CFG_PIN1[6], CFG_PIN1[0], CFG_PIN0[25], CFG_PIN0[19], CFG_PIN0[13], CFG_PIN0[7], CFG_PIN0[1]};  // NOT_Gate not_9, 22 bits wide
  assign not231 = ~{CFG_PIN4[7], CFG_PIN4[1], CFG_PIN3[25], CFG_PIN3[19], CFG_PIN3[13], CFG_PIN3[7], CFG_PIN3[1], CFG_PIN2[25], CFG_PIN2[19], CFG_PIN2[13], CFG_PIN2[7], CFG_PIN2[1], CFG_PIN1[25], CFG_PIN1[19], CFG_PIN1[13], CFG_PIN1[7], CFG_PIN1[1], CFG_PIN0[26], CFG_PIN0[20], CFG_PIN0[14], CFG_PIN0[8], CFG_PIN0[2]};  // NOT_Gate not_10, 22 bits wide
  assign not232 = ~{CFG_PIN4[8], CFG_PIN4[2], CFG_PIN3[26], CFG_PIN3[20], CFG_PIN3[14], CFG_PIN3[8], CFG_PIN3[2], CFG_PIN2[26], CFG_PIN2[20], CFG_PIN2[14], CFG_PIN2[8], CFG_PIN2[2], CFG_PIN1[26], CFG_PIN1[20], CFG_PIN1[14], CFG_PIN1[8], CFG_PIN1[2], CFG_PIN0[27], CFG_PIN0[21], CFG_PIN0[15], CFG_PIN0[9], CFG_PIN0[3]};  // NOT_Gate not_11, 22 bits wide
  assign and240 = {dato_escrito[31:15], CFG_IOMUX0_nuevo[29:27], dato_escrito[11], CFG_SALIDA0_nuevo[21], CFG_IOMUX0_nuevo[31:30], CFG_PIN0_nuevo[25], CFG_ENTRADA0_nuevo} & 32'h3fffff;  // AND_Gate and_22, 32 bits wide
  assign and242 = {dato_escrito[31:15], CFG_IOMUX0_nuevo[29:27], dato_escrito[11], CFG_SALIDA0_nuevo[21], CFG_IOMUX0_nuevo[31:30], CFG_PIN0_nuevo[25], CFG_ENTRADA0_nuevo} & 32'h3fffff;  // AND_Gate and_23, 32 bits wide
  assign not245 = ~{dato_escrito[31:15], CFG_IOMUX0_nuevo[29:27], dato_escrito[11], CFG_SALIDA0_nuevo[21], CFG_IOMUX0_nuevo[31:30], CFG_PIN0_nuevo[25], CFG_ENTRADA0_nuevo};  // NOT_Gate not_12, 32 bits wide
  xor xor_19 (xor253, matriz_U0RXD, CFG_ENTRADA0[5]);
  assign and268 = registros_gpio_valor & rep267;  // AND_Gate and_24, 32 bits wide
  xor xor_20 (xor255, matriz_U1RXD, CFG_ENTRADA0[12]);
  xor xor_21 (xor256, matriz_I2C_SCL, CFG_ENTRADA0[19]);
  xor xor_22 (xor257, matriz_I2C_SDA, CFG_ENTRADA0[26]);
  assign and264 = {dato_escrito[31:15], CFG_IOMUX0_nuevo[29:27], dato_escrito[11], CFG_SALIDA0_nuevo[21], CFG_IOMUX0_nuevo[31:30], CFG_PIN0_nuevo[25], CFG_ENTRADA0_nuevo} & registros_gpio_bits_rw;  // AND_Gate and_25, 32 bits wide
  assign and286 = {dato_escrito[31:15], CFG_IOMUX0_nuevo[29:27], dato_escrito[11], CFG_SALIDA0_nuevo[21], CFG_IOMUX0_nuevo[31:30], CFG_PIN0_nuevo[25], CFG_ENTRADA0_nuevo} & registros_iomux_bits_rw;  // AND_Gate and_26, 32 bits wide
  assign and290 = registros_iomux_valor & rep289;  // AND_Gate and_27, 32 bits wide
  and and_28 (r004, SEL, pag_0, lin_1);
  and and_29 (r008, SEL, pag_0, lin_2);
  and and_30 (r00C, SEL, pag_0, lin_3);
  and and_31 (r020, SEL, pag_0, lin_8);
  and and_32 (r024, SEL, pag_0, lin_9);
  and and_33 (r028, SEL, pag_0, lin_10);
  and and_34 (r074, SEL, pag_0, lin_29);
  and and_35 (r078, SEL, pag_0, lin_30);
  and and_36 (r07C, SEL, pag_0, lin_31);
  and and_37 (r080, SEL, pag_1, lin_0);
  and and_38 (r084, SEL, pag_1, lin_1);
  and and_39 (r088, SEL, pag_1, lin_2);
  and and_40 (r08C, SEL, pag_1, lin_3);
  and and_41 (r090, SEL, pag_1, lin_4);
  and and_42 (r094, SEL, pag_1, lin_5);
  and and_43 (r098, SEL, pag_1, lin_6);
  and and_44 (r09C, SEL, pag_1, lin_7);
  and and_45 (r0A0, SEL, pag_1, lin_8);
  and and_46 (r0A4, SEL, pag_1, lin_9);
  and and_47 (r0A8, SEL, pag_1, lin_10);
  and and_48 (r0AC, SEL, pag_1, lin_11);
  and and_49 (r0B0, SEL, pag_1, lin_12);
  and and_50 (r0B4, SEL, pag_1, lin_13);
  and and_51 (r0B8, SEL, pag_1, lin_14);
  and and_52 (r0BC, SEL, pag_1, lin_15);
  and and_53 (r0C0, SEL, pag_1, lin_16);
  and and_54 (r0C4, SEL, pag_1, lin_17);
  and and_55 (r0C8, SEL, pag_1, lin_18);
  and and_56 (r554, SEL, pag_10, lin_21);
  and and_57 (r558, SEL, pag_10, lin_22);
  and and_58 (r55C, SEL, pag_10, lin_23);
  and and_59 (r560, SEL, pag_10, lin_24);
  and and_60 (r564, SEL, pag_10, lin_25);
  and and_61 (r568, SEL, pag_10, lin_26);
  and and_62 (r56C, SEL, pag_10, lin_27);
  and and_63 (r570, SEL, pag_10, lin_28);
  and and_64 (r574, SEL, pag_10, lin_29);
  and and_65 (r578, SEL, pag_10, lin_30);
  and and_66 (r57C, SEL, pag_10, lin_31);
  and and_67 (r580, SEL, pag_11, lin_0);
  and and_68 (r584, SEL, pag_11, lin_1);
  and and_69 (r588, SEL, pag_11, lin_2);
  and and_70 (r58C, SEL, pag_11, lin_3);
  and and_71 (r590, SEL, pag_11, lin_4);
  and and_72 (r594, SEL, pag_11, lin_5);
  and and_73 (r598, SEL, pag_11, lin_6);
  and and_74 (r59C, SEL, pag_11, lin_7);
  and and_75 (r5A0, SEL, pag_11, lin_8);
  and and_76 (r5A4, SEL, pag_11, lin_9);
  and and_77 (r5A8, SEL, pag_11, lin_10);
  and and_78 (r16C, SEL, pag_2, lin_27);
  and and_79 (r178, SEL, pag_2, lin_30);
  and and_80 (r228, SEL, pag_4, lin_10);
  and and_81 (r22C, SEL, pag_4, lin_11);
  and and_82 (r254, SEL, pag_4, lin_21);
  and and_83 (iomux_r004, SEL_IOMUX, pag_0, lin_1);
  and and_84 (iomux_r008, SEL_IOMUX, pag_0, lin_2);
  and and_85 (iomux_r00C, SEL_IOMUX, pag_0, lin_3);
  and and_86 (iomux_r010, SEL_IOMUX, pag_0, lin_4);
  and and_87 (iomux_r014, SEL_IOMUX, pag_0, lin_5);
  and and_88 (iomux_r018, SEL_IOMUX, pag_0, lin_6);
  and and_89 (iomux_r01C, SEL_IOMUX, pag_0, lin_7);
  and and_90 (iomux_r020, SEL_IOMUX, pag_0, lin_8);
  and and_91 (iomux_r024, SEL_IOMUX, pag_0, lin_9);
  and and_92 (iomux_r028, SEL_IOMUX, pag_0, lin_10);
  and and_93 (iomux_r02C, SEL_IOMUX, pag_0, lin_11);
  and and_94 (iomux_r030, SEL_IOMUX, pag_0, lin_12);
  and and_95 (iomux_r034, SEL_IOMUX, pag_0, lin_13);
  and and_96 (iomux_r038, SEL_IOMUX, pag_0, lin_14);
  and and_97 (iomux_r03C, SEL_IOMUX, pag_0, lin_15);
  and and_98 (iomux_r040, SEL_IOMUX, pag_0, lin_16);
  and and_99 (iomux_r044, SEL_IOMUX, pag_0, lin_17);
  and and_100 (iomux_r048, SEL_IOMUX, pag_0, lin_18);
  and and_101 (iomux_r04C, SEL_IOMUX, pag_0, lin_19);
  and and_102 (iomux_r050, SEL_IOMUX, pag_0, lin_20);
  and and_103 (iomux_r054, SEL_IOMUX, pag_0, lin_21);
  and and_104 (r044, SEL, pag_0, lin_17);
  and and_105 (r048, SEL, pag_0, lin_18);
  and and_106 (r04C, SEL, pag_0, lin_19);
  Multiplexer #(.select(1), .width(1), .enable("false")) multiplexer_8 (
    .in0(1'b1), .in1(xor255), .out(U1RXD), .sel(CFG_ENTRADA0[13]));
  Multiplexer #(.select(1), .width(1), .enable("false")) multiplexer_9 (
    .in0(1'b1), .in1(xor256), .out(I2C_SCL), .sel(CFG_ENTRADA0[20]));
  Multiplexer #(.select(1), .width(1), .enable("false")) multiplexer_10 (
    .in0(1'b1), .in1(xor257), .out(I2C_SDA), .sel(CFG_ENTRADA0[27]));
  and and_107 (r03C, SEL, pag_0, lin_15);
  and and_108 (r038, SEL, pag_0, lin_14);
  and and_109 (r14C, SEL, pag_2, lin_19);
  and and_110 (r05C, SEL, pag_0, lin_23);
  and and_111 (r060, SEL, pag_0, lin_24);
  and and_112 (iomux_r058, SEL_IOMUX, pag_0, lin_22);
  assign int_subida = not232 & {CFG_PIN4[6], CFG_PIN4[0], CFG_PIN3[24], CFG_PIN3[18], CFG_PIN3[12], CFG_PIN3[6], CFG_PIN3[0], CFG_PIN2[24], CFG_PIN2[18], CFG_PIN2[12], CFG_PIN2[6], CFG_PIN2[0], CFG_PIN1[24], CFG_PIN1[18], CFG_PIN1[12], CFG_PIN1[6], CFG_PIN1[0], CFG_PIN0[25], CFG_PIN0[19], CFG_PIN0[13], CFG_PIN0[7], CFG_PIN0[1]};  // AND_Gate and_113, 22 bits wide
  assign int_bajada = not232 & {CFG_PIN4[7], CFG_PIN4[1], CFG_PIN3[25], CFG_PIN3[19], CFG_PIN3[13], CFG_PIN3[7], CFG_PIN3[1], CFG_PIN2[25], CFG_PIN2[19], CFG_PIN2[13], CFG_PIN2[7], CFG_PIN2[1], CFG_PIN1[25], CFG_PIN1[19], CFG_PIN1[13], CFG_PIN1[7], CFG_PIN1[1], CFG_PIN0[26], CFG_PIN0[20], CFG_PIN0[14], CFG_PIN0[8], CFG_PIN0[2]};  // AND_Gate and_114, 22 bits wide
  assign int_nivel_bajo = {CFG_PIN4[8], CFG_PIN4[2], CFG_PIN3[26], CFG_PIN3[20], CFG_PIN3[14], CFG_PIN3[8], CFG_PIN3[2], CFG_PIN2[26], CFG_PIN2[20], CFG_PIN2[14], CFG_PIN2[8], CFG_PIN2[2], CFG_PIN1[26], CFG_PIN1[20], CFG_PIN1[14], CFG_PIN1[8], CFG_PIN1[2], CFG_PIN0[27], CFG_PIN0[21], CFG_PIN0[15], CFG_PIN0[9], CFG_PIN0[3]} & not231 & not230;  // AND_Gate and_115, 22 bits wide
  assign int_nivel_alto = {CFG_PIN4[8], CFG_PIN4[2], CFG_PIN3[26], CFG_PIN3[20], CFG_PIN3[14], CFG_PIN3[8], CFG_PIN3[2], CFG_PIN2[26], CFG_PIN2[20], CFG_PIN2[14], CFG_PIN2[8], CFG_PIN2[2], CFG_PIN1[26], CFG_PIN1[20], CFG_PIN1[14], CFG_PIN1[8], CFG_PIN1[2], CFG_PIN0[27], CFG_PIN0[21], CFG_PIN0[15], CFG_PIN0[9], CFG_PIN0[3]} & not231 & {CFG_PIN4[6], CFG_PIN4[0], CFG_PIN3[24], CFG_PIN3[18], CFG_PIN3[12], CFG_PIN3[6], CFG_PIN3[0], CFG_PIN2[24], CFG_PIN2[18], CFG_PIN2[12], CFG_PIN2[6], CFG_PIN2[0], CFG_PIN1[24], CFG_PIN1[18], CFG_PIN1[12], CFG_PIN1[6], CFG_PIN1[0], CFG_PIN0[25], CFG_PIN0[19], CFG_PIN0[13], CFG_PIN0[7], CFG_PIN0[1]};  // AND_Gate and_116, 22 bits wide
  Comparator #(.width(32), .mode("unsigned")) comparator_3 (.a(PCPU_INT), .b({32{1'b0}}), .eq(eq249));  // open: gt, lt
  Comparator #(.width(32), .mode("unsigned")) comparator_4 (
    .a(PCPU_NMI_INT), .b({32{1'b0}}), .eq(eq251));  // open: gt, lt
  Multiplexer #(.select(1), .width(1), .enable("false")) multiplexer_11 (
    .in0(directo_U0RXD), .in1(xor253), .out(U0RXD), .sel(CFG_ENTRADA0[6]));
  Multiplexer #(.select(1), .width(1), .enable("false")) multiplexer_12 (
    .in0(directo_FSPIQ), .in1(xor258), .out(FSPIQ), .sel(CFG_ENTRADA1[6]));
  assign registros_gpio_a_guardar = and264 ^ registros_gpio_reset_rw;  // XOR_Gate xor_23, 32 bits wide
  and and_117 (iomux_r0FC, SEL_IOMUX, pag_1, lin_31);
  assign registros_iomux_a_guardar = and286 ^ registros_iomux_reset_rw;  // XOR_Gate xor_24, 32 bits wide
  and and_118 (esc_004, escribe, r004);
  and and_119 (esc_008, escribe, r008);
  and and_120 (esc_00C, escribe, r00C);
  and and_121 (esc_020, escribe, r020);
  and and_122 (esc_024, escribe, r024);
  and and_123 (esc_028, escribe, r028);
  and and_124 (CFG_PIN0_mascara[0], escribe, r074);
  and and_125 (CFG_PIN0_mascara[6], escribe, r078);
  and and_126 (CFG_PIN0_mascara[12], escribe, r07C);
  and and_127 (CFG_PIN0_mascara[18], escribe, r080);
  and and_128 (CFG_PIN0_mascara[24], escribe, r084);
  and and_129 (CFG_PIN0_mascara[30], escribe, r088);
  and and_130 (CFG_PIN1_mascara[5], escribe, r08C);
  and and_131 (CFG_PIN1_mascara[11], escribe, r090);
  and and_132 (CFG_PIN1_mascara[17], escribe, r094);
  and and_133 (CFG_PIN1_mascara[23], escribe, r098);
  and and_134 (CFG_PIN1_mascara[29], escribe, r09C);
  and and_135 (CFG_PIN2_mascara[5], escribe, r0A0);
  and and_136 (CFG_PIN2_mascara[11], escribe, r0A4);
  and and_137 (CFG_PIN2_mascara[17], escribe, r0A8);
  and and_138 (CFG_PIN2_mascara[23], escribe, r0AC);
  and and_139 (CFG_PIN2_mascara[29], escribe, r0B0);
  and and_140 (CFG_PIN3_mascara[5], escribe, r0B4);
  and and_141 (CFG_PIN3_mascara[11], escribe, r0B8);
  and and_142 (CFG_PIN3_mascara[17], escribe, r0BC);
  and and_143 (CFG_PIN3_mascara[23], escribe, r0C0);
  and and_144 (CFG_PIN3_mascara[29], escribe, r0C4);
  and and_145 (CFG_PIN4_mascara[5], escribe, r0C8);
  and and_146 (esc_554, escribe, r554);
  and and_147 (esc_558, escribe, r558);
  and and_148 (esc_55C, escribe, r55C);
  and and_149 (esc_560, escribe, r560);
  and and_150 (esc_564, escribe, r564);
  and and_151 (esc_568, escribe, r568);
  and and_152 (esc_56C, escribe, r56C);
  and and_153 (esc_570, escribe, r570);
  and and_154 (esc_574, escribe, r574);
  and and_155 (esc_578, escribe, r578);
  and and_156 (esc_57C, escribe, r57C);
  and and_157 (esc_580, escribe, r580);
  and and_158 (esc_584, escribe, r584);
  and and_159 (esc_588, escribe, r588);
  and and_160 (esc_58C, escribe, r58C);
  and and_161 (esc_590, escribe, r590);
  and and_162 (esc_594, escribe, r594);
  and and_163 (esc_598, escribe, r598);
  and and_164 (esc_59C, escribe, r59C);
  and and_165 (esc_5A0, escribe, r5A0);
  and and_166 (esc_5A4, escribe, r5A4);
  and and_167 (esc_5A8, escribe, r5A8);
  and and_168 (esc_16C, escribe, r16C);
  and and_169 (esc_178, escribe, r178);
  and and_170 (esc_228, escribe, r228);
  and and_171 (esc_22C, escribe, r22C);
  and and_172 (CFG_ENTRADA1_escribe, escribe, r254);
  and and_173 (esc_044, escribe, r044);
  and and_174 (esc_048, escribe, r048);
  and and_175 (esc_04C, escribe, r04C);
  not not_13 (IRQ, eq249);
  not not_14 (IRQ_NMI, eq251);
  assign rep269 = {{31{r004}}, r004};  // Bit_Extender bit_extender_6
  assign rep271 = {{31{r020}}, r020};  // Bit_Extender bit_extender_7
  and and_176 (iomux_esc_004, escribe, iomux_r004);
  and and_177 (iomux_esc_008, escribe, iomux_r008);
  and and_178 (iomux_esc_00C, escribe, iomux_r00C);
  and and_179 (iomux_esc_010, escribe, iomux_r010);
  and and_180 (iomux_esc_014, escribe, iomux_r014);
  and and_181 (iomux_esc_018, escribe, iomux_r018);
  and and_182 (iomux_esc_01C, escribe, iomux_r01C);
  and and_183 (iomux_esc_020, escribe, iomux_r020);
  and and_184 (iomux_esc_024, escribe, iomux_r024);
  and and_185 (iomux_esc_028, escribe, iomux_r028);
  and and_186 (iomux_esc_02C, escribe, iomux_r02C);
  and and_187 (iomux_esc_030, escribe, iomux_r030);
  and and_188 (iomux_esc_034, escribe, iomux_r034);
  and and_189 (iomux_esc_038, escribe, iomux_r038);
  and and_190 (iomux_esc_03C, escribe, iomux_r03C);
  and and_191 (iomux_esc_040, escribe, iomux_r040);
  and and_192 (iomux_esc_044, escribe, iomux_r044);
  and and_193 (iomux_esc_048, escribe, iomux_r048);
  and and_194 (iomux_esc_04C, escribe, iomux_r04C);
  and and_195 (iomux_esc_050, escribe, iomux_r050);
  and and_196 (iomux_esc_054, escribe, iomux_r054);
  and and_197 (iomux_esc_058, escribe, iomux_r058);
  assign and233 = flancos_subida & int_subida;  // AND_Gate and_198, 22 bits wide
  assign and234 = flancos_bajada & int_bajada;  // AND_Gate and_199, 22 bits wide
  assign and236 = not235 & int_nivel_bajo;  // AND_Gate and_200, 22 bits wide
  assign and237 = {in21, in20, in19, in18, in17, in16, in15, in14, in13, in12, in11, in10, in9, in8, in7, in6, in5, in4, in3, in2, in1, in0} & int_nivel_alto;  // AND_Gate and_201, 22 bits wide
  assign rep273 = {{31{r03C}}, r03C};  // Bit_Extender bit_extender_8
  assign rep275 = {{31{r038}}, r038};  // Bit_Extender bit_extender_9
  assign rep277 = {{31{r044}}, r044};  // Bit_Extender bit_extender_10
  assign rep279 = {{31{r14C}}, r14C};  // Bit_Extender bit_extender_11
  assign rep281 = {{31{r05C}}, r05C};  // Bit_Extender bit_extender_12
  assign rep283 = {{31{r060}}, r060};  // Bit_Extender bit_extender_13
  Multiplexer #(.select(1), .width(32), .enable("false")) multiplexer_13 (
    .in0({32{1'b0}}), .in1(32'h2006050), .out(mux291), .sel(iomux_r0FC));
  Multiplexer #(.select(1), .width(32), .enable("false")) multiplexer_14 (
    .in0(GPIO_OUT), .in1(and1), .out(mux2), .sel(esc_004));
  or or_4 (or8, esc_004, esc_008, esc_00C);
  Multiplexer #(.select(1), .width(32), .enable("false")) multiplexer_15 (
    .in0(GPIO_ENABLE), .in1(and9), .out(mux10), .sel(esc_020));
  or or_5 (or16, esc_020, esc_024, esc_028);
  assign CFG_PIN0_mascara[3:1] = {{2{CFG_PIN0_mascara[0]}}, CFG_PIN0_mascara[0]};  // Bit_Extender bit_extender_14
  assign CFG_PIN0_mascara[5:4] = {{1{CFG_PIN0_mascara[0]}}, CFG_PIN0_mascara[0]};  // Bit_Extender bit_extender_15
  assign CFG_PIN0_mascara[9:7] = {{2{CFG_PIN0_mascara[6]}}, CFG_PIN0_mascara[6]};  // Bit_Extender bit_extender_16
  assign CFG_PIN0_mascara[11:10] = {{1{CFG_PIN0_mascara[6]}}, CFG_PIN0_mascara[6]};  // Bit_Extender bit_extender_17
  assign CFG_PIN0_mascara[15:13] = {{2{CFG_PIN0_mascara[12]}}, CFG_PIN0_mascara[12]};  // Bit_Extender bit_extender_18
  assign CFG_PIN0_mascara[17:16] = {{1{CFG_PIN0_mascara[12]}}, CFG_PIN0_mascara[12]};  // Bit_Extender bit_extender_19
  assign CFG_PIN0_mascara[21:19] = {{2{CFG_PIN0_mascara[18]}}, CFG_PIN0_mascara[18]};  // Bit_Extender bit_extender_20
  assign CFG_PIN0_mascara[23:22] = {{1{CFG_PIN0_mascara[18]}}, CFG_PIN0_mascara[18]};  // Bit_Extender bit_extender_21
  assign CFG_PIN0_mascara[27:25] = {{2{CFG_PIN0_mascara[24]}}, CFG_PIN0_mascara[24]};  // Bit_Extender bit_extender_22
  assign CFG_PIN0_mascara[29:28] = {{1{CFG_PIN0_mascara[24]}}, CFG_PIN0_mascara[24]};  // Bit_Extender bit_extender_23
  or or_6 (CFG_PIN0_escribe, CFG_PIN0_mascara[0], CFG_PIN0_mascara[6], CFG_PIN0_mascara[12], CFG_PIN0_mascara[18], CFG_PIN0_mascara[24], CFG_PIN0_mascara[30]);
  assign CFG_PIN1_mascara[2:0] = {{2{CFG_PIN0_mascara[30]}}, CFG_PIN0_mascara[30]};  // Bit_Extender bit_extender_24
  assign CFG_PIN1_mascara[4:3] = {{1{CFG_PIN0_mascara[30]}}, CFG_PIN0_mascara[30]};  // Bit_Extender bit_extender_25
  assign CFG_PIN1_mascara[8:6] = {{2{CFG_PIN1_mascara[5]}}, CFG_PIN1_mascara[5]};  // Bit_Extender bit_extender_26
  assign CFG_PIN1_mascara[10:9] = {{1{CFG_PIN1_mascara[5]}}, CFG_PIN1_mascara[5]};  // Bit_Extender bit_extender_27
  assign CFG_PIN1_mascara[14:12] = {{2{CFG_PIN1_mascara[11]}}, CFG_PIN1_mascara[11]};  // Bit_Extender bit_extender_28
  assign CFG_PIN1_mascara[16:15] = {{1{CFG_PIN1_mascara[11]}}, CFG_PIN1_mascara[11]};  // Bit_Extender bit_extender_29
  assign CFG_PIN1_mascara[20:18] = {{2{CFG_PIN1_mascara[17]}}, CFG_PIN1_mascara[17]};  // Bit_Extender bit_extender_30
  assign CFG_PIN1_mascara[22:21] = {{1{CFG_PIN1_mascara[17]}}, CFG_PIN1_mascara[17]};  // Bit_Extender bit_extender_31
  assign CFG_PIN1_mascara[26:24] = {{2{CFG_PIN1_mascara[23]}}, CFG_PIN1_mascara[23]};  // Bit_Extender bit_extender_32
  assign CFG_PIN1_mascara[28:27] = {{1{CFG_PIN1_mascara[23]}}, CFG_PIN1_mascara[23]};  // Bit_Extender bit_extender_33
  or or_7 (CFG_PIN1_escribe, CFG_PIN0_mascara[30], CFG_PIN1_mascara[5], CFG_PIN1_mascara[11], CFG_PIN1_mascara[17], CFG_PIN1_mascara[23], CFG_PIN1_mascara[29]);
  assign CFG_PIN2_mascara[2:0] = {{2{CFG_PIN1_mascara[29]}}, CFG_PIN1_mascara[29]};  // Bit_Extender bit_extender_34
  assign CFG_PIN2_mascara[4:3] = {{1{CFG_PIN1_mascara[29]}}, CFG_PIN1_mascara[29]};  // Bit_Extender bit_extender_35
  assign CFG_PIN2_mascara[8:6] = {{2{CFG_PIN2_mascara[5]}}, CFG_PIN2_mascara[5]};  // Bit_Extender bit_extender_36
  assign CFG_PIN2_mascara[10:9] = {{1{CFG_PIN2_mascara[5]}}, CFG_PIN2_mascara[5]};  // Bit_Extender bit_extender_37
  assign CFG_PIN2_mascara[14:12] = {{2{CFG_PIN2_mascara[11]}}, CFG_PIN2_mascara[11]};  // Bit_Extender bit_extender_38
  assign CFG_PIN2_mascara[16:15] = {{1{CFG_PIN2_mascara[11]}}, CFG_PIN2_mascara[11]};  // Bit_Extender bit_extender_39
  assign CFG_PIN2_mascara[20:18] = {{2{CFG_PIN2_mascara[17]}}, CFG_PIN2_mascara[17]};  // Bit_Extender bit_extender_40
  assign CFG_PIN2_mascara[22:21] = {{1{CFG_PIN2_mascara[17]}}, CFG_PIN2_mascara[17]};  // Bit_Extender bit_extender_41
  assign CFG_PIN2_mascara[26:24] = {{2{CFG_PIN2_mascara[23]}}, CFG_PIN2_mascara[23]};  // Bit_Extender bit_extender_42
  assign CFG_PIN2_mascara[28:27] = {{1{CFG_PIN2_mascara[23]}}, CFG_PIN2_mascara[23]};  // Bit_Extender bit_extender_43
  or or_8 (CFG_PIN2_escribe, CFG_PIN1_mascara[29], CFG_PIN2_mascara[5], CFG_PIN2_mascara[11], CFG_PIN2_mascara[17], CFG_PIN2_mascara[23], CFG_PIN2_mascara[29]);
  assign CFG_PIN3_mascara[2:0] = {{2{CFG_PIN2_mascara[29]}}, CFG_PIN2_mascara[29]};  // Bit_Extender bit_extender_44
  assign CFG_PIN3_mascara[4:3] = {{1{CFG_PIN2_mascara[29]}}, CFG_PIN2_mascara[29]};  // Bit_Extender bit_extender_45
  assign CFG_PIN3_mascara[8:6] = {{2{CFG_PIN3_mascara[5]}}, CFG_PIN3_mascara[5]};  // Bit_Extender bit_extender_46
  assign CFG_PIN3_mascara[10:9] = {{1{CFG_PIN3_mascara[5]}}, CFG_PIN3_mascara[5]};  // Bit_Extender bit_extender_47
  assign CFG_PIN3_mascara[14:12] = {{2{CFG_PIN3_mascara[11]}}, CFG_PIN3_mascara[11]};  // Bit_Extender bit_extender_48
  assign CFG_PIN3_mascara[16:15] = {{1{CFG_PIN3_mascara[11]}}, CFG_PIN3_mascara[11]};  // Bit_Extender bit_extender_49
  assign CFG_PIN3_mascara[20:18] = {{2{CFG_PIN3_mascara[17]}}, CFG_PIN3_mascara[17]};  // Bit_Extender bit_extender_50
  assign CFG_PIN3_mascara[22:21] = {{1{CFG_PIN3_mascara[17]}}, CFG_PIN3_mascara[17]};  // Bit_Extender bit_extender_51
  assign CFG_PIN3_mascara[26:24] = {{2{CFG_PIN3_mascara[23]}}, CFG_PIN3_mascara[23]};  // Bit_Extender bit_extender_52
  assign CFG_PIN3_mascara[28:27] = {{1{CFG_PIN3_mascara[23]}}, CFG_PIN3_mascara[23]};  // Bit_Extender bit_extender_53
  or or_9 (CFG_PIN3_escribe, CFG_PIN2_mascara[29], CFG_PIN3_mascara[5], CFG_PIN3_mascara[11], CFG_PIN3_mascara[17], CFG_PIN3_mascara[23], CFG_PIN3_mascara[29]);
  assign CFG_PIN4_mascara[2:0] = {{2{CFG_PIN3_mascara[29]}}, CFG_PIN3_mascara[29]};  // Bit_Extender bit_extender_54
  assign CFG_PIN4_mascara[4:3] = {{1{CFG_PIN3_mascara[29]}}, CFG_PIN3_mascara[29]};  // Bit_Extender bit_extender_55
  assign CFG_PIN4_mascara[8:6] = {{2{CFG_PIN4_mascara[5]}}, CFG_PIN4_mascara[5]};  // Bit_Extender bit_extender_56
  assign CFG_PIN4_mascara[10:9] = {{1{CFG_PIN4_mascara[5]}}, CFG_PIN4_mascara[5]};  // Bit_Extender bit_extender_57
  or or_10 (CFG_PIN4_escribe, CFG_PIN3_mascara[29], CFG_PIN4_mascara[5]);
  assign CFG_SALIDA0_mascara[10:0] = {{10{esc_554}}, esc_554};  // Bit_Extender bit_extender_58
  assign CFG_SALIDA0_mascara[21:11] = {{10{esc_558}}, esc_558};  // Bit_Extender bit_extender_59
  or or_11 (CFG_SALIDA0_escribe, esc_554, esc_558);
  assign CFG_SALIDA1_mascara[10:0] = {{10{esc_55C}}, esc_55C};  // Bit_Extender bit_extender_60
  assign CFG_SALIDA1_mascara[21:11] = {{10{esc_560}}, esc_560};  // Bit_Extender bit_extender_61
  or or_12 (CFG_SALIDA1_escribe, esc_55C, esc_560);
  assign CFG_SALIDA2_mascara[10:0] = {{10{esc_564}}, esc_564};  // Bit_Extender bit_extender_62
  assign CFG_SALIDA2_mascara[21:11] = {{10{esc_568}}, esc_568};  // Bit_Extender bit_extender_63
  or or_13 (CFG_SALIDA2_escribe, esc_564, esc_568);
  assign CFG_SALIDA3_mascara[10:0] = {{10{esc_56C}}, esc_56C};  // Bit_Extender bit_extender_64
  assign CFG_SALIDA3_mascara[21:11] = {{10{esc_570}}, esc_570};  // Bit_Extender bit_extender_65
  or or_14 (CFG_SALIDA3_escribe, esc_56C, esc_570);
  assign CFG_SALIDA4_mascara[10:0] = {{10{esc_574}}, esc_574};  // Bit_Extender bit_extender_66
  assign CFG_SALIDA4_mascara[21:11] = {{10{esc_578}}, esc_578};  // Bit_Extender bit_extender_67
  or or_15 (CFG_SALIDA4_escribe, esc_574, esc_578);
  assign CFG_SALIDA5_mascara[10:0] = {{10{esc_57C}}, esc_57C};  // Bit_Extender bit_extender_68
  assign CFG_SALIDA5_mascara[21:11] = {{10{esc_580}}, esc_580};  // Bit_Extender bit_extender_69
  or or_16 (CFG_SALIDA5_escribe, esc_57C, esc_580);
  assign CFG_SALIDA6_mascara[10:0] = {{10{esc_584}}, esc_584};  // Bit_Extender bit_extender_70
  assign CFG_SALIDA6_mascara[21:11] = {{10{esc_588}}, esc_588};  // Bit_Extender bit_extender_71
  or or_17 (CFG_SALIDA6_escribe, esc_584, esc_588);
  assign CFG_SALIDA7_mascara[10:0] = {{10{esc_58C}}, esc_58C};  // Bit_Extender bit_extender_72
  assign CFG_SALIDA7_mascara[21:11] = {{10{esc_590}}, esc_590};  // Bit_Extender bit_extender_73
  or or_18 (CFG_SALIDA7_escribe, esc_58C, esc_590);
  assign CFG_SALIDA8_mascara[10:0] = {{10{esc_594}}, esc_594};  // Bit_Extender bit_extender_74
  assign CFG_SALIDA8_mascara[21:11] = {{10{esc_598}}, esc_598};  // Bit_Extender bit_extender_75
  or or_19 (CFG_SALIDA8_escribe, esc_594, esc_598);
  assign CFG_SALIDA9_mascara[10:0] = {{10{esc_59C}}, esc_59C};  // Bit_Extender bit_extender_76
  assign CFG_SALIDA9_mascara[21:11] = {{10{esc_5A0}}, esc_5A0};  // Bit_Extender bit_extender_77
  or or_20 (CFG_SALIDA9_escribe, esc_59C, esc_5A0);
  assign CFG_SALIDA10_mascara[10:0] = {{10{esc_5A4}}, esc_5A4};  // Bit_Extender bit_extender_78
  assign CFG_SALIDA10_mascara[21:11] = {{10{esc_5A8}}, esc_5A8};  // Bit_Extender bit_extender_79
  or or_21 (CFG_SALIDA10_escribe, esc_5A4, esc_5A8);
  assign CFG_ENTRADA0_mascara[6:0] = {{6{esc_16C}}, esc_16C};  // Bit_Extender bit_extender_80
  assign CFG_ENTRADA0_mascara[13:7] = {{6{esc_178}}, esc_178};  // Bit_Extender bit_extender_81
  assign CFG_ENTRADA0_mascara[20:14] = {{6{esc_228}}, esc_228};  // Bit_Extender bit_extender_82
  assign CFG_ENTRADA0_mascara[27:21] = {{6{esc_22C}}, esc_22C};  // Bit_Extender bit_extender_83
  or or_22 (CFG_ENTRADA0_escribe, esc_16C, esc_178, esc_228, esc_22C);
  assign CFG_ENTRADA1_mascara = {{6{CFG_ENTRADA1_escribe}}, CFG_ENTRADA1_escribe};  // Bit_Extender bit_extender_84
  assign CFG_IOMUX0_mascara[1:0] = {{1{iomux_esc_004}}, iomux_esc_004};  // Bit_Extender bit_extender_85
  assign CFG_IOMUX0_mascara[4:2] = {{2{iomux_esc_004}}, iomux_esc_004};  // Bit_Extender bit_extender_86
  assign CFG_IOMUX0_mascara[6:5] = {{1{iomux_esc_008}}, iomux_esc_008};  // Bit_Extender bit_extender_87
  assign CFG_IOMUX0_mascara[9:7] = {{2{iomux_esc_008}}, iomux_esc_008};  // Bit_Extender bit_extender_88
  assign CFG_IOMUX0_mascara[11:10] = {{1{iomux_esc_00C}}, iomux_esc_00C};  // Bit_Extender bit_extender_89
  assign CFG_IOMUX0_mascara[14:12] = {{2{iomux_esc_00C}}, iomux_esc_00C};  // Bit_Extender bit_extender_90
  assign CFG_IOMUX0_mascara[16:15] = {{1{iomux_esc_010}}, iomux_esc_010};  // Bit_Extender bit_extender_91
  assign CFG_IOMUX0_mascara[19:17] = {{2{iomux_esc_010}}, iomux_esc_010};  // Bit_Extender bit_extender_92
  assign CFG_IOMUX0_mascara[21:20] = {{1{iomux_esc_014}}, iomux_esc_014};  // Bit_Extender bit_extender_93
  assign CFG_IOMUX0_mascara[24:22] = {{2{iomux_esc_014}}, iomux_esc_014};  // Bit_Extender bit_extender_94
  assign CFG_IOMUX0_mascara[26:25] = {{1{iomux_esc_018}}, iomux_esc_018};  // Bit_Extender bit_extender_95
  assign CFG_IOMUX0_mascara[29:27] = {{2{iomux_esc_018}}, iomux_esc_018};  // Bit_Extender bit_extender_96
  assign CFG_IOMUX0_mascara[31:30] = {{1{iomux_esc_01C}}, iomux_esc_01C};  // Bit_Extender bit_extender_97
  or or_23 (CFG_IOMUX0_escribe, iomux_esc_004, iomux_esc_008, iomux_esc_00C, iomux_esc_010, iomux_esc_014, iomux_esc_018, iomux_esc_01C);
  assign CFG_IOMUX1_mascara[2:0] = {{2{iomux_esc_01C}}, iomux_esc_01C};  // Bit_Extender bit_extender_98
  assign CFG_IOMUX1_mascara[4:3] = {{1{iomux_esc_020}}, iomux_esc_020};  // Bit_Extender bit_extender_99
  assign CFG_IOMUX1_mascara[7:5] = {{2{iomux_esc_020}}, iomux_esc_020};  // Bit_Extender bit_extender_100
  assign CFG_IOMUX1_mascara[9:8] = {{1{iomux_esc_024}}, iomux_esc_024};  // Bit_Extender bit_extender_101
  assign CFG_IOMUX1_mascara[12:10] = {{2{iomux_esc_024}}, iomux_esc_024};  // Bit_Extender bit_extender_102
  assign CFG_IOMUX1_mascara[14:13] = {{1{iomux_esc_028}}, iomux_esc_028};  // Bit_Extender bit_extender_103
  assign CFG_IOMUX1_mascara[17:15] = {{2{iomux_esc_028}}, iomux_esc_028};  // Bit_Extender bit_extender_104
  assign CFG_IOMUX1_mascara[19:18] = {{1{iomux_esc_02C}}, iomux_esc_02C};  // Bit_Extender bit_extender_105
  assign CFG_IOMUX1_mascara[22:20] = {{2{iomux_esc_02C}}, iomux_esc_02C};  // Bit_Extender bit_extender_106
  assign CFG_IOMUX1_mascara[24:23] = {{1{iomux_esc_030}}, iomux_esc_030};  // Bit_Extender bit_extender_107
  assign CFG_IOMUX1_mascara[27:25] = {{2{iomux_esc_030}}, iomux_esc_030};  // Bit_Extender bit_extender_108
  assign CFG_IOMUX1_mascara[29:28] = {{1{iomux_esc_034}}, iomux_esc_034};  // Bit_Extender bit_extender_109
  or or_24 (CFG_IOMUX1_escribe, iomux_esc_01C, iomux_esc_020, iomux_esc_024, iomux_esc_028, iomux_esc_02C, iomux_esc_030, iomux_esc_034);
  assign CFG_IOMUX2_mascara[2:0] = {{2{iomux_esc_034}}, iomux_esc_034};  // Bit_Extender bit_extender_110
  assign CFG_IOMUX2_mascara[4:3] = {{1{iomux_esc_038}}, iomux_esc_038};  // Bit_Extender bit_extender_111
  assign CFG_IOMUX2_mascara[7:5] = {{2{iomux_esc_038}}, iomux_esc_038};  // Bit_Extender bit_extender_112
  assign CFG_IOMUX2_mascara[9:8] = {{1{iomux_esc_03C}}, iomux_esc_03C};  // Bit_Extender bit_extender_113
  assign CFG_IOMUX2_mascara[12:10] = {{2{iomux_esc_03C}}, iomux_esc_03C};  // Bit_Extender bit_extender_114
  assign CFG_IOMUX2_mascara[14:13] = {{1{iomux_esc_040}}, iomux_esc_040};  // Bit_Extender bit_extender_115
  assign CFG_IOMUX2_mascara[17:15] = {{2{iomux_esc_040}}, iomux_esc_040};  // Bit_Extender bit_extender_116
  assign CFG_IOMUX2_mascara[19:18] = {{1{iomux_esc_044}}, iomux_esc_044};  // Bit_Extender bit_extender_117
  assign CFG_IOMUX2_mascara[22:20] = {{2{iomux_esc_044}}, iomux_esc_044};  // Bit_Extender bit_extender_118
  assign CFG_IOMUX2_mascara[24:23] = {{1{iomux_esc_048}}, iomux_esc_048};  // Bit_Extender bit_extender_119
  assign CFG_IOMUX2_mascara[27:25] = {{2{iomux_esc_048}}, iomux_esc_048};  // Bit_Extender bit_extender_120
  assign CFG_IOMUX2_mascara[29:28] = {{1{iomux_esc_04C}}, iomux_esc_04C};  // Bit_Extender bit_extender_121
  or or_25 (CFG_IOMUX2_escribe, iomux_esc_034, iomux_esc_038, iomux_esc_03C, iomux_esc_040, iomux_esc_044, iomux_esc_048, iomux_esc_04C);
  assign CFG_IOMUX3_mascara[2:0] = {{2{iomux_esc_04C}}, iomux_esc_04C};  // Bit_Extender bit_extender_122
  assign CFG_IOMUX3_mascara[4:3] = {{1{iomux_esc_050}}, iomux_esc_050};  // Bit_Extender bit_extender_123
  assign CFG_IOMUX3_mascara[7:5] = {{2{iomux_esc_050}}, iomux_esc_050};  // Bit_Extender bit_extender_124
  assign CFG_IOMUX3_mascara[9:8] = {{1{iomux_esc_054}}, iomux_esc_054};  // Bit_Extender bit_extender_125
  assign CFG_IOMUX3_mascara[12:10] = {{2{iomux_esc_054}}, iomux_esc_054};  // Bit_Extender bit_extender_126
  assign CFG_IOMUX3_mascara[14:13] = {{1{iomux_esc_058}}, iomux_esc_058};  // Bit_Extender bit_extender_127
  assign CFG_IOMUX3_mascara[17:15] = {{2{iomux_esc_058}}, iomux_esc_058};  // Bit_Extender bit_extender_128
  or or_26 (CFG_IOMUX3_escribe, iomux_esc_04C, iomux_esc_050, iomux_esc_054, iomux_esc_058);
  assign eventos_pads = and233 | and234 | and236 | and237;  // OR_Gate or_27, 22 bits wide
  Multiplexer #(.select(1), .width(32), .enable("false")) multiplexer_16 (
    .in0(STATUS), .in1(and240), .out(mux241), .sel(esc_044));
  assign and270 = GPIO_OUT & rep269;  // AND_Gate and_202, 32 bits wide
  assign and272 = GPIO_ENABLE & rep271;  // AND_Gate and_203, 32 bits wide
  assign and274 = GPIO_IN & rep273;  // AND_Gate and_204, 32 bits wide
  assign and276 = STRAP & rep275;  // AND_Gate and_205, 32 bits wide
  assign and278 = STATUS & rep277;  // AND_Gate and_206, 32 bits wide
  assign and282 = PCPU_INT & rep281;  // AND_Gate and_207, 32 bits wide
  assign and284 = PCPU_NMI_INT & rep283;  // AND_Gate and_208, 32 bits wide
  assign or4 = mux2 | and3;  // OR_Gate or_28, 32 bits wide
  assign or12 = mux10 | and11;  // OR_Gate or_29, 32 bits wide
  assign eventos = {{10{1'b0}}, eventos_pads};  // Bit_Extender bit_extender_129
  assign or243 = mux241 | and242;  // OR_Gate or_30, 32 bits wide
  Multiplexer #(.select(1), .width(32), .enable("false")) multiplexer_17 (
    .in0(mux2), .in1(or4), .out(mux5), .sel(esc_008));
  Multiplexer #(.select(1), .width(32), .enable("false")) multiplexer_18 (
    .in0(mux10), .in1(or12), .out(mux13), .sel(esc_024));
  assign not27 = ~CFG_PIN0_mascara;  // NOT_Gate not_15, 31 bits wide
  assign and29 = {CFG_ENTRADA0_nuevo[23], CFG_IOMUX0_nuevo[29:28], CFG_IOMUX0_nuevo[31:30], CFG_PIN0_nuevo[25], CFG_ENTRADA0_nuevo[23], CFG_IOMUX0_nuevo[29:28], CFG_IOMUX0_nuevo[31:30], CFG_PIN0_nuevo[25], CFG_ENTRADA0_nuevo[23], CFG_IOMUX0_nuevo[29:28], CFG_IOMUX0_nuevo[31:30], CFG_PIN0_nuevo[25], CFG_ENTRADA0_nuevo[23], CFG_IOMUX0_nuevo[29:28], CFG_IOMUX0_nuevo[31:30], CFG_PIN0_nuevo[25], CFG_ENTRADA0_nuevo[23], CFG_IOMUX0_nuevo[29:28], CFG_IOMUX0_nuevo[31:30], CFG_PIN0_nuevo[25], CFG_ENTRADA0_nuevo[23]} & CFG_PIN0_mascara;  // AND_Gate and_209, 31 bits wide
  assign not40 = ~CFG_PIN1_mascara;  // NOT_Gate not_16, 30 bits wide
  assign and42 = {CFG_ENTRADA0_nuevo[23], CFG_IOMUX0_nuevo[29:28], CFG_IOMUX0_nuevo[31:30], CFG_PIN0_nuevo[25], CFG_ENTRADA0_nuevo[23], CFG_IOMUX0_nuevo[29:28], CFG_IOMUX0_nuevo[31:30], CFG_PIN0_nuevo[25], CFG_ENTRADA0_nuevo[23], CFG_IOMUX0_nuevo[29:28], CFG_IOMUX0_nuevo[31:30], CFG_PIN0_nuevo[25], CFG_ENTRADA0_nuevo[23], CFG_IOMUX0_nuevo[29:28], CFG_IOMUX0_nuevo[31:30], CFG_PIN0_nuevo[25], CFG_ENTRADA0_nuevo[23], CFG_IOMUX0_nuevo[29:28], CFG_IOMUX0_nuevo[31:30], CFG_PIN0_nuevo[25]} & CFG_PIN1_mascara;  // AND_Gate and_210, 30 bits wide
  assign not53 = ~CFG_PIN2_mascara;  // NOT_Gate not_17, 30 bits wide
  assign and55 = {CFG_ENTRADA0_nuevo[23], CFG_IOMUX0_nuevo[29:28], CFG_IOMUX0_nuevo[31:30], CFG_PIN0_nuevo[25], CFG_ENTRADA0_nuevo[23], CFG_IOMUX0_nuevo[29:28], CFG_IOMUX0_nuevo[31:30], CFG_PIN0_nuevo[25], CFG_ENTRADA0_nuevo[23], CFG_IOMUX0_nuevo[29:28], CFG_IOMUX0_nuevo[31:30], CFG_PIN0_nuevo[25], CFG_ENTRADA0_nuevo[23], CFG_IOMUX0_nuevo[29:28], CFG_IOMUX0_nuevo[31:30], CFG_PIN0_nuevo[25], CFG_ENTRADA0_nuevo[23], CFG_IOMUX0_nuevo[29:28], CFG_IOMUX0_nuevo[31:30], CFG_PIN0_nuevo[25]} & CFG_PIN2_mascara;  // AND_Gate and_211, 30 bits wide
  assign not66 = ~CFG_PIN3_mascara;  // NOT_Gate not_18, 30 bits wide
  assign and68 = {CFG_ENTRADA0_nuevo[23], CFG_IOMUX0_nuevo[29:28], CFG_IOMUX0_nuevo[31:30], CFG_PIN0_nuevo[25], CFG_ENTRADA0_nuevo[23], CFG_IOMUX0_nuevo[29:28], CFG_IOMUX0_nuevo[31:30], CFG_PIN0_nuevo[25], CFG_ENTRADA0_nuevo[23], CFG_IOMUX0_nuevo[29:28], CFG_IOMUX0_nuevo[31:30], CFG_PIN0_nuevo[25], CFG_ENTRADA0_nuevo[23], CFG_IOMUX0_nuevo[29:28], CFG_IOMUX0_nuevo[31:30], CFG_PIN0_nuevo[25], CFG_ENTRADA0_nuevo[23], CFG_IOMUX0_nuevo[29:28], CFG_IOMUX0_nuevo[31:30], CFG_PIN0_nuevo[25]} & CFG_PIN3_mascara;  // AND_Gate and_212, 30 bits wide
  assign not73 = ~CFG_PIN4_mascara;  // NOT_Gate not_19, 11 bits wide
  assign and75 = {CFG_IOMUX0_nuevo[29:28], CFG_IOMUX0_nuevo[31:30], CFG_PIN0_nuevo[25], CFG_ENTRADA0_nuevo[23], CFG_IOMUX0_nuevo[29:28], CFG_IOMUX0_nuevo[31:30], CFG_PIN0_nuevo[25]} & CFG_PIN4_mascara;  // AND_Gate and_213, 11 bits wide
  assign not78 = ~CFG_SALIDA0_mascara;  // NOT_Gate not_20, 22 bits wide
  assign not85 = ~CFG_SALIDA1_mascara;  // NOT_Gate not_21, 22 bits wide
  assign not92 = ~CFG_SALIDA2_mascara;  // NOT_Gate not_22, 22 bits wide
  assign not99 = ~CFG_SALIDA3_mascara;  // NOT_Gate not_23, 22 bits wide
  assign not106 = ~CFG_SALIDA4_mascara;  // NOT_Gate not_24, 22 bits wide
  assign not113 = ~CFG_SALIDA5_mascara;  // NOT_Gate not_25, 22 bits wide
  assign not120 = ~CFG_SALIDA6_mascara;  // NOT_Gate not_26, 22 bits wide
  assign not127 = ~CFG_SALIDA7_mascara;  // NOT_Gate not_27, 22 bits wide
  assign not134 = ~CFG_SALIDA8_mascara;  // NOT_Gate not_28, 22 bits wide
  assign not141 = ~CFG_SALIDA9_mascara;  // NOT_Gate not_29, 22 bits wide
  assign not148 = ~CFG_SALIDA10_mascara;  // NOT_Gate not_30, 22 bits wide
  assign not157 = ~CFG_ENTRADA0_mascara;  // NOT_Gate not_31, 28 bits wide
  assign not161 = ~CFG_ENTRADA1_mascara;  // NOT_Gate not_32, 7 bits wide
  assign not177 = ~CFG_IOMUX0_mascara;  // NOT_Gate not_33, 32 bits wide
  assign and179 = {CFG_IOMUX0_nuevo, CFG_IOMUX0_nuevo, CFG_IOMUX0_nuevo, CFG_IOMUX0_nuevo, CFG_IOMUX0_nuevo, CFG_IOMUX0_nuevo, CFG_IOMUX0_nuevo[31:30]} & CFG_IOMUX0_mascara;  // AND_Gate and_214, 32 bits wide
  assign not194 = ~CFG_IOMUX1_mascara;  // NOT_Gate not_34, 30 bits wide
  assign and196 = {CFG_IOMUX0_nuevo, CFG_IOMUX0_nuevo, CFG_IOMUX0_nuevo, CFG_IOMUX0_nuevo, CFG_IOMUX0_nuevo, CFG_IOMUX0_nuevo} & CFG_IOMUX1_mascara;  // AND_Gate and_215, 30 bits wide
  assign not211 = ~CFG_IOMUX2_mascara;  // NOT_Gate not_35, 30 bits wide
  assign and213 = {CFG_IOMUX0_nuevo, CFG_IOMUX0_nuevo, CFG_IOMUX0_nuevo, CFG_IOMUX0_nuevo, CFG_IOMUX0_nuevo, CFG_IOMUX0_nuevo} & CFG_IOMUX2_mascara;  // AND_Gate and_216, 30 bits wide
  assign not223 = ~CFG_IOMUX3_mascara;  // NOT_Gate not_36, 18 bits wide
  assign and225 = {CFG_IOMUX0_nuevo[29:27], CFG_IOMUX0_nuevo, CFG_IOMUX0_nuevo, CFG_IOMUX0_nuevo} & CFG_IOMUX3_mascara;  // AND_Gate and_217, 18 bits wide
  Multiplexer #(.select(1), .width(32), .enable("false")) multiplexer_19 (
    .in0(mux241), .in1(or243), .out(mux244), .sel(esc_048));
  assign and280 = eventos & rep279;  // AND_Gate and_218, 32 bits wide
  assign and80 = {CFG_SALIDA0_nuevo[21], CFG_IOMUX0_nuevo[31:30], CFG_PIN0_nuevo[25], CFG_ENTRADA0_nuevo, CFG_SALIDA0_nuevo[21], CFG_IOMUX0_nuevo[31:30], CFG_PIN0_nuevo[25], CFG_ENTRADA0_nuevo} & CFG_SALIDA0_mascara;  // AND_Gate and_219, 22 bits wide
  assign and87 = {CFG_SALIDA0_nuevo[21], CFG_IOMUX0_nuevo[31:30], CFG_PIN0_nuevo[25], CFG_ENTRADA0_nuevo, CFG_SALIDA0_nuevo[21], CFG_IOMUX0_nuevo[31:30], CFG_PIN0_nuevo[25], CFG_ENTRADA0_nuevo} & CFG_SALIDA1_mascara;  // AND_Gate and_220, 22 bits wide
  assign and94 = {CFG_SALIDA0_nuevo[21], CFG_IOMUX0_nuevo[31:30], CFG_PIN0_nuevo[25], CFG_ENTRADA0_nuevo, CFG_SALIDA0_nuevo[21], CFG_IOMUX0_nuevo[31:30], CFG_PIN0_nuevo[25], CFG_ENTRADA0_nuevo} & CFG_SALIDA2_mascara;  // AND_Gate and_221, 22 bits wide
  assign and101 = {CFG_SALIDA0_nuevo[21], CFG_IOMUX0_nuevo[31:30], CFG_PIN0_nuevo[25], CFG_ENTRADA0_nuevo, CFG_SALIDA0_nuevo[21], CFG_IOMUX0_nuevo[31:30], CFG_PIN0_nuevo[25], CFG_ENTRADA0_nuevo} & CFG_SALIDA3_mascara;  // AND_Gate and_222, 22 bits wide
  assign and108 = {CFG_SALIDA0_nuevo[21], CFG_IOMUX0_nuevo[31:30], CFG_PIN0_nuevo[25], CFG_ENTRADA0_nuevo, CFG_SALIDA0_nuevo[21], CFG_IOMUX0_nuevo[31:30], CFG_PIN0_nuevo[25], CFG_ENTRADA0_nuevo} & CFG_SALIDA4_mascara;  // AND_Gate and_223, 22 bits wide
  assign and115 = {CFG_SALIDA0_nuevo[21], CFG_IOMUX0_nuevo[31:30], CFG_PIN0_nuevo[25], CFG_ENTRADA0_nuevo, CFG_SALIDA0_nuevo[21], CFG_IOMUX0_nuevo[31:30], CFG_PIN0_nuevo[25], CFG_ENTRADA0_nuevo} & CFG_SALIDA5_mascara;  // AND_Gate and_224, 22 bits wide
  assign and122 = {CFG_SALIDA0_nuevo[21], CFG_IOMUX0_nuevo[31:30], CFG_PIN0_nuevo[25], CFG_ENTRADA0_nuevo, CFG_SALIDA0_nuevo[21], CFG_IOMUX0_nuevo[31:30], CFG_PIN0_nuevo[25], CFG_ENTRADA0_nuevo} & CFG_SALIDA6_mascara;  // AND_Gate and_225, 22 bits wide
  assign and129 = {CFG_SALIDA0_nuevo[21], CFG_IOMUX0_nuevo[31:30], CFG_PIN0_nuevo[25], CFG_ENTRADA0_nuevo, CFG_SALIDA0_nuevo[21], CFG_IOMUX0_nuevo[31:30], CFG_PIN0_nuevo[25], CFG_ENTRADA0_nuevo} & CFG_SALIDA7_mascara;  // AND_Gate and_226, 22 bits wide
  assign and136 = {CFG_SALIDA0_nuevo[21], CFG_IOMUX0_nuevo[31:30], CFG_PIN0_nuevo[25], CFG_ENTRADA0_nuevo, CFG_SALIDA0_nuevo[21], CFG_IOMUX0_nuevo[31:30], CFG_PIN0_nuevo[25], CFG_ENTRADA0_nuevo} & CFG_SALIDA8_mascara;  // AND_Gate and_227, 22 bits wide
  assign and143 = {CFG_SALIDA0_nuevo[21], CFG_IOMUX0_nuevo[31:30], CFG_PIN0_nuevo[25], CFG_ENTRADA0_nuevo, CFG_SALIDA0_nuevo[21], CFG_IOMUX0_nuevo[31:30], CFG_PIN0_nuevo[25], CFG_ENTRADA0_nuevo} & CFG_SALIDA9_mascara;  // AND_Gate and_228, 22 bits wide
  assign and150 = {CFG_SALIDA0_nuevo[21], CFG_IOMUX0_nuevo[31:30], CFG_PIN0_nuevo[25], CFG_ENTRADA0_nuevo, CFG_SALIDA0_nuevo[21], CFG_IOMUX0_nuevo[31:30], CFG_PIN0_nuevo[25], CFG_ENTRADA0_nuevo} & CFG_SALIDA10_mascara;  // AND_Gate and_229, 22 bits wide
  assign and159 = {CFG_ENTRADA0_nuevo, CFG_ENTRADA0_nuevo, CFG_ENTRADA0_nuevo, CFG_ENTRADA0_nuevo} & CFG_ENTRADA0_mascara;  // AND_Gate and_230, 28 bits wide
  assign and163 = CFG_ENTRADA0_nuevo & CFG_ENTRADA1_mascara;  // AND_Gate and_231, 7 bits wide
  assign and7 = mux5 & not6;  // AND_Gate and_232, 32 bits wide
  assign and15 = mux13 & not14;  // AND_Gate and_233, 32 bits wide
  assign and246 = mux244 & not245;  // AND_Gate and_234, 32 bits wide
  assign RD = and270 | and272 | and274 | and276 | and278 | and280 | and282 | and284 | and268 | mux291 | and290;  // OR_Gate or_31, 32 bits wide
  assign and28 = CFG_PIN0 & not27;  // AND_Gate and_235, 31 bits wide
  assign and41 = CFG_PIN1 & not40;  // AND_Gate and_236, 30 bits wide
  assign and54 = CFG_PIN2 & not53;  // AND_Gate and_237, 30 bits wide
  assign and67 = CFG_PIN3 & not66;  // AND_Gate and_238, 30 bits wide
  assign and74 = CFG_PIN4 & not73;  // AND_Gate and_239, 11 bits wide
  assign and79 = CFG_SALIDA0 & not78;  // AND_Gate and_240, 22 bits wide
  assign and86 = CFG_SALIDA1 & not85;  // AND_Gate and_241, 22 bits wide
  assign and93 = CFG_SALIDA2 & not92;  // AND_Gate and_242, 22 bits wide
  assign and100 = CFG_SALIDA3 & not99;  // AND_Gate and_243, 22 bits wide
  assign and107 = CFG_SALIDA4 & not106;  // AND_Gate and_244, 22 bits wide
  assign and114 = CFG_SALIDA5 & not113;  // AND_Gate and_245, 22 bits wide
  assign and121 = CFG_SALIDA6 & not120;  // AND_Gate and_246, 22 bits wide
  assign and128 = CFG_SALIDA7 & not127;  // AND_Gate and_247, 22 bits wide
  assign and135 = CFG_SALIDA8 & not134;  // AND_Gate and_248, 22 bits wide
  assign and142 = CFG_SALIDA9 & not141;  // AND_Gate and_249, 22 bits wide
  assign and149 = CFG_SALIDA10 & not148;  // AND_Gate and_250, 22 bits wide
  assign and158 = CFG_ENTRADA0 & not157;  // AND_Gate and_251, 28 bits wide
  assign and162 = CFG_ENTRADA1 & not161;  // AND_Gate and_252, 7 bits wide
  assign and178 = CFG_IOMUX0 & not177;  // AND_Gate and_253, 32 bits wide
  assign and195 = CFG_IOMUX1 & not194;  // AND_Gate and_254, 30 bits wide
  assign and212 = CFG_IOMUX2 & not211;  // AND_Gate and_255, 30 bits wide
  assign and224 = CFG_IOMUX3 & not223;  // AND_Gate and_256, 18 bits wide
  Multiplexer #(.select(1), .width(32), .enable("false")) multiplexer_20 (
    .in0(mux5), .in1(and7), .out(GPIO_OUT_sig), .sel(esc_00C));
  Multiplexer #(.select(1), .width(32), .enable("false")) multiplexer_21 (
    .in0(mux13), .in1(and15), .out(GPIO_ENABLE_sig), .sel(esc_028));
  assign CFG_PIN0_sig = and28 | and29;  // OR_Gate or_32, 31 bits wide
  assign CFG_PIN1_sig = and41 | and42;  // OR_Gate or_33, 30 bits wide
  assign CFG_PIN2_sig = and54 | and55;  // OR_Gate or_34, 30 bits wide
  assign CFG_PIN3_sig = and67 | and68;  // OR_Gate or_35, 30 bits wide
  assign CFG_PIN4_sig = and74 | and75;  // OR_Gate or_36, 11 bits wide
  assign CFG_SALIDA0_sig = and79 | and80;  // OR_Gate or_37, 22 bits wide
  assign CFG_SALIDA1_sig = and86 | and87;  // OR_Gate or_38, 22 bits wide
  assign CFG_SALIDA2_sig = and93 | and94;  // OR_Gate or_39, 22 bits wide
  assign CFG_SALIDA3_sig = and100 | and101;  // OR_Gate or_40, 22 bits wide
  assign CFG_SALIDA4_sig = and107 | and108;  // OR_Gate or_41, 22 bits wide
  assign CFG_SALIDA5_sig = and114 | and115;  // OR_Gate or_42, 22 bits wide
  assign CFG_SALIDA6_sig = and121 | and122;  // OR_Gate or_43, 22 bits wide
  assign CFG_SALIDA7_sig = and128 | and129;  // OR_Gate or_44, 22 bits wide
  assign CFG_SALIDA8_sig = and135 | and136;  // OR_Gate or_45, 22 bits wide
  assign CFG_SALIDA9_sig = and142 | and143;  // OR_Gate or_46, 22 bits wide
  assign CFG_SALIDA10_sig = and149 | and150;  // OR_Gate or_47, 22 bits wide
  assign CFG_ENTRADA0_sig = and158 | and159;  // OR_Gate or_48, 28 bits wide
  assign CFG_ENTRADA1_sig = and162 | and163;  // OR_Gate or_49, 7 bits wide
  assign CFG_IOMUX0_sig = and178 | and179;  // OR_Gate or_50, 32 bits wide
  assign CFG_IOMUX1_sig = and195 | and196;  // OR_Gate or_51, 30 bits wide
  assign CFG_IOMUX2_sig = and212 | and213;  // OR_Gate or_52, 30 bits wide
  assign CFG_IOMUX3_sig = and224 | and225;  // OR_Gate or_53, 18 bits wide
  Multiplexer #(.select(1), .width(32), .enable("false")) multiplexer_22 (
    .in0(mux244), .in1(and246), .out(mux247), .sel(esc_04C));
  assign or248 = mux247 | eventos;  // OR_Gate or_54, 32 bits wide
  assign xor81 = CFG_SALIDA0_sig ^ 22'h40080;  // XOR_Gate xor_25, 22 bits wide
  assign xor88 = CFG_SALIDA1_sig ^ 22'h40080;  // XOR_Gate xor_26, 22 bits wide
  assign xor95 = CFG_SALIDA2_sig ^ 22'h40080;  // XOR_Gate xor_27, 22 bits wide
  assign xor102 = CFG_SALIDA3_sig ^ 22'h40080;  // XOR_Gate xor_28, 22 bits wide
  assign xor109 = CFG_SALIDA4_sig ^ 22'h40080;  // XOR_Gate xor_29, 22 bits wide
  assign xor116 = CFG_SALIDA5_sig ^ 22'h40080;  // XOR_Gate xor_30, 22 bits wide
  assign xor123 = CFG_SALIDA6_sig ^ 22'h40080;  // XOR_Gate xor_31, 22 bits wide
  assign xor130 = CFG_SALIDA7_sig ^ 22'h40080;  // XOR_Gate xor_32, 22 bits wide
  assign xor137 = CFG_SALIDA8_sig ^ 22'h40080;  // XOR_Gate xor_33, 22 bits wide
  assign xor144 = CFG_SALIDA9_sig ^ 22'h40080;  // XOR_Gate xor_34, 22 bits wide
  assign xor151 = CFG_SALIDA10_sig ^ 22'h40080;  // XOR_Gate xor_35, 22 bits wide
  assign xor180 = CFG_IOMUX0_sig ^ 32'h84210800;  // XOR_Gate xor_36, 32 bits wide
  assign xor197 = CFG_IOMUX1_sig ^ 30'h31086210;  // XOR_Gate xor_37, 30 bits wide
  assign xor214 = CFG_IOMUX2_sig ^ 30'h218c6318;  // XOR_Gate xor_38, 30 bits wide
  assign xor226 = CFG_IOMUX3_sig ^ 18'h4310;  // XOR_Gate xor_39, 18 bits wide

  // Other names for the same wires on the sheet: directa2 = cat238[1];
  //   entradas[21:0] = {directa21, directa20, directa19, directa18, directa17, directa16, directa15, directa14, directa13, directa12, directa11, directa10, cat238[3:2], directa7, directa6, directa5, directa4, directa3, cat238[1], directa1, directa0};
  //   directa8 = cat238[2]; directa9 = cat238[3]; CFG_ENTRADA0_6_0[6:0] = CFG_ENTRADA0[6:0];
  //   CFG_ENTRADA0_6_0_4_0[4:0] = CFG_ENTRADA0[4:0]; CFG_ENTRADA0_6_0_5 = CFG_ENTRADA0[5];
  //   CFG_ENTRADA0_6_0_6 = CFG_ENTRADA0[6]; CFG_ENTRADA0_13_7[6:0] = CFG_ENTRADA0[13:7];
  //   CFG_ENTRADA0_13_7_4_0[4:0] = CFG_ENTRADA0[11:7]; CFG_ENTRADA0_13_7_5 = CFG_ENTRADA0[12];
  //   CFG_ENTRADA0_13_7_6 = CFG_ENTRADA0[13]; CFG_ENTRADA0_20_14[6:0] = CFG_ENTRADA0[20:14];
  //   CFG_ENTRADA0_20_14_4_0[4:0] = CFG_ENTRADA0[18:14]; CFG_ENTRADA0_20_14_5 = CFG_ENTRADA0[19];
  //   CFG_ENTRADA0_20_14_6 = CFG_ENTRADA0[20]; CFG_ENTRADA0_27_21[6:0] = CFG_ENTRADA0[27:21];
  //   CFG_ENTRADA0_27_21_4_0[4:0] = CFG_ENTRADA0[25:21]; CFG_ENTRADA0_27_21_5 = CFG_ENTRADA0[26];
  //   CFG_ENTRADA0_27_21_6 = CFG_ENTRADA0[27]; rep153[6:0] = CFG_ENTRADA0_mascara[6:0];
  //   rep154[6:0] = CFG_ENTRADA0_mascara[13:7]; rep155[6:0] = CFG_ENTRADA0_mascara[20:14];
  //   rep156[6:0] = CFG_ENTRADA0_mascara[27:21]; CFG_ENTRADA1_4_0[4:0] = CFG_ENTRADA1[4:0];
  //   CFG_ENTRADA1_5 = CFG_ENTRADA1[5]; CFG_ENTRADA1_6 = CFG_ENTRADA1[6]; esc_254 = CFG_ENTRADA1_escribe;
  //   rep160[6:0] = CFG_ENTRADA1_mascara;
  //   CFG_ENTRADA0_nuevo[20:0] = {CFG_ENTRADA0_nuevo, CFG_ENTRADA0_nuevo, CFG_ENTRADA0_nuevo};
  //   CFG_ENTRADA1_nuevo[6:0] = CFG_ENTRADA0_nuevo;
  //   CFG_SALIDA0_nuevo[20:0] = {CFG_IOMUX0_nuevo[31:30], CFG_PIN0_nuevo[25], CFG_ENTRADA0_nuevo, CFG_SALIDA0_nuevo[21], CFG_IOMUX0_nuevo[31:30], CFG_PIN0_nuevo[25], CFG_ENTRADA0_nuevo};
  //   CFG_SALIDA1_nuevo[21:0] = {CFG_SALIDA0_nuevo[21], CFG_IOMUX0_nuevo[31:30], CFG_PIN0_nuevo[25], CFG_ENTRADA0_nuevo, CFG_SALIDA0_nuevo[21], CFG_IOMUX0_nuevo[31:30], CFG_PIN0_nuevo[25], CFG_ENTRADA0_nuevo};
  //   CFG_SALIDA2_nuevo[21:0] = {CFG_SALIDA0_nuevo[21], CFG_IOMUX0_nuevo[31:30], CFG_PIN0_nuevo[25], CFG_ENTRADA0_nuevo, CFG_SALIDA0_nuevo[21], CFG_IOMUX0_nuevo[31:30], CFG_PIN0_nuevo[25], CFG_ENTRADA0_nuevo};
  //   CFG_SALIDA3_nuevo[21:0] = {CFG_SALIDA0_nuevo[21], CFG_IOMUX0_nuevo[31:30], CFG_PIN0_nuevo[25], CFG_ENTRADA0_nuevo, CFG_SALIDA0_nuevo[21], CFG_IOMUX0_nuevo[31:30], CFG_PIN0_nuevo[25], CFG_ENTRADA0_nuevo};
  //   CFG_SALIDA4_nuevo[21:0] = {CFG_SALIDA0_nuevo[21], CFG_IOMUX0_nuevo[31:30], CFG_PIN0_nuevo[25], CFG_ENTRADA0_nuevo, CFG_SALIDA0_nuevo[21], CFG_IOMUX0_nuevo[31:30], CFG_PIN0_nuevo[25], CFG_ENTRADA0_nuevo};
  //   CFG_SALIDA5_nuevo[21:0] = {CFG_SALIDA0_nuevo[21], CFG_IOMUX0_nuevo[31:30], CFG_PIN0_nuevo[25], CFG_ENTRADA0_nuevo, CFG_SALIDA0_nuevo[21], CFG_IOMUX0_nuevo[31:30], CFG_PIN0_nuevo[25], CFG_ENTRADA0_nuevo};
  //   CFG_SALIDA6_nuevo[21:0] = {CFG_SALIDA0_nuevo[21], CFG_IOMUX0_nuevo[31:30], CFG_PIN0_nuevo[25], CFG_ENTRADA0_nuevo, CFG_SALIDA0_nuevo[21], CFG_IOMUX0_nuevo[31:30], CFG_PIN0_nuevo[25], CFG_ENTRADA0_nuevo};
  //   CFG_SALIDA7_nuevo[21:0] = {CFG_SALIDA0_nuevo[21], CFG_IOMUX0_nuevo[31:30], CFG_PIN0_nuevo[25], CFG_ENTRADA0_nuevo, CFG_SALIDA0_nuevo[21], CFG_IOMUX0_nuevo[31:30], CFG_PIN0_nuevo[25], CFG_ENTRADA0_nuevo};
  //   CFG_SALIDA8_nuevo[21:0] = {CFG_SALIDA0_nuevo[21], CFG_IOMUX0_nuevo[31:30], CFG_PIN0_nuevo[25], CFG_ENTRADA0_nuevo, CFG_SALIDA0_nuevo[21], CFG_IOMUX0_nuevo[31:30], CFG_PIN0_nuevo[25], CFG_ENTRADA0_nuevo};
  //   CFG_SALIDA9_nuevo[21:0] = {CFG_SALIDA0_nuevo[21], CFG_IOMUX0_nuevo[31:30], CFG_PIN0_nuevo[25], CFG_ENTRADA0_nuevo, CFG_SALIDA0_nuevo[21], CFG_IOMUX0_nuevo[31:30], CFG_PIN0_nuevo[25], CFG_ENTRADA0_nuevo};
  //   CFG_SALIDA10_nuevo[21:0] = {CFG_SALIDA0_nuevo[21], CFG_IOMUX0_nuevo[31:30], CFG_PIN0_nuevo[25], CFG_ENTRADA0_nuevo, CFG_SALIDA0_nuevo[21], CFG_IOMUX0_nuevo[31:30], CFG_PIN0_nuevo[25], CFG_ENTRADA0_nuevo};
  //   dato_escrito (some bits) = {CFG_IOMUX0_nuevo[29:27], CFG_SALIDA0_nuevo[21], CFG_IOMUX0_nuevo[31:30], CFG_PIN0_nuevo[25], CFG_ENTRADA0_nuevo};
  //   dato_escrito_6_0[6:0] = CFG_ENTRADA0_nuevo;
  //   dato_escrito_10_0[10:0] = {CFG_SALIDA0_nuevo[21], CFG_IOMUX0_nuevo[31:30], CFG_PIN0_nuevo[25], CFG_ENTRADA0_nuevo};
  //   CFG_PIN0_nuevo (some bits) = {CFG_ENTRADA0_nuevo[23], CFG_IOMUX0_nuevo[29:28], CFG_IOMUX0_nuevo[31:30], CFG_ENTRADA0_nuevo[23], CFG_IOMUX0_nuevo[29:28], CFG_IOMUX0_nuevo[31:30], CFG_PIN0_nuevo[25], CFG_ENTRADA0_nuevo[23], CFG_IOMUX0_nuevo[29:28], CFG_IOMUX0_nuevo[31:30], CFG_PIN0_nuevo[25], CFG_ENTRADA0_nuevo[23], CFG_IOMUX0_nuevo[29:28], CFG_IOMUX0_nuevo[31:30], CFG_PIN0_nuevo[25], CFG_ENTRADA0_nuevo[23], CFG_IOMUX0_nuevo[29:28], CFG_IOMUX0_nuevo[31:30], CFG_PIN0_nuevo[25], CFG_ENTRADA0_nuevo[23]};
  //   CFG_PIN1_nuevo[29:0] = {CFG_ENTRADA0_nuevo[23], CFG_IOMUX0_nuevo[29:28], CFG_IOMUX0_nuevo[31:30], CFG_PIN0_nuevo[25], CFG_ENTRADA0_nuevo[23], CFG_IOMUX0_nuevo[29:28], CFG_IOMUX0_nuevo[31:30], CFG_PIN0_nuevo[25], CFG_ENTRADA0_nuevo[23], CFG_IOMUX0_nuevo[29:28], CFG_IOMUX0_nuevo[31:30], CFG_PIN0_nuevo[25], CFG_ENTRADA0_nuevo[23], CFG_IOMUX0_nuevo[29:28], CFG_IOMUX0_nuevo[31:30], CFG_PIN0_nuevo[25], CFG_ENTRADA0_nuevo[23], CFG_IOMUX0_nuevo[29:28], CFG_IOMUX0_nuevo[31:30], CFG_PIN0_nuevo[25]};
  //   CFG_PIN2_nuevo[29:0] = {CFG_ENTRADA0_nuevo[23], CFG_IOMUX0_nuevo[29:28], CFG_IOMUX0_nuevo[31:30], CFG_PIN0_nuevo[25], CFG_ENTRADA0_nuevo[23], CFG_IOMUX0_nuevo[29:28], CFG_IOMUX0_nuevo[31:30], CFG_PIN0_nuevo[25], CFG_ENTRADA0_nuevo[23], CFG_IOMUX0_nuevo[29:28], CFG_IOMUX0_nuevo[31:30], CFG_PIN0_nuevo[25], CFG_ENTRADA0_nuevo[23], CFG_IOMUX0_nuevo[29:28], CFG_IOMUX0_nuevo[31:30], CFG_PIN0_nuevo[25], CFG_ENTRADA0_nuevo[23], CFG_IOMUX0_nuevo[29:28], CFG_IOMUX0_nuevo[31:30], CFG_PIN0_nuevo[25]};
  //   CFG_PIN3_nuevo[29:0] = {CFG_ENTRADA0_nuevo[23], CFG_IOMUX0_nuevo[29:28], CFG_IOMUX0_nuevo[31:30], CFG_PIN0_nuevo[25], CFG_ENTRADA0_nuevo[23], CFG_IOMUX0_nuevo[29:28], CFG_IOMUX0_nuevo[31:30], CFG_PIN0_nuevo[25], CFG_ENTRADA0_nuevo[23], CFG_IOMUX0_nuevo[29:28], CFG_IOMUX0_nuevo[31:30], CFG_PIN0_nuevo[25], CFG_ENTRADA0_nuevo[23], CFG_IOMUX0_nuevo[29:28], CFG_IOMUX0_nuevo[31:30], CFG_PIN0_nuevo[25], CFG_ENTRADA0_nuevo[23], CFG_IOMUX0_nuevo[29:28], CFG_IOMUX0_nuevo[31:30], CFG_PIN0_nuevo[25]};
  //   CFG_PIN4_nuevo[10:0] = {CFG_IOMUX0_nuevo[29:28], CFG_IOMUX0_nuevo[31:30], CFG_PIN0_nuevo[25], CFG_ENTRADA0_nuevo[23], CFG_IOMUX0_nuevo[29:28], CFG_IOMUX0_nuevo[31:30], CFG_PIN0_nuevo[25]};
  //   dato_escrito_2 = CFG_ENTRADA0_nuevo[23]; rep164[1:0] = CFG_IOMUX0_mascara[1:0];
  //   rep165[2:0] = CFG_IOMUX0_mascara[4:2]; rep166[1:0] = CFG_IOMUX0_mascara[6:5];
  //   rep167[2:0] = CFG_IOMUX0_mascara[9:7]; rep168[1:0] = CFG_IOMUX0_mascara[11:10];
  //   rep169[2:0] = CFG_IOMUX0_mascara[14:12]; rep170[1:0] = CFG_IOMUX0_mascara[16:15];
  //   rep171[2:0] = CFG_IOMUX0_mascara[19:17]; rep172[1:0] = CFG_IOMUX0_mascara[21:20];
  //   rep173[2:0] = CFG_IOMUX0_mascara[24:22]; rep174[1:0] = CFG_IOMUX0_mascara[26:25];
  //   rep175[2:0] = CFG_IOMUX0_mascara[29:27]; rep176[1:0] = CFG_IOMUX0_mascara[31:30];
  //   rep182[2:0] = CFG_IOMUX1_mascara[2:0]; rep183[1:0] = CFG_IOMUX1_mascara[4:3];
  //   rep184[2:0] = CFG_IOMUX1_mascara[7:5]; rep185[1:0] = CFG_IOMUX1_mascara[9:8];
  //   rep186[2:0] = CFG_IOMUX1_mascara[12:10]; rep187[1:0] = CFG_IOMUX1_mascara[14:13];
  //   rep188[2:0] = CFG_IOMUX1_mascara[17:15]; rep189[1:0] = CFG_IOMUX1_mascara[19:18];
  //   rep190[2:0] = CFG_IOMUX1_mascara[22:20]; rep191[1:0] = CFG_IOMUX1_mascara[24:23];
  //   rep192[2:0] = CFG_IOMUX1_mascara[27:25]; rep193[1:0] = CFG_IOMUX1_mascara[29:28];
  //   rep199[2:0] = CFG_IOMUX2_mascara[2:0]; rep200[1:0] = CFG_IOMUX2_mascara[4:3];
  //   rep201[2:0] = CFG_IOMUX2_mascara[7:5]; rep202[1:0] = CFG_IOMUX2_mascara[9:8];
  //   rep203[2:0] = CFG_IOMUX2_mascara[12:10]; rep204[1:0] = CFG_IOMUX2_mascara[14:13];
  //   rep205[2:0] = CFG_IOMUX2_mascara[17:15]; rep206[1:0] = CFG_IOMUX2_mascara[19:18];
  //   rep207[2:0] = CFG_IOMUX2_mascara[22:20]; rep208[1:0] = CFG_IOMUX2_mascara[24:23];
  //   rep209[2:0] = CFG_IOMUX2_mascara[27:25]; rep210[1:0] = CFG_IOMUX2_mascara[29:28];
  //   rep216[2:0] = CFG_IOMUX3_mascara[2:0]; rep217[1:0] = CFG_IOMUX3_mascara[4:3];
  //   rep218[2:0] = CFG_IOMUX3_mascara[7:5]; rep219[1:0] = CFG_IOMUX3_mascara[9:8];
  //   rep220[2:0] = CFG_IOMUX3_mascara[12:10]; rep221[1:0] = CFG_IOMUX3_mascara[14:13];
  //   rep222[2:0] = CFG_IOMUX3_mascara[17:15];
  //   CFG_IOMUX0_nuevo[26:0] = {CFG_IOMUX0_nuevo, CFG_IOMUX0_nuevo, CFG_IOMUX0_nuevo, CFG_IOMUX0_nuevo, CFG_IOMUX0_nuevo, CFG_IOMUX0_nuevo[31:30]};
  //   CFG_IOMUX1_nuevo[29:0] = {CFG_IOMUX0_nuevo, CFG_IOMUX0_nuevo, CFG_IOMUX0_nuevo, CFG_IOMUX0_nuevo, CFG_IOMUX0_nuevo, CFG_IOMUX0_nuevo};
  //   CFG_IOMUX2_nuevo[29:0] = {CFG_IOMUX0_nuevo, CFG_IOMUX0_nuevo, CFG_IOMUX0_nuevo, CFG_IOMUX0_nuevo, CFG_IOMUX0_nuevo, CFG_IOMUX0_nuevo};
  //   CFG_IOMUX3_nuevo[17:0] = {CFG_IOMUX0_nuevo[29:27], CFG_IOMUX0_nuevo, CFG_IOMUX0_nuevo, CFG_IOMUX0_nuevo};
  //   dato_escrito_9_7[2:0] = {CFG_IOMUX0_nuevo[31:30], CFG_PIN0_nuevo[25]};
  //   dato_escrito_9_8[1:0] = CFG_IOMUX0_nuevo[31:30]; dato_escrito_14_12[2:0] = CFG_IOMUX0_nuevo[29:27];
  //   dato_escrito_14_13[1:0] = CFG_IOMUX0_nuevo[29:28]; CFG_PIN0_0 = CFG_PIN0[0]; CFG_PIN0_6 = CFG_PIN0[6];
  //   CFG_PIN0_12 = CFG_PIN0[12]; CFG_PIN0_18 = CFG_PIN0[18]; CFG_PIN0_24 = CFG_PIN0[24]; CFG_PIN0_30 = CFG_PIN0[30];
  //   esc_074 = CFG_PIN0_mascara[0]; rep17[2:0] = CFG_PIN0_mascara[3:1]; rep18[1:0] = CFG_PIN0_mascara[5:4];
  //   esc_078 = CFG_PIN0_mascara[6]; rep19[2:0] = CFG_PIN0_mascara[9:7]; rep20[1:0] = CFG_PIN0_mascara[11:10];
  //   esc_07C = CFG_PIN0_mascara[12]; rep21[2:0] = CFG_PIN0_mascara[15:13]; rep22[1:0] = CFG_PIN0_mascara[17:16];
  //   esc_080 = CFG_PIN0_mascara[18]; rep23[2:0] = CFG_PIN0_mascara[21:19]; rep24[1:0] = CFG_PIN0_mascara[23:22];
  //   esc_084 = CFG_PIN0_mascara[24]; rep25[2:0] = CFG_PIN0_mascara[27:25]; rep26[1:0] = CFG_PIN0_mascara[29:28];
  //   esc_088 = CFG_PIN0_mascara[30]; CFG_PIN1_5 = CFG_PIN1[5]; CFG_PIN1_11 = CFG_PIN1[11];
  //   CFG_PIN1_17 = CFG_PIN1[17]; CFG_PIN1_23 = CFG_PIN1[23]; CFG_PIN1_29 = CFG_PIN1[29];
  //   rep30[2:0] = CFG_PIN1_mascara[2:0]; rep31[1:0] = CFG_PIN1_mascara[4:3]; esc_08C = CFG_PIN1_mascara[5];
  //   rep32[2:0] = CFG_PIN1_mascara[8:6]; rep33[1:0] = CFG_PIN1_mascara[10:9]; esc_090 = CFG_PIN1_mascara[11];
  //   rep34[2:0] = CFG_PIN1_mascara[14:12]; rep35[1:0] = CFG_PIN1_mascara[16:15]; esc_094 = CFG_PIN1_mascara[17];
  //   rep36[2:0] = CFG_PIN1_mascara[20:18]; rep37[1:0] = CFG_PIN1_mascara[22:21]; esc_098 = CFG_PIN1_mascara[23];
  //   rep38[2:0] = CFG_PIN1_mascara[26:24]; rep39[1:0] = CFG_PIN1_mascara[28:27]; esc_09C = CFG_PIN1_mascara[29];
  //   CFG_PIN2_5 = CFG_PIN2[5]; CFG_PIN2_11 = CFG_PIN2[11]; CFG_PIN2_17 = CFG_PIN2[17]; CFG_PIN2_23 = CFG_PIN2[23];
  //   CFG_PIN2_29 = CFG_PIN2[29]; rep43[2:0] = CFG_PIN2_mascara[2:0]; rep44[1:0] = CFG_PIN2_mascara[4:3];
  //   esc_0A0 = CFG_PIN2_mascara[5]; rep45[2:0] = CFG_PIN2_mascara[8:6]; rep46[1:0] = CFG_PIN2_mascara[10:9];
  //   esc_0A4 = CFG_PIN2_mascara[11]; rep47[2:0] = CFG_PIN2_mascara[14:12]; rep48[1:0] = CFG_PIN2_mascara[16:15];
  //   esc_0A8 = CFG_PIN2_mascara[17]; rep49[2:0] = CFG_PIN2_mascara[20:18]; rep50[1:0] = CFG_PIN2_mascara[22:21];
  //   esc_0AC = CFG_PIN2_mascara[23]; rep51[2:0] = CFG_PIN2_mascara[26:24]; rep52[1:0] = CFG_PIN2_mascara[28:27];
  //   esc_0B0 = CFG_PIN2_mascara[29]; CFG_PIN3_5 = CFG_PIN3[5]; CFG_PIN3_11 = CFG_PIN3[11];
  //   CFG_PIN3_17 = CFG_PIN3[17]; CFG_PIN3_23 = CFG_PIN3[23]; CFG_PIN3_29 = CFG_PIN3[29];
  //   rep56[2:0] = CFG_PIN3_mascara[2:0]; rep57[1:0] = CFG_PIN3_mascara[4:3]; esc_0B4 = CFG_PIN3_mascara[5];
  //   rep58[2:0] = CFG_PIN3_mascara[8:6]; rep59[1:0] = CFG_PIN3_mascara[10:9]; esc_0B8 = CFG_PIN3_mascara[11];
  //   rep60[2:0] = CFG_PIN3_mascara[14:12]; rep61[1:0] = CFG_PIN3_mascara[16:15]; esc_0BC = CFG_PIN3_mascara[17];
  //   rep62[2:0] = CFG_PIN3_mascara[20:18]; rep63[1:0] = CFG_PIN3_mascara[22:21]; esc_0C0 = CFG_PIN3_mascara[23];
  //   rep64[2:0] = CFG_PIN3_mascara[26:24]; rep65[1:0] = CFG_PIN3_mascara[28:27]; esc_0C4 = CFG_PIN3_mascara[29];
  //   CFG_PIN4_5 = CFG_PIN4[5]; rep69[2:0] = CFG_PIN4_mascara[2:0]; rep70[1:0] = CFG_PIN4_mascara[4:3];
  //   esc_0C8 = CFG_PIN4_mascara[5]; rep71[2:0] = CFG_PIN4_mascara[8:6]; rep72[1:0] = CFG_PIN4_mascara[10:9];
  //   CFG_SALIDA0_10_0[10:0] = CFG_SALIDA0[10:0]; CFG_SALIDA0_21_11[10:0] = CFG_SALIDA0[21:11];
  //   rep76[10:0] = CFG_SALIDA0_mascara[10:0]; rep77[10:0] = CFG_SALIDA0_mascara[21:11];
  //   CFG_SALIDA1_10_0[10:0] = CFG_SALIDA1[10:0]; CFG_SALIDA1_21_11[10:0] = CFG_SALIDA1[21:11];
  //   rep83[10:0] = CFG_SALIDA1_mascara[10:0]; rep84[10:0] = CFG_SALIDA1_mascara[21:11];
  //   CFG_SALIDA2_10_0[10:0] = CFG_SALIDA2[10:0]; CFG_SALIDA2_21_11[10:0] = CFG_SALIDA2[21:11];
  //   rep90[10:0] = CFG_SALIDA2_mascara[10:0]; rep91[10:0] = CFG_SALIDA2_mascara[21:11];
  //   CFG_SALIDA3_10_0[10:0] = CFG_SALIDA3[10:0]; CFG_SALIDA3_21_11[10:0] = CFG_SALIDA3[21:11];
  //   rep97[10:0] = CFG_SALIDA3_mascara[10:0]; rep98[10:0] = CFG_SALIDA3_mascara[21:11];
  //   CFG_SALIDA4_10_0[10:0] = CFG_SALIDA4[10:0]; CFG_SALIDA4_21_11[10:0] = CFG_SALIDA4[21:11];
  //   rep104[10:0] = CFG_SALIDA4_mascara[10:0]; rep105[10:0] = CFG_SALIDA4_mascara[21:11];
  //   CFG_SALIDA5_10_0[10:0] = CFG_SALIDA5[10:0]; CFG_SALIDA5_21_11[10:0] = CFG_SALIDA5[21:11];
  //   rep111[10:0] = CFG_SALIDA5_mascara[10:0]; rep112[10:0] = CFG_SALIDA5_mascara[21:11];
  //   CFG_SALIDA6_10_0[10:0] = CFG_SALIDA6[10:0]; CFG_SALIDA6_21_11[10:0] = CFG_SALIDA6[21:11];
  //   rep118[10:0] = CFG_SALIDA6_mascara[10:0]; rep119[10:0] = CFG_SALIDA6_mascara[21:11];
  //   CFG_SALIDA7_10_0[10:0] = CFG_SALIDA7[10:0]; CFG_SALIDA7_21_11[10:0] = CFG_SALIDA7[21:11];
  //   rep125[10:0] = CFG_SALIDA7_mascara[10:0]; rep126[10:0] = CFG_SALIDA7_mascara[21:11];
  //   CFG_SALIDA8_10_0[10:0] = CFG_SALIDA8[10:0]; CFG_SALIDA8_21_11[10:0] = CFG_SALIDA8[21:11];
  //   rep132[10:0] = CFG_SALIDA8_mascara[10:0]; rep133[10:0] = CFG_SALIDA8_mascara[21:11];
  //   CFG_SALIDA9_10_0[10:0] = CFG_SALIDA9[10:0]; CFG_SALIDA9_21_11[10:0] = CFG_SALIDA9[21:11];
  //   rep139[10:0] = CFG_SALIDA9_mascara[10:0]; rep140[10:0] = CFG_SALIDA9_mascara[21:11];
  //   CFG_SALIDA10_10_0[10:0] = CFG_SALIDA10[10:0]; CFG_SALIDA10_21_11[10:0] = CFG_SALIDA10[21:11];
  //   rep146[10:0] = CFG_SALIDA10_mascara[10:0]; rep147[10:0] = CFG_SALIDA10_mascara[21:11];
  //   dir_registro_4_0[4:0] = dir_registro[4:0]; dir_registro_9_5[4:0] = dir_registro[9:5];
  //   CFG_PIN0_5_4[1:0] = CFG_PIN0[5:4]; CFG_PIN0_5_4_0 = CFG_PIN0[4];
  //   ena_cpu[21:0] = {CFG_PIN4[9], CFG_PIN4[3], CFG_PIN3[27], CFG_PIN3[21], CFG_PIN3[15], CFG_PIN3[9], CFG_PIN3[3], CFG_PIN2[27], CFG_PIN2[21], CFG_PIN2[15], CFG_PIN2[9], CFG_PIN2[3], CFG_PIN1[27], CFG_PIN1[21], CFG_PIN1[15], CFG_PIN1[9], CFG_PIN1[3], CFG_PIN0[28], CFG_PIN0[22], CFG_PIN0[16], CFG_PIN0[10], CFG_PIN0[4]};
  //   CFG_PIN0_11_10[1:0] = CFG_PIN0[11:10]; CFG_PIN0_11_10_0 = CFG_PIN0[10]; CFG_PIN0_17_16[1:0] = CFG_PIN0[17:16];
  //   CFG_PIN0_17_16_0 = CFG_PIN0[16]; CFG_PIN0_23_22[1:0] = CFG_PIN0[23:22]; CFG_PIN0_23_22_0 = CFG_PIN0[22];
  //   CFG_PIN0_29_28[1:0] = CFG_PIN0[29:28]; CFG_PIN0_29_28_0 = CFG_PIN0[28]; CFG_PIN1_4_3[1:0] = CFG_PIN1[4:3];
  //   CFG_PIN1_4_3_0 = CFG_PIN1[3]; CFG_PIN1_10_9[1:0] = CFG_PIN1[10:9]; CFG_PIN1_10_9_0 = CFG_PIN1[9];
  //   CFG_PIN1_16_15[1:0] = CFG_PIN1[16:15]; CFG_PIN1_16_15_0 = CFG_PIN1[15]; CFG_PIN1_22_21[1:0] = CFG_PIN1[22:21];
  //   CFG_PIN1_22_21_0 = CFG_PIN1[21]; CFG_PIN1_28_27[1:0] = CFG_PIN1[28:27]; CFG_PIN1_28_27_0 = CFG_PIN1[27];
  //   CFG_PIN2_4_3[1:0] = CFG_PIN2[4:3]; CFG_PIN2_4_3_0 = CFG_PIN2[3]; CFG_PIN2_10_9[1:0] = CFG_PIN2[10:9];
  //   CFG_PIN2_10_9_0 = CFG_PIN2[9]; CFG_PIN2_16_15[1:0] = CFG_PIN2[16:15]; CFG_PIN2_16_15_0 = CFG_PIN2[15];
  //   CFG_PIN2_22_21[1:0] = CFG_PIN2[22:21]; CFG_PIN2_22_21_0 = CFG_PIN2[21]; CFG_PIN2_28_27[1:0] = CFG_PIN2[28:27];
  //   CFG_PIN2_28_27_0 = CFG_PIN2[27]; CFG_PIN3_4_3[1:0] = CFG_PIN3[4:3]; CFG_PIN3_4_3_0 = CFG_PIN3[3];
  //   CFG_PIN3_10_9[1:0] = CFG_PIN3[10:9]; CFG_PIN3_10_9_0 = CFG_PIN3[9]; CFG_PIN3_16_15[1:0] = CFG_PIN3[16:15];
  //   CFG_PIN3_16_15_0 = CFG_PIN3[15]; CFG_PIN3_22_21[1:0] = CFG_PIN3[22:21]; CFG_PIN3_22_21_0 = CFG_PIN3[21];
  //   CFG_PIN3_28_27[1:0] = CFG_PIN3[28:27]; CFG_PIN3_28_27_0 = CFG_PIN3[27]; CFG_PIN4_4_3[1:0] = CFG_PIN4[4:3];
  //   CFG_PIN4_4_3_0 = CFG_PIN4[3]; CFG_PIN4_10_9[1:0] = CFG_PIN4[10:9]; CFG_PIN4_10_9_0 = CFG_PIN4[9];
  //   CFG_PIN0_5_4_1 = CFG_PIN0[5];
  //   ena_nmi[21:0] = {CFG_PIN4[10], CFG_PIN4[4], CFG_PIN3[28], CFG_PIN3[22], CFG_PIN3[16], CFG_PIN3[10], CFG_PIN3[4], CFG_PIN2[28], CFG_PIN2[22], CFG_PIN2[16], CFG_PIN2[10], CFG_PIN2[4], CFG_PIN1[28], CFG_PIN1[22], CFG_PIN1[16], CFG_PIN1[10], CFG_PIN1[4], CFG_PIN0[29], CFG_PIN0[23], CFG_PIN0[17], CFG_PIN0[11], CFG_PIN0[5]};
  //   CFG_PIN0_11_10_1 = CFG_PIN0[11]; CFG_PIN0_17_16_1 = CFG_PIN0[17]; CFG_PIN0_23_22_1 = CFG_PIN0[23];
  //   CFG_PIN0_29_28_1 = CFG_PIN0[29]; CFG_PIN1_4_3_1 = CFG_PIN1[4]; CFG_PIN1_10_9_1 = CFG_PIN1[10];
  //   CFG_PIN1_16_15_1 = CFG_PIN1[16]; CFG_PIN1_22_21_1 = CFG_PIN1[22]; CFG_PIN1_28_27_1 = CFG_PIN1[28];
  //   CFG_PIN2_4_3_1 = CFG_PIN2[4]; CFG_PIN2_10_9_1 = CFG_PIN2[10]; CFG_PIN2_16_15_1 = CFG_PIN2[16];
  //   CFG_PIN2_22_21_1 = CFG_PIN2[22]; CFG_PIN2_28_27_1 = CFG_PIN2[28]; CFG_PIN3_4_3_1 = CFG_PIN3[4];
  //   CFG_PIN3_10_9_1 = CFG_PIN3[10]; CFG_PIN3_16_15_1 = CFG_PIN3[16]; CFG_PIN3_22_21_1 = CFG_PIN3[22];
  //   CFG_PIN3_28_27_1 = CFG_PIN3[28]; CFG_PIN4_4_3_1 = CFG_PIN4[4]; CFG_PIN4_10_9_1 = CFG_PIN4[10];
  //   FSPI_OE_0 = FSPI_OE[0]; FSPI_OE_1 = FSPI_OE[1]; FSPI_OE_2 = FSPI_OE[2]; FSPI_OE_3 = FSPI_OE[3];
  //   FSPI_OE_4 = FSPI_OE[4]; FSPI_OE_5 = FSPI_OE[5]; FSPI_OUT_0 = FSPI_OUT[0]; FSPI_OUT_1 = FSPI_OUT[1];
  //   FSPI_OUT_2 = FSPI_OUT[2]; FSPI_OUT_3 = FSPI_OUT[3]; FSPI_OUT_4 = FSPI_OUT[4]; FSPI_OUT_5 = FSPI_OUT[5];
  //   sig_FSPIQ = FSPIQ; GPIO_ENABLE_0 = GPIO_ENABLE[0]; GPIO_ENABLE_1 = GPIO_ENABLE[1];
  //   GPIO_ENABLE_2 = GPIO_ENABLE[2]; GPIO_ENABLE_3 = GPIO_ENABLE[3]; GPIO_ENABLE_4 = GPIO_ENABLE[4];
  //   GPIO_ENABLE_5 = GPIO_ENABLE[5]; GPIO_ENABLE_6 = GPIO_ENABLE[6]; GPIO_ENABLE_7 = GPIO_ENABLE[7];
  //   GPIO_ENABLE_8 = GPIO_ENABLE[8]; GPIO_ENABLE_9 = GPIO_ENABLE[9]; GPIO_ENABLE_10 = GPIO_ENABLE[10];
  //   GPIO_ENABLE_11 = GPIO_ENABLE[11]; GPIO_ENABLE_12 = GPIO_ENABLE[12]; GPIO_ENABLE_13 = GPIO_ENABLE[13];
  //   GPIO_ENABLE_14 = GPIO_ENABLE[14]; GPIO_ENABLE_15 = GPIO_ENABLE[15]; GPIO_ENABLE_16 = GPIO_ENABLE[16];
  //   GPIO_ENABLE_17 = GPIO_ENABLE[17]; GPIO_ENABLE_18 = GPIO_ENABLE[18]; GPIO_ENABLE_19 = GPIO_ENABLE[19];
  //   GPIO_ENABLE_20 = GPIO_ENABLE[20]; GPIO_ENABLE_21 = GPIO_ENABLE[21]; GPIO_OUT_0 = GPIO_OUT[0];
  //   GPIO_OUT_1 = GPIO_OUT[1]; GPIO_OUT_2 = GPIO_OUT[2]; GPIO_OUT_3 = GPIO_OUT[3]; GPIO_OUT_4 = GPIO_OUT[4];
  //   GPIO_OUT_5 = GPIO_OUT[5]; GPIO_OUT_6 = GPIO_OUT[6]; GPIO_OUT_7 = GPIO_OUT[7]; GPIO_OUT_8 = GPIO_OUT[8];
  //   GPIO_OUT_9 = GPIO_OUT[9]; GPIO_OUT_10 = GPIO_OUT[10]; GPIO_OUT_11 = GPIO_OUT[11]; GPIO_OUT_12 = GPIO_OUT[12];
  //   GPIO_OUT_13 = GPIO_OUT[13]; GPIO_OUT_14 = GPIO_OUT[14]; GPIO_OUT_15 = GPIO_OUT[15]; GPIO_OUT_16 = GPIO_OUT[16];
  //   GPIO_OUT_17 = GPIO_OUT[17]; GPIO_OUT_18 = GPIO_OUT[18]; GPIO_OUT_19 = GPIO_OUT[19]; GPIO_OUT_20 = GPIO_OUT[20];
  //   GPIO_OUT_21 = GPIO_OUT[21]; sig_I2C_SCL_2 = I2C_SCL; sig_I2C_SDA_2 = I2C_SDA;
  //   CFG_IOMUX0_1_0[1:0] = CFG_IOMUX0[1:0]; iomux0[4:0] = CFG_IOMUX0[4:0]; CFG_IOMUX0_4_2[2:0] = CFG_IOMUX0[4:2];
  //   CFG_IOMUX0_6_5[1:0] = CFG_IOMUX0[6:5]; iomux1[4:0] = CFG_IOMUX0[9:5]; CFG_IOMUX0_9_7[2:0] = CFG_IOMUX0[9:7];
  //   CFG_IOMUX0_11_10[1:0] = CFG_IOMUX0[11:10]; iomux2[4:0] = CFG_IOMUX0[14:10];
  //   CFG_IOMUX0_14_12[2:0] = CFG_IOMUX0[14:12]; CFG_IOMUX0_16_15[1:0] = CFG_IOMUX0[16:15];
  //   iomux3[4:0] = CFG_IOMUX0[19:15]; CFG_IOMUX0_19_17[2:0] = CFG_IOMUX0[19:17];
  //   CFG_IOMUX0_21_20[1:0] = CFG_IOMUX0[21:20]; iomux4[4:0] = CFG_IOMUX0[24:20];
  //   CFG_IOMUX0_24_22[2:0] = CFG_IOMUX0[24:22]; CFG_IOMUX0_26_25[1:0] = CFG_IOMUX0[26:25];
  //   iomux5[4:0] = CFG_IOMUX0[29:25]; CFG_IOMUX0_29_27[2:0] = CFG_IOMUX0[29:27];
  //   CFG_IOMUX0_31_30[1:0] = CFG_IOMUX0[31:30]; iomux6[4:0] = {CFG_IOMUX1[2:0], CFG_IOMUX0[31:30]};
  //   CFG_IOMUX1_2_0[2:0] = CFG_IOMUX1[2:0]; CFG_IOMUX1_4_3[1:0] = CFG_IOMUX1[4:3]; iomux7[4:0] = CFG_IOMUX1[7:3];
  //   CFG_IOMUX1_7_5[2:0] = CFG_IOMUX1[7:5]; CFG_IOMUX1_9_8[1:0] = CFG_IOMUX1[9:8]; iomux8[4:0] = CFG_IOMUX1[12:8];
  //   CFG_IOMUX1_12_10[2:0] = CFG_IOMUX1[12:10]; CFG_IOMUX1_14_13[1:0] = CFG_IOMUX1[14:13];
  //   iomux9[4:0] = CFG_IOMUX1[17:13]; CFG_IOMUX1_17_15[2:0] = CFG_IOMUX1[17:15];
  //   CFG_IOMUX1_19_18[1:0] = CFG_IOMUX1[19:18]; iomux10[4:0] = CFG_IOMUX1[22:18];
  //   CFG_IOMUX1_22_20[2:0] = CFG_IOMUX1[22:20]; CFG_IOMUX1_24_23[1:0] = CFG_IOMUX1[24:23];
  //   iomux11[4:0] = CFG_IOMUX1[27:23]; CFG_IOMUX1_27_25[2:0] = CFG_IOMUX1[27:25];
  //   CFG_IOMUX1_29_28[1:0] = CFG_IOMUX1[29:28]; iomux12[4:0] = {CFG_IOMUX2[2:0], CFG_IOMUX1[29:28]};
  //   CFG_IOMUX2_2_0[2:0] = CFG_IOMUX2[2:0]; CFG_IOMUX2_4_3[1:0] = CFG_IOMUX2[4:3]; iomux13[4:0] = CFG_IOMUX2[7:3];
  //   CFG_IOMUX2_7_5[2:0] = CFG_IOMUX2[7:5]; CFG_IOMUX2_9_8[1:0] = CFG_IOMUX2[9:8]; iomux14[4:0] = CFG_IOMUX2[12:8];
  //   CFG_IOMUX2_12_10[2:0] = CFG_IOMUX2[12:10]; CFG_IOMUX2_14_13[1:0] = CFG_IOMUX2[14:13];
  //   iomux15[4:0] = CFG_IOMUX2[17:13]; CFG_IOMUX2_17_15[2:0] = CFG_IOMUX2[17:15];
  //   CFG_IOMUX2_19_18[1:0] = CFG_IOMUX2[19:18]; iomux16[4:0] = CFG_IOMUX2[22:18];
  //   CFG_IOMUX2_22_20[2:0] = CFG_IOMUX2[22:20]; CFG_IOMUX2_24_23[1:0] = CFG_IOMUX2[24:23];
  //   iomux17[4:0] = CFG_IOMUX2[27:23]; CFG_IOMUX2_27_25[2:0] = CFG_IOMUX2[27:25];
  //   CFG_IOMUX2_29_28[1:0] = CFG_IOMUX2[29:28]; iomux18[4:0] = {CFG_IOMUX3[2:0], CFG_IOMUX2[29:28]};
  //   CFG_IOMUX3_2_0[2:0] = CFG_IOMUX3[2:0]; CFG_IOMUX3_4_3[1:0] = CFG_IOMUX3[4:3]; iomux19[4:0] = CFG_IOMUX3[7:3];
  //   CFG_IOMUX3_7_5[2:0] = CFG_IOMUX3[7:5]; CFG_IOMUX3_9_8[1:0] = CFG_IOMUX3[9:8]; iomux20[4:0] = CFG_IOMUX3[12:8];
  //   CFG_IOMUX3_12_10[2:0] = CFG_IOMUX3[12:10]; CFG_IOMUX3_14_13[1:0] = CFG_IOMUX3[14:13];
  //   iomux21[4:0] = CFG_IOMUX3[17:13]; CFG_IOMUX3_17_15[2:0] = CFG_IOMUX3[17:15]; not250 = IRQ; not252 = IRQ_NMI;
  //   pads_salida[21:0] = PAD_OUT; or292[31:0] = RD;
  //   senales_perifericos[12:0] = {SIG_FSPICS0, SIG_FSPID, SIG_FSPICLK, SIG_I2C_SDA, SIG_I2C_SCL, SIG_LEDC5, SIG_LEDC4, SIG_LEDC3, SIG_LEDC2, SIG_LEDC1, SIG_LEDC0, SIG_U1TXD, SIG_U0TXD};
  //   sinc2[21:0] = {in21, in20, in19, in18, in17, in16, in15, in14, in13, in12, in11, in10, in9, in8, in7, in6, in5, in4, in3, in2, in1, in0};
  //   CFG_PIN0_3_1[2:0] = CFG_PIN0[3:1]; CFG_PIN0_3_1_0 = CFG_PIN0[1];
  //   tipo_int_b0[21:0] = {CFG_PIN4[6], CFG_PIN4[0], CFG_PIN3[24], CFG_PIN3[18], CFG_PIN3[12], CFG_PIN3[6], CFG_PIN3[0], CFG_PIN2[24], CFG_PIN2[18], CFG_PIN2[12], CFG_PIN2[6], CFG_PIN2[0], CFG_PIN1[24], CFG_PIN1[18], CFG_PIN1[12], CFG_PIN1[6], CFG_PIN1[0], CFG_PIN0[25], CFG_PIN0[19], CFG_PIN0[13], CFG_PIN0[7], CFG_PIN0[1]};
  //   CFG_PIN0_9_7[2:0] = CFG_PIN0[9:7]; CFG_PIN0_9_7_0 = CFG_PIN0[7]; CFG_PIN0_15_13[2:0] = CFG_PIN0[15:13];
  //   CFG_PIN0_15_13_0 = CFG_PIN0[13]; CFG_PIN0_21_19[2:0] = CFG_PIN0[21:19]; CFG_PIN0_21_19_0 = CFG_PIN0[19];
  //   CFG_PIN0_27_25[2:0] = CFG_PIN0[27:25]; CFG_PIN0_27_25_0 = CFG_PIN0[25]; CFG_PIN1_2_0[2:0] = CFG_PIN1[2:0];
  //   CFG_PIN1_2_0_0 = CFG_PIN1[0]; CFG_PIN1_8_6[2:0] = CFG_PIN1[8:6]; CFG_PIN1_8_6_0 = CFG_PIN1[6];
  //   CFG_PIN1_14_12[2:0] = CFG_PIN1[14:12]; CFG_PIN1_14_12_0 = CFG_PIN1[12]; CFG_PIN1_20_18[2:0] = CFG_PIN1[20:18];
  //   CFG_PIN1_20_18_0 = CFG_PIN1[18]; CFG_PIN1_26_24[2:0] = CFG_PIN1[26:24]; CFG_PIN1_26_24_0 = CFG_PIN1[24];
  //   CFG_PIN2_2_0[2:0] = CFG_PIN2[2:0]; CFG_PIN2_2_0_0 = CFG_PIN2[0]; CFG_PIN2_8_6[2:0] = CFG_PIN2[8:6];
  //   CFG_PIN2_8_6_0 = CFG_PIN2[6]; CFG_PIN2_14_12[2:0] = CFG_PIN2[14:12]; CFG_PIN2_14_12_0 = CFG_PIN2[12];
  //   CFG_PIN2_20_18[2:0] = CFG_PIN2[20:18]; CFG_PIN2_20_18_0 = CFG_PIN2[18]; CFG_PIN2_26_24[2:0] = CFG_PIN2[26:24];
  //   CFG_PIN2_26_24_0 = CFG_PIN2[24]; CFG_PIN3_2_0[2:0] = CFG_PIN3[2:0]; CFG_PIN3_2_0_0 = CFG_PIN3[0];
  //   CFG_PIN3_8_6[2:0] = CFG_PIN3[8:6]; CFG_PIN3_8_6_0 = CFG_PIN3[6]; CFG_PIN3_14_12[2:0] = CFG_PIN3[14:12];
  //   CFG_PIN3_14_12_0 = CFG_PIN3[12]; CFG_PIN3_20_18[2:0] = CFG_PIN3[20:18]; CFG_PIN3_20_18_0 = CFG_PIN3[18];
  //   CFG_PIN3_26_24[2:0] = CFG_PIN3[26:24]; CFG_PIN3_26_24_0 = CFG_PIN3[24]; CFG_PIN4_2_0[2:0] = CFG_PIN4[2:0];
  //   CFG_PIN4_2_0_0 = CFG_PIN4[0]; CFG_PIN4_8_6[2:0] = CFG_PIN4[8:6]; CFG_PIN4_8_6_0 = CFG_PIN4[6];
  //   CFG_PIN0_3_1_1 = CFG_PIN0[2];
  //   tipo_int_b1[21:0] = {CFG_PIN4[7], CFG_PIN4[1], CFG_PIN3[25], CFG_PIN3[19], CFG_PIN3[13], CFG_PIN3[7], CFG_PIN3[1], CFG_PIN2[25], CFG_PIN2[19], CFG_PIN2[13], CFG_PIN2[7], CFG_PIN2[1], CFG_PIN1[25], CFG_PIN1[19], CFG_PIN1[13], CFG_PIN1[7], CFG_PIN1[1], CFG_PIN0[26], CFG_PIN0[20], CFG_PIN0[14], CFG_PIN0[8], CFG_PIN0[2]};
  //   CFG_PIN0_9_7_1 = CFG_PIN0[8]; CFG_PIN0_15_13_1 = CFG_PIN0[14]; CFG_PIN0_21_19_1 = CFG_PIN0[20];
  //   CFG_PIN0_27_25_1 = CFG_PIN0[26]; CFG_PIN1_2_0_1 = CFG_PIN1[1]; CFG_PIN1_8_6_1 = CFG_PIN1[7];
  //   CFG_PIN1_14_12_1 = CFG_PIN1[13]; CFG_PIN1_20_18_1 = CFG_PIN1[19]; CFG_PIN1_26_24_1 = CFG_PIN1[25];
  //   CFG_PIN2_2_0_1 = CFG_PIN2[1]; CFG_PIN2_8_6_1 = CFG_PIN2[7]; CFG_PIN2_14_12_1 = CFG_PIN2[13];
  //   CFG_PIN2_20_18_1 = CFG_PIN2[19]; CFG_PIN2_26_24_1 = CFG_PIN2[25]; CFG_PIN3_2_0_1 = CFG_PIN3[1];
  //   CFG_PIN3_8_6_1 = CFG_PIN3[7]; CFG_PIN3_14_12_1 = CFG_PIN3[13]; CFG_PIN3_20_18_1 = CFG_PIN3[19];
  //   CFG_PIN3_26_24_1 = CFG_PIN3[25]; CFG_PIN4_2_0_1 = CFG_PIN4[1]; CFG_PIN4_8_6_1 = CFG_PIN4[7];
  //   CFG_PIN0_3_1_2 = CFG_PIN0[3];
  //   tipo_int_b2[21:0] = {CFG_PIN4[8], CFG_PIN4[2], CFG_PIN3[26], CFG_PIN3[20], CFG_PIN3[14], CFG_PIN3[8], CFG_PIN3[2], CFG_PIN2[26], CFG_PIN2[20], CFG_PIN2[14], CFG_PIN2[8], CFG_PIN2[2], CFG_PIN1[26], CFG_PIN1[20], CFG_PIN1[14], CFG_PIN1[8], CFG_PIN1[2], CFG_PIN0[27], CFG_PIN0[21], CFG_PIN0[15], CFG_PIN0[9], CFG_PIN0[3]};
  //   CFG_PIN0_9_7_2 = CFG_PIN0[9]; CFG_PIN0_15_13_2 = CFG_PIN0[15]; CFG_PIN0_21_19_2 = CFG_PIN0[21];
  //   CFG_PIN0_27_25_2 = CFG_PIN0[27]; CFG_PIN1_2_0_2 = CFG_PIN1[2]; CFG_PIN1_8_6_2 = CFG_PIN1[8];
  //   CFG_PIN1_14_12_2 = CFG_PIN1[14]; CFG_PIN1_20_18_2 = CFG_PIN1[20]; CFG_PIN1_26_24_2 = CFG_PIN1[26];
  //   CFG_PIN2_2_0_2 = CFG_PIN2[2]; CFG_PIN2_8_6_2 = CFG_PIN2[8]; CFG_PIN2_14_12_2 = CFG_PIN2[14];
  //   CFG_PIN2_20_18_2 = CFG_PIN2[20]; CFG_PIN2_26_24_2 = CFG_PIN2[26]; CFG_PIN3_2_0_2 = CFG_PIN3[2];
  //   CFG_PIN3_8_6_2 = CFG_PIN3[8]; CFG_PIN3_14_12_2 = CFG_PIN3[14]; CFG_PIN3_20_18_2 = CFG_PIN3[20];
  //   CFG_PIN3_26_24_2 = CFG_PIN3[26]; CFG_PIN4_2_0_2 = CFG_PIN4[2]; CFG_PIN4_8_6_2 = CFG_PIN4[8]; sig_U0RXD = U0RXD;
  //   sig_U1RXD = U1RXD

  // Notes on the sheet:
  //   contents of REGISTROS_GPIO_EXISTE (hex, n*v repeats v):
  //   1 6*0 1 21*0 22*1 34*0 128*1 128*0 22*1 32*0 1 51*0 1
  //   contents of REGISTROS_GPIO_VALOR_RESET (hex, n*v repeats v):
  //   341*0 22*80 32*0 1 51*0 2006130
  //   contents of REGISTROS_GPIO_BITS_RW (hex, n*v repeats v):
  //   ffffffff 6*0 ff 21*0 22*3ff9f 34*0 128*7f 128*0 22*7ff 32*0 1 51*0 fffffff
  //   contents of REGISTROS_IOMUX_EXISTE (hex, n*v repeats v):
  //   23*1
  //   contents of REGISTROS_IOMUX_VALOR_RESET (hex, n*v repeats v):
  //   7ff 800 800 7*a00 b00 a00 a00 6*b00 a00 a00 b00 a00
  //   contents of REGISTROS_IOMUX_BITS_RW (hex, n*v repeats v):
  //   ffffffff 22*ffff
endmodule

module WatchdogEtapas (
  input  CLK,
  input  RST,
  input  EN,
  input  FEED,
  input  [15:0] PRESCALE,
  input  [7:0] STG,
  input  [31:0] HOLD0,
  input  [31:0] HOLD1,
  input  [31:0] HOLD2,
  input  [31:0] HOLD3,
  output INT,
  output RESET_CPU,
  output RESET_SIS
);

  wire actua, eq16, eq18, eq20, eq22, lt3, lt8, not1, not4, not9, not17, or5, or10, or12, or15, reinicia,
       tick, vence_etapa;
  wire [1:0] accion, etapa, mux14, sum13;
  wire [15:0] mux6, preescalador, sum2;
  wire [31:0] cuenta, limite_etapa, mux11, sum7;

  not not_1 (not1, EN);
  Register #(.width(16)) PREESC (.D(mux6), .en(1'b1), .Q(preescalador), .clk(CLK), .clr(RST));
  Register #(.width(32)) u_CUENTA (.D(mux11), .en(or12), .Q(cuenta), .clk(CLK), .clr(RST));
  Register #(.width(2)) u_ETAPA (.D(mux14), .en(or15), .Q(etapa), .clk(CLK), .clr(RST));
  or or_1 (reinicia, FEED, not1);
  Adder #(.width(16)) adder_1 (.a(preescalador), .b(16'h1), .out(sum2));  // open: cin, cout
  Multiplexer #(.select(2), .width(32), .enable("false")) multiplexer_1 (
    .in0(HOLD0), .in1(HOLD1), .in2(HOLD2), .in3(HOLD3), .out(limite_etapa), .sel(etapa));
  Adder #(.width(32)) adder_2 (.a(cuenta), .b(32'h1), .out(sum7));  // open: cin, cout
  Multiplexer #(.select(2), .width(2), .enable("false")) multiplexer_2 (
    .in0(STG[1:0]), .in1(STG[3:2]), .in2(STG[5:4]), .in3(STG[7:6]), .out(accion), .sel(etapa));
  Adder #(.width(2)) adder_3 (.a(etapa), .b(2'b01), .out(sum13));  // open: cin, cout
  Comparator #(.width(16), .mode("unsigned")) comparator_1 (.a(sum2), .b(PRESCALE), .lt(lt3));  // open: gt, eq
  Multiplexer #(.select(1), .width(2), .enable("false")) multiplexer_3 (
    .in0(sum13), .in1(2'b00), .out(mux14), .sel(reinicia));
  Comparator #(.width(2), .mode("unsigned")) comparator_2 (.a(accion), .b(2'b00), .eq(eq16));  // open: gt, lt
  Comparator #(.width(2), .mode("unsigned")) comparator_3 (.a(accion), .b(2'b01), .eq(eq18));  // open: gt, lt
  Comparator #(.width(2), .mode("unsigned")) comparator_4 (.a(accion), .b(2'b10), .eq(eq20));  // open: gt, lt
  Comparator #(.width(2), .mode("unsigned")) comparator_5 (.a(accion), .b(2'b11), .eq(eq22));  // open: gt, lt
  Comparator #(.width(32), .mode("unsigned")) comparator_6 (.a(sum7), .b(limite_etapa), .lt(lt8));  // open: gt, eq
  not not_2 (not4, lt3);
  not not_3 (not9, lt8);
  not not_4 (not17, eq16);
  and and_1 (tick, EN, not4);
  and and_2 (vence_etapa, tick, not9);
  or or_2 (or5, tick, reinicia);
  or or_3 (or12, tick, reinicia);
  Multiplexer #(.select(1), .width(16), .enable("false")) multiplexer_4 (
    .in0(sum2), .in1({16{1'b0}}), .out(mux6), .sel(or5));
  or or_4 (or10, vence_etapa, reinicia);
  or or_5 (or15, vence_etapa, reinicia);
  and and_3 (actua, vence_etapa, not17);
  Multiplexer #(.select(1), .width(32), .enable("false")) multiplexer_5 (
    .in0(sum7), .in1({32{1'b0}}), .out(mux11), .sel(or10));
  and and_4 (INT, actua, eq18);
  and and_5 (RESET_CPU, actua, eq20);
  and and_6 (RESET_SIS, actua, eq22);

  // Other names for the same wires on the sheet: and19 = INT; and21 = RESET_CPU; and23 = RESET_SIS;
  //   STG_1_0[1:0] = STG[1:0]; STG_3_2[1:0] = STG[3:2]; STG_5_4[1:0] = STG[5:4]; STG_7_6[1:0] = STG[7:6]
endmodule

module SYSTIMER (
  input  CLK,
  input  RST,
  input  SEL,
  input  [9:0] A,
  input  [31:0] WD,
  input  WE,
  input  RE,
  output IRQ_T0,
  output IRQ_T1,
  output IRQ_T2,
  output [31:0] RD
);

  wire and5, and6, and7, and11, and12, and13, and18, and29, and35, and39, and43, and54, and60, and64, and68,
       and79, and85, and89, and101, co22, co24, co47, co49, co72, co74, eq26, eq51, eq76, eq97, esc_000,
       esc_00C, esc_0FC, esc_01C, esc_02C, esc_03C, esc_004, esc_05C, esc_06C, esc_008, esc_010, esc_014,
       esc_018, esc_020, esc_024, esc_028, esc_030, esc_034, esc_038, esc_050, esc_054, esc_058, esc_060,
       esc_064, escribe, gt25, gt50, gt75, INT_irq, lee, lin_0, lin_1, lin_2, lin_3, lin_4, lin_5, lin_6,
       lin_7, lin_8, lin_9, lin_10, lin_11, lin_12, lin_13, lin_14, lin_15, lin_16, lin_17, lin_18, lin_19,
       lin_20, lin_21, lin_22, lin_23, lin_24, lin_25, lin_26, lin_27, lin_28, lin_29, lin_30, lin_31, lt27,
       lt52, lt77, mux37, mux62, mux87, not28, not30, not38, not53, not55, not63, not78, not80, not88, or36,
       or40, or61, or65, or86, or90, pag_0, pag_1, pag_2, pag_3, pag_4, pag_5, pag_6, pag_7, pag_8, pag_9,
       pag_10, pag_11, pag_12, pag_13, pag_14, pag_15, pag_16, pag_17, pag_18, pag_19, pag_20, pag_21,
       pag_22, pag_23, pag_24, pag_25, pag_26, pag_27, pag_28, pag_29, pag_30, pag_31, r000, r00C, r0FC,
       r01C, r02C, r03C, r004, r04C, r05C, r06C, r008, r010, r014, r018, r020, r024, r028, r030, r034, r038,
       r040, r044, r048, r050, r054, r058, r060, r064, r068, r070, T0_alcanzado, T0_disparado,
       T0_modo_periodo, T0_unidad, T1_alcanzado, T1_disparado, T1_modo_periodo, T1_unidad, T2_alcanzado,
       T2_disparado, T2_modo_periodo, T2_unidad, U0_cuenta_hi_max, U0_cuenta_lo_max, U1_cuenta_hi_max,
       U1_cuenta_lo_max;
  wire [2:0] INT_eventos;
  wire [9:0] dir_registro, rep100;
  wire [19:0] mux19, mux31, mux32, mux44, mux56, mux57, mux69, mux81, mux82, T0_cnt_hi, T0_obj_hi,
       T0_primero_hi, T0_siguiente_hi, T1_cnt_hi, T1_obj_hi, T1_primero_hi, T1_siguiente_hi, T2_cnt_hi,
       T2_obj_hi, T2_primero_hi, T2_siguiente_hi, U0_cuenta_hi, U0_VALUE_HI, U1_cuenta_hi, U1_VALUE_HI;
  wire [25:0] T0_periodo, T1_periodo, T2_periodo;
  wire [29:29] cat8, cat14;
  wire [31:0] and1, and4, and10, and16, and17, and41, and42, and66, and67, and93, and95, and96, and104,
       and106, and108, and110, and112, and114, and116, and118, and120, and122, and124, and126, and128,
       and130, and132, and134, and136, and138, and140, and142, and144, and146, and148, and150, CONF, DATE,
       dato_escrito, INT_clr, INT_ENA, INT_raw, mux20, mux33, mux34, mux45, mux58, mux59, mux70, mux83,
       mux84, not92, or94, qx3, qx99, rep91, rep102, rep103, rep105, rep107, rep109, rep111, rep113, rep115,
       rep117, rep119, rep121, rep123, rep125, rep127, rep129, rep131, rep133, rep135, rep137, rep139,
       rep141, rep143, rep145, rep147, rep149, T0_cnt_lo, T0_CONF, T0_HI, T0_LO, T0_obj_lo, T0_primero_lo,
       T0_siguiente_lo, T1_cnt_lo, T1_CONF, T1_HI, T1_LO, T1_obj_lo, T1_primero_lo, T1_siguiente_lo,
       T2_cnt_lo, T2_CONF, T2_HI, T2_LO, T2_obj_lo, T2_primero_lo, T2_siguiente_lo, U0_cuenta_lo, U0_LOAD_HI,
       U0_LOAD_LO, U0_VALUE_LO, U1_cuenta_lo, U1_LOAD_HI, U1_LOAD_LO, U1_VALUE_LO, xor2, xor98, zx9, zx15,
       zx21, zx23, zx46, zx48, zx71, zx73;
  wire [31:3] INT_st;

  Register #(.width(32)) u_CONF (.D(xor2), .en(esc_000), .Q(qx3), .clk(CLK), .clr(RST));
  Register #(.width(32)) u_U0_LOAD_HI (.D(and4), .en(esc_00C), .Q(U0_LOAD_HI), .clk(CLK), .clr(RST));
  Counter #(.width(32), .max('hffffffff), .ongoal("wrap")) u_U0_cuenta_lo (
    .load(and5), .D(U0_LOAD_LO), .count(CONF[30]), .Q(U0_cuenta_lo), .carry(U0_cuenta_lo_max), .up(1'b1),
    .clk(CLK), .clr(RST));
  Register #(.width(1)) U0_VALID (.D(1'b1), .en(and7), .Q(cat8[29]), .clk(CLK), .clr(RST));
  Register #(.width(32)) u_U1_LOAD_HI (.D(and10), .en(esc_014), .Q(U1_LOAD_HI), .clk(CLK), .clr(RST));
  Counter #(.width(32), .max('hffffffff), .ongoal("wrap")) u_U1_cuenta_lo (
    .load(and11), .D(U1_LOAD_LO), .count(CONF[29]), .Q(U1_cuenta_lo), .carry(U1_cuenta_lo_max), .up(1'b1),
    .clk(CLK), .clr(RST));
  Register #(.width(1)) U1_VALID (.D(1'b1), .en(and13), .Q(cat14[29]), .clk(CLK), .clr(RST));
  Register #(.width(32)) u_T0_HI (.D(and16), .en(esc_01C), .Q(T0_HI), .clk(CLK), .clr(RST));
  Register #(.width(32)) u_T0_CONF (.D(and17), .en(esc_034), .Q(T0_CONF), .clk(CLK), .clr(RST));
  Register #(.width(1)) T0_MODO (.D(T0_CONF[30]), .en(and18), .Q(T0_modo_periodo), .clk(CLK), .clr(RST));
  Register #(.width(1)) u_T0_UNIDAD (.D(T0_CONF[31]), .en(and18), .Q(T0_unidad), .clk(CLK), .clr(RST));
  Register #(.width(32)) u_U0_LOAD_LO (.D(dato_escrito), .en(esc_010), .Q(U0_LOAD_LO), .clk(CLK), .clr(RST));
  Counter #(.width(20), .max('hfffff), .ongoal("wrap")) u_U0_cuenta_hi (
    .load(and5), .D(U0_LOAD_HI[19:0]), .count(and6), .Q(U0_cuenta_hi), .carry(U0_cuenta_hi_max), .up(1'b1),
    .clk(CLK), .clr(RST));
  Register #(.width(20)) u_U0_VALUE_HI (.D(U0_cuenta_hi), .en(and7), .Q(U0_VALUE_HI), .clk(CLK), .clr(RST));
  Register #(.width(32)) u_U0_VALUE_LO (.D(U0_cuenta_lo), .en(and7), .Q(U0_VALUE_LO), .clk(CLK), .clr(RST));
  Register #(.width(32)) u_U1_LOAD_LO (.D(dato_escrito), .en(esc_018), .Q(U1_LOAD_LO), .clk(CLK), .clr(RST));
  Counter #(.width(20), .max('hfffff), .ongoal("wrap")) u_U1_cuenta_hi (
    .load(and11), .D(U1_LOAD_HI[19:0]), .count(and12), .Q(U1_cuenta_hi), .carry(U1_cuenta_hi_max), .up(1'b1),
    .clk(CLK), .clr(RST));
  Register #(.width(20)) u_U1_VALUE_HI (.D(U1_cuenta_hi), .en(and13), .Q(U1_VALUE_HI), .clk(CLK), .clr(RST));
  Register #(.width(32)) u_U1_VALUE_LO (.D(U1_cuenta_lo), .en(and13), .Q(U1_VALUE_LO), .clk(CLK), .clr(RST));
  Register #(.width(32)) u_T0_LO (.D(dato_escrito), .en(esc_020), .Q(T0_LO), .clk(CLK), .clr(RST));
  Register #(.width(26)) u_T0_PERIODO (.D(T0_CONF[25:0]), .en(and18), .Q(T0_periodo), .clk(CLK), .clr(RST));
  Register #(.width(20)) u_T0_OBJ_HI (.D(mux32), .en(or36), .Q(T0_obj_hi), .clk(CLK), .clr(RST));
  Register #(.width(32)) u_T0_OBJ_LO (.D(mux34), .en(or36), .Q(T0_obj_lo), .clk(CLK), .clr(RST));
  Register #(.width(1)) T0_FIRED (.D(mux37), .en(or40), .Q(T0_disparado), .clk(CLK), .clr(RST));
  Register #(.width(32)) u_T1_HI (.D(and41), .en(esc_024), .Q(T1_HI), .clk(CLK), .clr(RST));
  Register #(.width(32)) u_T1_CONF (.D(and42), .en(esc_038), .Q(T1_CONF), .clk(CLK), .clr(RST));
  Register #(.width(1)) T1_MODO (.D(T1_CONF[30]), .en(and43), .Q(T1_modo_periodo), .clk(CLK), .clr(RST));
  Register #(.width(1)) u_T1_UNIDAD (.D(T1_CONF[31]), .en(and43), .Q(T1_unidad), .clk(CLK), .clr(RST));
  Register #(.width(20)) u_T1_OBJ_HI (.D(mux57), .en(or61), .Q(T1_obj_hi), .clk(CLK), .clr(RST));
  Register #(.width(32)) u_T1_OBJ_LO (.D(mux59), .en(or61), .Q(T1_obj_lo), .clk(CLK), .clr(RST));
  Register #(.width(1)) T1_FIRED (.D(mux62), .en(or65), .Q(T1_disparado), .clk(CLK), .clr(RST));
  Register #(.width(32)) u_T2_HI (.D(and66), .en(esc_02C), .Q(T2_HI), .clk(CLK), .clr(RST));
  Register #(.width(32)) u_T2_CONF (.D(and67), .en(esc_03C), .Q(T2_CONF), .clk(CLK), .clr(RST));
  Register #(.width(1)) T2_MODO (.D(T2_CONF[30]), .en(and68), .Q(T2_modo_periodo), .clk(CLK), .clr(RST));
  Register #(.width(1)) u_T2_UNIDAD (.D(T2_CONF[31]), .en(and68), .Q(T2_unidad), .clk(CLK), .clr(RST));
  Register #(.width(20)) u_T2_OBJ_HI (.D(mux82), .en(or86), .Q(T2_obj_hi), .clk(CLK), .clr(RST));
  Register #(.width(32)) u_T2_OBJ_LO (.D(mux84), .en(or86), .Q(T2_obj_lo), .clk(CLK), .clr(RST));
  Register #(.width(1)) T2_FIRED (.D(mux87), .en(or90), .Q(T2_disparado), .clk(CLK), .clr(RST));
  Register #(.width(32)) u_INT_RAW (.D(and95), .en(1'b1), .Q(INT_raw), .clk(CLK), .clr(RST));
  Register #(.width(32)) u_T1_LO (.D(dato_escrito), .en(esc_028), .Q(T1_LO), .clk(CLK), .clr(RST));
  Register #(.width(26)) u_T1_PERIODO (.D(T1_CONF[25:0]), .en(and43), .Q(T1_periodo), .clk(CLK), .clr(RST));
  Register #(.width(32)) u_T2_LO (.D(dato_escrito), .en(esc_030), .Q(T2_LO), .clk(CLK), .clr(RST));
  Register #(.width(26)) u_T2_PERIODO (.D(T2_CONF[25:0]), .en(and68), .Q(T2_periodo), .clk(CLK), .clr(RST));
  and and_1 (and101, SEL, WE);
  and and_2 (escribe, WE, SEL);
  and and_3 (lee, RE, SEL);
  Register #(.width(32)) u_INT_ENA (.D(and96), .en(esc_064), .Q(INT_ENA), .clk(CLK), .clr(RST));
  Register #(.width(32)) u_DATE (.D(xor98), .en(esc_0FC), .Q(qx99), .clk(CLK), .clr(RST));
  assign rep100 = {{9{SEL}}, SEL};  // Bit_Extender bit_extender_1
  assign CONF = qx3 ^ 32'h46000000;  // XOR_Gate xor_1, 32 bits wide
  assign zx9 = {{12{1'b0}}, U0_VALUE_HI};  // Bit_Extender bit_extender_2
  assign zx15 = {{12{1'b0}}, U1_VALUE_HI};  // Bit_Extender bit_extender_3
  Multiplexer #(.select(1), .width(20), .enable("false")) multiplexer_1 (
    .in0(U0_cuenta_hi), .in1(U1_cuenta_hi), .out(T0_cnt_hi), .sel(T0_unidad));
  Multiplexer #(.select(1), .width(32), .enable("false")) multiplexer_2 (
    .in0(U0_cuenta_lo), .in1(U1_cuenta_lo), .out(T0_cnt_lo), .sel(T0_unidad));
  assign zx23 = {{6{1'b0}}, T0_periodo};  // Bit_Extender bit_extender_4
  not not_1 (not30, T0_disparado);
  not not_2 (not38, T0_modo_periodo);
  Multiplexer #(.select(1), .width(20), .enable("false")) multiplexer_3 (
    .in0(U0_cuenta_hi), .in1(U1_cuenta_hi), .out(T1_cnt_hi), .sel(T1_unidad));
  Multiplexer #(.select(1), .width(32), .enable("false")) multiplexer_4 (
    .in0(U0_cuenta_lo), .in1(U1_cuenta_lo), .out(T1_cnt_lo), .sel(T1_unidad));
  assign zx48 = {{6{1'b0}}, T1_periodo};  // Bit_Extender bit_extender_5
  not not_3 (not55, T1_disparado);
  not not_4 (not63, T1_modo_periodo);
  Multiplexer #(.select(1), .width(20), .enable("false")) multiplexer_5 (
    .in0(U0_cuenta_hi), .in1(U1_cuenta_hi), .out(T2_cnt_hi), .sel(T2_unidad));
  Multiplexer #(.select(1), .width(32), .enable("false")) multiplexer_6 (
    .in0(U0_cuenta_lo), .in1(U1_cuenta_lo), .out(T2_cnt_lo), .sel(T2_unidad));
  assign zx73 = {{6{1'b0}}, T2_periodo};  // Bit_Extender bit_extender_6
  not not_5 (not80, T2_disparado);
  not not_6 (not88, T2_modo_periodo);
  assign {INT_st, IRQ_T2, IRQ_T1, IRQ_T0} = INT_raw & INT_ENA;  // AND_Gate and_4, 32 bits wide
  assign DATE = qx99 ^ 32'h2006171;  // XOR_Gate xor_2, 32 bits wide
  assign dir_registro = A & rep100;  // AND_Gate and_5, 10 bits wide
  assign rep102 = {{31{and101}}, and101};  // Bit_Extender bit_extender_7
  assign dato_escrito = WD & rep102;  // AND_Gate and_6, 32 bits wide
  Multiplexer #(.select(1), .width(20), .enable("false")) multiplexer_7 (
    .in0(U0_cuenta_hi), .in1(U1_cuenta_hi), .out(mux19), .sel(T0_CONF[31]));
  Multiplexer #(.select(1), .width(32), .enable("false")) multiplexer_8 (
    .in0(U0_cuenta_lo), .in1(U1_cuenta_lo), .out(mux20), .sel(T0_CONF[31]));
  assign zx21 = {{6{1'b0}}, T0_CONF[25:0]};  // Bit_Extender bit_extender_8
  Adder #(.width(32)) adder_1 (.a(T0_obj_lo), .b(zx23), .out(T0_siguiente_lo), .cout(co24));  // open: cin
  Comparator #(.width(20), .mode("unsigned")) comparator_1 (.a(T0_cnt_hi), .b(T0_obj_hi), .gt(gt25));  // open: eq, lt
  Comparator #(.width(20), .mode("unsigned")) comparator_2 (.a(T0_cnt_hi), .b(T0_obj_hi), .eq(eq26));  // open: gt, lt
  Comparator #(.width(32), .mode("unsigned")) comparator_3 (.a(T0_cnt_lo), .b(T0_obj_lo), .lt(lt27));  // open: gt, eq
  Multiplexer #(.select(1), .width(20), .enable("false")) multiplexer_9 (
    .in0(U0_cuenta_hi), .in1(U1_cuenta_hi), .out(mux44), .sel(T1_CONF[31]));
  Multiplexer #(.select(1), .width(32), .enable("false")) multiplexer_10 (
    .in0(U0_cuenta_lo), .in1(U1_cuenta_lo), .out(mux45), .sel(T1_CONF[31]));
  assign zx46 = {{6{1'b0}}, T1_CONF[25:0]};  // Bit_Extender bit_extender_9
  Adder #(.width(32)) adder_2 (.a(T1_obj_lo), .b(zx48), .out(T1_siguiente_lo), .cout(co49));  // open: cin
  Comparator #(.width(20), .mode("unsigned")) comparator_4 (.a(T1_cnt_hi), .b(T1_obj_hi), .gt(gt50));  // open: eq, lt
  Comparator #(.width(20), .mode("unsigned")) comparator_5 (.a(T1_cnt_hi), .b(T1_obj_hi), .eq(eq51));  // open: gt, lt
  Comparator #(.width(32), .mode("unsigned")) comparator_6 (.a(T1_cnt_lo), .b(T1_obj_lo), .lt(lt52));  // open: gt, eq
  Multiplexer #(.select(1), .width(20), .enable("false")) multiplexer_11 (
    .in0(U0_cuenta_hi), .in1(U1_cuenta_hi), .out(mux69), .sel(T2_CONF[31]));
  Multiplexer #(.select(1), .width(32), .enable("false")) multiplexer_12 (
    .in0(U0_cuenta_lo), .in1(U1_cuenta_lo), .out(mux70), .sel(T2_CONF[31]));
  assign zx71 = {{6{1'b0}}, T2_CONF[25:0]};  // Bit_Extender bit_extender_10
  Adder #(.width(32)) adder_3 (.a(T2_obj_lo), .b(zx73), .out(T2_siguiente_lo), .cout(co74));  // open: cin
  Comparator #(.width(20), .mode("unsigned")) comparator_7 (.a(T2_cnt_hi), .b(T2_obj_hi), .gt(gt75));  // open: eq, lt
  Comparator #(.width(20), .mode("unsigned")) comparator_8 (.a(T2_cnt_hi), .b(T2_obj_hi), .eq(eq76));  // open: gt, lt
  Comparator #(.width(32), .mode("unsigned")) comparator_9 (.a(T2_cnt_lo), .b(T2_obj_lo), .lt(lt77));  // open: gt, eq
  Comparator #(.width(32), .mode("unsigned")) comparator_10 (
    .a({INT_st, IRQ_T2, IRQ_T1, IRQ_T0}), .b({32{1'b0}}), .eq(eq97));  // open: gt, lt
  Decoder #(.select(5), .enable("false")) decoder_1 (
    .out0(pag_0), .out1(pag_1), .out2(pag_2), .out3(pag_3), .out4(pag_4), .out5(pag_5), .out6(pag_6),
    .out7(pag_7), .out8(pag_8), .out9(pag_9), .out10(pag_10), .out11(pag_11), .out12(pag_12), .out13(pag_13),
    .out14(pag_14), .out15(pag_15), .out16(pag_16), .out17(pag_17), .out18(pag_18), .out19(pag_19),
    .out20(pag_20), .out21(pag_21), .out22(pag_22), .out23(pag_23), .out24(pag_24), .out25(pag_25),
    .out26(pag_26), .out27(pag_27), .out28(pag_28), .out29(pag_29), .out30(pag_30), .out31(pag_31),
    .sel(dir_registro[9:5]));
  Decoder #(.select(5), .enable("false")) decoder_2 (
    .out0(lin_0), .out1(lin_1), .out2(lin_2), .out3(lin_3), .out4(lin_4), .out5(lin_5), .out6(lin_6),
    .out7(lin_7), .out8(lin_8), .out9(lin_9), .out10(lin_10), .out11(lin_11), .out12(lin_12), .out13(lin_13),
    .out14(lin_14), .out15(lin_15), .out16(lin_16), .out17(lin_17), .out18(lin_18), .out19(lin_19),
    .out20(lin_20), .out21(lin_21), .out22(lin_22), .out23(lin_23), .out24(lin_24), .out25(lin_25),
    .out26(lin_26), .out27(lin_27), .out28(lin_28), .out29(lin_29), .out30(lin_30), .out31(lin_31),
    .sel(dir_registro[4:0]));
  Adder #(.width(32)) adder_4 (.a(mux20), .b(zx21), .out(T0_primero_lo), .cout(co22));  // open: cin
  not not_7 (not28, lt27);
  Adder #(.width(32)) adder_5 (.a(mux45), .b(zx46), .out(T1_primero_lo), .cout(co47));  // open: cin
  not not_8 (not53, lt52);
  Adder #(.width(32)) adder_6 (.a(mux70), .b(zx71), .out(T2_primero_lo), .cout(co72));  // open: cin
  not not_9 (not78, lt77);
  not not_10 (INT_irq, eq97);
  assign and1 = dato_escrito & 32'hffc00001;  // AND_Gate and_7, 32 bits wide
  assign and4 = dato_escrito & 32'hfffff;  // AND_Gate and_8, 32 bits wide
  and and_9 (and6, CONF[30], U0_cuenta_lo_max);
  assign and10 = dato_escrito & 32'hfffff;  // AND_Gate and_10, 32 bits wide
  and and_11 (and12, CONF[29], U1_cuenta_lo_max);
  assign and16 = dato_escrito & 32'hfffff;  // AND_Gate and_12, 32 bits wide
  assign and17 = dato_escrito & 32'hc3ffffff;  // AND_Gate and_13, 32 bits wide
  Adder #(.width(20)) adder_7 (.a(T0_obj_hi), .b({20{1'b0}}), .out(T0_siguiente_hi), .cin(co24));  // open: cout
  assign and41 = dato_escrito & 32'hfffff;  // AND_Gate and_14, 32 bits wide
  assign and42 = dato_escrito & 32'hc3ffffff;  // AND_Gate and_15, 32 bits wide
  Adder #(.width(20)) adder_8 (.a(T1_obj_hi), .b({20{1'b0}}), .out(T1_siguiente_hi), .cin(co49));  // open: cout
  assign and66 = dato_escrito & 32'hfffff;  // AND_Gate and_16, 32 bits wide
  assign and67 = dato_escrito & 32'hc3ffffff;  // AND_Gate and_17, 32 bits wide
  Adder #(.width(20)) adder_9 (.a(T2_obj_hi), .b({20{1'b0}}), .out(T2_siguiente_hi), .cin(co74));  // open: cout
  assign and96 = dato_escrito & 32'h7;  // AND_Gate and_18, 32 bits wide
  assign xor98 = dato_escrito ^ 32'h2006171;  // XOR_Gate xor_3, 32 bits wide
  and and_19 (r000, SEL, pag_0, lin_0);
  and and_20 (r00C, SEL, pag_0, lin_3);
  and and_21 (r010, SEL, pag_0, lin_4);
  and and_22 (r05C, SEL, pag_0, lin_23);
  and and_23 (r004, SEL, pag_0, lin_1);
  and and_24 (r014, SEL, pag_0, lin_5);
  and and_25 (r018, SEL, pag_0, lin_6);
  and and_26 (r060, SEL, pag_0, lin_24);
  and and_27 (r008, SEL, pag_0, lin_2);
  and and_28 (r01C, SEL, pag_0, lin_7);
  and and_29 (r020, SEL, pag_0, lin_8);
  and and_30 (r034, SEL, pag_0, lin_13);
  and and_31 (r050, SEL, pag_0, lin_20);
  Adder #(.width(20)) adder_10 (.a(mux19), .b({20{1'b0}}), .out(T0_primero_hi), .cin(co22));  // open: cout
  and and_32 (and29, eq26, not28);
  and and_33 (r024, SEL, pag_0, lin_9);
  and and_34 (r028, SEL, pag_0, lin_10);
  and and_35 (r038, SEL, pag_0, lin_14);
  and and_36 (r054, SEL, pag_0, lin_21);
  Adder #(.width(20)) adder_11 (.a(mux44), .b({20{1'b0}}), .out(T1_primero_hi), .cin(co47));  // open: cout
  and and_37 (and54, eq51, not53);
  and and_38 (r02C, SEL, pag_0, lin_11);
  and and_39 (r030, SEL, pag_0, lin_12);
  and and_40 (r03C, SEL, pag_0, lin_15);
  and and_41 (r058, SEL, pag_0, lin_22);
  Adder #(.width(20)) adder_12 (.a(mux69), .b({20{1'b0}}), .out(T2_primero_hi), .cin(co72));  // open: cout
  and and_42 (and79, eq76, not78);
  and and_43 (r06C, SEL, pag_0, lin_27);
  and and_44 (r064, SEL, pag_0, lin_25);
  and and_45 (r0FC, SEL, pag_1, lin_31);
  and and_46 (r040, SEL, pag_0, lin_16);
  and and_47 (r044, SEL, pag_0, lin_17);
  and and_48 (r048, SEL, pag_0, lin_18);
  and and_49 (r04C, SEL, pag_0, lin_19);
  and and_50 (r068, SEL, pag_0, lin_26);
  and and_51 (r070, SEL, pag_0, lin_28);
  assign xor2 = and1 ^ 32'h46000000;  // XOR_Gate xor_4, 32 bits wide
  Multiplexer #(.select(1), .width(32), .enable("false")) multiplexer_13 (
    .in0(T0_LO), .in1(T0_primero_lo), .out(mux33), .sel(T0_CONF[30]));
  Multiplexer #(.select(1), .width(32), .enable("false")) multiplexer_14 (
    .in0(T1_LO), .in1(T1_primero_lo), .out(mux58), .sel(T1_CONF[30]));
  Multiplexer #(.select(1), .width(32), .enable("false")) multiplexer_15 (
    .in0(T2_LO), .in1(T2_primero_lo), .out(mux83), .sel(T2_CONF[30]));
  and and_52 (esc_000, escribe, r000);
  and and_53 (esc_00C, escribe, r00C);
  and and_54 (esc_010, escribe, r010);
  and and_55 (esc_05C, escribe, r05C);
  and and_56 (esc_004, escribe, r004);
  and and_57 (esc_014, escribe, r014);
  and and_58 (esc_018, escribe, r018);
  and and_59 (esc_060, escribe, r060);
  and and_60 (esc_008, escribe, r008);
  and and_61 (esc_01C, escribe, r01C);
  and and_62 (esc_020, escribe, r020);
  and and_63 (esc_034, escribe, r034);
  and and_64 (esc_050, escribe, r050);
  or or_1 (T0_alcanzado, gt25, and29);
  Multiplexer #(.select(1), .width(20), .enable("false")) multiplexer_16 (
    .in0(T0_HI[19:0]), .in1(T0_primero_hi), .out(mux31), .sel(T0_CONF[30]));
  and and_65 (esc_024, escribe, r024);
  and and_66 (esc_028, escribe, r028);
  and and_67 (esc_038, escribe, r038);
  and and_68 (esc_054, escribe, r054);
  or or_2 (T1_alcanzado, gt50, and54);
  Multiplexer #(.select(1), .width(20), .enable("false")) multiplexer_17 (
    .in0(T1_HI[19:0]), .in1(T1_primero_hi), .out(mux56), .sel(T1_CONF[30]));
  and and_69 (esc_02C, escribe, r02C);
  and and_70 (esc_030, escribe, r030);
  and and_71 (esc_03C, escribe, r03C);
  and and_72 (esc_058, escribe, r058);
  or or_3 (T2_alcanzado, gt75, and79);
  Multiplexer #(.select(1), .width(20), .enable("false")) multiplexer_18 (
    .in0(T2_HI[19:0]), .in1(T2_primero_hi), .out(mux81), .sel(T2_CONF[30]));
  and and_73 (esc_06C, escribe, r06C);
  and and_74 (esc_064, escribe, r064);
  and and_75 (esc_0FC, escribe, r0FC);
  assign rep103 = {{31{r000}}, r000};  // Bit_Extender bit_extender_11
  assign rep105 = {{31{r00C}}, r00C};  // Bit_Extender bit_extender_12
  assign rep107 = {{31{r010}}, r010};  // Bit_Extender bit_extender_13
  assign rep109 = {{31{r004}}, r004};  // Bit_Extender bit_extender_14
  assign rep111 = {{31{r040}}, r040};  // Bit_Extender bit_extender_15
  assign rep113 = {{31{r044}}, r044};  // Bit_Extender bit_extender_16
  assign rep115 = {{31{r014}}, r014};  // Bit_Extender bit_extender_17
  assign rep117 = {{31{r018}}, r018};  // Bit_Extender bit_extender_18
  assign rep119 = {{31{r008}}, r008};  // Bit_Extender bit_extender_19
  assign rep121 = {{31{r048}}, r048};  // Bit_Extender bit_extender_20
  assign rep123 = {{31{r04C}}, r04C};  // Bit_Extender bit_extender_21
  assign rep125 = {{31{r01C}}, r01C};  // Bit_Extender bit_extender_22
  assign rep127 = {{31{r020}}, r020};  // Bit_Extender bit_extender_23
  assign rep129 = {{31{r034}}, r034};  // Bit_Extender bit_extender_24
  assign rep131 = {{31{r024}}, r024};  // Bit_Extender bit_extender_25
  assign rep133 = {{31{r028}}, r028};  // Bit_Extender bit_extender_26
  assign rep135 = {{31{r038}}, r038};  // Bit_Extender bit_extender_27
  assign rep137 = {{31{r02C}}, r02C};  // Bit_Extender bit_extender_28
  assign rep139 = {{31{r030}}, r030};  // Bit_Extender bit_extender_29
  assign rep141 = {{31{r03C}}, r03C};  // Bit_Extender bit_extender_30
  assign rep143 = {{31{r064}}, r064};  // Bit_Extender bit_extender_31
  assign rep145 = {{31{r068}}, r068};  // Bit_Extender bit_extender_32
  assign rep147 = {{31{r070}}, r070};  // Bit_Extender bit_extender_33
  assign rep149 = {{31{r0FC}}, r0FC};  // Bit_Extender bit_extender_34
  and and_76 (and5, esc_05C, dato_escrito[0]);
  and and_77 (and7, esc_004, dato_escrito[30]);
  and and_78 (and11, esc_060, dato_escrito[0]);
  and and_79 (and13, esc_008, dato_escrito[30]);
  and and_80 (and18, esc_050, dato_escrito[0]);
  and and_81 (INT_eventos[0], CONF[24], T0_alcanzado, not30);
  and and_82 (and43, esc_054, dato_escrito[0]);
  and and_83 (INT_eventos[1], CONF[23], T1_alcanzado, not55);
  and and_84 (and68, esc_058, dato_escrito[0]);
  and and_85 (INT_eventos[2], CONF[22], T2_alcanzado, not80);
  assign rep91 = {{31{esc_06C}}, esc_06C};  // Bit_Extender bit_extender_35
  assign and104 = CONF & rep103;  // AND_Gate and_86, 32 bits wide
  assign and106 = U0_LOAD_HI & rep105;  // AND_Gate and_87, 32 bits wide
  assign and108 = U0_LOAD_LO & rep107;  // AND_Gate and_88, 32 bits wide
  assign and110 = {2'b00, cat8[29], {29{1'b0}}} & rep109;  // AND_Gate and_89, 32 bits wide
  assign and112 = zx9 & rep111;  // AND_Gate and_90, 32 bits wide
  assign and114 = U0_VALUE_LO & rep113;  // AND_Gate and_91, 32 bits wide
  assign and116 = U1_LOAD_HI & rep115;  // AND_Gate and_92, 32 bits wide
  assign and118 = U1_LOAD_LO & rep117;  // AND_Gate and_93, 32 bits wide
  assign and120 = {2'b00, cat14[29], {29{1'b0}}} & rep119;  // AND_Gate and_94, 32 bits wide
  assign and122 = zx15 & rep121;  // AND_Gate and_95, 32 bits wide
  assign and124 = U1_VALUE_LO & rep123;  // AND_Gate and_96, 32 bits wide
  assign and126 = T0_HI & rep125;  // AND_Gate and_97, 32 bits wide
  assign and128 = T0_LO & rep127;  // AND_Gate and_98, 32 bits wide
  assign and130 = T0_CONF & rep129;  // AND_Gate and_99, 32 bits wide
  assign and132 = T1_HI & rep131;  // AND_Gate and_100, 32 bits wide
  assign and134 = T1_LO & rep133;  // AND_Gate and_101, 32 bits wide
  assign and136 = T1_CONF & rep135;  // AND_Gate and_102, 32 bits wide
  assign and138 = T2_HI & rep137;  // AND_Gate and_103, 32 bits wide
  assign and140 = T2_LO & rep139;  // AND_Gate and_104, 32 bits wide
  assign and142 = T2_CONF & rep141;  // AND_Gate and_105, 32 bits wide
  assign and144 = INT_ENA & rep143;  // AND_Gate and_106, 32 bits wide
  assign and146 = INT_raw & rep145;  // AND_Gate and_107, 32 bits wide
  assign and148 = {INT_st, IRQ_T2, IRQ_T1, IRQ_T0} & rep147;  // AND_Gate and_108, 32 bits wide
  assign and150 = DATE & rep149;  // AND_Gate and_109, 32 bits wide
  Multiplexer #(.select(1), .width(1), .enable("false")) multiplexer_19 (
    .in0(1'b1), .in1(1'b0), .out(mux37), .sel(and18));
  and and_110 (and39, INT_eventos[0], not38);
  Multiplexer #(.select(1), .width(1), .enable("false")) multiplexer_20 (
    .in0(1'b1), .in1(1'b0), .out(mux62), .sel(and43));
  and and_111 (and64, INT_eventos[1], not63);
  Multiplexer #(.select(1), .width(1), .enable("false")) multiplexer_21 (
    .in0(1'b1), .in1(1'b0), .out(mux87), .sel(and68));
  and and_112 (and89, INT_eventos[2], not88);
  assign INT_clr = dato_escrito & rep91;  // AND_Gate and_113, 32 bits wide
  assign RD = and104 | and106 | and108 | and110 | and112 | and114 | and116 | and118 | and120 | and122 | and124 | and126 | and128 | and130 | and132 | and134 | and136 | and138 | and140 | and142 | and144 | and146 | and148 | and150;  // OR_Gate or_4, 32 bits wide
  Multiplexer #(.select(1), .width(20), .enable("false")) multiplexer_22 (
    .in0(T0_siguiente_hi), .in1(mux31), .out(mux32), .sel(and18));
  Multiplexer #(.select(1), .width(32), .enable("false")) multiplexer_23 (
    .in0(T0_siguiente_lo), .in1(mux33), .out(mux34), .sel(and18));
  and and_114 (and35, INT_eventos[0], T0_modo_periodo);
  Multiplexer #(.select(1), .width(20), .enable("false")) multiplexer_24 (
    .in0(T1_siguiente_hi), .in1(mux56), .out(mux57), .sel(and43));
  Multiplexer #(.select(1), .width(32), .enable("false")) multiplexer_25 (
    .in0(T1_siguiente_lo), .in1(mux58), .out(mux59), .sel(and43));
  and and_115 (and60, INT_eventos[1], T1_modo_periodo);
  Multiplexer #(.select(1), .width(20), .enable("false")) multiplexer_26 (
    .in0(T2_siguiente_hi), .in1(mux81), .out(mux82), .sel(and68));
  Multiplexer #(.select(1), .width(32), .enable("false")) multiplexer_27 (
    .in0(T2_siguiente_lo), .in1(mux83), .out(mux84), .sel(and68));
  and and_116 (and85, INT_eventos[2], T2_modo_periodo);
  or or_5 (or36, and18, and35);
  or or_6 (or40, and18, and39);
  or or_7 (or61, and43, and60);
  or or_8 (or65, and43, and64);
  or or_9 (or86, and68, and85);
  or or_10 (or90, and68, and89);
  assign not92 = ~INT_clr;  // NOT_Gate not_11, 32 bits wide
  assign and93 = INT_raw & not92;  // AND_Gate and_117, 32 bits wide
  assign or94 = and93 | {{29{1'b0}}, INT_eventos};  // OR_Gate or_11, 32 bits wide
  assign and95 = or94 & 32'h7;  // AND_Gate and_118, 32 bits wide

  // Other names for the same wires on the sheet: U0_VALID = cat8[29]; U1_VALID = cat14[29]; CONF_22 = CONF[22];
  //   CONF_23 = CONF[23]; CONF_24 = CONF[24]; CONF_29 = CONF[29]; CONF_30 = CONF[30];
  //   dato_escrito_0 = dato_escrito[0]; dato_escrito_30 = dato_escrito[30]; dir_registro_4_0[4:0] = dir_registro[4:0];
  //   dir_registro_9_5[4:0] = dir_registro[9:5]; T0_alarma = INT_eventos[0]; T1_alarma = INT_eventos[1];
  //   T2_alarma = INT_eventos[2]; INT_st[2:0] = {IRQ_T2, IRQ_T1, IRQ_T0}; INT_st_0 = IRQ_T0; INT_st_1 = IRQ_T1;
  //   INT_st_2 = IRQ_T2; or151[31:0] = RD; T0_CONF_25_0[25:0] = T0_CONF[25:0]; T0_CONF_30 = T0_CONF[30];
  //   T0_CONF_31 = T0_CONF[31]; T0_HI_19_0[19:0] = T0_HI[19:0]; T1_CONF_25_0[25:0] = T1_CONF[25:0];
  //   T1_CONF_30 = T1_CONF[30]; T1_CONF_31 = T1_CONF[31]; T1_HI_19_0[19:0] = T1_HI[19:0];
  //   T2_CONF_25_0[25:0] = T2_CONF[25:0]; T2_CONF_30 = T2_CONF[30]; T2_CONF_31 = T2_CONF[31];
  //   T2_HI_19_0[19:0] = T2_HI[19:0]; U0_LOAD_HI_19_0[19:0] = U0_LOAD_HI[19:0];
  //   U1_LOAD_HI_19_0[19:0] = U1_LOAD_HI[19:0]
endmodule

module TIMG (
  input  CLK,
  input  RST,
  input  SEL,
  input  [9:0] A,
  input  [31:0] WD,
  input  WE,
  input  RE,
  output IRQ_T0,
  output IRQ_WDT,
  output WDT_RESET_CPU,
  output WDT_RESET_SIS,
  output [31:0] RD
);

  wire alarma_disparada, and7, and21, and31, and35, and39, and43, and47, and51, and63, and67, co15, co16,
       eq11, eq19, eq20, eq61, esc_000, esc_00C, esc_01C, esc_04C, esc_05C, esc_07C, esc_010, esc_014,
       esc_018, esc_020, esc_048, esc_050, esc_054, esc_058, esc_060, esc_064, esc_070, escribe, INT_irq,
       lee, lin_0, lin_1, lin_2, lin_3, lin_4, lin_5, lin_6, lin_7, lin_8, lin_9, lin_10, lin_11, lin_12,
       lin_13, lin_14, lin_15, lin_16, lin_17, lin_18, lin_19, lin_20, lin_21, lin_22, lin_23, lin_24,
       lin_25, lin_26, lin_27, lin_28, lin_29, lin_30, lin_31, or4, or12, or14, or22, or25, or26, pag_0,
       pag_1, pag_2, pag_3, pag_4, pag_5, pag_6, pag_7, pag_8, pag_9, pag_10, pag_11, pag_12, pag_13, pag_14,
       pag_15, pag_16, pag_17, pag_18, pag_19, pag_20, pag_21, pag_22, pag_23, pag_24, pag_25, pag_26,
       pag_27, pag_28, pag_29, pag_30, pag_31, r000, r00C, r01C, r004, r04C, r05C, r07C, r008, r010, r014,
       r018, r020, r048, r050, r054, r058, r060, r064, r070, r074, r078, registros_timg_acceso,
       registros_timg_existe, t0_alarma, t0_tick, wdt_alimenta, wdt_desbloqueado, wdt_habilitado;
  wire [1:1] INT_eventos;
  wire [7:0] cat54;
  wire [9:0] dir_registro, rep62;
  wire [15:0] divisor_menos1, mux13, sum10, t0_preescala;
  wire [21:0] mux18, mux24, t0_cuenta_hi, t0_mas1_hi, t0_menos1_hi, T0HI_copia;
  wire [31:0] and1, and2, and8, and9, and30, and34, and38, and42, and46, and50, and57, and59, and60, and66,
       and70, and72, and74, and76, and78, and80, and82, and84, and86, and88, and90, and92, and94, and96,
       and98, and100, and102, and104, dato_escrito, INT_clr, INT_ENA, INT_raw, mux3, mux17, mux23, not56,
       not65, or58, qx6, qx29, qx33, qx37, qx41, qx45, qx49, qx53, registros_timg_a_guardar,
       registros_timg_bits_fijos, registros_timg_bits_rw, registros_timg_guardado, registros_timg_reset_rw,
       registros_timg_valor, registros_timg_valor_reset, rep55, rep64, rep69, rep71, rep73, rep75, rep77,
       rep79, rep81, rep83, rep85, rep87, rep89, rep91, rep93, rep95, rep97, rep99, rep101, rep103,
       t0_cuenta_lo, t0_mas1_lo, t0_menos1_lo, T0ALARMHI, T0ALARMLO, T0CONFIG, T0LO_copia, T0LOADHI,
       T0LOADLO, WDTCONFIG0, WDTCONFIG1, WDTCONFIG2, WDTCONFIG3, WDTCONFIG4, WDTCONFIG5, WDTWPROTECT, xor5,
       xor28, xor32, xor36, xor40, xor44, xor48, xor52, xor68, zx27;
  wire [31:2] INT_st;

  Register #(.width(32)) u_T0CONFIG (.D(xor5), .en(or4), .Q(qx6), .clk(CLK), .clr(RST));
  Register #(.width(32)) u_T0ALARMHI (.D(and8), .en(esc_014), .Q(T0ALARMHI), .clk(CLK), .clr(RST));
  Register #(.width(32)) u_T0LOADHI (.D(and9), .en(esc_01C), .Q(T0LOADHI), .clk(CLK), .clr(RST));
  Register #(.width(16)) T0_PREESC (.D(mux13), .en(or14), .Q(t0_preescala), .clk(CLK), .clr(RST));
  Register #(.width(32)) T0_LO (.D(mux23), .en(or25), .Q(t0_cuenta_lo), .clk(CLK), .clr(RST));
  Register #(.width(22)) T0_HI (.D(mux24), .en(or26), .Q(t0_cuenta_hi), .clk(CLK), .clr(RST));
  Register #(.width(32)) u_WDTWPROTECT (.D(xor28), .en(esc_064), .Q(qx29), .clk(CLK), .clr(RST));
  Register #(.width(32)) u_WDTCONFIG0 (.D(xor32), .en(and31), .Q(qx33), .clk(CLK), .clr(RST));
  Register #(.width(32)) u_WDTCONFIG1 (.D(xor36), .en(and35), .Q(qx37), .clk(CLK), .clr(RST));
  Register #(.width(32)) u_WDTCONFIG2 (.D(xor40), .en(and39), .Q(qx41), .clk(CLK), .clr(RST));
  Register #(.width(32)) u_WDTCONFIG3 (.D(xor44), .en(and43), .Q(qx45), .clk(CLK), .clr(RST));
  Register #(.width(32)) u_WDTCONFIG4 (.D(xor48), .en(and47), .Q(qx49), .clk(CLK), .clr(RST));
  Register #(.width(32)) u_WDTCONFIG5 (.D(xor52), .en(and51), .Q(qx53), .clk(CLK), .clr(RST));
  Register #(.width(32)) u_INT_RAW (.D(and59), .en(1'b1), .Q(INT_raw), .clk(CLK), .clr(RST));
  Register #(.width(32)) u_INT_ENA (.D(and60), .en(esc_070), .Q(INT_ENA), .clk(CLK), .clr(RST));
  assign rep62 = {{9{SEL}}, SEL};  // Bit_Extender bit_extender_1
  and and_1 (and63, SEL, WE);
  and and_2 (escribe, WE, SEL);
  and and_3 (lee, RE, SEL);
  ROM #(.addrWidth(10), .dataWidth(1)) u_REGISTROS_TIMG_EXISTE (.addr(dir_registro), .data(registros_timg_existe));
  Register #(.width(32)) u_T0ALARMLO (.D(dato_escrito), .en(esc_010), .Q(T0ALARMLO), .clk(CLK), .clr(RST));
  Register #(.width(32)) u_T0LOADLO (.D(dato_escrito), .en(esc_018), .Q(T0LOADLO), .clk(CLK), .clr(RST));
  Register #(.width(32)) T0LO (.D(t0_cuenta_lo), .en(esc_00C), .Q(T0LO_copia), .clk(CLK), .clr(RST));
  Register #(.width(22)) T0HI (.D(t0_cuenta_hi), .en(esc_00C), .Q(T0HI_copia), .clk(CLK), .clr(RST));
  ROM #(.addrWidth(10), .dataWidth(32)) u_REGISTROS_TIMG_VALOR_RESET (
    .addr(dir_registro), .data(registros_timg_valor_reset));
  ROM #(.addrWidth(10), .dataWidth(32)) u_REGISTROS_TIMG_BITS_RW (.addr(dir_registro), .data(registros_timg_bits_rw));
  RAM #(.addrWidth(10), .dataWidth(32), .enables("byte"), .trigger("rising"), .asyncread("true"), .databus("bibus"), .clearpin("true")) REGISTROS_TIMG (
    .addr(dir_registro), .we(and67), .oe(1'b1), .clk(CLK), .din(registros_timg_a_guardar),
    .dout(registros_timg_guardado), .clr(RST));
  assign T0CONFIG = qx6 ^ 32'h60002000;  // XOR_Gate xor_1, 32 bits wide
  assign zx27 = {{10{1'b0}}, T0HI_copia};  // Bit_Extender bit_extender_2
  assign WDTWPROTECT = qx29 ^ 32'h50d83aa1;  // XOR_Gate xor_2, 32 bits wide
  assign {WDTCONFIG0[31], cat54[1:0], cat54[3:2], cat54[5:4], cat54[7:6], WDTCONFIG0[22:0]} = qx33 ^ 32'h4c000;  // XOR_Gate xor_3, 32 bits wide
  assign WDTCONFIG1 = qx37 ^ 32'h10000;  // XOR_Gate xor_4, 32 bits wide
  assign WDTCONFIG2 = qx41 ^ 32'h18cba80;  // XOR_Gate xor_5, 32 bits wide
  assign WDTCONFIG3 = qx45 ^ 32'h7ffffff;  // XOR_Gate xor_6, 32 bits wide
  assign WDTCONFIG4 = qx49 ^ 32'hfffff;  // XOR_Gate xor_7, 32 bits wide
  assign WDTCONFIG5 = qx53 ^ 32'hfffff;  // XOR_Gate xor_8, 32 bits wide
  assign {INT_st, IRQ_WDT, IRQ_T0} = INT_raw & INT_ENA;  // AND_Gate and_4, 32 bits wide
  assign dir_registro = A & rep62;  // AND_Gate and_5, 10 bits wide
  assign rep64 = {{31{and63}}, and63};  // Bit_Extender bit_extender_3
  Adder #(.width(16)) adder_1 (.a(t0_preescala), .b(16'h1), .out(sum10));  // open: cin, cout
  Adder #(.width(32)) adder_2 (.a(t0_cuenta_lo), .b(32'h1), .out(t0_mas1_lo), .cout(co15));  // open: cin
  Adder #(.width(32)) adder_3 (.a(t0_cuenta_lo), .b({32{1'b1}}), .out(t0_menos1_lo), .cout(co16));  // open: cin
  Comparator #(.width(32), .mode("unsigned")) comparator_1 (
    .a(t0_cuenta_lo), .b(T0ALARMLO), .eq(eq19));  // open: gt, lt
  and and_6 (registros_timg_acceso, SEL, registros_timg_existe);
  assign not65 = ~registros_timg_bits_rw;  // NOT_Gate not_1, 32 bits wide
  assign registros_timg_reset_rw = registros_timg_valor_reset & registros_timg_bits_rw;  // AND_Gate and_7, 32 bits wide
  assign and1 = T0CONFIG & 32'hfffffbff;  // AND_Gate and_8, 32 bits wide
  Adder #(.width(22)) adder_4 (.a(t0_cuenta_hi), .b({22{1'b0}}), .out(t0_mas1_hi), .cin(co15));  // open: cout
  Adder #(.width(22)) adder_5 (.a(t0_cuenta_hi), .b({22{1'b1}}), .out(t0_menos1_hi), .cin(co16));  // open: cout
  Comparator #(.width(22), .mode("unsigned")) comparator_2 (
    .a(t0_cuenta_hi), .b(T0ALARMHI[21:0]), .eq(eq20));  // open: gt, lt
  Comparator #(.width(32), .mode("unsigned")) comparator_3 (
    .a(WDTWPROTECT), .b(32'h50d83aa1), .eq(wdt_desbloqueado));  // open: gt, lt
  Comparator #(.width(32), .mode("unsigned")) comparator_4 (
    .a({INT_st, IRQ_WDT, IRQ_T0}), .b({32{1'b0}}), .eq(eq61));  // open: gt, lt
  assign dato_escrito = WD & rep64;  // AND_Gate and_9, 32 bits wide
  assign registros_timg_bits_fijos = registros_timg_valor_reset & not65;  // AND_Gate and_10, 32 bits wide
  and and_11 (and67, escribe, registros_timg_acceso);
  assign xor68 = registros_timg_guardado ^ registros_timg_reset_rw;  // XOR_Gate xor_9, 32 bits wide
  assign rep69 = {{31{registros_timg_acceso}}, registros_timg_acceso};  // Bit_Extender bit_extender_4
  Decoder #(.select(5), .enable("false")) decoder_1 (
    .out0(pag_0), .out1(pag_1), .out2(pag_2), .out3(pag_3), .out4(pag_4), .out5(pag_5), .out6(pag_6),
    .out7(pag_7), .out8(pag_8), .out9(pag_9), .out10(pag_10), .out11(pag_11), .out12(pag_12), .out13(pag_13),
    .out14(pag_14), .out15(pag_15), .out16(pag_16), .out17(pag_17), .out18(pag_18), .out19(pag_19),
    .out20(pag_20), .out21(pag_21), .out22(pag_22), .out23(pag_23), .out24(pag_24), .out25(pag_25),
    .out26(pag_26), .out27(pag_27), .out28(pag_28), .out29(pag_29), .out30(pag_30), .out31(pag_31),
    .sel(dir_registro[9:5]));
  Decoder #(.select(5), .enable("false")) decoder_2 (
    .out0(lin_0), .out1(lin_1), .out2(lin_2), .out3(lin_3), .out4(lin_4), .out5(lin_5), .out6(lin_6),
    .out7(lin_7), .out8(lin_8), .out9(lin_9), .out10(lin_10), .out11(lin_11), .out12(lin_12), .out13(lin_13),
    .out14(lin_14), .out15(lin_15), .out16(lin_16), .out17(lin_17), .out18(lin_18), .out19(lin_19),
    .out20(lin_20), .out21(lin_21), .out22(lin_22), .out23(lin_23), .out24(lin_24), .out25(lin_25),
    .out26(lin_26), .out27(lin_27), .out28(lin_28), .out29(lin_29), .out30(lin_30), .out31(lin_31),
    .sel(dir_registro[4:0]));
  not not_2 (INT_irq, eq61);
  assign and2 = dato_escrito & 32'hffffe600;  // AND_Gate and_12, 32 bits wide
  assign and8 = dato_escrito & 32'h3fffff;  // AND_Gate and_13, 32 bits wide
  assign and9 = dato_escrito & 32'h3fffff;  // AND_Gate and_14, 32 bits wide
  Adder #(.width(16)) adder_6 (.a(T0CONFIG[28:13]), .b({16{1'b1}}), .out(divisor_menos1));  // open: cin, cout
  Multiplexer #(.select(1), .width(32), .enable("false")) multiplexer_1 (
    .in0(t0_menos1_lo), .in1(t0_mas1_lo), .out(mux17), .sel(T0CONFIG[30]));
  Multiplexer #(.select(1), .width(22), .enable("false")) multiplexer_2 (
    .in0(t0_menos1_hi), .in1(t0_mas1_hi), .out(mux18), .sel(T0CONFIG[30]));
  and and_15 (t0_alarma, T0CONFIG[10], eq19, eq20);
  assign xor28 = dato_escrito ^ 32'h50d83aa1;  // XOR_Gate xor_10, 32 bits wide
  assign and30 = dato_escrito & 32'hffbff000;  // AND_Gate and_16, 32 bits wide
  assign and34 = dato_escrito & 32'hffff0000;  // AND_Gate and_17, 32 bits wide
  assign and38 = dato_escrito & {32{1'b1}};  // AND_Gate and_18, 32 bits wide
  assign and42 = dato_escrito & {32{1'b1}};  // AND_Gate and_19, 32 bits wide
  assign and46 = dato_escrito & {32{1'b1}};  // AND_Gate and_20, 32 bits wide
  assign and50 = dato_escrito & {32{1'b1}};  // AND_Gate and_21, 32 bits wide
  or or_1 (wdt_habilitado, WDTCONFIG0[31], 1'b0);
  assign and60 = dato_escrito & 32'h3;  // AND_Gate and_22, 32 bits wide
  assign and66 = dato_escrito & registros_timg_bits_rw;  // AND_Gate and_23, 32 bits wide
  assign registros_timg_valor = xor68 | registros_timg_bits_fijos;  // OR_Gate or_2, 32 bits wide
  and and_24 (r000, SEL, pag_0, lin_0);
  and and_25 (r010, SEL, pag_0, lin_4);
  and and_26 (r014, SEL, pag_0, lin_5);
  and and_27 (r018, SEL, pag_0, lin_6);
  and and_28 (r01C, SEL, pag_0, lin_7);
  and and_29 (r020, SEL, pag_0, lin_8);
  and and_30 (r00C, SEL, pag_0, lin_3);
  and and_31 (r064, SEL, pag_0, lin_25);
  and and_32 (r048, SEL, pag_0, lin_18);
  assign xor32 = and30 ^ 32'h4c000;  // XOR_Gate xor_11, 32 bits wide
  and and_33 (r04C, SEL, pag_0, lin_19);
  assign xor36 = and34 ^ 32'h10000;  // XOR_Gate xor_12, 32 bits wide
  and and_34 (r050, SEL, pag_0, lin_20);
  assign xor40 = and38 ^ 32'h18cba80;  // XOR_Gate xor_13, 32 bits wide
  and and_35 (r054, SEL, pag_0, lin_21);
  assign xor44 = and42 ^ 32'h7ffffff;  // XOR_Gate xor_14, 32 bits wide
  and and_36 (r058, SEL, pag_0, lin_22);
  assign xor48 = and46 ^ 32'hfffff;  // XOR_Gate xor_15, 32 bits wide
  and and_37 (r05C, SEL, pag_0, lin_23);
  assign xor52 = and50 ^ 32'hfffff;  // XOR_Gate xor_16, 32 bits wide
  and and_38 (r060, SEL, pag_0, lin_24);
  and and_39 (r07C, SEL, pag_0, lin_31);
  and and_40 (r070, SEL, pag_0, lin_28);
  and and_41 (r004, SEL, pag_0, lin_1);
  and and_42 (r008, SEL, pag_0, lin_2);
  and and_43 (r074, SEL, pag_0, lin_29);
  and and_44 (r078, SEL, pag_0, lin_30);
  Comparator #(.width(16), .mode("unsigned")) comparator_5 (
    .a(t0_preescala), .b(divisor_menos1), .eq(eq11));  // open: gt, lt
  assign registros_timg_a_guardar = and66 ^ registros_timg_reset_rw;  // XOR_Gate xor_17, 32 bits wide
  assign and70 = registros_timg_valor & rep69;  // AND_Gate and_45, 32 bits wide
  and and_46 (esc_000, escribe, r000);
  and and_47 (esc_010, escribe, r010);
  and and_48 (esc_014, escribe, r014);
  and and_49 (esc_018, escribe, r018);
  and and_50 (esc_01C, escribe, r01C);
  and and_51 (esc_020, escribe, r020);
  and and_52 (esc_00C, escribe, r00C);
  and and_53 (esc_064, escribe, r064);
  and and_54 (esc_048, escribe, r048);
  and and_55 (esc_04C, escribe, r04C);
  and and_56 (esc_050, escribe, r050);
  and and_57 (esc_054, escribe, r054);
  and and_58 (esc_058, escribe, r058);
  and and_59 (esc_05C, escribe, r05C);
  and and_60 (esc_060, escribe, r060);
  and and_61 (esc_07C, escribe, r07C);
  and and_62 (esc_070, escribe, r070);
  assign rep71 = {{31{r000}}, r000};  // Bit_Extender bit_extender_5
  assign rep73 = {{31{r010}}, r010};  // Bit_Extender bit_extender_6
  assign rep75 = {{31{r014}}, r014};  // Bit_Extender bit_extender_7
  assign rep77 = {{31{r018}}, r018};  // Bit_Extender bit_extender_8
  assign rep79 = {{31{r01C}}, r01C};  // Bit_Extender bit_extender_9
  assign rep81 = {{31{r004}}, r004};  // Bit_Extender bit_extender_10
  assign rep83 = {{31{r008}}, r008};  // Bit_Extender bit_extender_11
  assign rep85 = {{31{r064}}, r064};  // Bit_Extender bit_extender_12
  assign rep87 = {{31{r048}}, r048};  // Bit_Extender bit_extender_13
  assign rep89 = {{31{r04C}}, r04C};  // Bit_Extender bit_extender_14
  assign rep91 = {{31{r050}}, r050};  // Bit_Extender bit_extender_15
  assign rep93 = {{31{r054}}, r054};  // Bit_Extender bit_extender_16
  assign rep95 = {{31{r058}}, r058};  // Bit_Extender bit_extender_17
  assign rep97 = {{31{r05C}}, r05C};  // Bit_Extender bit_extender_18
  assign rep99 = {{31{r070}}, r070};  // Bit_Extender bit_extender_19
  assign rep101 = {{31{r074}}, r074};  // Bit_Extender bit_extender_20
  assign rep103 = {{31{r078}}, r078};  // Bit_Extender bit_extender_21
  and and_63 (t0_tick, T0CONFIG[31], eq11);
  Multiplexer #(.select(1), .width(32), .enable("false")) multiplexer_3 (
    .in0(and1), .in1(and2), .out(mux3), .sel(esc_000));
  and and_64 (and7, esc_000, dato_escrito[12]);
  and and_65 (and21, t0_alarma, T0CONFIG[29], t0_tick);
  or or_3 (or25, t0_tick, esc_020);
  or or_4 (or26, t0_tick, esc_020);
  and and_66 (alarma_disparada, t0_alarma, t0_tick);
  assign rep55 = {{31{esc_07C}}, esc_07C};  // Bit_Extender bit_extender_22
  assign and72 = T0CONFIG & rep71;  // AND_Gate and_67, 32 bits wide
  assign and74 = T0ALARMLO & rep73;  // AND_Gate and_68, 32 bits wide
  assign and76 = T0ALARMHI & rep75;  // AND_Gate and_69, 32 bits wide
  assign and78 = T0LOADLO & rep77;  // AND_Gate and_70, 32 bits wide
  assign and80 = T0LOADHI & rep79;  // AND_Gate and_71, 32 bits wide
  assign and82 = T0LO_copia & rep81;  // AND_Gate and_72, 32 bits wide
  assign and84 = zx27 & rep83;  // AND_Gate and_73, 32 bits wide
  assign and86 = WDTWPROTECT & rep85;  // AND_Gate and_74, 32 bits wide
  assign and88 = {WDTCONFIG0[31], cat54[1:0], cat54[3:2], cat54[5:4], cat54[7:6], WDTCONFIG0[22:0]} & rep87;  // AND_Gate and_75, 32 bits wide
  assign and90 = WDTCONFIG1 & rep89;  // AND_Gate and_76, 32 bits wide
  assign and92 = WDTCONFIG2 & rep91;  // AND_Gate and_77, 32 bits wide
  assign and94 = WDTCONFIG3 & rep93;  // AND_Gate and_78, 32 bits wide
  assign and96 = WDTCONFIG4 & rep95;  // AND_Gate and_79, 32 bits wide
  assign and98 = WDTCONFIG5 & rep97;  // AND_Gate and_80, 32 bits wide
  assign and100 = INT_ENA & rep99;  // AND_Gate and_81, 32 bits wide
  assign and102 = INT_raw & rep101;  // AND_Gate and_82, 32 bits wide
  assign and104 = {INT_st, IRQ_WDT, IRQ_T0} & rep103;  // AND_Gate and_83, 32 bits wide
  and and_84 (and31, esc_048, wdt_desbloqueado);
  and and_85 (and35, esc_04C, wdt_desbloqueado);
  and and_86 (and39, esc_050, wdt_desbloqueado);
  and and_87 (and43, esc_054, wdt_desbloqueado);
  and and_88 (and47, esc_058, wdt_desbloqueado);
  and and_89 (and51, esc_05C, wdt_desbloqueado);
  and and_90 (wdt_alimenta, esc_060, wdt_desbloqueado);
  assign xor5 = mux3 ^ 32'h60002000;  // XOR_Gate xor_18, 32 bits wide
  or or_5 (or12, t0_tick, and7);
  or or_6 (or14, T0CONFIG[31], and7);
  or or_7 (or22, esc_020, and21);
  WatchdogEtapas MWDT (
    .CLK(CLK), .RST(RST), .EN(wdt_habilitado), .FEED(wdt_alimenta), .PRESCALE(WDTCONFIG1[31:16]),
    .STG(cat54), .HOLD0(WDTCONFIG2), .HOLD1(WDTCONFIG3), .HOLD2(WDTCONFIG4), .HOLD3(WDTCONFIG5),
    .INT(INT_eventos[1]), .RESET_CPU(WDT_RESET_CPU), .RESET_SIS(WDT_RESET_SIS));
  assign INT_clr = dato_escrito & rep55;  // AND_Gate and_91, 32 bits wide
  assign RD = and72 | and74 | and76 | and78 | and80 | and82 | and84 | and86 | and88 | and90 | and92 | and94 | and96 | and98 | and100 | and102 | and104 | and70;  // OR_Gate or_8, 32 bits wide
  Multiplexer #(.select(1), .width(16), .enable("false")) multiplexer_4 (
    .in0(sum10), .in1({16{1'b0}}), .out(mux13), .sel(or12));
  Multiplexer #(.select(1), .width(32), .enable("false")) multiplexer_5 (
    .in0(mux17), .in1(T0LOADLO), .out(mux23), .sel(or22));
  assign not56 = ~INT_clr;  // NOT_Gate not_3, 32 bits wide
  or or_9 (or4, esc_000, alarma_disparada);
  Multiplexer #(.select(1), .width(22), .enable("false")) multiplexer_6 (
    .in0(mux18), .in1(T0LOADHI[21:0]), .out(mux24), .sel(or22));
  assign and57 = INT_raw & not56;  // AND_Gate and_92, 32 bits wide
  assign or58 = and57 | {{30{1'b0}}, INT_eventos[1], alarma_disparada};  // OR_Gate or_10, 32 bits wide
  assign and59 = or58 & 32'h3;  // AND_Gate and_93, 32 bits wide

  // Other names for the same wires on the sheet: WDTCONFIG0[30:23] = {cat54[1:0], cat54[3:2], cat54[5:4], cat54[7:6]};
  //   WDTCONFIG0_30_29[1:0] = cat54[1:0]; WDTCONFIG0_28_27[1:0] = cat54[3:2]; WDTCONFIG0_26_25[1:0] = cat54[5:4];
  //   WDTCONFIG0_24_23[1:0] = cat54[7:6]; dato_escrito_12 = dato_escrito[12];
  //   dir_registro_4_0[4:0] = dir_registro[4:0]; dir_registro_9_5[4:0] = dir_registro[9:5];
  //   evento_alarma = alarma_disparada; INT_eventos[0] = alarma_disparada; wdt_int = INT_eventos[1];
  //   INT_st[1:0] = {IRQ_WDT, IRQ_T0}; INT_st_0 = IRQ_T0; INT_st_1 = IRQ_WDT; or105[31:0] = RD;
  //   T0ALARMHI_21_0[21:0] = T0ALARMHI[21:0]; T0CONFIG_10 = T0CONFIG[10]; T0CONFIG_28_13[15:0] = T0CONFIG[28:13];
  //   T0CONFIG_29 = T0CONFIG[29]; T0CONFIG_30 = T0CONFIG[30]; T0CONFIG_31 = T0CONFIG[31];
  //   T0LOADHI_21_0[21:0] = T0LOADHI[21:0]; WDT_RESET_CPU_2 = WDT_RESET_CPU; wdt_reset_cpu_t = WDT_RESET_CPU;
  //   WDT_RESET_SIS_2 = WDT_RESET_SIS; wdt_reset_sis_t = WDT_RESET_SIS; WDTCONFIG0_31 = WDTCONFIG0[31];
  //   WDTCONFIG1_31_16[15:0] = WDTCONFIG1[31:16]

  // Notes on the sheet:
  //   contents of REGISTROS_TIMG_EXISTE (hex, n*v repeats v):
  //   26*0 1 5*0 1 29*0 1 1
  //   contents of REGISTROS_TIMG_VALOR_RESET (hex, n*v repeats v):
  //   26*0 13000 5*0 ffffff98 29*0 2006191 60000000
  //   contents of REGISTROS_TIMG_BITS_RW (hex, n*v repeats v):
  //   26*0 ffff7000 5*0 fffffff8 29*0 fffffff e0000000
endmodule
module MatrizInterrupciones (
  input  CLK,
  input  RST,
  input  SEL,
  input  [9:0] A,
  input  [31:0] WD,
  input  WE,
  input  RE,
  input  INT_GPIO,
  input  INT_GPIO_NMI,
  input  INT_SPI2,
  input  INT_UART0,
  input  INT_UART1,
  input  INT_LEDC,
  input  INT_USB_SERIAL_JTAG,
  input  INT_RTC_CORE,
  input  INT_I2C_EXT0,
  input  INT_TG0_T0,
  input  INT_TG0_WDT,
  input  INT_TG1_T0,
  input  INT_TG1_WDT,
  input  INT_SYSTIMER_T0,
  input  INT_SYSTIMER_T1,
  input  INT_SYSTIMER_T2,
  input  INT_SHA,
  input  INT_FROM_CPU0,
  input  INT_FROM_CPU1,
  input  INT_FROM_CPU2,
  input  INT_FROM_CPU3,
  output IRQ,
  output [4:0] IRQ_ID,
  output [31:0] IRQ_LINEAS,
  output [31:0] RD
);

  wire and294, and298, esc_0C4, esc_0C8, esc_0CC, esc_0D0, esc_0D4, esc_04C, esc_05C, esc_06C, esc_08C,
       esc_09C, esc_10C, esc_11C, esc_12C, esc_13C, esc_14C, esc_15C, esc_16C, esc_17C, esc_18C, esc_040,
       esc_044, esc_054, esc_058, esc_068, esc_074, esc_080, esc_084, esc_088, esc_094, esc_098, esc_104,
       esc_108, esc_118, esc_120, esc_124, esc_128, esc_130, esc_134, esc_138, esc_140, esc_144, esc_148,
       esc_150, esc_154, esc_158, esc_160, esc_164, esc_168, esc_170, esc_174, esc_178, esc_180, esc_184,
       esc_188, esc_190, esc_194, escribe, gana_A_0_0, gana_A_0_1, gana_A_0_2, gana_A_0_3, gana_A_0_4,
       gana_A_0_5, gana_A_0_6, gana_A_0_7, gana_A_0_8, gana_A_0_9, gana_A_0_10, gana_A_0_11, gana_A_0_12,
       gana_A_0_13, gana_A_0_14, gana_A_0_15, gana_A_1_0, gana_A_1_1, gana_A_1_2, gana_A_1_3, gana_A_1_4,
       gana_A_1_5, gana_A_1_6, gana_A_1_7, gana_A_2_0, gana_A_2_1, gana_A_2_2, gana_A_2_3, gana_A_3_0,
       gana_A_3_1, gana_A_4_0, lee, lin_0, lin_1, lin_2, lin_3, lin_4, lin_5, lin_6, lin_7, lin_8, lin_9,
       lin_10, lin_11, lin_12, lin_13, lin_14, lin_15, lin_16, lin_17, lin_18, lin_19, lin_20, lin_21,
       lin_22, lin_23, lin_24, lin_25, lin_26, lin_27, lin_28, lin_29, lin_30, lin_31, lt107, lt109, lt111,
       lt113, lt115, lt117, lt119, lt121, lt123, lt125, lt127, lt129, lt131, lt133, lt135, lt137, lt139,
       lt141, lt143, lt145, lt147, lt149, lt151, lt153, lt155, lt157, lt159, lt161, lt163, lt165, lt167,
       lt170, lt174, lt178, lt182, lt186, lt190, lt194, lt198, lt202, lt206, lt210, lt214, lt218, lt222,
       lt226, lt230, lt234, lt238, lt242, lt246, lt250, lt254, lt258, lt262, lt266, lt270, lt274, lt278,
       lt282, lt286, lt290, MAPAS0_escribe, MAPAS1_escribe, MAPAS2_escribe, MAPAS3_escribe, not108, not110,
       not112, not114, not116, not118, not120, not122, not124, not126, not128, not130, not132, not134,
       not136, not138, not140, not142, not144, not146, not148, not150, not152, not154, not156, not158,
       not160, not162, not164, not166, not168, not169, not171, not173, not175, not177, not179, not181,
       not183, not185, not187, not189, not191, not193, not195, not197, not199, not201, not203, not205,
       not207, not209, not211, not213, not215, not217, not219, not221, not223, not225, not227, not229,
       not231, not233, not235, not237, not239, not241, not243, not245, not247, not249, not251, not253,
       not255, not257, not259, not261, not263, not265, not267, not269, not271, not273, not275, not277,
       not279, not281, not283, not285, not287, not289, not291, or172, or176, or180, or184, or188, or192,
       or196, or200, or204, or208, or212, or216, or220, or224, or228, or232, or236, or240, or244, or248,
       or252, or256, or260, or264, or268, or272, or276, or280, or284, or288, or292, pag_0, pag_1, pag_2,
       pag_3, pag_4, pag_5, pag_6, pag_7, pag_8, pag_9, pag_10, pag_11, pag_12, pag_13, pag_14, pag_15,
       pag_16, pag_17, pag_18, pag_19, pag_20, pag_21, pag_22, pag_23, pag_24, pag_25, pag_26, pag_27,
       pag_28, pag_29, pag_30, pag_31, pide1, pide2, pide3, pide4, pide5, pide6, pide7, pide8, pide9, pide10,
       pide11, pide12, pide13, pide14, pide15, pide16, pide17, pide18, pide19, pide20, pide21, pide22,
       pide23, pide24, pide25, pide26, pide27, pide28, pide29, pide30, pide31, PRIORIDADES0_escribe,
       PRIORIDADES1_escribe, PRIORIDADES2_escribe, PRIORIDADES3_escribe, r0C4, r0C8, r0CC, r0D0, r0D4, r0F8,
       r0FC, r04C, r05C, r06C, r08C, r09C, r10C, r11C, r12C, r13C, r14C, r15C, r16C, r17C, r18C, r040, r044,
       r054, r058, r068, r074, r080, r084, r088, r094, r098, r104, r108, r110, r118, r120, r124, r128, r130,
       r134, r138, r140, r144, r148, r150, r154, r158, r160, r164, r168, r170, r174, r178, r180, r184, r188,
       r190, r194, registros_acceso, registros_existe, v_0_0, v_0_1, v_0_2, v_0_3, v_0_4, v_0_5, v_0_6,
       v_0_7, v_0_8, v_0_9, v_0_10, v_0_11, v_0_12, v_0_13, v_0_14, v_0_15, v_1_0, v_1_1, v_1_2, v_1_3,
       v_1_4, v_1_5, v_1_6, v_1_7, v_2_0, v_2_1, v_2_2, v_2_3, v_3_0, v_3_1;
  wire [3:0] p_0_0, p_0_1, p_0_2, p_0_3, p_0_4, p_0_5, p_0_6, p_0_7, p_0_8, p_0_9, p_0_10, p_0_11, p_0_12,
       p_0_13, p_0_14, p_0_15, p_1_0, p_1_1, p_1_2, p_1_3, p_1_4, p_1_5, p_1_6, p_1_7, p_2_0, p_2_1, p_2_2,
       p_2_3, p_3_0, p_3_1, p_4_0;
  wire [4:0] i_0_0, i_0_1, i_0_2, i_0_3, i_0_4, i_0_5, i_0_6, i_0_7, i_0_8, i_0_9, i_0_10, i_0_11, i_0_12,
       i_0_13, i_0_14, i_0_15, i_1_0, i_1_1, i_1_2, i_1_3, i_1_4, i_1_5, i_1_6, i_1_7, i_2_0, i_2_1, i_2_2,
       i_2_3, i_3_0, i_3_1;
  wire [9:0] dir_registro, rep293;
  wire [14:0] and32, and33, MAPAS3, MAPAS3_mascara, MAPAS3_sig, not31;
  wire [29:0] and8, and9, and17, and18, and26, and27, MAPAS0, MAPAS0_mascara, MAPAS0_sig, MAPAS1,
       MAPAS1_mascara, MAPAS1_sig, MAPAS2, MAPAS2_mascara, MAPAS2_sig, not7, not16, not25;
  wire [31:0] and55, and59, and60, and62, and72, and73, and83, and84, and94, and95, and105, and106, and297,
       and301, and303, and305, and307, and309, and311, and313, aporte_16_GPIO, aporte_17_GPIO_NMI,
       aporte_19_SPI2, aporte_21_UART0, aporte_22_UART1, aporte_23_LEDC, aporte_26_USB_SERIAL_JTAG,
       aporte_27_RTC_CORE, aporte_29_I2C_EXT0, aporte_32_TG0_T0, aporte_33_TG0_WDT, aporte_34_TG1_T0,
       aporte_35_TG1_WDT, aporte_37_SYSTIMER_T0, aporte_38_SYSTIMER_T1, aporte_39_SYSTIMER_T2, aporte_49_SHA,
       aporte_50_FROM_CPU0, aporte_51_FROM_CPU1, aporte_52_FROM_CPU2, aporte_53_FROM_CPU3, CPU_INT_CLEAR,
       CPU_INT_ENABLE, CPU_INT_TYPE, dato_escrito, flancos, linea_de_16, linea_de_17, linea_de_19,
       linea_de_21, linea_de_22, linea_de_23, linea_de_26, linea_de_27, linea_de_29, linea_de_32,
       linea_de_33, linea_de_34, linea_de_35, linea_de_37, linea_de_38, linea_de_39, linea_de_49,
       linea_de_50, linea_de_51, linea_de_52, linea_de_53, lineas_antes, lineas_cpu, not56, not58, not61,
       not71, not82, not93, not104, not296, or57, pend_flanco, pendientes, PRIORIDADES0,
       PRIORIDADES0_mascara, PRIORIDADES0_sig, PRIORIDADES1, PRIORIDADES1_mascara, PRIORIDADES1_sig,
       PRIORIDADES2, PRIORIDADES2_mascara, PRIORIDADES2_sig, PRIORIDADES3, PRIORIDADES3_mascara,
       PRIORIDADES3_sig, registros_a_guardar, registros_bits_fijos, registros_bits_rw, registros_guardado,
       registros_reset_rw, registros_valor, registros_valor_reset, rep34, rep35, rep36, rep37, rep38, rep39,
       rep40, rep41, rep42, rep43, rep44, rep45, rep46, rep47, rep48, rep49, rep50, rep51, rep52, rep53,
       rep54, rep295, rep300, rep302, rep304, rep306, rep308, rep310, rep312, xor299;

  Register #(.width(32)) u_PEND_FLANCO (.D(and59), .en(1'b1), .Q(pend_flanco), .clk(CLK), .clr(RST));
  Register #(.width(30)) u_MAPAS0 (.D(MAPAS0_sig), .en(MAPAS0_escribe), .Q(MAPAS0), .clk(CLK), .clr(RST));
  Register #(.width(30)) u_MAPAS1 (.D(MAPAS1_sig), .en(MAPAS1_escribe), .Q(MAPAS1), .clk(CLK), .clr(RST));
  Register #(.width(30)) u_MAPAS2 (.D(MAPAS2_sig), .en(MAPAS2_escribe), .Q(MAPAS2), .clk(CLK), .clr(RST));
  Register #(.width(15)) u_MAPAS3 (.D(MAPAS3_sig), .en(MAPAS3_escribe), .Q(MAPAS3), .clk(CLK), .clr(RST));
  Register #(.width(32)) u_CPU_INT_ENABLE (.D(dato_escrito), .en(esc_104), .Q(CPU_INT_ENABLE), .clk(CLK), .clr(RST));
  Register #(.width(32)) u_CPU_INT_TYPE (.D(dato_escrito), .en(esc_108), .Q(CPU_INT_TYPE), .clk(CLK), .clr(RST));
  Register #(.width(32)) u_CPU_INT_CLEAR (.D(dato_escrito), .en(esc_10C), .Q(CPU_INT_CLEAR), .clk(CLK), .clr(RST));
  Register #(.width(32)) u_LINEAS_ANTES (.D(lineas_cpu), .en(1'b1), .Q(lineas_antes), .clk(CLK), .clr(RST));
  Register #(.width(32)) u_PRIORIDADES0 (
    .D(PRIORIDADES0_sig), .en(PRIORIDADES0_escribe), .Q(PRIORIDADES0), .clk(CLK), .clr(RST));
  Register #(.width(32)) u_PRIORIDADES1 (
    .D(PRIORIDADES1_sig), .en(PRIORIDADES1_escribe), .Q(PRIORIDADES1), .clk(CLK), .clr(RST));
  assign rep293 = {{9{SEL}}, SEL};  // Bit_Extender bit_extender_1
  and and_1 (and294, SEL, WE);
  and and_2 (escribe, WE, SEL);
  and and_3 (lee, RE, SEL);
  ROM #(.addrWidth(10), .dataWidth(1)) u_REGISTROS_EXISTE (.addr(dir_registro), .data(registros_existe));
  ROM #(.addrWidth(10), .dataWidth(32)) u_REGISTROS_VALOR_RESET (.addr(dir_registro), .data(registros_valor_reset));
  ROM #(.addrWidth(10), .dataWidth(32)) u_REGISTROS_BITS_RW (.addr(dir_registro), .data(registros_bits_rw));
  RAM #(.addrWidth(10), .dataWidth(32), .enables("byte"), .trigger("rising"), .asyncread("true"), .databus("bibus"), .clearpin("true")) REGISTROS (
    .addr(dir_registro), .we(and298), .oe(1'b1), .clk(CLK), .din(registros_a_guardar),
    .dout(registros_guardado), .clr(RST));
  Register #(.width(32)) u_PRIORIDADES2 (
    .D(PRIORIDADES2_sig), .en(PRIORIDADES2_escribe), .Q(PRIORIDADES2), .clk(CLK), .clr(RST));
  Register #(.width(32)) u_PRIORIDADES3 (
    .D(PRIORIDADES3_sig), .en(PRIORIDADES3_escribe), .Q(PRIORIDADES3), .clk(CLK), .clr(RST));
  assign not56 = ~lineas_antes;  // NOT_Gate not_1, 32 bits wide
  assign not58 = ~CPU_INT_CLEAR;  // NOT_Gate not_2, 32 bits wide
  assign not61 = ~CPU_INT_TYPE;  // NOT_Gate not_3, 32 bits wide
  assign and55 = {{10{1'b0}}, INT_FROM_CPU3, INT_FROM_CPU2, INT_FROM_CPU1, INT_FROM_CPU0, INT_SHA, {9{1'b0}}, INT_SYSTIMER_T2, INT_SYSTIMER_T1, INT_SYSTIMER_T0, 1'b0, INT_TG1_WDT, INT_TG1_T0, INT_TG0_WDT, INT_TG0_T0} & 32'h3fffffff;  // AND_Gate and_4, 32 bits wide
  assign and60 = CPU_INT_TYPE & pend_flanco;  // AND_Gate and_5, 32 bits wide
  assign dir_registro = A & rep293;  // AND_Gate and_6, 10 bits wide
  assign rep295 = {{31{and294}}, and294};  // Bit_Extender bit_extender_2
  and and_7 (registros_acceso, SEL, registros_existe);
  assign registros_reset_rw = registros_valor_reset & registros_bits_rw;  // AND_Gate and_8, 32 bits wide
  assign not296 = ~registros_bits_rw;  // NOT_Gate not_4, 32 bits wide
  Decoder #(.select(5), .enable("false")) decoder_1 (
    .out0(linea_de_16[0]), .out1(linea_de_16[1]), .out2(linea_de_16[2]), .out3(linea_de_16[3]),
    .out4(linea_de_16[4]), .out5(linea_de_16[5]), .out6(linea_de_16[6]), .out7(linea_de_16[7]),
    .out8(linea_de_16[8]), .out9(linea_de_16[9]), .out10(linea_de_16[10]), .out11(linea_de_16[11]),
    .out12(linea_de_16[12]), .out13(linea_de_16[13]), .out14(linea_de_16[14]), .out15(linea_de_16[15]),
    .out16(linea_de_16[16]), .out17(linea_de_16[17]), .out18(linea_de_16[18]), .out19(linea_de_16[19]),
    .out20(linea_de_16[20]), .out21(linea_de_16[21]), .out22(linea_de_16[22]), .out23(linea_de_16[23]),
    .out24(linea_de_16[24]), .out25(linea_de_16[25]), .out26(linea_de_16[26]), .out27(linea_de_16[27]),
    .out28(linea_de_16[28]), .out29(linea_de_16[29]), .out30(linea_de_16[30]), .out31(linea_de_16[31]),
    .sel(MAPAS0[4:0]));
  Decoder #(.select(5), .enable("false")) decoder_2 (
    .out0(linea_de_17[0]), .out1(linea_de_17[1]), .out2(linea_de_17[2]), .out3(linea_de_17[3]),
    .out4(linea_de_17[4]), .out5(linea_de_17[5]), .out6(linea_de_17[6]), .out7(linea_de_17[7]),
    .out8(linea_de_17[8]), .out9(linea_de_17[9]), .out10(linea_de_17[10]), .out11(linea_de_17[11]),
    .out12(linea_de_17[12]), .out13(linea_de_17[13]), .out14(linea_de_17[14]), .out15(linea_de_17[15]),
    .out16(linea_de_17[16]), .out17(linea_de_17[17]), .out18(linea_de_17[18]), .out19(linea_de_17[19]),
    .out20(linea_de_17[20]), .out21(linea_de_17[21]), .out22(linea_de_17[22]), .out23(linea_de_17[23]),
    .out24(linea_de_17[24]), .out25(linea_de_17[25]), .out26(linea_de_17[26]), .out27(linea_de_17[27]),
    .out28(linea_de_17[28]), .out29(linea_de_17[29]), .out30(linea_de_17[30]), .out31(linea_de_17[31]),
    .sel(MAPAS0[9:5]));
  Decoder #(.select(5), .enable("false")) decoder_3 (
    .out0(linea_de_19[0]), .out1(linea_de_19[1]), .out2(linea_de_19[2]), .out3(linea_de_19[3]),
    .out4(linea_de_19[4]), .out5(linea_de_19[5]), .out6(linea_de_19[6]), .out7(linea_de_19[7]),
    .out8(linea_de_19[8]), .out9(linea_de_19[9]), .out10(linea_de_19[10]), .out11(linea_de_19[11]),
    .out12(linea_de_19[12]), .out13(linea_de_19[13]), .out14(linea_de_19[14]), .out15(linea_de_19[15]),
    .out16(linea_de_19[16]), .out17(linea_de_19[17]), .out18(linea_de_19[18]), .out19(linea_de_19[19]),
    .out20(linea_de_19[20]), .out21(linea_de_19[21]), .out22(linea_de_19[22]), .out23(linea_de_19[23]),
    .out24(linea_de_19[24]), .out25(linea_de_19[25]), .out26(linea_de_19[26]), .out27(linea_de_19[27]),
    .out28(linea_de_19[28]), .out29(linea_de_19[29]), .out30(linea_de_19[30]), .out31(linea_de_19[31]),
    .sel(MAPAS0[14:10]));
  Decoder #(.select(5), .enable("false")) decoder_4 (
    .out0(linea_de_21[0]), .out1(linea_de_21[1]), .out2(linea_de_21[2]), .out3(linea_de_21[3]),
    .out4(linea_de_21[4]), .out5(linea_de_21[5]), .out6(linea_de_21[6]), .out7(linea_de_21[7]),
    .out8(linea_de_21[8]), .out9(linea_de_21[9]), .out10(linea_de_21[10]), .out11(linea_de_21[11]),
    .out12(linea_de_21[12]), .out13(linea_de_21[13]), .out14(linea_de_21[14]), .out15(linea_de_21[15]),
    .out16(linea_de_21[16]), .out17(linea_de_21[17]), .out18(linea_de_21[18]), .out19(linea_de_21[19]),
    .out20(linea_de_21[20]), .out21(linea_de_21[21]), .out22(linea_de_21[22]), .out23(linea_de_21[23]),
    .out24(linea_de_21[24]), .out25(linea_de_21[25]), .out26(linea_de_21[26]), .out27(linea_de_21[27]),
    .out28(linea_de_21[28]), .out29(linea_de_21[29]), .out30(linea_de_21[30]), .out31(linea_de_21[31]),
    .sel(MAPAS0[19:15]));
  Decoder #(.select(5), .enable("false")) decoder_5 (
    .out0(linea_de_22[0]), .out1(linea_de_22[1]), .out2(linea_de_22[2]), .out3(linea_de_22[3]),
    .out4(linea_de_22[4]), .out5(linea_de_22[5]), .out6(linea_de_22[6]), .out7(linea_de_22[7]),
    .out8(linea_de_22[8]), .out9(linea_de_22[9]), .out10(linea_de_22[10]), .out11(linea_de_22[11]),
    .out12(linea_de_22[12]), .out13(linea_de_22[13]), .out14(linea_de_22[14]), .out15(linea_de_22[15]),
    .out16(linea_de_22[16]), .out17(linea_de_22[17]), .out18(linea_de_22[18]), .out19(linea_de_22[19]),
    .out20(linea_de_22[20]), .out21(linea_de_22[21]), .out22(linea_de_22[22]), .out23(linea_de_22[23]),
    .out24(linea_de_22[24]), .out25(linea_de_22[25]), .out26(linea_de_22[26]), .out27(linea_de_22[27]),
    .out28(linea_de_22[28]), .out29(linea_de_22[29]), .out30(linea_de_22[30]), .out31(linea_de_22[31]),
    .sel(MAPAS0[24:20]));
  assign rep34 = {{31{INT_GPIO}}, INT_GPIO};  // Bit_Extender bit_extender_3
  assign rep35 = {{31{INT_GPIO_NMI}}, INT_GPIO_NMI};  // Bit_Extender bit_extender_4
  assign rep36 = {{31{INT_SPI2}}, INT_SPI2};  // Bit_Extender bit_extender_5
  assign rep37 = {{31{INT_UART0}}, INT_UART0};  // Bit_Extender bit_extender_6
  assign rep38 = {{31{INT_UART1}}, INT_UART1};  // Bit_Extender bit_extender_7
  Decoder #(.select(5), .enable("false")) decoder_6 (
    .out0(linea_de_23[0]), .out1(linea_de_23[1]), .out2(linea_de_23[2]), .out3(linea_de_23[3]),
    .out4(linea_de_23[4]), .out5(linea_de_23[5]), .out6(linea_de_23[6]), .out7(linea_de_23[7]),
    .out8(linea_de_23[8]), .out9(linea_de_23[9]), .out10(linea_de_23[10]), .out11(linea_de_23[11]),
    .out12(linea_de_23[12]), .out13(linea_de_23[13]), .out14(linea_de_23[14]), .out15(linea_de_23[15]),
    .out16(linea_de_23[16]), .out17(linea_de_23[17]), .out18(linea_de_23[18]), .out19(linea_de_23[19]),
    .out20(linea_de_23[20]), .out21(linea_de_23[21]), .out22(linea_de_23[22]), .out23(linea_de_23[23]),
    .out24(linea_de_23[24]), .out25(linea_de_23[25]), .out26(linea_de_23[26]), .out27(linea_de_23[27]),
    .out28(linea_de_23[28]), .out29(linea_de_23[29]), .out30(linea_de_23[30]), .out31(linea_de_23[31]),
    .sel(MAPAS0[29:25]));
  Decoder #(.select(5), .enable("false")) decoder_7 (
    .out0(linea_de_26[0]), .out1(linea_de_26[1]), .out2(linea_de_26[2]), .out3(linea_de_26[3]),
    .out4(linea_de_26[4]), .out5(linea_de_26[5]), .out6(linea_de_26[6]), .out7(linea_de_26[7]),
    .out8(linea_de_26[8]), .out9(linea_de_26[9]), .out10(linea_de_26[10]), .out11(linea_de_26[11]),
    .out12(linea_de_26[12]), .out13(linea_de_26[13]), .out14(linea_de_26[14]), .out15(linea_de_26[15]),
    .out16(linea_de_26[16]), .out17(linea_de_26[17]), .out18(linea_de_26[18]), .out19(linea_de_26[19]),
    .out20(linea_de_26[20]), .out21(linea_de_26[21]), .out22(linea_de_26[22]), .out23(linea_de_26[23]),
    .out24(linea_de_26[24]), .out25(linea_de_26[25]), .out26(linea_de_26[26]), .out27(linea_de_26[27]),
    .out28(linea_de_26[28]), .out29(linea_de_26[29]), .out30(linea_de_26[30]), .out31(linea_de_26[31]),
    .sel(MAPAS1[4:0]));
  Decoder #(.select(5), .enable("false")) decoder_8 (
    .out0(linea_de_27[0]), .out1(linea_de_27[1]), .out2(linea_de_27[2]), .out3(linea_de_27[3]),
    .out4(linea_de_27[4]), .out5(linea_de_27[5]), .out6(linea_de_27[6]), .out7(linea_de_27[7]),
    .out8(linea_de_27[8]), .out9(linea_de_27[9]), .out10(linea_de_27[10]), .out11(linea_de_27[11]),
    .out12(linea_de_27[12]), .out13(linea_de_27[13]), .out14(linea_de_27[14]), .out15(linea_de_27[15]),
    .out16(linea_de_27[16]), .out17(linea_de_27[17]), .out18(linea_de_27[18]), .out19(linea_de_27[19]),
    .out20(linea_de_27[20]), .out21(linea_de_27[21]), .out22(linea_de_27[22]), .out23(linea_de_27[23]),
    .out24(linea_de_27[24]), .out25(linea_de_27[25]), .out26(linea_de_27[26]), .out27(linea_de_27[27]),
    .out28(linea_de_27[28]), .out29(linea_de_27[29]), .out30(linea_de_27[30]), .out31(linea_de_27[31]),
    .sel(MAPAS1[9:5]));
  Decoder #(.select(5), .enable("false")) decoder_9 (
    .out0(linea_de_29[0]), .out1(linea_de_29[1]), .out2(linea_de_29[2]), .out3(linea_de_29[3]),
    .out4(linea_de_29[4]), .out5(linea_de_29[5]), .out6(linea_de_29[6]), .out7(linea_de_29[7]),
    .out8(linea_de_29[8]), .out9(linea_de_29[9]), .out10(linea_de_29[10]), .out11(linea_de_29[11]),
    .out12(linea_de_29[12]), .out13(linea_de_29[13]), .out14(linea_de_29[14]), .out15(linea_de_29[15]),
    .out16(linea_de_29[16]), .out17(linea_de_29[17]), .out18(linea_de_29[18]), .out19(linea_de_29[19]),
    .out20(linea_de_29[20]), .out21(linea_de_29[21]), .out22(linea_de_29[22]), .out23(linea_de_29[23]),
    .out24(linea_de_29[24]), .out25(linea_de_29[25]), .out26(linea_de_29[26]), .out27(linea_de_29[27]),
    .out28(linea_de_29[28]), .out29(linea_de_29[29]), .out30(linea_de_29[30]), .out31(linea_de_29[31]),
    .sel(MAPAS1[14:10]));
  Decoder #(.select(5), .enable("false")) decoder_10 (
    .out0(linea_de_32[0]), .out1(linea_de_32[1]), .out2(linea_de_32[2]), .out3(linea_de_32[3]),
    .out4(linea_de_32[4]), .out5(linea_de_32[5]), .out6(linea_de_32[6]), .out7(linea_de_32[7]),
    .out8(linea_de_32[8]), .out9(linea_de_32[9]), .out10(linea_de_32[10]), .out11(linea_de_32[11]),
    .out12(linea_de_32[12]), .out13(linea_de_32[13]), .out14(linea_de_32[14]), .out15(linea_de_32[15]),
    .out16(linea_de_32[16]), .out17(linea_de_32[17]), .out18(linea_de_32[18]), .out19(linea_de_32[19]),
    .out20(linea_de_32[20]), .out21(linea_de_32[21]), .out22(linea_de_32[22]), .out23(linea_de_32[23]),
    .out24(linea_de_32[24]), .out25(linea_de_32[25]), .out26(linea_de_32[26]), .out27(linea_de_32[27]),
    .out28(linea_de_32[28]), .out29(linea_de_32[29]), .out30(linea_de_32[30]), .out31(linea_de_32[31]),
    .sel(MAPAS1[19:15]));
  Decoder #(.select(5), .enable("false")) decoder_11 (
    .out0(linea_de_33[0]), .out1(linea_de_33[1]), .out2(linea_de_33[2]), .out3(linea_de_33[3]),
    .out4(linea_de_33[4]), .out5(linea_de_33[5]), .out6(linea_de_33[6]), .out7(linea_de_33[7]),
    .out8(linea_de_33[8]), .out9(linea_de_33[9]), .out10(linea_de_33[10]), .out11(linea_de_33[11]),
    .out12(linea_de_33[12]), .out13(linea_de_33[13]), .out14(linea_de_33[14]), .out15(linea_de_33[15]),
    .out16(linea_de_33[16]), .out17(linea_de_33[17]), .out18(linea_de_33[18]), .out19(linea_de_33[19]),
    .out20(linea_de_33[20]), .out21(linea_de_33[21]), .out22(linea_de_33[22]), .out23(linea_de_33[23]),
    .out24(linea_de_33[24]), .out25(linea_de_33[25]), .out26(linea_de_33[26]), .out27(linea_de_33[27]),
    .out28(linea_de_33[28]), .out29(linea_de_33[29]), .out30(linea_de_33[30]), .out31(linea_de_33[31]),
    .sel(MAPAS1[24:20]));
  assign rep39 = {{31{INT_LEDC}}, INT_LEDC};  // Bit_Extender bit_extender_8
  assign rep40 = {{31{INT_USB_SERIAL_JTAG}}, INT_USB_SERIAL_JTAG};  // Bit_Extender bit_extender_9
  assign rep41 = {{31{INT_RTC_CORE}}, INT_RTC_CORE};  // Bit_Extender bit_extender_10
  assign rep42 = {{31{INT_I2C_EXT0}}, INT_I2C_EXT0};  // Bit_Extender bit_extender_11
  assign rep43 = {{31{INT_TG0_T0}}, INT_TG0_T0};  // Bit_Extender bit_extender_12
  assign rep44 = {{31{INT_TG0_WDT}}, INT_TG0_WDT};  // Bit_Extender bit_extender_13
  Decoder #(.select(5), .enable("false")) decoder_12 (
    .out0(linea_de_34[0]), .out1(linea_de_34[1]), .out2(linea_de_34[2]), .out3(linea_de_34[3]),
    .out4(linea_de_34[4]), .out5(linea_de_34[5]), .out6(linea_de_34[6]), .out7(linea_de_34[7]),
    .out8(linea_de_34[8]), .out9(linea_de_34[9]), .out10(linea_de_34[10]), .out11(linea_de_34[11]),
    .out12(linea_de_34[12]), .out13(linea_de_34[13]), .out14(linea_de_34[14]), .out15(linea_de_34[15]),
    .out16(linea_de_34[16]), .out17(linea_de_34[17]), .out18(linea_de_34[18]), .out19(linea_de_34[19]),
    .out20(linea_de_34[20]), .out21(linea_de_34[21]), .out22(linea_de_34[22]), .out23(linea_de_34[23]),
    .out24(linea_de_34[24]), .out25(linea_de_34[25]), .out26(linea_de_34[26]), .out27(linea_de_34[27]),
    .out28(linea_de_34[28]), .out29(linea_de_34[29]), .out30(linea_de_34[30]), .out31(linea_de_34[31]),
    .sel(MAPAS1[29:25]));
  Decoder #(.select(5), .enable("false")) decoder_13 (
    .out0(linea_de_35[0]), .out1(linea_de_35[1]), .out2(linea_de_35[2]), .out3(linea_de_35[3]),
    .out4(linea_de_35[4]), .out5(linea_de_35[5]), .out6(linea_de_35[6]), .out7(linea_de_35[7]),
    .out8(linea_de_35[8]), .out9(linea_de_35[9]), .out10(linea_de_35[10]), .out11(linea_de_35[11]),
    .out12(linea_de_35[12]), .out13(linea_de_35[13]), .out14(linea_de_35[14]), .out15(linea_de_35[15]),
    .out16(linea_de_35[16]), .out17(linea_de_35[17]), .out18(linea_de_35[18]), .out19(linea_de_35[19]),
    .out20(linea_de_35[20]), .out21(linea_de_35[21]), .out22(linea_de_35[22]), .out23(linea_de_35[23]),
    .out24(linea_de_35[24]), .out25(linea_de_35[25]), .out26(linea_de_35[26]), .out27(linea_de_35[27]),
    .out28(linea_de_35[28]), .out29(linea_de_35[29]), .out30(linea_de_35[30]), .out31(linea_de_35[31]),
    .sel(MAPAS2[4:0]));
  Decoder #(.select(5), .enable("false")) decoder_14 (
    .out0(linea_de_37[0]), .out1(linea_de_37[1]), .out2(linea_de_37[2]), .out3(linea_de_37[3]),
    .out4(linea_de_37[4]), .out5(linea_de_37[5]), .out6(linea_de_37[6]), .out7(linea_de_37[7]),
    .out8(linea_de_37[8]), .out9(linea_de_37[9]), .out10(linea_de_37[10]), .out11(linea_de_37[11]),
    .out12(linea_de_37[12]), .out13(linea_de_37[13]), .out14(linea_de_37[14]), .out15(linea_de_37[15]),
    .out16(linea_de_37[16]), .out17(linea_de_37[17]), .out18(linea_de_37[18]), .out19(linea_de_37[19]),
    .out20(linea_de_37[20]), .out21(linea_de_37[21]), .out22(linea_de_37[22]), .out23(linea_de_37[23]),
    .out24(linea_de_37[24]), .out25(linea_de_37[25]), .out26(linea_de_37[26]), .out27(linea_de_37[27]),
    .out28(linea_de_37[28]), .out29(linea_de_37[29]), .out30(linea_de_37[30]), .out31(linea_de_37[31]),
    .sel(MAPAS2[9:5]));
  Decoder #(.select(5), .enable("false")) decoder_15 (
    .out0(linea_de_38[0]), .out1(linea_de_38[1]), .out2(linea_de_38[2]), .out3(linea_de_38[3]),
    .out4(linea_de_38[4]), .out5(linea_de_38[5]), .out6(linea_de_38[6]), .out7(linea_de_38[7]),
    .out8(linea_de_38[8]), .out9(linea_de_38[9]), .out10(linea_de_38[10]), .out11(linea_de_38[11]),
    .out12(linea_de_38[12]), .out13(linea_de_38[13]), .out14(linea_de_38[14]), .out15(linea_de_38[15]),
    .out16(linea_de_38[16]), .out17(linea_de_38[17]), .out18(linea_de_38[18]), .out19(linea_de_38[19]),
    .out20(linea_de_38[20]), .out21(linea_de_38[21]), .out22(linea_de_38[22]), .out23(linea_de_38[23]),
    .out24(linea_de_38[24]), .out25(linea_de_38[25]), .out26(linea_de_38[26]), .out27(linea_de_38[27]),
    .out28(linea_de_38[28]), .out29(linea_de_38[29]), .out30(linea_de_38[30]), .out31(linea_de_38[31]),
    .sel(MAPAS2[14:10]));
  Decoder #(.select(5), .enable("false")) decoder_16 (
    .out0(linea_de_39[0]), .out1(linea_de_39[1]), .out2(linea_de_39[2]), .out3(linea_de_39[3]),
    .out4(linea_de_39[4]), .out5(linea_de_39[5]), .out6(linea_de_39[6]), .out7(linea_de_39[7]),
    .out8(linea_de_39[8]), .out9(linea_de_39[9]), .out10(linea_de_39[10]), .out11(linea_de_39[11]),
    .out12(linea_de_39[12]), .out13(linea_de_39[13]), .out14(linea_de_39[14]), .out15(linea_de_39[15]),
    .out16(linea_de_39[16]), .out17(linea_de_39[17]), .out18(linea_de_39[18]), .out19(linea_de_39[19]),
    .out20(linea_de_39[20]), .out21(linea_de_39[21]), .out22(linea_de_39[22]), .out23(linea_de_39[23]),
    .out24(linea_de_39[24]), .out25(linea_de_39[25]), .out26(linea_de_39[26]), .out27(linea_de_39[27]),
    .out28(linea_de_39[28]), .out29(linea_de_39[29]), .out30(linea_de_39[30]), .out31(linea_de_39[31]),
    .sel(MAPAS2[19:15]));
  Decoder #(.select(5), .enable("false")) decoder_17 (
    .out0(linea_de_49[0]), .out1(linea_de_49[1]), .out2(linea_de_49[2]), .out3(linea_de_49[3]),
    .out4(linea_de_49[4]), .out5(linea_de_49[5]), .out6(linea_de_49[6]), .out7(linea_de_49[7]),
    .out8(linea_de_49[8]), .out9(linea_de_49[9]), .out10(linea_de_49[10]), .out11(linea_de_49[11]),
    .out12(linea_de_49[12]), .out13(linea_de_49[13]), .out14(linea_de_49[14]), .out15(linea_de_49[15]),
    .out16(linea_de_49[16]), .out17(linea_de_49[17]), .out18(linea_de_49[18]), .out19(linea_de_49[19]),
    .out20(linea_de_49[20]), .out21(linea_de_49[21]), .out22(linea_de_49[22]), .out23(linea_de_49[23]),
    .out24(linea_de_49[24]), .out25(linea_de_49[25]), .out26(linea_de_49[26]), .out27(linea_de_49[27]),
    .out28(linea_de_49[28]), .out29(linea_de_49[29]), .out30(linea_de_49[30]), .out31(linea_de_49[31]),
    .sel(MAPAS2[24:20]));
  assign rep45 = {{31{INT_TG1_T0}}, INT_TG1_T0};  // Bit_Extender bit_extender_14
  assign rep46 = {{31{INT_TG1_WDT}}, INT_TG1_WDT};  // Bit_Extender bit_extender_15
  assign rep47 = {{31{INT_SYSTIMER_T0}}, INT_SYSTIMER_T0};  // Bit_Extender bit_extender_16
  assign rep48 = {{31{INT_SYSTIMER_T1}}, INT_SYSTIMER_T1};  // Bit_Extender bit_extender_17
  assign rep49 = {{31{INT_SYSTIMER_T2}}, INT_SYSTIMER_T2};  // Bit_Extender bit_extender_18
  assign rep50 = {{31{INT_SHA}}, INT_SHA};  // Bit_Extender bit_extender_19
  Decoder #(.select(5), .enable("false")) decoder_18 (
    .out0(linea_de_50[0]), .out1(linea_de_50[1]), .out2(linea_de_50[2]), .out3(linea_de_50[3]),
    .out4(linea_de_50[4]), .out5(linea_de_50[5]), .out6(linea_de_50[6]), .out7(linea_de_50[7]),
    .out8(linea_de_50[8]), .out9(linea_de_50[9]), .out10(linea_de_50[10]), .out11(linea_de_50[11]),
    .out12(linea_de_50[12]), .out13(linea_de_50[13]), .out14(linea_de_50[14]), .out15(linea_de_50[15]),
    .out16(linea_de_50[16]), .out17(linea_de_50[17]), .out18(linea_de_50[18]), .out19(linea_de_50[19]),
    .out20(linea_de_50[20]), .out21(linea_de_50[21]), .out22(linea_de_50[22]), .out23(linea_de_50[23]),
    .out24(linea_de_50[24]), .out25(linea_de_50[25]), .out26(linea_de_50[26]), .out27(linea_de_50[27]),
    .out28(linea_de_50[28]), .out29(linea_de_50[29]), .out30(linea_de_50[30]), .out31(linea_de_50[31]),
    .sel(MAPAS2[29:25]));
  Decoder #(.select(5), .enable("false")) decoder_19 (
    .out0(linea_de_51[0]), .out1(linea_de_51[1]), .out2(linea_de_51[2]), .out3(linea_de_51[3]),
    .out4(linea_de_51[4]), .out5(linea_de_51[5]), .out6(linea_de_51[6]), .out7(linea_de_51[7]),
    .out8(linea_de_51[8]), .out9(linea_de_51[9]), .out10(linea_de_51[10]), .out11(linea_de_51[11]),
    .out12(linea_de_51[12]), .out13(linea_de_51[13]), .out14(linea_de_51[14]), .out15(linea_de_51[15]),
    .out16(linea_de_51[16]), .out17(linea_de_51[17]), .out18(linea_de_51[18]), .out19(linea_de_51[19]),
    .out20(linea_de_51[20]), .out21(linea_de_51[21]), .out22(linea_de_51[22]), .out23(linea_de_51[23]),
    .out24(linea_de_51[24]), .out25(linea_de_51[25]), .out26(linea_de_51[26]), .out27(linea_de_51[27]),
    .out28(linea_de_51[28]), .out29(linea_de_51[29]), .out30(linea_de_51[30]), .out31(linea_de_51[31]),
    .sel(MAPAS3[4:0]));
  Decoder #(.select(5), .enable("false")) decoder_20 (
    .out0(linea_de_52[0]), .out1(linea_de_52[1]), .out2(linea_de_52[2]), .out3(linea_de_52[3]),
    .out4(linea_de_52[4]), .out5(linea_de_52[5]), .out6(linea_de_52[6]), .out7(linea_de_52[7]),
    .out8(linea_de_52[8]), .out9(linea_de_52[9]), .out10(linea_de_52[10]), .out11(linea_de_52[11]),
    .out12(linea_de_52[12]), .out13(linea_de_52[13]), .out14(linea_de_52[14]), .out15(linea_de_52[15]),
    .out16(linea_de_52[16]), .out17(linea_de_52[17]), .out18(linea_de_52[18]), .out19(linea_de_52[19]),
    .out20(linea_de_52[20]), .out21(linea_de_52[21]), .out22(linea_de_52[22]), .out23(linea_de_52[23]),
    .out24(linea_de_52[24]), .out25(linea_de_52[25]), .out26(linea_de_52[26]), .out27(linea_de_52[27]),
    .out28(linea_de_52[28]), .out29(linea_de_52[29]), .out30(linea_de_52[30]), .out31(linea_de_52[31]),
    .sel(MAPAS3[9:5]));
  Decoder #(.select(5), .enable("false")) decoder_21 (
    .out0(linea_de_53[0]), .out1(linea_de_53[1]), .out2(linea_de_53[2]), .out3(linea_de_53[3]),
    .out4(linea_de_53[4]), .out5(linea_de_53[5]), .out6(linea_de_53[6]), .out7(linea_de_53[7]),
    .out8(linea_de_53[8]), .out9(linea_de_53[9]), .out10(linea_de_53[10]), .out11(linea_de_53[11]),
    .out12(linea_de_53[12]), .out13(linea_de_53[13]), .out14(linea_de_53[14]), .out15(linea_de_53[15]),
    .out16(linea_de_53[16]), .out17(linea_de_53[17]), .out18(linea_de_53[18]), .out19(linea_de_53[19]),
    .out20(linea_de_53[20]), .out21(linea_de_53[21]), .out22(linea_de_53[22]), .out23(linea_de_53[23]),
    .out24(linea_de_53[24]), .out25(linea_de_53[25]), .out26(linea_de_53[26]), .out27(linea_de_53[27]),
    .out28(linea_de_53[28]), .out29(linea_de_53[29]), .out30(linea_de_53[30]), .out31(linea_de_53[31]),
    .sel(MAPAS3[14:10]));
  assign rep51 = {{31{INT_FROM_CPU0}}, INT_FROM_CPU0};  // Bit_Extender bit_extender_20
  assign rep52 = {{31{INT_FROM_CPU1}}, INT_FROM_CPU1};  // Bit_Extender bit_extender_21
  assign rep53 = {{31{INT_FROM_CPU2}}, INT_FROM_CPU2};  // Bit_Extender bit_extender_22
  assign rep54 = {{31{INT_FROM_CPU3}}, INT_FROM_CPU3};  // Bit_Extender bit_extender_23
  Comparator #(.width(4), .mode("unsigned")) comparator_1 (
    .a(PRIORIDADES0[3:0]), .b(PRIORIDADES3[31:28]), .lt(lt107));  // open: gt, eq
  Comparator #(.width(4), .mode("unsigned")) comparator_2 (
    .a(PRIORIDADES0[7:4]), .b(PRIORIDADES3[31:28]), .lt(lt109));  // open: gt, eq
  Comparator #(.width(4), .mode("unsigned")) comparator_3 (
    .a(PRIORIDADES0[11:8]), .b(PRIORIDADES3[31:28]), .lt(lt111));  // open: gt, eq
  Comparator #(.width(4), .mode("unsigned")) comparator_4 (
    .a(PRIORIDADES0[15:12]), .b(PRIORIDADES3[31:28]), .lt(lt113));  // open: gt, eq
  Comparator #(.width(4), .mode("unsigned")) comparator_5 (
    .a(PRIORIDADES0[19:16]), .b(PRIORIDADES3[31:28]), .lt(lt115));  // open: gt, eq
  Comparator #(.width(4), .mode("unsigned")) comparator_6 (
    .a(PRIORIDADES0[23:20]), .b(PRIORIDADES3[31:28]), .lt(lt117));  // open: gt, eq
  Comparator #(.width(4), .mode("unsigned")) comparator_7 (
    .a(PRIORIDADES0[27:24]), .b(PRIORIDADES3[31:28]), .lt(lt119));  // open: gt, eq
  Comparator #(.width(4), .mode("unsigned")) comparator_8 (
    .a(PRIORIDADES0[31:28]), .b(PRIORIDADES3[31:28]), .lt(lt121));  // open: gt, eq
  Comparator #(.width(4), .mode("unsigned")) comparator_9 (
    .a(PRIORIDADES1[3:0]), .b(PRIORIDADES3[31:28]), .lt(lt123));  // open: gt, eq
  Comparator #(.width(4), .mode("unsigned")) comparator_10 (
    .a(PRIORIDADES1[7:4]), .b(PRIORIDADES3[31:28]), .lt(lt125));  // open: gt, eq
  Comparator #(.width(4), .mode("unsigned")) comparator_11 (
    .a(PRIORIDADES1[11:8]), .b(PRIORIDADES3[31:28]), .lt(lt127));  // open: gt, eq
  Comparator #(.width(4), .mode("unsigned")) comparator_12 (
    .a(PRIORIDADES1[15:12]), .b(PRIORIDADES3[31:28]), .lt(lt129));  // open: gt, eq
  Comparator #(.width(4), .mode("unsigned")) comparator_13 (
    .a(PRIORIDADES1[19:16]), .b(PRIORIDADES3[31:28]), .lt(lt131));  // open: gt, eq
  Comparator #(.width(4), .mode("unsigned")) comparator_14 (
    .a(PRIORIDADES1[23:20]), .b(PRIORIDADES3[31:28]), .lt(lt133));  // open: gt, eq
  Comparator #(.width(4), .mode("unsigned")) comparator_15 (
    .a(4'b0000), .b(PRIORIDADES0[3:0]), .lt(lt170));  // open: gt, eq
  Comparator #(.width(4), .mode("unsigned")) comparator_16 (
    .a(PRIORIDADES0[7:4]), .b(PRIORIDADES0[11:8]), .lt(lt174));  // open: gt, eq
  Comparator #(.width(4), .mode("unsigned")) comparator_17 (
    .a(PRIORIDADES1[7:4]), .b(PRIORIDADES1[11:8]), .lt(lt190));  // open: gt, eq
  Comparator #(.width(4), .mode("unsigned")) comparator_18 (
    .a(PRIORIDADES2[7:4]), .b(PRIORIDADES2[11:8]), .lt(lt206));  // open: gt, eq
  Comparator #(.width(4), .mode("unsigned")) comparator_19 (
    .a(PRIORIDADES3[7:4]), .b(PRIORIDADES3[11:8]), .lt(lt222));  // open: gt, eq
  assign dato_escrito = WD & rep295;  // AND_Gate and_9, 32 bits wide
  and and_10 (and298, escribe, registros_acceso);
  assign rep300 = {{31{registros_acceso}}, registros_acceso};  // Bit_Extender bit_extender_24
  Comparator #(.width(4), .mode("unsigned")) comparator_20 (
    .a(PRIORIDADES1[27:24]), .b(PRIORIDADES3[31:28]), .lt(lt135));  // open: gt, eq
  Comparator #(.width(4), .mode("unsigned")) comparator_21 (
    .a(PRIORIDADES1[31:28]), .b(PRIORIDADES3[31:28]), .lt(lt137));  // open: gt, eq
  Comparator #(.width(4), .mode("unsigned")) comparator_22 (
    .a(PRIORIDADES2[3:0]), .b(PRIORIDADES3[31:28]), .lt(lt139));  // open: gt, eq
  Comparator #(.width(4), .mode("unsigned")) comparator_23 (
    .a(PRIORIDADES2[7:4]), .b(PRIORIDADES3[31:28]), .lt(lt141));  // open: gt, eq
  Comparator #(.width(4), .mode("unsigned")) comparator_24 (
    .a(PRIORIDADES2[11:8]), .b(PRIORIDADES3[31:28]), .lt(lt143));  // open: gt, eq
  Comparator #(.width(4), .mode("unsigned")) comparator_25 (
    .a(PRIORIDADES2[15:12]), .b(PRIORIDADES3[31:28]), .lt(lt145));  // open: gt, eq
  Comparator #(.width(4), .mode("unsigned")) comparator_26 (
    .a(PRIORIDADES2[19:16]), .b(PRIORIDADES3[31:28]), .lt(lt147));  // open: gt, eq
  Comparator #(.width(4), .mode("unsigned")) comparator_27 (
    .a(PRIORIDADES2[23:20]), .b(PRIORIDADES3[31:28]), .lt(lt149));  // open: gt, eq
  Comparator #(.width(4), .mode("unsigned")) comparator_28 (
    .a(PRIORIDADES2[27:24]), .b(PRIORIDADES3[31:28]), .lt(lt151));  // open: gt, eq
  Comparator #(.width(4), .mode("unsigned")) comparator_29 (
    .a(PRIORIDADES2[31:28]), .b(PRIORIDADES3[31:28]), .lt(lt153));  // open: gt, eq
  Comparator #(.width(4), .mode("unsigned")) comparator_30 (
    .a(PRIORIDADES3[3:0]), .b(PRIORIDADES3[31:28]), .lt(lt155));  // open: gt, eq
  Comparator #(.width(4), .mode("unsigned")) comparator_31 (
    .a(PRIORIDADES3[7:4]), .b(PRIORIDADES3[31:28]), .lt(lt157));  // open: gt, eq
  Comparator #(.width(4), .mode("unsigned")) comparator_32 (
    .a(PRIORIDADES3[11:8]), .b(PRIORIDADES3[31:28]), .lt(lt159));  // open: gt, eq
  Comparator #(.width(4), .mode("unsigned")) comparator_33 (
    .a(PRIORIDADES3[15:12]), .b(PRIORIDADES3[31:28]), .lt(lt161));  // open: gt, eq
  Comparator #(.width(4), .mode("unsigned")) comparator_34 (
    .a(PRIORIDADES3[19:16]), .b(PRIORIDADES3[31:28]), .lt(lt163));  // open: gt, eq
  Comparator #(.width(4), .mode("unsigned")) comparator_35 (
    .a(PRIORIDADES3[23:20]), .b(PRIORIDADES3[31:28]), .lt(lt165));  // open: gt, eq
  Comparator #(.width(4), .mode("unsigned")) comparator_36 (
    .a(PRIORIDADES3[27:24]), .b(PRIORIDADES3[31:28]), .lt(lt167));  // open: gt, eq
  Comparator #(.width(4), .mode("unsigned")) comparator_37 (
    .a(PRIORIDADES0[15:12]), .b(PRIORIDADES0[19:16]), .lt(lt178));  // open: gt, eq
  Comparator #(.width(4), .mode("unsigned")) comparator_38 (
    .a(PRIORIDADES0[23:20]), .b(PRIORIDADES0[27:24]), .lt(lt182));  // open: gt, eq
  Comparator #(.width(4), .mode("unsigned")) comparator_39 (
    .a(PRIORIDADES0[31:28]), .b(PRIORIDADES1[3:0]), .lt(lt186));  // open: gt, eq
  Comparator #(.width(4), .mode("unsigned")) comparator_40 (
    .a(PRIORIDADES1[15:12]), .b(PRIORIDADES1[19:16]), .lt(lt194));  // open: gt, eq
  Comparator #(.width(4), .mode("unsigned")) comparator_41 (
    .a(PRIORIDADES1[23:20]), .b(PRIORIDADES1[27:24]), .lt(lt198));  // open: gt, eq
  Comparator #(.width(4), .mode("unsigned")) comparator_42 (
    .a(PRIORIDADES1[31:28]), .b(PRIORIDADES2[3:0]), .lt(lt202));  // open: gt, eq
  Comparator #(.width(4), .mode("unsigned")) comparator_43 (
    .a(PRIORIDADES2[15:12]), .b(PRIORIDADES2[19:16]), .lt(lt210));  // open: gt, eq
  Comparator #(.width(4), .mode("unsigned")) comparator_44 (
    .a(PRIORIDADES2[23:20]), .b(PRIORIDADES2[27:24]), .lt(lt214));  // open: gt, eq
  Comparator #(.width(4), .mode("unsigned")) comparator_45 (
    .a(PRIORIDADES2[31:28]), .b(PRIORIDADES3[3:0]), .lt(lt218));  // open: gt, eq
  Comparator #(.width(4), .mode("unsigned")) comparator_46 (
    .a(PRIORIDADES3[15:12]), .b(PRIORIDADES3[19:16]), .lt(lt226));  // open: gt, eq
  Comparator #(.width(4), .mode("unsigned")) comparator_47 (
    .a(PRIORIDADES3[23:20]), .b(PRIORIDADES3[27:24]), .lt(lt230));  // open: gt, eq
  assign registros_bits_fijos = registros_valor_reset & not296;  // AND_Gate and_11, 32 bits wide
  assign xor299 = registros_guardado ^ registros_reset_rw;  // XOR_Gate xor_1, 32 bits wide
  Decoder #(.select(5), .enable("false")) decoder_22 (
    .out0(pag_0), .out1(pag_1), .out2(pag_2), .out3(pag_3), .out4(pag_4), .out5(pag_5), .out6(pag_6),
    .out7(pag_7), .out8(pag_8), .out9(pag_9), .out10(pag_10), .out11(pag_11), .out12(pag_12), .out13(pag_13),
    .out14(pag_14), .out15(pag_15), .out16(pag_16), .out17(pag_17), .out18(pag_18), .out19(pag_19),
    .out20(pag_20), .out21(pag_21), .out22(pag_22), .out23(pag_23), .out24(pag_24), .out25(pag_25),
    .out26(pag_26), .out27(pag_27), .out28(pag_28), .out29(pag_29), .out30(pag_30), .out31(pag_31),
    .sel(dir_registro[9:5]));
  Decoder #(.select(5), .enable("false")) decoder_23 (
    .out0(lin_0), .out1(lin_1), .out2(lin_2), .out3(lin_3), .out4(lin_4), .out5(lin_5), .out6(lin_6),
    .out7(lin_7), .out8(lin_8), .out9(lin_9), .out10(lin_10), .out11(lin_11), .out12(lin_12), .out13(lin_13),
    .out14(lin_14), .out15(lin_15), .out16(lin_16), .out17(lin_17), .out18(lin_18), .out19(lin_19),
    .out20(lin_20), .out21(lin_21), .out22(lin_22), .out23(lin_23), .out24(lin_24), .out25(lin_25),
    .out26(lin_26), .out27(lin_27), .out28(lin_28), .out29(lin_29), .out30(lin_30), .out31(lin_31),
    .sel(dir_registro[4:0]));
  not not_5 (not108, lt107);
  not not_6 (not110, lt109);
  not not_7 (not112, lt111);
  not not_8 (not114, lt113);
  not not_9 (not116, lt115);
  not not_10 (not118, lt117);
  not not_11 (not120, lt119);
  not not_12 (not122, lt121);
  not not_13 (not124, lt123);
  not not_14 (not126, lt125);
  not not_15 (not128, lt127);
  not not_16 (not130, lt129);
  not not_17 (not132, lt131);
  not not_18 (not134, lt133);
  not not_19 (not136, lt135);
  not not_20 (not138, lt137);
  not not_21 (not140, lt139);
  not not_22 (not142, lt141);
  not not_23 (not144, lt143);
  not not_24 (not146, lt145);
  not not_25 (not148, lt147);
  not not_26 (not150, lt149);
  not not_27 (not152, lt151);
  not not_28 (not154, lt153);
  not not_29 (not156, lt155);
  not not_30 (not158, lt157);
  not not_31 (not160, lt159);
  not not_32 (not162, lt161);
  not not_33 (not164, lt163);
  not not_34 (not166, lt165);
  not not_35 (not168, lt167);
  not not_36 (not171, lt170);
  not not_37 (not175, lt174);
  not not_38 (not179, lt178);
  not not_39 (not183, lt182);
  not not_40 (not187, lt186);
  not not_41 (not191, lt190);
  not not_42 (not195, lt194);
  not not_43 (not199, lt198);
  not not_44 (not203, lt202);
  not not_45 (not207, lt206);
  not not_46 (not211, lt210);
  not not_47 (not215, lt214);
  not not_48 (not219, lt218);
  not not_49 (not223, lt222);
  not not_50 (not227, lt226);
  not not_51 (not231, lt230);
  assign and297 = dato_escrito & registros_bits_rw;  // AND_Gate and_12, 32 bits wide
  assign registros_valor = xor299 | registros_bits_fijos;  // OR_Gate or_1, 32 bits wide
  and and_13 (r080, SEL, pag_1, lin_0);
  and and_14 (r084, SEL, pag_1, lin_1);
  and and_15 (r088, SEL, pag_1, lin_2);
  and and_16 (r08C, SEL, pag_1, lin_3);
  and and_17 (r094, SEL, pag_1, lin_5);
  and and_18 (r098, SEL, pag_1, lin_6);
  and and_19 (r09C, SEL, pag_1, lin_7);
  and and_20 (r040, SEL, pag_0, lin_16);
  and and_21 (r044, SEL, pag_0, lin_17);
  and and_22 (r04C, SEL, pag_0, lin_19);
  and and_23 (r054, SEL, pag_0, lin_21);
  and and_24 (r058, SEL, pag_0, lin_22);
  and and_25 (r05C, SEL, pag_0, lin_23);
  and and_26 (r068, SEL, pag_0, lin_26);
  and and_27 (r06C, SEL, pag_0, lin_27);
  and and_28 (r074, SEL, pag_0, lin_29);
  and and_29 (r0C4, SEL, pag_1, lin_17);
  and and_30 (r0C8, SEL, pag_1, lin_18);
  and and_31 (r0CC, SEL, pag_1, lin_19);
  and and_32 (r0D0, SEL, pag_1, lin_20);
  and and_33 (r0D4, SEL, pag_1, lin_21);
  assign aporte_16_GPIO = linea_de_16 & rep34;  // AND_Gate and_34, 32 bits wide
  assign aporte_17_GPIO_NMI = linea_de_17 & rep35;  // AND_Gate and_35, 32 bits wide
  assign aporte_19_SPI2 = linea_de_19 & rep36;  // AND_Gate and_36, 32 bits wide
  assign aporte_21_UART0 = linea_de_21 & rep37;  // AND_Gate and_37, 32 bits wide
  assign aporte_22_UART1 = linea_de_22 & rep38;  // AND_Gate and_38, 32 bits wide
  assign aporte_23_LEDC = linea_de_23 & rep39;  // AND_Gate and_39, 32 bits wide
  assign aporte_26_USB_SERIAL_JTAG = linea_de_26 & rep40;  // AND_Gate and_40, 32 bits wide
  assign aporte_27_RTC_CORE = linea_de_27 & rep41;  // AND_Gate and_41, 32 bits wide
  assign aporte_29_I2C_EXT0 = linea_de_29 & rep42;  // AND_Gate and_42, 32 bits wide
  assign aporte_32_TG0_T0 = linea_de_32 & rep43;  // AND_Gate and_43, 32 bits wide
  assign aporte_33_TG0_WDT = linea_de_33 & rep44;  // AND_Gate and_44, 32 bits wide
  assign aporte_34_TG1_T0 = linea_de_34 & rep45;  // AND_Gate and_45, 32 bits wide
  assign aporte_35_TG1_WDT = linea_de_35 & rep46;  // AND_Gate and_46, 32 bits wide
  assign aporte_37_SYSTIMER_T0 = linea_de_37 & rep47;  // AND_Gate and_47, 32 bits wide
  assign aporte_38_SYSTIMER_T1 = linea_de_38 & rep48;  // AND_Gate and_48, 32 bits wide
  assign aporte_39_SYSTIMER_T2 = linea_de_39 & rep49;  // AND_Gate and_49, 32 bits wide
  assign aporte_49_SHA = linea_de_49 & rep50;  // AND_Gate and_50, 32 bits wide
  assign aporte_50_FROM_CPU0 = linea_de_50 & rep51;  // AND_Gate and_51, 32 bits wide
  assign aporte_51_FROM_CPU1 = linea_de_51 & rep52;  // AND_Gate and_52, 32 bits wide
  assign aporte_52_FROM_CPU2 = linea_de_52 & rep53;  // AND_Gate and_53, 32 bits wide
  assign aporte_53_FROM_CPU3 = linea_de_53 & rep54;  // AND_Gate and_54, 32 bits wide
  and and_55 (r104, SEL, pag_2, lin_1);
  and and_56 (r108, SEL, pag_2, lin_2);
  and and_57 (r10C, SEL, pag_2, lin_3);
  and and_58 (r118, SEL, pag_2, lin_6);
  and and_59 (r11C, SEL, pag_2, lin_7);
  and and_60 (r120, SEL, pag_2, lin_8);
  and and_61 (r124, SEL, pag_2, lin_9);
  and and_62 (r128, SEL, pag_2, lin_10);
  and and_63 (r12C, SEL, pag_2, lin_11);
  and and_64 (r130, SEL, pag_2, lin_12);
  and and_65 (r134, SEL, pag_2, lin_13);
  and and_66 (r138, SEL, pag_2, lin_14);
  and and_67 (r13C, SEL, pag_2, lin_15);
  and and_68 (r140, SEL, pag_2, lin_16);
  and and_69 (r144, SEL, pag_2, lin_17);
  and and_70 (r148, SEL, pag_2, lin_18);
  and and_71 (r14C, SEL, pag_2, lin_19);
  and and_72 (r150, SEL, pag_2, lin_20);
  and and_73 (r154, SEL, pag_2, lin_21);
  and and_74 (r158, SEL, pag_2, lin_22);
  and and_75 (r15C, SEL, pag_2, lin_23);
  and and_76 (r160, SEL, pag_2, lin_24);
  and and_77 (r164, SEL, pag_2, lin_25);
  and and_78 (r168, SEL, pag_2, lin_26);
  and and_79 (r16C, SEL, pag_2, lin_27);
  and and_80 (r170, SEL, pag_2, lin_28);
  and and_81 (r174, SEL, pag_2, lin_29);
  and and_82 (r178, SEL, pag_2, lin_30);
  and and_83 (r17C, SEL, pag_2, lin_31);
  and and_84 (r180, SEL, pag_3, lin_0);
  and and_85 (r184, SEL, pag_3, lin_1);
  and and_86 (r188, SEL, pag_3, lin_2);
  and and_87 (r18C, SEL, pag_3, lin_3);
  and and_88 (r190, SEL, pag_3, lin_4);
  and and_89 (r194, SEL, pag_3, lin_5);
  and and_90 (r0F8, SEL, pag_1, lin_30);
  and and_91 (r0FC, SEL, pag_1, lin_31);
  and and_92 (r110, SEL, pag_2, lin_4);
  assign registros_a_guardar = and297 ^ registros_reset_rw;  // XOR_Gate xor_2, 32 bits wide
  assign and301 = registros_valor & rep300;  // AND_Gate and_93, 32 bits wide
  and and_94 (esc_040, escribe, r040);
  and and_95 (esc_044, escribe, r044);
  and and_96 (esc_04C, escribe, r04C);
  and and_97 (esc_054, escribe, r054);
  and and_98 (esc_058, escribe, r058);
  and and_99 (esc_05C, escribe, r05C);
  and and_100 (esc_068, escribe, r068);
  and and_101 (esc_06C, escribe, r06C);
  and and_102 (esc_074, escribe, r074);
  and and_103 (esc_080, escribe, r080);
  and and_104 (esc_084, escribe, r084);
  and and_105 (esc_088, escribe, r088);
  and and_106 (esc_08C, escribe, r08C);
  and and_107 (esc_094, escribe, r094);
  and and_108 (esc_098, escribe, r098);
  and and_109 (esc_09C, escribe, r09C);
  and and_110 (esc_0C4, escribe, r0C4);
  and and_111 (esc_0C8, escribe, r0C8);
  and and_112 (esc_0CC, escribe, r0CC);
  and and_113 (esc_0D0, escribe, r0D0);
  and and_114 (esc_0D4, escribe, r0D4);
  and and_115 (esc_104, escribe, r104);
  and and_116 (esc_108, escribe, r108);
  and and_117 (esc_10C, escribe, r10C);
  and and_118 (esc_118, escribe, r118);
  and and_119 (esc_11C, escribe, r11C);
  and and_120 (esc_120, escribe, r120);
  and and_121 (esc_124, escribe, r124);
  and and_122 (esc_128, escribe, r128);
  and and_123 (esc_12C, escribe, r12C);
  and and_124 (esc_130, escribe, r130);
  and and_125 (esc_134, escribe, r134);
  and and_126 (esc_138, escribe, r138);
  and and_127 (esc_13C, escribe, r13C);
  and and_128 (esc_140, escribe, r140);
  and and_129 (esc_144, escribe, r144);
  and and_130 (esc_148, escribe, r148);
  and and_131 (esc_14C, escribe, r14C);
  and and_132 (esc_150, escribe, r150);
  and and_133 (esc_154, escribe, r154);
  and and_134 (esc_158, escribe, r158);
  and and_135 (esc_15C, escribe, r15C);
  and and_136 (esc_160, escribe, r160);
  and and_137 (esc_164, escribe, r164);
  assign lineas_cpu = aporte_16_GPIO | aporte_17_GPIO_NMI | aporte_19_SPI2 | aporte_21_UART0 | aporte_22_UART1 | aporte_23_LEDC | aporte_26_USB_SERIAL_JTAG | aporte_27_RTC_CORE | aporte_29_I2C_EXT0 | aporte_32_TG0_T0 | aporte_33_TG0_WDT | aporte_34_TG1_T0 | aporte_35_TG1_WDT | aporte_37_SYSTIMER_T0 | aporte_38_SYSTIMER_T1 | aporte_39_SYSTIMER_T2 | aporte_49_SHA | aporte_50_FROM_CPU0 | aporte_51_FROM_CPU1 | aporte_52_FROM_CPU2 | aporte_53_FROM_CPU3;  // OR_Gate or_2, 32 bits wide
  and and_138 (esc_168, escribe, r168);
  and and_139 (esc_16C, escribe, r16C);
  and and_140 (esc_170, escribe, r170);
  and and_141 (esc_174, escribe, r174);
  and and_142 (esc_178, escribe, r178);
  and and_143 (esc_17C, escribe, r17C);
  and and_144 (esc_180, escribe, r180);
  and and_145 (esc_184, escribe, r184);
  and and_146 (esc_188, escribe, r188);
  and and_147 (esc_18C, escribe, r18C);
  and and_148 (esc_190, escribe, r190);
  and and_149 (esc_194, escribe, r194);
  assign rep302 = {{31{r0F8}}, r0F8};  // Bit_Extender bit_extender_25
  assign rep304 = {{31{r0FC}}, r0FC};  // Bit_Extender bit_extender_26
  assign rep306 = {{31{r104}}, r104};  // Bit_Extender bit_extender_27
  assign rep308 = {{31{r108}}, r108};  // Bit_Extender bit_extender_28
  assign rep310 = {{31{r10C}}, r10C};  // Bit_Extender bit_extender_29
  assign rep312 = {{31{r110}}, r110};  // Bit_Extender bit_extender_30
  assign MAPAS0_mascara[4:0] = {{4{esc_040}}, esc_040};  // Bit_Extender bit_extender_31
  assign MAPAS0_mascara[9:5] = {{4{esc_044}}, esc_044};  // Bit_Extender bit_extender_32
  assign MAPAS0_mascara[14:10] = {{4{esc_04C}}, esc_04C};  // Bit_Extender bit_extender_33
  assign MAPAS0_mascara[19:15] = {{4{esc_054}}, esc_054};  // Bit_Extender bit_extender_34
  assign MAPAS0_mascara[24:20] = {{4{esc_058}}, esc_058};  // Bit_Extender bit_extender_35
  assign MAPAS0_mascara[29:25] = {{4{esc_05C}}, esc_05C};  // Bit_Extender bit_extender_36
  or or_3 (MAPAS0_escribe, esc_040, esc_044, esc_04C, esc_054, esc_058, esc_05C);
  assign MAPAS1_mascara[4:0] = {{4{esc_068}}, esc_068};  // Bit_Extender bit_extender_37
  assign MAPAS1_mascara[9:5] = {{4{esc_06C}}, esc_06C};  // Bit_Extender bit_extender_38
  assign MAPAS1_mascara[14:10] = {{4{esc_074}}, esc_074};  // Bit_Extender bit_extender_39
  assign MAPAS1_mascara[19:15] = {{4{esc_080}}, esc_080};  // Bit_Extender bit_extender_40
  assign MAPAS1_mascara[24:20] = {{4{esc_084}}, esc_084};  // Bit_Extender bit_extender_41
  assign MAPAS1_mascara[29:25] = {{4{esc_088}}, esc_088};  // Bit_Extender bit_extender_42
  or or_4 (MAPAS1_escribe, esc_068, esc_06C, esc_074, esc_080, esc_084, esc_088);
  assign MAPAS2_mascara[4:0] = {{4{esc_08C}}, esc_08C};  // Bit_Extender bit_extender_43
  assign MAPAS2_mascara[9:5] = {{4{esc_094}}, esc_094};  // Bit_Extender bit_extender_44
  assign MAPAS2_mascara[14:10] = {{4{esc_098}}, esc_098};  // Bit_Extender bit_extender_45
  assign MAPAS2_mascara[19:15] = {{4{esc_09C}}, esc_09C};  // Bit_Extender bit_extender_46
  assign MAPAS2_mascara[24:20] = {{4{esc_0C4}}, esc_0C4};  // Bit_Extender bit_extender_47
  assign MAPAS2_mascara[29:25] = {{4{esc_0C8}}, esc_0C8};  // Bit_Extender bit_extender_48
  or or_5 (MAPAS2_escribe, esc_08C, esc_094, esc_098, esc_09C, esc_0C4, esc_0C8);
  assign MAPAS3_mascara[4:0] = {{4{esc_0CC}}, esc_0CC};  // Bit_Extender bit_extender_49
  assign MAPAS3_mascara[9:5] = {{4{esc_0D0}}, esc_0D0};  // Bit_Extender bit_extender_50
  assign MAPAS3_mascara[14:10] = {{4{esc_0D4}}, esc_0D4};  // Bit_Extender bit_extender_51
  or or_6 (MAPAS3_escribe, esc_0CC, esc_0D0, esc_0D4);
  assign PRIORIDADES0_mascara[3:0] = {{3{esc_118}}, esc_118};  // Bit_Extender bit_extender_52
  assign PRIORIDADES0_mascara[7:4] = {{3{esc_11C}}, esc_11C};  // Bit_Extender bit_extender_53
  assign PRIORIDADES0_mascara[11:8] = {{3{esc_120}}, esc_120};  // Bit_Extender bit_extender_54
  assign PRIORIDADES0_mascara[15:12] = {{3{esc_124}}, esc_124};  // Bit_Extender bit_extender_55
  assign PRIORIDADES0_mascara[19:16] = {{3{esc_128}}, esc_128};  // Bit_Extender bit_extender_56
  assign PRIORIDADES0_mascara[23:20] = {{3{esc_12C}}, esc_12C};  // Bit_Extender bit_extender_57
  assign PRIORIDADES0_mascara[27:24] = {{3{esc_130}}, esc_130};  // Bit_Extender bit_extender_58
  assign PRIORIDADES0_mascara[31:28] = {{3{esc_134}}, esc_134};  // Bit_Extender bit_extender_59
  or or_7 (PRIORIDADES0_escribe, esc_118, esc_11C, esc_120, esc_124, esc_128, esc_12C, esc_130, esc_134);
  assign PRIORIDADES1_mascara[3:0] = {{3{esc_138}}, esc_138};  // Bit_Extender bit_extender_60
  assign PRIORIDADES1_mascara[7:4] = {{3{esc_13C}}, esc_13C};  // Bit_Extender bit_extender_61
  assign PRIORIDADES1_mascara[11:8] = {{3{esc_140}}, esc_140};  // Bit_Extender bit_extender_62
  assign PRIORIDADES1_mascara[15:12] = {{3{esc_144}}, esc_144};  // Bit_Extender bit_extender_63
  assign flancos = lineas_cpu & not56;  // AND_Gate and_150, 32 bits wide
  assign and62 = not61 & lineas_cpu;  // AND_Gate and_151, 32 bits wide
  assign PRIORIDADES1_mascara[19:16] = {{3{esc_148}}, esc_148};  // Bit_Extender bit_extender_64
  assign PRIORIDADES1_mascara[23:20] = {{3{esc_14C}}, esc_14C};  // Bit_Extender bit_extender_65
  assign PRIORIDADES1_mascara[27:24] = {{3{esc_150}}, esc_150};  // Bit_Extender bit_extender_66
  assign PRIORIDADES1_mascara[31:28] = {{3{esc_154}}, esc_154};  // Bit_Extender bit_extender_67
  or or_8 (PRIORIDADES1_escribe, esc_138, esc_13C, esc_140, esc_144, esc_148, esc_14C, esc_150, esc_154);
  assign PRIORIDADES2_mascara[3:0] = {{3{esc_158}}, esc_158};  // Bit_Extender bit_extender_68
  assign PRIORIDADES2_mascara[7:4] = {{3{esc_15C}}, esc_15C};  // Bit_Extender bit_extender_69
  assign PRIORIDADES2_mascara[11:8] = {{3{esc_160}}, esc_160};  // Bit_Extender bit_extender_70
  assign PRIORIDADES2_mascara[15:12] = {{3{esc_164}}, esc_164};  // Bit_Extender bit_extender_71
  assign PRIORIDADES2_mascara[19:16] = {{3{esc_168}}, esc_168};  // Bit_Extender bit_extender_72
  assign PRIORIDADES2_mascara[23:20] = {{3{esc_16C}}, esc_16C};  // Bit_Extender bit_extender_73
  assign PRIORIDADES2_mascara[27:24] = {{3{esc_170}}, esc_170};  // Bit_Extender bit_extender_74
  assign PRIORIDADES2_mascara[31:28] = {{3{esc_174}}, esc_174};  // Bit_Extender bit_extender_75
  or or_9 (PRIORIDADES2_escribe, esc_158, esc_15C, esc_160, esc_164, esc_168, esc_16C, esc_170, esc_174);
  assign PRIORIDADES3_mascara[3:0] = {{3{esc_178}}, esc_178};  // Bit_Extender bit_extender_76
  assign PRIORIDADES3_mascara[7:4] = {{3{esc_17C}}, esc_17C};  // Bit_Extender bit_extender_77
  assign PRIORIDADES3_mascara[11:8] = {{3{esc_180}}, esc_180};  // Bit_Extender bit_extender_78
  assign PRIORIDADES3_mascara[15:12] = {{3{esc_184}}, esc_184};  // Bit_Extender bit_extender_79
  assign PRIORIDADES3_mascara[19:16] = {{3{esc_188}}, esc_188};  // Bit_Extender bit_extender_80
  assign PRIORIDADES3_mascara[23:20] = {{3{esc_18C}}, esc_18C};  // Bit_Extender bit_extender_81
  assign PRIORIDADES3_mascara[27:24] = {{3{esc_190}}, esc_190};  // Bit_Extender bit_extender_82
  assign PRIORIDADES3_mascara[31:28] = {{3{esc_194}}, esc_194};  // Bit_Extender bit_extender_83
  or or_10 (PRIORIDADES3_escribe, esc_178, esc_17C, esc_180, esc_184, esc_188, esc_18C, esc_190, esc_194);
  assign and303 = {2'b00, INT_I2C_EXT0, 1'b0, INT_RTC_CORE, INT_USB_SERIAL_JTAG, 2'b00, INT_LEDC, INT_UART1, INT_UART0, 1'b0, INT_SPI2, 1'b0, INT_GPIO_NMI, INT_GPIO, {16{1'b0}}} & rep302;  // AND_Gate and_152, 32 bits wide
  assign and305 = and55 & rep304;  // AND_Gate and_153, 32 bits wide
  assign and309 = CPU_INT_TYPE & rep308;  // AND_Gate and_154, 32 bits wide
  assign and307 = CPU_INT_ENABLE & rep306;  // AND_Gate and_155, 32 bits wide
  assign and311 = CPU_INT_CLEAR & rep310;  // AND_Gate and_156, 32 bits wide
  assign or57 = pend_flanco | flancos;  // OR_Gate or_11, 32 bits wide
  assign pendientes = and60 | and62;  // OR_Gate or_12, 32 bits wide
  assign not7 = ~MAPAS0_mascara;  // NOT_Gate not_52, 30 bits wide
  assign not16 = ~MAPAS1_mascara;  // NOT_Gate not_53, 30 bits wide
  assign not25 = ~MAPAS2_mascara;  // NOT_Gate not_54, 30 bits wide
  assign not31 = ~MAPAS3_mascara;  // NOT_Gate not_55, 15 bits wide
  assign and59 = or57 & not58;  // AND_Gate and_157, 32 bits wide
  assign and313 = pendientes & rep312;  // AND_Gate and_158, 32 bits wide
  assign and9 = {dato_escrito[4:0], dato_escrito[4:0], dato_escrito[4:0], dato_escrito[4:0], dato_escrito[4:0], dato_escrito[4:0]} & MAPAS0_mascara;  // AND_Gate and_159, 30 bits wide
  assign and18 = {dato_escrito[4:0], dato_escrito[4:0], dato_escrito[4:0], dato_escrito[4:0], dato_escrito[4:0], dato_escrito[4:0]} & MAPAS1_mascara;  // AND_Gate and_160, 30 bits wide
  assign and27 = {dato_escrito[4:0], dato_escrito[4:0], dato_escrito[4:0], dato_escrito[4:0], dato_escrito[4:0], dato_escrito[4:0]} & MAPAS2_mascara;  // AND_Gate and_161, 30 bits wide
  assign and33 = {dato_escrito[4:0], dato_escrito[4:0], dato_escrito[4:0]} & MAPAS3_mascara;  // AND_Gate and_162, 15 bits wide
  assign not71 = ~PRIORIDADES0_mascara;  // NOT_Gate not_56, 32 bits wide
  assign and73 = {dato_escrito[3:0], dato_escrito[3:0], dato_escrito[3:0], dato_escrito[3:0], dato_escrito[3:0], dato_escrito[3:0], dato_escrito[3:0], dato_escrito[3:0]} & PRIORIDADES0_mascara;  // AND_Gate and_163, 32 bits wide
  assign not82 = ~PRIORIDADES1_mascara;  // NOT_Gate not_57, 32 bits wide
  assign and84 = {dato_escrito[3:0], dato_escrito[3:0], dato_escrito[3:0], dato_escrito[3:0], dato_escrito[3:0], dato_escrito[3:0], dato_escrito[3:0], dato_escrito[3:0]} & PRIORIDADES1_mascara;  // AND_Gate and_164, 32 bits wide
  assign not93 = ~PRIORIDADES2_mascara;  // NOT_Gate not_58, 32 bits wide
  assign and95 = {dato_escrito[3:0], dato_escrito[3:0], dato_escrito[3:0], dato_escrito[3:0], dato_escrito[3:0], dato_escrito[3:0], dato_escrito[3:0], dato_escrito[3:0]} & PRIORIDADES2_mascara;  // AND_Gate and_165, 32 bits wide
  assign not104 = ~PRIORIDADES3_mascara;  // NOT_Gate not_59, 32 bits wide
  assign and106 = {dato_escrito[3:0], dato_escrito[3:0], dato_escrito[3:0], dato_escrito[3:0], dato_escrito[3:0], dato_escrito[3:0], dato_escrito[3:0], dato_escrito[3:0]} & PRIORIDADES3_mascara;  // AND_Gate and_166, 32 bits wide
  assign IRQ_LINEAS = pendientes & CPU_INT_ENABLE;  // AND_Gate and_167, 32 bits wide
  assign and8 = MAPAS0 & not7;  // AND_Gate and_168, 30 bits wide
  assign and17 = MAPAS1 & not16;  // AND_Gate and_169, 30 bits wide
  assign and26 = MAPAS2 & not25;  // AND_Gate and_170, 30 bits wide
  assign and32 = MAPAS3 & not31;  // AND_Gate and_171, 15 bits wide
  assign and72 = PRIORIDADES0 & not71;  // AND_Gate and_172, 32 bits wide
  assign and83 = PRIORIDADES1 & not82;  // AND_Gate and_173, 32 bits wide
  assign and94 = PRIORIDADES2 & not93;  // AND_Gate and_174, 32 bits wide
  assign and105 = PRIORIDADES3 & not104;  // AND_Gate and_175, 32 bits wide
  assign RD = and303 | and305 | and307 | and309 | and311 | and313 | and301;  // OR_Gate or_13, 32 bits wide
  assign MAPAS0_sig = and8 | and9;  // OR_Gate or_14, 30 bits wide
  assign MAPAS1_sig = and17 | and18;  // OR_Gate or_15, 30 bits wide
  assign MAPAS2_sig = and26 | and27;  // OR_Gate or_16, 30 bits wide
  assign MAPAS3_sig = and32 | and33;  // OR_Gate or_17, 15 bits wide
  assign PRIORIDADES0_sig = and72 | and73;  // OR_Gate or_18, 32 bits wide
  assign PRIORIDADES1_sig = and83 | and84;  // OR_Gate or_19, 32 bits wide
  assign PRIORIDADES2_sig = and94 | and95;  // OR_Gate or_20, 32 bits wide
  assign PRIORIDADES3_sig = and105 | and106;  // OR_Gate or_21, 32 bits wide
  and and_176 (pide1, IRQ_LINEAS[1], not108);
  and and_177 (pide2, IRQ_LINEAS[2], not110);
  and and_178 (pide3, IRQ_LINEAS[3], not112);
  and and_179 (pide4, IRQ_LINEAS[4], not114);
  and and_180 (pide5, IRQ_LINEAS[5], not116);
  and and_181 (pide6, IRQ_LINEAS[6], not118);
  and and_182 (pide7, IRQ_LINEAS[7], not120);
  and and_183 (pide8, IRQ_LINEAS[8], not122);
  and and_184 (pide9, IRQ_LINEAS[9], not124);
  and and_185 (pide10, IRQ_LINEAS[10], not126);
  and and_186 (pide11, IRQ_LINEAS[11], not128);
  and and_187 (pide12, IRQ_LINEAS[12], not130);
  and and_188 (pide13, IRQ_LINEAS[13], not132);
  and and_189 (pide14, IRQ_LINEAS[14], not134);
  and and_190 (pide15, IRQ_LINEAS[15], not136);
  and and_191 (pide16, IRQ_LINEAS[16], not138);
  and and_192 (pide17, IRQ_LINEAS[17], not140);
  and and_193 (pide18, IRQ_LINEAS[18], not142);
  and and_194 (pide19, IRQ_LINEAS[19], not144);
  and and_195 (pide20, IRQ_LINEAS[20], not146);
  and and_196 (pide21, IRQ_LINEAS[21], not148);
  and and_197 (pide22, IRQ_LINEAS[22], not150);
  and and_198 (pide23, IRQ_LINEAS[23], not152);
  and and_199 (pide24, IRQ_LINEAS[24], not154);
  and and_200 (pide25, IRQ_LINEAS[25], not156);
  and and_201 (pide26, IRQ_LINEAS[26], not158);
  and and_202 (pide27, IRQ_LINEAS[27], not160);
  and and_203 (pide28, IRQ_LINEAS[28], not162);
  and and_204 (pide29, IRQ_LINEAS[29], not164);
  and and_205 (pide30, IRQ_LINEAS[30], not166);
  and and_206 (pide31, IRQ_LINEAS[31], not168);
  not not_60 (not169, pide1);
  or or_22 (v_0_0, 1'b0, pide1);
  not not_61 (not173, pide3);
  or or_23 (v_0_1, pide2, pide3);
  not not_62 (not177, pide5);
  or or_24 (v_0_2, pide4, pide5);
  not not_63 (not181, pide7);
  or or_25 (v_0_3, pide6, pide7);
  not not_64 (not185, pide9);
  or or_26 (v_0_4, pide8, pide9);
  not not_65 (not189, pide11);
  or or_27 (v_0_5, pide10, pide11);
  not not_66 (not193, pide13);
  or or_28 (v_0_6, pide12, pide13);
  not not_67 (not197, pide15);
  or or_29 (v_0_7, pide14, pide15);
  not not_68 (not201, pide17);
  or or_30 (v_0_8, pide16, pide17);
  not not_69 (not205, pide19);
  or or_31 (v_0_9, pide18, pide19);
  not not_70 (not209, pide21);
  or or_32 (v_0_10, pide20, pide21);
  not not_71 (not213, pide23);
  or or_33 (v_0_11, pide22, pide23);
  not not_72 (not217, pide25);
  or or_34 (v_0_12, pide24, pide25);
  not not_73 (not221, pide27);
  or or_35 (v_0_13, pide26, pide27);
  not not_74 (not225, pide29);
  or or_36 (v_0_14, pide28, pide29);
  not not_75 (not229, pide31);
  or or_37 (v_0_15, pide30, pide31);
  or or_38 (or172, not169, not171);
  or or_39 (or176, not173, not175);
  or or_40 (or180, not177, not179);
  or or_41 (or184, not181, not183);
  or or_42 (or188, not185, not187);
  or or_43 (or192, not189, not191);
  or or_44 (or196, not193, not195);
  or or_45 (or200, not197, not199);
  or or_46 (or204, not201, not203);
  or or_47 (or208, not205, not207);
  or or_48 (or212, not209, not211);
  or or_49 (or216, not213, not215);
  or or_50 (or220, not217, not219);
  or or_51 (or224, not221, not223);
  or or_52 (or228, not225, not227);
  or or_53 (or232, not229, not231);
  not not_76 (not233, v_0_1);
  or or_54 (v_1_0, v_0_0, v_0_1);
  not not_77 (not237, v_0_3);
  or or_55 (v_1_1, v_0_2, v_0_3);
  not not_78 (not241, v_0_5);
  or or_56 (v_1_2, v_0_4, v_0_5);
  not not_79 (not245, v_0_7);
  or or_57 (v_1_3, v_0_6, v_0_7);
  not not_80 (not249, v_0_9);
  or or_58 (v_1_4, v_0_8, v_0_9);
  not not_81 (not253, v_0_11);
  or or_59 (v_1_5, v_0_10, v_0_11);
  not not_82 (not257, v_0_13);
  or or_60 (v_1_6, v_0_12, v_0_13);
  not not_83 (not261, v_0_15);
  or or_61 (v_1_7, v_0_14, v_0_15);
  and and_207 (gana_A_0_0, 1'b0, or172);
  and and_208 (gana_A_0_1, pide2, or176);
  and and_209 (gana_A_0_2, pide4, or180);
  and and_210 (gana_A_0_3, pide6, or184);
  and and_211 (gana_A_0_4, pide8, or188);
  and and_212 (gana_A_0_5, pide10, or192);
  and and_213 (gana_A_0_6, pide12, or196);
  and and_214 (gana_A_0_7, pide14, or200);
  and and_215 (gana_A_0_8, pide16, or204);
  and and_216 (gana_A_0_9, pide18, or208);
  and and_217 (gana_A_0_10, pide20, or212);
  and and_218 (gana_A_0_11, pide22, or216);
  and and_219 (gana_A_0_12, pide24, or220);
  and and_220 (gana_A_0_13, pide26, or224);
  and and_221 (gana_A_0_14, pide28, or228);
  and and_222 (gana_A_0_15, pide30, or232);
  not not_84 (not265, v_1_1);
  or or_62 (v_2_0, v_1_0, v_1_1);
  not not_85 (not269, v_1_3);
  or or_63 (v_2_1, v_1_2, v_1_3);
  not not_86 (not273, v_1_5);
  or or_64 (v_2_2, v_1_4, v_1_5);
  not not_87 (not277, v_1_7);
  or or_65 (v_2_3, v_1_6, v_1_7);
  Multiplexer #(.select(1), .width(5), .enable("false")) multiplexer_1 (
    .in0(5'b00001), .in1({5{1'b0}}), .out(i_0_0), .sel(gana_A_0_0));
  Multiplexer #(.select(1), .width(5), .enable("false")) multiplexer_2 (
    .in0(5'b00011), .in1(5'b00010), .out(i_0_1), .sel(gana_A_0_1));
  Multiplexer #(.select(1), .width(5), .enable("false")) multiplexer_3 (
    .in0(5'b00101), .in1(5'b00100), .out(i_0_2), .sel(gana_A_0_2));
  Multiplexer #(.select(1), .width(5), .enable("false")) multiplexer_4 (
    .in0(5'b00111), .in1(5'b00110), .out(i_0_3), .sel(gana_A_0_3));
  Multiplexer #(.select(1), .width(5), .enable("false")) multiplexer_5 (
    .in0(5'b01001), .in1(5'b01000), .out(i_0_4), .sel(gana_A_0_4));
  Multiplexer #(.select(1), .width(5), .enable("false")) multiplexer_6 (
    .in0(5'b01011), .in1(5'b01010), .out(i_0_5), .sel(gana_A_0_5));
  Multiplexer #(.select(1), .width(5), .enable("false")) multiplexer_7 (
    .in0(5'b01101), .in1(5'b01100), .out(i_0_6), .sel(gana_A_0_6));
  Multiplexer #(.select(1), .width(5), .enable("false")) multiplexer_8 (
    .in0(5'b01111), .in1(5'b01110), .out(i_0_7), .sel(gana_A_0_7));
  Multiplexer #(.select(1), .width(5), .enable("false")) multiplexer_9 (
    .in0(5'b10001), .in1(5'b10000), .out(i_0_8), .sel(gana_A_0_8));
  Multiplexer #(.select(1), .width(5), .enable("false")) multiplexer_10 (
    .in0(5'b10011), .in1(5'b10010), .out(i_0_9), .sel(gana_A_0_9));
  Multiplexer #(.select(1), .width(5), .enable("false")) multiplexer_11 (
    .in0(5'b10101), .in1(5'b10100), .out(i_0_10), .sel(gana_A_0_10));
  Multiplexer #(.select(1), .width(5), .enable("false")) multiplexer_12 (
    .in0(5'b10111), .in1(5'b10110), .out(i_0_11), .sel(gana_A_0_11));
  Multiplexer #(.select(1), .width(5), .enable("false")) multiplexer_13 (
    .in0(5'b11001), .in1(5'b11000), .out(i_0_12), .sel(gana_A_0_12));
  Multiplexer #(.select(1), .width(4), .enable("false")) multiplexer_14 (
    .in0(PRIORIDADES0[3:0]), .in1(4'b0000), .out(p_0_0), .sel(gana_A_0_0));
  Multiplexer #(.select(1), .width(4), .enable("false")) multiplexer_15 (
    .in0(PRIORIDADES0[11:8]), .in1(PRIORIDADES0[7:4]), .out(p_0_1), .sel(gana_A_0_1));
  Multiplexer #(.select(1), .width(4), .enable("false")) multiplexer_16 (
    .in0(PRIORIDADES0[19:16]), .in1(PRIORIDADES0[15:12]), .out(p_0_2), .sel(gana_A_0_2));
  Multiplexer #(.select(1), .width(4), .enable("false")) multiplexer_17 (
    .in0(PRIORIDADES0[27:24]), .in1(PRIORIDADES0[23:20]), .out(p_0_3), .sel(gana_A_0_3));
  Multiplexer #(.select(1), .width(4), .enable("false")) multiplexer_18 (
    .in0(PRIORIDADES1[3:0]), .in1(PRIORIDADES0[31:28]), .out(p_0_4), .sel(gana_A_0_4));
  Multiplexer #(.select(1), .width(4), .enable("false")) multiplexer_19 (
    .in0(PRIORIDADES1[11:8]), .in1(PRIORIDADES1[7:4]), .out(p_0_5), .sel(gana_A_0_5));
  Multiplexer #(.select(1), .width(4), .enable("false")) multiplexer_20 (
    .in0(PRIORIDADES1[19:16]), .in1(PRIORIDADES1[15:12]), .out(p_0_6), .sel(gana_A_0_6));
  Multiplexer #(.select(1), .width(4), .enable("false")) multiplexer_21 (
    .in0(PRIORIDADES1[27:24]), .in1(PRIORIDADES1[23:20]), .out(p_0_7), .sel(gana_A_0_7));
  Multiplexer #(.select(1), .width(4), .enable("false")) multiplexer_22 (
    .in0(PRIORIDADES2[3:0]), .in1(PRIORIDADES1[31:28]), .out(p_0_8), .sel(gana_A_0_8));
  Multiplexer #(.select(1), .width(4), .enable("false")) multiplexer_23 (
    .in0(PRIORIDADES2[11:8]), .in1(PRIORIDADES2[7:4]), .out(p_0_9), .sel(gana_A_0_9));
  Multiplexer #(.select(1), .width(4), .enable("false")) multiplexer_24 (
    .in0(PRIORIDADES2[19:16]), .in1(PRIORIDADES2[15:12]), .out(p_0_10), .sel(gana_A_0_10));
  Multiplexer #(.select(1), .width(4), .enable("false")) multiplexer_25 (
    .in0(PRIORIDADES2[27:24]), .in1(PRIORIDADES2[23:20]), .out(p_0_11), .sel(gana_A_0_11));
  Multiplexer #(.select(1), .width(4), .enable("false")) multiplexer_26 (
    .in0(PRIORIDADES3[3:0]), .in1(PRIORIDADES2[31:28]), .out(p_0_12), .sel(gana_A_0_12));
  Multiplexer #(.select(1), .width(5), .enable("false")) multiplexer_27 (
    .in0(5'b11011), .in1(5'b11010), .out(i_0_13), .sel(gana_A_0_13));
  Multiplexer #(.select(1), .width(5), .enable("false")) multiplexer_28 (
    .in0(5'b11101), .in1(5'b11100), .out(i_0_14), .sel(gana_A_0_14));
  Multiplexer #(.select(1), .width(5), .enable("false")) multiplexer_29 (
    .in0({5{1'b1}}), .in1(5'b11110), .out(i_0_15), .sel(gana_A_0_15));
  not not_88 (not281, v_2_1);
  not not_89 (not285, v_2_3);
  Multiplexer #(.select(1), .width(4), .enable("false")) multiplexer_30 (
    .in0(PRIORIDADES3[11:8]), .in1(PRIORIDADES3[7:4]), .out(p_0_13), .sel(gana_A_0_13));
  or or_66 (v_3_0, v_2_0, v_2_1);
  or or_67 (v_3_1, v_2_2, v_2_3);
  Multiplexer #(.select(1), .width(4), .enable("false")) multiplexer_31 (
    .in0(PRIORIDADES3[19:16]), .in1(PRIORIDADES3[15:12]), .out(p_0_14), .sel(gana_A_0_14));
  Multiplexer #(.select(1), .width(4), .enable("false")) multiplexer_32 (
    .in0(PRIORIDADES3[27:24]), .in1(PRIORIDADES3[23:20]), .out(p_0_15), .sel(gana_A_0_15));
  Comparator #(.width(4), .mode("unsigned")) comparator_48 (.a(p_0_0), .b(p_0_1), .lt(lt234));  // open: gt, eq
  Comparator #(.width(4), .mode("unsigned")) comparator_49 (.a(p_0_2), .b(p_0_3), .lt(lt238));  // open: gt, eq
  Comparator #(.width(4), .mode("unsigned")) comparator_50 (.a(p_0_4), .b(p_0_5), .lt(lt242));  // open: gt, eq
  Comparator #(.width(4), .mode("unsigned")) comparator_51 (.a(p_0_6), .b(p_0_7), .lt(lt246));  // open: gt, eq
  Comparator #(.width(4), .mode("unsigned")) comparator_52 (.a(p_0_8), .b(p_0_9), .lt(lt250));  // open: gt, eq
  not not_90 (not289, v_3_1);
  or or_68 (IRQ, v_3_0, v_3_1);
  Comparator #(.width(4), .mode("unsigned")) comparator_53 (.a(p_0_10), .b(p_0_11), .lt(lt254));  // open: gt, eq
  Comparator #(.width(4), .mode("unsigned")) comparator_54 (.a(p_0_12), .b(p_0_13), .lt(lt258));  // open: gt, eq
  Comparator #(.width(4), .mode("unsigned")) comparator_55 (.a(p_0_14), .b(p_0_15), .lt(lt262));  // open: gt, eq
  not not_91 (not235, lt234);
  not not_92 (not239, lt238);
  not not_93 (not243, lt242);
  not not_94 (not247, lt246);
  not not_95 (not251, lt250);
  not not_96 (not255, lt254);
  not not_97 (not259, lt258);
  not not_98 (not263, lt262);
  or or_69 (or236, not233, not235);
  or or_70 (or240, not237, not239);
  or or_71 (or244, not241, not243);
  or or_72 (or248, not245, not247);
  or or_73 (or252, not249, not251);
  or or_74 (or256, not253, not255);
  or or_75 (or260, not257, not259);
  or or_76 (or264, not261, not263);
  and and_223 (gana_A_1_0, v_0_0, or236);
  and and_224 (gana_A_1_1, v_0_2, or240);
  and and_225 (gana_A_1_2, v_0_4, or244);
  and and_226 (gana_A_1_3, v_0_6, or248);
  and and_227 (gana_A_1_4, v_0_8, or252);
  and and_228 (gana_A_1_5, v_0_10, or256);
  and and_229 (gana_A_1_6, v_0_12, or260);
  and and_230 (gana_A_1_7, v_0_14, or264);
  Multiplexer #(.select(1), .width(4), .enable("false")) multiplexer_33 (
    .in0(p_0_1), .in1(p_0_0), .out(p_1_0), .sel(gana_A_1_0));
  Multiplexer #(.select(1), .width(5), .enable("false")) multiplexer_34 (
    .in0(i_0_1), .in1(i_0_0), .out(i_1_0), .sel(gana_A_1_0));
  Multiplexer #(.select(1), .width(4), .enable("false")) multiplexer_35 (
    .in0(p_0_3), .in1(p_0_2), .out(p_1_1), .sel(gana_A_1_1));
  Multiplexer #(.select(1), .width(5), .enable("false")) multiplexer_36 (
    .in0(i_0_3), .in1(i_0_2), .out(i_1_1), .sel(gana_A_1_1));
  Multiplexer #(.select(1), .width(4), .enable("false")) multiplexer_37 (
    .in0(p_0_5), .in1(p_0_4), .out(p_1_2), .sel(gana_A_1_2));
  Multiplexer #(.select(1), .width(5), .enable("false")) multiplexer_38 (
    .in0(i_0_5), .in1(i_0_4), .out(i_1_2), .sel(gana_A_1_2));
  Multiplexer #(.select(1), .width(4), .enable("false")) multiplexer_39 (
    .in0(p_0_7), .in1(p_0_6), .out(p_1_3), .sel(gana_A_1_3));
  Multiplexer #(.select(1), .width(5), .enable("false")) multiplexer_40 (
    .in0(i_0_7), .in1(i_0_6), .out(i_1_3), .sel(gana_A_1_3));
  Multiplexer #(.select(1), .width(4), .enable("false")) multiplexer_41 (
    .in0(p_0_9), .in1(p_0_8), .out(p_1_4), .sel(gana_A_1_4));
  Multiplexer #(.select(1), .width(5), .enable("false")) multiplexer_42 (
    .in0(i_0_9), .in1(i_0_8), .out(i_1_4), .sel(gana_A_1_4));
  Multiplexer #(.select(1), .width(4), .enable("false")) multiplexer_43 (
    .in0(p_0_11), .in1(p_0_10), .out(p_1_5), .sel(gana_A_1_5));
  Multiplexer #(.select(1), .width(5), .enable("false")) multiplexer_44 (
    .in0(i_0_11), .in1(i_0_10), .out(i_1_5), .sel(gana_A_1_5));
  Multiplexer #(.select(1), .width(4), .enable("false")) multiplexer_45 (
    .in0(p_0_13), .in1(p_0_12), .out(p_1_6), .sel(gana_A_1_6));
  Multiplexer #(.select(1), .width(5), .enable("false")) multiplexer_46 (
    .in0(i_0_13), .in1(i_0_12), .out(i_1_6), .sel(gana_A_1_6));
  Multiplexer #(.select(1), .width(4), .enable("false")) multiplexer_47 (
    .in0(p_0_15), .in1(p_0_14), .out(p_1_7), .sel(gana_A_1_7));
  Multiplexer #(.select(1), .width(5), .enable("false")) multiplexer_48 (
    .in0(i_0_15), .in1(i_0_14), .out(i_1_7), .sel(gana_A_1_7));
  Comparator #(.width(4), .mode("unsigned")) comparator_56 (.a(p_1_0), .b(p_1_1), .lt(lt266));  // open: gt, eq
  Comparator #(.width(4), .mode("unsigned")) comparator_57 (.a(p_1_2), .b(p_1_3), .lt(lt270));  // open: gt, eq
  Comparator #(.width(4), .mode("unsigned")) comparator_58 (.a(p_1_4), .b(p_1_5), .lt(lt274));  // open: gt, eq
  Comparator #(.width(4), .mode("unsigned")) comparator_59 (.a(p_1_6), .b(p_1_7), .lt(lt278));  // open: gt, eq
  not not_99 (not267, lt266);
  not not_100 (not271, lt270);
  not not_101 (not275, lt274);
  not not_102 (not279, lt278);
  or or_77 (or268, not265, not267);
  or or_78 (or272, not269, not271);
  or or_79 (or276, not273, not275);
  or or_80 (or280, not277, not279);
  and and_231 (gana_A_2_0, v_1_0, or268);
  and and_232 (gana_A_2_1, v_1_2, or272);
  and and_233 (gana_A_2_2, v_1_4, or276);
  and and_234 (gana_A_2_3, v_1_6, or280);
  Multiplexer #(.select(1), .width(4), .enable("false")) multiplexer_49 (
    .in0(p_1_1), .in1(p_1_0), .out(p_2_0), .sel(gana_A_2_0));
  Multiplexer #(.select(1), .width(5), .enable("false")) multiplexer_50 (
    .in0(i_1_1), .in1(i_1_0), .out(i_2_0), .sel(gana_A_2_0));
  Multiplexer #(.select(1), .width(4), .enable("false")) multiplexer_51 (
    .in0(p_1_3), .in1(p_1_2), .out(p_2_1), .sel(gana_A_2_1));
  Multiplexer #(.select(1), .width(5), .enable("false")) multiplexer_52 (
    .in0(i_1_3), .in1(i_1_2), .out(i_2_1), .sel(gana_A_2_1));
  Multiplexer #(.select(1), .width(4), .enable("false")) multiplexer_53 (
    .in0(p_1_5), .in1(p_1_4), .out(p_2_2), .sel(gana_A_2_2));
  Multiplexer #(.select(1), .width(5), .enable("false")) multiplexer_54 (
    .in0(i_1_5), .in1(i_1_4), .out(i_2_2), .sel(gana_A_2_2));
  Multiplexer #(.select(1), .width(4), .enable("false")) multiplexer_55 (
    .in0(p_1_7), .in1(p_1_6), .out(p_2_3), .sel(gana_A_2_3));
  Multiplexer #(.select(1), .width(5), .enable("false")) multiplexer_56 (
    .in0(i_1_7), .in1(i_1_6), .out(i_2_3), .sel(gana_A_2_3));
  Comparator #(.width(4), .mode("unsigned")) comparator_60 (.a(p_2_0), .b(p_2_1), .lt(lt282));  // open: gt, eq
  Comparator #(.width(4), .mode("unsigned")) comparator_61 (.a(p_2_2), .b(p_2_3), .lt(lt286));  // open: gt, eq
  not not_103 (not283, lt282);
  not not_104 (not287, lt286);
  or or_81 (or284, not281, not283);
  or or_82 (or288, not285, not287);
  and and_235 (gana_A_3_0, v_2_0, or284);
  and and_236 (gana_A_3_1, v_2_2, or288);
  Multiplexer #(.select(1), .width(4), .enable("false")) multiplexer_57 (
    .in0(p_2_1), .in1(p_2_0), .out(p_3_0), .sel(gana_A_3_0));
  Multiplexer #(.select(1), .width(5), .enable("false")) multiplexer_58 (
    .in0(i_2_1), .in1(i_2_0), .out(i_3_0), .sel(gana_A_3_0));
  Multiplexer #(.select(1), .width(4), .enable("false")) multiplexer_59 (
    .in0(p_2_3), .in1(p_2_2), .out(p_3_1), .sel(gana_A_3_1));
  Multiplexer #(.select(1), .width(5), .enable("false")) multiplexer_60 (
    .in0(i_2_3), .in1(i_2_2), .out(i_3_1), .sel(gana_A_3_1));
  Comparator #(.width(4), .mode("unsigned")) comparator_62 (.a(p_3_0), .b(p_3_1), .lt(lt290));  // open: gt, eq
  not not_105 (not291, lt290);
  or or_83 (or292, not289, not291);
  and and_237 (gana_A_4_0, v_3_0, or292);
  Multiplexer #(.select(1), .width(4), .enable("false")) multiplexer_61 (
    .in0(p_3_1), .in1(p_3_0), .out(p_4_0), .sel(gana_A_4_0));
  Multiplexer #(.select(1), .width(5), .enable("false")) multiplexer_62 (
    .in0(i_3_1), .in1(i_3_0), .out(IRQ_ID), .sel(gana_A_4_0));

  // Other names for the same wires on the sheet: dir_registro_4_0[4:0] = dir_registro[4:0];
  //   dir_registro_9_5[4:0] = dir_registro[9:5];
  //   fuentes_0_31 (some bits) = {INT_I2C_EXT0, INT_RTC_CORE, INT_USB_SERIAL_JTAG, INT_LEDC, INT_UART1, INT_UART0, INT_SPI2, INT_GPIO_NMI, INT_GPIO};
  //   fuentes_0_31_16 = INT_GPIO; fuentes_0_31_17 = INT_GPIO_NMI; fuentes_0_31_19 = INT_SPI2;
  //   fuentes_0_31_21 = INT_UART0; fuentes_0_31_22 = INT_UART1; fuentes_0_31_23 = INT_LEDC;
  //   fuentes_0_31_26 = INT_USB_SERIAL_JTAG; fuentes_0_31_27 = INT_RTC_CORE; fuentes_0_31_29 = INT_I2C_EXT0;
  //   fuentes_32_63 (some bits) = {INT_FROM_CPU3, INT_FROM_CPU2, INT_FROM_CPU1, INT_FROM_CPU0, INT_SHA, INT_SYSTIMER_T2, INT_SYSTIMER_T1, INT_SYSTIMER_T0, INT_TG1_WDT, INT_TG1_T0, INT_TG0_WDT, INT_TG0_T0};
  //   fuentes_32_63_0 = INT_TG0_T0; fuentes_32_63_1 = INT_TG0_WDT; fuentes_32_63_2 = INT_TG1_T0;
  //   fuentes_32_63_3 = INT_TG1_WDT; fuentes_32_63_5 = INT_SYSTIMER_T0; fuentes_32_63_6 = INT_SYSTIMER_T1;
  //   fuentes_32_63_7 = INT_SYSTIMER_T2; fuentes_32_63_17 = INT_SHA; fuentes_32_63_18 = INT_FROM_CPU0;
  //   fuentes_32_63_19 = INT_FROM_CPU1; fuentes_32_63_20 = INT_FROM_CPU2; fuentes_32_63_21 = INT_FROM_CPU3;
  //   v_4_0 = IRQ; i_4_0[4:0] = IRQ_ID; activas[31:0] = IRQ_LINEAS; activas_1 = IRQ_LINEAS[1];
  //   activas_2 = IRQ_LINEAS[2]; activas_3 = IRQ_LINEAS[3]; activas_4 = IRQ_LINEAS[4]; activas_5 = IRQ_LINEAS[5];
  //   activas_6 = IRQ_LINEAS[6]; activas_7 = IRQ_LINEAS[7]; activas_8 = IRQ_LINEAS[8]; activas_9 = IRQ_LINEAS[9];
  //   activas_10 = IRQ_LINEAS[10]; activas_11 = IRQ_LINEAS[11]; activas_12 = IRQ_LINEAS[12];
  //   activas_13 = IRQ_LINEAS[13]; activas_14 = IRQ_LINEAS[14]; activas_15 = IRQ_LINEAS[15];
  //   activas_16 = IRQ_LINEAS[16]; activas_17 = IRQ_LINEAS[17]; activas_18 = IRQ_LINEAS[18];
  //   activas_19 = IRQ_LINEAS[19]; activas_20 = IRQ_LINEAS[20]; activas_21 = IRQ_LINEAS[21];
  //   activas_22 = IRQ_LINEAS[22]; activas_23 = IRQ_LINEAS[23]; activas_24 = IRQ_LINEAS[24];
  //   activas_25 = IRQ_LINEAS[25]; activas_26 = IRQ_LINEAS[26]; activas_27 = IRQ_LINEAS[27];
  //   activas_28 = IRQ_LINEAS[28]; activas_29 = IRQ_LINEAS[29]; activas_30 = IRQ_LINEAS[30];
  //   activas_31 = IRQ_LINEAS[31]; ruta16_0 = linea_de_16[0]; ruta16_1 = linea_de_16[1]; ruta16_2 = linea_de_16[2];
  //   ruta16_3 = linea_de_16[3]; ruta16_4 = linea_de_16[4]; ruta16_5 = linea_de_16[5]; ruta16_6 = linea_de_16[6];
  //   ruta16_7 = linea_de_16[7]; ruta16_8 = linea_de_16[8]; ruta16_9 = linea_de_16[9]; ruta16_10 = linea_de_16[10];
  //   ruta16_11 = linea_de_16[11]; ruta16_12 = linea_de_16[12]; ruta16_13 = linea_de_16[13];
  //   ruta16_14 = linea_de_16[14]; ruta16_15 = linea_de_16[15]; ruta16_16 = linea_de_16[16];
  //   ruta16_17 = linea_de_16[17]; ruta16_18 = linea_de_16[18]; ruta16_19 = linea_de_16[19];
  //   ruta16_20 = linea_de_16[20]; ruta16_21 = linea_de_16[21]; ruta16_22 = linea_de_16[22];
  //   ruta16_23 = linea_de_16[23]; ruta16_24 = linea_de_16[24]; ruta16_25 = linea_de_16[25];
  //   ruta16_26 = linea_de_16[26]; ruta16_27 = linea_de_16[27]; ruta16_28 = linea_de_16[28];
  //   ruta16_29 = linea_de_16[29]; ruta16_30 = linea_de_16[30]; ruta16_31 = linea_de_16[31];
  //   ruta17_0 = linea_de_17[0]; ruta17_1 = linea_de_17[1]; ruta17_2 = linea_de_17[2]; ruta17_3 = linea_de_17[3];
  //   ruta17_4 = linea_de_17[4]; ruta17_5 = linea_de_17[5]; ruta17_6 = linea_de_17[6]; ruta17_7 = linea_de_17[7];
  //   ruta17_8 = linea_de_17[8]; ruta17_9 = linea_de_17[9]; ruta17_10 = linea_de_17[10]; ruta17_11 = linea_de_17[11];
  //   ruta17_12 = linea_de_17[12]; ruta17_13 = linea_de_17[13]; ruta17_14 = linea_de_17[14];
  //   ruta17_15 = linea_de_17[15]; ruta17_16 = linea_de_17[16]; ruta17_17 = linea_de_17[17];
  //   ruta17_18 = linea_de_17[18]; ruta17_19 = linea_de_17[19]; ruta17_20 = linea_de_17[20];
  //   ruta17_21 = linea_de_17[21]; ruta17_22 = linea_de_17[22]; ruta17_23 = linea_de_17[23];
  //   ruta17_24 = linea_de_17[24]; ruta17_25 = linea_de_17[25]; ruta17_26 = linea_de_17[26];
  //   ruta17_27 = linea_de_17[27]; ruta17_28 = linea_de_17[28]; ruta17_29 = linea_de_17[29];
  //   ruta17_30 = linea_de_17[30]; ruta17_31 = linea_de_17[31]; ruta19_0 = linea_de_19[0]; ruta19_1 = linea_de_19[1];
  //   ruta19_2 = linea_de_19[2]; ruta19_3 = linea_de_19[3]; ruta19_4 = linea_de_19[4]; ruta19_5 = linea_de_19[5];
  //   ruta19_6 = linea_de_19[6]; ruta19_7 = linea_de_19[7]; ruta19_8 = linea_de_19[8]; ruta19_9 = linea_de_19[9];
  //   ruta19_10 = linea_de_19[10]; ruta19_11 = linea_de_19[11]; ruta19_12 = linea_de_19[12];
  //   ruta19_13 = linea_de_19[13]; ruta19_14 = linea_de_19[14]; ruta19_15 = linea_de_19[15];
  //   ruta19_16 = linea_de_19[16]; ruta19_17 = linea_de_19[17]; ruta19_18 = linea_de_19[18];
  //   ruta19_19 = linea_de_19[19]; ruta19_20 = linea_de_19[20]; ruta19_21 = linea_de_19[21];
  //   ruta19_22 = linea_de_19[22]; ruta19_23 = linea_de_19[23]; ruta19_24 = linea_de_19[24];
  //   ruta19_25 = linea_de_19[25]; ruta19_26 = linea_de_19[26]; ruta19_27 = linea_de_19[27];
  //   ruta19_28 = linea_de_19[28]; ruta19_29 = linea_de_19[29]; ruta19_30 = linea_de_19[30];
  //   ruta19_31 = linea_de_19[31]; ruta21_0 = linea_de_21[0]; ruta21_1 = linea_de_21[1]; ruta21_2 = linea_de_21[2];
  //   ruta21_3 = linea_de_21[3]; ruta21_4 = linea_de_21[4]; ruta21_5 = linea_de_21[5]; ruta21_6 = linea_de_21[6];
  //   ruta21_7 = linea_de_21[7]; ruta21_8 = linea_de_21[8]; ruta21_9 = linea_de_21[9]; ruta21_10 = linea_de_21[10];
  //   ruta21_11 = linea_de_21[11]; ruta21_12 = linea_de_21[12]; ruta21_13 = linea_de_21[13];
  //   ruta21_14 = linea_de_21[14]; ruta21_15 = linea_de_21[15]; ruta21_16 = linea_de_21[16];
  //   ruta21_17 = linea_de_21[17]; ruta21_18 = linea_de_21[18]; ruta21_19 = linea_de_21[19];
  //   ruta21_20 = linea_de_21[20]; ruta21_21 = linea_de_21[21]; ruta21_22 = linea_de_21[22];
  //   ruta21_23 = linea_de_21[23]; ruta21_24 = linea_de_21[24]; ruta21_25 = linea_de_21[25];
  //   ruta21_26 = linea_de_21[26]; ruta21_27 = linea_de_21[27]; ruta21_28 = linea_de_21[28];
  //   ruta21_29 = linea_de_21[29]; ruta21_30 = linea_de_21[30]; ruta21_31 = linea_de_21[31];
  //   ruta22_0 = linea_de_22[0]; ruta22_1 = linea_de_22[1]; ruta22_2 = linea_de_22[2]; ruta22_3 = linea_de_22[3];
  //   ruta22_4 = linea_de_22[4]; ruta22_5 = linea_de_22[5]; ruta22_6 = linea_de_22[6]; ruta22_7 = linea_de_22[7];
  //   ruta22_8 = linea_de_22[8]; ruta22_9 = linea_de_22[9]; ruta22_10 = linea_de_22[10]; ruta22_11 = linea_de_22[11];
  //   ruta22_12 = linea_de_22[12]; ruta22_13 = linea_de_22[13]; ruta22_14 = linea_de_22[14];
  //   ruta22_15 = linea_de_22[15]; ruta22_16 = linea_de_22[16]; ruta22_17 = linea_de_22[17];
  //   ruta22_18 = linea_de_22[18]; ruta22_19 = linea_de_22[19]; ruta22_20 = linea_de_22[20];
  //   ruta22_21 = linea_de_22[21]; ruta22_22 = linea_de_22[22]; ruta22_23 = linea_de_22[23];
  //   ruta22_24 = linea_de_22[24]; ruta22_25 = linea_de_22[25]; ruta22_26 = linea_de_22[26];
  //   ruta22_27 = linea_de_22[27]; ruta22_28 = linea_de_22[28]; ruta22_29 = linea_de_22[29];
  //   ruta22_30 = linea_de_22[30]; ruta22_31 = linea_de_22[31]; ruta23_0 = linea_de_23[0]; ruta23_1 = linea_de_23[1];
  //   ruta23_2 = linea_de_23[2]; ruta23_3 = linea_de_23[3]; ruta23_4 = linea_de_23[4]; ruta23_5 = linea_de_23[5];
  //   ruta23_6 = linea_de_23[6]; ruta23_7 = linea_de_23[7]; ruta23_8 = linea_de_23[8]; ruta23_9 = linea_de_23[9];
  //   ruta23_10 = linea_de_23[10]; ruta23_11 = linea_de_23[11]; ruta23_12 = linea_de_23[12];
  //   ruta23_13 = linea_de_23[13]; ruta23_14 = linea_de_23[14]; ruta23_15 = linea_de_23[15];
  //   ruta23_16 = linea_de_23[16]; ruta23_17 = linea_de_23[17]; ruta23_18 = linea_de_23[18];
  //   ruta23_19 = linea_de_23[19]; ruta23_20 = linea_de_23[20]; ruta23_21 = linea_de_23[21];
  //   ruta23_22 = linea_de_23[22]; ruta23_23 = linea_de_23[23]; ruta23_24 = linea_de_23[24];
  //   ruta23_25 = linea_de_23[25]; ruta23_26 = linea_de_23[26]; ruta23_27 = linea_de_23[27];
  //   ruta23_28 = linea_de_23[28]; ruta23_29 = linea_de_23[29]; ruta23_30 = linea_de_23[30];
  //   ruta23_31 = linea_de_23[31]; ruta26_0 = linea_de_26[0]; ruta26_1 = linea_de_26[1]; ruta26_2 = linea_de_26[2];
  //   ruta26_3 = linea_de_26[3]; ruta26_4 = linea_de_26[4]; ruta26_5 = linea_de_26[5]; ruta26_6 = linea_de_26[6];
  //   ruta26_7 = linea_de_26[7]; ruta26_8 = linea_de_26[8]; ruta26_9 = linea_de_26[9]; ruta26_10 = linea_de_26[10];
  //   ruta26_11 = linea_de_26[11]; ruta26_12 = linea_de_26[12]; ruta26_13 = linea_de_26[13];
  //   ruta26_14 = linea_de_26[14]; ruta26_15 = linea_de_26[15]; ruta26_16 = linea_de_26[16];
  //   ruta26_17 = linea_de_26[17]; ruta26_18 = linea_de_26[18]; ruta26_19 = linea_de_26[19];
  //   ruta26_20 = linea_de_26[20]; ruta26_21 = linea_de_26[21]; ruta26_22 = linea_de_26[22];
  //   ruta26_23 = linea_de_26[23]; ruta26_24 = linea_de_26[24]; ruta26_25 = linea_de_26[25];
  //   ruta26_26 = linea_de_26[26]; ruta26_27 = linea_de_26[27]; ruta26_28 = linea_de_26[28];
  //   ruta26_29 = linea_de_26[29]; ruta26_30 = linea_de_26[30]; ruta26_31 = linea_de_26[31];
  //   ruta27_0 = linea_de_27[0]; ruta27_1 = linea_de_27[1]; ruta27_2 = linea_de_27[2]; ruta27_3 = linea_de_27[3];
  //   ruta27_4 = linea_de_27[4]; ruta27_5 = linea_de_27[5]; ruta27_6 = linea_de_27[6]; ruta27_7 = linea_de_27[7];
  //   ruta27_8 = linea_de_27[8]; ruta27_9 = linea_de_27[9]; ruta27_10 = linea_de_27[10]; ruta27_11 = linea_de_27[11];
  //   ruta27_12 = linea_de_27[12]; ruta27_13 = linea_de_27[13]; ruta27_14 = linea_de_27[14];
  //   ruta27_15 = linea_de_27[15]; ruta27_16 = linea_de_27[16]; ruta27_17 = linea_de_27[17];
  //   ruta27_18 = linea_de_27[18]; ruta27_19 = linea_de_27[19]; ruta27_20 = linea_de_27[20];
  //   ruta27_21 = linea_de_27[21]; ruta27_22 = linea_de_27[22]; ruta27_23 = linea_de_27[23];
  //   ruta27_24 = linea_de_27[24]; ruta27_25 = linea_de_27[25]; ruta27_26 = linea_de_27[26];
  //   ruta27_27 = linea_de_27[27]; ruta27_28 = linea_de_27[28]; ruta27_29 = linea_de_27[29];
  //   ruta27_30 = linea_de_27[30]; ruta27_31 = linea_de_27[31]; ruta29_0 = linea_de_29[0]; ruta29_1 = linea_de_29[1];
  //   ruta29_2 = linea_de_29[2]; ruta29_3 = linea_de_29[3]; ruta29_4 = linea_de_29[4]; ruta29_5 = linea_de_29[5];
  //   ruta29_6 = linea_de_29[6]; ruta29_7 = linea_de_29[7]; ruta29_8 = linea_de_29[8]; ruta29_9 = linea_de_29[9];
  //   ruta29_10 = linea_de_29[10]; ruta29_11 = linea_de_29[11]; ruta29_12 = linea_de_29[12];
  //   ruta29_13 = linea_de_29[13]; ruta29_14 = linea_de_29[14]; ruta29_15 = linea_de_29[15];
  //   ruta29_16 = linea_de_29[16]; ruta29_17 = linea_de_29[17]; ruta29_18 = linea_de_29[18];
  //   ruta29_19 = linea_de_29[19]; ruta29_20 = linea_de_29[20]; ruta29_21 = linea_de_29[21];
  //   ruta29_22 = linea_de_29[22]; ruta29_23 = linea_de_29[23]; ruta29_24 = linea_de_29[24];
  //   ruta29_25 = linea_de_29[25]; ruta29_26 = linea_de_29[26]; ruta29_27 = linea_de_29[27];
  //   ruta29_28 = linea_de_29[28]; ruta29_29 = linea_de_29[29]; ruta29_30 = linea_de_29[30];
  //   ruta29_31 = linea_de_29[31]; ruta32_0 = linea_de_32[0]; ruta32_1 = linea_de_32[1]; ruta32_2 = linea_de_32[2];
  //   ruta32_3 = linea_de_32[3]; ruta32_4 = linea_de_32[4]; ruta32_5 = linea_de_32[5]; ruta32_6 = linea_de_32[6];
  //   ruta32_7 = linea_de_32[7]; ruta32_8 = linea_de_32[8]; ruta32_9 = linea_de_32[9]; ruta32_10 = linea_de_32[10];
  //   ruta32_11 = linea_de_32[11]; ruta32_12 = linea_de_32[12]; ruta32_13 = linea_de_32[13];
  //   ruta32_14 = linea_de_32[14]; ruta32_15 = linea_de_32[15]; ruta32_16 = linea_de_32[16];
  //   ruta32_17 = linea_de_32[17]; ruta32_18 = linea_de_32[18]; ruta32_19 = linea_de_32[19];
  //   ruta32_20 = linea_de_32[20]; ruta32_21 = linea_de_32[21]; ruta32_22 = linea_de_32[22];
  //   ruta32_23 = linea_de_32[23]; ruta32_24 = linea_de_32[24]; ruta32_25 = linea_de_32[25];
  //   ruta32_26 = linea_de_32[26]; ruta32_27 = linea_de_32[27]; ruta32_28 = linea_de_32[28];
  //   ruta32_29 = linea_de_32[29]; ruta32_30 = linea_de_32[30]; ruta32_31 = linea_de_32[31];
  //   ruta33_0 = linea_de_33[0]; ruta33_1 = linea_de_33[1]; ruta33_2 = linea_de_33[2]; ruta33_3 = linea_de_33[3];
  //   ruta33_4 = linea_de_33[4]; ruta33_5 = linea_de_33[5]; ruta33_6 = linea_de_33[6]; ruta33_7 = linea_de_33[7];
  //   ruta33_8 = linea_de_33[8]; ruta33_9 = linea_de_33[9]; ruta33_10 = linea_de_33[10]; ruta33_11 = linea_de_33[11];
  //   ruta33_12 = linea_de_33[12]; ruta33_13 = linea_de_33[13]; ruta33_14 = linea_de_33[14];
  //   ruta33_15 = linea_de_33[15]; ruta33_16 = linea_de_33[16]; ruta33_17 = linea_de_33[17];
  //   ruta33_18 = linea_de_33[18]; ruta33_19 = linea_de_33[19]; ruta33_20 = linea_de_33[20];
  //   ruta33_21 = linea_de_33[21]; ruta33_22 = linea_de_33[22]; ruta33_23 = linea_de_33[23];
  //   ruta33_24 = linea_de_33[24]; ruta33_25 = linea_de_33[25]; ruta33_26 = linea_de_33[26];
  //   ruta33_27 = linea_de_33[27]; ruta33_28 = linea_de_33[28]; ruta33_29 = linea_de_33[29];
  //   ruta33_30 = linea_de_33[30]; ruta33_31 = linea_de_33[31]; ruta34_0 = linea_de_34[0]; ruta34_1 = linea_de_34[1];
  //   ruta34_2 = linea_de_34[2]; ruta34_3 = linea_de_34[3]; ruta34_4 = linea_de_34[4]; ruta34_5 = linea_de_34[5];
  //   ruta34_6 = linea_de_34[6]; ruta34_7 = linea_de_34[7]; ruta34_8 = linea_de_34[8]; ruta34_9 = linea_de_34[9];
  //   ruta34_10 = linea_de_34[10]; ruta34_11 = linea_de_34[11]; ruta34_12 = linea_de_34[12];
  //   ruta34_13 = linea_de_34[13]; ruta34_14 = linea_de_34[14]; ruta34_15 = linea_de_34[15];
  //   ruta34_16 = linea_de_34[16]; ruta34_17 = linea_de_34[17]; ruta34_18 = linea_de_34[18];
  //   ruta34_19 = linea_de_34[19]; ruta34_20 = linea_de_34[20]; ruta34_21 = linea_de_34[21];
  //   ruta34_22 = linea_de_34[22]; ruta34_23 = linea_de_34[23]; ruta34_24 = linea_de_34[24];
  //   ruta34_25 = linea_de_34[25]; ruta34_26 = linea_de_34[26]; ruta34_27 = linea_de_34[27];
  //   ruta34_28 = linea_de_34[28]; ruta34_29 = linea_de_34[29]; ruta34_30 = linea_de_34[30];
  //   ruta34_31 = linea_de_34[31]; ruta35_0 = linea_de_35[0]; ruta35_1 = linea_de_35[1]; ruta35_2 = linea_de_35[2];
  //   ruta35_3 = linea_de_35[3]; ruta35_4 = linea_de_35[4]; ruta35_5 = linea_de_35[5]; ruta35_6 = linea_de_35[6];
  //   ruta35_7 = linea_de_35[7]; ruta35_8 = linea_de_35[8]; ruta35_9 = linea_de_35[9]; ruta35_10 = linea_de_35[10];
  //   ruta35_11 = linea_de_35[11]; ruta35_12 = linea_de_35[12]; ruta35_13 = linea_de_35[13];
  //   ruta35_14 = linea_de_35[14]; ruta35_15 = linea_de_35[15]; ruta35_16 = linea_de_35[16];
  //   ruta35_17 = linea_de_35[17]; ruta35_18 = linea_de_35[18]; ruta35_19 = linea_de_35[19];
  //   ruta35_20 = linea_de_35[20]; ruta35_21 = linea_de_35[21]; ruta35_22 = linea_de_35[22];
  //   ruta35_23 = linea_de_35[23]; ruta35_24 = linea_de_35[24]; ruta35_25 = linea_de_35[25];
  //   ruta35_26 = linea_de_35[26]; ruta35_27 = linea_de_35[27]; ruta35_28 = linea_de_35[28];
  //   ruta35_29 = linea_de_35[29]; ruta35_30 = linea_de_35[30]; ruta35_31 = linea_de_35[31];
  //   ruta37_0 = linea_de_37[0]; ruta37_1 = linea_de_37[1]; ruta37_2 = linea_de_37[2]; ruta37_3 = linea_de_37[3];
  //   ruta37_4 = linea_de_37[4]; ruta37_5 = linea_de_37[5]; ruta37_6 = linea_de_37[6]; ruta37_7 = linea_de_37[7];
  //   ruta37_8 = linea_de_37[8]; ruta37_9 = linea_de_37[9]; ruta37_10 = linea_de_37[10]; ruta37_11 = linea_de_37[11];
  //   ruta37_12 = linea_de_37[12]; ruta37_13 = linea_de_37[13]; ruta37_14 = linea_de_37[14];
  //   ruta37_15 = linea_de_37[15]; ruta37_16 = linea_de_37[16]; ruta37_17 = linea_de_37[17];
  //   ruta37_18 = linea_de_37[18]; ruta37_19 = linea_de_37[19]; ruta37_20 = linea_de_37[20];
  //   ruta37_21 = linea_de_37[21]; ruta37_22 = linea_de_37[22]; ruta37_23 = linea_de_37[23];
  //   ruta37_24 = linea_de_37[24]; ruta37_25 = linea_de_37[25]; ruta37_26 = linea_de_37[26];
  //   ruta37_27 = linea_de_37[27]; ruta37_28 = linea_de_37[28]; ruta37_29 = linea_de_37[29];
  //   ruta37_30 = linea_de_37[30]; ruta37_31 = linea_de_37[31]; ruta38_0 = linea_de_38[0]; ruta38_1 = linea_de_38[1];
  //   ruta38_2 = linea_de_38[2]; ruta38_3 = linea_de_38[3]; ruta38_4 = linea_de_38[4]; ruta38_5 = linea_de_38[5];
  //   ruta38_6 = linea_de_38[6]; ruta38_7 = linea_de_38[7]; ruta38_8 = linea_de_38[8]; ruta38_9 = linea_de_38[9];
  //   ruta38_10 = linea_de_38[10]; ruta38_11 = linea_de_38[11]; ruta38_12 = linea_de_38[12];
  //   ruta38_13 = linea_de_38[13]; ruta38_14 = linea_de_38[14]; ruta38_15 = linea_de_38[15];
  //   ruta38_16 = linea_de_38[16]; ruta38_17 = linea_de_38[17]; ruta38_18 = linea_de_38[18];
  //   ruta38_19 = linea_de_38[19]; ruta38_20 = linea_de_38[20]; ruta38_21 = linea_de_38[21];
  //   ruta38_22 = linea_de_38[22]; ruta38_23 = linea_de_38[23]; ruta38_24 = linea_de_38[24];
  //   ruta38_25 = linea_de_38[25]; ruta38_26 = linea_de_38[26]; ruta38_27 = linea_de_38[27];
  //   ruta38_28 = linea_de_38[28]; ruta38_29 = linea_de_38[29]; ruta38_30 = linea_de_38[30];
  //   ruta38_31 = linea_de_38[31]; ruta39_0 = linea_de_39[0]; ruta39_1 = linea_de_39[1]; ruta39_2 = linea_de_39[2];
  //   ruta39_3 = linea_de_39[3]; ruta39_4 = linea_de_39[4]; ruta39_5 = linea_de_39[5]; ruta39_6 = linea_de_39[6];
  //   ruta39_7 = linea_de_39[7]; ruta39_8 = linea_de_39[8]; ruta39_9 = linea_de_39[9]; ruta39_10 = linea_de_39[10];
  //   ruta39_11 = linea_de_39[11]; ruta39_12 = linea_de_39[12]; ruta39_13 = linea_de_39[13];
  //   ruta39_14 = linea_de_39[14]; ruta39_15 = linea_de_39[15]; ruta39_16 = linea_de_39[16];
  //   ruta39_17 = linea_de_39[17]; ruta39_18 = linea_de_39[18]; ruta39_19 = linea_de_39[19];
  //   ruta39_20 = linea_de_39[20]; ruta39_21 = linea_de_39[21]; ruta39_22 = linea_de_39[22];
  //   ruta39_23 = linea_de_39[23]; ruta39_24 = linea_de_39[24]; ruta39_25 = linea_de_39[25];
  //   ruta39_26 = linea_de_39[26]; ruta39_27 = linea_de_39[27]; ruta39_28 = linea_de_39[28];
  //   ruta39_29 = linea_de_39[29]; ruta39_30 = linea_de_39[30]; ruta39_31 = linea_de_39[31];
  //   ruta49_0 = linea_de_49[0]; ruta49_1 = linea_de_49[1]; ruta49_2 = linea_de_49[2]; ruta49_3 = linea_de_49[3];
  //   ruta49_4 = linea_de_49[4]; ruta49_5 = linea_de_49[5]; ruta49_6 = linea_de_49[6]; ruta49_7 = linea_de_49[7];
  //   ruta49_8 = linea_de_49[8]; ruta49_9 = linea_de_49[9]; ruta49_10 = linea_de_49[10]; ruta49_11 = linea_de_49[11];
  //   ruta49_12 = linea_de_49[12]; ruta49_13 = linea_de_49[13]; ruta49_14 = linea_de_49[14];
  //   ruta49_15 = linea_de_49[15]; ruta49_16 = linea_de_49[16]; ruta49_17 = linea_de_49[17];
  //   ruta49_18 = linea_de_49[18]; ruta49_19 = linea_de_49[19]; ruta49_20 = linea_de_49[20];
  //   ruta49_21 = linea_de_49[21]; ruta49_22 = linea_de_49[22]; ruta49_23 = linea_de_49[23];
  //   ruta49_24 = linea_de_49[24]; ruta49_25 = linea_de_49[25]; ruta49_26 = linea_de_49[26];
  //   ruta49_27 = linea_de_49[27]; ruta49_28 = linea_de_49[28]; ruta49_29 = linea_de_49[29];
  //   ruta49_30 = linea_de_49[30]; ruta49_31 = linea_de_49[31]; ruta50_0 = linea_de_50[0]; ruta50_1 = linea_de_50[1];
  //   ruta50_2 = linea_de_50[2]; ruta50_3 = linea_de_50[3]; ruta50_4 = linea_de_50[4]; ruta50_5 = linea_de_50[5];
  //   ruta50_6 = linea_de_50[6]; ruta50_7 = linea_de_50[7]; ruta50_8 = linea_de_50[8]; ruta50_9 = linea_de_50[9];
  //   ruta50_10 = linea_de_50[10]; ruta50_11 = linea_de_50[11]; ruta50_12 = linea_de_50[12];
  //   ruta50_13 = linea_de_50[13]; ruta50_14 = linea_de_50[14]; ruta50_15 = linea_de_50[15];
  //   ruta50_16 = linea_de_50[16]; ruta50_17 = linea_de_50[17]; ruta50_18 = linea_de_50[18];
  //   ruta50_19 = linea_de_50[19]; ruta50_20 = linea_de_50[20]; ruta50_21 = linea_de_50[21];
  //   ruta50_22 = linea_de_50[22]; ruta50_23 = linea_de_50[23]; ruta50_24 = linea_de_50[24];
  //   ruta50_25 = linea_de_50[25]; ruta50_26 = linea_de_50[26]; ruta50_27 = linea_de_50[27];
  //   ruta50_28 = linea_de_50[28]; ruta50_29 = linea_de_50[29]; ruta50_30 = linea_de_50[30];
  //   ruta50_31 = linea_de_50[31]; ruta51_0 = linea_de_51[0]; ruta51_1 = linea_de_51[1]; ruta51_2 = linea_de_51[2];
  //   ruta51_3 = linea_de_51[3]; ruta51_4 = linea_de_51[4]; ruta51_5 = linea_de_51[5]; ruta51_6 = linea_de_51[6];
  //   ruta51_7 = linea_de_51[7]; ruta51_8 = linea_de_51[8]; ruta51_9 = linea_de_51[9]; ruta51_10 = linea_de_51[10];
  //   ruta51_11 = linea_de_51[11]; ruta51_12 = linea_de_51[12]; ruta51_13 = linea_de_51[13];
  //   ruta51_14 = linea_de_51[14]; ruta51_15 = linea_de_51[15]; ruta51_16 = linea_de_51[16];
  //   ruta51_17 = linea_de_51[17]; ruta51_18 = linea_de_51[18]; ruta51_19 = linea_de_51[19];
  //   ruta51_20 = linea_de_51[20]; ruta51_21 = linea_de_51[21]; ruta51_22 = linea_de_51[22];
  //   ruta51_23 = linea_de_51[23]; ruta51_24 = linea_de_51[24]; ruta51_25 = linea_de_51[25];
  //   ruta51_26 = linea_de_51[26]; ruta51_27 = linea_de_51[27]; ruta51_28 = linea_de_51[28];
  //   ruta51_29 = linea_de_51[29]; ruta51_30 = linea_de_51[30]; ruta51_31 = linea_de_51[31];
  //   ruta52_0 = linea_de_52[0]; ruta52_1 = linea_de_52[1]; ruta52_2 = linea_de_52[2]; ruta52_3 = linea_de_52[3];
  //   ruta52_4 = linea_de_52[4]; ruta52_5 = linea_de_52[5]; ruta52_6 = linea_de_52[6]; ruta52_7 = linea_de_52[7];
  //   ruta52_8 = linea_de_52[8]; ruta52_9 = linea_de_52[9]; ruta52_10 = linea_de_52[10]; ruta52_11 = linea_de_52[11];
  //   ruta52_12 = linea_de_52[12]; ruta52_13 = linea_de_52[13]; ruta52_14 = linea_de_52[14];
  //   ruta52_15 = linea_de_52[15]; ruta52_16 = linea_de_52[16]; ruta52_17 = linea_de_52[17];
  //   ruta52_18 = linea_de_52[18]; ruta52_19 = linea_de_52[19]; ruta52_20 = linea_de_52[20];
  //   ruta52_21 = linea_de_52[21]; ruta52_22 = linea_de_52[22]; ruta52_23 = linea_de_52[23];
  //   ruta52_24 = linea_de_52[24]; ruta52_25 = linea_de_52[25]; ruta52_26 = linea_de_52[26];
  //   ruta52_27 = linea_de_52[27]; ruta52_28 = linea_de_52[28]; ruta52_29 = linea_de_52[29];
  //   ruta52_30 = linea_de_52[30]; ruta52_31 = linea_de_52[31]; ruta53_0 = linea_de_53[0]; ruta53_1 = linea_de_53[1];
  //   ruta53_2 = linea_de_53[2]; ruta53_3 = linea_de_53[3]; ruta53_4 = linea_de_53[4]; ruta53_5 = linea_de_53[5];
  //   ruta53_6 = linea_de_53[6]; ruta53_7 = linea_de_53[7]; ruta53_8 = linea_de_53[8]; ruta53_9 = linea_de_53[9];
  //   ruta53_10 = linea_de_53[10]; ruta53_11 = linea_de_53[11]; ruta53_12 = linea_de_53[12];
  //   ruta53_13 = linea_de_53[13]; ruta53_14 = linea_de_53[14]; ruta53_15 = linea_de_53[15];
  //   ruta53_16 = linea_de_53[16]; ruta53_17 = linea_de_53[17]; ruta53_18 = linea_de_53[18];
  //   ruta53_19 = linea_de_53[19]; ruta53_20 = linea_de_53[20]; ruta53_21 = linea_de_53[21];
  //   ruta53_22 = linea_de_53[22]; ruta53_23 = linea_de_53[23]; ruta53_24 = linea_de_53[24];
  //   ruta53_25 = linea_de_53[25]; ruta53_26 = linea_de_53[26]; ruta53_27 = linea_de_53[27];
  //   ruta53_28 = linea_de_53[28]; ruta53_29 = linea_de_53[29]; ruta53_30 = linea_de_53[30];
  //   ruta53_31 = linea_de_53[31]; MAPAS0_4_0[4:0] = MAPAS0[4:0]; MAPAS0_9_5[4:0] = MAPAS0[9:5];
  //   MAPAS0_14_10[4:0] = MAPAS0[14:10]; MAPAS0_19_15[4:0] = MAPAS0[19:15]; MAPAS0_24_20[4:0] = MAPAS0[24:20];
  //   MAPAS0_29_25[4:0] = MAPAS0[29:25]; rep1[4:0] = MAPAS0_mascara[4:0]; rep2[4:0] = MAPAS0_mascara[9:5];
  //   rep3[4:0] = MAPAS0_mascara[14:10]; rep4[4:0] = MAPAS0_mascara[19:15]; rep5[4:0] = MAPAS0_mascara[24:20];
  //   rep6[4:0] = MAPAS0_mascara[29:25]; MAPAS1_4_0[4:0] = MAPAS1[4:0]; MAPAS1_9_5[4:0] = MAPAS1[9:5];
  //   MAPAS1_14_10[4:0] = MAPAS1[14:10]; MAPAS1_19_15[4:0] = MAPAS1[19:15]; MAPAS1_24_20[4:0] = MAPAS1[24:20];
  //   MAPAS1_29_25[4:0] = MAPAS1[29:25]; rep10[4:0] = MAPAS1_mascara[4:0]; rep11[4:0] = MAPAS1_mascara[9:5];
  //   rep12[4:0] = MAPAS1_mascara[14:10]; rep13[4:0] = MAPAS1_mascara[19:15]; rep14[4:0] = MAPAS1_mascara[24:20];
  //   rep15[4:0] = MAPAS1_mascara[29:25]; MAPAS2_4_0[4:0] = MAPAS2[4:0]; MAPAS2_9_5[4:0] = MAPAS2[9:5];
  //   MAPAS2_14_10[4:0] = MAPAS2[14:10]; MAPAS2_19_15[4:0] = MAPAS2[19:15]; MAPAS2_24_20[4:0] = MAPAS2[24:20];
  //   MAPAS2_29_25[4:0] = MAPAS2[29:25]; rep19[4:0] = MAPAS2_mascara[4:0]; rep20[4:0] = MAPAS2_mascara[9:5];
  //   rep21[4:0] = MAPAS2_mascara[14:10]; rep22[4:0] = MAPAS2_mascara[19:15]; rep23[4:0] = MAPAS2_mascara[24:20];
  //   rep24[4:0] = MAPAS2_mascara[29:25]; MAPAS3_4_0[4:0] = MAPAS3[4:0]; MAPAS3_9_5[4:0] = MAPAS3[9:5];
  //   MAPAS3_14_10[4:0] = MAPAS3[14:10]; rep28[4:0] = MAPAS3_mascara[4:0]; rep29[4:0] = MAPAS3_mascara[9:5];
  //   rep30[4:0] = MAPAS3_mascara[14:10]; dato_escrito_4_0[4:0] = dato_escrito[4:0];
  //   MAPAS0_nuevo[29:0] = {dato_escrito[4:0], dato_escrito[4:0], dato_escrito[4:0], dato_escrito[4:0], dato_escrito[4:0], dato_escrito[4:0]};
  //   MAPAS1_nuevo[29:0] = {dato_escrito[4:0], dato_escrito[4:0], dato_escrito[4:0], dato_escrito[4:0], dato_escrito[4:0], dato_escrito[4:0]};
  //   MAPAS2_nuevo[29:0] = {dato_escrito[4:0], dato_escrito[4:0], dato_escrito[4:0], dato_escrito[4:0], dato_escrito[4:0], dato_escrito[4:0]};
  //   MAPAS3_nuevo[14:0] = {dato_escrito[4:0], dato_escrito[4:0], dato_escrito[4:0]};
  //   PRIORIDADES0_3_0[3:0] = PRIORIDADES0[3:0]; PRIORIDADES0_7_4[3:0] = PRIORIDADES0[7:4];
  //   PRIORIDADES0_11_8[3:0] = PRIORIDADES0[11:8]; PRIORIDADES0_15_12[3:0] = PRIORIDADES0[15:12];
  //   PRIORIDADES0_19_16[3:0] = PRIORIDADES0[19:16]; PRIORIDADES0_23_20[3:0] = PRIORIDADES0[23:20];
  //   PRIORIDADES0_27_24[3:0] = PRIORIDADES0[27:24]; PRIORIDADES0_31_28[3:0] = PRIORIDADES0[31:28];
  //   rep63[3:0] = PRIORIDADES0_mascara[3:0]; rep64[3:0] = PRIORIDADES0_mascara[7:4];
  //   rep65[3:0] = PRIORIDADES0_mascara[11:8]; rep66[3:0] = PRIORIDADES0_mascara[15:12];
  //   rep67[3:0] = PRIORIDADES0_mascara[19:16]; rep68[3:0] = PRIORIDADES0_mascara[23:20];
  //   rep69[3:0] = PRIORIDADES0_mascara[27:24]; rep70[3:0] = PRIORIDADES0_mascara[31:28];
  //   PRIORIDADES1_3_0[3:0] = PRIORIDADES1[3:0]; PRIORIDADES1_7_4[3:0] = PRIORIDADES1[7:4];
  //   PRIORIDADES1_11_8[3:0] = PRIORIDADES1[11:8]; PRIORIDADES1_15_12[3:0] = PRIORIDADES1[15:12];
  //   PRIORIDADES1_19_16[3:0] = PRIORIDADES1[19:16]; PRIORIDADES1_23_20[3:0] = PRIORIDADES1[23:20];
  //   PRIORIDADES1_27_24[3:0] = PRIORIDADES1[27:24]; PRIORIDADES1_31_28[3:0] = PRIORIDADES1[31:28];
  //   rep74[3:0] = PRIORIDADES1_mascara[3:0]; rep75[3:0] = PRIORIDADES1_mascara[7:4];
  //   rep76[3:0] = PRIORIDADES1_mascara[11:8]; rep77[3:0] = PRIORIDADES1_mascara[15:12];
  //   rep78[3:0] = PRIORIDADES1_mascara[19:16]; rep79[3:0] = PRIORIDADES1_mascara[23:20];
  //   rep80[3:0] = PRIORIDADES1_mascara[27:24]; rep81[3:0] = PRIORIDADES1_mascara[31:28];
  //   PRIORIDADES2_3_0[3:0] = PRIORIDADES2[3:0]; PRIORIDADES2_7_4[3:0] = PRIORIDADES2[7:4];
  //   PRIORIDADES2_11_8[3:0] = PRIORIDADES2[11:8]; PRIORIDADES2_15_12[3:0] = PRIORIDADES2[15:12];
  //   PRIORIDADES2_19_16[3:0] = PRIORIDADES2[19:16]; PRIORIDADES2_23_20[3:0] = PRIORIDADES2[23:20];
  //   PRIORIDADES2_27_24[3:0] = PRIORIDADES2[27:24]; PRIORIDADES2_31_28[3:0] = PRIORIDADES2[31:28];
  //   rep85[3:0] = PRIORIDADES2_mascara[3:0]; rep86[3:0] = PRIORIDADES2_mascara[7:4];
  //   rep87[3:0] = PRIORIDADES2_mascara[11:8]; rep88[3:0] = PRIORIDADES2_mascara[15:12];
  //   rep89[3:0] = PRIORIDADES2_mascara[19:16]; rep90[3:0] = PRIORIDADES2_mascara[23:20];
  //   rep91[3:0] = PRIORIDADES2_mascara[27:24]; rep92[3:0] = PRIORIDADES2_mascara[31:28];
  //   PRIORIDADES3_3_0[3:0] = PRIORIDADES3[3:0]; PRIORIDADES3_7_4[3:0] = PRIORIDADES3[7:4];
  //   PRIORIDADES3_11_8[3:0] = PRIORIDADES3[11:8]; PRIORIDADES3_15_12[3:0] = PRIORIDADES3[15:12];
  //   PRIORIDADES3_19_16[3:0] = PRIORIDADES3[19:16]; PRIORIDADES3_23_20[3:0] = PRIORIDADES3[23:20];
  //   PRIORIDADES3_27_24[3:0] = PRIORIDADES3[27:24]; PRIORIDADES3_31_28[3:0] = PRIORIDADES3[31:28];
  //   rep96[3:0] = PRIORIDADES3_mascara[3:0]; rep97[3:0] = PRIORIDADES3_mascara[7:4];
  //   rep98[3:0] = PRIORIDADES3_mascara[11:8]; rep99[3:0] = PRIORIDADES3_mascara[15:12];
  //   rep100[3:0] = PRIORIDADES3_mascara[19:16]; rep101[3:0] = PRIORIDADES3_mascara[23:20];
  //   rep102[3:0] = PRIORIDADES3_mascara[27:24]; rep103[3:0] = PRIORIDADES3_mascara[31:28];
  //   dato_escrito_3_0[3:0] = dato_escrito[3:0];
  //   PRIORIDADES0_nuevo[31:0] = {dato_escrito[3:0], dato_escrito[3:0], dato_escrito[3:0], dato_escrito[3:0], dato_escrito[3:0], dato_escrito[3:0], dato_escrito[3:0], dato_escrito[3:0]};
  //   PRIORIDADES1_nuevo[31:0] = {dato_escrito[3:0], dato_escrito[3:0], dato_escrito[3:0], dato_escrito[3:0], dato_escrito[3:0], dato_escrito[3:0], dato_escrito[3:0], dato_escrito[3:0]};
  //   PRIORIDADES2_nuevo[31:0] = {dato_escrito[3:0], dato_escrito[3:0], dato_escrito[3:0], dato_escrito[3:0], dato_escrito[3:0], dato_escrito[3:0], dato_escrito[3:0], dato_escrito[3:0]};
  //   PRIORIDADES3_nuevo[31:0] = {dato_escrito[3:0], dato_escrito[3:0], dato_escrito[3:0], dato_escrito[3:0], dato_escrito[3:0], dato_escrito[3:0], dato_escrito[3:0], dato_escrito[3:0]};
  //   or314[31:0] = RD

  // Notes on the sheet:
  //   contents of REGISTROS_EXISTE (hex, n*v repeats v):
  //   62*1 0 0 1 5*0 32*1 409*0 1
  //   contents of REGISTROS_VALOR_RESET (hex, n*v repeats v):
  //   64*0 1 446*0 2007210
  //   contents of REGISTROS_BITS_RW (hex, n*v repeats v):
  //   62*1f 0 0 1 5*0 32*f 409*0 fffffff
endmodule

module RTC_CNTL (
  input  CHIP_EN,
  input  CLK,
  input  SEL,
  input  [9:0] A,
  input  [31:0] WD,
  input  WE,
  input  RE,
  input  TG0_RESET_SIS,
  input  TG1_RESET_SIS,
  input  TG0_RESET_CPU,
  input  TG1_RESET_CPU,
  output IRQ,
  output RST_SIS,
  output RST_CPU,
  output [31:0] RD
);

  wire and1, and2, and4, and9, and12, and15, and18, and21, and24, and64, and68, chip_en_pullup, co3, eq36,
       eq51, eq56, eq59, eq61, esc_000, esc_0A0, esc_0A4, esc_0A8, esc_00C, esc_04C, esc_09C, esc_040,
       esc_090, esc_094, esc_098, escribe, lee, lin_0, lin_1, lin_2, lin_3, lin_4, lin_5, lin_6, lin_7,
       lin_8, lin_9, lin_10, lin_11, lin_12, lin_13, lin_14, lin_15, lin_16, lin_17, lin_18, lin_19, lin_20,
       lin_21, lin_22, lin_23, lin_24, lin_25, lin_26, lin_27, lin_28, lin_29, lin_30, lin_31, not52, not57,
       not60, not62, or45, or53, or58, pag_0, pag_1, pag_2, pag_3, pag_4, pag_5, pag_6, pag_7, pag_8, pag_9,
       pag_10, pag_11, pag_12, pag_13, pag_14, pag_15, pag_16, pag_17, pag_18, pag_19, pag_20, pag_21,
       pag_22, pag_23, pag_24, pag_25, pag_26, pag_27, pag_28, pag_29, pag_30, pag_31, pide_reset_cpu,
       pide_reset_sistema, r000, r0A0, r0A4, r0A8, r00C, r04C, r09C, r010, r014, r038, r040, r044, r048,
       r090, r094, r098, registros_acceso, registros_existe, reset_encendido, rwdt_alimenta,
       rwdt_desbloqueado, rwdt_reset_cpu, rwdt_reset_sis;
  wire [1:0] cuenta_reset_cpu, cuenta_reset_sis, mux50, mux55, sum49, sum54;
  wire [3:3] INT_eventos;
  wire [5:0] causa_nueva, mux37, mux38, mux39, mux40, mux41, mux42, mux43, mux44, qx47, RESET_CAUSE, xor46;
  wire [7:0] cat29;
  wire [9:0] dir_registro, rep63;
  wire [15:0] rtc_mas1_hi, rtc_tiempo_hi, TIME_HIGH0;
  wire [31:0] and8, and32, and34, and35, and67, and71, and73, and75, and77, and79, and81, and83, and85,
       and87, and89, and91, and93, and95, dato_escrito, INT_clr, INT_ENA, INT_raw, INT_st, not31, not66,
       or33, qx7, qx11, qx14, qx17, qx20, qx23, registros_a_guardar, registros_bits_fijos, registros_bits_rw,
       registros_guardado, registros_reset_rw, registros_valor, registros_valor_reset, rep30, rep65, rep70,
       rep72, rep74, rep76, rep78, rep80, rep82, rep84, rep86, rep88, rep90, rep92, rep94, rtc_mas1,
       rtc_tiempo_lo, TIME_LOW0, WDTCONFIG0, WDTCONFIG1, WDTCONFIG2, WDTCONFIG3, WDTCONFIG4, WDTWPROTECT,
       xor6, xor10, xor13, xor16, xor19, xor22, xor69, zx5, zx48;

  Pull_Resistor #(.pull(1)) pull_resistor_1 (.node(chip_en_pullup));
  assign chip_en_pullup = 1'b1 ? CHIP_EN : 1'bz;  // Controlled_Buffer controlled_buffer_1
  Register #(.width(32)) RTC_LO (.D(rtc_mas1), .en(1'b1), .Q(rtc_tiempo_lo), .clk(CLK), .clr(reset_encendido));
  Register #(.width(16)) RTC_HI (.D(rtc_mas1_hi), .en(1'b1), .Q(rtc_tiempo_hi), .clk(CLK), .clr(reset_encendido));
  Register #(.width(32)) u_TIME_LOW0 (.D(rtc_tiempo_lo), .en(and4), .Q(TIME_LOW0), .clk(CLK), .clr(reset_encendido));
  Register #(.width(16)) u_TIME_HIGH0 (.D(rtc_tiempo_hi), .en(and4), .Q(TIME_HIGH0), .clk(CLK), .clr(reset_encendido));
  Register #(.width(32)) u_WDTWPROTECT (.D(xor6), .en(esc_0A8), .Q(qx7), .clk(CLK), .clr(reset_encendido));
  Register #(.width(32)) u_WDTCONFIG0 (.D(xor10), .en(and9), .Q(qx11), .clk(CLK), .clr(reset_encendido));
  Register #(.width(32)) u_WDTCONFIG1 (.D(xor13), .en(and12), .Q(qx14), .clk(CLK), .clr(reset_encendido));
  Register #(.width(32)) u_WDTCONFIG2 (.D(xor16), .en(and15), .Q(qx17), .clk(CLK), .clr(reset_encendido));
  Register #(.width(32)) u_WDTCONFIG3 (.D(xor19), .en(and18), .Q(qx20), .clk(CLK), .clr(reset_encendido));
  Register #(.width(32)) u_WDTCONFIG4 (.D(xor22), .en(and21), .Q(qx23), .clk(CLK), .clr(reset_encendido));
  Register #(.width(32)) u_INT_RAW (.D(and34), .en(1'b1), .Q(INT_raw), .clk(CLK), .clr(reset_encendido));
  Register #(.width(32)) u_INT_ENA (.D(and35), .en(esc_040), .Q(INT_ENA), .clk(CLK), .clr(reset_encendido));
  Register #(.width(6)) u_RESET_CAUSE (.D(xor46), .en(or45), .Q(qx47), .clk(CLK), .clr(reset_encendido));
  Register #(.width(2)) RST_SIS_2 (.D(mux50), .en(or53), .Q(cuenta_reset_sis), .clk(CLK), .clr(reset_encendido));
  Register #(.width(2)) RST_CPU_2 (.D(mux55), .en(or58), .Q(cuenta_reset_cpu), .clk(CLK), .clr(reset_encendido));
  assign rep63 = {{9{SEL}}, SEL};  // Bit_Extender bit_extender_1
  and and_1 (and64, SEL, WE);
  and and_2 (escribe, WE, SEL);
  and and_3 (lee, RE, SEL);
  ROM #(.addrWidth(10), .dataWidth(1)) u_REGISTROS_EXISTE (.addr(dir_registro), .data(registros_existe));
  ROM #(.addrWidth(10), .dataWidth(32)) u_REGISTROS_VALOR_RESET (.addr(dir_registro), .data(registros_valor_reset));
  ROM #(.addrWidth(10), .dataWidth(32)) u_REGISTROS_BITS_RW (.addr(dir_registro), .data(registros_bits_rw));
  RAM #(.addrWidth(10), .dataWidth(32), .enables("byte"), .trigger("rising"), .asyncread("true"), .databus("bibus"), .clearpin("true")) REGISTROS (
    .addr(dir_registro), .we(and68), .oe(1'b1), .clk(CLK), .din(registros_a_guardar),
    .dout(registros_guardado), .clr(reset_encendido));
  assign zx5 = {{16{1'b0}}, TIME_HIGH0};  // Bit_Extender bit_extender_2
  assign WDTWPROTECT = qx7 ^ 32'h50d83aa1;  // XOR_Gate xor_1, 32 bits wide
  assign WDTCONFIG0 = qx11 ^ 32'h13214;  // XOR_Gate xor_2, 32 bits wide
  assign WDTCONFIG1 = qx14 ^ 32'h30d40;  // XOR_Gate xor_3, 32 bits wide
  assign WDTCONFIG2 = qx17 ^ 32'h13880;  // XOR_Gate xor_4, 32 bits wide
  assign WDTCONFIG3 = qx20 ^ 32'hfff;  // XOR_Gate xor_5, 32 bits wide
  assign WDTCONFIG4 = qx23 ^ 32'hfff;  // XOR_Gate xor_6, 32 bits wide
  assign INT_st = INT_raw & INT_ENA;  // AND_Gate and_4, 32 bits wide
  assign RESET_CAUSE = qx47 ^ 6'b000001;  // XOR_Gate xor_7, 6 bits wide
  assign dir_registro = A & rep63;  // AND_Gate and_5, 10 bits wide
  assign rep65 = {{31{and64}}, and64};  // Bit_Extender bit_extender_3
  not not_1 (reset_encendido, chip_en_pullup);
  Adder #(.width(32)) adder_1 (.a(rtc_tiempo_lo), .b(32'h1), .out(rtc_mas1), .cout(co3));  // open: cin
  Adder #(.width(2)) adder_2 (.a(cuenta_reset_sis), .b(2'b11), .out(sum49));  // open: cin, cout
  Comparator #(.width(2), .mode("unsigned")) comparator_1 (.a(cuenta_reset_sis), .b(2'b00), .eq(eq51));  // open: gt, lt
  Adder #(.width(2)) adder_3 (.a(cuenta_reset_cpu), .b(2'b11), .out(sum54));  // open: cin, cout
  Comparator #(.width(2), .mode("unsigned")) comparator_2 (.a(cuenta_reset_cpu), .b(2'b00), .eq(eq56));  // open: gt, lt
  Comparator #(.width(2), .mode("unsigned")) comparator_3 (.a(cuenta_reset_sis), .b(2'b00), .eq(eq59));  // open: gt, lt
  Comparator #(.width(2), .mode("unsigned")) comparator_4 (.a(cuenta_reset_cpu), .b(2'b00), .eq(eq61));  // open: gt, lt
  and and_6 (registros_acceso, SEL, registros_existe);
  assign registros_reset_rw = registros_valor_reset & registros_bits_rw;  // AND_Gate and_7, 32 bits wide
  assign not66 = ~registros_bits_rw;  // NOT_Gate not_2, 32 bits wide
  Comparator #(.width(32), .mode("unsigned")) comparator_5 (
    .a(WDTWPROTECT), .b(32'h50d83aa1), .eq(rwdt_desbloqueado));  // open: gt, lt
  Comparator #(.width(32), .mode("unsigned")) comparator_6 (.a(INT_st), .b({32{1'b0}}), .eq(eq36));  // open: gt, lt
  assign zx48 = {{26{1'b0}}, RESET_CAUSE};  // Bit_Extender bit_extender_4
  not not_3 (not52, eq51);
  not not_4 (not57, eq56);
  not not_5 (not60, eq59);
  not not_6 (not62, eq61);
  assign dato_escrito = WD & rep65;  // AND_Gate and_8, 32 bits wide
  Adder #(.width(16)) adder_4 (.a(rtc_tiempo_hi), .b({16{1'b0}}), .out(rtc_mas1_hi), .cin(co3));  // open: cout
  assign registros_bits_fijos = registros_valor_reset & not66;  // AND_Gate and_9, 32 bits wide
  and and_10 (and68, escribe, registros_acceso);
  assign xor69 = registros_guardado ^ registros_reset_rw;  // XOR_Gate xor_8, 32 bits wide
  assign rep70 = {{31{registros_acceso}}, registros_acceso};  // Bit_Extender bit_extender_5
  Decoder #(.select(5), .enable("false")) decoder_1 (
    .out0(pag_0), .out1(pag_1), .out2(pag_2), .out3(pag_3), .out4(pag_4), .out5(pag_5), .out6(pag_6),
    .out7(pag_7), .out8(pag_8), .out9(pag_9), .out10(pag_10), .out11(pag_11), .out12(pag_12), .out13(pag_13),
    .out14(pag_14), .out15(pag_15), .out16(pag_16), .out17(pag_17), .out18(pag_18), .out19(pag_19),
    .out20(pag_20), .out21(pag_21), .out22(pag_22), .out23(pag_23), .out24(pag_24), .out25(pag_25),
    .out26(pag_26), .out27(pag_27), .out28(pag_28), .out29(pag_29), .out30(pag_30), .out31(pag_31),
    .sel(dir_registro[9:5]));
  Decoder #(.select(5), .enable("false")) decoder_2 (
    .out0(lin_0), .out1(lin_1), .out2(lin_2), .out3(lin_3), .out4(lin_4), .out5(lin_5), .out6(lin_6),
    .out7(lin_7), .out8(lin_8), .out9(lin_9), .out10(lin_10), .out11(lin_11), .out12(lin_12), .out13(lin_13),
    .out14(lin_14), .out15(lin_15), .out16(lin_16), .out17(lin_17), .out18(lin_18), .out19(lin_19),
    .out20(lin_20), .out21(lin_21), .out22(lin_22), .out23(lin_23), .out24(lin_24), .out25(lin_25),
    .out26(lin_26), .out27(lin_27), .out28(lin_28), .out29(lin_29), .out30(lin_30), .out31(lin_31),
    .sel(dir_registro[4:0]));
  assign xor6 = dato_escrito ^ 32'h50d83aa1;  // XOR_Gate xor_9, 32 bits wide
  assign and8 = dato_escrito & {32{1'b1}};  // AND_Gate and_11, 32 bits wide
  assign xor13 = dato_escrito ^ 32'h30d40;  // XOR_Gate xor_10, 32 bits wide
  assign xor16 = dato_escrito ^ 32'h13880;  // XOR_Gate xor_11, 32 bits wide
  assign xor19 = dato_escrito ^ 32'hfff;  // XOR_Gate xor_12, 32 bits wide
  assign xor22 = dato_escrito ^ 32'hfff;  // XOR_Gate xor_13, 32 bits wide
  assign and35 = dato_escrito & 32'h8;  // AND_Gate and_12, 32 bits wide
  not not_7 (IRQ, eq36);
  or or_1 (RST_SIS, reset_encendido, not60);
  assign and67 = dato_escrito & registros_bits_rw;  // AND_Gate and_13, 32 bits wide
  assign registros_valor = xor69 | registros_bits_fijos;  // OR_Gate or_2, 32 bits wide
  and and_14 (r000, SEL, pag_0, lin_0);
  and and_15 (r00C, SEL, pag_0, lin_3);
  and and_16 (r090, SEL, pag_1, lin_4);
  and and_17 (r094, SEL, pag_1, lin_5);
  and and_18 (r098, SEL, pag_1, lin_6);
  and and_19 (r09C, SEL, pag_1, lin_7);
  and and_20 (r0A0, SEL, pag_1, lin_8);
  and and_21 (r0A4, SEL, pag_1, lin_9);
  and and_22 (r010, SEL, pag_0, lin_4);
  and and_23 (r014, SEL, pag_0, lin_5);
  and and_24 (r0A8, SEL, pag_1, lin_10);
  assign xor10 = and8 ^ 32'h13214;  // XOR_Gate xor_14, 32 bits wide
  and and_25 (r04C, SEL, pag_0, lin_19);
  and and_26 (r040, SEL, pag_0, lin_16);
  or or_3 (RST_CPU, RST_SIS, not62);
  assign and71 = registros_valor & rep70;  // AND_Gate and_27, 32 bits wide
  and and_28 (r044, SEL, pag_0, lin_17);
  and and_29 (r048, SEL, pag_0, lin_18);
  and and_30 (r038, SEL, pag_0, lin_14);
  Multiplexer #(.select(1), .width(2), .enable("false")) multiplexer_1 (
    .in0(WDTCONFIG0[29:28]), .in1(2'b11), .out(cat29[1:0]), .sel(WDTCONFIG0[30]));
  Multiplexer #(.select(1), .width(2), .enable("false")) multiplexer_2 (
    .in0(WDTCONFIG0[26:25]), .in1(2'b11), .out(cat29[3:2]), .sel(WDTCONFIG0[27]));
  Multiplexer #(.select(1), .width(2), .enable("false")) multiplexer_3 (
    .in0(WDTCONFIG0[23:22]), .in1(2'b11), .out(cat29[5:4]), .sel(WDTCONFIG0[24]));
  Multiplexer #(.select(1), .width(2), .enable("false")) multiplexer_4 (
    .in0(WDTCONFIG0[20:19]), .in1(2'b11), .out(cat29[7:6]), .sel(WDTCONFIG0[21]));
  assign registros_a_guardar = and67 ^ registros_reset_rw;  // XOR_Gate xor_15, 32 bits wide
  and and_31 (esc_000, escribe, r000);
  and and_32 (esc_00C, escribe, r00C);
  and and_33 (esc_0A8, escribe, r0A8);
  and and_34 (esc_090, escribe, r090);
  and and_35 (esc_094, escribe, r094);
  and and_36 (esc_098, escribe, r098);
  and and_37 (esc_09C, escribe, r09C);
  and and_38 (esc_0A0, escribe, r0A0);
  and and_39 (esc_0A4, escribe, r0A4);
  and and_40 (esc_04C, escribe, r04C);
  and and_41 (esc_040, escribe, r040);
  assign rep72 = {{31{r010}}, r010};  // Bit_Extender bit_extender_6
  assign rep74 = {{31{r014}}, r014};  // Bit_Extender bit_extender_7
  assign rep76 = {{31{r0A8}}, r0A8};  // Bit_Extender bit_extender_8
  assign rep78 = {{31{r090}}, r090};  // Bit_Extender bit_extender_9
  assign rep80 = {{31{r094}}, r094};  // Bit_Extender bit_extender_10
  assign rep82 = {{31{r098}}, r098};  // Bit_Extender bit_extender_11
  assign rep84 = {{31{r09C}}, r09C};  // Bit_Extender bit_extender_12
  assign rep86 = {{31{r0A0}}, r0A0};  // Bit_Extender bit_extender_13
  assign rep88 = {{31{r040}}, r040};  // Bit_Extender bit_extender_14
  assign rep90 = {{31{r044}}, r044};  // Bit_Extender bit_extender_15
  assign rep92 = {{31{r048}}, r048};  // Bit_Extender bit_extender_16
  assign rep94 = {{31{r038}}, r038};  // Bit_Extender bit_extender_17
  assign and75 = zx5 & rep74;  // AND_Gate and_42, 32 bits wide
  assign and89 = INT_ENA & rep88;  // AND_Gate and_43, 32 bits wide
  assign and91 = INT_raw & rep90;  // AND_Gate and_44, 32 bits wide
  assign and93 = INT_st & rep92;  // AND_Gate and_45, 32 bits wide
  assign and95 = zx48 & rep94;  // AND_Gate and_46, 32 bits wide
  and and_47 (and1, esc_000, dato_escrito[31]);
  and and_48 (and2, esc_000, dato_escrito[5]);
  and and_49 (and4, esc_00C, dato_escrito[31]);
  and and_50 (and9, esc_090, rwdt_desbloqueado);
  and and_51 (and12, esc_094, rwdt_desbloqueado);
  and and_52 (and15, esc_098, rwdt_desbloqueado);
  and and_53 (and18, esc_09C, rwdt_desbloqueado);
  and and_54 (and21, esc_0A0, rwdt_desbloqueado);
  and and_55 (and24, esc_0A4, dato_escrito[31]);
  assign rep30 = {{31{esc_04C}}, esc_04C};  // Bit_Extender bit_extender_18
  assign and73 = TIME_LOW0 & rep72;  // AND_Gate and_56, 32 bits wide
  assign and77 = WDTWPROTECT & rep76;  // AND_Gate and_57, 32 bits wide
  assign and79 = WDTCONFIG0 & rep78;  // AND_Gate and_58, 32 bits wide
  assign and81 = WDTCONFIG1 & rep80;  // AND_Gate and_59, 32 bits wide
  assign and83 = WDTCONFIG2 & rep82;  // AND_Gate and_60, 32 bits wide
  assign and85 = WDTCONFIG3 & rep84;  // AND_Gate and_61, 32 bits wide
  assign and87 = WDTCONFIG4 & rep86;  // AND_Gate and_62, 32 bits wide
  assign INT_clr = dato_escrito & rep30;  // AND_Gate and_63, 32 bits wide
  assign RD = and73 | and75 | and77 | and79 | and81 | and83 | and85 | and87 | and89 | and91 | and93 | and95 | and71;  // OR_Gate or_4, 32 bits wide
  and and_64 (rwdt_alimenta, and24, rwdt_desbloqueado);
  assign not31 = ~INT_clr;  // NOT_Gate not_8, 32 bits wide
  WatchdogEtapas RWDT (
    .CLK(CLK), .RST(reset_encendido), .EN(WDTCONFIG0[31]), .FEED(rwdt_alimenta), .PRESCALE(16'h1),
    .STG(cat29), .HOLD0(WDTCONFIG1), .HOLD1(WDTCONFIG2), .HOLD2(WDTCONFIG3), .HOLD3(WDTCONFIG4),
    .INT(INT_eventos[3]), .RESET_CPU(rwdt_reset_cpu), .RESET_SIS(rwdt_reset_sis));
  Multiplexer #(.select(1), .width(6), .enable("false")) multiplexer_5 (
    .in0(6'b000011), .in1(6'b010000), .out(mux37), .sel(rwdt_reset_sis));
  Multiplexer #(.select(1), .width(6), .enable("false")) multiplexer_6 (
    .in0(6'b001100), .in1(6'b001101), .out(mux41), .sel(rwdt_reset_cpu));
  assign and32 = INT_raw & not31;  // AND_Gate and_65, 32 bits wide
  or or_5 (pide_reset_sistema, and1, TG0_RESET_SIS, TG1_RESET_SIS, rwdt_reset_sis);
  or or_6 (pide_reset_cpu, and2, TG0_RESET_CPU, TG1_RESET_CPU, rwdt_reset_cpu);
  assign or33 = and32 | {{28{1'b0}}, INT_eventos[3], 3'b000};  // OR_Gate or_7, 32 bits wide
  Multiplexer #(.select(1), .width(6), .enable("false")) multiplexer_7 (
    .in0(mux37), .in1(6'b001000), .out(mux38), .sel(TG1_RESET_SIS));
  Multiplexer #(.select(1), .width(6), .enable("false")) multiplexer_8 (
    .in0(mux41), .in1(6'b010001), .out(mux42), .sel(TG1_RESET_CPU));
  Multiplexer #(.select(1), .width(2), .enable("false")) multiplexer_9 (
    .in0(sum49), .in1(2'b11), .out(mux50), .sel(pide_reset_sistema));
  Multiplexer #(.select(1), .width(2), .enable("false")) multiplexer_10 (
    .in0(sum54), .in1(2'b11), .out(mux55), .sel(pide_reset_cpu));
  or or_8 (or45, pide_reset_sistema, pide_reset_cpu);
  or or_9 (or53, pide_reset_sistema, not52);
  or or_10 (or58, pide_reset_cpu, not57);
  assign and34 = or33 & 32'h8;  // AND_Gate and_66, 32 bits wide
  Multiplexer #(.select(1), .width(6), .enable("false")) multiplexer_11 (
    .in0(mux38), .in1(6'b000111), .out(mux39), .sel(TG0_RESET_SIS));
  Multiplexer #(.select(1), .width(6), .enable("false")) multiplexer_12 (
    .in0(mux42), .in1(6'b001011), .out(mux43), .sel(TG0_RESET_CPU));
  Multiplexer #(.select(1), .width(6), .enable("false")) multiplexer_13 (
    .in0(mux39), .in1(6'b000011), .out(mux40), .sel(and1));
  Multiplexer #(.select(1), .width(6), .enable("false")) multiplexer_14 (
    .in0(mux43), .in1(6'b001100), .out(mux44), .sel(and2));
  Multiplexer #(.select(1), .width(6), .enable("false")) multiplexer_15 (
    .in0(mux44), .in1(mux40), .out(causa_nueva), .sel(pide_reset_sistema));
  assign xor46 = causa_nueva ^ 6'b000001;  // XOR_Gate xor_16, 6 bits wide

  // Other names for the same wires on the sheet: mux25[1:0] = cat29[1:0]; mux26[1:0] = cat29[3:2];
  //   mux27[1:0] = cat29[5:4]; mux28[1:0] = cat29[7:6]; dato_escrito_5 = dato_escrito[5];
  //   dato_escrito_31 = dato_escrito[31]; dir_registro_4_0[4:0] = dir_registro[4:0];
  //   dir_registro_9_5[4:0] = dir_registro[9:5]; rwdt_int = INT_eventos[3]; INT_irq = IRQ; or96[31:0] = RD;
  //   reset_cpu = RST_CPU; reset_sistema = RST_SIS; WDTCONFIG0_21_19[2:0] = WDTCONFIG0[21:19];
  //   WDTCONFIG0_21_19_1_0[1:0] = WDTCONFIG0[20:19]; WDTCONFIG0_21_19_2 = WDTCONFIG0[21];
  //   WDTCONFIG0_24_22[2:0] = WDTCONFIG0[24:22]; WDTCONFIG0_24_22_1_0[1:0] = WDTCONFIG0[23:22];
  //   WDTCONFIG0_24_22_2 = WDTCONFIG0[24]; WDTCONFIG0_27_25[2:0] = WDTCONFIG0[27:25];
  //   WDTCONFIG0_27_25_1_0[1:0] = WDTCONFIG0[26:25]; WDTCONFIG0_27_25_2 = WDTCONFIG0[27];
  //   WDTCONFIG0_30_28[2:0] = WDTCONFIG0[30:28]; WDTCONFIG0_30_28_1_0[1:0] = WDTCONFIG0[29:28];
  //   WDTCONFIG0_30_28_2 = WDTCONFIG0[30]; WDTCONFIG0_31 = WDTCONFIG0[31]

  // Notes on the sheet:
  //   contents of REGISTROS_EXISTE (hex, n*v repeats v):
  //   4*1 0 0 10*1 4*0 16*1 7*0 7*1 0 0 1 1 1 0 0 1 1 1 0 1 0 1 0 0 1 1 1 58*0 1
  //   contents of REGISTROS_VALOR_RESET (hex, n*v repeats v):
  //   1c00a000 6*0 28140403 1000000 a080a08 10200a08 8000 a080000 c40000 3000 60000 8*0 66c80 0 0 0
  //   11583218 400000 ab0be0a 10800 a0000000 0 555010 aa805080 7*0 4b00000 8f1d312a 9*0 43ff0010 0 0 0
  //   ff00000 4*0 c800 0 0 a0d00000 7 59*0 2007270
  //   contents of REGISTROS_BITS_RW (hex, n*v repeats v):
  //   7ff3ffcf ffffffff ffff 38000000 0 0 e0400000 ffffffff ff000000 ffffffff ffffffff ff00 ffff0000
  //   dfdc0000 30c3000 ffff8000 4*0 4*ffffffff c08fffff 80000000 fffff000 e0000000 fffff7fe ffc00000
  //   fefffeff 3fffdff f03fc080 200000 f87ff81f ffc0f980 7*0 cffe0000 ffffffff fff00000 4*ffffffff 0 0 3f
  //   ffffffff 5ffffff0 0 0 ffffffff ffffffff 40000 0 1 0 ffffff00 0 0 fffc0000 7 ffffffc0 58*0 fffffff
endmodule

module SYSTEM (
  input  CLK,
  input  RST,
  input  SEL,
  input  [9:0] A,
  input  [31:0] WD,
  input  WE,
  input  RE,
  output FROM_CPU0,
  output FROM_CPU1,
  output FROM_CPU2,
  output FROM_CPU3,
  output CLKEN_UART0,
  output RST_UART0,
  output CLKEN_UART1,
  output RST_UART1,
  output CLKEN_SPI2,
  output RST_SPI2,
  output CLKEN_I2C,
  output RST_I2C,
  output CLKEN_LEDC,
  output RST_LEDC,
  output CLKEN_TIMG0,
  output RST_TIMG0,
  output CLKEN_TIMG1,
  output RST_TIMG1,
  output CLKEN_SYSTIMER,
  output RST_SYSTIMER,
  output [31:0] RD
);

  wire and13, and17, DESDE_CPU0_escribe, esc_010, esc_018, escribe, lee, lin_0, lin_1, lin_2, lin_3, lin_4,
       lin_5, lin_6, lin_7, lin_8, lin_9, lin_10, lin_11, lin_12, lin_13, lin_14, lin_15, lin_16, lin_17,
       lin_18, lin_19, lin_20, lin_21, lin_22, lin_23, lin_24, lin_25, lin_26, lin_27, lin_28, lin_29,
       lin_30, lin_31, pag_0, pag_1, pag_2, pag_3, pag_4, pag_5, pag_6, pag_7, pag_8, pag_9, pag_10, pag_11,
       pag_12, pag_13, pag_14, pag_15, pag_16, pag_17, pag_18, pag_19, pag_20, pag_21, pag_22, pag_23,
       pag_24, pag_25, pag_26, pag_27, pag_28, pag_29, pag_30, pag_31, r02C, r010, r018, r028, r030, r034,
       registros_acceso, registros_existe;
  wire [3:0] and2, and3, DESDE_CPU0_mascara, DESDE_CPU0_sig, not1;
  wire [7:0] and5, and6, and10, and11, not4, not9, qx8, RELOJES_ON0_sig, RESETS_ON0, RESETS_ON0_sig, xor7;
  wire [9:0] dir_registro, rep12;
  wire [31:0] and16, dato_escrito, not15, registros_a_guardar, registros_bits_fijos, registros_bits_rw,
       registros_guardado, registros_reset_rw, registros_valor, registros_valor_reset, rep14, rep19, xor18;

  assign rep12 = {{9{SEL}}, SEL};  // Bit_Extender bit_extender_1
  and and_1 (and13, SEL, WE);
  and and_2 (escribe, WE, SEL);
  and and_3 (lee, RE, SEL);
  ROM #(.addrWidth(10), .dataWidth(1)) u_REGISTROS_EXISTE (.addr(dir_registro), .data(registros_existe));
  ROM #(.addrWidth(10), .dataWidth(32)) u_REGISTROS_VALOR_RESET (.addr(dir_registro), .data(registros_valor_reset));
  ROM #(.addrWidth(10), .dataWidth(32)) u_REGISTROS_BITS_RW (.addr(dir_registro), .data(registros_bits_rw));
  Register #(.width(4)) DESDE_CPU0 (
    .D(DESDE_CPU0_sig), .en(DESDE_CPU0_escribe), .Q({FROM_CPU3, FROM_CPU2, FROM_CPU1, FROM_CPU0}), .clk(CLK),
    .clr(RST));
  Register #(.width(8)) RELOJES_ON0 (.D(xor7), .en(esc_010), .Q(qx8), .clk(CLK), .clr(RST));
  Register #(.width(8)) u_RESETS_ON0 (.D(RESETS_ON0_sig), .en(esc_018), .Q(RESETS_ON0), .clk(CLK), .clr(RST));
  RAM #(.addrWidth(10), .dataWidth(32), .enables("byte"), .trigger("rising"), .asyncread("true"), .databus("bibus"), .clearpin("true")) REGISTROS (
    .addr(dir_registro), .we(and17), .oe(1'b1), .clk(CLK), .din(registros_a_guardar),
    .dout(registros_guardado), .clr(RST));
  assign dir_registro = A & rep12;  // AND_Gate and_4, 10 bits wide
  assign {CLKEN_SYSTIMER, CLKEN_TIMG1, CLKEN_TIMG0, CLKEN_LEDC, CLKEN_I2C, CLKEN_SPI2, CLKEN_UART1, CLKEN_UART0} = qx8 ^ 8'he7;  // XOR_Gate xor_1, 8 bits wide
  assign rep14 = {{31{and13}}, and13};  // Bit_Extender bit_extender_2
  and and_5 (registros_acceso, SEL, registros_existe);
  assign not15 = ~registros_bits_rw;  // NOT_Gate not_1, 32 bits wide
  assign registros_reset_rw = registros_valor_reset & registros_bits_rw;  // AND_Gate and_6, 32 bits wide
  assign dato_escrito = WD & rep14;  // AND_Gate and_7, 32 bits wide
  or or_1 (RST_UART0, RST, RESETS_ON0[0]);
  or or_2 (RST_UART1, RST, RESETS_ON0[1]);
  or or_3 (RST_SPI2, RST, RESETS_ON0[2]);
  or or_4 (RST_I2C, RST, RESETS_ON0[3]);
  or or_5 (RST_LEDC, RST, RESETS_ON0[4]);
  or or_6 (RST_TIMG0, RST, RESETS_ON0[5]);
  or or_7 (RST_TIMG1, RST, RESETS_ON0[6]);
  or or_8 (RST_SYSTIMER, RST, RESETS_ON0[7]);
  and and_8 (and17, escribe, registros_acceso);
  assign xor18 = registros_guardado ^ registros_reset_rw;  // XOR_Gate xor_2, 32 bits wide
  assign rep19 = {{31{registros_acceso}}, registros_acceso};  // Bit_Extender bit_extender_3
  assign registros_bits_fijos = registros_valor_reset & not15;  // AND_Gate and_9, 32 bits wide
  Decoder #(.select(5), .enable("false")) decoder_1 (
    .out0(pag_0), .out1(pag_1), .out2(pag_2), .out3(pag_3), .out4(pag_4), .out5(pag_5), .out6(pag_6),
    .out7(pag_7), .out8(pag_8), .out9(pag_9), .out10(pag_10), .out11(pag_11), .out12(pag_12), .out13(pag_13),
    .out14(pag_14), .out15(pag_15), .out16(pag_16), .out17(pag_17), .out18(pag_18), .out19(pag_19),
    .out20(pag_20), .out21(pag_21), .out22(pag_22), .out23(pag_23), .out24(pag_24), .out25(pag_25),
    .out26(pag_26), .out27(pag_27), .out28(pag_28), .out29(pag_29), .out30(pag_30), .out31(pag_31),
    .sel(dir_registro[9:5]));
  Decoder #(.select(5), .enable("false")) decoder_2 (
    .out0(lin_0), .out1(lin_1), .out2(lin_2), .out3(lin_3), .out4(lin_4), .out5(lin_5), .out6(lin_6),
    .out7(lin_7), .out8(lin_8), .out9(lin_9), .out10(lin_10), .out11(lin_11), .out12(lin_12), .out13(lin_13),
    .out14(lin_14), .out15(lin_15), .out16(lin_16), .out17(lin_17), .out18(lin_18), .out19(lin_19),
    .out20(lin_20), .out21(lin_21), .out22(lin_22), .out23(lin_23), .out24(lin_24), .out25(lin_25),
    .out26(lin_26), .out27(lin_27), .out28(lin_28), .out29(lin_29), .out30(lin_30), .out31(lin_31),
    .sel(dir_registro[4:0]));
  assign and16 = dato_escrito & registros_bits_rw;  // AND_Gate and_10, 32 bits wide
  assign registros_valor = xor18 | registros_bits_fijos;  // OR_Gate or_9, 32 bits wide
  and and_11 (r028, SEL, pag_0, lin_10);
  and and_12 (r02C, SEL, pag_0, lin_11);
  and and_13 (r030, SEL, pag_0, lin_12);
  and and_14 (r034, SEL, pag_0, lin_13);
  and and_15 (r010, SEL, pag_0, lin_4);
  and and_16 (r018, SEL, pag_0, lin_6);
  assign registros_a_guardar = and16 ^ registros_reset_rw;  // XOR_Gate xor_3, 32 bits wide
  assign RD = registros_valor & rep19;  // AND_Gate and_17, 32 bits wide
  and and_18 (DESDE_CPU0_mascara[0], escribe, r028);
  and and_19 (DESDE_CPU0_mascara[1], escribe, r02C);
  and and_20 (DESDE_CPU0_mascara[2], escribe, r030);
  and and_21 (DESDE_CPU0_mascara[3], escribe, r034);
  and and_22 (esc_010, escribe, r010);
  and and_23 (esc_018, escribe, r018);
  or or_10 (DESDE_CPU0_escribe, DESDE_CPU0_mascara[0], DESDE_CPU0_mascara[1], DESDE_CPU0_mascara[2], DESDE_CPU0_mascara[3]);
  assign not1 = ~DESDE_CPU0_mascara;  // NOT_Gate not_2, 4 bits wide
  assign and3 = {4{dato_escrito[0]}} & DESDE_CPU0_mascara;  // AND_Gate and_24, 4 bits wide
  assign not4 = ~{8{esc_010}};  // NOT_Gate not_3, 8 bits wide
  assign and6 = {dato_escrito[29], dato_escrito[15], dato_escrito[13], dato_escrito[11], dato_escrito[7:5], dato_escrito[2]} & {8{esc_010}};  // AND_Gate and_25, 8 bits wide
  assign not9 = ~{8{esc_018}};  // NOT_Gate not_4, 8 bits wide
  assign and11 = {dato_escrito[29], dato_escrito[15], dato_escrito[13], dato_escrito[11], dato_escrito[7:5], dato_escrito[2]} & {8{esc_018}};  // AND_Gate and_26, 8 bits wide
  assign and2 = {FROM_CPU3, FROM_CPU2, FROM_CPU1, FROM_CPU0} & not1;  // AND_Gate and_27, 4 bits wide
  assign and5 = {CLKEN_SYSTIMER, CLKEN_TIMG1, CLKEN_TIMG0, CLKEN_LEDC, CLKEN_I2C, CLKEN_SPI2, CLKEN_UART1, CLKEN_UART0} & not4;  // AND_Gate and_28, 8 bits wide
  assign and10 = RESETS_ON0 & not9;  // AND_Gate and_29, 8 bits wide
  assign DESDE_CPU0_sig = and2 | and3;  // OR_Gate or_11, 4 bits wide
  assign RELOJES_ON0_sig = and5 | and6;  // OR_Gate or_12, 8 bits wide
  assign RESETS_ON0_sig = and10 | and11;  // OR_Gate or_13, 8 bits wide
  assign xor7 = RELOJES_ON0_sig ^ 8'he7;  // XOR_Gate xor_4, 8 bits wide

  // Other names for the same wires on the sheet: RELOJES_ON0[7:0] = {CLKEN_SYSTIMER, CLKEN_TIMG1, CLKEN_TIMG0, CLKEN_LEDC, CLKEN_I2C, CLKEN_SPI2, CLKEN_UART1, CLKEN_UART0};
  //   RELOJES_ON0_3 = CLKEN_I2C; RELOJES_ON0_4 = CLKEN_LEDC; RELOJES_ON0_2 = CLKEN_SPI2;
  //   RELOJES_ON0_7 = CLKEN_SYSTIMER; RELOJES_ON0_5 = CLKEN_TIMG0; RELOJES_ON0_6 = CLKEN_TIMG1;
  //   RELOJES_ON0_0 = CLKEN_UART0; RELOJES_ON0_1 = CLKEN_UART1; esc_028 = DESDE_CPU0_mascara[0];
  //   esc_02C = DESDE_CPU0_mascara[1]; esc_030 = DESDE_CPU0_mascara[2]; esc_034 = DESDE_CPU0_mascara[3];
  //   dato_escrito_0 = dato_escrito[0]; DESDE_CPU0_nuevo[3:0] = {4{dato_escrito[0]}};
  //   dir_registro_4_0[4:0] = dir_registro[4:0]; dir_registro_9_5[4:0] = dir_registro[9:5];
  //   DESDE_CPU0[3:0] = {FROM_CPU3, FROM_CPU2, FROM_CPU1, FROM_CPU0}; DESDE_CPU0_0 = FROM_CPU0;
  //   DESDE_CPU0_1 = FROM_CPU1; DESDE_CPU0_2 = FROM_CPU2; DESDE_CPU0_3 = FROM_CPU3; and20[31:0] = RD;
  //   RELOJES_ON0_escribe = esc_010; RELOJES_ON0_mascara[7:0] = {8{esc_010}}; RESETS_ON0_0 = RESETS_ON0[0];
  //   RESETS_ON0_1 = RESETS_ON0[1]; RESETS_ON0_2 = RESETS_ON0[2]; RESETS_ON0_3 = RESETS_ON0[3];
  //   RESETS_ON0_4 = RESETS_ON0[4]; RESETS_ON0_5 = RESETS_ON0[5]; RESETS_ON0_6 = RESETS_ON0[6];
  //   RESETS_ON0_7 = RESETS_ON0[7]; RESETS_ON0_escribe = esc_018; RESETS_ON0_mascara[7:0] = {8{esc_018}};
  //   dato_escrito_2 = dato_escrito[2];
  //   RELOJES_ON0_nuevo[7:0] = {dato_escrito[29], dato_escrito[15], dato_escrito[13], dato_escrito[11], dato_escrito[7:5], dato_escrito[2]};
  //   RESETS_ON0_nuevo[7:0] = {dato_escrito[29], dato_escrito[15], dato_escrito[13], dato_escrito[11], dato_escrito[7:5], dato_escrito[2]};
  //   dato_escrito_5 = dato_escrito[5]; dato_escrito_6 = dato_escrito[6]; dato_escrito_7 = dato_escrito[7];
  //   dato_escrito_11 = dato_escrito[11]; dato_escrito_13 = dato_escrito[13]; dato_escrito_15 = dato_escrito[15];
  //   dato_escrito_29 = dato_escrito[29]; reset_I2C = RST_I2C; reset_LEDC = RST_LEDC; reset_SPI2 = RST_SPI2;
  //   reset_SYSTIMER = RST_SYSTIMER; reset_TIMG0 = RST_TIMG0; reset_TIMG1 = RST_TIMG1; reset_UART0 = RST_UART0;
  //   reset_UART1 = RST_UART1

  // Notes on the sheet:
  //   contents of REGISTROS_EXISTE (hex, n*v repeats v):
  //   19*1 0 0 1 1 1000*0 1
  //   contents of REGISTROS_VALOR_RESET (hex, n*v repeats v):
  //   0 c0 c 1 f9c1e06f 0 0 1fe ff 2001001 4*0 1 1 5 0 7ff00000 0 0 1 28001 1000*0 2007150
  //   contents of REGISTROS_BITS_RW (hex, n*v repeats v):
  //   c0 c0 ff 1 ffffffef 5fe ffffffef 5fe fff 1fffffff 4*1 7 3 f f 7fffff00 0 0 1 fff 1000*0 fffffff
endmodule

module SYSCON (
  input  CLK,
  input  RST,
  input  SEL,
  input  [9:0] A,
  input  [31:0] WD,
  input  WE,
  input  RE,
  output [31:0] RD
);

  wire and2, and6, escribe, lee, lin_0, lin_1, lin_2, lin_3, lin_4, lin_5, lin_6, lin_7, lin_8, lin_9,
       lin_10, lin_11, lin_12, lin_13, lin_14, lin_15, lin_16, lin_17, lin_18, lin_19, lin_20, lin_21,
       lin_22, lin_23, lin_24, lin_25, lin_26, lin_27, lin_28, lin_29, lin_30, lin_31, pag_0, pag_1, pag_2,
       pag_3, pag_4, pag_5, pag_6, pag_7, pag_8, pag_9, pag_10, pag_11, pag_12, pag_13, pag_14, pag_15,
       pag_16, pag_17, pag_18, pag_19, pag_20, pag_21, pag_22, pag_23, pag_24, pag_25, pag_26, pag_27,
       pag_28, pag_29, pag_30, pag_31, r0B0, registros_acceso, registros_existe;
  wire [9:0] dir_registro, rep1;
  wire [31:0] aleatorio, and5, and9, and11, dato_escrito, not4, registros_a_guardar, registros_bits_fijos,
       registros_bits_rw, registros_guardado, registros_reset_rw, registros_valor, registros_valor_reset,
       rep3, rep8, rep10, xor7;

  // Random #(.width(32), .seed(0)) RNG: pin names not known; wires that end beside it: 1'b1, CLK, 1'b0
  assign rep1 = {{9{SEL}}, SEL};  // Bit_Extender bit_extender_1
  and and_1 (and2, SEL, WE);
  and and_2 (escribe, WE, SEL);
  and and_3 (lee, RE, SEL);
  ROM #(.addrWidth(10), .dataWidth(1)) u_REGISTROS_EXISTE (.addr(dir_registro), .data(registros_existe));
  ROM #(.addrWidth(10), .dataWidth(32)) u_REGISTROS_VALOR_RESET (.addr(dir_registro), .data(registros_valor_reset));
  ROM #(.addrWidth(10), .dataWidth(32)) u_REGISTROS_BITS_RW (.addr(dir_registro), .data(registros_bits_rw));
  RAM #(.addrWidth(10), .dataWidth(32), .enables("byte"), .trigger("rising"), .asyncread("true"), .databus("bibus"), .clearpin("true")) REGISTROS (
    .addr(dir_registro), .we(and6), .oe(1'b1), .clk(CLK), .din(registros_a_guardar),
    .dout(registros_guardado), .clr(RST));
  assign dir_registro = A & rep1;  // AND_Gate and_4, 10 bits wide
  assign rep3 = {{31{and2}}, and2};  // Bit_Extender bit_extender_2
  and and_5 (registros_acceso, SEL, registros_existe);
  assign not4 = ~registros_bits_rw;  // NOT_Gate not_1, 32 bits wide
  assign registros_reset_rw = registros_valor_reset & registros_bits_rw;  // AND_Gate and_6, 32 bits wide
  assign dato_escrito = WD & rep3;  // AND_Gate and_7, 32 bits wide
  and and_8 (and6, escribe, registros_acceso);
  assign xor7 = registros_guardado ^ registros_reset_rw;  // XOR_Gate xor_1, 32 bits wide
  assign rep8 = {{31{registros_acceso}}, registros_acceso};  // Bit_Extender bit_extender_3
  assign registros_bits_fijos = registros_valor_reset & not4;  // AND_Gate and_9, 32 bits wide
  Decoder #(.select(5), .enable("false")) decoder_1 (
    .out0(pag_0), .out1(pag_1), .out2(pag_2), .out3(pag_3), .out4(pag_4), .out5(pag_5), .out6(pag_6),
    .out7(pag_7), .out8(pag_8), .out9(pag_9), .out10(pag_10), .out11(pag_11), .out12(pag_12), .out13(pag_13),
    .out14(pag_14), .out15(pag_15), .out16(pag_16), .out17(pag_17), .out18(pag_18), .out19(pag_19),
    .out20(pag_20), .out21(pag_21), .out22(pag_22), .out23(pag_23), .out24(pag_24), .out25(pag_25),
    .out26(pag_26), .out27(pag_27), .out28(pag_28), .out29(pag_29), .out30(pag_30), .out31(pag_31),
    .sel(dir_registro[9:5]));
  Decoder #(.select(5), .enable("false")) decoder_2 (
    .out0(lin_0), .out1(lin_1), .out2(lin_2), .out3(lin_3), .out4(lin_4), .out5(lin_5), .out6(lin_6),
    .out7(lin_7), .out8(lin_8), .out9(lin_9), .out10(lin_10), .out11(lin_11), .out12(lin_12), .out13(lin_13),
    .out14(lin_14), .out15(lin_15), .out16(lin_16), .out17(lin_17), .out18(lin_18), .out19(lin_19),
    .out20(lin_20), .out21(lin_21), .out22(lin_22), .out23(lin_23), .out24(lin_24), .out25(lin_25),
    .out26(lin_26), .out27(lin_27), .out28(lin_28), .out29(lin_29), .out30(lin_30), .out31(lin_31),
    .sel(dir_registro[4:0]));
  assign and5 = dato_escrito & registros_bits_rw;  // AND_Gate and_10, 32 bits wide
  assign registros_valor = xor7 | registros_bits_fijos;  // OR_Gate or_1, 32 bits wide
  and and_11 (r0B0, SEL, pag_1, lin_12);
  assign registros_a_guardar = and5 ^ registros_reset_rw;  // XOR_Gate xor_2, 32 bits wide
  assign and9 = registros_valor & rep8;  // AND_Gate and_12, 32 bits wide
  assign rep10 = {{31{r0B0}}, r0B0};  // Bit_Extender bit_extender_4
  assign and11 = aleatorio & rep10;  // AND_Gate and_13, 32 bits wide
  assign RD = and11 | and9;  // OR_Gate or_2, 32 bits wide

  // Other names for the same wires on the sheet: dir_registro_4_0[4:0] = dir_registro[4:0];
  //   dir_registro_9_5[4:0] = dir_registro[9:5]; or12[31:0] = RD

  // Notes on the sheet:
  //   contents of REGISTROS_EXISTE (hex, n*v repeats v):
  //   9*1 0 12*1 17*0 1 0 1 1 1 211*0 1
  //   contents of REGISTROS_VALOR_RESET (hex, n*v repeats v):
  //   1 10727 7ff 0 0 fffce030 fffce030 0 0 0 4*3 0 400000 800000 c00000 4*400 17*0 15 0 3f 0 3f 211*0
  //   2007210
  //   contents of REGISTROS_BITS_RW (hex, n*v repeats v):
  //   1fff 1ffff 7ff 4*ffffffff ff 1 0 4*3 4*ffffffff 4*1fff 17*0 3f 0 3f 3f 3f 211*0 ffffffff
endmodule

module EFUSE (
  input  CLK,
  input  RST,
  input  SEL,
  input  [9:0] A,
  input  [31:0] WD,
  input  WE,
  input  RE,
  output [31:0] RD
);

  wire and2, escribe, lee, lin_0, lin_1, lin_2, lin_3, lin_4, lin_5, lin_6, lin_7, lin_8, lin_9, lin_10,
       lin_11, lin_12, lin_13, lin_14, lin_15, lin_16, lin_17, lin_18, lin_19, lin_20, lin_21, lin_22,
       lin_23, lin_24, lin_25, lin_26, lin_27, lin_28, lin_29, lin_30, lin_31, pag_0, pag_1, pag_2, pag_3,
       pag_4, pag_5, pag_6, pag_7, pag_8, pag_9, pag_10, pag_11, pag_12, pag_13, pag_14, pag_15, pag_16,
       pag_17, pag_18, pag_19, pag_20, pag_21, pag_22, pag_23, pag_24, pag_25, pag_26, pag_27, pag_28,
       pag_29, pag_30, pag_31, r9FC, r844, r848, r850;
  wire [9:0] dir_registro, rep1;
  wire [31:0] dato_escrito, mux4, mux5, mux6, mux7, rep3;

  assign rep1 = {{9{SEL}}, SEL};  // Bit_Extender bit_extender_1
  and and_1 (and2, SEL, WE);
  and and_2 (escribe, WE, SEL);
  and and_3 (lee, RE, SEL);
  assign dir_registro = A & rep1;  // AND_Gate and_4, 10 bits wide
  assign rep3 = {{31{and2}}, and2};  // Bit_Extender bit_extender_2
  assign dato_escrito = WD & rep3;  // AND_Gate and_5, 32 bits wide
  Decoder #(.select(5), .enable("false")) decoder_1 (
    .out0(pag_0), .out1(pag_1), .out2(pag_2), .out3(pag_3), .out4(pag_4), .out5(pag_5), .out6(pag_6),
    .out7(pag_7), .out8(pag_8), .out9(pag_9), .out10(pag_10), .out11(pag_11), .out12(pag_12), .out13(pag_13),
    .out14(pag_14), .out15(pag_15), .out16(pag_16), .out17(pag_17), .out18(pag_18), .out19(pag_19),
    .out20(pag_20), .out21(pag_21), .out22(pag_22), .out23(pag_23), .out24(pag_24), .out25(pag_25),
    .out26(pag_26), .out27(pag_27), .out28(pag_28), .out29(pag_29), .out30(pag_30), .out31(pag_31),
    .sel(dir_registro[9:5]));
  Decoder #(.select(5), .enable("false")) decoder_2 (
    .out0(lin_0), .out1(lin_1), .out2(lin_2), .out3(lin_3), .out4(lin_4), .out5(lin_5), .out6(lin_6),
    .out7(lin_7), .out8(lin_8), .out9(lin_9), .out10(lin_10), .out11(lin_11), .out12(lin_12), .out13(lin_13),
    .out14(lin_14), .out15(lin_15), .out16(lin_16), .out17(lin_17), .out18(lin_18), .out19(lin_19),
    .out20(lin_20), .out21(lin_21), .out22(lin_22), .out23(lin_23), .out24(lin_24), .out25(lin_25),
    .out26(lin_26), .out27(lin_27), .out28(lin_28), .out29(lin_29), .out30(lin_30), .out31(lin_31),
    .sel(dir_registro[4:0]));
  and and_6 (r844, SEL, pag_16, lin_17);
  and and_7 (r848, SEL, pag_16, lin_18);
  and and_8 (r850, SEL, pag_16, lin_20);
  and and_9 (r9FC, SEL, pag_19, lin_31);
  Multiplexer #(.select(1), .width(32), .enable("false")) multiplexer_1 (
    .in0({32{1'b0}}), .in1(32'h47534333), .out(mux4), .sel(r844));
  Multiplexer #(.select(1), .width(32), .enable("false")) multiplexer_2 (
    .in0({32{1'b0}}), .in1(32'h24c), .out(mux5), .sel(r848));
  Multiplexer #(.select(1), .width(32), .enable("false")) multiplexer_3 (
    .in0({32{1'b0}}), .in1(32'h100000), .out(mux6), .sel(r850));
  Multiplexer #(.select(1), .width(32), .enable("false")) multiplexer_4 (
    .in0({32{1'b0}}), .in1(32'h2007200), .out(mux7), .sel(r9FC));
  assign RD = mux4 | mux5 | mux6 | mux7;  // OR_Gate or_1, 32 bits wide

  // Other names for the same wires on the sheet: dir_registro_4_0[4:0] = dir_registro[4:0];
  //   dir_registro_9_5[4:0] = dir_registro[9:5]; or8[31:0] = RD
endmodule

module TemporizadorLEDC (
  input  CLK,
  input  RST,
  input  ANDA,
  input  [9:0] DIVISOR,
  input  [3:0] BITS,
  input  PAUSA,
  input  RESET_TIM,
  output [13:0] CUENTA,
  output DESBORDE
);

  wire and8, en_maximo, lt3, not1, not2, not4, not7, or5, or10, or13, tick;
  wire [9:0] mux6, preescala, preescala_mas1;
  wire [13:0] mux12, sum11;
  wire [14:0] maximo, uno_desplazado, zx9;

  not not_1 (not1, PAUSA);
  not not_2 (not7, PAUSA);
  not not_3 (not2, RESET_TIM);
  Register #(.width(10)) PREESC (.D(mux6), .en(and8), .Q(preescala), .clk(CLK), .clr(RST));
  Shifter #(.width(15), .shift("ll")) shifter_1 (.in(15'h1), .\dist (BITS), .out(uno_desplazado));
  Register #(.width(14)) CUENTA_2 (.D(mux12), .en(or13), .Q(CUENTA), .clk(CLK), .clr(RST));
  and and_1 (and8, ANDA, not7);
  assign zx9 = {{1{1'b0}}, CUENTA};  // Bit_Extender bit_extender_1
  Adder #(.width(14)) adder_1 (.a(CUENTA), .b(14'h1), .out(sum11));  // open: cin, cout
  Adder #(.width(10)) adder_2 (.a(preescala), .b(10'h1), .out(preescala_mas1));  // open: cin, cout
  Adder #(.width(15)) adder_3 (.a(uno_desplazado), .b({15{1'b1}}), .out(maximo));  // open: cin, cout
  Comparator #(.width(15), .mode("unsigned")) comparator_1 (.a(zx9), .b(maximo), .eq(en_maximo));  // open: gt, lt
  Comparator #(.width(10), .mode("unsigned")) comparator_2 (.a(preescala_mas1), .b(DIVISOR), .lt(lt3));  // open: gt, eq
  not not_4 (not4, lt3);
  or or_1 (or10, en_maximo, RESET_TIM);
  and and_2 (tick, ANDA, not1, not2, not4);
  Multiplexer #(.select(1), .width(14), .enable("false")) multiplexer_1 (
    .in0(sum11), .in1({14{1'b0}}), .out(mux12), .sel(or10));
  or or_2 (or5, tick, RESET_TIM);
  and and_3 (DESBORDE, tick, en_maximo);
  or or_3 (or13, tick, RESET_TIM);
  Multiplexer #(.select(1), .width(10), .enable("false")) multiplexer_2 (
    .in0(preescala_mas1), .in1({10{1'b0}}), .out(mux6), .sel(or5));

  // Other names for the same wires on the sheet: CUENTA_2[13:0] = CUENTA; cuenta_t[13:0] = CUENTA;
  //   DESBORDE_2 = DESBORDE; desborde_t = DESBORDE
endmodule

module CanalPWM (
  input  CLK,
  input  RST,
  input  [13:0] CUENTA,
  input  DESBORDE,
  input  PARA_UP,
  input  [13:0] HPOINT,
  input  [18:0] DUTY,
  input  DUTY_START,
  input  DUTY_INC,
  input  [9:0] DUTY_NUM,
  input  [9:0] DUTY_CYCLE,
  input  [9:0] DUTY_SCALE,
  input  SIG_OUT_EN,
  input  IDLE_LV,
  input  OVF_CNT_EN,
  input  [9:0] OVF_NUM,
  input  OVF_CNT_RESET,
  output SALIDA,
  output [18:0] DUTY_R,
  output FIN_VARIACION,
  output OVF_CNT
);

  wire and6, and20, and31, empieza, eq3, eq11, eq27, lt1, lt22, lt25, mux13, mux26, not2, not12, not23, or4,
       or7, or10, or14, or19, or28, or32, pwm, toca_paso, ultimo_paso, variando;
  wire [9:0] cuenta_desbordes, mux5, mux9, mux30, pasos_restantes, periodos, periodos_mas1, sum8, sum29;
  wire [13:0] hpoint_activo;
  wire [14:0] lpoint, zx21, zx24;
  wire [18:0] duty_baja, duty_sube, mux17, mux18, not15, sum16;

  Register #(.width(14)) HPOINT_2 (.D(HPOINT), .en(PARA_UP), .Q(hpoint_activo), .clk(CLK), .clr(RST));
  Register #(.width(10)) u_PERIODOS (.D(mux5), .en(or7), .Q(periodos), .clk(CLK), .clr(RST));
  and and_1 (empieza, PARA_UP, DUTY_START);
  Register #(.width(10)) PASOS (.D(mux9), .en(or10), .Q(pasos_restantes), .clk(CLK), .clr(RST));
  Comparator #(.width(10), .mode("unsigned")) comparator_1 (.a(DUTY_NUM), .b({10{1'b0}}), .eq(eq11));  // open: gt, lt
  Register #(.width(1)) u_VARIANDO (.D(mux13), .en(or14), .Q(variando), .clk(CLK), .clr(RST));
  Register #(.width(19)) DUTY_2 (.D(mux18), .en(or19), .Q(DUTY_R), .clk(CLK), .clr(RST));
  assign zx24 = {{1{1'b0}}, CUENTA};  // Bit_Extender bit_extender_1
  Register #(.width(1)) SALIDA_2 (.D(mux26), .en(1'b1), .Q(SALIDA), .clk(CLK), .clr(RST));
  and and_2 (and31, OVF_CNT_EN, DESBORDE);
  Register #(.width(10)) DESBORDES (.D(mux30), .en(or32), .Q(cuenta_desbordes), .clk(CLK), .clr(RST));
  not not_1 (not12, eq11);
  assign not15 = ~{{5{1'b0}}, DUTY_SCALE, 4'b0000};  // NOT_Gate not_2, 19 bits wide
  and and_3 (and20, empieza, eq11);
  Adder #(.width(10)) adder_1 (.a(periodos), .b(10'h1), .out(periodos_mas1));  // open: cin, cout
  Comparator #(.width(10), .mode("unsigned")) comparator_2 (.a(pasos_restantes), .b(10'h1), .eq(eq3));  // open: gt, lt
  and and_4 (and6, variando, DESBORDE);
  Adder #(.width(10)) adder_2 (.a(pasos_restantes), .b({10{1'b1}}), .out(sum8));  // open: cin, cout
  Adder #(.width(19)) adder_3 (.a(DUTY_R), .b({{5{1'b0}}, DUTY_SCALE, 4'b0000}), .out(duty_sube));  // open: cin, cout
  assign zx21 = {{1{1'b0}}, hpoint_activo};  // Bit_Extender bit_extender_2
  Comparator #(.width(14), .mode("unsigned")) comparator_3 (.a(CUENTA), .b(hpoint_activo), .lt(lt22));  // open: gt, eq
  Comparator #(.width(10), .mode("unsigned")) comparator_4 (
    .a(cuenta_desbordes), .b(OVF_NUM), .eq(eq27));  // open: gt, lt
  Adder #(.width(10)) adder_4 (.a(cuenta_desbordes), .b(10'h1), .out(sum29));  // open: cin, cout
  or or_1 (or32, and31, OVF_CNT_RESET);
  or or_2 (or7, and6, PARA_UP);
  Multiplexer #(.select(1), .width(10), .enable("false")) multiplexer_1 (
    .in0(sum8), .in1(DUTY_NUM), .out(mux9), .sel(empieza));
  Multiplexer #(.select(1), .width(1), .enable("false")) multiplexer_2 (
    .in0(1'b0), .in1(not12), .out(mux13), .sel(empieza));
  Adder #(.width(19)) adder_5 (.a(not15), .b(19'h1), .out(sum16));  // open: cin, cout
  not not_3 (not23, lt22);
  and and_5 (OVF_CNT, OVF_CNT_EN, DESBORDE, eq27);
  Comparator #(.width(10), .mode("unsigned")) comparator_5 (
    .a(periodos_mas1), .b(DUTY_CYCLE), .lt(lt1));  // open: gt, eq
  Adder #(.width(15)) adder_6 (.a(zx21), .b(DUTY_R[18:4]), .out(lpoint));  // open: cin, cout
  not not_4 (not2, lt1);
  Comparator #(.width(15), .mode("unsigned")) comparator_6 (.a(zx24), .b(lpoint), .lt(lt25));  // open: gt, eq
  Adder #(.width(19)) adder_7 (.a(DUTY_R), .b(sum16), .out(duty_baja));  // open: cin, cout
  or or_3 (or28, OVF_CNT, OVF_CNT_RESET);
  and and_6 (toca_paso, variando, DESBORDE, not2);
  Multiplexer #(.select(1), .width(19), .enable("false")) multiplexer_3 (
    .in0(duty_baja), .in1(duty_sube), .out(mux17), .sel(DUTY_INC));
  and and_7 (pwm, not23, lt25);
  Multiplexer #(.select(1), .width(10), .enable("false")) multiplexer_4 (
    .in0(sum29), .in1({10{1'b0}}), .out(mux30), .sel(or28));
  and and_8 (ultimo_paso, toca_paso, eq3);
  or or_4 (or4, toca_paso, PARA_UP);
  or or_5 (or10, empieza, toca_paso);
  Multiplexer #(.select(1), .width(19), .enable("false")) multiplexer_5 (
    .in0(mux17), .in1(DUTY), .out(mux18), .sel(PARA_UP));
  or or_6 (or19, PARA_UP, toca_paso);
  Multiplexer #(.select(1), .width(1), .enable("false")) multiplexer_6 (
    .in0(IDLE_LV), .in1(pwm), .out(mux26), .sel(SIG_OUT_EN));
  Multiplexer #(.select(1), .width(10), .enable("false")) multiplexer_7 (
    .in0(periodos_mas1), .in1({10{1'b0}}), .out(mux5), .sel(or4));
  or or_7 (or14, empieza, ultimo_paso);
  or or_8 (FIN_VARIACION, ultimo_paso, and20);

  // Other names for the same wires on the sheet: duty_actual[18:0] = DUTY_R; duty_actual_18_4[14:0] = DUTY_R[18:4];
  //   FIN_VARIACION_2 = FIN_VARIACION; fin_variacion_t = FIN_VARIACION; desbordes_completos = OVF_CNT;
  //   paso[13:4] = DUTY_SCALE; SALIDA_2 = SALIDA; salida_t = SALIDA
endmodule
module LEDC (
  input  CLK,
  input  RST,
  input  SEL,
  input  [9:0] A,
  input  [31:0] WD,
  input  WE,
  input  RE,
  output PWM0,
  output PWM1,
  output PWM2,
  output PWM3,
  output PWM4,
  output PWM5,
  output IRQ,
  output [31:0] RD
);

  wire and49, and50, and73, and74, and97, and98, and121, and122, and145, and146, and169, and170, and180,
       and184, CFG0_CANAL00_escribe, CFG0_CANAL10_escribe, CFG0_CANAL20_escribe, CFG0_CANAL30_escribe,
       CFG0_CANAL40_escribe, CFG0_CANAL50_escribe, CFG1_CANAL00_escribe, CFG1_CANAL10_escribe,
       CFG1_CANAL20_escribe, CFG1_CANAL30_escribe, CFG1_CANAL40_escribe, CFG1_CANAL50_escribe,
       CFG_RELOJ0_escribe, CFG_TEMP0_escribe, CFG_TEMP1_escribe, desborde_canal0, desborde_canal1,
       desborde_canal2, desborde_canal3, desborde_canal4, desborde_canal5, desborde_t0, desborde_t1,
       desborde_t2, desborde_t3, eq23, eq178, esc_0C8, esc_0CC, esc_01C, esc_02C, esc_004, esc_06C, esc_008,
       esc_018, esc_030, esc_040, esc_044, esc_054, esc_058, esc_068, escribe, fin0, fin1, fin2, fin3, fin4,
       fin5, lee, lin_0, lin_1, lin_2, lin_3, lin_4, lin_5, lin_6, lin_7, lin_8, lin_9, lin_10, lin_11,
       lin_12, lin_13, lin_14, lin_15, lin_16, lin_17, lin_18, lin_19, lin_20, lin_21, lin_22, lin_23,
       lin_24, lin_25, lin_26, lin_27, lin_28, lin_29, lin_30, lin_31, pag_0, pag_1, pag_2, pag_3, pag_4,
       pag_5, pag_6, pag_7, pag_8, pag_9, pag_10, pag_11, pag_12, pag_13, pag_14, pag_15, pag_16, pag_17,
       pag_18, pag_19, pag_20, pag_21, pag_22, pag_23, pag_24, pag_25, pag_26, pag_27, pag_28, pag_29,
       pag_30, pag_31, r000, r0A0, r0A4, r0A8, r0AC, r0B0, r0B4, r0B8, r0BC, r00C, r0C0, r0C4, r0C8, r0CC,
       r0D0, r01C, r02C, r03C, r004, r04C, r05C, r06C, r008, r010, r014, r018, r020, r024, r028, r030, r034,
       r038, r040, r044, r048, r050, r054, r058, r060, r064, r068, r070, r074, registros_ledc_acceso,
       registros_ledc_existe, reloj_elegido;
  wire [1:0] and21, and22, CFG_RELOJ0, CFG_RELOJ0_mascara, CFG_RELOJ0_sig, not20;
  wire [9:0] dir_registro, rep179;
  wire [13:0] and35, and36, and59, and60, and83, and84, and107, and108, and131, and132, and155, and156,
       CFG0_CANAL00_mascara, CFG0_CANAL10_mascara, CFG0_CANAL20_mascara, CFG0_CANAL30_mascara,
       CFG0_CANAL40_mascara, CFG0_CANAL50_mascara, cuenta_canal0, cuenta_canal1, cuenta_canal2,
       cuenta_canal3, cuenta_canal4, cuenta_canal5, cuenta_t0, cuenta_t1, cuenta_t2, cuenta_t3, not34, not58,
       not82, not106, not130, not154, PUNTOS_CANAL00, PUNTOS_CANAL00_mascara, PUNTOS_CANAL00_sig,
       PUNTOS_CANAL10, PUNTOS_CANAL10_mascara, PUNTOS_CANAL10_sig, PUNTOS_CANAL20, PUNTOS_CANAL20_mascara,
       PUNTOS_CANAL20_sig, PUNTOS_CANAL30, PUNTOS_CANAL30_mascara, PUNTOS_CANAL30_sig, PUNTOS_CANAL40,
       PUNTOS_CANAL40_mascara, PUNTOS_CANAL40_sig, PUNTOS_CANAL50, PUNTOS_CANAL50_mascara, PUNTOS_CANAL50_sig;
  wire [14:0] and31, and32, and55, and56, and79, and80, and103, and104, and127, and128, and151, and152,
       CFG0_CANAL00, CFG0_CANAL00_nuevo, CFG0_CANAL00_sig, CFG0_CANAL10, CFG0_CANAL10_sig, CFG0_CANAL20,
       CFG0_CANAL20_sig, CFG0_CANAL30, CFG0_CANAL30_sig, CFG0_CANAL40, CFG0_CANAL40_sig, CFG0_CANAL50,
       CFG0_CANAL50_sig, not30, not54, not78, not102, not126, not150;
  wire [15:10] INT_eventos;
  wire [18:0] and39, and40, and63, and64, and87, and88, and111, and112, and135, and136, and159, and160,
       duty_r0, duty_r1, duty_r2, duty_r3, duty_r4, duty_r5, not38, not62, not86, not110, not134, not158,
       PUNTOS_CANAL01, PUNTOS_CANAL01_mascara, PUNTOS_CANAL01_sig, PUNTOS_CANAL11, PUNTOS_CANAL11_mascara,
       PUNTOS_CANAL11_sig, PUNTOS_CANAL21, PUNTOS_CANAL21_mascara, PUNTOS_CANAL21_sig, PUNTOS_CANAL31,
       PUNTOS_CANAL31_mascara, PUNTOS_CANAL31_sig, PUNTOS_CANAL41, PUNTOS_CANAL41_mascara,
       PUNTOS_CANAL41_sig, PUNTOS_CANAL51, PUNTOS_CANAL51_mascara, PUNTOS_CANAL51_sig;
  wire [29:0] CFG1_CANAL00_mascara, CFG1_CANAL10_mascara, CFG1_CANAL20_mascara, CFG1_CANAL30_mascara,
       CFG1_CANAL40_mascara, CFG1_CANAL50_mascara;
  wire [31:0] and6, and7, and15, and16, and45, and46, and69, and70, and93, and94, and117, and118, and141,
       and142, and165, and166, and174, and176, and177, and183, and187, and189, and191, and193, and195,
       and197, and199, and201, and203, and205, and207, and209, and211, and213, CFG1_CANAL00,
       CFG1_CANAL00_sig, CFG1_CANAL10, CFG1_CANAL10_sig, CFG1_CANAL20, CFG1_CANAL20_sig, CFG1_CANAL30,
       CFG1_CANAL30_sig, CFG1_CANAL40, CFG1_CANAL40_sig, CFG1_CANAL50, CFG1_CANAL50_sig, CFG_TEMP0,
       CFG_TEMP0_mascara, CFG_TEMP0_sig, CFG_TEMP1, CFG_TEMP1_mascara, CFG_TEMP1_sig, INT_clr, INT_ENA,
       INT_raw, INT_st, not5, not14, not44, not68, not92, not116, not140, not164, not173, not182, or175, qx9,
       qx18, qx48, qx72, qx96, qx120, qx144, qx168, registros_ledc_a_guardar, registros_ledc_bits_fijos,
       registros_ledc_bits_rw, registros_ledc_guardado, registros_ledc_reset_rw, registros_ledc_valor,
       registros_ledc_valor_reset, rep172, rep181, rep186, rep188, rep190, rep192, rep194, rep196, rep198,
       rep200, rep202, rep204, rep206, rep208, rep210, rep212, xor8, xor17, xor47, xor71, xor95, xor119,
       xor143, xor167, xor185, zx24, zx25, zx26, zx27, zx51, zx75, zx99, zx123, zx147, zx171;
  wire [31:4] CFG1_CANAL00_nuevo;

  Register #(.width(32)) u_CFG_TEMP0 (.D(xor8), .en(CFG_TEMP0_escribe), .Q(qx9), .clk(CLK), .clr(RST));
  Register #(.width(32)) u_CFG_TEMP1 (.D(xor17), .en(CFG_TEMP1_escribe), .Q(qx18), .clk(CLK), .clr(RST));
  Register #(.width(2)) u_CFG_RELOJ0 (
    .D(CFG_RELOJ0_sig), .en(CFG_RELOJ0_escribe), .Q(CFG_RELOJ0), .clk(CLK), .clr(RST));
  Register #(.width(15)) u_CFG0_CANAL00 (
    .D(CFG0_CANAL00_sig), .en(CFG0_CANAL00_escribe), .Q(CFG0_CANAL00), .clk(CLK), .clr(RST));
  Register #(.width(14)) u_PUNTOS_CANAL00 (
    .D(PUNTOS_CANAL00_sig), .en(esc_004), .Q(PUNTOS_CANAL00), .clk(CLK), .clr(RST));
  Register #(.width(19)) u_PUNTOS_CANAL01 (
    .D(PUNTOS_CANAL01_sig), .en(esc_008), .Q(PUNTOS_CANAL01), .clk(CLK), .clr(RST));
  Register #(.width(32)) u_CFG1_CANAL00 (.D(xor47), .en(CFG1_CANAL00_escribe), .Q(qx48), .clk(CLK), .clr(RST));
  Register #(.width(15)) u_CFG0_CANAL10 (
    .D(CFG0_CANAL10_sig), .en(CFG0_CANAL10_escribe), .Q(CFG0_CANAL10), .clk(CLK), .clr(RST));
  Register #(.width(14)) u_PUNTOS_CANAL10 (
    .D(PUNTOS_CANAL10_sig), .en(esc_018), .Q(PUNTOS_CANAL10), .clk(CLK), .clr(RST));
  Register #(.width(19)) u_PUNTOS_CANAL11 (
    .D(PUNTOS_CANAL11_sig), .en(esc_01C), .Q(PUNTOS_CANAL11), .clk(CLK), .clr(RST));
  Register #(.width(32)) u_CFG1_CANAL10 (.D(xor71), .en(CFG1_CANAL10_escribe), .Q(qx72), .clk(CLK), .clr(RST));
  Register #(.width(15)) u_CFG0_CANAL20 (
    .D(CFG0_CANAL20_sig), .en(CFG0_CANAL20_escribe), .Q(CFG0_CANAL20), .clk(CLK), .clr(RST));
  Register #(.width(14)) u_PUNTOS_CANAL20 (
    .D(PUNTOS_CANAL20_sig), .en(esc_02C), .Q(PUNTOS_CANAL20), .clk(CLK), .clr(RST));
  Register #(.width(19)) u_PUNTOS_CANAL21 (
    .D(PUNTOS_CANAL21_sig), .en(esc_030), .Q(PUNTOS_CANAL21), .clk(CLK), .clr(RST));
  Register #(.width(32)) u_CFG1_CANAL20 (.D(xor95), .en(CFG1_CANAL20_escribe), .Q(qx96), .clk(CLK), .clr(RST));
  Register #(.width(15)) u_CFG0_CANAL30 (
    .D(CFG0_CANAL30_sig), .en(CFG0_CANAL30_escribe), .Q(CFG0_CANAL30), .clk(CLK), .clr(RST));
  Register #(.width(14)) u_PUNTOS_CANAL30 (
    .D(PUNTOS_CANAL30_sig), .en(esc_040), .Q(PUNTOS_CANAL30), .clk(CLK), .clr(RST));
  Register #(.width(19)) u_PUNTOS_CANAL31 (
    .D(PUNTOS_CANAL31_sig), .en(esc_044), .Q(PUNTOS_CANAL31), .clk(CLK), .clr(RST));
  Register #(.width(32)) u_CFG1_CANAL30 (.D(xor119), .en(CFG1_CANAL30_escribe), .Q(qx120), .clk(CLK), .clr(RST));
  Register #(.width(15)) u_CFG0_CANAL40 (
    .D(CFG0_CANAL40_sig), .en(CFG0_CANAL40_escribe), .Q(CFG0_CANAL40), .clk(CLK), .clr(RST));
  Register #(.width(14)) u_PUNTOS_CANAL40 (
    .D(PUNTOS_CANAL40_sig), .en(esc_054), .Q(PUNTOS_CANAL40), .clk(CLK), .clr(RST));
  Register #(.width(19)) u_PUNTOS_CANAL41 (
    .D(PUNTOS_CANAL41_sig), .en(esc_058), .Q(PUNTOS_CANAL41), .clk(CLK), .clr(RST));
  assign rep179 = {{9{SEL}}, SEL};  // Bit_Extender bit_extender_1
  and and_1 (and180, SEL, WE);
  and and_2 (escribe, WE, SEL);
  and and_3 (lee, RE, SEL);
  Register #(.width(32)) u_INT_RAW (.D(and176), .en(1'b1), .Q(INT_raw), .clk(CLK), .clr(RST));
  Register #(.width(32)) u_INT_ENA (.D(and177), .en(esc_0C8), .Q(INT_ENA), .clk(CLK), .clr(RST));
  ROM #(.addrWidth(10), .dataWidth(1)) u_REGISTROS_LEDC_EXISTE (.addr(dir_registro), .data(registros_ledc_existe));
  ROM #(.addrWidth(10), .dataWidth(32)) u_REGISTROS_LEDC_VALOR_RESET (
    .addr(dir_registro), .data(registros_ledc_valor_reset));
  ROM #(.addrWidth(10), .dataWidth(32)) u_REGISTROS_LEDC_BITS_RW (.addr(dir_registro), .data(registros_ledc_bits_rw));
  Register #(.width(32)) u_CFG1_CANAL40 (.D(xor143), .en(CFG1_CANAL40_escribe), .Q(qx144), .clk(CLK), .clr(RST));
  Register #(.width(15)) u_CFG0_CANAL50 (
    .D(CFG0_CANAL50_sig), .en(CFG0_CANAL50_escribe), .Q(CFG0_CANAL50), .clk(CLK), .clr(RST));
  Register #(.width(14)) u_PUNTOS_CANAL50 (
    .D(PUNTOS_CANAL50_sig), .en(esc_068), .Q(PUNTOS_CANAL50), .clk(CLK), .clr(RST));
  Register #(.width(19)) u_PUNTOS_CANAL51 (
    .D(PUNTOS_CANAL51_sig), .en(esc_06C), .Q(PUNTOS_CANAL51), .clk(CLK), .clr(RST));
  Register #(.width(32)) u_CFG1_CANAL50 (.D(xor167), .en(CFG1_CANAL50_escribe), .Q(qx168), .clk(CLK), .clr(RST));
  RAM #(.addrWidth(10), .dataWidth(32), .enables("byte"), .trigger("rising"), .asyncread("true"), .databus("bibus"), .clearpin("true")) REGISTROS_LEDC (
    .addr(dir_registro), .we(and184), .oe(1'b1), .clk(CLK), .din(registros_ledc_a_guardar),
    .dout(registros_ledc_guardado), .clr(RST));
  assign CFG_TEMP0 = qx9 ^ 32'h80008000;  // XOR_Gate xor_1, 32 bits wide
  assign CFG_TEMP1 = qx18 ^ 32'h80008000;  // XOR_Gate xor_2, 32 bits wide
  Comparator #(.width(2), .mode("unsigned")) comparator_1 (.a(CFG_RELOJ0), .b(2'b00), .eq(eq23));  // open: gt, lt
  assign CFG1_CANAL00 = qx48 ^ 32'h40000000;  // XOR_Gate xor_3, 32 bits wide
  assign CFG1_CANAL10 = qx72 ^ 32'h40000000;  // XOR_Gate xor_4, 32 bits wide
  assign CFG1_CANAL20 = qx96 ^ 32'h40000000;  // XOR_Gate xor_5, 32 bits wide
  assign CFG1_CANAL30 = qx120 ^ 32'h40000000;  // XOR_Gate xor_6, 32 bits wide
  assign CFG1_CANAL40 = qx144 ^ 32'h40000000;  // XOR_Gate xor_7, 32 bits wide
  assign INT_st = INT_raw & INT_ENA;  // AND_Gate and_4, 32 bits wide
  assign dir_registro = A & rep179;  // AND_Gate and_5, 10 bits wide
  assign rep181 = {{31{and180}}, and180};  // Bit_Extender bit_extender_2
  assign CFG1_CANAL50 = qx168 ^ 32'h40000000;  // XOR_Gate xor_8, 32 bits wide
  and and_6 (registros_ledc_acceso, SEL, registros_ledc_existe);
  assign not182 = ~registros_ledc_bits_rw;  // NOT_Gate not_1, 32 bits wide
  assign registros_ledc_reset_rw = registros_ledc_valor_reset & registros_ledc_bits_rw;  // AND_Gate and_7, 32 bits wide
  not not_2 (reloj_elegido, eq23);
  Comparator #(.width(32), .mode("unsigned")) comparator_2 (.a(INT_st), .b({32{1'b0}}), .eq(eq178));  // open: gt, lt
  assign {CFG1_CANAL00_nuevo[31:16], CFG0_CANAL00_nuevo[14:4], CFG1_CANAL00_nuevo[4], CFG0_CANAL00_nuevo[3:0]} = WD & rep181;  // AND_Gate and_8, 32 bits wide
  assign registros_ledc_bits_fijos = registros_ledc_valor_reset & not182;  // AND_Gate and_9, 32 bits wide
  and and_10 (and184, escribe, registros_ledc_acceso);
  assign xor185 = registros_ledc_guardado ^ registros_ledc_reset_rw;  // XOR_Gate xor_9, 32 bits wide
  assign rep186 = {{31{registros_ledc_acceso}}, registros_ledc_acceso};  // Bit_Extender bit_extender_3
  Decoder #(.select(5), .enable("false")) decoder_1 (
    .out0(pag_0), .out1(pag_1), .out2(pag_2), .out3(pag_3), .out4(pag_4), .out5(pag_5), .out6(pag_6),
    .out7(pag_7), .out8(pag_8), .out9(pag_9), .out10(pag_10), .out11(pag_11), .out12(pag_12), .out13(pag_13),
    .out14(pag_14), .out15(pag_15), .out16(pag_16), .out17(pag_17), .out18(pag_18), .out19(pag_19),
    .out20(pag_20), .out21(pag_21), .out22(pag_22), .out23(pag_23), .out24(pag_24), .out25(pag_25),
    .out26(pag_26), .out27(pag_27), .out28(pag_28), .out29(pag_29), .out30(pag_30), .out31(pag_31),
    .sel(dir_registro[9:5]));
  Decoder #(.select(5), .enable("false")) decoder_2 (
    .out0(lin_0), .out1(lin_1), .out2(lin_2), .out3(lin_3), .out4(lin_4), .out5(lin_5), .out6(lin_6),
    .out7(lin_7), .out8(lin_8), .out9(lin_9), .out10(lin_10), .out11(lin_11), .out12(lin_12), .out13(lin_13),
    .out14(lin_14), .out15(lin_15), .out16(lin_16), .out17(lin_17), .out18(lin_18), .out19(lin_19),
    .out20(lin_20), .out21(lin_21), .out22(lin_22), .out23(lin_23), .out24(lin_24), .out25(lin_25),
    .out26(lin_26), .out27(lin_27), .out28(lin_28), .out29(lin_29), .out30(lin_30), .out31(lin_31),
    .sel(dir_registro[4:0]));
  TemporizadorLEDC TIMER0 (
    .CLK(CLK), .RST(RST), .ANDA(reloj_elegido), .DIVISOR(CFG_TEMP0[13:4]), .BITS(CFG_TEMP0[3:0]),
    .PAUSA(CFG_TEMP0[14]), .RESET_TIM(CFG_TEMP0[15]), .CUENTA(cuenta_t0), .DESBORDE(desborde_t0));
  TemporizadorLEDC TIMER1 (
    .CLK(CLK), .RST(RST), .ANDA(reloj_elegido), .DIVISOR(CFG_TEMP0[29:20]), .BITS(CFG_TEMP0[19:16]),
    .PAUSA(CFG_TEMP0[30]), .RESET_TIM(CFG_TEMP0[31]), .CUENTA(cuenta_t1), .DESBORDE(desborde_t1));
  TemporizadorLEDC TIMER2 (
    .CLK(CLK), .RST(RST), .ANDA(reloj_elegido), .DIVISOR(CFG_TEMP1[13:4]), .BITS(CFG_TEMP1[3:0]),
    .PAUSA(CFG_TEMP1[14]), .RESET_TIM(CFG_TEMP1[15]), .CUENTA(cuenta_t2), .DESBORDE(desborde_t2));
  TemporizadorLEDC TIMER3 (
    .CLK(CLK), .RST(RST), .ANDA(reloj_elegido), .DIVISOR(CFG_TEMP1[29:20]), .BITS(CFG_TEMP1[19:16]),
    .PAUSA(CFG_TEMP1[30]), .RESET_TIM(CFG_TEMP1[31]), .CUENTA(cuenta_t3), .DESBORDE(desborde_t3));
  assign and177 = {CFG1_CANAL00_nuevo[31:16], CFG0_CANAL00_nuevo[14:4], CFG1_CANAL00_nuevo[4], CFG0_CANAL00_nuevo[3:0]} & 32'hffff;  // AND_Gate and_11, 32 bits wide
  not not_3 (IRQ, eq178);
  assign and183 = {CFG1_CANAL00_nuevo[31:16], CFG0_CANAL00_nuevo[14:4], CFG1_CANAL00_nuevo[4], CFG0_CANAL00_nuevo[3:0]} & registros_ledc_bits_rw;  // AND_Gate and_12, 32 bits wide
  assign registros_ledc_valor = xor185 | registros_ledc_bits_fijos;  // OR_Gate or_1, 32 bits wide
  and and_13 (r0A0, SEL, pag_1, lin_8);
  and and_14 (r0A8, SEL, pag_1, lin_10);
  and and_15 (r0B0, SEL, pag_1, lin_12);
  and and_16 (r0B8, SEL, pag_1, lin_14);
  and and_17 (r0D0, SEL, pag_1, lin_20);
  and and_18 (r000, SEL, pag_0, lin_0);
  and and_19 (r004, SEL, pag_0, lin_1);
  and and_20 (r008, SEL, pag_0, lin_2);
  and and_21 (r00C, SEL, pag_0, lin_3);
  and and_22 (r014, SEL, pag_0, lin_5);
  and and_23 (r018, SEL, pag_0, lin_6);
  and and_24 (r01C, SEL, pag_0, lin_7);
  and and_25 (r020, SEL, pag_0, lin_8);
  assign zx24 = {{18{1'b0}}, cuenta_t0};  // Bit_Extender bit_extender_4
  assign zx25 = {{18{1'b0}}, cuenta_t1};  // Bit_Extender bit_extender_5
  assign zx26 = {{18{1'b0}}, cuenta_t2};  // Bit_Extender bit_extender_6
  assign zx27 = {{18{1'b0}}, cuenta_t3};  // Bit_Extender bit_extender_7
  Multiplexer #(.select(2), .width(14), .enable("false")) multiplexer_1 (
    .in0(cuenta_t0), .in1(cuenta_t1), .in2(cuenta_t2), .in3(cuenta_t3), .out(cuenta_canal0),
    .sel(CFG0_CANAL00[1:0]));
  Multiplexer #(.select(2), .width(1), .enable("false")) multiplexer_2 (
    .in0(desborde_t0), .in1(desborde_t1), .in2(desborde_t2), .in3(desborde_t3), .out(desborde_canal0),
    .sel(CFG0_CANAL00[1:0]));
  Multiplexer #(.select(2), .width(14), .enable("false")) multiplexer_3 (
    .in0(cuenta_t0), .in1(cuenta_t1), .in2(cuenta_t2), .in3(cuenta_t3), .out(cuenta_canal1),
    .sel(CFG0_CANAL10[1:0]));
  Multiplexer #(.select(2), .width(1), .enable("false")) multiplexer_4 (
    .in0(desborde_t0), .in1(desborde_t1), .in2(desborde_t2), .in3(desborde_t3), .out(desborde_canal1),
    .sel(CFG0_CANAL10[1:0]));
  and and_26 (r028, SEL, pag_0, lin_10);
  and and_27 (r02C, SEL, pag_0, lin_11);
  and and_28 (r030, SEL, pag_0, lin_12);
  and and_29 (r034, SEL, pag_0, lin_13);
  Multiplexer #(.select(2), .width(14), .enable("false")) multiplexer_5 (
    .in0(cuenta_t0), .in1(cuenta_t1), .in2(cuenta_t2), .in3(cuenta_t3), .out(cuenta_canal2),
    .sel(CFG0_CANAL20[1:0]));
  Multiplexer #(.select(2), .width(1), .enable("false")) multiplexer_6 (
    .in0(desborde_t0), .in1(desborde_t1), .in2(desborde_t2), .in3(desborde_t3), .out(desborde_canal2),
    .sel(CFG0_CANAL20[1:0]));
  and and_30 (r03C, SEL, pag_0, lin_15);
  and and_31 (r040, SEL, pag_0, lin_16);
  and and_32 (r044, SEL, pag_0, lin_17);
  and and_33 (r048, SEL, pag_0, lin_18);
  Multiplexer #(.select(2), .width(14), .enable("false")) multiplexer_7 (
    .in0(cuenta_t0), .in1(cuenta_t1), .in2(cuenta_t2), .in3(cuenta_t3), .out(cuenta_canal3),
    .sel(CFG0_CANAL30[1:0]));
  Multiplexer #(.select(2), .width(1), .enable("false")) multiplexer_8 (
    .in0(desborde_t0), .in1(desborde_t1), .in2(desborde_t2), .in3(desborde_t3), .out(desborde_canal3),
    .sel(CFG0_CANAL30[1:0]));
  and and_34 (r050, SEL, pag_0, lin_20);
  and and_35 (r054, SEL, pag_0, lin_21);
  and and_36 (r058, SEL, pag_0, lin_22);
  and and_37 (r05C, SEL, pag_0, lin_23);
  Multiplexer #(.select(2), .width(14), .enable("false")) multiplexer_9 (
    .in0(cuenta_t0), .in1(cuenta_t1), .in2(cuenta_t2), .in3(cuenta_t3), .out(cuenta_canal4),
    .sel(CFG0_CANAL40[1:0]));
  Multiplexer #(.select(2), .width(1), .enable("false")) multiplexer_10 (
    .in0(desborde_t0), .in1(desborde_t1), .in2(desborde_t2), .in3(desborde_t3), .out(desborde_canal4),
    .sel(CFG0_CANAL40[1:0]));
  and and_38 (r064, SEL, pag_0, lin_25);
  and and_39 (r068, SEL, pag_0, lin_26);
  and and_40 (r06C, SEL, pag_0, lin_27);
  and and_41 (r070, SEL, pag_0, lin_28);
  Multiplexer #(.select(2), .width(14), .enable("false")) multiplexer_11 (
    .in0(cuenta_t0), .in1(cuenta_t1), .in2(cuenta_t2), .in3(cuenta_t3), .out(cuenta_canal5),
    .sel(CFG0_CANAL50[1:0]));
  Multiplexer #(.select(2), .width(1), .enable("false")) multiplexer_12 (
    .in0(desborde_t0), .in1(desborde_t1), .in2(desborde_t2), .in3(desborde_t3), .out(desborde_canal5),
    .sel(CFG0_CANAL50[1:0]));
  and and_42 (r0CC, SEL, pag_1, lin_19);
  and and_43 (r0C8, SEL, pag_1, lin_18);
  and and_44 (r0A4, SEL, pag_1, lin_9);
  and and_45 (r0AC, SEL, pag_1, lin_11);
  and and_46 (r0B4, SEL, pag_1, lin_13);
  and and_47 (r0BC, SEL, pag_1, lin_15);
  and and_48 (r010, SEL, pag_0, lin_4);
  and and_49 (r024, SEL, pag_0, lin_9);
  and and_50 (r038, SEL, pag_0, lin_14);
  and and_51 (r04C, SEL, pag_0, lin_19);
  and and_52 (r060, SEL, pag_0, lin_24);
  and and_53 (r074, SEL, pag_0, lin_29);
  and and_54 (r0C0, SEL, pag_1, lin_16);
  and and_55 (r0C4, SEL, pag_1, lin_17);
  assign registros_ledc_a_guardar = and183 ^ registros_ledc_reset_rw;  // XOR_Gate xor_10, 32 bits wide
  assign and187 = registros_ledc_valor & rep186;  // AND_Gate and_56, 32 bits wide
  and and_57 (CFG_TEMP0_mascara[15], escribe, r0A0);
  and and_58 (CFG_TEMP0_mascara[31], escribe, r0A8);
  and and_59 (CFG_TEMP1_mascara[15], escribe, r0B0);
  and and_60 (CFG_TEMP1_mascara[31], escribe, r0B8);
  and and_61 (CFG_RELOJ0_escribe, escribe, r0D0);
  and and_62 (CFG0_CANAL00_escribe, escribe, r000);
  and and_63 (esc_004, escribe, r004);
  and and_64 (esc_008, escribe, r008);
  and and_65 (CFG1_CANAL00_escribe, escribe, r00C);
  and and_66 (CFG0_CANAL10_escribe, escribe, r014);
  and and_67 (esc_018, escribe, r018);
  and and_68 (esc_01C, escribe, r01C);
  and and_69 (CFG1_CANAL10_escribe, escribe, r020);
  and and_70 (CFG0_CANAL20_escribe, escribe, r028);
  and and_71 (esc_02C, escribe, r02C);
  and and_72 (esc_030, escribe, r030);
  and and_73 (CFG1_CANAL20_escribe, escribe, r034);
  and and_74 (CFG0_CANAL30_escribe, escribe, r03C);
  and and_75 (esc_040, escribe, r040);
  and and_76 (esc_044, escribe, r044);
  and and_77 (CFG1_CANAL30_escribe, escribe, r048);
  and and_78 (CFG0_CANAL40_escribe, escribe, r050);
  and and_79 (esc_054, escribe, r054);
  and and_80 (esc_058, escribe, r058);
  and and_81 (CFG1_CANAL40_escribe, escribe, r05C);
  and and_82 (CFG0_CANAL50_escribe, escribe, r064);
  and and_83 (esc_068, escribe, r068);
  and and_84 (esc_06C, escribe, r06C);
  and and_85 (CFG1_CANAL50_escribe, escribe, r070);
  and and_86 (esc_0CC, escribe, r0CC);
  and and_87 (esc_0C8, escribe, r0C8);
  assign rep188 = {{31{r0A4}}, r0A4};  // Bit_Extender bit_extender_8
  assign rep190 = {{31{r0AC}}, r0AC};  // Bit_Extender bit_extender_9
  assign rep192 = {{31{r0B4}}, r0B4};  // Bit_Extender bit_extender_10
  assign rep194 = {{31{r0BC}}, r0BC};  // Bit_Extender bit_extender_11
  assign rep196 = {{31{r010}}, r010};  // Bit_Extender bit_extender_12
  assign rep198 = {{31{r024}}, r024};  // Bit_Extender bit_extender_13
  assign rep200 = {{31{r038}}, r038};  // Bit_Extender bit_extender_14
  assign rep202 = {{31{r04C}}, r04C};  // Bit_Extender bit_extender_15
  assign rep204 = {{31{r060}}, r060};  // Bit_Extender bit_extender_16
  assign rep206 = {{31{r074}}, r074};  // Bit_Extender bit_extender_17
  assign rep208 = {{31{r0C8}}, r0C8};  // Bit_Extender bit_extender_18
  assign rep210 = {{31{r0C0}}, r0C0};  // Bit_Extender bit_extender_19
  assign rep212 = {{31{r0C4}}, r0C4};  // Bit_Extender bit_extender_20
  or or_2 (CFG_TEMP0_escribe, CFG_TEMP0_mascara[15], CFG_TEMP0_mascara[31]);
  or or_3 (CFG_TEMP1_escribe, CFG_TEMP1_mascara[15], CFG_TEMP1_mascara[31]);
  assign CFG_TEMP0_mascara[3:0] = {{3{CFG_TEMP0_mascara[15]}}, CFG_TEMP0_mascara[15]};  // Bit_Extender bit_extender_21
  assign CFG_TEMP0_mascara[13:4] = {{9{CFG_TEMP0_mascara[15]}}, CFG_TEMP0_mascara[15]};  // Bit_Extender bit_extender_22
  assign CFG_TEMP0_mascara[19:16] = {{3{CFG_TEMP0_mascara[31]}}, CFG_TEMP0_mascara[31]};  // Bit_Extender bit_extender_23
  assign CFG_TEMP0_mascara[29:20] = {{9{CFG_TEMP0_mascara[31]}}, CFG_TEMP0_mascara[31]};  // Bit_Extender bit_extender_24
  assign CFG_TEMP1_mascara[3:0] = {{3{CFG_TEMP1_mascara[15]}}, CFG_TEMP1_mascara[15]};  // Bit_Extender bit_extender_25
  assign CFG_TEMP1_mascara[13:4] = {{9{CFG_TEMP1_mascara[15]}}, CFG_TEMP1_mascara[15]};  // Bit_Extender bit_extender_26
  assign CFG_TEMP1_mascara[19:16] = {{3{CFG_TEMP1_mascara[31]}}, CFG_TEMP1_mascara[31]};  // Bit_Extender bit_extender_27
  assign CFG_TEMP1_mascara[29:20] = {{9{CFG_TEMP1_mascara[31]}}, CFG_TEMP1_mascara[31]};  // Bit_Extender bit_extender_28
  assign CFG_RELOJ0_mascara = {{1{CFG_RELOJ0_escribe}}, CFG_RELOJ0_escribe};  // Bit_Extender bit_extender_29
  assign CFG0_CANAL00_mascara[1:0] = {{1{CFG0_CANAL00_escribe}}, CFG0_CANAL00_escribe};  // Bit_Extender bit_extender_30
  assign CFG0_CANAL00_mascara[13:4] = {{9{CFG0_CANAL00_escribe}}, CFG0_CANAL00_escribe};  // Bit_Extender bit_extender_31
  assign PUNTOS_CANAL00_mascara = {{13{esc_004}}, esc_004};  // Bit_Extender bit_extender_32
  assign PUNTOS_CANAL01_mascara = {{18{esc_008}}, esc_008};  // Bit_Extender bit_extender_33
  assign CFG1_CANAL00_mascara[9:0] = {{9{CFG1_CANAL00_escribe}}, CFG1_CANAL00_escribe};  // Bit_Extender bit_extender_34
  assign CFG1_CANAL00_mascara[19:10] = {{9{CFG1_CANAL00_escribe}}, CFG1_CANAL00_escribe};  // Bit_Extender bit_extender_35
  assign CFG1_CANAL00_mascara[29:20] = {{9{CFG1_CANAL00_escribe}}, CFG1_CANAL00_escribe};  // Bit_Extender bit_extender_36
  and and_88 (and49, CFG0_CANAL00_escribe, CFG1_CANAL00_nuevo[4]);
  and and_89 (and50, CFG0_CANAL00_escribe, CFG1_CANAL00_nuevo[16]);
  assign CFG0_CANAL10_mascara[1:0] = {{1{CFG0_CANAL10_escribe}}, CFG0_CANAL10_escribe};  // Bit_Extender bit_extender_37
  assign CFG0_CANAL10_mascara[13:4] = {{9{CFG0_CANAL10_escribe}}, CFG0_CANAL10_escribe};  // Bit_Extender bit_extender_38
  assign PUNTOS_CANAL10_mascara = {{13{esc_018}}, esc_018};  // Bit_Extender bit_extender_39
  assign PUNTOS_CANAL11_mascara = {{18{esc_01C}}, esc_01C};  // Bit_Extender bit_extender_40
  assign CFG1_CANAL10_mascara[9:0] = {{9{CFG1_CANAL10_escribe}}, CFG1_CANAL10_escribe};  // Bit_Extender bit_extender_41
  assign CFG1_CANAL10_mascara[19:10] = {{9{CFG1_CANAL10_escribe}}, CFG1_CANAL10_escribe};  // Bit_Extender bit_extender_42
  assign CFG1_CANAL10_mascara[29:20] = {{9{CFG1_CANAL10_escribe}}, CFG1_CANAL10_escribe};  // Bit_Extender bit_extender_43
  and and_90 (and73, CFG0_CANAL10_escribe, CFG1_CANAL00_nuevo[4]);
  and and_91 (and74, CFG0_CANAL10_escribe, CFG1_CANAL00_nuevo[16]);
  assign CFG0_CANAL20_mascara[1:0] = {{1{CFG0_CANAL20_escribe}}, CFG0_CANAL20_escribe};  // Bit_Extender bit_extender_44
  assign CFG0_CANAL20_mascara[13:4] = {{9{CFG0_CANAL20_escribe}}, CFG0_CANAL20_escribe};  // Bit_Extender bit_extender_45
  assign PUNTOS_CANAL20_mascara = {{13{esc_02C}}, esc_02C};  // Bit_Extender bit_extender_46
  assign PUNTOS_CANAL21_mascara = {{18{esc_030}}, esc_030};  // Bit_Extender bit_extender_47
  assign CFG1_CANAL20_mascara[9:0] = {{9{CFG1_CANAL20_escribe}}, CFG1_CANAL20_escribe};  // Bit_Extender bit_extender_48
  assign CFG1_CANAL20_mascara[19:10] = {{9{CFG1_CANAL20_escribe}}, CFG1_CANAL20_escribe};  // Bit_Extender bit_extender_49
  assign CFG1_CANAL20_mascara[29:20] = {{9{CFG1_CANAL20_escribe}}, CFG1_CANAL20_escribe};  // Bit_Extender bit_extender_50
  and and_92 (and97, CFG0_CANAL20_escribe, CFG1_CANAL00_nuevo[4]);
  assign CFG0_CANAL30_mascara[1:0] = {{1{CFG0_CANAL30_escribe}}, CFG0_CANAL30_escribe};  // Bit_Extender bit_extender_51
  assign CFG0_CANAL30_mascara[13:4] = {{9{CFG0_CANAL30_escribe}}, CFG0_CANAL30_escribe};  // Bit_Extender bit_extender_52
  assign PUNTOS_CANAL30_mascara = {{13{esc_040}}, esc_040};  // Bit_Extender bit_extender_53
  assign PUNTOS_CANAL31_mascara = {{18{esc_044}}, esc_044};  // Bit_Extender bit_extender_54
  assign CFG1_CANAL30_mascara[9:0] = {{9{CFG1_CANAL30_escribe}}, CFG1_CANAL30_escribe};  // Bit_Extender bit_extender_55
  assign CFG1_CANAL30_mascara[19:10] = {{9{CFG1_CANAL30_escribe}}, CFG1_CANAL30_escribe};  // Bit_Extender bit_extender_56
  assign CFG1_CANAL30_mascara[29:20] = {{9{CFG1_CANAL30_escribe}}, CFG1_CANAL30_escribe};  // Bit_Extender bit_extender_57
  and and_93 (and121, CFG0_CANAL30_escribe, CFG1_CANAL00_nuevo[4]);
  assign CFG0_CANAL40_mascara[1:0] = {{1{CFG0_CANAL40_escribe}}, CFG0_CANAL40_escribe};  // Bit_Extender bit_extender_58
  assign CFG0_CANAL40_mascara[13:4] = {{9{CFG0_CANAL40_escribe}}, CFG0_CANAL40_escribe};  // Bit_Extender bit_extender_59
  assign PUNTOS_CANAL40_mascara = {{13{esc_054}}, esc_054};  // Bit_Extender bit_extender_60
  assign PUNTOS_CANAL41_mascara = {{18{esc_058}}, esc_058};  // Bit_Extender bit_extender_61
  assign CFG1_CANAL40_mascara[9:0] = {{9{CFG1_CANAL40_escribe}}, CFG1_CANAL40_escribe};  // Bit_Extender bit_extender_62
  assign CFG1_CANAL40_mascara[19:10] = {{9{CFG1_CANAL40_escribe}}, CFG1_CANAL40_escribe};  // Bit_Extender bit_extender_63
  assign CFG1_CANAL40_mascara[29:20] = {{9{CFG1_CANAL40_escribe}}, CFG1_CANAL40_escribe};  // Bit_Extender bit_extender_64
  and and_94 (and145, CFG0_CANAL40_escribe, CFG1_CANAL00_nuevo[4]);
  assign CFG0_CANAL50_mascara[1:0] = {{1{CFG0_CANAL50_escribe}}, CFG0_CANAL50_escribe};  // Bit_Extender bit_extender_65
  assign CFG0_CANAL50_mascara[13:4] = {{9{CFG0_CANAL50_escribe}}, CFG0_CANAL50_escribe};  // Bit_Extender bit_extender_66
  and and_95 (and98, CFG0_CANAL20_escribe, CFG1_CANAL00_nuevo[16]);
  and and_96 (and122, CFG0_CANAL30_escribe, CFG1_CANAL00_nuevo[16]);
  and and_97 (and146, CFG0_CANAL40_escribe, CFG1_CANAL00_nuevo[16]);
  assign PUNTOS_CANAL50_mascara = {{13{esc_068}}, esc_068};  // Bit_Extender bit_extender_67
  assign PUNTOS_CANAL51_mascara = {{18{esc_06C}}, esc_06C};  // Bit_Extender bit_extender_68
  assign CFG1_CANAL50_mascara[9:0] = {{9{CFG1_CANAL50_escribe}}, CFG1_CANAL50_escribe};  // Bit_Extender bit_extender_69
  assign CFG1_CANAL50_mascara[19:10] = {{9{CFG1_CANAL50_escribe}}, CFG1_CANAL50_escribe};  // Bit_Extender bit_extender_70
  assign CFG1_CANAL50_mascara[29:20] = {{9{CFG1_CANAL50_escribe}}, CFG1_CANAL50_escribe};  // Bit_Extender bit_extender_71
  assign rep172 = {{31{esc_0CC}}, esc_0CC};  // Bit_Extender bit_extender_72
  assign and189 = zx24 & rep188;  // AND_Gate and_98, 32 bits wide
  assign and191 = zx25 & rep190;  // AND_Gate and_99, 32 bits wide
  assign and193 = zx26 & rep192;  // AND_Gate and_100, 32 bits wide
  assign and195 = zx27 & rep194;  // AND_Gate and_101, 32 bits wide
  assign and209 = INT_ENA & rep208;  // AND_Gate and_102, 32 bits wide
  assign and211 = INT_raw & rep210;  // AND_Gate and_103, 32 bits wide
  assign and213 = INT_st & rep212;  // AND_Gate and_104, 32 bits wide
  and and_105 (and169, CFG0_CANAL50_escribe, CFG1_CANAL00_nuevo[4]);
  and and_106 (and170, CFG0_CANAL50_escribe, CFG1_CANAL00_nuevo[16]);
  CanalPWM CANAL0 (
    .CLK(CLK), .RST(RST), .CUENTA(cuenta_canal0), .DESBORDE(desborde_canal0), .PARA_UP(and49),
    .HPOINT(PUNTOS_CANAL00), .DUTY(PUNTOS_CANAL01), .DUTY_START(CFG1_CANAL00[31]),
    .DUTY_INC(CFG1_CANAL00[30]), .DUTY_NUM(CFG1_CANAL00[29:20]), .DUTY_CYCLE(CFG1_CANAL00[19:10]),
    .DUTY_SCALE(CFG1_CANAL00[9:0]), .SIG_OUT_EN(CFG0_CANAL00[2]), .IDLE_LV(CFG0_CANAL00[3]),
    .OVF_CNT_EN(CFG0_CANAL00[14]), .OVF_NUM(CFG0_CANAL00[13:4]), .OVF_CNT_RESET(and50), .SALIDA(PWM0),
    .DUTY_R(duty_r0), .FIN_VARIACION(fin0), .OVF_CNT(INT_eventos[10]));
  CanalPWM CANAL1 (
    .CLK(CLK), .RST(RST), .CUENTA(cuenta_canal1), .DESBORDE(desborde_canal1), .PARA_UP(and73),
    .HPOINT(PUNTOS_CANAL10), .DUTY(PUNTOS_CANAL11), .DUTY_START(CFG1_CANAL10[31]),
    .DUTY_INC(CFG1_CANAL10[30]), .DUTY_NUM(CFG1_CANAL10[29:20]), .DUTY_CYCLE(CFG1_CANAL10[19:10]),
    .DUTY_SCALE(CFG1_CANAL10[9:0]), .SIG_OUT_EN(CFG0_CANAL10[2]), .IDLE_LV(CFG0_CANAL10[3]),
    .OVF_CNT_EN(CFG0_CANAL10[14]), .OVF_NUM(CFG0_CANAL10[13:4]), .OVF_CNT_RESET(and74), .SALIDA(PWM1),
    .DUTY_R(duty_r1), .FIN_VARIACION(fin1), .OVF_CNT(INT_eventos[11]));
  CanalPWM CANAL2 (
    .CLK(CLK), .RST(RST), .CUENTA(cuenta_canal2), .DESBORDE(desborde_canal2), .PARA_UP(and97),
    .HPOINT(PUNTOS_CANAL20), .DUTY(PUNTOS_CANAL21), .DUTY_START(CFG1_CANAL20[31]),
    .DUTY_INC(CFG1_CANAL20[30]), .DUTY_NUM(CFG1_CANAL20[29:20]), .DUTY_CYCLE(CFG1_CANAL20[19:10]),
    .DUTY_SCALE(CFG1_CANAL20[9:0]), .SIG_OUT_EN(CFG0_CANAL20[2]), .IDLE_LV(CFG0_CANAL20[3]),
    .OVF_CNT_EN(CFG0_CANAL20[14]), .OVF_NUM(CFG0_CANAL20[13:4]), .OVF_CNT_RESET(and98), .SALIDA(PWM2),
    .DUTY_R(duty_r2), .FIN_VARIACION(fin2), .OVF_CNT(INT_eventos[12]));
  CanalPWM CANAL3 (
    .CLK(CLK), .RST(RST), .CUENTA(cuenta_canal3), .DESBORDE(desborde_canal3), .PARA_UP(and121),
    .HPOINT(PUNTOS_CANAL30), .DUTY(PUNTOS_CANAL31), .DUTY_START(CFG1_CANAL30[31]),
    .DUTY_INC(CFG1_CANAL30[30]), .DUTY_NUM(CFG1_CANAL30[29:20]), .DUTY_CYCLE(CFG1_CANAL30[19:10]),
    .DUTY_SCALE(CFG1_CANAL30[9:0]), .SIG_OUT_EN(CFG0_CANAL30[2]), .IDLE_LV(CFG0_CANAL30[3]),
    .OVF_CNT_EN(CFG0_CANAL30[14]), .OVF_NUM(CFG0_CANAL30[13:4]), .OVF_CNT_RESET(and122), .SALIDA(PWM3),
    .DUTY_R(duty_r3), .FIN_VARIACION(fin3), .OVF_CNT(INT_eventos[13]));
  CanalPWM CANAL4 (
    .CLK(CLK), .RST(RST), .CUENTA(cuenta_canal4), .DESBORDE(desborde_canal4), .PARA_UP(and145),
    .HPOINT(PUNTOS_CANAL40), .DUTY(PUNTOS_CANAL41), .DUTY_START(CFG1_CANAL40[31]),
    .DUTY_INC(CFG1_CANAL40[30]), .DUTY_NUM(CFG1_CANAL40[29:20]), .DUTY_CYCLE(CFG1_CANAL40[19:10]),
    .DUTY_SCALE(CFG1_CANAL40[9:0]), .SIG_OUT_EN(CFG0_CANAL40[2]), .IDLE_LV(CFG0_CANAL40[3]),
    .OVF_CNT_EN(CFG0_CANAL40[14]), .OVF_NUM(CFG0_CANAL40[13:4]), .OVF_CNT_RESET(and146), .SALIDA(PWM4),
    .DUTY_R(duty_r4), .FIN_VARIACION(fin4), .OVF_CNT(INT_eventos[14]));
  CanalPWM CANAL5 (
    .CLK(CLK), .RST(RST), .CUENTA(cuenta_canal5), .DESBORDE(desborde_canal5), .PARA_UP(and169),
    .HPOINT(PUNTOS_CANAL50), .DUTY(PUNTOS_CANAL51), .DUTY_START(CFG1_CANAL50[31]),
    .DUTY_INC(CFG1_CANAL50[30]), .DUTY_NUM(CFG1_CANAL50[29:20]), .DUTY_CYCLE(CFG1_CANAL50[19:10]),
    .DUTY_SCALE(CFG1_CANAL50[9:0]), .SIG_OUT_EN(CFG0_CANAL50[2]), .IDLE_LV(CFG0_CANAL50[3]),
    .OVF_CNT_EN(CFG0_CANAL50[14]), .OVF_NUM(CFG0_CANAL50[13:4]), .OVF_CNT_RESET(and170), .SALIDA(PWM5),
    .DUTY_R(duty_r5), .FIN_VARIACION(fin5), .OVF_CNT(INT_eventos[15]));
  assign INT_clr = {CFG1_CANAL00_nuevo[31:16], CFG0_CANAL00_nuevo[14:4], CFG1_CANAL00_nuevo[4], CFG0_CANAL00_nuevo[3:0]} & rep172;  // AND_Gate and_107, 32 bits wide
  assign zx51 = {{13{1'b0}}, duty_r0};  // Bit_Extender bit_extender_73
  assign zx75 = {{13{1'b0}}, duty_r1};  // Bit_Extender bit_extender_74
  assign zx99 = {{13{1'b0}}, duty_r2};  // Bit_Extender bit_extender_75
  assign zx123 = {{13{1'b0}}, duty_r3};  // Bit_Extender bit_extender_76
  assign zx147 = {{13{1'b0}}, duty_r4};  // Bit_Extender bit_extender_77
  assign not5 = ~{{2{CFG_TEMP0_mascara[31]}}, CFG_TEMP0_mascara[29:15], CFG_TEMP0_mascara[15], CFG_TEMP0_mascara[13:0]};  // NOT_Gate not_4, 32 bits wide
  assign and7 = {CFG1_CANAL00_nuevo[23:16], CFG0_CANAL00_nuevo[14:11], CFG0_CANAL00_nuevo[3:0], CFG1_CANAL00_nuevo[23:16], CFG0_CANAL00_nuevo[14:11], CFG0_CANAL00_nuevo[3:0]} & {{2{CFG_TEMP0_mascara[31]}}, CFG_TEMP0_mascara[29:15], CFG_TEMP0_mascara[15], CFG_TEMP0_mascara[13:0]};  // AND_Gate and_108, 32 bits wide
  assign not14 = ~{{2{CFG_TEMP1_mascara[31]}}, CFG_TEMP1_mascara[29:15], CFG_TEMP1_mascara[15], CFG_TEMP1_mascara[13:0]};  // NOT_Gate not_5, 32 bits wide
  assign and16 = {CFG1_CANAL00_nuevo[23:16], CFG0_CANAL00_nuevo[14:11], CFG0_CANAL00_nuevo[3:0], CFG1_CANAL00_nuevo[23:16], CFG0_CANAL00_nuevo[14:11], CFG0_CANAL00_nuevo[3:0]} & {{2{CFG_TEMP1_mascara[31]}}, CFG_TEMP1_mascara[29:15], CFG_TEMP1_mascara[15], CFG_TEMP1_mascara[13:0]};  // AND_Gate and_109, 32 bits wide
  assign not20 = ~CFG_RELOJ0_mascara;  // NOT_Gate not_6, 2 bits wide
  assign and22 = CFG0_CANAL00_nuevo[1:0] & CFG_RELOJ0_mascara;  // AND_Gate and_110, 2 bits wide
  assign not30 = ~{CFG0_CANAL00_escribe, CFG0_CANAL00_mascara[13:4], {2{CFG0_CANAL00_escribe}}, CFG0_CANAL00_mascara[1:0]};  // NOT_Gate not_7, 15 bits wide
  assign and32 = CFG0_CANAL00_nuevo & {CFG0_CANAL00_escribe, CFG0_CANAL00_mascara[13:4], {2{CFG0_CANAL00_escribe}}, CFG0_CANAL00_mascara[1:0]};  // AND_Gate and_111, 15 bits wide
  assign not34 = ~PUNTOS_CANAL00_mascara;  // NOT_Gate not_8, 14 bits wide
  assign and36 = {CFG0_CANAL00_nuevo[12:4], CFG1_CANAL00_nuevo[4], CFG0_CANAL00_nuevo[3:0]} & PUNTOS_CANAL00_mascara;  // AND_Gate and_112, 14 bits wide
  assign not38 = ~PUNTOS_CANAL01_mascara;  // NOT_Gate not_9, 19 bits wide
  assign and40 = {CFG1_CANAL00_nuevo[18:16], CFG0_CANAL00_nuevo[14:4], CFG1_CANAL00_nuevo[4], CFG0_CANAL00_nuevo[3:0]} & PUNTOS_CANAL01_mascara;  // AND_Gate and_113, 19 bits wide
  assign not44 = ~{{2{CFG1_CANAL00_escribe}}, CFG1_CANAL00_mascara};  // NOT_Gate not_10, 32 bits wide
  assign and46 = {CFG1_CANAL00_nuevo[31:16], CFG0_CANAL00_nuevo[14:4], CFG1_CANAL00_nuevo[4], CFG0_CANAL00_nuevo[3:0]} & {{2{CFG1_CANAL00_escribe}}, CFG1_CANAL00_mascara};  // AND_Gate and_114, 32 bits wide
  assign not54 = ~{CFG0_CANAL10_escribe, CFG0_CANAL10_mascara[13:4], {2{CFG0_CANAL10_escribe}}, CFG0_CANAL10_mascara[1:0]};  // NOT_Gate not_11, 15 bits wide
  assign and56 = CFG0_CANAL00_nuevo & {CFG0_CANAL10_escribe, CFG0_CANAL10_mascara[13:4], {2{CFG0_CANAL10_escribe}}, CFG0_CANAL10_mascara[1:0]};  // AND_Gate and_115, 15 bits wide
  assign not58 = ~PUNTOS_CANAL10_mascara;  // NOT_Gate not_12, 14 bits wide
  assign and60 = {CFG0_CANAL00_nuevo[12:4], CFG1_CANAL00_nuevo[4], CFG0_CANAL00_nuevo[3:0]} & PUNTOS_CANAL10_mascara;  // AND_Gate and_116, 14 bits wide
  assign not62 = ~PUNTOS_CANAL11_mascara;  // NOT_Gate not_13, 19 bits wide
  assign and64 = {CFG1_CANAL00_nuevo[18:16], CFG0_CANAL00_nuevo[14:4], CFG1_CANAL00_nuevo[4], CFG0_CANAL00_nuevo[3:0]} & PUNTOS_CANAL11_mascara;  // AND_Gate and_117, 19 bits wide
  assign not68 = ~{{2{CFG1_CANAL10_escribe}}, CFG1_CANAL10_mascara};  // NOT_Gate not_14, 32 bits wide
  assign and70 = {CFG1_CANAL00_nuevo[31:16], CFG0_CANAL00_nuevo[14:4], CFG1_CANAL00_nuevo[4], CFG0_CANAL00_nuevo[3:0]} & {{2{CFG1_CANAL10_escribe}}, CFG1_CANAL10_mascara};  // AND_Gate and_118, 32 bits wide
  assign not78 = ~{CFG0_CANAL20_escribe, CFG0_CANAL20_mascara[13:4], {2{CFG0_CANAL20_escribe}}, CFG0_CANAL20_mascara[1:0]};  // NOT_Gate not_15, 15 bits wide
  assign and80 = CFG0_CANAL00_nuevo & {CFG0_CANAL20_escribe, CFG0_CANAL20_mascara[13:4], {2{CFG0_CANAL20_escribe}}, CFG0_CANAL20_mascara[1:0]};  // AND_Gate and_119, 15 bits wide
  assign not82 = ~PUNTOS_CANAL20_mascara;  // NOT_Gate not_16, 14 bits wide
  assign and84 = {CFG0_CANAL00_nuevo[12:4], CFG1_CANAL00_nuevo[4], CFG0_CANAL00_nuevo[3:0]} & PUNTOS_CANAL20_mascara;  // AND_Gate and_120, 14 bits wide
  assign not86 = ~PUNTOS_CANAL21_mascara;  // NOT_Gate not_17, 19 bits wide
  assign and88 = {CFG1_CANAL00_nuevo[18:16], CFG0_CANAL00_nuevo[14:4], CFG1_CANAL00_nuevo[4], CFG0_CANAL00_nuevo[3:0]} & PUNTOS_CANAL21_mascara;  // AND_Gate and_121, 19 bits wide
  assign not92 = ~{{2{CFG1_CANAL20_escribe}}, CFG1_CANAL20_mascara};  // NOT_Gate not_18, 32 bits wide
  assign and94 = {CFG1_CANAL00_nuevo[31:16], CFG0_CANAL00_nuevo[14:4], CFG1_CANAL00_nuevo[4], CFG0_CANAL00_nuevo[3:0]} & {{2{CFG1_CANAL20_escribe}}, CFG1_CANAL20_mascara};  // AND_Gate and_122, 32 bits wide
  assign not102 = ~{CFG0_CANAL30_escribe, CFG0_CANAL30_mascara[13:4], {2{CFG0_CANAL30_escribe}}, CFG0_CANAL30_mascara[1:0]};  // NOT_Gate not_19, 15 bits wide
  assign and104 = CFG0_CANAL00_nuevo & {CFG0_CANAL30_escribe, CFG0_CANAL30_mascara[13:4], {2{CFG0_CANAL30_escribe}}, CFG0_CANAL30_mascara[1:0]};  // AND_Gate and_123, 15 bits wide
  assign not106 = ~PUNTOS_CANAL30_mascara;  // NOT_Gate not_20, 14 bits wide
  assign and108 = {CFG0_CANAL00_nuevo[12:4], CFG1_CANAL00_nuevo[4], CFG0_CANAL00_nuevo[3:0]} & PUNTOS_CANAL30_mascara;  // AND_Gate and_124, 14 bits wide
  assign not110 = ~PUNTOS_CANAL31_mascara;  // NOT_Gate not_21, 19 bits wide
  assign and112 = {CFG1_CANAL00_nuevo[18:16], CFG0_CANAL00_nuevo[14:4], CFG1_CANAL00_nuevo[4], CFG0_CANAL00_nuevo[3:0]} & PUNTOS_CANAL31_mascara;  // AND_Gate and_125, 19 bits wide
  assign not116 = ~{{2{CFG1_CANAL30_escribe}}, CFG1_CANAL30_mascara};  // NOT_Gate not_22, 32 bits wide
  assign and118 = {CFG1_CANAL00_nuevo[31:16], CFG0_CANAL00_nuevo[14:4], CFG1_CANAL00_nuevo[4], CFG0_CANAL00_nuevo[3:0]} & {{2{CFG1_CANAL30_escribe}}, CFG1_CANAL30_mascara};  // AND_Gate and_126, 32 bits wide
  assign not126 = ~{CFG0_CANAL40_escribe, CFG0_CANAL40_mascara[13:4], {2{CFG0_CANAL40_escribe}}, CFG0_CANAL40_mascara[1:0]};  // NOT_Gate not_23, 15 bits wide
  assign and128 = CFG0_CANAL00_nuevo & {CFG0_CANAL40_escribe, CFG0_CANAL40_mascara[13:4], {2{CFG0_CANAL40_escribe}}, CFG0_CANAL40_mascara[1:0]};  // AND_Gate and_127, 15 bits wide
  assign not130 = ~PUNTOS_CANAL40_mascara;  // NOT_Gate not_24, 14 bits wide
  assign and132 = {CFG0_CANAL00_nuevo[12:4], CFG1_CANAL00_nuevo[4], CFG0_CANAL00_nuevo[3:0]} & PUNTOS_CANAL40_mascara;  // AND_Gate and_128, 14 bits wide
  assign not134 = ~PUNTOS_CANAL41_mascara;  // NOT_Gate not_25, 19 bits wide
  assign and136 = {CFG1_CANAL00_nuevo[18:16], CFG0_CANAL00_nuevo[14:4], CFG1_CANAL00_nuevo[4], CFG0_CANAL00_nuevo[3:0]} & PUNTOS_CANAL41_mascara;  // AND_Gate and_129, 19 bits wide
  assign not140 = ~{{2{CFG1_CANAL40_escribe}}, CFG1_CANAL40_mascara};  // NOT_Gate not_26, 32 bits wide
  assign and142 = {CFG1_CANAL00_nuevo[31:16], CFG0_CANAL00_nuevo[14:4], CFG1_CANAL00_nuevo[4], CFG0_CANAL00_nuevo[3:0]} & {{2{CFG1_CANAL40_escribe}}, CFG1_CANAL40_mascara};  // AND_Gate and_130, 32 bits wide
  assign not150 = ~{CFG0_CANAL50_escribe, CFG0_CANAL50_mascara[13:4], {2{CFG0_CANAL50_escribe}}, CFG0_CANAL50_mascara[1:0]};  // NOT_Gate not_27, 15 bits wide
  assign and152 = CFG0_CANAL00_nuevo & {CFG0_CANAL50_escribe, CFG0_CANAL50_mascara[13:4], {2{CFG0_CANAL50_escribe}}, CFG0_CANAL50_mascara[1:0]};  // AND_Gate and_131, 15 bits wide
  assign not154 = ~PUNTOS_CANAL50_mascara;  // NOT_Gate not_28, 14 bits wide
  assign and156 = {CFG0_CANAL00_nuevo[12:4], CFG1_CANAL00_nuevo[4], CFG0_CANAL00_nuevo[3:0]} & PUNTOS_CANAL50_mascara;  // AND_Gate and_132, 14 bits wide
  assign zx171 = {{13{1'b0}}, duty_r5};  // Bit_Extender bit_extender_78
  assign not173 = ~INT_clr;  // NOT_Gate not_29, 32 bits wide
  assign not158 = ~PUNTOS_CANAL51_mascara;  // NOT_Gate not_30, 19 bits wide
  assign and160 = {CFG1_CANAL00_nuevo[18:16], CFG0_CANAL00_nuevo[14:4], CFG1_CANAL00_nuevo[4], CFG0_CANAL00_nuevo[3:0]} & PUNTOS_CANAL51_mascara;  // AND_Gate and_133, 19 bits wide
  assign not164 = ~{{2{CFG1_CANAL50_escribe}}, CFG1_CANAL50_mascara};  // NOT_Gate not_31, 32 bits wide
  assign and166 = {CFG1_CANAL00_nuevo[31:16], CFG0_CANAL00_nuevo[14:4], CFG1_CANAL00_nuevo[4], CFG0_CANAL00_nuevo[3:0]} & {{2{CFG1_CANAL50_escribe}}, CFG1_CANAL50_mascara};  // AND_Gate and_134, 32 bits wide
  assign and6 = CFG_TEMP0 & not5;  // AND_Gate and_135, 32 bits wide
  assign and15 = CFG_TEMP1 & not14;  // AND_Gate and_136, 32 bits wide
  assign and21 = CFG_RELOJ0 & not20;  // AND_Gate and_137, 2 bits wide
  assign and31 = CFG0_CANAL00 & not30;  // AND_Gate and_138, 15 bits wide
  assign and45 = CFG1_CANAL00 & not44;  // AND_Gate and_139, 32 bits wide
  assign and55 = CFG0_CANAL10 & not54;  // AND_Gate and_140, 15 bits wide
  assign and69 = CFG1_CANAL10 & not68;  // AND_Gate and_141, 32 bits wide
  assign and79 = CFG0_CANAL20 & not78;  // AND_Gate and_142, 15 bits wide
  assign and93 = CFG1_CANAL20 & not92;  // AND_Gate and_143, 32 bits wide
  assign and103 = CFG0_CANAL30 & not102;  // AND_Gate and_144, 15 bits wide
  assign and117 = CFG1_CANAL30 & not116;  // AND_Gate and_145, 32 bits wide
  assign and127 = CFG0_CANAL40 & not126;  // AND_Gate and_146, 15 bits wide
  assign and141 = CFG1_CANAL40 & not140;  // AND_Gate and_147, 32 bits wide
  assign and151 = CFG0_CANAL50 & not150;  // AND_Gate and_148, 15 bits wide
  assign and165 = CFG1_CANAL50 & not164;  // AND_Gate and_149, 32 bits wide
  assign and174 = INT_raw & not173;  // AND_Gate and_150, 32 bits wide
  assign and197 = zx51 & rep196;  // AND_Gate and_151, 32 bits wide
  assign and199 = zx75 & rep198;  // AND_Gate and_152, 32 bits wide
  assign and201 = zx99 & rep200;  // AND_Gate and_153, 32 bits wide
  assign and203 = zx123 & rep202;  // AND_Gate and_154, 32 bits wide
  assign and205 = zx147 & rep204;  // AND_Gate and_155, 32 bits wide
  assign and207 = zx171 & rep206;  // AND_Gate and_156, 32 bits wide
  assign and35 = PUNTOS_CANAL00 & not34;  // AND_Gate and_157, 14 bits wide
  assign and39 = PUNTOS_CANAL01 & not38;  // AND_Gate and_158, 19 bits wide
  assign and59 = PUNTOS_CANAL10 & not58;  // AND_Gate and_159, 14 bits wide
  assign and63 = PUNTOS_CANAL11 & not62;  // AND_Gate and_160, 19 bits wide
  assign and83 = PUNTOS_CANAL20 & not82;  // AND_Gate and_161, 14 bits wide
  assign and87 = PUNTOS_CANAL21 & not86;  // AND_Gate and_162, 19 bits wide
  assign and107 = PUNTOS_CANAL30 & not106;  // AND_Gate and_163, 14 bits wide
  assign and111 = PUNTOS_CANAL31 & not110;  // AND_Gate and_164, 19 bits wide
  assign and131 = PUNTOS_CANAL40 & not130;  // AND_Gate and_165, 14 bits wide
  assign and135 = PUNTOS_CANAL41 & not134;  // AND_Gate and_166, 19 bits wide
  assign and155 = PUNTOS_CANAL50 & not154;  // AND_Gate and_167, 14 bits wide
  assign and159 = PUNTOS_CANAL51 & not158;  // AND_Gate and_168, 19 bits wide
  assign CFG_TEMP0_sig = and6 | and7;  // OR_Gate or_4, 32 bits wide
  assign CFG_TEMP1_sig = and15 | and16;  // OR_Gate or_5, 32 bits wide
  assign CFG_RELOJ0_sig = and21 | and22;  // OR_Gate or_6, 2 bits wide
  assign CFG0_CANAL00_sig = and31 | and32;  // OR_Gate or_7, 15 bits wide
  assign PUNTOS_CANAL00_sig = and35 | and36;  // OR_Gate or_8, 14 bits wide
  assign PUNTOS_CANAL01_sig = and39 | and40;  // OR_Gate or_9, 19 bits wide
  assign CFG1_CANAL00_sig = and45 | and46;  // OR_Gate or_10, 32 bits wide
  assign CFG0_CANAL10_sig = and55 | and56;  // OR_Gate or_11, 15 bits wide
  assign PUNTOS_CANAL10_sig = and59 | and60;  // OR_Gate or_12, 14 bits wide
  assign PUNTOS_CANAL11_sig = and63 | and64;  // OR_Gate or_13, 19 bits wide
  assign CFG1_CANAL10_sig = and69 | and70;  // OR_Gate or_14, 32 bits wide
  assign CFG0_CANAL20_sig = and79 | and80;  // OR_Gate or_15, 15 bits wide
  assign PUNTOS_CANAL20_sig = and83 | and84;  // OR_Gate or_16, 14 bits wide
  assign PUNTOS_CANAL21_sig = and87 | and88;  // OR_Gate or_17, 19 bits wide
  assign CFG1_CANAL20_sig = and93 | and94;  // OR_Gate or_18, 32 bits wide
  assign CFG0_CANAL30_sig = and103 | and104;  // OR_Gate or_19, 15 bits wide
  assign PUNTOS_CANAL30_sig = and107 | and108;  // OR_Gate or_20, 14 bits wide
  assign PUNTOS_CANAL31_sig = and111 | and112;  // OR_Gate or_21, 19 bits wide
  assign CFG1_CANAL30_sig = and117 | and118;  // OR_Gate or_22, 32 bits wide
  assign CFG0_CANAL40_sig = and127 | and128;  // OR_Gate or_23, 15 bits wide
  assign PUNTOS_CANAL40_sig = and131 | and132;  // OR_Gate or_24, 14 bits wide
  assign PUNTOS_CANAL41_sig = and135 | and136;  // OR_Gate or_25, 19 bits wide
  assign CFG1_CANAL40_sig = and141 | and142;  // OR_Gate or_26, 32 bits wide
  assign CFG0_CANAL50_sig = and151 | and152;  // OR_Gate or_27, 15 bits wide
  assign PUNTOS_CANAL50_sig = and155 | and156;  // OR_Gate or_28, 14 bits wide
  assign PUNTOS_CANAL51_sig = and159 | and160;  // OR_Gate or_29, 19 bits wide
  assign CFG1_CANAL50_sig = and165 | and166;  // OR_Gate or_30, 32 bits wide
  assign or175 = and174 | {{16{1'b0}}, INT_eventos, fin5, fin4, fin3, fin2, fin1, fin0, desborde_t3, desborde_t2, desborde_t1, desborde_t0};  // OR_Gate or_31, 32 bits wide
  assign RD = and189 | and191 | and193 | and195 | and197 | and199 | and201 | and203 | and205 | and207 | and209 | and211 | and213 | and187;  // OR_Gate or_32, 32 bits wide
  assign and176 = or175 & 32'hffff;  // AND_Gate and_169, 32 bits wide
  assign xor8 = CFG_TEMP0_sig ^ 32'h80008000;  // XOR_Gate xor_11, 32 bits wide
  assign xor17 = CFG_TEMP1_sig ^ 32'h80008000;  // XOR_Gate xor_12, 32 bits wide
  assign xor47 = CFG1_CANAL00_sig ^ 32'h40000000;  // XOR_Gate xor_13, 32 bits wide
  assign xor71 = CFG1_CANAL10_sig ^ 32'h40000000;  // XOR_Gate xor_14, 32 bits wide
  assign xor95 = CFG1_CANAL20_sig ^ 32'h40000000;  // XOR_Gate xor_15, 32 bits wide
  assign xor119 = CFG1_CANAL30_sig ^ 32'h40000000;  // XOR_Gate xor_16, 32 bits wide
  assign xor143 = CFG1_CANAL40_sig ^ 32'h40000000;  // XOR_Gate xor_17, 32 bits wide
  assign xor167 = CFG1_CANAL50_sig ^ 32'h40000000;  // XOR_Gate xor_18, 32 bits wide

  // Other names for the same wires on the sheet: CFG0_CANAL00_1_0[1:0] = CFG0_CANAL00[1:0];
  //   CFG0_CANAL00_2 = CFG0_CANAL00[2]; CFG0_CANAL00_3 = CFG0_CANAL00[3]; CFG0_CANAL00_13_4[9:0] = CFG0_CANAL00[13:4];
  //   CFG0_CANAL00_14 = CFG0_CANAL00[14]; rep28[1:0] = CFG0_CANAL00_mascara[1:0];
  //   rep29[9:0] = CFG0_CANAL00_mascara[13:4]; CFG0_CANAL00_mascara (some bits) = {3{CFG0_CANAL00_escribe}};
  //   esc_000 = CFG0_CANAL00_escribe; CFG0_CANAL10_1_0[1:0] = CFG0_CANAL10[1:0]; CFG0_CANAL10_2 = CFG0_CANAL10[2];
  //   CFG0_CANAL10_3 = CFG0_CANAL10[3]; CFG0_CANAL10_13_4[9:0] = CFG0_CANAL10[13:4];
  //   CFG0_CANAL10_14 = CFG0_CANAL10[14]; rep52[1:0] = CFG0_CANAL10_mascara[1:0];
  //   rep53[9:0] = CFG0_CANAL10_mascara[13:4]; CFG0_CANAL10_mascara (some bits) = {3{CFG0_CANAL10_escribe}};
  //   esc_014 = CFG0_CANAL10_escribe; CFG0_CANAL20_1_0[1:0] = CFG0_CANAL20[1:0]; CFG0_CANAL20_2 = CFG0_CANAL20[2];
  //   CFG0_CANAL20_3 = CFG0_CANAL20[3]; CFG0_CANAL20_13_4[9:0] = CFG0_CANAL20[13:4];
  //   CFG0_CANAL20_14 = CFG0_CANAL20[14]; rep76[1:0] = CFG0_CANAL20_mascara[1:0];
  //   rep77[9:0] = CFG0_CANAL20_mascara[13:4]; CFG0_CANAL20_mascara (some bits) = {3{CFG0_CANAL20_escribe}};
  //   esc_028 = CFG0_CANAL20_escribe; CFG0_CANAL30_1_0[1:0] = CFG0_CANAL30[1:0]; CFG0_CANAL30_2 = CFG0_CANAL30[2];
  //   CFG0_CANAL30_3 = CFG0_CANAL30[3]; CFG0_CANAL30_13_4[9:0] = CFG0_CANAL30[13:4];
  //   CFG0_CANAL30_14 = CFG0_CANAL30[14]; rep100[1:0] = CFG0_CANAL30_mascara[1:0];
  //   rep101[9:0] = CFG0_CANAL30_mascara[13:4]; CFG0_CANAL30_mascara (some bits) = {3{CFG0_CANAL30_escribe}};
  //   esc_03C = CFG0_CANAL30_escribe; CFG0_CANAL40_1_0[1:0] = CFG0_CANAL40[1:0]; CFG0_CANAL40_2 = CFG0_CANAL40[2];
  //   CFG0_CANAL40_3 = CFG0_CANAL40[3]; CFG0_CANAL40_13_4[9:0] = CFG0_CANAL40[13:4];
  //   CFG0_CANAL40_14 = CFG0_CANAL40[14]; rep124[1:0] = CFG0_CANAL40_mascara[1:0];
  //   rep125[9:0] = CFG0_CANAL40_mascara[13:4]; CFG0_CANAL40_mascara (some bits) = {3{CFG0_CANAL40_escribe}};
  //   esc_050 = CFG0_CANAL40_escribe; CFG0_CANAL50_1_0[1:0] = CFG0_CANAL50[1:0]; CFG0_CANAL50_2 = CFG0_CANAL50[2];
  //   CFG0_CANAL50_3 = CFG0_CANAL50[3]; CFG0_CANAL50_13_4[9:0] = CFG0_CANAL50[13:4];
  //   CFG0_CANAL50_14 = CFG0_CANAL50[14]; rep148[1:0] = CFG0_CANAL50_mascara[1:0];
  //   rep149[9:0] = CFG0_CANAL50_mascara[13:4]; CFG0_CANAL50_mascara (some bits) = {3{CFG0_CANAL50_escribe}};
  //   esc_064 = CFG0_CANAL50_escribe; CFG1_CANAL00_9_0[9:0] = CFG1_CANAL00[9:0];
  //   CFG1_CANAL00_19_10[9:0] = CFG1_CANAL00[19:10]; CFG1_CANAL00_29_20[9:0] = CFG1_CANAL00[29:20];
  //   CFG1_CANAL00_30 = CFG1_CANAL00[30]; CFG1_CANAL00_31 = CFG1_CANAL00[31]; rep41[9:0] = CFG1_CANAL00_mascara[9:0];
  //   rep42[9:0] = CFG1_CANAL00_mascara[19:10]; rep43[9:0] = CFG1_CANAL00_mascara[29:20];
  //   CFG1_CANAL00_mascara[31:30] = {2{CFG1_CANAL00_escribe}}; esc_00C = CFG1_CANAL00_escribe;
  //   CFG1_CANAL10_9_0[9:0] = CFG1_CANAL10[9:0]; CFG1_CANAL10_19_10[9:0] = CFG1_CANAL10[19:10];
  //   CFG1_CANAL10_29_20[9:0] = CFG1_CANAL10[29:20]; CFG1_CANAL10_30 = CFG1_CANAL10[30];
  //   CFG1_CANAL10_31 = CFG1_CANAL10[31]; rep65[9:0] = CFG1_CANAL10_mascara[9:0];
  //   rep66[9:0] = CFG1_CANAL10_mascara[19:10]; rep67[9:0] = CFG1_CANAL10_mascara[29:20];
  //   CFG1_CANAL10_mascara[31:30] = {2{CFG1_CANAL10_escribe}}; esc_020 = CFG1_CANAL10_escribe;
  //   CFG1_CANAL20_9_0[9:0] = CFG1_CANAL20[9:0]; CFG1_CANAL20_19_10[9:0] = CFG1_CANAL20[19:10];
  //   CFG1_CANAL20_29_20[9:0] = CFG1_CANAL20[29:20]; CFG1_CANAL20_30 = CFG1_CANAL20[30];
  //   CFG1_CANAL20_31 = CFG1_CANAL20[31]; rep89[9:0] = CFG1_CANAL20_mascara[9:0];
  //   rep90[9:0] = CFG1_CANAL20_mascara[19:10]; rep91[9:0] = CFG1_CANAL20_mascara[29:20];
  //   CFG1_CANAL20_mascara[31:30] = {2{CFG1_CANAL20_escribe}}; esc_034 = CFG1_CANAL20_escribe;
  //   CFG1_CANAL30_9_0[9:0] = CFG1_CANAL30[9:0]; CFG1_CANAL30_19_10[9:0] = CFG1_CANAL30[19:10];
  //   CFG1_CANAL30_29_20[9:0] = CFG1_CANAL30[29:20]; CFG1_CANAL30_30 = CFG1_CANAL30[30];
  //   CFG1_CANAL30_31 = CFG1_CANAL30[31]; rep113[9:0] = CFG1_CANAL30_mascara[9:0];
  //   rep114[9:0] = CFG1_CANAL30_mascara[19:10]; rep115[9:0] = CFG1_CANAL30_mascara[29:20];
  //   CFG1_CANAL30_mascara[31:30] = {2{CFG1_CANAL30_escribe}}; esc_048 = CFG1_CANAL30_escribe;
  //   CFG1_CANAL40_9_0[9:0] = CFG1_CANAL40[9:0]; CFG1_CANAL40_19_10[9:0] = CFG1_CANAL40[19:10];
  //   CFG1_CANAL40_29_20[9:0] = CFG1_CANAL40[29:20]; CFG1_CANAL40_30 = CFG1_CANAL40[30];
  //   CFG1_CANAL40_31 = CFG1_CANAL40[31]; rep137[9:0] = CFG1_CANAL40_mascara[9:0];
  //   rep138[9:0] = CFG1_CANAL40_mascara[19:10]; rep139[9:0] = CFG1_CANAL40_mascara[29:20];
  //   CFG1_CANAL40_mascara[31:30] = {2{CFG1_CANAL40_escribe}}; esc_05C = CFG1_CANAL40_escribe;
  //   CFG1_CANAL50_9_0[9:0] = CFG1_CANAL50[9:0]; CFG1_CANAL50_19_10[9:0] = CFG1_CANAL50[19:10];
  //   CFG1_CANAL50_29_20[9:0] = CFG1_CANAL50[29:20]; CFG1_CANAL50_30 = CFG1_CANAL50[30];
  //   CFG1_CANAL50_31 = CFG1_CANAL50[31]; rep161[9:0] = CFG1_CANAL50_mascara[9:0];
  //   rep162[9:0] = CFG1_CANAL50_mascara[19:10]; rep163[9:0] = CFG1_CANAL50_mascara[29:20];
  //   CFG1_CANAL50_mascara[31:30] = {2{CFG1_CANAL50_escribe}}; esc_070 = CFG1_CANAL50_escribe;
  //   CFG0_CANAL10_nuevo[14:0] = CFG0_CANAL00_nuevo; CFG0_CANAL20_nuevo[14:0] = CFG0_CANAL00_nuevo;
  //   CFG0_CANAL30_nuevo[14:0] = CFG0_CANAL00_nuevo; CFG0_CANAL40_nuevo[14:0] = CFG0_CANAL00_nuevo;
  //   CFG0_CANAL50_nuevo[14:0] = CFG0_CANAL00_nuevo; CFG1_CANAL00_nuevo (some bits) = CFG0_CANAL00_nuevo;
  //   CFG1_CANAL10_nuevo[31:0] = {CFG1_CANAL00_nuevo[31:16], CFG0_CANAL00_nuevo[14:4], CFG1_CANAL00_nuevo[4], CFG0_CANAL00_nuevo[3:0]};
  //   CFG1_CANAL20_nuevo[31:0] = {CFG1_CANAL00_nuevo[31:16], CFG0_CANAL00_nuevo[14:4], CFG1_CANAL00_nuevo[4], CFG0_CANAL00_nuevo[3:0]};
  //   CFG1_CANAL30_nuevo[31:0] = {CFG1_CANAL00_nuevo[31:16], CFG0_CANAL00_nuevo[14:4], CFG1_CANAL00_nuevo[4], CFG0_CANAL00_nuevo[3:0]};
  //   CFG1_CANAL40_nuevo[31:0] = {CFG1_CANAL00_nuevo[31:16], CFG0_CANAL00_nuevo[14:4], CFG1_CANAL00_nuevo[4], CFG0_CANAL00_nuevo[3:0]};
  //   CFG1_CANAL50_nuevo[31:0] = {CFG1_CANAL00_nuevo[31:16], CFG0_CANAL00_nuevo[14:4], CFG1_CANAL00_nuevo[4], CFG0_CANAL00_nuevo[3:0]};
  //   CFG_RELOJ0_nuevo[1:0] = CFG0_CANAL00_nuevo[1:0];
  //   CFG_TEMP0_nuevo[31:0] = {CFG1_CANAL00_nuevo[23:16], CFG0_CANAL00_nuevo[14:11], CFG0_CANAL00_nuevo[3:0], CFG1_CANAL00_nuevo[23:16], CFG0_CANAL00_nuevo[14:11], CFG0_CANAL00_nuevo[3:0]};
  //   CFG_TEMP1_nuevo[31:0] = {CFG1_CANAL00_nuevo[23:16], CFG0_CANAL00_nuevo[14:11], CFG0_CANAL00_nuevo[3:0], CFG1_CANAL00_nuevo[23:16], CFG0_CANAL00_nuevo[14:11], CFG0_CANAL00_nuevo[3:0]};
  //   dato_escrito[31:0] = {CFG1_CANAL00_nuevo[31:16], CFG0_CANAL00_nuevo[14:4], CFG1_CANAL00_nuevo[4], CFG0_CANAL00_nuevo[3:0]};
  //   dato_escrito_1_0[1:0] = CFG0_CANAL00_nuevo[1:0]; dato_escrito_3_0[3:0] = CFG0_CANAL00_nuevo[3:0];
  //   dato_escrito_9_0[9:0] = {CFG0_CANAL00_nuevo[8:4], CFG1_CANAL00_nuevo[4], CFG0_CANAL00_nuevo[3:0]};
  //   dato_escrito_13_0[13:0] = {CFG0_CANAL00_nuevo[12:4], CFG1_CANAL00_nuevo[4], CFG0_CANAL00_nuevo[3:0]};
  //   dato_escrito_18_0[18:0] = {CFG1_CANAL00_nuevo[18:16], CFG0_CANAL00_nuevo[14:4], CFG1_CANAL00_nuevo[4], CFG0_CANAL00_nuevo[3:0]};
  //   PUNTOS_CANAL00_nuevo[13:0] = {CFG0_CANAL00_nuevo[12:4], CFG1_CANAL00_nuevo[4], CFG0_CANAL00_nuevo[3:0]};
  //   PUNTOS_CANAL01_nuevo[18:0] = {CFG1_CANAL00_nuevo[18:16], CFG0_CANAL00_nuevo[14:4], CFG1_CANAL00_nuevo[4], CFG0_CANAL00_nuevo[3:0]};
  //   PUNTOS_CANAL10_nuevo[13:0] = {CFG0_CANAL00_nuevo[12:4], CFG1_CANAL00_nuevo[4], CFG0_CANAL00_nuevo[3:0]};
  //   PUNTOS_CANAL11_nuevo[18:0] = {CFG1_CANAL00_nuevo[18:16], CFG0_CANAL00_nuevo[14:4], CFG1_CANAL00_nuevo[4], CFG0_CANAL00_nuevo[3:0]};
  //   PUNTOS_CANAL20_nuevo[13:0] = {CFG0_CANAL00_nuevo[12:4], CFG1_CANAL00_nuevo[4], CFG0_CANAL00_nuevo[3:0]};
  //   PUNTOS_CANAL21_nuevo[18:0] = {CFG1_CANAL00_nuevo[18:16], CFG0_CANAL00_nuevo[14:4], CFG1_CANAL00_nuevo[4], CFG0_CANAL00_nuevo[3:0]};
  //   PUNTOS_CANAL30_nuevo[13:0] = {CFG0_CANAL00_nuevo[12:4], CFG1_CANAL00_nuevo[4], CFG0_CANAL00_nuevo[3:0]};
  //   PUNTOS_CANAL31_nuevo[18:0] = {CFG1_CANAL00_nuevo[18:16], CFG0_CANAL00_nuevo[14:4], CFG1_CANAL00_nuevo[4], CFG0_CANAL00_nuevo[3:0]};
  //   PUNTOS_CANAL40_nuevo[13:0] = {CFG0_CANAL00_nuevo[12:4], CFG1_CANAL00_nuevo[4], CFG0_CANAL00_nuevo[3:0]};
  //   PUNTOS_CANAL41_nuevo[18:0] = {CFG1_CANAL00_nuevo[18:16], CFG0_CANAL00_nuevo[14:4], CFG1_CANAL00_nuevo[4], CFG0_CANAL00_nuevo[3:0]};
  //   PUNTOS_CANAL50_nuevo[13:0] = {CFG0_CANAL00_nuevo[12:4], CFG1_CANAL00_nuevo[4], CFG0_CANAL00_nuevo[3:0]};
  //   PUNTOS_CANAL51_nuevo[18:0] = {CFG1_CANAL00_nuevo[18:16], CFG0_CANAL00_nuevo[14:4], CFG1_CANAL00_nuevo[4], CFG0_CANAL00_nuevo[3:0]};
  //   dato_escrito_2 = CFG0_CANAL00_nuevo[2]; dato_escrito_3 = CFG0_CANAL00_nuevo[3];
  //   dato_escrito_4 = CFG1_CANAL00_nuevo[4]; dato_escrito_14_5[9:0] = CFG0_CANAL00_nuevo[13:4];
  //   dato_escrito_19_10[9:0] = {CFG1_CANAL00_nuevo[19:16], CFG0_CANAL00_nuevo[14:9]};
  //   dato_escrito_21_12[9:0] = {CFG1_CANAL00_nuevo[21:16], CFG0_CANAL00_nuevo[14:11]};
  //   dato_escrito_15 = CFG0_CANAL00_nuevo[14]; dato_escrito_16 = CFG1_CANAL00_nuevo[16];
  //   dato_escrito_29_20[9:0] = CFG1_CANAL00_nuevo[29:20]; dato_escrito_22 = CFG1_CANAL00_nuevo[22];
  //   dato_escrito_23 = CFG1_CANAL00_nuevo[23]; dato_escrito_30 = CFG1_CANAL00_nuevo[30];
  //   dato_escrito_31 = CFG1_CANAL00_nuevo[31]; esc_0D0 = CFG_RELOJ0_escribe; rep19[1:0] = CFG_RELOJ0_mascara;
  //   CFG_TEMP0_3_0[3:0] = CFG_TEMP0[3:0]; CFG_TEMP0_13_4[9:0] = CFG_TEMP0[13:4]; CFG_TEMP0_14 = CFG_TEMP0[14];
  //   CFG_TEMP0_15 = CFG_TEMP0[15]; CFG_TEMP0_19_16[3:0] = CFG_TEMP0[19:16]; CFG_TEMP0_29_20[9:0] = CFG_TEMP0[29:20];
  //   CFG_TEMP0_30 = CFG_TEMP0[30]; CFG_TEMP0_31 = CFG_TEMP0[31]; rep1[3:0] = CFG_TEMP0_mascara[3:0];
  //   rep2[9:0] = CFG_TEMP0_mascara[13:4];
  //   CFG_TEMP0_mascara (some bits) = {CFG_TEMP0_mascara[31], CFG_TEMP0_mascara[15]}; esc_0A0 = CFG_TEMP0_mascara[15];
  //   rep3[3:0] = CFG_TEMP0_mascara[19:16]; rep4[9:0] = CFG_TEMP0_mascara[29:20]; esc_0A8 = CFG_TEMP0_mascara[31];
  //   CFG_TEMP1_3_0[3:0] = CFG_TEMP1[3:0]; CFG_TEMP1_13_4[9:0] = CFG_TEMP1[13:4]; CFG_TEMP1_14 = CFG_TEMP1[14];
  //   CFG_TEMP1_15 = CFG_TEMP1[15]; CFG_TEMP1_19_16[3:0] = CFG_TEMP1[19:16]; CFG_TEMP1_29_20[9:0] = CFG_TEMP1[29:20];
  //   CFG_TEMP1_30 = CFG_TEMP1[30]; CFG_TEMP1_31 = CFG_TEMP1[31]; rep10[3:0] = CFG_TEMP1_mascara[3:0];
  //   rep11[9:0] = CFG_TEMP1_mascara[13:4];
  //   CFG_TEMP1_mascara (some bits) = {CFG_TEMP1_mascara[31], CFG_TEMP1_mascara[15]}; esc_0B0 = CFG_TEMP1_mascara[15];
  //   rep12[3:0] = CFG_TEMP1_mascara[19:16]; rep13[9:0] = CFG_TEMP1_mascara[29:20]; esc_0B8 = CFG_TEMP1_mascara[31];
  //   dir_registro_4_0[4:0] = dir_registro[4:0]; dir_registro_9_5[4:0] = dir_registro[9:5];
  //   INT_eventos[9:0] = {fin5, fin4, fin3, fin2, fin1, fin0, desborde_t3, desborde_t2, desborde_t1, desborde_t0};
  //   ovfcnt0 = INT_eventos[10]; ovfcnt1 = INT_eventos[11]; ovfcnt2 = INT_eventos[12]; ovfcnt3 = INT_eventos[13];
  //   ovfcnt4 = INT_eventos[14]; ovfcnt5 = INT_eventos[15]; INT_irq = IRQ; PUNTOS_CANAL00_escribe = esc_004;
  //   rep33[13:0] = PUNTOS_CANAL00_mascara; PUNTOS_CANAL01_escribe = esc_008; rep37[18:0] = PUNTOS_CANAL01_mascara;
  //   PUNTOS_CANAL10_escribe = esc_018; rep57[13:0] = PUNTOS_CANAL10_mascara; PUNTOS_CANAL11_escribe = esc_01C;
  //   rep61[18:0] = PUNTOS_CANAL11_mascara; PUNTOS_CANAL20_escribe = esc_02C; rep81[13:0] = PUNTOS_CANAL20_mascara;
  //   PUNTOS_CANAL21_escribe = esc_030; rep85[18:0] = PUNTOS_CANAL21_mascara; PUNTOS_CANAL30_escribe = esc_040;
  //   rep105[13:0] = PUNTOS_CANAL30_mascara; PUNTOS_CANAL31_escribe = esc_044; rep109[18:0] = PUNTOS_CANAL31_mascara;
  //   PUNTOS_CANAL40_escribe = esc_054; rep129[13:0] = PUNTOS_CANAL40_mascara; PUNTOS_CANAL41_escribe = esc_058;
  //   rep133[18:0] = PUNTOS_CANAL41_mascara; PUNTOS_CANAL50_escribe = esc_068; rep153[13:0] = PUNTOS_CANAL50_mascara;
  //   PUNTOS_CANAL51_escribe = esc_06C; rep157[18:0] = PUNTOS_CANAL51_mascara; PWM0_2 = PWM0; pwm0_t = PWM0;
  //   PWM1_2 = PWM1; pwm1_t = PWM1; PWM2_2 = PWM2; pwm2_t = PWM2; PWM3_2 = PWM3; pwm3_t = PWM3; PWM4_2 = PWM4;
  //   pwm4_t = PWM4; PWM5_2 = PWM5; pwm5_t = PWM5; or214[31:0] = RD

  // Notes on the sheet:
  //   contents of REGISTROS_LEDC_EXISTE (hex, n*v repeats v):
  //   4*1 0 4*1 0 4*1 0 4*1 0 4*1 0 4*1 11*0 1 0 1 0 1 0 1 5*0 1 10*0 1
  //   contents of REGISTROS_LEDC_VALOR_RESET (hex, n*v repeats v):
  //   0 0 0 40000000 4*0 40000000 4*0 40000000 4*0 40000000 4*0 40000000 4*0 40000000 11*0 800000 0 800000
  //   0 800000 0 800000 16*0 19061700
  //   contents of REGISTROS_LEDC_BITS_RW (hex, n*v repeats v):
  //   ffef 3fff 7ffff ffffffff 0 ffef 3fff 7ffff ffffffff 0 ffef 3fff 7ffff ffffffff 0 ffef 3fff 7ffff
  //   ffffffff 0 ffef 3fff 7ffff ffffffff 0 ffef 3fff 7ffff ffffffff 11*0 1ffffff 0 1ffffff 0 1ffffff 0
  //   1ffffff 5*0 80000003 10*0 ffffffff
endmodule

module SPI2 (
  input  CLK,
  input  RST,
  input  SEL,
  input  [9:0] A,
  input  [31:0] WD,
  input  WE,
  input  RE,
  input  MISO,
  output SCK,
  output MOSI,
  output CS0,
  output IRQ,
  output [31:0] RD
);

  wire acceso_buffer, and33, and67, and69, and81, and83, and84, and86, and87, and89, and90, and92, and93,
       and96, and106, and107, and108, and110, and120, and124, bit_comando, bit_dato, bit_direccion,
       byte_recibido, carriles_0, carriles_1, carriles_2, carriles_3, CFG_DATOS0_escribe, CFG_FASES0_escribe,
       CFG_LARGOS0_escribe, CFG_LARGOS1_escribe, CFG_RELOJ0_escribe, cs_activo, DIRECCION0_escribe, empieza,
       eq66, eq68, eq82, eq118, esc_000, esc_01C, esc_014, esc_034, esc_038, escribe, fase_comando,
       fase_datos, fase_direccion, fin_transferencia, flanco_bajada, flanco_subida, gt76, lee, lin_0, lin_1,
       lin_2, lin_3, lin_4, lin_5, lin_6, lin_7, lin_8, lin_9, lin_10, lin_11, lin_12, lin_13, lin_14,
       lin_15, lin_16, lin_17, lin_18, lin_19, lin_20, lin_21, lin_22, lin_23, lin_24, lin_25, lin_26,
       lin_27, lin_28, lin_29, lin_30, lin_31, lt49, lt50, lt57, lt74, mosi_bit, mux64, mux72, not34, not48,
       not58, not62, not63, not75, not77, not109, not111, or46, or59, or61, or65, or71, or73, or85, or88,
       or91, or94, or97, pag_0, pag_1, pag_2, pag_3, pag_4, pag_5, pag_6, pag_7, pag_8, pag_9, pag_10,
       pag_11, pag_12, pag_13, pag_14, pag_15, pag_16, pag_17, pag_18, pag_19, pag_20, pag_21, pag_22,
       pag_23, pag_24, pag_25, pag_26, pag_27, pag_28, pag_29, pag_30, pag_31, r000, r00C, r01C, r03C, r004,
       r010, r014, r018, r020, r034, r038, r040, registros_acceso, registros_existe, sck_interno, tick_medio;
  wire [2:0] not105;
  wire [3:0] dir_buffer, palabra_cpu, sum52, xor100;
  wire [4:0] CFG_FASES0_nuevo, not101, not104, sum102, sum103;
  wire [5:0] and13, and14, CFG_FASES0, CFG_FASES0_sig, not12, qx16, sum54, xor15;
  wire [7:0] byte_actual;
  wire [8:0] cuenta_medio, medio_periodo, mux60, sum56;
  wire [9:0] bit_actual, bit_de_datos, bit_siguiente, bits_comando, bits_datos, bits_direccion, bits_total,
       ciclos_espera, dir_registro, division, fin_direccion, fin_espera, mux70, not79, rep38, rep41, rep44,
       rep47, rep119, sum37, sum40, sum43, sum45, sum80, zx36, zx39, zx42, zx53, zx55;
  wire [9:4] sum78;
  wire [10:0] and8, and9, CFG_RELOJ0, CFG_RELOJ0_sig, not7, qx11, xor10;
  wire [10:1] CFG_RELOJ0_mascara, CFG_RELOJ0_nuevo;
  wire [12:0] and31, and32, CFG_DATOS0, CFG_DATOS0_mascara, CFG_DATOS0_sig, not30;
  wire [12:1] CFG_DATOS0_nuevo;
  wire [15:0] and27, and28, CFG_LARGOS1, CFG_LARGOS1_mascara, CFG_LARGOS1_sig, not26;
  wire [15:10] CFG_LARGOS1_nuevo;
  wire [16:0] and21, and22, CFG_LARGOS0, CFG_LARGOS0_mascara, CFG_LARGOS0_sig, not20, qx24, xor23;
  wire [24:24] cat35;
  wire [26:22] dato_escrito;
  wire [31:0] and3, and4, and99, and114, and116, and117, and123, and127, and129, and131, and133, and135,
       buffer_leido, dato_buffer, DIRECCION0, DIRECCION0_mascara, DIRECCION0_sig, INT_clr, INT_ENA, INT_raw,
       INT_st, not2, not113, not122, or115, registros_a_guardar, registros_bits_fijos, registros_bits_rw,
       registros_guardado, registros_reset_rw, registros_valor, registros_valor_reset, rep98, rep112, rep121,
       rep126, rep128, rep130, rep132, rep134, xor125;
  wire [31:24] cat95;

  Register #(.width(9)) MEDIO (.D(mux60), .en(or61), .Q(cuenta_medio), .clk(CLK), .clr(RST));
  Register #(.width(1)) SCK_2 (.D(mux64), .en(or65), .Q(sck_interno), .clk(CLK), .clr(RST));
  Register #(.width(10)) BIT (.D(mux70), .en(or71), .Q(bit_actual), .clk(CLK), .clr(RST));
  Register #(.width(1)) OCUPADO (.D(mux72), .en(or73), .Q(cat35[24]), .clk(CLK), .clr(RST));
  RAM #(.addrWidth(4), .dataWidth(32), .enables("byte"), .trigger("rising"), .asyncread("true"), .byteenables("byteEnables"), .databus("bibus")) BUFFER_W0_W15 (
    .addr(dir_buffer), .we(or97), .oe(1'b1), .clk(CLK), .din(dato_buffer), .dout(buffer_leido), .be3(or94),
    .be2(or91), .be1(or88), .be0(or85));
  Register #(.width(32)) u_INT_RAW (.D(and116), .en(1'b1), .Q(INT_raw), .clk(CLK), .clr(RST));
  Register #(.width(32)) u_INT_ENA (.D(and117), .en(esc_034), .Q(INT_ENA), .clk(CLK), .clr(RST));
  assign rep119 = {{9{SEL}}, SEL};  // Bit_Extender bit_extender_1
  and and_1 (and120, SEL, WE);
  and and_2 (escribe, WE, SEL);
  and and_3 (lee, RE, SEL);
  ROM #(.addrWidth(10), .dataWidth(1)) u_REGISTROS_EXISTE (.addr(dir_registro), .data(registros_existe));
  ROM #(.addrWidth(10), .dataWidth(32)) u_REGISTROS_VALOR_RESET (.addr(dir_registro), .data(registros_valor_reset));
  ROM #(.addrWidth(10), .dataWidth(32)) u_REGISTROS_BITS_RW (.addr(dir_registro), .data(registros_bits_rw));
  Register #(.width(32)) u_DIRECCION0 (
    .D(DIRECCION0_sig), .en(DIRECCION0_escribe), .Q(DIRECCION0), .clk(CLK), .clr(RST));
  Register #(.width(11)) u_CFG_RELOJ0 (.D(xor10), .en(CFG_RELOJ0_escribe), .Q(qx11), .clk(CLK), .clr(RST));
  Register #(.width(6)) u_CFG_FASES0 (.D(xor15), .en(CFG_FASES0_escribe), .Q(qx16), .clk(CLK), .clr(RST));
  Register #(.width(17)) u_CFG_LARGOS0 (.D(xor23), .en(CFG_LARGOS0_escribe), .Q(qx24), .clk(CLK), .clr(RST));
  Register #(.width(16)) u_CFG_LARGOS1 (
    .D(CFG_LARGOS1_sig), .en(CFG_LARGOS1_escribe), .Q(CFG_LARGOS1), .clk(CLK), .clr(RST));
  Register #(.width(13)) u_CFG_DATOS0 (
    .D(CFG_DATOS0_sig), .en(CFG_DATOS0_escribe), .Q(CFG_DATOS0), .clk(CLK), .clr(RST));
  Register #(.width(8)) RX (.D({cat95[30:24], MISO}), .en(and81), .Q(cat95), .clk(CLK), .clr(RST));
  RAM #(.addrWidth(10), .dataWidth(32), .enables("byte"), .trigger("rising"), .asyncread("true"), .databus("bibus"), .clearpin("true")) REGISTROS (
    .addr(dir_registro), .we(and124), .oe(1'b1), .clk(CLK), .din(registros_a_guardar),
    .dout(registros_guardado), .clr(RST));
  assign CFG_RELOJ0 = qx11 ^ 11'h61;  // XOR_Gate xor_1, 11 bits wide
  assign CFG_FASES0 = qx16 ^ 6'b000001;  // XOR_Gate xor_2, 6 bits wide
  assign CFG_LARGOS0 = qx24 ^ 17'he0f7;  // XOR_Gate xor_3, 17 bits wide
  not not_1 (not34, cat35[24]);
  Adder #(.width(9)) adder_1 (.a(cuenta_medio), .b(9'h1), .out(sum56));  // open: cin, cout
  not not_2 (not62, sck_interno);
  not not_3 (not63, sck_interno);
  Adder #(.width(10)) adder_2 (.a(bit_actual), .b(10'h1), .out(bit_siguiente));  // open: cin, cout
  assign INT_st = INT_raw & INT_ENA;  // AND_Gate and_4, 32 bits wide
  assign dir_registro = A & rep119;  // AND_Gate and_5, 10 bits wide
  assign rep121 = {{31{and120}}, and120};  // Bit_Extender bit_extender_2
  and and_6 (and110, sck_interno, cat35[24]);
  and and_7 (registros_acceso, SEL, registros_existe);
  assign registros_reset_rw = registros_valor_reset & registros_bits_rw;  // AND_Gate and_8, 32 bits wide
  assign not122 = ~registros_bits_rw;  // NOT_Gate not_4, 32 bits wide
  Comparator #(.width(32), .mode("unsigned")) comparator_1 (.a(INT_st), .b({32{1'b0}}), .eq(eq118));  // open: gt, lt
  assign {CFG_FASES0_nuevo[0], CFG_FASES0_nuevo[1], CFG_DATOS0_nuevo[10], CFG_FASES0_nuevo[3], CFG_FASES0_nuevo[4], dato_escrito, CFG_RELOJ0_nuevo[4:1], CFG_RELOJ0_nuevo[10:9], CFG_LARGOS1_nuevo, CFG_DATOS0_nuevo[9:8], CFG_DATOS0_nuevo[11], CFG_DATOS0_nuevo[6:1], CFG_DATOS0_nuevo[12]} = WD & rep121;  // AND_Gate and_9, 32 bits wide
  Adder #(.width(10)) adder_3 (.a(CFG_DATOS0[9:0]), .b(10'h1), .out(sum45));  // open: cin, cout
  Comparator #(.width(10), .mode("unsigned")) comparator_2 (.a(dir_registro), .b(10'h26), .lt(lt74));  // open: gt, eq
  Comparator #(.width(10), .mode("unsigned")) comparator_3 (.a(dir_registro), .b(10'h35), .gt(gt76));  // open: eq, lt
  Adder #(.width(10)) adder_4 (.a(dir_registro), .b(10'h3da), .out({sum78, palabra_cpu}));  // open: cin, cout
  assign xor100 = bit_actual[3:0] ^ 4'b0111;  // XOR_Gate xor_4, 4 bits wide
  not not_5 (not109, CFG_DATOS0[12]);
  xor xor_5 (SCK, and110, CFG_DATOS0[10]);
  assign registros_bits_fijos = registros_valor_reset & not122;  // AND_Gate and_10, 32 bits wide
  and and_11 (and124, escribe, registros_acceso);
  assign xor125 = registros_guardado ^ registros_reset_rw;  // XOR_Gate xor_6, 32 bits wide
  assign rep126 = {{31{registros_acceso}}, registros_acceso};  // Bit_Extender bit_extender_3
  Decoder #(.select(5), .enable("false")) decoder_1 (
    .out0(pag_0), .out1(pag_1), .out2(pag_2), .out3(pag_3), .out4(pag_4), .out5(pag_5), .out6(pag_6),
    .out7(pag_7), .out8(pag_8), .out9(pag_9), .out10(pag_10), .out11(pag_11), .out12(pag_12), .out13(pag_13),
    .out14(pag_14), .out15(pag_15), .out16(pag_16), .out17(pag_17), .out18(pag_18), .out19(pag_19),
    .out20(pag_20), .out21(pag_21), .out22(pag_22), .out23(pag_23), .out24(pag_24), .out25(pag_25),
    .out26(pag_26), .out27(pag_27), .out28(pag_28), .out29(pag_29), .out30(pag_30), .out31(pag_31),
    .sel(dir_registro[9:5]));
  Decoder #(.select(5), .enable("false")) decoder_2 (
    .out0(lin_0), .out1(lin_1), .out2(lin_2), .out3(lin_3), .out4(lin_4), .out5(lin_5), .out6(lin_6),
    .out7(lin_7), .out8(lin_8), .out9(lin_9), .out10(lin_10), .out11(lin_11), .out12(lin_12), .out13(lin_13),
    .out14(lin_14), .out15(lin_15), .out16(lin_16), .out17(lin_17), .out18(lin_18), .out19(lin_19),
    .out20(lin_20), .out21(lin_21), .out22(lin_22), .out23(lin_23), .out24(lin_24), .out25(lin_25),
    .out26(lin_26), .out27(lin_27), .out28(lin_28), .out29(lin_29), .out30(lin_30), .out31(lin_31),
    .sel(dir_registro[4:0]));
  not not_6 (not75, lt74);
  not not_7 (not77, gt76);
  assign zx36 = {{6{1'b0}}, CFG_LARGOS0[16:13]};  // Bit_Extender bit_extender_4
  assign rep38 = {{9{CFG_FASES0[0]}}, CFG_FASES0[0]};  // Bit_Extender bit_extender_5
  assign zx39 = {{5{1'b0}}, CFG_LARGOS0[4:0]};  // Bit_Extender bit_extender_6
  assign rep41 = {{9{CFG_FASES0[1]}}, CFG_FASES0[1]};  // Bit_Extender bit_extender_7
  assign zx42 = {{2{1'b0}}, CFG_LARGOS0[12:5]};  // Bit_Extender bit_extender_8
  assign rep44 = {{9{CFG_FASES0[2]}}, CFG_FASES0[2]};  // Bit_Extender bit_extender_9
  or or_1 (or46, CFG_FASES0[4], CFG_FASES0[3]);
  Adder #(.width(4)) adder_5 (.a(CFG_RELOJ0[4:1]), .b(4'b0001), .out(sum52));  // open: cin, cout
  Adder #(.width(6)) adder_6 (.a(CFG_RELOJ0[10:5]), .b(6'b000001), .out(sum54));  // open: cin, cout
  not not_8 (IRQ, eq118);
  Multiplexer #(.select(1), .width(32), .enable("false")) multiplexer_1 (
    .in0({CFG_FASES0_nuevo[0], CFG_FASES0_nuevo[1], CFG_DATOS0_nuevo[10], CFG_FASES0_nuevo[3], CFG_FASES0_nuevo[4], dato_escrito, CFG_RELOJ0_nuevo[4:1], CFG_RELOJ0_nuevo[10:9], CFG_LARGOS1_nuevo, CFG_DATOS0_nuevo[9:8], CFG_DATOS0_nuevo[11], CFG_DATOS0_nuevo[6:1], CFG_DATOS0_nuevo[12]}),
    .in1({cat95, cat95, cat95, cat95}), .out(dato_buffer), .sel(cat35[24]));
  Multiplexer #(.select(4), .width(1), .enable("false")) multiplexer_2 (
    .in0(CFG_LARGOS1[0]), .in1(CFG_LARGOS1[1]), .in2(CFG_LARGOS1[2]), .in3(CFG_LARGOS1[3]),
    .in4(CFG_LARGOS1[4]), .in5(CFG_LARGOS1[5]), .in6(CFG_LARGOS1[6]), .in7(CFG_LARGOS1[7]),
    .in8(CFG_LARGOS1[8]), .in9(CFG_LARGOS1[9]), .in10(CFG_LARGOS1[10]), .in11(CFG_LARGOS1[11]),
    .in12(CFG_LARGOS1[12]), .in13(CFG_LARGOS1[13]), .in14(CFG_LARGOS1[14]), .in15(CFG_LARGOS1[15]),
    .out(bit_comando), .sel(xor100));
  and and_12 (cs_activo, cat35[24], not109);
  assign and117 = {CFG_FASES0_nuevo[0], CFG_FASES0_nuevo[1], CFG_DATOS0_nuevo[10], CFG_FASES0_nuevo[3], CFG_FASES0_nuevo[4], dato_escrito, CFG_RELOJ0_nuevo[4:1], CFG_RELOJ0_nuevo[10:9], CFG_LARGOS1_nuevo, CFG_DATOS0_nuevo[9:8], CFG_DATOS0_nuevo[11], CFG_DATOS0_nuevo[6:1], CFG_DATOS0_nuevo[12]} & 32'h1000;  // AND_Gate and_13, 32 bits wide
  assign and123 = {CFG_FASES0_nuevo[0], CFG_FASES0_nuevo[1], CFG_DATOS0_nuevo[10], CFG_FASES0_nuevo[3], CFG_FASES0_nuevo[4], dato_escrito, CFG_RELOJ0_nuevo[4:1], CFG_RELOJ0_nuevo[10:9], CFG_LARGOS1_nuevo, CFG_DATOS0_nuevo[9:8], CFG_DATOS0_nuevo[11], CFG_DATOS0_nuevo[6:1], CFG_DATOS0_nuevo[12]} & registros_bits_rw;  // AND_Gate and_14, 32 bits wide
  assign registros_valor = xor125 | registros_bits_fijos;  // OR_Gate or_2, 32 bits wide
  and and_15 (r004, SEL, pag_0, lin_1);
  and and_16 (r00C, SEL, pag_0, lin_3);
  and and_17 (r010, SEL, pag_0, lin_4);
  and and_18 (r014, SEL, pag_0, lin_5);
  and and_19 (r018, SEL, pag_0, lin_6);
  and and_20 (r01C, SEL, pag_0, lin_7);
  and and_21 (r020, SEL, pag_0, lin_8);
  and and_22 (r000, SEL, pag_0, lin_0);
  Adder #(.width(10)) adder_7 (.a(zx36), .b(10'h1), .out(sum37));  // open: cin, cout
  Adder #(.width(10)) adder_8 (.a(zx39), .b(10'h1), .out(sum40));  // open: cin, cout
  Adder #(.width(10)) adder_9 (.a(zx42), .b(10'h1), .out(sum43));  // open: cin, cout
  assign rep47 = {{9{or46}}, or46};  // Bit_Extender bit_extender_10
  assign zx53 = {{6{1'b0}}, sum52};  // Bit_Extender bit_extender_11
  assign zx55 = {{4{1'b0}}, sum54};  // Bit_Extender bit_extender_12
  and and_23 (acceso_buffer, SEL, not75, not77);
  not not_9 (not111, cs_activo);
  and and_24 (r038, SEL, pag_0, lin_14);
  and and_25 (r034, SEL, pag_0, lin_13);
  and and_26 (r03C, SEL, pag_0, lin_15);
  and and_27 (r040, SEL, pag_0, lin_16);
  assign registros_a_guardar = and123 ^ registros_reset_rw;  // XOR_Gate xor_7, 32 bits wide
  assign and127 = registros_valor & rep126;  // AND_Gate and_28, 32 bits wide
  and and_29 (DIRECCION0_escribe, escribe, r004);
  and and_30 (CFG_RELOJ0_escribe, escribe, r00C);
  and and_31 (CFG_FASES0_escribe, escribe, r010);
  and and_32 (esc_014, escribe, r014);
  and and_33 (CFG_LARGOS1_escribe, escribe, r018);
  and and_34 (esc_01C, escribe, r01C);
  and and_35 (CFG_DATOS0_mascara[12], escribe, r020);
  and and_36 (esc_000, escribe, r000);
  assign bits_comando = sum37 & rep38;  // AND_Gate and_37, 10 bits wide
  assign bits_direccion = sum40 & rep41;  // AND_Gate and_38, 10 bits wide
  assign ciclos_espera = sum43 & rep44;  // AND_Gate and_39, 10 bits wide
  assign bits_datos = sum45 & rep47;  // AND_Gate and_40, 10 bits wide
  Multiplier #(.width(10)) multiplier_1 (.a(zx53), .b(zx55), .out(division), .cin({10{1'b0}}));  // open: cout
  and and_41 (esc_038, escribe, r038);
  and and_42 (esc_034, escribe, r034);
  assign rep128 = {{31{r000}}, r000};  // Bit_Extender bit_extender_13
  assign rep130 = {{31{r034}}, r034};  // Bit_Extender bit_extender_14
  assign rep132 = {{31{r03C}}, r03C};  // Bit_Extender bit_extender_15
  assign rep134 = {{31{r040}}, r040};  // Bit_Extender bit_extender_16
  and and_43 (and83, escribe, acceso_buffer);
  and and_44 (and86, escribe, acceso_buffer);
  and and_45 (and89, escribe, acceso_buffer);
  and and_46 (and92, escribe, acceso_buffer);
  and and_47 (and96, escribe, acceso_buffer);
  assign rep98 = {{31{acceso_buffer}}, acceso_buffer};  // Bit_Extender bit_extender_17
  xor xor_8 (CS0, not111, CFG_DATOS0[11]);
  assign DIRECCION0_mascara = {{31{DIRECCION0_escribe}}, DIRECCION0_escribe};  // Bit_Extender bit_extender_18
  assign CFG_RELOJ0_mascara[4:1] = {{3{CFG_RELOJ0_escribe}}, CFG_RELOJ0_escribe};  // Bit_Extender bit_extender_19
  assign CFG_RELOJ0_mascara[10:5] = {{5{CFG_RELOJ0_escribe}}, CFG_RELOJ0_escribe};  // Bit_Extender bit_extender_20
  assign CFG_LARGOS0_mascara[4:0] = {{4{esc_014}}, esc_014};  // Bit_Extender bit_extender_21
  assign CFG_LARGOS0_mascara[12:5] = {{7{esc_014}}, esc_014};  // Bit_Extender bit_extender_22
  assign CFG_LARGOS0_mascara[16:13] = {{3{CFG_LARGOS1_escribe}}, CFG_LARGOS1_escribe};  // Bit_Extender bit_extender_23
  or or_3 (CFG_LARGOS0_escribe, esc_014, CFG_LARGOS1_escribe);
  assign CFG_LARGOS1_mascara = {{15{CFG_LARGOS1_escribe}}, CFG_LARGOS1_escribe};  // Bit_Extender bit_extender_24
  assign CFG_DATOS0_mascara[9:0] = {{9{esc_01C}}, esc_01C};  // Bit_Extender bit_extender_25
  or or_4 (CFG_DATOS0_escribe, esc_01C, CFG_DATOS0_mascara[12]);
  and and_48 (and33, esc_000, dato_escrito[24]);
  Adder #(.width(10)) adder_10 (.a(bits_comando), .b(bits_direccion), .out(fin_direccion));  // open: cin, cout
  Comparator #(.width(10), .mode("unsigned")) comparator_4 (
    .a(bit_actual), .b(bits_comando), .lt(fase_comando));  // open: gt, eq
  assign and99 = buffer_leido & rep98;  // AND_Gate and_49, 32 bits wide
  assign rep112 = {{31{esc_038}}, esc_038};  // Bit_Extender bit_extender_26
  assign and129 = {{7{1'b0}}, cat35[24], {24{1'b0}}} & rep128;  // AND_Gate and_50, 32 bits wide
  assign and131 = INT_ENA & rep130;  // AND_Gate and_51, 32 bits wide
  assign and133 = INT_raw & rep132;  // AND_Gate and_52, 32 bits wide
  assign and135 = INT_st & rep134;  // AND_Gate and_53, 32 bits wide
  assign not12 = ~{6{CFG_FASES0_escribe}};  // NOT_Gate not_10, 6 bits wide
  and and_54 (empieza, and33, not34);
  Adder #(.width(10)) adder_11 (.a(fin_direccion), .b(ciclos_espera), .out(fin_espera));  // open: cin, cout
  not not_11 (not48, fase_comando);
  Comparator #(.width(10), .mode("unsigned")) comparator_5 (
    .a(bit_actual), .b(fin_direccion), .lt(lt49));  // open: gt, eq
  Multiplexer #(.select(1), .width(9), .enable("false")) multiplexer_3 (
    .in0(division[9:1]), .in1({9{1'b0}}), .out(medio_periodo), .sel(CFG_RELOJ0[0]));
  assign not101 = ~bits_comando[4:0];  // NOT_Gate not_12, 5 bits wide
  and and_55 (and106, fase_comando, bit_comando);
  assign INT_clr = {CFG_FASES0_nuevo[0], CFG_FASES0_nuevo[1], CFG_DATOS0_nuevo[10], CFG_FASES0_nuevo[3], CFG_FASES0_nuevo[4], dato_escrito, CFG_RELOJ0_nuevo[4:1], CFG_RELOJ0_nuevo[10:9], CFG_LARGOS1_nuevo, CFG_DATOS0_nuevo[9:8], CFG_DATOS0_nuevo[11], CFG_DATOS0_nuevo[6:1], CFG_DATOS0_nuevo[12]} & rep112;  // AND_Gate and_56, 32 bits wide
  assign RD = and129 | and131 | and133 | and135 | and99 | and127;  // OR_Gate or_5, 32 bits wide
  assign and14 = {CFG_DATOS0_nuevo[12], CFG_FASES0_nuevo[4:3], CFG_DATOS0_nuevo[10], CFG_FASES0_nuevo[1:0]} & {6{CFG_FASES0_escribe}};  // AND_Gate and_57, 6 bits wide
  and and_58 (fase_direccion, not48, lt49);
  Multiplexer #(.select(1), .width(1), .enable("false")) multiplexer_4 (
    .in0(not63), .in1(1'b0), .out(mux64), .sel(empieza));
  Multiplexer #(.select(1), .width(1), .enable("false")) multiplexer_5 (
    .in0(1'b0), .in1(1'b1), .out(mux72), .sel(empieza));
  assign not113 = ~INT_clr;  // NOT_Gate not_13, 32 bits wide
  assign not2 = ~DIRECCION0_mascara;  // NOT_Gate not_14, 32 bits wide
  assign and4 = {CFG_FASES0_nuevo[0], CFG_FASES0_nuevo[1], CFG_DATOS0_nuevo[10], CFG_FASES0_nuevo[3], CFG_FASES0_nuevo[4], dato_escrito, CFG_RELOJ0_nuevo[4:1], CFG_RELOJ0_nuevo[10:9], CFG_LARGOS1_nuevo, CFG_DATOS0_nuevo[9:8], CFG_DATOS0_nuevo[11], CFG_DATOS0_nuevo[6:1], CFG_DATOS0_nuevo[12]} & DIRECCION0_mascara;  // AND_Gate and_59, 32 bits wide
  assign not7 = ~{CFG_RELOJ0_mascara, CFG_RELOJ0_escribe};  // NOT_Gate not_15, 11 bits wide
  assign and9 = {CFG_RELOJ0_nuevo[10:9], CFG_LARGOS1_nuevo[15:12], CFG_RELOJ0_nuevo[4:1], CFG_FASES0_nuevo[0]} & {CFG_RELOJ0_mascara, CFG_RELOJ0_escribe};  // AND_Gate and_60, 11 bits wide
  assign and13 = CFG_FASES0 & not12;  // AND_Gate and_61, 6 bits wide
  assign not20 = ~CFG_LARGOS0_mascara;  // NOT_Gate not_16, 17 bits wide
  assign not26 = ~CFG_LARGOS1_mascara;  // NOT_Gate not_17, 16 bits wide
  assign not30 = ~{{3{CFG_DATOS0_mascara[12]}}, CFG_DATOS0_mascara[9:0]};  // NOT_Gate not_18, 13 bits wide
  assign and32 = {CFG_DATOS0_nuevo[12:8], CFG_DATOS0_nuevo[11], CFG_DATOS0_nuevo[6:1], CFG_DATOS0_nuevo[12]} & {{3{CFG_DATOS0_mascara[12]}}, CFG_DATOS0_mascara[9:0]};  // AND_Gate and_62, 13 bits wide
  Adder #(.width(10)) adder_12 (.a(fin_espera), .b(bits_datos), .out(bits_total));  // open: cin, cout
  Comparator #(.width(10), .mode("unsigned")) comparator_6 (.a(bit_actual), .b(fin_espera), .lt(lt50));  // open: gt, eq
  Comparator #(.width(9), .mode("unsigned")) comparator_7 (.a(sum56), .b(medio_periodo), .lt(lt57));  // open: gt, eq
  or or_6 (or61, cat35[24], empieza);
  Multiplexer #(.select(1), .width(10), .enable("false")) multiplexer_6 (
    .in0(bit_siguiente), .in1({10{1'b0}}), .out(mux70), .sel(empieza));
  assign not79 = ~fin_espera;  // NOT_Gate not_19, 10 bits wide
  Adder #(.width(5)) adder_13 (.a(not101), .b(5'b00001), .out(sum102));  // open: cin, cout
  assign and22 = {CFG_FASES0_nuevo[0], CFG_FASES0_nuevo[1], CFG_DATOS0_nuevo[10], CFG_FASES0_nuevo[3], CFG_DATOS0_nuevo[11], CFG_DATOS0_nuevo[6:1], CFG_DATOS0_nuevo[12], CFG_FASES0_nuevo[0], CFG_FASES0_nuevo[1], CFG_DATOS0_nuevo[10], CFG_FASES0_nuevo[3], CFG_FASES0_nuevo[4]} & CFG_LARGOS0_mascara;  // AND_Gate and_63, 17 bits wide
  assign and28 = {CFG_LARGOS1_nuevo, CFG_DATOS0_nuevo[9:8], CFG_DATOS0_nuevo[11], CFG_DATOS0_nuevo[6:1], CFG_DATOS0_nuevo[12]} & CFG_LARGOS1_mascara;  // AND_Gate and_64, 16 bits wide
  assign CFG_FASES0_sig = and13 | and14;  // OR_Gate or_7, 6 bits wide
  not not_20 (fase_datos, lt50);
  not not_21 (not58, lt57);
  Adder #(.width(10)) adder_14 (.a(not79), .b(10'h1), .out(sum80));  // open: cin, cout
  assign and114 = INT_raw & not113;  // AND_Gate and_65, 32 bits wide
  assign and3 = DIRECCION0 & not2;  // AND_Gate and_66, 32 bits wide
  assign and8 = CFG_RELOJ0 & not7;  // AND_Gate and_67, 11 bits wide
  assign and21 = CFG_LARGOS0 & not20;  // AND_Gate and_68, 17 bits wide
  assign and27 = CFG_LARGOS1 & not26;  // AND_Gate and_69, 16 bits wide
  assign and31 = CFG_DATOS0 & not30;  // AND_Gate and_70, 13 bits wide
  Comparator #(.width(10), .mode("unsigned")) comparator_8 (
    .a(bit_siguiente), .b(bits_total), .eq(eq66));  // open: gt, lt
  Comparator #(.width(10), .mode("unsigned")) comparator_9 (.a(bits_total), .b({10{1'b0}}), .eq(eq68));  // open: gt, lt
  Adder #(.width(5)) adder_15 (.a(bit_actual[4:0]), .b(sum102), .out(sum103));  // open: cin, cout
  assign DIRECCION0_sig = and3 | and4;  // OR_Gate or_8, 32 bits wide
  assign CFG_RELOJ0_sig = and8 | and9;  // OR_Gate or_9, 11 bits wide
  assign CFG_LARGOS0_sig = and21 | and22;  // OR_Gate or_10, 17 bits wide
  assign CFG_LARGOS1_sig = and27 | and28;  // OR_Gate or_11, 16 bits wide
  assign CFG_DATOS0_sig = and31 | and32;  // OR_Gate or_12, 13 bits wide
  and and_71 (tick_medio, cat35[24], not58);
  and and_72 (and69, empieza, eq68);
  Adder #(.width(10)) adder_16 (.a(bit_actual), .b(sum80), .out(bit_de_datos));  // open: cin, cout
  assign not104 = ~sum103;  // NOT_Gate not_22, 5 bits wide
  assign xor15 = CFG_FASES0_sig ^ 6'b000001;  // XOR_Gate xor_9, 6 bits wide
  assign xor10 = CFG_RELOJ0_sig ^ 11'h61;  // XOR_Gate xor_10, 11 bits wide
  assign xor23 = CFG_LARGOS0_sig ^ 17'he0f7;  // XOR_Gate xor_11, 17 bits wide
  or or_13 (or59, tick_medio, empieza);
  and and_73 (flanco_subida, tick_medio, not62);
  and and_74 (flanco_bajada, tick_medio, sck_interno);
  or or_14 (or65, tick_medio, empieza);
  Multiplexer #(.select(5), .width(1), .enable("false")) multiplexer_7 (
    .in0(DIRECCION0[0]), .in1(DIRECCION0[1]), .in2(DIRECCION0[2]), .in3(DIRECCION0[3]), .in4(DIRECCION0[4]),
    .in5(DIRECCION0[5]), .in6(DIRECCION0[6]), .in7(DIRECCION0[7]), .in8(DIRECCION0[8]), .in9(DIRECCION0[9]),
    .in10(DIRECCION0[10]), .in11(DIRECCION0[11]), .in12(DIRECCION0[12]), .in13(DIRECCION0[13]),
    .in14(DIRECCION0[14]), .in15(DIRECCION0[15]), .in16(DIRECCION0[16]), .in17(DIRECCION0[17]),
    .in18(DIRECCION0[18]), .in19(DIRECCION0[19]), .in20(DIRECCION0[20]), .in21(DIRECCION0[21]),
    .in22(DIRECCION0[22]), .in23(DIRECCION0[23]), .in24(DIRECCION0[24]), .in25(DIRECCION0[25]),
    .in26(DIRECCION0[26]), .in27(DIRECCION0[27]), .in28(DIRECCION0[28]), .in29(DIRECCION0[29]),
    .in30(DIRECCION0[30]), .in31(DIRECCION0[31]), .out(bit_direccion), .sel(not104));
  Multiplexer #(.select(1), .width(9), .enable("false")) multiplexer_8 (
    .in0(sum56), .in1({9{1'b0}}), .out(mux60), .sel(or59));
  and and_75 (and67, flanco_bajada, eq66);
  or or_15 (or71, flanco_bajada, empieza);
  and and_76 (and81, flanco_subida, fase_datos, CFG_FASES0[3]);
  assign not105 = ~bit_de_datos[2:0];  // NOT_Gate not_23, 3 bits wide
  and and_77 (and107, fase_direccion, bit_direccion);
  Comparator #(.width(3), .mode("unsigned")) comparator_10 (
    .a(bit_de_datos[2:0]), .b(3'b111), .eq(eq82));  // open: gt, lt
  Decoder #(.select(2), .enable("false")) decoder_3 (
    .out0(carriles_0), .out1(carriles_1), .out2(carriles_2), .out3(carriles_3), .sel(bit_de_datos[4:3]));
  or or_16 (fin_transferencia, and67, and69);
  Multiplexer #(.select(1), .width(4), .enable("false")) multiplexer_9 (
    .in0(palabra_cpu), .in1(bit_de_datos[8:5]), .out(dir_buffer), .sel(cat35[24]));
  and and_78 (byte_recibido, flanco_bajada, fase_datos, CFG_FASES0[3], eq82);
  Multiplexer #(.select(2), .width(8), .enable("false")) multiplexer_10 (
    .in0(buffer_leido[7:0]), .in1(buffer_leido[15:8]), .in2(buffer_leido[23:16]), .in3(buffer_leido[31:24]),
    .out(byte_actual), .sel(bit_de_datos[4:3]));
  or or_17 (or73, empieza, fin_transferencia);
  and and_79 (and84, byte_recibido, carriles_0);
  and and_80 (and87, byte_recibido, carriles_1);
  and and_81 (and90, byte_recibido, carriles_2);
  and and_82 (and93, byte_recibido, carriles_3);
  or or_18 (or97, and96, byte_recibido);
  or or_19 (or85, and83, and84);
  or or_20 (or88, and86, and87);
  or or_21 (or91, and89, and90);
  or or_22 (or94, and92, and93);
  Multiplexer #(.select(3), .width(1), .enable("false")) multiplexer_11 (
    .in0(byte_actual[0]), .in1(byte_actual[1]), .in2(byte_actual[2]), .in3(byte_actual[3]),
    .in4(byte_actual[4]), .in5(byte_actual[5]), .in6(byte_actual[6]), .in7(byte_actual[7]), .out(bit_dato),
    .sel(not105));
  assign or115 = and114 | {{19{1'b0}}, fin_transferencia, {12{1'b0}}};  // OR_Gate or_23, 32 bits wide
  assign and116 = or115 & 32'h1000;  // AND_Gate and_83, 32 bits wide
  and and_84 (and108, fase_datos, CFG_FASES0[4], bit_dato);
  or or_24 (mosi_bit, and106, and107, and108);
  and and_85 (MOSI, mosi_bit, cat35[24]);

  // Other names for the same wires on the sheet: bit_actual_3_0[3:0] = bit_actual[3:0];
  //   bit_actual_4_0[4:0] = bit_actual[4:0]; bit_de_datos_2_0[2:0] = bit_de_datos[2:0];
  //   byte_de_datos[5:0] = bit_de_datos[8:3]; carril[1:0] = bit_de_datos[4:3]; palabra_motor[3:0] = bit_de_datos[8:5];
  //   bits_comando_4_0[4:0] = bits_comando[4:0]; buffer_leido_7_0[7:0] = buffer_leido[7:0];
  //   buffer_leido_15_8[7:0] = buffer_leido[15:8]; buffer_leido_23_16[7:0] = buffer_leido[23:16];
  //   buffer_leido_31_24[7:0] = buffer_leido[31:24]; byte_actual_0 = byte_actual[0]; byte_actual_1 = byte_actual[1];
  //   byte_actual_2 = byte_actual[2]; byte_actual_3 = byte_actual[3]; byte_actual_4 = byte_actual[4];
  //   byte_actual_5 = byte_actual[5]; byte_actual_6 = byte_actual[6]; byte_actual_7 = byte_actual[7];
  //   ocupado = cat35[24]; cat95[23:0] = {cat95, cat95, cat95}; recibido[7:0] = cat95;
  //   CFG_DATOS0_9_0[9:0] = CFG_DATOS0[9:0]; CFG_DATOS0_10 = CFG_DATOS0[10]; CFG_DATOS0_11 = CFG_DATOS0[11];
  //   CFG_DATOS0_12 = CFG_DATOS0[12]; rep29[9:0] = CFG_DATOS0_mascara[9:0];
  //   CFG_DATOS0_mascara[11:10] = {2{CFG_DATOS0_mascara[12]}}; esc_020 = CFG_DATOS0_mascara[12];
  //   CFG_LARGOS0_nuevo[16:0] = {CFG_FASES0_nuevo[0], CFG_FASES0_nuevo[1], CFG_DATOS0_nuevo[10], CFG_FASES0_nuevo[3], CFG_DATOS0_nuevo[11], CFG_DATOS0_nuevo[6:1], CFG_DATOS0_nuevo[12], CFG_FASES0_nuevo[0], CFG_FASES0_nuevo[1], CFG_DATOS0_nuevo[10], CFG_FASES0_nuevo[3], CFG_FASES0_nuevo[4]};
  //   CFG_LARGOS1_nuevo[9:0] = {CFG_DATOS0_nuevo[9:8], CFG_DATOS0_nuevo[11], CFG_DATOS0_nuevo[6:1], CFG_DATOS0_nuevo[12]};
  //   dato_escrito (some bits) = {CFG_FASES0_nuevo[0], CFG_FASES0_nuevo[1], CFG_DATOS0_nuevo[10], CFG_FASES0_nuevo[3], CFG_FASES0_nuevo[4], CFG_RELOJ0_nuevo[4:1], CFG_RELOJ0_nuevo[10:9], CFG_LARGOS1_nuevo, CFG_DATOS0_nuevo[9:8], CFG_DATOS0_nuevo[11], CFG_DATOS0_nuevo[6:1], CFG_DATOS0_nuevo[12]};
  //   dato_escrito_7_0[7:0] = {CFG_DATOS0_nuevo[11], CFG_DATOS0_nuevo[6:1], CFG_DATOS0_nuevo[12]};
  //   dato_escrito_9_0[9:0] = {CFG_DATOS0_nuevo[9:8], CFG_DATOS0_nuevo[11], CFG_DATOS0_nuevo[6:1], CFG_DATOS0_nuevo[12]};
  //   dato_escrito_15_0[15:0] = {CFG_LARGOS1_nuevo, CFG_DATOS0_nuevo[9:8], CFG_DATOS0_nuevo[11], CFG_DATOS0_nuevo[6:1], CFG_DATOS0_nuevo[12]};
  //   DIRECCION0_nuevo[31:0] = {CFG_FASES0_nuevo[0], CFG_FASES0_nuevo[1], CFG_DATOS0_nuevo[10], CFG_FASES0_nuevo[3], CFG_FASES0_nuevo[4], dato_escrito, CFG_RELOJ0_nuevo[4:1], CFG_RELOJ0_nuevo[10:9], CFG_LARGOS1_nuevo, CFG_DATOS0_nuevo[9:8], CFG_DATOS0_nuevo[11], CFG_DATOS0_nuevo[6:1], CFG_DATOS0_nuevo[12]};
  //   CFG_FASES0_nuevo (some bits) = {CFG_DATOS0_nuevo[12], CFG_DATOS0_nuevo[10]};
  //   dato_escrito_29 = CFG_DATOS0_nuevo[10];
  //   dato_escrito_31_27[4:0] = {CFG_FASES0_nuevo[0], CFG_FASES0_nuevo[1], CFG_DATOS0_nuevo[10], CFG_FASES0_nuevo[3], CFG_FASES0_nuevo[4]};
  //   dato_escrito_31_28[3:0] = {CFG_FASES0_nuevo[0], CFG_FASES0_nuevo[1], CFG_DATOS0_nuevo[10], CFG_FASES0_nuevo[3]};
  //   CFG_DATOS0_nuevo (some bits) = {CFG_DATOS0_nuevo[11], CFG_DATOS0_nuevo[12]};
  //   dato_escrito_7 = CFG_DATOS0_nuevo[11]; dato_escrito_0 = CFG_DATOS0_nuevo[12]; CFG_FASES0_0 = CFG_FASES0[0];
  //   CFG_FASES0_1 = CFG_FASES0[1]; CFG_FASES0_2 = CFG_FASES0[2]; CFG_FASES0_3 = CFG_FASES0[3];
  //   CFG_FASES0_4 = CFG_FASES0[4]; CFG_FASES0_5 = CFG_FASES0[5]; CFG_FASES0_mascara[5:0] = {6{CFG_FASES0_escribe}};
  //   esc_010 = CFG_FASES0_escribe; CFG_LARGOS0_4_0[4:0] = CFG_LARGOS0[4:0];
  //   CFG_LARGOS0_12_5[7:0] = CFG_LARGOS0[12:5]; CFG_LARGOS0_16_13[3:0] = CFG_LARGOS0[16:13];
  //   rep17[4:0] = CFG_LARGOS0_mascara[4:0]; rep18[7:0] = CFG_LARGOS0_mascara[12:5];
  //   rep19[3:0] = CFG_LARGOS0_mascara[16:13]; dato_escrito_27 = CFG_FASES0_nuevo[4];
  //   dato_escrito_28 = CFG_FASES0_nuevo[3]; dato_escrito_30 = CFG_FASES0_nuevo[1];
  //   CFG_RELOJ0_nuevo (some bits) = {CFG_LARGOS1_nuevo[15:12], CFG_FASES0_nuevo[0]};
  //   dato_escrito_31 = CFG_FASES0_nuevo[0]; CFG_LARGOS1_0 = CFG_LARGOS1[0]; CFG_LARGOS1_1 = CFG_LARGOS1[1];
  //   CFG_LARGOS1_2 = CFG_LARGOS1[2]; CFG_LARGOS1_3 = CFG_LARGOS1[3]; CFG_LARGOS1_4 = CFG_LARGOS1[4];
  //   CFG_LARGOS1_5 = CFG_LARGOS1[5]; CFG_LARGOS1_6 = CFG_LARGOS1[6]; CFG_LARGOS1_7 = CFG_LARGOS1[7];
  //   CFG_LARGOS1_8 = CFG_LARGOS1[8]; CFG_LARGOS1_9 = CFG_LARGOS1[9]; CFG_LARGOS1_10 = CFG_LARGOS1[10];
  //   CFG_LARGOS1_11 = CFG_LARGOS1[11]; CFG_LARGOS1_12 = CFG_LARGOS1[12]; CFG_LARGOS1_13 = CFG_LARGOS1[13];
  //   CFG_LARGOS1_14 = CFG_LARGOS1[14]; CFG_LARGOS1_15 = CFG_LARGOS1[15]; esc_018 = CFG_LARGOS1_escribe;
  //   rep25[15:0] = CFG_LARGOS1_mascara; dato_escrito_17_12[5:0] = {CFG_RELOJ0_nuevo[10:9], CFG_LARGOS1_nuevo[15:12]};
  //   CFG_RELOJ0_0 = CFG_RELOJ0[0]; CFG_RELOJ0_4_1[3:0] = CFG_RELOJ0[4:1]; CFG_RELOJ0_10_5[5:0] = CFG_RELOJ0[10:5];
  //   CFG_RELOJ0_mascara[0] = CFG_RELOJ0_escribe; esc_00C = CFG_RELOJ0_escribe; rep5[3:0] = CFG_RELOJ0_mascara[4:1];
  //   rep6[5:0] = CFG_RELOJ0_mascara[10:5]; dato_escrito_21_18[3:0] = CFG_RELOJ0_nuevo[4:1]; cs_pin = CS0;
  //   dir_registro_4_0[4:0] = dir_registro[4:0]; dir_registro_9_5[4:0] = dir_registro[9:5];
  //   DIRECCION0_0 = DIRECCION0[0]; DIRECCION0_1 = DIRECCION0[1]; DIRECCION0_2 = DIRECCION0[2];
  //   DIRECCION0_3 = DIRECCION0[3]; DIRECCION0_4 = DIRECCION0[4]; DIRECCION0_5 = DIRECCION0[5];
  //   DIRECCION0_6 = DIRECCION0[6]; DIRECCION0_7 = DIRECCION0[7]; DIRECCION0_8 = DIRECCION0[8];
  //   DIRECCION0_9 = DIRECCION0[9]; DIRECCION0_10 = DIRECCION0[10]; DIRECCION0_11 = DIRECCION0[11];
  //   DIRECCION0_12 = DIRECCION0[12]; DIRECCION0_13 = DIRECCION0[13]; DIRECCION0_14 = DIRECCION0[14];
  //   DIRECCION0_15 = DIRECCION0[15]; DIRECCION0_16 = DIRECCION0[16]; DIRECCION0_17 = DIRECCION0[17];
  //   DIRECCION0_18 = DIRECCION0[18]; DIRECCION0_19 = DIRECCION0[19]; DIRECCION0_20 = DIRECCION0[20];
  //   DIRECCION0_21 = DIRECCION0[21]; DIRECCION0_22 = DIRECCION0[22]; DIRECCION0_23 = DIRECCION0[23];
  //   DIRECCION0_24 = DIRECCION0[24]; DIRECCION0_25 = DIRECCION0[25]; DIRECCION0_26 = DIRECCION0[26];
  //   DIRECCION0_27 = DIRECCION0[27]; DIRECCION0_28 = DIRECCION0[28]; DIRECCION0_29 = DIRECCION0[29];
  //   DIRECCION0_30 = DIRECCION0[30]; DIRECCION0_31 = DIRECCION0[31]; esc_004 = DIRECCION0_escribe;
  //   rep1[31:0] = DIRECCION0_mascara; dato_escrito_24 = dato_escrito[24]; division_9_1[8:0] = division[9:1];
  //   not51 = fase_datos; INT_eventos[12] = fin_transferencia; INT_irq = IRQ; mosi_pin = MOSI; or136[31:0] = RD;
  //   recibido_sig[7:0] = {cat95[30:24], MISO}; recibido_6_0[6:0] = cat95[30:24]; sck_pin = SCK;
  //   sum78[3:0] = palabra_cpu

  // Notes on the sheet:
  //   contents of REGISTROS_EXISTE (hex, n*v repeats v):
  //   13*1 43*0 1 1 1 0 1
  //   contents of REGISTROS_VALOR_RESET (hex, n*v repeats v):
  //   0 0 3c0000 80003043 800000c0 b8410007 78000000 0 3e 47*0 2800000 0 0 0 2007220
  //   contents of REGISTROS_BITS_RW (hex, n*v repeats v):
  //   3ffff ffffffff 63cc368 803fffff ff02b3e1 ffff00ff f800ffff 3ffff e0801fff 100ff ff f 183c0000 43*0
  //   17c00f0f ffffffff 7 0 fffffff
endmodule

module FIFO32x8 (
  input  CLK,
  input  RST,
  input  PUSH,
  input  [7:0] DIN,
  input  POP,
  output [7:0] DOUT,
  output [5:0] COUNT,
  output FULL,
  output EMPTY
);

  wire mete, not1, not2, not3, or9, saca;
  wire [4:0] dir_ram, puntero_esc, puntero_lec, sum4, sum5;
  wire [5:0] mux8, sum6, sum7;

  not not_1 (not3, PUSH);
  Register #(.width(5)) WPTR (.D(sum4), .en(mete), .Q(puntero_esc), .clk(CLK), .clr(RST));
  Register #(.width(5)) RPTR (.D(sum5), .en(saca), .Q(puntero_lec), .clk(CLK), .clr(RST));
  Register #(.width(6)) CUENTA (.D(mux8), .en(or9), .Q(COUNT), .clk(CLK), .clr(RST));
  RAM #(.addrWidth(5), .dataWidth(8), .enables("byte"), .trigger("rising"), .asyncread("true"), .databus("bibus")) MEM_FIFO (
    .addr(dir_ram), .we(mete), .oe(1'b1), .clk(CLK), .din(DIN), .dout(DOUT));
  Comparator #(.width(6), .mode("unsigned")) comparator_1 (.a(COUNT), .b(6'b100000), .eq(FULL));  // open: gt, lt
  Comparator #(.width(6), .mode("unsigned")) comparator_2 (.a(COUNT), .b({6{1'b0}}), .eq(EMPTY));  // open: gt, lt
  Adder #(.width(6)) adder_1 (.a(COUNT), .b(6'b000001), .out(sum6));  // open: cin, cout
  Adder #(.width(6)) adder_2 (.a(COUNT), .b({6{1'b1}}), .out(sum7));  // open: cin, cout
  Adder #(.width(5)) adder_3 (.a(puntero_esc), .b(5'b00001), .out(sum4));  // open: cin, cout
  Adder #(.width(5)) adder_4 (.a(puntero_lec), .b(5'b00001), .out(sum5));  // open: cin, cout
  Multiplexer #(.select(1), .width(5), .enable("false")) multiplexer_1 (
    .in0(puntero_lec), .in1(puntero_esc), .out(dir_ram), .sel(PUSH));
  not not_2 (not1, FULL);
  not not_3 (not2, EMPTY);
  and and_1 (mete, PUSH, not1);
  and and_2 (saca, POP, not2, not3);
  Multiplexer #(.select(1), .width(6), .enable("false")) multiplexer_2 (.in0(sum7), .in1(sum6), .out(mux8), .sel(mete));
  or or_1 (or9, mete, saca);

  // Other names for the same wires on the sheet: cuenta[5:0] = COUNT; dato_salida[7:0] = DOUT; vacio = EMPTY;
  //   lleno = FULL
endmodule
module I2C (
  input  CLK,
  input  RST,
  input  SEL,
  input  [9:0] A,
  input  [31:0] WD,
  input  WE,
  input  RE,
  input  SCL_ENTRA,
  input  SDA_ENTRA,
  output SCL_SALE,
  output SDA_SALE,
  output IRQ,
  output [31:0] RD
);

  wire ack_recibido, and32, and33, and48, and49, and50, and57, and60, and64, and74, and76, and77, and88,
       and92, and95, and97, and98, and115, and116, and117, and126, and130, bit_a_enviar, bus_ocupado,
       carga_byte, CFG_MODO0_escribe, CFG_SCL0_escribe, comando_hecho, COMANDOS0_escribe, COMANDOS1_escribe,
       COMANDOS2_escribe, COMANDOS3_escribe, en_marcha, eq69, eq70, eq124, es_byte, es_end, es_read,
       es_rstart, es_stop, es_write, esc_01C, esc_05C, esc_06C, esc_024, esc_028, esc_058, esc_060, esc_064,
       esc_068, esc_070, esc_074, escribe, fin_byte, fin_cuarto, fin_ranura, inicio_ranura, lee, lee_01C,
       lin_0, lin_1, lin_2, lin_3, lin_4, lin_5, lin_6, lin_7, lin_8, lin_9, lin_10, lin_11, lin_12, lin_13,
       lin_14, lin_15, lin_16, lin_17, lin_18, lin_19, lin_20, lin_21, lin_22, lin_23, lin_24, lin_25,
       lin_26, lin_27, lin_28, lin_29, lin_30, lin_31, lt36, lt45, muestreo, mux58, mux79, mux80, mux81,
       mux83, mux84, mux96, nor51, not35, not37, not73, not82, not86, not87, not91, or28, or29, or38, or40,
       or43, or47, or52, or55, or56, or59, or61, or65, or66, or68, or75, or85, or99, pag_0, pag_1, pag_2,
       pag_3, pag_4, pag_5, pag_6, pag_7, pag_8, pag_9, pag_10, pag_11, pag_12, pag_13, pag_14, pag_15,
       pag_16, pag_17, pag_18, pag_19, pag_20, pag_21, pag_22, pag_23, pag_24, pag_25, pag_26, pag_27,
       pag_28, pag_29, pag_30, pag_31, primera_mitad, q_0, q_1, q_2, q_3, qx90, qx94, r000, r01C, r02C, r004,
       r05C, r06C, r008, r018, r020, r024, r028, r058, r060, r064, r068, r070, r074, ranura_ack,
       registros_acceso, registros_existe, scl_siguiente, sda_siguiente, se_detiene, siguiente_comando,
       trans_start, ultimo_byte, xor46, xor89, xor93;
  wire [1:0] cuarto, mux42, sum41;
  wire [2:0] and6, and7, CFG_MODO0, CFG_MODO0_mascara, CFG_MODO0_nuevo, CFG_MODO0_sig, codigo,
       comando_actual, mux54, not5, not78, sum53;
  wire [3:0] \bit , mux63, sum62;
  wire [7:0] and101, and103, and105, byte_leido, bytes_hechos, cual_hecho, mux67, mux72, not102, or106,
       rep100, rep104, rx_dato, sum44, tx_dato;
  wire [8:0] and3, and4, CFG_SCL0, CFG_SCL0_mascara, CFG_SCL0_nuevo, CFG_SCL0_sig, cuenta_cuarto, mux39,
       not2, sum34;
  wire [9:0] dir_registro, rep125;
  wire [10:0] comando;
  wire [10:10] INT_eventos;
  wire [23:8] estado;
  wire [25:23] COMANDOS0_nuevo;
  wire [27:0] and11, and12, and16, and17, and21, and22, and26, and27, COMANDOS0, COMANDOS0_mascara,
       COMANDOS0_sig, COMANDOS1, COMANDOS1_mascara, COMANDOS1_sig, COMANDOS2, COMANDOS2_mascara,
       COMANDOS2_sig, COMANDOS3, COMANDOS3_mascara, COMANDOS3_sig, not10, not15, not20, not25;
  wire [31:0] and120, and122, and123, and129, and133, and135, and137, and139, and141, and143, and145, and147,
       and149, and151, and153, and155, and157, and159, INT_clr, INT_ENA, INT_raw, INT_st, not119, not128,
       or121, registros_a_guardar, registros_bits_fijos, registros_bits_rw, registros_guardado,
       registros_reset_rw, registros_valor, registros_valor_reset, rep118, rep127, rep132, rep134, rep136,
       rep138, rep140, rep142, rep144, rep146, rep148, rep150, rep152, rep154, rep156, rep158, xor131, zx30;
  wire [31:14] dato_escrito;
  wire [31:31] cat107, cat108, cat109, cat110, cat111, cat112, cat113, cat114;

  and and_1 (and126, SEL, WE);
  and and_2 (escribe, WE, SEL);
  and and_3 (lee, RE, SEL);
  Register #(.width(9)) u_CFG_SCL0 (.D(CFG_SCL0_sig), .en(CFG_SCL0_escribe), .Q(CFG_SCL0), .clk(CLK), .clr(RST));
  Register #(.width(3)) u_CFG_MODO0 (.D(CFG_MODO0_sig), .en(CFG_MODO0_escribe), .Q(CFG_MODO0), .clk(CLK), .clr(RST));
  Register #(.width(28)) u_COMANDOS0 (.D(COMANDOS0_sig), .en(COMANDOS0_escribe), .Q(COMANDOS0), .clk(CLK), .clr(RST));
  Register #(.width(28)) u_COMANDOS1 (.D(COMANDOS1_sig), .en(COMANDOS1_escribe), .Q(COMANDOS1), .clk(CLK), .clr(RST));
  Register #(.width(28)) u_COMANDOS2 (.D(COMANDOS2_sig), .en(COMANDOS2_escribe), .Q(COMANDOS2), .clk(CLK), .clr(RST));
  Register #(.width(28)) u_COMANDOS3 (.D(COMANDOS3_sig), .en(COMANDOS3_escribe), .Q(COMANDOS3), .clk(CLK), .clr(RST));
  Register #(.width(9)) CUARTO_T (.D(mux39), .en(or40), .Q(cuenta_cuarto), .clk(CLK), .clr(RST));
  Register #(.width(2)) u_CUARTO (.D(mux42), .en(or43), .Q(cuarto), .clk(CLK), .clr(RST));
  Register #(.width(3)) u_COMANDO (.D(mux54), .en(or55), .Q(comando_actual), .clk(CLK), .clr(RST));
  Register #(.width(1)) u_EN_MARCHA (.D(mux58), .en(or59), .Q(en_marcha), .clk(CLK), .clr(RST));
  Register #(.width(4)) u_BIT (.D(mux63), .en(or65), .Q(\bit ), .clk(CLK), .clr(RST));
  Register #(.width(8)) BYTES (.D(mux67), .en(or68), .Q(bytes_hechos), .clk(CLK), .clr(RST));
  Register #(.width(8)) DESPLAZA (.D(mux72), .en(or75), .Q(byte_leido), .clk(CLK), .clr(RST));
  Register #(.width(1)) RESP_REC (.D(SDA_ENTRA), .en(and77), .Q(ack_recibido), .clk(CLK), .clr(RST));
  Register #(.width(1)) SDA (.D(xor89), .en(and88), .Q(qx90), .clk(CLK), .clr(RST));
  Register #(.width(1)) SCL (.D(xor93), .en(and92), .Q(qx94), .clk(CLK), .clr(RST));
  Register #(.width(1)) OCUPADO (.D(mux96), .en(or99), .Q(bus_ocupado), .clk(CLK), .clr(RST));
  Register #(.width(8)) HECHOS (
    .D(or106), .en(1'b1),
    .Q({cat114[31], cat113[31], cat112[31], cat111[31], cat110[31], cat109[31], cat108[31], cat107[31]}),
    .clk(CLK), .clr(RST));
  Register #(.width(32)) u_INT_RAW (.D(and122), .en(1'b1), .Q(INT_raw), .clk(CLK), .clr(RST));
  Register #(.width(32)) u_INT_ENA (.D(and123), .en(esc_028), .Q(INT_ENA), .clk(CLK), .clr(RST));
  assign rep125 = {{9{SEL}}, SEL};  // Bit_Extender bit_extender_1
  ROM #(.addrWidth(10), .dataWidth(1)) u_REGISTROS_EXISTE (.addr(dir_registro), .data(registros_existe));
  ROM #(.addrWidth(10), .dataWidth(32)) u_REGISTROS_VALOR_RESET (.addr(dir_registro), .data(registros_valor_reset));
  ROM #(.addrWidth(10), .dataWidth(32)) u_REGISTROS_BITS_RW (.addr(dir_registro), .data(registros_bits_rw));
  RAM #(.addrWidth(10), .dataWidth(32), .enables("byte"), .trigger("rising"), .asyncread("true"), .databus("bibus"), .clearpin("true")) REGISTROS (
    .addr(dir_registro), .we(and130), .oe(1'b1), .clk(CLK), .din(registros_a_guardar),
    .dout(registros_guardado), .clr(RST));
  Decoder #(.select(2), .enable("false")) decoder_1 (.out0(q_0), .out1(q_1), .out2(q_2), .out3(q_3), .sel(cuarto));
  Decoder #(.select(3), .enable("false")) decoder_2 (
    .out0(cual_hecho[0]), .out1(cual_hecho[1]), .out2(cual_hecho[2]), .out3(cual_hecho[3]),
    .out4(cual_hecho[4]), .out5(cual_hecho[5]), .out6(cual_hecho[6]), .out7(cual_hecho[7]),
    .sel(comando_actual));
  Adder #(.width(9)) adder_1 (.a(cuenta_cuarto), .b(9'h1), .out(sum34));  // open: cin, cout
  Comparator #(.width(9), .mode("unsigned")) comparator_1 (.a(cuenta_cuarto), .b(CFG_SCL0), .lt(lt36));  // open: gt, eq
  Adder #(.width(2)) adder_2 (.a(cuarto), .b(2'b01), .out(sum41));  // open: cin, cout
  Comparator #(.width(4), .mode("unsigned")) comparator_2 (.a(\bit ), .b(4'b1000), .eq(ranura_ack));  // open: gt, lt
  Adder #(.width(8)) adder_3 (.a(bytes_hechos), .b(8'h1), .out(sum44));  // open: cin, cout
  Adder #(.width(3)) adder_4 (.a(comando_actual), .b(3'b001), .out(sum53));  // open: cin, cout
  Adder #(.width(4)) adder_5 (.a(\bit ), .b(4'b0001), .out(sum62));  // open: cin, cout
  Comparator #(.width(9), .mode("unsigned")) comparator_3 (
    .a(cuenta_cuarto), .b({9{1'b0}}), .eq(eq69));  // open: gt, lt
  Comparator #(.width(4), .mode("unsigned")) comparator_4 (.a(\bit ), .b(4'b0000), .eq(eq70));  // open: gt, lt
  xor xor_1 (SDA_SALE, qx90, 1'b1);
  xor xor_2 (SCL_SALE, qx94, 1'b1);
  assign INT_st = INT_raw & INT_ENA;  // AND_Gate and_4, 32 bits wide
  assign dir_registro = A & rep125;  // AND_Gate and_5, 10 bits wide
  assign rep127 = {{31{and126}}, and126};  // Bit_Extender bit_extender_2
  and and_6 (registros_acceso, SEL, registros_existe);
  assign registros_reset_rw = registros_valor_reset & registros_bits_rw;  // AND_Gate and_7, 32 bits wide
  assign not128 = ~registros_bits_rw;  // NOT_Gate not_1, 32 bits wide
  not not_2 (not86, q_0);
  or or_1 (or28, RST, CFG_MODO0[1]);
  or or_2 (or29, RST, CFG_MODO0[2]);
  not not_3 (not37, lt36);
  and and_8 (inicio_ranura, en_marcha, q_0, eq69);
  not not_4 (not73, ranura_ack);
  assign not78 = ~\bit [2:0];  // NOT_Gate not_5, 3 bits wide
  or or_3 (primera_mitad, q_0, q_1);
  or or_4 (or85, q_1, q_2);
  Comparator #(.width(32), .mode("unsigned")) comparator_5 (.a(INT_st), .b({32{1'b0}}), .eq(eq124));  // open: gt, lt
  assign {dato_escrito, CFG_MODO0_nuevo[1], CFG_MODO0_nuevo[2], COMANDOS0_nuevo, CFG_SCL0_nuevo[8:5], CFG_MODO0_nuevo[0], CFG_SCL0_nuevo[3:0]} = WD & rep127;  // AND_Gate and_9, 32 bits wide
  Multiplexer #(.select(3), .width(14), .enable("false")) multiplexer_1 (
    .in0(COMANDOS0[13:0]), .in1(COMANDOS0[27:14]), .in2(COMANDOS1[13:0]), .in3(COMANDOS1[27:14]),
    .in4(COMANDOS2[13:0]), .in5(COMANDOS2[27:14]), .in6(COMANDOS3[13:0]), .in7(COMANDOS3[27:14]),
    .out({codigo, comando}), .sel(comando_actual));
  assign registros_bits_fijos = registros_valor_reset & not128;  // AND_Gate and_10, 32 bits wide
  and and_11 (and130, escribe, registros_acceso);
  assign xor131 = registros_guardado ^ registros_reset_rw;  // XOR_Gate xor_3, 32 bits wide
  assign rep132 = {{31{registros_acceso}}, registros_acceso};  // Bit_Extender bit_extender_3
  Decoder #(.select(5), .enable("false")) decoder_3 (
    .out0(pag_0), .out1(pag_1), .out2(pag_2), .out3(pag_3), .out4(pag_4), .out5(pag_5), .out6(pag_6),
    .out7(pag_7), .out8(pag_8), .out9(pag_9), .out10(pag_10), .out11(pag_11), .out12(pag_12), .out13(pag_13),
    .out14(pag_14), .out15(pag_15), .out16(pag_16), .out17(pag_17), .out18(pag_18), .out19(pag_19),
    .out20(pag_20), .out21(pag_21), .out22(pag_22), .out23(pag_23), .out24(pag_24), .out25(pag_25),
    .out26(pag_26), .out27(pag_27), .out28(pag_28), .out29(pag_29), .out30(pag_30), .out31(pag_31),
    .sel(dir_registro[9:5]));
  Decoder #(.select(5), .enable("false")) decoder_4 (
    .out0(lin_0), .out1(lin_1), .out2(lin_2), .out3(lin_3), .out4(lin_4), .out5(lin_5), .out6(lin_6),
    .out7(lin_7), .out8(lin_8), .out9(lin_9), .out10(lin_10), .out11(lin_11), .out12(lin_12), .out13(lin_13),
    .out14(lin_14), .out15(lin_15), .out16(lin_16), .out17(lin_17), .out18(lin_18), .out19(lin_19),
    .out20(lin_20), .out21(lin_21), .out22(lin_22), .out23(lin_23), .out24(lin_24), .out25(lin_25),
    .out26(lin_26), .out27(lin_27), .out28(lin_28), .out29(lin_29), .out30(lin_30), .out31(lin_31),
    .sel(dir_registro[4:0]));
  Multiplexer #(.select(3), .width(1), .enable("false")) multiplexer_2 (
    .in0(byte_leido[0]), .in1(byte_leido[1]), .in2(byte_leido[2]), .in3(byte_leido[3]), .in4(byte_leido[4]),
    .in5(byte_leido[5]), .in6(byte_leido[6]), .in7(byte_leido[7]), .out(bit_a_enviar), .sel(not78));
  not not_6 (not82, primera_mitad);
  assign and123 = {dato_escrito, CFG_MODO0_nuevo[1], CFG_MODO0_nuevo[2], COMANDOS0_nuevo, CFG_SCL0_nuevo[8:5], CFG_MODO0_nuevo[0], CFG_SCL0_nuevo[3:0]} & 32'h698;  // AND_Gate and_12, 32 bits wide
  not not_7 (IRQ, eq124);
  assign and129 = {dato_escrito, CFG_MODO0_nuevo[1], CFG_MODO0_nuevo[2], COMANDOS0_nuevo, CFG_SCL0_nuevo[8:5], CFG_MODO0_nuevo[0], CFG_SCL0_nuevo[3:0]} & registros_bits_rw;  // AND_Gate and_13, 32 bits wide
  assign registros_valor = xor131 | registros_bits_fijos;  // OR_Gate or_5, 32 bits wide
  and and_14 (r000, SEL, pag_0, lin_0);
  and and_15 (r004, SEL, pag_0, lin_1);
  and and_16 (r018, SEL, pag_0, lin_6);
  and and_17 (r058, SEL, pag_0, lin_22);
  and and_18 (r05C, SEL, pag_0, lin_23);
  and and_19 (r060, SEL, pag_0, lin_24);
  and and_20 (r064, SEL, pag_0, lin_25);
  and and_21 (r068, SEL, pag_0, lin_26);
  and and_22 (r06C, SEL, pag_0, lin_27);
  and and_23 (r070, SEL, pag_0, lin_28);
  and and_24 (r074, SEL, pag_0, lin_29);
  and and_25 (r01C, SEL, pag_0, lin_7);
  and and_26 (r024, SEL, pag_0, lin_9);
  and and_27 (r028, SEL, pag_0, lin_10);
  and and_28 (r008, SEL, pag_0, lin_2);
  and and_29 (r020, SEL, pag_0, lin_8);
  and and_30 (r02C, SEL, pag_0, lin_11);
  Comparator #(.width(3), .mode("unsigned")) comparator_6 (.a(codigo), .b(3'b110), .eq(es_rstart));  // open: gt, lt
  Comparator #(.width(3), .mode("unsigned")) comparator_7 (.a(codigo), .b(3'b001), .eq(es_write));  // open: gt, lt
  Comparator #(.width(3), .mode("unsigned")) comparator_8 (.a(codigo), .b(3'b011), .eq(es_read));  // open: gt, lt
  Comparator #(.width(3), .mode("unsigned")) comparator_9 (.a(codigo), .b(3'b010), .eq(es_stop));  // open: gt, lt
  Comparator #(.width(8), .mode("unsigned")) comparator_10 (.a(sum44), .b(comando[7:0]), .lt(lt45));  // open: gt, eq
  xor xor_4 (xor46, SDA_ENTRA, comando[9]);
  Multiplexer #(.select(1), .width(1), .enable("false")) multiplexer_3 (
    .in0(bit_a_enviar), .in1(1'b1), .out(mux79), .sel(ranura_ack));
  Multiplexer #(.select(1), .width(1), .enable("false")) multiplexer_4 (
    .in0(1'b1), .in1(comando[10]), .out(mux80), .sel(ranura_ack));
  assign rep104 = {{7{dato_escrito[31]}}, dato_escrito[31]};  // Bit_Extender bit_extender_4
  assign registros_a_guardar = and129 ^ registros_reset_rw;  // XOR_Gate xor_5, 32 bits wide
  assign and133 = registros_valor & rep132;  // AND_Gate and_31, 32 bits wide
  and and_32 (CFG_SCL0_escribe, escribe, r000);
  and and_33 (CFG_MODO0_mascara[0], escribe, r004);
  and and_34 (CFG_MODO0_mascara[2], escribe, r018);
  and and_35 (esc_058, escribe, r058);
  and and_36 (esc_05C, escribe, r05C);
  and and_37 (esc_060, escribe, r060);
  and and_38 (esc_064, escribe, r064);
  and and_39 (esc_068, escribe, r068);
  and and_40 (esc_06C, escribe, r06C);
  and and_41 (esc_070, escribe, r070);
  and and_42 (esc_074, escribe, r074);
  and and_43 (esc_01C, escribe, r01C);
  and and_44 (lee_01C, lee, r01C);
  or or_6 (es_byte, es_write, es_read);
  not not_8 (ultimo_byte, lt45);
  Multiplexer #(.select(1), .width(1), .enable("false")) multiplexer_5 (
    .in0(mux79), .in1(mux80), .out(mux81), .sel(es_read));
  Multiplexer #(.select(1), .width(1), .enable("false")) multiplexer_6 (
    .in0(1'b1), .in1(not82), .out(mux83), .sel(es_stop));
  Multiplexer #(.select(1), .width(1), .enable("false")) multiplexer_7 (
    .in0(or85), .in1(not86), .out(scl_siguiente), .sel(es_stop));
  and and_45 (esc_024, escribe, r024);
  and and_46 (esc_028, escribe, r028);
  assign rep134 = {{31{r01C}}, r01C};  // Bit_Extender bit_extender_5
  assign rep136 = {{31{r058}}, r058};  // Bit_Extender bit_extender_6
  assign rep138 = {{31{r05C}}, r05C};  // Bit_Extender bit_extender_7
  assign rep140 = {{31{r060}}, r060};  // Bit_Extender bit_extender_8
  assign rep142 = {{31{r064}}, r064};  // Bit_Extender bit_extender_9
  assign rep144 = {{31{r068}}, r068};  // Bit_Extender bit_extender_10
  assign rep146 = {{31{r06C}}, r06C};  // Bit_Extender bit_extender_11
  assign rep148 = {{31{r070}}, r070};  // Bit_Extender bit_extender_12
  assign rep150 = {{31{r074}}, r074};  // Bit_Extender bit_extender_13
  assign rep152 = {{31{r008}}, r008};  // Bit_Extender bit_extender_14
  assign rep154 = {{31{r028}}, r028};  // Bit_Extender bit_extender_15
  assign rep156 = {{31{r020}}, r020};  // Bit_Extender bit_extender_16
  assign rep158 = {{31{r02C}}, r02C};  // Bit_Extender bit_extender_17
  nor nor_1 (es_end, es_rstart, es_write, es_read, es_stop);
  or or_7 (or47, es_rstart, es_stop);
  and and_47 (carga_byte, inicio_ranura, es_write, eq70);
  assign CFG_SCL0_mascara = {{8{CFG_SCL0_escribe}}, CFG_SCL0_escribe};  // Bit_Extender bit_extender_18
  or or_8 (CFG_MODO0_escribe, CFG_MODO0_mascara[0], CFG_MODO0_mascara[2]);
  assign COMANDOS0_mascara[13:0] = {{13{esc_058}}, esc_058};  // Bit_Extender bit_extender_19
  assign COMANDOS0_mascara[27:14] = {{13{esc_05C}}, esc_05C};  // Bit_Extender bit_extender_20
  or or_9 (COMANDOS0_escribe, esc_058, esc_05C);
  assign COMANDOS1_mascara[13:0] = {{13{esc_060}}, esc_060};  // Bit_Extender bit_extender_21
  assign COMANDOS1_mascara[27:14] = {{13{esc_064}}, esc_064};  // Bit_Extender bit_extender_22
  or or_10 (COMANDOS1_escribe, esc_060, esc_064);
  assign COMANDOS2_mascara[13:0] = {{13{esc_068}}, esc_068};  // Bit_Extender bit_extender_23
  assign COMANDOS2_mascara[27:14] = {{13{esc_06C}}, esc_06C};  // Bit_Extender bit_extender_24
  or or_11 (COMANDOS2_escribe, esc_068, esc_06C);
  assign COMANDOS3_mascara[13:0] = {{13{esc_070}}, esc_070};  // Bit_Extender bit_extender_25
  assign COMANDOS3_mascara[27:14] = {{13{esc_074}}, esc_074};  // Bit_Extender bit_extender_26
  or or_12 (COMANDOS3_escribe, esc_070, esc_074);
  assign rep118 = {{31{esc_024}}, esc_024};  // Bit_Extender bit_extender_27
  assign and137 = {cat107[31], {31{1'b0}}} & rep136;  // AND_Gate and_48, 32 bits wide
  assign and139 = {cat108[31], {31{1'b0}}} & rep138;  // AND_Gate and_49, 32 bits wide
  assign and141 = {cat109[31], {31{1'b0}}} & rep140;  // AND_Gate and_50, 32 bits wide
  assign and143 = {cat110[31], {31{1'b0}}} & rep142;  // AND_Gate and_51, 32 bits wide
  assign and145 = {cat111[31], {31{1'b0}}} & rep144;  // AND_Gate and_52, 32 bits wide
  assign and147 = {cat112[31], {31{1'b0}}} & rep146;  // AND_Gate and_53, 32 bits wide
  assign and149 = {cat113[31], {31{1'b0}}} & rep148;  // AND_Gate and_54, 32 bits wide
  assign and151 = {cat114[31], {31{1'b0}}} & rep150;  // AND_Gate and_55, 32 bits wide
  assign and155 = INT_ENA & rep154;  // AND_Gate and_56, 32 bits wide
  assign and157 = INT_raw & rep156;  // AND_Gate and_57, 32 bits wide
  assign and159 = INT_st & rep158;  // AND_Gate and_58, 32 bits wide
  and and_59 (and32, CFG_MODO0_mascara[0], CFG_SCL0_nuevo[5]);
  and and_60 (and33, CFG_MODO0_mascara[0], COMANDOS0_nuevo[24]);
  Multiplexer #(.select(1), .width(1), .enable("false")) multiplexer_8 (
    .in0(mux83), .in1(primera_mitad), .out(mux84), .sel(es_rstart));
  xor xor_6 (xor93, scl_siguiente, 1'b1);
  assign not5 = ~{{2{CFG_MODO0_mascara[2]}}, CFG_MODO0_mascara[0]};  // NOT_Gate not_9, 3 bits wide
  FIFO32x8 FIFO_TX (
    .CLK(CLK), .RST(or28), .PUSH(esc_01C),
    .DIN({CFG_SCL0_nuevo[7:5], CFG_MODO0_nuevo[0], CFG_SCL0_nuevo[3:0]}), .POP(carga_byte), .DOUT(tx_dato),
    .COUNT(estado[23:18]));  // open: FULL, EMPTY
  and and_61 (trans_start, and32, CFG_MODO0[0]);
  not not_10 (not35, es_end);
  and and_62 (and50, en_marcha, es_end);
  nor nor_2 (nor51, es_stop, es_end);
  or or_13 (or56, es_stop, es_end);
  Multiplexer #(.select(1), .width(1), .enable("false")) multiplexer_9 (
    .in0(mux84), .in1(mux81), .out(sda_siguiente), .sel(es_byte));
  not not_11 (not87, es_end);
  not not_12 (not91, es_end);
  assign not102 = ~{esc_074, esc_070, esc_06C, esc_068, esc_064, esc_060, esc_05C, esc_058};  // NOT_Gate not_13, 8 bits wide
  assign and105 = {esc_074, esc_070, esc_06C, esc_068, esc_064, esc_060, esc_05C, esc_058} & rep104;  // AND_Gate and_63, 8 bits wide
  and and_64 (and115, en_marcha, es_end);
  assign INT_clr = {dato_escrito, CFG_MODO0_nuevo[1], CFG_MODO0_nuevo[2], COMANDOS0_nuevo, CFG_SCL0_nuevo[8:5], CFG_MODO0_nuevo[0], CFG_SCL0_nuevo[3:0]} & rep118;  // AND_Gate and_65, 32 bits wide
  assign and7 = CFG_MODO0_nuevo & {{2{CFG_MODO0_mascara[2]}}, CFG_MODO0_mascara[0]};  // AND_Gate and_66, 3 bits wide
  assign not2 = ~CFG_SCL0_mascara;  // NOT_Gate not_14, 9 bits wide
  assign and6 = CFG_MODO0 & not5;  // AND_Gate and_67, 3 bits wide
  assign not10 = ~COMANDOS0_mascara;  // NOT_Gate not_15, 28 bits wide
  assign not15 = ~COMANDOS1_mascara;  // NOT_Gate not_16, 28 bits wide
  assign not20 = ~COMANDOS2_mascara;  // NOT_Gate not_17, 28 bits wide
  assign not25 = ~COMANDOS3_mascara;  // NOT_Gate not_18, 28 bits wide
  and and_68 (fin_cuarto, en_marcha, not35, not37);
  or or_14 (or40, en_marcha, trans_start);
  Multiplexer #(.select(1), .width(2), .enable("false")) multiplexer_10 (
    .in0(sum41), .in1(2'b00), .out(mux42), .sel(trans_start));
  or or_15 (or52, trans_start, and33);
  Multiplexer #(.select(1), .width(1), .enable("false")) multiplexer_11 (
    .in0(1'b0), .in1(1'b1), .out(mux58), .sel(trans_start));
  Multiplexer #(.select(1), .width(8), .enable("false")) multiplexer_12 (
    .in0({byte_leido[6:0], SDA_ENTRA}), .in1(tx_dato), .out(mux72), .sel(carga_byte));
  and and_69 (and88, en_marcha, not87);
  xor xor_7 (xor89, sda_siguiente, 1'b1);
  and and_70 (and92, en_marcha, not91);
  assign and103 = {cat114[31], cat113[31], cat112[31], cat111[31], cat110[31], cat109[31], cat108[31], cat107[31]} & not102;  // AND_Gate and_71, 8 bits wide
  assign not119 = ~INT_clr;  // NOT_Gate not_19, 32 bits wide
  assign and4 = {CFG_SCL0_nuevo[8:5], CFG_MODO0_nuevo[0], CFG_SCL0_nuevo[3:0]} & CFG_SCL0_mascara;  // AND_Gate and_72, 9 bits wide
  assign and12 = {CFG_MODO0_nuevo[1], CFG_MODO0_nuevo[2], COMANDOS0_nuevo, CFG_SCL0_nuevo[8:5], CFG_MODO0_nuevo[0], CFG_SCL0_nuevo[3:0], CFG_MODO0_nuevo[1], CFG_MODO0_nuevo[2], COMANDOS0_nuevo, CFG_SCL0_nuevo[8:5], CFG_MODO0_nuevo[0], CFG_SCL0_nuevo[3:0]} & COMANDOS0_mascara;  // AND_Gate and_73, 28 bits wide
  assign and17 = {CFG_MODO0_nuevo[1], CFG_MODO0_nuevo[2], COMANDOS0_nuevo, CFG_SCL0_nuevo[8:5], CFG_MODO0_nuevo[0], CFG_SCL0_nuevo[3:0], CFG_MODO0_nuevo[1], CFG_MODO0_nuevo[2], COMANDOS0_nuevo, CFG_SCL0_nuevo[8:5], CFG_MODO0_nuevo[0], CFG_SCL0_nuevo[3:0]} & COMANDOS1_mascara;  // AND_Gate and_74, 28 bits wide
  assign and22 = {CFG_MODO0_nuevo[1], CFG_MODO0_nuevo[2], COMANDOS0_nuevo, CFG_SCL0_nuevo[8:5], CFG_MODO0_nuevo[0], CFG_SCL0_nuevo[3:0], CFG_MODO0_nuevo[1], CFG_MODO0_nuevo[2], COMANDOS0_nuevo, CFG_SCL0_nuevo[8:5], CFG_MODO0_nuevo[0], CFG_SCL0_nuevo[3:0]} & COMANDOS2_mascara;  // AND_Gate and_75, 28 bits wide
  assign and27 = {CFG_MODO0_nuevo[1], CFG_MODO0_nuevo[2], COMANDOS0_nuevo, CFG_SCL0_nuevo[8:5], CFG_MODO0_nuevo[0], CFG_SCL0_nuevo[3:0], CFG_MODO0_nuevo[1], CFG_MODO0_nuevo[2], COMANDOS0_nuevo, CFG_SCL0_nuevo[8:5], CFG_MODO0_nuevo[0], CFG_SCL0_nuevo[3:0]} & COMANDOS3_mascara;  // AND_Gate and_76, 28 bits wide
  assign CFG_MODO0_sig = and6 | and7;  // OR_Gate or_16, 3 bits wide
  Multiplexer #(.select(1), .width(3), .enable("false")) multiplexer_13 (
    .in0(sum53), .in1(3'b000), .out(mux54), .sel(or52));
  assign and120 = INT_raw & not119;  // AND_Gate and_77, 32 bits wide
  assign and3 = CFG_SCL0 & not2;  // AND_Gate and_78, 9 bits wide
  assign and11 = COMANDOS0 & not10;  // AND_Gate and_79, 28 bits wide
  assign and16 = COMANDOS1 & not15;  // AND_Gate and_80, 28 bits wide
  assign and21 = COMANDOS2 & not20;  // AND_Gate and_81, 28 bits wide
  assign and26 = COMANDOS3 & not25;  // AND_Gate and_82, 28 bits wide
  or or_17 (or38, fin_cuarto, trans_start);
  or or_18 (or43, fin_cuarto, trans_start);
  and and_83 (fin_ranura, fin_cuarto, q_3);
  and and_84 (muestreo, fin_cuarto, q_1);
  assign CFG_SCL0_sig = and3 | and4;  // OR_Gate or_19, 9 bits wide
  assign COMANDOS0_sig = and11 | and12;  // OR_Gate or_20, 28 bits wide
  assign COMANDOS1_sig = and16 | and17;  // OR_Gate or_21, 28 bits wide
  assign COMANDOS2_sig = and21 | and22;  // OR_Gate or_22, 28 bits wide
  assign COMANDOS3_sig = and26 | and27;  // OR_Gate or_23, 28 bits wide
  Multiplexer #(.select(1), .width(9), .enable("false")) multiplexer_14 (
    .in0(sum34), .in1({9{1'b0}}), .out(mux39), .sel(or38));
  and and_85 (fin_byte, fin_ranura, es_byte, ranura_ack);
  and and_86 (INT_eventos[10], muestreo, es_write, ranura_ack, comando[8], xor46);
  and and_87 (and48, fin_ranura, or47);
  and and_88 (and60, fin_ranura, ranura_ack);
  and and_89 (and64, fin_ranura, es_byte);
  and and_90 (and74, muestreo, es_read, not73);
  and and_91 (and77, muestreo, ranura_ack);
  and and_92 (and95, fin_ranura, es_rstart);
  and and_93 (and97, fin_ranura, es_rstart);
  and and_94 (and98, fin_ranura, es_stop);
  and and_95 (and117, fin_ranura, es_rstart);
  and and_96 (and76, fin_byte, es_read);
  Multiplexer #(.select(1), .width(1), .enable("false")) multiplexer_15 (
    .in0(1'b0), .in1(1'b1), .out(mux96), .sel(and95));
  or or_24 (or99, and97, and98, and33);
  and and_97 (and49, fin_byte, ultimo_byte);
  or or_25 (or75, carga_byte, and74);
  or or_26 (comando_hecho, and48, and49, and50);
  FIFO32x8 FIFO_RX (
    .CLK(CLK), .RST(or29), .PUSH(and76), .DIN(byte_leido), .POP(lee_01C), .DOUT(rx_dato), .COUNT(estado[13:8]));  // open: FULL, EMPTY
  and and_98 (siguiente_comando, comando_hecho, nor51);
  and and_99 (and57, comando_hecho, or56);
  assign rep100 = {{7{comando_hecho}}, comando_hecho};  // Bit_Extender bit_extender_28
  and and_100 (and116, comando_hecho, es_stop);
  assign zx30 = {{24{1'b0}}, rx_dato};  // Bit_Extender bit_extender_29
  or or_27 (se_detiene, and57, INT_eventos[10], and33);
  or or_28 (or55, siguiente_comando, trans_start, and33);
  or or_29 (or61, and60, trans_start, siguiente_comando);
  or or_30 (or65, and64, trans_start, siguiente_comando);
  or or_31 (or66, trans_start, siguiente_comando);
  or or_32 (or68, fin_byte, trans_start, siguiente_comando);
  assign and101 = cual_hecho & rep100;  // AND_Gate and_101, 8 bits wide
  or or_33 (or59, trans_start, se_detiene);
  Multiplexer #(.select(1), .width(4), .enable("false")) multiplexer_16 (
    .in0(sum62), .in1(4'b0000), .out(mux63), .sel(or61));
  Multiplexer #(.select(1), .width(8), .enable("false")) multiplexer_17 (
    .in0(sum44), .in1({8{1'b0}}), .out(mux67), .sel(or66));
  assign or106 = and103 | and105 | and101;  // OR_Gate or_34, 8 bits wide
  assign or121 = and120 | {{21{1'b0}}, INT_eventos[10], and117, 1'b0, and116, 2'b00, fin_byte, and115, 3'b000};  // OR_Gate or_35, 32 bits wide
  assign and135 = zx30 & rep134;  // AND_Gate and_102, 32 bits wide
  assign and153 = {{8{1'b0}}, estado[23:18], 4'b0000, estado[13:8], 3'b000, bus_ocupado, 3'b000, ack_recibido} & rep152;  // AND_Gate and_103, 32 bits wide
  assign and122 = or121 & 32'h698;  // AND_Gate and_104, 32 bits wide
  assign RD = and135 | and137 | and139 | and141 | and143 | and145 | and147 | and149 | and151 | and153 | and155 | and157 | and159 | and133;  // OR_Gate or_36, 32 bits wide

  // Other names for the same wires on the sheet: bit_2_0[2:0] = \bit [2:0]; desplaza[7:0] = byte_leido;
  //   desplaza_7 = byte_leido[7]; cat71[7:0] = {byte_leido[6:0], SDA_ENTRA}; desplaza_0 = byte_leido[0];
  //   desplaza_6_0[6:0] = byte_leido[6:0]; desplaza_1 = byte_leido[1]; desplaza_2 = byte_leido[2];
  //   desplaza_3 = byte_leido[3]; desplaza_4 = byte_leido[4]; desplaza_5 = byte_leido[5]; desplaza_6 = byte_leido[6];
  //   hechos[7:0] = {cat114[31], cat113[31], cat112[31], cat111[31], cat110[31], cat109[31], cat108[31], cat107[31]};
  //   hechos_0 = cat107[31]; hechos_1 = cat108[31]; hechos_2 = cat109[31]; hechos_3 = cat110[31];
  //   hechos_4 = cat111[31]; hechos_5 = cat112[31]; hechos_6 = cat113[31]; hechos_7 = cat114[31];
  //   CFG_MODO0_0 = CFG_MODO0[0]; CFG_MODO0_1 = CFG_MODO0[1]; CFG_MODO0_2 = CFG_MODO0[2];
  //   esc_004 = CFG_MODO0_mascara[0]; CFG_MODO0_mascara[1] = CFG_MODO0_mascara[2]; esc_018 = CFG_MODO0_mascara[2];
  //   esc_000 = CFG_SCL0_escribe; rep1[8:0] = CFG_SCL0_mascara; num_bytes[7:0] = comando[7:0]; comando_8 = comando[8];
  //   comando_9 = comando[9]; comando_10 = comando[10]; comando[13:11] = codigo;
  //   COMANDOS0_13_0[13:0] = COMANDOS0[13:0]; COMANDOS0_27_14[13:0] = COMANDOS0[27:14];
  //   rep8[13:0] = COMANDOS0_mascara[13:0]; rep9[13:0] = COMANDOS0_mascara[27:14];
  //   COMANDOS1_13_0[13:0] = COMANDOS1[13:0]; COMANDOS1_27_14[13:0] = COMANDOS1[27:14];
  //   rep13[13:0] = COMANDOS1_mascara[13:0]; rep14[13:0] = COMANDOS1_mascara[27:14];
  //   COMANDOS2_13_0[13:0] = COMANDOS2[13:0]; COMANDOS2_27_14[13:0] = COMANDOS2[27:14];
  //   rep18[13:0] = COMANDOS2_mascara[13:0]; rep19[13:0] = COMANDOS2_mascara[27:14];
  //   COMANDOS3_13_0[13:0] = COMANDOS3[13:0]; COMANDOS3_27_14[13:0] = COMANDOS3[27:14];
  //   rep23[13:0] = COMANDOS3_mascara[13:0]; rep24[13:0] = COMANDOS3_mascara[27:14];
  //   COMANDOS0_nuevo (some bits) = {CFG_MODO0_nuevo[1], CFG_MODO0_nuevo[2], CFG_SCL0_nuevo[8:5], CFG_MODO0_nuevo[0], CFG_SCL0_nuevo[3:0], CFG_MODO0_nuevo[1], CFG_MODO0_nuevo[2], COMANDOS0_nuevo, CFG_SCL0_nuevo[8:5], CFG_MODO0_nuevo[0], CFG_SCL0_nuevo[3:0]};
  //   COMANDOS1_nuevo[27:0] = {CFG_MODO0_nuevo[1], CFG_MODO0_nuevo[2], COMANDOS0_nuevo, CFG_SCL0_nuevo[8:5], CFG_MODO0_nuevo[0], CFG_SCL0_nuevo[3:0], CFG_MODO0_nuevo[1], CFG_MODO0_nuevo[2], COMANDOS0_nuevo, CFG_SCL0_nuevo[8:5], CFG_MODO0_nuevo[0], CFG_SCL0_nuevo[3:0]};
  //   COMANDOS2_nuevo[27:0] = {CFG_MODO0_nuevo[1], CFG_MODO0_nuevo[2], COMANDOS0_nuevo, CFG_SCL0_nuevo[8:5], CFG_MODO0_nuevo[0], CFG_SCL0_nuevo[3:0], CFG_MODO0_nuevo[1], CFG_MODO0_nuevo[2], COMANDOS0_nuevo, CFG_SCL0_nuevo[8:5], CFG_MODO0_nuevo[0], CFG_SCL0_nuevo[3:0]};
  //   COMANDOS3_nuevo[27:0] = {CFG_MODO0_nuevo[1], CFG_MODO0_nuevo[2], COMANDOS0_nuevo, CFG_SCL0_nuevo[8:5], CFG_MODO0_nuevo[0], CFG_SCL0_nuevo[3:0], CFG_MODO0_nuevo[1], CFG_MODO0_nuevo[2], COMANDOS0_nuevo, CFG_SCL0_nuevo[8:5], CFG_MODO0_nuevo[0], CFG_SCL0_nuevo[3:0]};
  //   dato_escrito[13:0] = {CFG_MODO0_nuevo[1], CFG_MODO0_nuevo[2], COMANDOS0_nuevo, CFG_SCL0_nuevo[8:5], CFG_MODO0_nuevo[0], CFG_SCL0_nuevo[3:0]};
  //   dato_escrito_7_0[7:0] = {CFG_SCL0_nuevo[7:5], CFG_MODO0_nuevo[0], CFG_SCL0_nuevo[3:0]};
  //   dato_escrito_8_0[8:0] = {CFG_SCL0_nuevo[8:5], CFG_MODO0_nuevo[0], CFG_SCL0_nuevo[3:0]};
  //   dato_escrito_13_0[13:0] = {CFG_MODO0_nuevo[1], CFG_MODO0_nuevo[2], COMANDOS0_nuevo, CFG_SCL0_nuevo[8:5], CFG_MODO0_nuevo[0], CFG_SCL0_nuevo[3:0]};
  //   CFG_SCL0_nuevo[4] = CFG_MODO0_nuevo[0]; dato_escrito_4 = CFG_MODO0_nuevo[0]; dato_escrito_5 = CFG_SCL0_nuevo[5];
  //   dato_escrito_10 = COMANDOS0_nuevo[24]; dato_escrito_12 = CFG_MODO0_nuevo[2];
  //   dato_escrito_13 = CFG_MODO0_nuevo[1]; hecho_0 = cual_hecho[0]; hecho_1 = cual_hecho[1]; hecho_2 = cual_hecho[2];
  //   hecho_3 = cual_hecho[3]; hecho_4 = cual_hecho[4]; hecho_5 = cual_hecho[5]; hecho_6 = cual_hecho[6];
  //   hecho_7 = cual_hecho[7]; dato_escrito_31 = dato_escrito[31]; dir_registro_4_0[4:0] = dir_registro[4:0];
  //   dir_registro_9_5[4:0] = dir_registro[9:5]; nor31 = es_end;
  //   escritura_comd[7:0] = {esc_074, esc_070, esc_06C, esc_068, esc_064, esc_060, esc_05C, esc_058};
  //   estado (some bits) = {bus_ocupado, ack_recibido}; rx_cuenta[5:0] = estado[13:8]; tx_cuenta[5:0] = estado[23:18];
  //   INT_eventos (some bits) = {and117, and116, fin_byte, and115}; nack = INT_eventos[10]; INT_irq = IRQ;
  //   mete_rx = and76; or160[31:0] = RD; saca_tx = carga_byte; scl_salida = SCL_SALE; sda_salida = SDA_SALE

  // Notes on the sheet:
  //   contents of REGISTROS_EXISTE (hex, n*v repeats v):
  //   1 1 0 1 1 0 1 5*0 1 1 1 0 18*1 28*0 1
  //   contents of REGISTROS_VALOR_RESET (hex, n*v repeats v):
  //   0 20b 0 10 0 0 408b 9*0 4*8 300 200000 8*0 10 10 30*0 20070201
  //   contents of REGISTROS_BITS_RW (hex, n*v repeats v):
  //   1ff 73df 0 3f 80007fff 0 7fff 5*0 1ff 1ff ffff 0 4*1ff 3ff 3fffff 8*3fff 1f 1f fe 37ff 28*0 ffffffff
endmodule

module BusSistema (
  input  [31:0] ADDR,
  input  FETCH,
  input  WR,
  output ERR,
  output SEL_ROM,
  output SEL_FLASH,
  output SEL_SRAM,
  output SEL_RTCMEM,
  output SEL_PERIF,
  output SEL_UART0,
  output SEL_UART1,
  output SEL_GPIO,
  output SEL_IO_MUX,
  output SEL_RTC_CNTL,
  output SEL_EFUSE,
  output SEL_TIMG0,
  output SEL_TIMG1,
  output SEL_SYSTIMER,
  output SEL_SYSCON,
  output SEL_SYSTEM,
  output SEL_INTERRUPT,
  output SEL_LEDC,
  output SEL_SPI2,
  output SEL_I2C
);

  wire a11_periferico, and1, and9, and10, desplazamiento_menor_384K, direccion_valida, ejecutable, eq2, eq3,
       eq4, not6, not7, not8, pagina_60008, sel_DRAM, sel_FLASH_D, sel_FLASH_I, sel_IRAM, sel_RTC_CNTL_t,
       solo_lectura;
  wire [19:0] pagina_periferico, rep5;

  and and_1 (and1, ADDR[18], ADDR[17]);
  Comparator #(.width(13), .mode("unsigned")) comparator_1 (.a(ADDR[31:19]), .b(13'h800), .eq(eq2));  // open: gt, lt
  Comparator #(.width(9), .mode("unsigned")) comparator_2 (
    .a(ADDR[31:23]), .b(9'h84), .eq(sel_FLASH_I));  // open: gt, lt
  Comparator #(.width(9), .mode("unsigned")) comparator_3 (
    .a(ADDR[31:23]), .b(9'h78), .eq(sel_FLASH_D));  // open: gt, lt
  Comparator #(.width(13), .mode("unsigned")) comparator_4 (.a(ADDR[31:19]), .b(13'h7f9), .eq(eq3));  // open: gt, lt
  Comparator #(.width(13), .mode("unsigned")) comparator_5 (.a(ADDR[31:19]), .b(13'h807), .eq(eq4));  // open: gt, lt
  Comparator #(.width(19), .mode("unsigned")) comparator_6 (
    .a(ADDR[31:13]), .b(19'h28000), .eq(SEL_RTCMEM));  // open: gt, lt
  Comparator #(.width(12), .mode("unsigned")) comparator_7 (
    .a(ADDR[31:20]), .b(12'h600), .eq(SEL_PERIF));  // open: gt, lt
  not not_1 (desplazamiento_menor_384K, and1);
  or or_1 (SEL_FLASH, sel_FLASH_I, sel_FLASH_D);
  assign rep5 = {{19{SEL_PERIF}}, SEL_PERIF};  // Bit_Extender bit_extender_1
  and and_2 (a11_periferico, ADDR[11], SEL_PERIF);
  assign pagina_periferico = ADDR[31:12] & rep5;  // AND_Gate and_3, 20 bits wide
  not not_2 (not6, a11_periferico);
  and and_4 (SEL_ROM, eq2, desplazamiento_menor_384K);
  and and_5 (sel_DRAM, eq3, desplazamiento_menor_384K);
  and and_6 (sel_IRAM, eq4, desplazamiento_menor_384K);
  or or_2 (SEL_SRAM, sel_IRAM, sel_DRAM);
  or or_3 (ejecutable, SEL_ROM, sel_FLASH_I, sel_IRAM, SEL_RTCMEM);
  or or_4 (solo_lectura, SEL_ROM, SEL_FLASH);
  Comparator #(.width(20), .mode("unsigned")) comparator_8 (
    .a(pagina_periferico), .b(20'h60000), .eq(SEL_UART0));  // open: gt, lt
  Comparator #(.width(20), .mode("unsigned")) comparator_9 (
    .a(pagina_periferico), .b(20'h60004), .eq(SEL_GPIO));  // open: gt, lt
  Comparator #(.width(20), .mode("unsigned")) comparator_10 (
    .a(pagina_periferico), .b(20'h60008), .eq(sel_RTC_CNTL_t));  // open: gt, lt
  Comparator #(.width(20), .mode("unsigned")) comparator_11 (
    .a(pagina_periferico), .b(20'h60009), .eq(SEL_IO_MUX));  // open: gt, lt
  Comparator #(.width(20), .mode("unsigned")) comparator_12 (
    .a(pagina_periferico), .b(20'h60010), .eq(SEL_UART1));  // open: gt, lt
  Comparator #(.width(20), .mode("unsigned")) comparator_13 (
    .a(pagina_periferico), .b(20'h60013), .eq(SEL_I2C));  // open: gt, lt
  Comparator #(.width(20), .mode("unsigned")) comparator_14 (
    .a(pagina_periferico), .b(20'h60019), .eq(SEL_LEDC));  // open: gt, lt
  Comparator #(.width(20), .mode("unsigned")) comparator_15 (
    .a(pagina_periferico), .b(20'h6001f), .eq(SEL_TIMG0));  // open: gt, lt
  Comparator #(.width(20), .mode("unsigned")) comparator_16 (
    .a(pagina_periferico), .b(20'h60020), .eq(SEL_TIMG1));  // open: gt, lt
  Comparator #(.width(20), .mode("unsigned")) comparator_17 (
    .a(pagina_periferico), .b(20'h60023), .eq(SEL_SYSTIMER));  // open: gt, lt
  Comparator #(.width(20), .mode("unsigned")) comparator_18 (
    .a(pagina_periferico), .b(20'h60024), .eq(SEL_SPI2));  // open: gt, lt
  Comparator #(.width(20), .mode("unsigned")) comparator_19 (
    .a(pagina_periferico), .b(20'h60026), .eq(SEL_SYSCON));  // open: gt, lt
  Comparator #(.width(20), .mode("unsigned")) comparator_20 (
    .a(pagina_periferico), .b(20'h600c0), .eq(SEL_SYSTEM));  // open: gt, lt
  Comparator #(.width(20), .mode("unsigned")) comparator_21 (
    .a(pagina_periferico), .b(20'h600c2), .eq(SEL_INTERRUPT));  // open: gt, lt
  Comparator #(.width(20), .mode("unsigned")) comparator_22 (
    .a(pagina_periferico), .b(20'h60008), .eq(pagina_60008));  // open: gt, lt
  not not_3 (not8, ejecutable);
  and and_7 (SEL_RTC_CNTL, pagina_60008, not6);
  and and_8 (SEL_EFUSE, pagina_60008, a11_periferico);
  or or_5 (direccion_valida, SEL_ROM, SEL_FLASH, SEL_SRAM, SEL_RTCMEM, SEL_PERIF);
  and and_9 (and10, WR, solo_lectura);
  and and_10 (and9, FETCH, not8);
  not not_4 (not7, direccion_valida);
  or or_6 (ERR, not7, and9, and10);

  // Other names for the same wires on the sheet: ADDR_11 = ADDR[11]; ADDR_31_12[19:0] = ADDR[31:12];
  //   ADDR_31_13[18:0] = ADDR[31:13]; ADDR_17 = ADDR[17]; ADDR_18 = ADDR[18]; ADDR_31_19[12:0] = ADDR[31:19];
  //   ADDR_31_20[11:0] = ADDR[31:20]; ADDR_31_23[8:0] = ADDR[31:23]; error_bus = ERR; SEL_EFUSE_2 = SEL_EFUSE;
  //   sel_EFUSE_t = SEL_EFUSE; SEL_FLASH_2 = SEL_FLASH; sel_FLASH_t = SEL_FLASH; SEL_GPIO_2 = SEL_GPIO;
  //   sel_GPIO_t = SEL_GPIO; SEL_I2C_2 = SEL_I2C; sel_I2C_t = SEL_I2C; SEL_INTERRUPT_2 = SEL_INTERRUPT;
  //   sel_INTERRUPT_t = SEL_INTERRUPT; SEL_IO_MUX_2 = SEL_IO_MUX; sel_IO_MUX_t = SEL_IO_MUX; SEL_LEDC_2 = SEL_LEDC;
  //   sel_LEDC_t = SEL_LEDC; sel_PERIFERICOS = SEL_PERIF; SEL_ROM_2 = SEL_ROM; sel_ROM_t = SEL_ROM;
  //   sel_RTC_CNTL_2 = SEL_RTC_CNTL; SEL_RTC_CNTL_3 = SEL_RTC_CNTL; sel_RTC_FAST = SEL_RTCMEM; SEL_SPI2_2 = SEL_SPI2;
  //   sel_SPI2_t = SEL_SPI2; SEL_SRAM_2 = SEL_SRAM; sel_SRAM_t = SEL_SRAM; SEL_SYSCON_2 = SEL_SYSCON;
  //   sel_SYSCON_t = SEL_SYSCON; SEL_SYSTEM_2 = SEL_SYSTEM; sel_SYSTEM_t = SEL_SYSTEM; SEL_SYSTIMER_2 = SEL_SYSTIMER;
  //   sel_SYSTIMER_t = SEL_SYSTIMER; SEL_TIMG0_2 = SEL_TIMG0; sel_TIMG0_t = SEL_TIMG0; SEL_TIMG1_2 = SEL_TIMG1;
  //   sel_TIMG1_t = SEL_TIMG1; SEL_UART0_2 = SEL_UART0; sel_UART0_t = SEL_UART0; SEL_UART1_2 = SEL_UART1;
  //   sel_UART1_t = SEL_UART1
endmodule

module MuxLectura (
  input  [31:0] RD_ROM,
  input  [31:0] RD_FLASH,
  input  [31:0] RD_SRAM,
  input  [31:0] RD_RTCMEM,
  input  SEL_ROM,
  input  SEL_FLASH,
  input  SEL_SRAM,
  input  SEL_RTCMEM,
  input  [31:0] RD_UART0,
  input  [31:0] RD_UART1,
  input  [31:0] RD_GPIO,
  input  [31:0] RD_RTC_CNTL,
  input  [31:0] RD_EFUSE,
  input  [31:0] RD_TIMG0,
  input  [31:0] RD_TIMG1,
  input  [31:0] RD_SYSTIMER,
  input  [31:0] RD_SYSCON,
  input  [31:0] RD_SYSTEM,
  input  [31:0] RD_INTERRUPT,
  input  [31:0] RD_LEDC,
  input  [31:0] RD_SPI2,
  input  [31:0] RD_I2C,
  output [31:0] RDATA
);

  wire [31:0] dato_FLASH, dato_ROM, dato_RTCMEM, dato_SRAM, rep1, rep2, rep3, rep4;

  assign rep1 = {{31{SEL_ROM}}, SEL_ROM};  // Bit_Extender bit_extender_1
  assign rep2 = {{31{SEL_FLASH}}, SEL_FLASH};  // Bit_Extender bit_extender_2
  assign rep3 = {{31{SEL_SRAM}}, SEL_SRAM};  // Bit_Extender bit_extender_3
  assign rep4 = {{31{SEL_RTCMEM}}, SEL_RTCMEM};  // Bit_Extender bit_extender_4
  assign dato_ROM = RD_ROM & rep1;  // AND_Gate and_1, 32 bits wide
  assign dato_FLASH = RD_FLASH & rep2;  // AND_Gate and_2, 32 bits wide
  assign dato_SRAM = RD_SRAM & rep3;  // AND_Gate and_3, 32 bits wide
  assign dato_RTCMEM = RD_RTCMEM & rep4;  // AND_Gate and_4, 32 bits wide
  assign RDATA = dato_ROM | dato_FLASH | dato_SRAM | dato_RTCMEM | RD_UART0 | RD_UART1 | RD_GPIO | RD_RTC_CNTL | RD_EFUSE | RD_TIMG0 | RD_TIMG1 | RD_SYSTIMER | RD_SYSCON | RD_SYSTEM | RD_INTERRUPT | RD_LEDC | RD_SPI2 | RD_I2C;  // OR_Gate or_1, 32 bits wide

  // Other names for the same wires on the sheet: dato_leido[31:0] = RDATA
endmodule

module InterfazPerifericos (
  input  [31:0] DIR,
  input  [31:0] WDATA,
  input  WE,
  input  RE,
  input  ERR,
  input  SEL_PERIF,
  output [9:0] A,
  output [31:0] WD,
  output WE_P,
  output RE_P
);

  wire and2, not4;
  wire [9:0] rep1;
  wire [31:0] rep3;

  not not_1 (not4, ERR);
  assign rep1 = {{9{SEL_PERIF}}, SEL_PERIF};  // Bit_Extender bit_extender_1
  and and_1 (and2, SEL_PERIF, WE);
  and and_2 (WE_P, WE, SEL_PERIF);
  assign A = DIR[11:2] & rep1;  // AND_Gate and_3, 10 bits wide
  assign rep3 = {{31{and2}}, and2};  // Bit_Extender bit_extender_2
  and and_4 (RE_P, RE, not4, SEL_PERIF);
  assign WD = WDATA & rep3;  // AND_Gate and_5, 32 bits wide

  // Other names for the same wires on the sheet: dir_registro[9:0] = A; DIR_11_2[9:0] = DIR[11:2]; lee = RE_P;
  //   dato_escrito[31:0] = WD; escribe = WE_P
endmodule

module PuenteUSB_Serie (
  input  CLK,
  input  RST,
  input  TECLADO_HAY,
  input  [6:0] TECLADO_DATO,
  input  RX_DESDE_CHIP,
  output TX_AL_CHIP,
  output TECLADO_LEER,
  output [6:0] TTY_DATO,
  output TTY_ESCRIBE
);

  wire byte_listo, eq3, not1, not4, ocupado;
  wire [7:0] zx2;
  wire [7:7] byte_recibido;

  assign zx2 = {{1{1'b0}}, TECLADO_DATO};  // Bit_Extender bit_extender_1
  ReceptorSerie RX_PC (
    .CLK(CLK), .RST(RST), .DIV(12'h4), .RXD(RX_DESDE_CHIP), .DATA({byte_recibido[7], TTY_DATO}),
    .VALID(byte_listo));  // open: FERR
  and and_1 (TECLADO_LEER, TECLADO_HAY, not1);
  TransmisorSerie TX_PC (
    .CLK(CLK), .RST(RST), .DIV(12'h4), .START(TECLADO_LEER), .DATA(zx2), .TXD(TX_AL_CHIP), .BUSY(ocupado));  // open: FIN
  Comparator #(.width(7), .mode("unsigned")) comparator_1 (.a(TTY_DATO), .b(7'b0001101), .eq(eq3));  // open: gt, lt
  not not_1 (not1, ocupado);
  not not_2 (not4, eq3);
  and and_2 (TTY_ESCRIBE, byte_listo, not4);

  // Other names for the same wires on the sheet: enviar = TECLADO_LEER; byte_recibido[6:0] = TTY_DATO;
  //   byte_recibido_6_0[6:0] = TTY_DATO; and5 = TTY_ESCRIBE; linea_al_chip = TX_AL_CHIP
endmodule

module Registro74HC595 (
  input  SER,
  input  SRCLK,
  input  RCLK,
  output QA,
  output QB,
  output QC,
  output QD,
  output QE,
  output QF,
  output QG,
  output QH
);

  wire [7:0] desplazado;

  Register #(.width(1)) ETAPA_A (.D(SER), .en(1'b1), .Q(desplazado[0]), .clk(SRCLK), .clr(1'b0));
  Register #(.width(1)) ETAPA_B (.D(desplazado[0]), .en(1'b1), .Q(desplazado[1]), .clk(SRCLK), .clr(1'b0));
  Register #(.width(1)) ETAPA_C (.D(desplazado[1]), .en(1'b1), .Q(desplazado[2]), .clk(SRCLK), .clr(1'b0));
  Register #(.width(1)) ETAPA_D (.D(desplazado[2]), .en(1'b1), .Q(desplazado[3]), .clk(SRCLK), .clr(1'b0));
  Register #(.width(1)) ETAPA_E (.D(desplazado[3]), .en(1'b1), .Q(desplazado[4]), .clk(SRCLK), .clr(1'b0));
  Register #(.width(1)) ETAPA_F (.D(desplazado[4]), .en(1'b1), .Q(desplazado[5]), .clk(SRCLK), .clr(1'b0));
  Register #(.width(1)) ETAPA_G (.D(desplazado[5]), .en(1'b1), .Q(desplazado[6]), .clk(SRCLK), .clr(1'b0));
  Register #(.width(1)) ETAPA_H (.D(desplazado[6]), .en(1'b1), .Q(desplazado[7]), .clk(SRCLK), .clr(1'b0));
  Register #(.width(8)) LATCH (.D(desplazado), .en(1'b1), .Q({QH, QG, QF, QE, QD, QC, QB, QA}), .clk(RCLK), .clr(1'b0));

  // Other names for the same wires on the sheet: etapa0 = desplazado[0]; etapa1 = desplazado[1];
  //   etapa2 = desplazado[2]; etapa3 = desplazado[3]; etapa4 = desplazado[4]; etapa5 = desplazado[5];
  //   etapa6 = desplazado[6]; etapa7 = desplazado[7]; q0 = QA; salidas[7:0] = {QH, QG, QF, QE, QD, QC, QB, QA};
  //   q1 = QB; q2 = QC; q3 = QD; q4 = QE; q5 = QF; q6 = QG; q7 = QH
endmodule

module MemoriaI2C (
  input  CLK,
  input  SCL,
  input  SDA,
  output SDA_SALE
);

  wire ack_maestro, and14, and18, and24, and26, and27, and29, and31, and33, and34, and41, and42, and46,
       and51, and53, and55, and57, and58, baja_bit, baja_scl, bit_a_enviar, byte_completo, byte_recibido,
       da_ack, eq23, es_mi_direccion, escribe, escritura_pendiente, espera_direccion, est_0, est_1, est_2,
       est_3, fin_ack, fin_de_start, manda_cero, mux15, mux49, not8, not9, not10, not11, not13, not17, not25,
       not28, not32, not40, not44, not48, not61, not62, or12, or16, or19, or22, or30, or35, or43, or45, or47,
       or50, or54, or56, or59, or63, ranura_ack, scl_2, seleccionada, start, stop, sube_scl, tira_sda;
  wire [0:0] desplaza_sig;
  wire [1:0] anterior, estado, mux36, mux37, mux38, mux39, qx3, qx5, qx7, sinc1, xor2, xor4, xor6;
  wire [2:0] not60;
  wire [3:0] \bit , mux21, sum20;
  wire [7:0] dato_memoria, desplaza, puntero, puntero_sig, sum52;

  Register #(.width(2)) u_SINC1 (.D(xor2), .en(1'b1), .Q(qx3), .clk(CLK), .clr(1'b0));
  Register #(.width(2)) SINC2 (.D(xor4), .en(1'b1), .Q(qx5), .clk(CLK), .clr(1'b0));
  Register #(.width(2)) u_ANTERIOR (.D(xor6), .en(1'b1), .Q(qx7), .clk(CLK), .clr(1'b0));
  Register #(.width(1)) TRAS_START (.D(mux15), .en(or16), .Q(fin_de_start), .clk(CLK), .clr(1'b0));
  Register #(.width(4)) u_BIT (.D(mux21), .en(or22), .Q(\bit ), .clk(CLK), .clr(1'b0));
  Register #(.width(1)) u_ACK_MAESTRO (.D(desplaza_sig[0]), .en(and24), .Q(ack_maestro), .clk(CLK), .clr(1'b0));
  Register #(.width(2)) u_ESTADO (.D(mux39), .en(1'b1), .Q(estado), .clk(CLK), .clr(1'b0));
  Register #(.width(1)) ELEGIDA (.D(and41), .en(or43), .Q(seleccionada), .clk(CLK), .clr(1'b0));
  Register #(.width(1)) PRIMERO (.D(and46), .en(or47), .Q(espera_direccion), .clk(CLK), .clr(1'b0));
  Register #(.width(1)) POR_ESCRIBIR (.D(mux49), .en(or50), .Q(escritura_pendiente), .clk(CLK), .clr(1'b0));
  RAM #(.addrWidth(8), .dataWidth(8), .enables("byte"), .trigger("rising"), .asyncread("true"), .databus("bibus")) MEMORIA_256B (
    .addr(puntero), .we(and57), .oe(1'b1), .clk(CLK), .din(desplaza), .dout(dato_memoria));
  Register #(.width(1)) u_TIRA_SDA (.D(or63), .en(1'b1), .Q(tira_sda), .clk(CLK), .clr(1'b0));
  Register #(.width(8)) u_DESPLAZA (
    .D({desplaza[6:0], desplaza_sig[0]}), .en(and14), .Q(desplaza), .clk(CLK), .clr(1'b0));
  Register #(.width(8)) u_PUNTERO (.D(puntero_sig), .en(or56), .Q(puntero), .clk(CLK), .clr(1'b0));
  Decoder #(.select(2), .enable("false")) decoder_1 (
    .out0(est_0), .out1(est_1), .out2(est_2), .out3(est_3), .sel(estado));
  assign xor2 = {SDA, SCL} ^ 2'b11;  // XOR_Gate xor_1, 2 bits wide
  assign sinc1 = qx3 ^ 2'b11;  // XOR_Gate xor_2, 2 bits wide
  assign {desplaza_sig[0], scl_2} = qx5 ^ 2'b11;  // XOR_Gate xor_3, 2 bits wide
  assign anterior = qx7 ^ 2'b11;  // XOR_Gate xor_4, 2 bits wide
  Comparator #(.width(4), .mode("unsigned")) comparator_1 (.a(\bit ), .b(4'b1000), .eq(ranura_ack));  // open: gt, lt
  Adder #(.width(4)) adder_1 (.a(\bit ), .b(4'b0001), .out(sum20));  // open: cin, cout
  Comparator #(.width(4), .mode("unsigned")) comparator_2 (.a(\bit ), .b(4'b0111), .eq(eq23));  // open: gt, lt
  Adder #(.width(8)) adder_2 (.a(puntero), .b(8'h1), .out(sum52));  // open: cin, cout
  assign SDA_SALE = tira_sda ? 1'b0 : 1'bz;  // Controlled_Buffer controlled_buffer_1
  not not_1 (not17, fin_de_start);
  not not_2 (not28, ack_maestro);
  not not_3 (not48, espera_direccion);
  assign xor4 = sinc1 ^ 2'b11;  // XOR_Gate xor_5, 2 bits wide
  assign xor6 = {desplaza_sig[0], scl_2} ^ 2'b11;  // XOR_Gate xor_6, 2 bits wide
  or or_1 (or12, est_1, est_2);
  not not_4 (not13, ranura_ack);
  Comparator #(.width(7), .mode("unsigned")) comparator_3 (
    .a(desplaza[7:1]), .b(7'b1010000), .eq(es_mi_direccion));  // open: gt, lt
  not not_5 (not25, desplaza[0]);
  and and_1 (and29, est_3, not28);
  assign not60 = ~\bit [2:0];  // NOT_Gate not_6, 3 bits wide
  not not_7 (not61, ranura_ack);
  or or_2 (or54, escritura_pendiente, est_3);
  not not_8 (not8, desplaza_sig[0]);
  not not_9 (not9, anterior[1]);
  not not_10 (not10, anterior[0]);
  not not_11 (not11, scl_2);
  and and_2 (and27, est_1, es_mi_direccion, desplaza[0]);
  not not_12 (not32, es_mi_direccion);
  and and_3 (and58, est_1, es_mi_direccion);
  Multiplexer #(.select(3), .width(1), .enable("false")) multiplexer_1 (
    .in0(dato_memoria[0]), .in1(dato_memoria[1]), .in2(dato_memoria[2]), .in3(dato_memoria[3]),
    .in4(dato_memoria[4]), .in5(dato_memoria[5]), .in6(dato_memoria[6]), .in7(dato_memoria[7]),
    .out(bit_a_enviar), .sel(not60));
  and and_4 (start, scl_2, anterior[0], anterior[1], not8);
  and and_5 (stop, scl_2, anterior[0], not9, desplaza_sig[0]);
  and and_6 (sube_scl, scl_2, not10);
  and and_7 (baja_scl, not11, anterior[0]);
  or or_3 (or30, and27, and29);
  or or_4 (or59, and58, est_2);
  not not_13 (not62, bit_a_enviar);
  and and_8 (and14, sube_scl, or12, not13);
  Multiplexer #(.select(1), .width(1), .enable("false")) multiplexer_2 (
    .in0(1'b0), .in1(1'b1), .out(mux15), .sel(start));
  or or_5 (or16, start, baja_scl);
  and and_9 (baja_bit, baja_scl, not17);
  and and_10 (and24, sube_scl, ranura_ack, est_3);
  not not_14 (not40, start);
  and and_11 (da_ack, ranura_ack, or59);
  and and_12 (manda_cero, est_3, not61, not62);
  or or_6 (or45, start, espera_direccion);
  and and_13 (and18, baja_bit, ranura_ack);
  or or_7 (or22, start, baja_bit);
  and and_14 (fin_ack, baja_bit, ranura_ack);
  and and_15 (byte_completo, baja_bit, eq23);
  and and_16 (and41, es_mi_direccion, not40);
  or or_8 (or63, da_ack, manda_cero);
  or or_9 (or19, start, and18);
  and and_17 (and31, fin_ack, or30);
  and and_18 (and33, fin_ack, est_1, not32);
  and and_19 (and55, fin_ack, or54);
  and and_20 (and26, fin_ack, est_1, es_mi_direccion, not25);
  and and_21 (and34, fin_ack, est_3, ack_maestro);
  and and_22 (and42, byte_completo, est_1);
  and and_23 (byte_recibido, byte_completo, est_2);
  and and_24 (and57, escritura_pendiente, fin_ack);
  Multiplexer #(.select(1), .width(4), .enable("false")) multiplexer_3 (
    .in0(sum20), .in1(4'b0000), .out(mux21), .sel(or19));
  or or_10 (or35, stop, and33, and34);
  or or_11 (or43, start, and42);
  not not_15 (not44, byte_recibido);
  or or_12 (or47, start, byte_recibido);
  and and_25 (escribe, byte_recibido, not48);
  and and_26 (and51, byte_recibido, espera_direccion);
  and and_27 (and53, byte_recibido, espera_direccion);
  and and_28 (and46, not44, or45);
  Multiplexer #(.select(1), .width(1), .enable("false")) multiplexer_4 (
    .in0(1'b0), .in1(1'b1), .out(mux49), .sel(escribe));
  or or_13 (or56, and53, and55);
  Multiplexer #(.select(1), .width(2), .enable("false")) multiplexer_5 (
    .in0(estado), .in1(2'b00), .out(mux36), .sel(or35));
  or or_14 (or50, escribe, fin_ack, start, stop);
  Multiplexer #(.select(1), .width(8), .enable("false")) multiplexer_6 (
    .in0(sum52), .in1(desplaza), .out(puntero_sig), .sel(and51));
  Multiplexer #(.select(1), .width(2), .enable("false")) multiplexer_7 (
    .in0(mux36), .in1(2'b10), .out(mux37), .sel(and26));
  Multiplexer #(.select(1), .width(2), .enable("false")) multiplexer_8 (
    .in0(mux37), .in1(2'b11), .out(mux38), .sel(and31));
  Multiplexer #(.select(1), .width(2), .enable("false")) multiplexer_9 (
    .in0(mux38), .in1(2'b01), .out(mux39), .sel(start));

  // Other names for the same wires on the sheet: anterior_0 = anterior[0]; anterior_1 = anterior[1];
  //   bit_2_0[2:0] = \bit [2:0]; cat1[1:0] = {SDA, SCL}; dato_memoria_0 = dato_memoria[0];
  //   dato_memoria_1 = dato_memoria[1]; dato_memoria_2 = dato_memoria[2]; dato_memoria_3 = dato_memoria[3];
  //   dato_memoria_4 = dato_memoria[4]; dato_memoria_5 = dato_memoria[5]; dato_memoria_6 = dato_memoria[6];
  //   dato_memoria_7 = dato_memoria[7]; desplaza_7_1[6:0] = desplaza[7:1]; sda_2 = desplaza_sig[0];
  //   sinc2[1:0] = {desplaza_sig[0], scl_2}; desplaza_6_0[6:0] = desplaza[6:0]; desplaza_sig[7:1] = desplaza[6:0];
  //   lectura = desplaza[0]; sda_salida = SDA_SALE
endmodule

module InversorCMOS (
  input  A,
  output Y
);

  Transistor #(.\type ("p"), .width(1)) transistor_1 (.in(1'b1), .out(Y), .gate(A));
  Transistor #(.\type ("n"), .width(1)) transistor_2 (.in(1'b0), .out(Y), .gate(A));

  // Notes on the sheet:
  //   Inversor (NOT) CMOS: 2 transistores
  //   A = 0: P conduce y N no -> Y = 1 (VDD)
  //   A = 1: N conduce y P no -> Y = 0 (GND)
  //   P (con circulito): conduce si su compuerta = 0; deja pasar el 1 de VDD
  //   N: conduce si su compuerta = 1; deja pasar el 0 de GND
  //   P
  //   N
endmodule

module NandCMOS (
  input  A,
  input  B,
  output Y
);

  wire transistor_4_out;

  Transistor #(.\type ("p"), .width(1)) transistor_1 (.in(1'b1), .out(Y), .gate(A));
  Transistor #(.\type ("p"), .width(1)) transistor_2 (.in(1'b1), .out(Y), .gate(B));
  Transistor #(.\type ("n"), .width(1)) transistor_3 (.in(transistor_4_out), .out(Y), .gate(B));
  Transistor #(.\type ("n"), .width(1)) transistor_4 (.in(1'b0), .out(transistor_4_out), .gate(A));

  // Notes on the sheet:
  //   NAND CMOS: 4 transistores
  //   P (con circulito): conduce si su compuerta = 0; deja pasar el 1 de VDD
  //   N: conduce si su compuerta = 1; deja pasar el 0 de GND
  //   2 N en serie: solo con A = 1 y B = 1 baja Y a 0
  //   2 P en paralelo: basta un 0 para subir Y a 1
endmodule

module NorCMOS (
  input  A,
  input  B,
  output Y
);

  wire transistor_2_out;

  Transistor #(.\type ("n"), .width(1)) transistor_1 (.in(1'b0), .out(Y), .gate(A));
  Transistor #(.\type ("p"), .width(1)) transistor_2 (.in(1'b1), .out(transistor_2_out), .gate(A));
  Transistor #(.\type ("p"), .width(1)) transistor_3 (.in(transistor_2_out), .out(Y), .gate(B));
  Transistor #(.\type ("n"), .width(1)) transistor_4 (.in(1'b0), .out(Y), .gate(B));

  // Notes on the sheet:
  //   NOR CMOS: 4 transistores
  //   P (con circulito): conduce si su compuerta = 0; deja pasar el 1 de VDD
  //   N: conduce si su compuerta = 1; deja pasar el 0 de GND
  //   2 P en serie: solo con A = 0 y B = 0 sube Y a 1
  //   2 N en paralelo: basta un 1 para bajar Y a 0
endmodule

module Sumador4CMOS (
  input  [3:0] A,
  input  [3:0] B,
  input  Cin,
  output Cout,
  output [3:0] S
);

  wire FA0_cout, FA1_cout, FA2_cout;

  SumadorCompletoCMOS FA3 (.A(A[3]), .B(B[3]), .Cin(FA2_cout), .Cout(Cout), .S(S[3]));
  SumadorCompletoCMOS FA2 (.A(A[2]), .B(B[2]), .Cin(FA1_cout), .Cout(FA2_cout), .S(S[2]));
  SumadorCompletoCMOS FA1 (.A(A[1]), .B(B[1]), .Cin(FA0_cout), .Cout(FA1_cout), .S(S[1]));
  SumadorCompletoCMOS FA0 (.A(A[0]), .B(B[0]), .Cin(Cin), .Cout(FA0_cout), .S(S[0]));

  // Notes on the sheet:
  //   Sumador de 4 bits: 4 sumadores completos de 28 transistores (112 en total)
  //   El acarreo viaja de derecha (bit 0) a izquierda (bit 3). Entra a cualquier FA para ver sus transistores.
endmodule

module LatchD (
  input  D,
  input  E,
  input  R,
  output Q,
  output Qn
);

  wire nand_1_out, nand_2_out, not_1_out;

  not not_1 (not_1_out, R);
  nand nand_1 (nand_1_out, D, E);
  nand nand_2 (nand_2_out, nand_1_out, E);
  nand nand_3 (Q, nand_1_out, Qn);
  nand nand_4 (Qn, Q, nand_2_out, not_1_out);

  // Notes on the sheet:
  //   Latch D con 4 NAND (cada NAND son 4 transistores)
  //   E = 1: Q copia a D (transparente).  E = 0: Q se queda guardado gracias a la realimentacion (Q y Qn se sostienen mutuamente).  R = 1 lo borra (Q = 0).
  //   Al encender, Q y Qn pueden quedar en rojo (E = indefinido): en un chip real el latch arranca en 0 o en 1 al azar. Por eso los circuitos reales tienen un reset al encender.
endmodule

module FlipFlopD (
  input  R,
  input  D,
  input  CLK,
  output Q
);

  wire MAESTRO_q, not_1_out;

  not not_1 (not_1_out, CLK);
  LatchD MAESTRO (.D(D), .E(not_1_out), .R(R), .Q(MAESTRO_q));  // open: Qn
  LatchD ESCLAVO (.D(MAESTRO_q), .E(CLK), .R(R), .Q(Q));  // open: Qn

  // Notes on the sheet:
  //   Flip-flop D disparado por flanco de subida: dos latches en cascada
  //   Con CLK = 0 el MAESTRO copia D y el ESCLAVO guarda; al subir CLK el maestro se cierra y el esclavo muestra lo que el maestro guardo. Asi Q solo cambia en el flanco de subida.
  //   Si lo abres solo y Q aparece en rojo (E = indefinido), es el 'estado al encender': pon R = 1 un momento o da un flanco de reloj y queda definido.
endmodule

module Contador4 (
  input  CLK,
  input  R,
  output [3:0] Q
);

  wire d0, d1, d2, d3, RESET_ENCENDIDO_qn, rst;

  D_Flip_Flop #(.trigger("rising")) RESET_ENCENDIDO (
    .clk(CLK), .D(1'b1), .Qn(RESET_ENCENDIDO_qn));  // open: Q, preset, reset
  FlipFlopD FF0 (.D(d0), .CLK(CLK), .R(rst), .Q(Q[0]));
  FlipFlopD FF1 (.D(d1), .CLK(CLK), .R(rst), .Q(Q[1]));
  FlipFlopD FF2 (.D(d2), .CLK(CLK), .R(rst), .Q(Q[2]));
  FlipFlopD FF3 (.D(d3), .CLK(CLK), .R(rst), .Q(Q[3]));
  or or_1 (rst, R, RESET_ENCENDIDO_qn);
  Sumador4CMOS MAS_UNO (.A(Q), .B(4'b0000), .Cin(1'b1), .S({d3, d2, d1, d0}));  // open: Cout

  // Notes on the sheet:
  //   Contador de 4 bits: memoria (flip-flops) + logica (sumador CMOS que calcula Q + 1)
  //   En cada flanco de subida del reloj los flip-flops guardan Q + 1; entre flancos el sumador ya calcula el siguiente.
  //   Reset al encender: el flip-flop RESET_ENCENDIDO arranca en 0, asi que su salida negada vale 1 y pone el contador en 0 hasta el primer flanco del reloj.
endmodule
